# Fritzing sketch BreadboardAdapter (saved by Fritzing 1.0.1rc)
breadboards: 1

parts:
  IC3 = IC, DIP package, 20 pins [chip_label=AT89C2051]
  5V = Power plug
  XTAL1 = Crystal [frequency="16 Mhz" package=THT]
  C1 = Ceramic Capacitor [capacitance=30pF voltage=35V package="100 mil [THT, multilayer]"]
  C2 = Ceramic Capacitor [capacitance=30pF voltage=35V package="100 mil [THT, multilayer]"]
  R2 = Resistor [tolerance=±5% resistance=56k power=0.25W package=THT]
  C3 = Electrolytic Capacitor [capacitance=2.2µF voltage=35V package="100 mil [THT, electrolytic]"]

nets:
  N1: IC3.pin1, R2.Pin_0, C3.-
  N2: IC3.pin4, XTAL1.pin_0, C1.0
  N3: IC3.pin5, XTAL1.pin_1, C2.1
  GND: IC3.pin10, 5V.GND, C1.1, C2.0, R2.Pin_1
  VCC: IC3.pin20, 5V.VCC, C3.+
