# Fritzing sketch Counters (saved by Fritzing 1.0.1rc)
breadboards: 1

parts:
  IC3 = IC, DIP package, 20 pins [chip_label=AT89C2051]
  5V = Power plug
  XTAL1 = Crystal [frequency="16 Mhz" package=THT]
  C1 = Ceramic Capacitor [capacitance=30pF voltage=35V package="100 mil [THT, multilayer]"]
  C2 = Ceramic Capacitor [capacitance=30pF voltage=35V package="100 mil [THT, multilayer]"]
  R2 = Resistor [tolerance=±5% resistance=56k power=0.25W package=THT]
  C3 = Electrolytic Capacitor [capacitance=2.2µF voltage=35V package="100 mil [THT, electrolytic]"]
  LCD1 = LCD screen
  R3 = Resistor [tolerance=±5% resistance=220 power=0.25W package=THT]
  VR1 = Rotary Potentiometer (Small) [maximum_resistance=100kΩ knob_status=50% power=0.5W package=THT]
  S1 = Pushbutton [package="[THT]"]
  R4 = Resistor [tolerance=±5% power=0.25W resistance=10k package=THT]
  C4 = Ceramic Capacitor [capacitance=100nF voltage=35V package="100 mil [THT, multilayer]"]

nets:
  N1: IC3.pin1, R2.Pin_0, C3.-
  RS: IC3.pin2, LCD1.RS
  E: IC3.pin3, LCD1.E
  N2: IC3.pin4, XTAL1.pin_0, C1.0
  N3: IC3.pin5, XTAL1.pin_1, C2.1
  T0: IC3.pin8, S1.Pin_3, S1.Pin_4, R4.Pin_1, C4.1
  GND: IC3.pin10, 5V.GND, C1.1, C2.0, R2.Pin_1, LCD1.VSS, LCD1.R/W, LCD1.LED-, VR1.leg1, S1.Pin_1, S1.Pin_2, C4.0
  DB0: IC3.pin12, LCD1.DB0
  DB1: IC3.pin13, LCD1.DB1
  DB2: IC3.pin14, LCD1.DB2
  DB3: IC3.pin15, LCD1.DB3
  DB4: IC3.pin16, LCD1.DB4
  DB5: IC3.pin17, LCD1.DB5
  DB6: IC3.pin18, LCD1.DB6
  DB7: IC3.pin19, LCD1.DB7
  VCC: IC3.pin20, 5V.VCC, C3.+, LCD1.VDD, R3.Pin_0, VR1.leg2, R4.Pin_0
  N4: LCD1.V0, VR1.wiper
  N5: LCD1.LED+, R3.Pin_1
