# Fritzing sketch Interrupts (saved by Fritzing 1.0.1rc)
breadboards: 1

parts:
  IC3 = IC, DIP package, 20 pins [chip_label=AT89C2051]
  5V = Power plug
  XTAL1 = Crystal [frequency="16 Mhz" package=THT]
  C1 = Ceramic Capacitor [capacitance=30pF voltage=35V package="100 mil [THT, multilayer]"]
  C2 = Ceramic Capacitor [capacitance=30pF voltage=35V package="100 mil [THT, multilayer]"]
  R2 = Resistor [tolerance=±5% resistance=56k power=0.25W package=THT]
  C3 = Electrolytic Capacitor [capacitance=2.2µF voltage=35V package="100 mil [THT, electrolytic]"]
  S1 = Pushbutton [package="[THT]"]
  R4 = Resistor [tolerance=±5% power=0.25W resistance=10k package=THT]
  C4 = Ceramic Capacitor [capacitance=100nF voltage=35V package="100 mil [THT, multilayer]"]
  R5 = Resistor [tolerance=±5% power=0.25W resistance=470 package=THT]
  LED1 = LED - 3mm [color="Red (633nm)" current=0.030A package="3 mm [THT]"]
  LED2 = LED - 3mm [color="Red (633nm)" current=0.030A package="3 mm [THT]"]
  R6 = Resistor [tolerance=±5% power=0.25W resistance=470 package=THT]

nets:
  N1: IC3.pin1, R2.Pin_0, C3.-
  N2: IC3.pin4, XTAL1.pin_0, C1.0
  N3: IC3.pin5, XTAL1.pin_1, C2.1
  CH1/INT0: IC3.pin6, S1.Pin_3, S1.Pin_4, R4.Pin_1, C4.1
  GND: IC3.pin10, 5V.GND, C1.1, C2.0, R2.Pin_1, S1.Pin_1, S1.Pin_2, C4.0
  CH2/P1_0: IC3.pin12, LED1.cathode
  P1_1: IC3.pin13, LED2.cathode
  VCC: IC3.pin20, 5V.VCC, C3.+, R4.Pin_0, R5.Pin_1, R6.Pin_1
  N4: R5.Pin_0, LED1.anode
  N5: LED2.anode, R6.Pin_0
