# Fritzing sketch LedChaser (saved by Fritzing 0.9.2b)
breadboards: 1

parts:
  IC3 = IC, DIP package, 20 pins [chip_label=AT89C2051]
  5V = Power plug
  XTAL1 = Crystal [frequency="16 Mhz" package=THT]
  C1 = Ceramic Capacitor [capacitance=30pF package="100 mil [THT, multilayer]"]
  C2 = Ceramic Capacitor [capacitance=30pF package="100 mil [THT, multilayer]"]
  LED1 = LED - 3mm [color="White (4500K)" package="3 mm [THT]"]
  R1 = Resistor [tolerance=±5% resistance=1k package=THT]
  R2 = Resistor [tolerance=±5% resistance=56k package=THT]
  C3 = Electrolytic Capacitor [capacitance=2.2µF package="100 mil [THT, electrolytic]"]
  LED2 = LED - 3mm [color="White (4500K)" package="3 mm [THT]"]
  R3 = Resistor [tolerance=±5% resistance=1k package=THT]
  R4 = Resistor [tolerance=±5% resistance=1k package=THT]
  R5 = Resistor [tolerance=±5% resistance=1k package=THT]
  R6 = Resistor [tolerance=±5% resistance=1k package=THT]
  R7 = Resistor [tolerance=±5% resistance=1k package=THT]
  R8 = Resistor [tolerance=±5% resistance=1k package=THT]
  R9 = Resistor [tolerance=±5% resistance=1k package=THT]
  LED3 = LED - 3mm [color="White (4500K)" package="3 mm [THT]"]
  LED4 = LED - 3mm [color="White (4500K)" package="3 mm [THT]"]
  LED5 = LED - 3mm [color="White (4500K)" package="3 mm [THT]"]
  LED6 = LED - 3mm [color="White (4500K)" package="3 mm [THT]"]
  LED7 = LED - 3mm [color="White (4500K)" package="3 mm [THT]"]
  LED8 = LED - 3mm [color="White (4500K)" package="3 mm [THT]"]

nets:
  N1: IC3.pin1, R2.Pin_0, C3.-
  N2: IC3.pin4, XTAL1.pin_0, C1.0
  N3: IC3.pin5, XTAL1.pin_1, C2.1
  GND: IC3.pin10, 5V.GND, C1.1, C2.0, R2.Pin_1
  N4: IC3.pin12, LED1.cathode
  N5: IC3.pin13, LED2.cathode
  N6: IC3.pin14, LED3.cathode
  N7: IC3.pin15, LED4.cathode
  N8: IC3.pin16, LED5.cathode
  N9: IC3.pin17, LED6.cathode
  N10: IC3.pin18, LED7.cathode
  N11: IC3.pin19, LED8.cathode
  VCC: IC3.pin20, 5V.VCC, R1.Pin_0, C3.+, R3.Pin_0, R4.Pin_0, R5.Pin_0, R6.Pin_0, R7.Pin_0, R8.Pin_0, R9.Pin_0
  N12: LED1.anode, R1.Pin_1
  N13: LED2.anode, R3.Pin_1
  N14: R4.Pin_1, LED3.anode
  N15: R5.Pin_1, LED4.anode
  N16: R6.Pin_1, LED5.anode
  N17: R7.Pin_1, LED6.anode
  N18: R8.Pin_1, LED7.anode
  N19: R9.Pin_1, LED8.anode
