# Fritzing sketch Programmer (saved by Fritzing 0.9.2b)
breadboards: 1

parts:
  D1 = Rectifier Diode [part_number=1N4148 package="300 mil [THT]"]
  D2 = Rectifier Diode [part_number=1N4148 package="300 mil [THT]"]
  D3 = Rectifier Diode [part_number=1N4148 package="300 mil [THT]"]
  D4 = Rectifier Diode [part_number=1N4148 package="300 mil [THT]"]
  C1 = Ceramic Capacitor [capacitance=220nF voltage=25V package="100 mil [THT, multilayer]"]
  C2 = Ceramic Capacitor [capacitance=220nF voltage=25V package="100 mil [THT, multilayer]"]
  C3 = Ceramic Capacitor [capacitance=220nF voltage=25V package="100 mil [THT, multilayer]"]
  C4 = Ceramic Capacitor [capacitance=1µF voltage=25V package="100 mil [THT, multilayer]"]
  Rp1 = Resistor [tolerance=±5% resistance=2.2k package=THT]
  D5 = Zener Diode [part_number=1N4742 breakdown_voltage=12V package="300 mil [THT]"]
  Part4 = Arduino Uno (Rev3)
  IC2 = IC, DIP package, 20 pins [chip_label=AT89C2051]
  D7 = Rectifier Diode [part_number=1N4148 package="300 mil [THT]"]
  Rp3 = Resistor [tolerance=±5% resistance=47k package=THT]
  Q1 = NPN-Transistor [part_number=2N3904 package="TO92 [THT]"]
  Q2 = NPN-Transistor [part_number=2N3904 package="TO92 [THT]"]
  R1 = Resistor [tolerance=±5% resistance=10k package=THT]
  R2 = Resistor [tolerance=±5% resistance=10k package=THT]

nets:
  N1: D1.cathode, D2.anode, C1.1
  VCC: D1.anode, Part4.5V, IC2.pin20, R2.Pin_1
  N2: D2.cathode, D3.anode, C2.1
  N3: D3.cathode, D4.anode, C3.1
  VPP: D4.cathode, C4.1, Rp1.Pin_0
  PUMP_A: C1.0, C3.0, Part4.D3_PWM
  PUMP_B: C2.0, Part4.D11_PWM/MOSI
  GND: C4.0, D5.anode, Part4.GND, IC2.pin10, Rp3.Pin_0, Q1.E, Q2.E
  RST_VPP: Rp1.Pin_1, D5.cathode, IC2.pin1, D7.cathode, Rp3.Pin_1, Q2.C
  RST: Part4.A0, D7.anode, R1.Pin_1
  XTAL1: Part4.A1, IC2.pin5
  P3.2: Part4.A2, IC2.pin6
  P3.3: Part4.A3, IC2.pin7
  P3.4: Part4.A4/SDA, IC2.pin8
  P3.5: Part4.A5/SCL, IC2.pin9
  P1.5: Part4.D8, IC2.pin17
  P1.6: Part4.D9_PWM, IC2.pin18
  P1.7: Part4.D10_PWM/SS, IC2.pin19
  P3.7: Part4.D12/MISO, IC2.pin11
  P1.0: Part4.D2, IC2.pin12
  P1.1: Part4.D4, IC2.pin13
  P1.2: Part4.D5_PWM, IC2.pin14
  P1.3: Part4.D6_PWM, IC2.pin15
  P1.4: Part4.D7, IC2.pin16
  N4: Q1.B, R1.Pin_0
  N5: Q1.C, Q2.B, R2.Pin_0

notes:
  ~16V
  VPP/RST
  12V/5V/0V
