# Fritzing sketch PovShakeStickKit (saved by Fritzing 0.9.2b)
breadboards: 1

parts:
  IC1 = IC, DIP package, 40 pins [chip_label=AT89S52]
  VCC1 = Battery
  XT1 = Crystal [frequency="16 Mhz" part_number=12MHz package=THT]
  C1 = Ceramic Capacitor [capacitance=22pF package="100 mil [THT, multilayer]"]
  C2 = Ceramic Capacitor [capacitance=22pF package="100 mil [THT, multilayer]"]
  R3 = Resistor [tolerance=±5% resistance=1.5k package=THT]
  C3 = Electrolytic Capacitor [capacitance=10µF package="100 mil [THT, electrolytic]"]
  S1 = Toggle Switch [package=THT]
  D18 = LED - 5mm [color="Red (633nm)" package="5 mm [THT]"]
  R4 = Resistor [tolerance=±5% resistance=1.5k package=THT]
  S2 = Pushbutton [package=THT]
  R1 = Resistor [tolerance=±5% resistance=10k package=THT]
  S3 = Pushbutton [package=THT]
  R2 = Resistor [tolerance=±5% resistance=10k package=THT]
  D17 = Rectifier Diode [part_number=1N4007 package="300 mil [THT]"]
  D1 = LED - 5mm [color="Red (633nm)" package="5 mm [THT]"]
  D2 = LED - 5mm [color="Red (633nm)" package="5 mm [THT]"]
  D3 = LED - 5mm [color="Red (633nm)" package="5 mm [THT]"]
  D4 = LED - 5mm [color="Red (633nm)" package="5 mm [THT]"]
  D5 = LED - 5mm [color="Red (633nm)" package="5 mm [THT]"]
  D6 = LED - 5mm [color="Red (633nm)" package="5 mm [THT]"]
  D7 = LED - 5mm [color="Red (633nm)" package="5 mm [THT]"]
  D8 = LED - 5mm [color="Red (633nm)" package="5 mm [THT]"]
  D9 = LED - 5mm [color="Red (633nm)" package="5 mm [THT]"]
  D10 = LED - 5mm [color="Red (633nm)" package="5 mm [THT]"]
  D11 = LED - 5mm [color="Red (633nm)" package="5 mm [THT]"]
  D12 = LED - 5mm [color="Red (633nm)" package="5 mm [THT]"]
  D13 = LED - 5mm [color="Red (633nm)" package="5 mm [THT]"]
  D14 = LED - 5mm [color="Red (633nm)" package="5 mm [THT]"]
  D15 = LED - 5mm [color="Red (633nm)" package="5 mm [THT]"]
  D16 = LED - 5mm [color="Red (633nm)" package="5 mm [THT]"]

nets:
  RESET: IC1.pin9, R3.Pin_0, C3.-
  SWING_TRIGGER: IC1.pin12, S2.leg1, R1.Pin_1
  DISPLAY_SELECT: IC1.pin17, S3.leg1, R2.Pin_1
  XTAL2: IC1.pin18, XT1.pin_1, C2.1
  XTAL1: IC1.pin19, XT1.pin_0, C1.1
  GND: IC1.pin20, VCC1.-, C1.0, C2.0, R3.Pin_1, R4.Pin_1, S2.leg0, S3.leg0
  N1: IC1.pin21, D16.cathode
  N2: IC1.pin22, D15.cathode
  N3: IC1.pin23, D14.cathode
  N4: IC1.pin24, D13.cathode
  N5: IC1.pin25, D12.cathode
  N6: IC1.pin26, D11.cathode
  N7: IC1.pin27, D10.cathode
  N8: IC1.pin28, D9.cathode
  VCC: IC1.pin31, IC1.pin40, C3.+, S1.L2, D18.anode, R1.Pin_0, R2.Pin_0, D17.anode
  N9: IC1.pin32, D8.cathode
  N10: IC1.pin33, D7.cathode
  N11: IC1.pin34, D6.cathode
  N12: IC1.pin35, D5.cathode
  N13: IC1.pin36, D4.cathode
  N14: IC1.pin37, D3.cathode
  N15: IC1.pin38, D2.cathode
  N16: IC1.pin39, D1.cathode
  N17: VCC1.+, S1.COM
  N18: D18.cathode, R4.Pin_0
  N19: D17.cathode, D1.anode, D2.anode, D3.anode, D4.anode, D5.anode, D6.anode, D7.anode, D8.anode, D9.anode, D10.anode, D11.anode, D12.anode, D13.anode, D14.anode, D15.anode, D16.anode

notes:
  ignore the breadboard - not laid out
