# Fritzing sketch DebugWithStlink (saved by Fritzing 0.9.2b)

parts:
  Part2 = BluePill  # not connected
  ST-LINK_V2 = shrouded pin header, 10 pins [form="♂ (shrouded male)"]

nets:
  RST: ST-LINK_V2.pin1
  GND: ST-LINK_V2.pin2, ST-LINK_V2.pin9
  SWIM: ST-LINK_V2.pin3
  3.3V: ST-LINK_V2.pin4, ST-LINK_V2.pin7
  5.0V: ST-LINK_V2.pin5, ST-LINK_V2.pin6
  SWCLK: ST-LINK_V2.pin8
  SWDIO: ST-LINK_V2.pin10

notes:
  GND
  SWDCLK
  SWDIO
  3.3V
