# Fritzing sketch LCD16x2 (saved by Fritzing 0.9.2b)
breadboards: 1

parts:
  Part2 = BluePill
  Part3 = FTDI Basic Programmer
  LCD1 = LCD screen
  R1 = Trimmer Potentiometer [maximum_resistance=10kΩ package=THT]
  R2 = Resistor [tolerance=±5% resistance=220 package=THT]

nets:
  N1: Part2.C13, LCD1.DB6
  N2: Part2.C14, LCD1.DB7
  N3: Part2.B0, LCD1.DB4
  N4: Part2.B10, LCD1.E
  N5: Part2.B11, LCD1.RS
  GND: Part2.GND3, Part3.GND, LCD1.VSS, LCD1.R/W, LCD1.LED-, R1.leg1
  VCC: Part2.5V, Part3.POWER, LCD1.VDD, R1.leg2, R2.Pin_0
  N6: Part2.A10, Part3.TXO
  N7: Part2.A9, Part3.RXI
  N8: Part2.B1, LCD1.DB5
  N9: LCD1.V0, R1.wiper
  N10: LCD1.LED+, R2.Pin_1
