# Fritzing sketch ElectretPreamp (saved by Fritzing 0.9.2b)
breadboards: 1

parts:
  MIC1 = Microphone
  R1 = Resistor [tolerance=±5% resistance=2.2k package=THT]
  R2 = Resistor [tolerance=±5% resistance=10k package=THT]
  U1 = LM 358 Dual Op-Amp [part_number=LM358 package="DIP8 [THT]"]
  C1 = Ceramic Capacitor [capacitance=220nF package="100 mil [THT, multilayer]"]
  R3 = Resistor [tolerance=±5% resistance=10k package=THT]
  R4 = Resistor [tolerance=±5% resistance=10k package=THT]
  R5 = Resistor [tolerance=±5% resistance=330k package=THT]
  5V = Power plug
  R6 = Trimmer Potentiometer [maximum_resistance=500kΩ package=THT]
  C3 = Ceramic Capacitor [capacitance=100nF package="100 mil [THT, multilayer]"]
  C2 = Electrolytic Capacitor [capacitance=4.7µF package="100 mil [THT, electrolytic]"]
  C4 = Electrolytic Capacitor [capacitance=4.7µF package="100 mil [THT, electrolytic]"]

nets:
  N1: MIC1.pin1, R1.Pin_1, C1.1
  GND: MIC1.pin2, U1.connector3, R4.Pin_1, 5V.GND, C3.1, C2.-
  5V: R1.Pin_0, U1.connector7, R3.Pin_0, 5V.VCC, C3.0
  N2: R2.Pin_0, C1.0
  N3: R2.Pin_1, U1.connector1, R5.Pin_0
  AOUT-DC: U1.connector0, R6.leg1, R6.wiper, C4.+
  N4: U1.connector2, R3.Pin_1, R4.Pin_0, C2.+
  N5: R5.Pin_1, R6.leg2
  AOUT-AC: C4.-

notes:
  AIN
  AOUT (AC)
  AOUT (DC)
