# Fritzing sketch ElectretSoundDetectionModule (saved by Fritzing 0.9.2b)
breadboards: 1

parts:
  U1 = LM 358 Dual Op-Amp [part_number=LM393 package="DIP8 [THT]"]
  MIC1 = Microphone
  C4 = Ceramic Capacitor [capacitance=100nF package="100 mil [THT, multilayer]"]
  LED1 = LED - 3mm [color="Red (633nm)" package="3 mm [THT]"]
  R8 = Resistor [tolerance=±5% resistance=1k package=THT]
  R7 = Resistor [tolerance=±5% resistance=1k package=THT]
  LED2 = LED - 3mm [color="Green (555nm)" package="3 mm [THT]"]
  J1 = female pin header, 3 pins [form="♀ (female)"]
  R6 = Resistor [tolerance=±5% resistance=10k package=THT]
  R3 = Resistor [tolerance=±5% resistance=510k package=THT]
  Q1 = NPN-Transistor [part_number=S9014 package="TO92 [THT]"]
  C2 = Ceramic Capacitor [capacitance=100nF package="100 mil [THT, multilayer]"]
  C3 = Ceramic Capacitor [capacitance=100nF package="100 mil [THT, multilayer]"]
  R5 = Trimmer Potentiometer [maximum_resistance=10kΩ package=THT]
  R4 = Resistor [tolerance=±5% resistance=1k package=THT]
  R2 = Resistor [tolerance=±5% resistance=51k package=THT]
  C1 = Ceramic Capacitor [capacitance=100nF package="100 mil [THT, multilayer]"]
  R1 = Resistor [tolerance=±5% resistance=10k package=THT]

nets:
  DO: U1.connector0, R7.Pin_0, J1.pin1, R6.Pin_0
  N1: U1.connector1, Q1.C, C3.0, R4.Pin_0
  N2: U1.connector2, R5.wiper
  GND: U1.connector3, MIC1.pin1, C4.1, R8.Pin_1, J1.pin2, Q1.E, C3.1, R5.leg2, R2.Pin_0, C1.0
  VCC: U1.connector7, C4.0, LED1.anode, LED2.anode, J1.pin3, R6.Pin_1, R3.Pin_1, R5.leg1, R4.Pin_1, R1.Pin_0
  N3: MIC1.pin2, C2.0, R2.Pin_1, C1.1, R1.Pin_1
  N4: LED1.cathode, R8.Pin_0
  N5: R7.Pin_1, LED2.cathode
  N6: R3.Pin_0, Q1.B, C2.1
