# Fritzing sketch GeneralPurpose358 (saved by Fritzing 0.9.2b)
breadboards: 1

parts:
  JOUT = Audio Jack (TRS) 3.5mm [package="4Ucon 08780 [THT]"]
  JIN = AMPHENOL - ACJS-MHDR [package=ACJS-MHDR]
  U1 = LM 358 Dual Op-Amp [part_number=LM358 package="DIP8 [THT]"]
  C1 = Ceramic Capacitor [capacitance=10nF package="100 mil [THT, multilayer]"]
  R1 = Resistor [tolerance=±5% resistance=1M package=THT]
  R2 = Resistor [tolerance=±5% resistance=3.3k package=THT]
  C2 = Electrolytic Capacitor [capacitance=1µF package="100 mil [THT, electrolytic]"]
  R3 = Resistor [tolerance=±5% resistance=3.3k package=THT]
  C3 = Ceramic Capacitor [capacitance=10nF package="100 mil [THT, multilayer]"]
  R4 = Resistor [tolerance=±5% resistance=1M package=THT]
  R5 = Resistor [tolerance=±5% resistance=1M package=THT]
  R6 = Resistor [tolerance=±5% resistance=10k package=THT]
  R7 = Resistor [tolerance=±5% resistance=6.8k package=THT]
  R8 = Resistor [tolerance=±5% resistance=1M package=THT]
  D2 = Rectifier Diode [part_number=1N4148 package="300 mil [THT]"]
  R9 = Resistor [tolerance=±5% resistance=1k package=THT]
  Q1 = NPN-Transistor [part_number=2N3904 package="TO92 [THT]"]
  R10 = Resistor [tolerance=±5% resistance=4.7 package=THT]
  R11 = Resistor [tolerance=±5% resistance=4.7 package=THT]
  Q2 = PNP-Transistor [part_number=2N3905 package="TO92 [THT]"]
  C4 = Electrolytic Capacitor [capacitance=220µF package="100 mil [THT, electrolytic]"]
  C5 = Electrolytic Capacitor [capacitance=100µF package="100 mil [THT, electrolytic]"]
  D1 = Rectifier Diode [part_number=1N4148 package="300 mil [THT]"]
  5V = Power plug

nets:
  GND: JOUT.Sleeve, JIN.Sleeve_(1), U1.connector3, C1.0, R1.Pin_1, R7.Pin_1, Q2.C, C5.-
  N1: JOUT.Ring, JOUT.Tip, C4.-
  N2: JIN.Ring_(2), 5V.GND
  N3: JIN.Tip_(3), C3.0
  N4: U1.connector0, R8.Pin_1, Q2.B, D1.cathode
  N5: U1.connector1, R3.Pin_0, R8.Pin_0
  N6: U1.connector2, C3.1, R5.Pin_1
  N7: U1.connector4, C1.1, R4.Pin_1
  N8: U1.connector5, R1.Pin_0, R2.Pin_0
  N9: U1.connector6, R2.Pin_1, C2.+
  VCC: U1.connector7, R6.Pin_0, R9.Pin_0, Q1.C, C5.+, 5V.VCC
  N10: C2.-, R3.Pin_1
  Vref: R4.Pin_0, R5.Pin_0, R6.Pin_1, R7.Pin_0
  N11: D2.cathode, D1.anode
  N12: D2.anode, R9.Pin_1, Q1.B
  N13: Q1.E, R10.Pin_0
  N14: R10.Pin_1, R11.Pin_1, C4.+
  N15: R11.Pin_0, Q2.E

notes:
  Ring/sleeve switches power on with mono cable connected
