# Fritzing sketch GuitarHeadphoneAmp (saved by Fritzing 0.9.2b)
breadboards: 1

parts:
  VCC1 = Battery block 9V
  CPS2 = Electrolytic Capacitor [capacitance=100µF package="100 mil [THT, electrolytic]"]
  IC1 = LM386 [package=dip08]
  C4 = Electrolytic Capacitor [capacitance=220µF package="100 mil [THT, electrolytic]"]
  RPS1 = Resistor [tolerance=±5% resistance=1k package=THT]
  LED1 = LED - 3mm [color="Green (555nm)" package="3 mm [THT]"]
  R2 = Resistor [tolerance=±5% resistance=10 package=THT]
  C5 = Ceramic Capacitor [capacitance=100nF package="100 mil [THT, multilayer]"]
  JOUT = Audio Jack (TRS) 3.5mm [package="4Ucon 08780 [THT]"]
  C1 = Ceramic Capacitor [capacitance=1µF package="100 mil [THT, multilayer]"]
  CPS1 = Ceramic Capacitor [capacitance=100nF package="100 mil [THT, multilayer]"]
  R1 = Resistor [tolerance=±5% resistance=47k package=THT]
  JIN = AMPHENOL - ACJS-MHDR [package=ACJS-MHDR]

nets:
  N1: VCC1.-, JIN.Ring_(2)
  N2: VCC1.+, CPS2.+, IC1.Vs, RPS1.Pin_0, CPS1.1
  GND: CPS2.-, IC1.-INPUT, IC1.GND, LED1.cathode, C5.0, JOUT.Sleeve, CPS1.0, R1.Pin_1, JIN.Sleeve_(1)
  N3: IC1.+INPUT, C1.1
  N4: IC1.Vout, C4.+, R2.Pin_0
  N5: C4.-, JOUT.Ring, JOUT.Tip
  N6: RPS1.Pin_1, LED1.anode
  N7: R2.Pin_1, C5.1
  N8: C1.0, R1.Pin_0, JIN.Tip_(3)

notes:
  Ring/sleeve switches power on with mono cable connected

custom parts:
  LM386: low voltage audio power amplifier
