# Fritzing sketch GuitarPracticeAmp (saved by Fritzing 0.9.2b)
breadboards: 1

parts:
  U1 = TL072/TLE2072 Dual Op. Amp [part_number=TL072 package="DIP8 [THT]"]
  J2 = AMPHENOL - ACJS-MHDR [package=ACJS-MHDR]
  J1 = Power plug [part_number=12V]
  R1 = Resistor [tolerance=±5% resistance=1M package=THT]
  C1 = Electrolytic Capacitor [capacitance=1µF package="100 mil [THT, electrolytic]"]
  C2 = Ceramic Capacitor [capacitance=47nF package="100 mil [THT, multilayer]"]
  R2 = Resistor [tolerance=±5% resistance=5.6k package=THT]
  R3 = Resistor [tolerance=±5% resistance=1M package=THT]
  R4 = Resistor [tolerance=±5% resistance=1M package=THT]
  R5 = Resistor [tolerance=±5% resistance=1k package=THT]
  R10 = Trimmer Potentiometer [maximum_resistance=50kΩ part_number=B50kΩ package=THT]
  C3 = Ceramic Capacitor [capacitance=10nF package="100 mil [THT, multilayer]"]
  R6 = Resistor [tolerance=±5% resistance=4.7k package=THT]
  D1 = Rectifier Diode [part_number=1N4001 package="300 mil [THT]"]
  D2 = Rectifier Diode [part_number=1N4001 package="300 mil [THT]"]
  R11 = Trimmer Potentiometer [maximum_resistance=10kΩ part_number=B10kΩ package=THT]
  C4 = Electrolytic Capacitor [capacitance=1µF package="100 mil [THT, electrolytic]"]
  R12 = Trimmer Potentiometer [maximum_resistance=10kΩ part_number=A10kΩ package=THT]
  C5 = Electrolytic Capacitor [capacitance=1µF package="100 mil [THT, electrolytic]"]
  U2 = IC, DIP package, 6 pins [chip_label=TDA2050]
  R7 = Resistor [tolerance=±5% resistance=22k package=THT]
  R14 = Resistor [tolerance=±5% resistance=22k package=THT]
  R16 = Resistor [tolerance=±5% resistance=22k package=THT]
  C11 = Electrolytic Capacitor [capacitance=1µF package="100 mil [THT, electrolytic]"]
  R8 = Resistor [tolerance=±5% resistance=10k package=THT]
  C6 = Electrolytic Capacitor [capacitance=10µF package="100 mil [THT, electrolytic]"]
  R9 = Resistor [tolerance=±5% resistance=100k package=THT]
  R13 = Resistor [tolerance=±5% resistance=1 package=THT]
  C7 = Ceramic Capacitor [capacitance=220nF package="100 mil [THT, multilayer]"]
  C8 = Electrolytic Capacitor [capacitance=1mF package="100 mil [THT, electrolytic]"]
  SPKR1 = Loudspeaker
  C10 = Ceramic Capacitor [capacitance=100nF package="100 mil [THT, multilayer]"]
  C9 = Electrolytic Capacitor [capacitance=100µF package="100 mil [THT, electrolytic]"]
  R15 = Resistor [tolerance=±5% resistance=2.2k package=THT]
  LED1 = LED - 3mm [color="Red (633nm)" package="3 mm [THT]"]
  S1 = Toggle Switch [package=THT]

nets:
  N1: U1.Pin_1, R5.Pin_1, R10.leg2, C3.0
  N2: U1.Pin_2, R2.Pin_1, R10.leg1
  VREF: U1.Pin_3, U1.Pin_5, C1.+, R3.Pin_1, R4.Pin_0
  GND: U1.Pin_4, J2.Sleeve_(1), J1.GND, R1.Pin_1, C1.-, R4.Pin_1, R12.leg2, U2.pin3, R16.Pin_0, C11.-, C6.-, C7.0, SPKR1.pin2, C10.0, C9.-, LED1.cathode
  N3: U1.Pin_6, R5.Pin_0, R6.Pin_0, D1.anode, D2.cathode
  N4: U1.Pin_7, D1.cathode, D2.anode, R11.leg1, R11.wiper, C4.+
  VDD: U1.Pin_8, R3.Pin_0, U2.pin5, R14.Pin_1, C10.1, C9.+, R15.Pin_1, S1.L2
  N5: J2.Tip_(3), R1.Pin_0, C2.0
  N6: J1.VCC, S1.COM
  N7: C2.1, R2.Pin_0
  N8: R10.wiper, C3.1
  N9: R6.Pin_1, R11.leg2
  N10: C4.-, R12.leg1
  N11: R12.wiper, C5.-
  N12: C5.+, U2.pin1, R7.Pin_1
  N13: U2.pin2, R8.Pin_1, R9.Pin_0
  N14: U2.pin4, R9.Pin_1, R13.Pin_1, C8.+
  N15: R7.Pin_0, R14.Pin_0, R16.Pin_1, C11.+
  N16: R8.Pin_0, C6.+
  N17: R13.Pin_0, C7.1
  N18: C8.-, SPKR1.pin1
  N19: R15.Pin_0, LED1.anode

custom parts:
  TL072/TLE2072 Dual Op. Amp: The classic LM 358 Dual Operational Amplifier (Op-Amp). The analog swiss-army knife.
