# Fritzing sketch LittleGem (saved by Fritzing 1.0.7)
breadboards: 1

parts:
  Power = Battery block 9V [internal_resistance=0.1Ω]
  D1 = Rectifier Diode [part_number=1N4001 package="300 mil [THT]"]
  C1 = Electrolytic Capacitor [capacitance=100µF voltage=35V package="100 mil [THT, electrolytic]"]
  R1 = Trimmer Potentiometer [maximum_resistance=5kΩ knob_status=50% power=0.5W package=THT]
  C2 = Electrolytic Capacitor [capacitance=220µF voltage=35V package="100 mil [THT, electrolytic]"]
  R2 = Trimmer Potentiometer [maximum_resistance=2kΩ knob_status=50% power=0.5W package=THT]
  R3 = Resistor [tolerance=±5% resistance=470 power=0.25W package=THT]
  LED1 = LED - 3mm [color="Green (555nm)" current=0.030A package="3 mm [THT]"]
  R4 = Resistor [tolerance=±5% resistance=10 power=0.25W package=THT]
  C3 = Ceramic Capacitor [capacitance=47nF voltage=35V package="100 mil [THT, multilayer]"]
  JIN = Audio Jack (TRS) 3.5mm [package="4Ucon 08780 [THT]"]
  C4 = Ceramic Capacitor [capacitance=10nF voltage=35V package="100 mil [THT, multilayer]"]
  SPKR1 = Loudspeaker
  R5 = Resistor [tolerance=±5% resistance=22 power=0.25W package=THT]
  U1 = LM386 [part_number=LM386 package=dip08]

nets:
  GND: Power.-, C1.-, R2.leg2, LED1.cathode, C3.0, JIN.Sleeve, SPKR1.pin2, R5.Pin_1, U1.+IN, U1.V-
  N1: Power.+, D1.anode
  9V: D1.cathode, C1.+, R3.Pin_0, U1.V+
  N2: R1.wiper, R1.leg2, U1.GAIN
  N3: C2.-, R2.leg1, R5.Pin_0
  N4: C2.+, R4.Pin_0, U1.OUT
  N5: R2.wiper, SPKR1.pin1
  N6: R3.Pin_1, LED1.anode
  N7: R4.Pin_1, C3.1
  N8: JIN.Tip, C4.0
  N9: C4.1, U1.-IN
