# Fritzing sketch Ruby (saved by Fritzing 0.9.2b)
breadboards: 1

parts:
  VCC1 = Battery block 9V
  D1 = Rectifier Diode [part_number=1N4001 package="300 mil [THT]"]
  C1 = Electrolytic Capacitor [capacitance=100µF package="100 mil [THT, electrolytic]"]
  IC1 = LM386 [package=dip08]
  R1 = Trimmer Potentiometer [maximum_resistance=5kΩ package=THT]
  C2 = Electrolytic Capacitor [capacitance=220µF package="100 mil [THT, electrolytic]"]
  R3 = Resistor [tolerance=±5% resistance=1k package=THT]
  LED1 = LED - 3mm [color="Green (555nm)" package="3 mm [THT]"]
  R4 = Resistor [tolerance=±5% resistance=10 package=THT]
  C3 = Ceramic Capacitor [capacitance=47nF package="100 mil [THT, multilayer]"]
  JIN = Audio Jack (TRS) 3.5mm [package="4Ucon 08780 [THT]"]
  C4 = Ceramic Capacitor [capacitance=47nF package="100 mil [THT, multilayer]"]
  SPKR1 = Loudspeaker
  Q1 = 2N7000 FET N-Channel [part_number=J201 package=TO92]
  R5 = Resistor [tolerance=±5% resistance=3.3k package=THT]
  R6 = Resistor [tolerance=±5% resistance=1M package=THT]
  R7 = Trimmer Potentiometer [maximum_resistance=10kΩ package=THT]
  C5 = Ceramic Capacitor [capacitance=100nF package="100 mil [THT, multilayer]"]
  C6 = Ceramic Capacitor [capacitance=100nF package="100 mil [THT, multilayer]"]
  C7 = Ceramic Capacitor [capacitance=100nF package="100 mil [THT, multilayer]"]

nets:
  GND: VCC1.-, C1.-, IC1.+INPUT, IC1.GND, LED1.cathode, C3.0, JIN.Sleeve, SPKR1.pin2, R5.Pin_1, R6.Pin_1, R7.leg2, C5.0, C7.1
  N1: VCC1.+, D1.anode
  VSS: D1.cathode, C1.+, IC1.Vs, R3.Pin_0, Q1.drain, C5.1
  N2: IC1.GAIN, R1.wiper, R1.leg2
  N3: IC1.-INPUT, R7.wiper
  N4: IC1.Vout, C2.+, R4.Pin_0
  N5: IC1.BYPASS, C7.0
  N6: C2.-, SPKR1.pin1
  N7: R3.Pin_1, LED1.anode
  N8: R4.Pin_1, C3.1
  N9: JIN.Tip, C6.0
  N10: C4.0, Q1.source, R5.Pin_0
  N11: C4.1, R7.leg1
  N12: Q1.gate, R6.Pin_0, C6.1

custom parts:
  LM386: low voltage audio power amplifier
  2N7000 FET N-Channel: A 2N7000 MOSFET N-Channel Transistor
