# Fritzing sketch Smokey (saved by Fritzing 0.9.2b)
breadboards: 1

parts:
  VCC1 = Battery block 9V
  IC1 = LM386 [package=dip08]
  C2 = Electrolytic Capacitor [capacitance=47µF package="100 mil [THT, electrolytic]"]
  JIN = Audio Jack (TRS) 3.5mm [package="4Ucon 08780 [THT]"]
  SPKR1 = Loudspeaker
  C1 = Electrolytic Capacitor [capacitance=47µF package="100 mil [THT, electrolytic]"]
  C3 = Electrolytic Capacitor [capacitance=100µF package="100 mil [THT, electrolytic]"]

nets:
  GND: VCC1.-, IC1.-INPUT, IC1.GND, JIN.Sleeve, SPKR1.pin2, C1.-, C3.-
  N1: VCC1.+, IC1.Vs, C3.+
  N2: IC1.+INPUT, JIN.Tip
  N3: IC1.Vout, C2.+
  N4: IC1.BYPASS, C1.+
  N5: C2.-, SPKR1.pin1

custom parts:
  LM386: low voltage audio power amplifier
