# Fritzing sketch VolumeControlPowerAmp (saved by Fritzing 0.9.2b)
breadboards: 1

parts:
  VCC1 = Battery block 9V
  CPS2 = Electrolytic Capacitor [capacitance=100µF package="100 mil [THT, electrolytic]"]
  IC1 = LM386 [package=dip08]
  C4 = Electrolytic Capacitor [capacitance=100µF package="100 mil [THT, electrolytic]"]
  RPS1 = Resistor [tolerance=±5% resistance=1k package=THT]
  LED1 = LED - 3mm [color="Green (555nm)" package="3 mm [THT]"]
  R2 = Resistor [tolerance=±5% resistance=10 package=THT]
  C3 = Ceramic Capacitor [capacitance=100nF package="100 mil [THT, multilayer]"]
  JIN = Audio Jack (TRS) 3.5mm [package="4Ucon 08780 [THT]"]
  C1 = Ceramic Capacitor [capacitance=100nF package="100 mil [THT, multilayer]"]
  SPKR1 = Loudspeaker
  C5 = Electrolytic Capacitor [capacitance=10µF package="100 mil [THT, electrolytic]"]
  CPS1 = Ceramic Capacitor [capacitance=100nF package="100 mil [THT, multilayer]"]
  R1 = Trimmer Potentiometer [maximum_resistance=10kΩ package=THT]
  C2 = Ceramic Capacitor [capacitance=1nF package="100 mil [THT, multilayer]"]

nets:
  GND: VCC1.-, CPS2.-, IC1.+INPUT, IC1.GND, LED1.cathode, C3.0, JIN.Sleeve, SPKR1.pin2, CPS1.0, R1.leg2, C2.0
  N1: VCC1.+, CPS2.+, IC1.Vs, RPS1.Pin_0, CPS1.1
  N2: IC1.GAIN, C5.-, C5.+
  N3: IC1.-INPUT, R1.wiper, C2.1
  N4: IC1.Vout, C4.+, R2.Pin_0
  N5: C4.-, SPKR1.pin1
  N6: RPS1.Pin_1, LED1.anode
  N7: R2.Pin_1, C3.1
  N8: JIN.Tip, C1.0
  N9: C1.1, R1.leg1

custom parts:
  LM386: low voltage audio power amplifier
