# Fritzing sketch CANary (saved by Fritzing 0.9.2b)
breadboards: 1

parts:
  IC1 = Hex Inverter Schmitt Trigger SN74HC14 [package="DIP (Dual Inline)"]
  3_3V = Power plug
  C1 = Electrolytic Capacitor [capacitance=1µF package="100 mil [THT, electrolytic]"]
  C2 = Electrolytic Capacitor [capacitance=1µF package="100 mil [THT, electrolytic]"]
  C3 = Electrolytic Capacitor [capacitance=47µF package="100 mil [THT, electrolytic]"]
  J1 = Piezo Speaker
  R1 = Resistor [tolerance=±5% resistance=10M package=THT]
  R2 = Resistor [tolerance=±5% resistance=10M package=THT]
  R3 = Resistor [tolerance=±5% resistance=100k package=THT]
  R4 = Resistor [tolerance=±5% resistance=5M package=THT]
  D1 = Rectifier Diode [part_number=1N4148 package="300 mil [THT]"]
  D2 = Rectifier Diode [part_number=1N4148 package="300 mil [THT]"]
  R5 = Resistor [tolerance=±5% resistance=2k package=THT]
  LDR1 = Photocell (LDR) [package=THT]
  C4 = Electrolytic Capacitor [capacitance=1µF package="100 mil [THT, electrolytic]"]
  R6 = Resistor [tolerance=±5% resistance=100k package=THT]
  R7 = Resistor [tolerance=±5% resistance=100k package=THT]
  R8 = Resistor [tolerance=±5% resistance=2k package=THT]
  C5 = Ceramic Capacitor [capacitance=1nF package="100 mil [THT, multilayer]"]
  C6 = Ceramic Capacitor [capacitance=1nF package="100 mil [THT, multilayer]"]
  D3 = Rectifier Diode [part_number=1N4148 package="300 mil [THT]"]

nets:
  N1: IC1.1A, C1.+, R1.Pin_1, R4.Pin_1
  N2: IC1.1Y, R1.Pin_0, D1.cathode, D3.cathode
  N3: IC1.2A, C2.+, R2.Pin_1
  N4: IC1.2Y, R2.Pin_0, D2.anode
  N5: IC1.3A, C3.+, R3.Pin_1, D2.cathode, R5.Pin_0
  N6: IC1.3Y, R3.Pin_0, LDR1.pin_0, C4.-
  GND: IC1.GND, 3_3V.GND, C1.-, C2.-, C3.-
  N7: IC1.4Y, C6.1
  N8: IC1.4A, R6.Pin_1, C5.1
  N9: IC1.5Y, R8.Pin_0, C5.0
  N10: IC1.5A, R7.Pin_1, C6.0, D3.anode
  N11: IC1.6Y, J1.pin2
  N12: IC1.6A, J1.pin1, R8.Pin_1
  VCC: IC1.VCC, 3_3V.VCC
  N13: R4.Pin_0, D1.anode
  N14: R5.Pin_1, LDR1.pin_1
  N15: C4.+, R6.Pin_0, R7.Pin_0
