# Fritzing sketch JetEngine (saved by Fritzing 0.9.2b)
breadboards: 1

parts:
  9-9_5V = Power plug
  L1 = Inductor [inductance=100µH package="400 mil [THT]"]
  C2 = Ceramic Capacitor [capacitance=1µF package="100 mil [THT, multilayer]"]
  R1 = Resistor [tolerance=±5% resistance=1M package=THT]
  C1 = Ceramic Capacitor [capacitance=10nF package="100 mil [THT, multilayer]"]
  Q1 = NPN-Transistor [part_number=BC337 package="TO92 [THT]"]
  Q2 = NPN-Transistor [part_number=BC337 package="TO92 [THT]"]
  C3 = Ceramic Capacitor [capacitance=100nF package="100 mil [THT, multilayer]"]
  R2 = Resistor [tolerance=±5% resistance=100k package=THT]
  R3 = Resistor [tolerance=±5% resistance=1M package=THT]
  C4 = Ceramic Capacitor [capacitance=100nF package="100 mil [THT, multilayer]"]
  IC2 = IC, DIP package, 16 pins [chip_label=CD4046]
  C5 = Ceramic Capacitor [capacitance=100nF package="100 mil [THT, multilayer]"]
  R4 = Resistor [tolerance=±5% resistance=680k package=THT]
  R5 = Resistor [tolerance=±5% resistance=47k package=THT]
  R6 = Resistor [tolerance=±5% resistance=4.7k package=THT]
  C6 = Ceramic Capacitor [capacitance=100nF package="100 mil [THT, multilayer]"]
  R7 = Resistor [tolerance=±5% resistance=100k package=THT]
  C7 = Electrolytic Capacitor [capacitance=47µF voltage=16V package="100 mil [THT, electrolytic]"]
  IC3 = LM386 [part_number=LM386 package=dip08]
  R8 = Trimmer Potentiometer [maximum_resistance=10kΩ package=THT]
  C8 = Electrolytic Capacitor [capacitance=100µF voltage=25V package="100 mil [THT, electrolytic]"]
  J1 = Piezo Speaker

nets:
  GND: 9-9_5V.GND, L1.pin_1, C2.1, Q2.E, IC2.pin5, IC2.pin8, R5.Pin_1, R6.Pin_1, C7.-, IC3.-INPUT, IC3.GND, R8.leg2, J1.pin1
  VCC: 9-9_5V.VCC, R1.Pin_1, C1.0, R2.Pin_0, IC2.pin16, R7.Pin_1, IC3.Vs
  N1: L1.pin_0, C2.0, C1.1, Q1.B
  N2: R1.Pin_0, Q1.E, C3.0
  N3: Q2.B, C3.1, R3.Pin_0
  N4: Q2.C, R2.Pin_1, R3.Pin_1, C4.0
  MIX_OUT/NOISE_OUT: C4.1, R4.Pin_1, R8.leg1
  N5: IC2.pin3, IC2.pin4, C5.0
  N6: IC2.pin6, C6.1
  N7: IC2.pin7, C6.0
  N8: IC2.pin9, R7.Pin_0, C7.+
  N9: IC2.pin11, R6.Pin_0
  N10: IC2.pin12, R5.Pin_0
  VCO_OUT: C5.1, R4.Pin_0
  N11: IC3.+INPUT, R8.wiper
  N12: IC3.Vout, C8.+
  N13: C8.-, J1.pin2

custom parts:
  LM386: low voltage audio power amplifier
