# Fritzing sketch WhiteNoiseGenerator (saved by Fritzing 0.9.2b)
breadboards: 1

parts:
  R1 = Resistor [tolerance=±5% resistance=1M package=THT]
  9V = Power plug
  C1 = Ceramic Capacitor [capacitance=100nF package="100 mil [THT, multilayer]"]
  R2 = Resistor [tolerance=±5% resistance=1M package=THT]
  R3 = Resistor [tolerance=±5% resistance=100k package=THT]
  C2 = Ceramic Capacitor [capacitance=100nF package="100 mil [THT, multilayer]"]
  R6 = Trimmer Potentiometer [maximum_resistance=10kΩ package=THT]
  C5 = Electrolytic Capacitor [capacitance=10µF package="100 mil [THT, electrolytic]"]
  R7 = Resistor [tolerance=±5% resistance=100k package=THT]
  R8 = Resistor [tolerance=±5% resistance=470 package=THT]
  C6 = Electrolytic Capacitor [capacitance=100µF package="100 mil [THT, electrolytic]"]
  TRS1 = Audio Jack (TRS) 3.5mm [package="4Ucon 08780 [THT]"]
  Q1 = NPN-Transistor [package="TO92 [THT]"]
  Q2 = NPN-Transistor [package="TO92 [THT]"]
  Q4 = NPN-Transistor [package="TO92 [THT]"]

nets:
  GND: R1.Pin_0, 9V.GND, R6.leg2, R8.Pin_1, TRS1.Sleeve, Q2.E
  N1: R1.Pin_1, C1.0, Q1.B
  N2: 9V.VCC, R3.Pin_1, R7.Pin_1, Q1.E, Q4.C
  N3: C1.1, R2.Pin_1, Q2.B
  N4: R2.Pin_0, R3.Pin_0, C2.0, Q2.C
  N5: C2.1, R6.leg1
  N6: R6.wiper, C5.-
  N7: C5.+, R7.Pin_0, Q4.B
  N8: R8.Pin_0, C6.+, Q4.E
  N9: C6.-, TRS1.Ring, TRS1.Tip
