# Fritzing sketch ZenerModeEffects (saved by Fritzing 0.9.2b)
breadboards: 1

parts:
  9V = Power plug
  Q2 = NPN-Transistor [part_number=A42 package="TO92 [THT]"]
  Q3 = NPN-Transistor [part_number=A42 package="TO92 [THT]"]
  Q4 = PNP-Transistor [part_number=A92 package="TO92 [THT]"]
  D1 = Rectifier Diode [part_number=1N4001 package="300 mil [THT]"]
  Q5 = NPN-Transistor [part_number=A42 package="TO92 [THT]"]
  C1 = Electrolytic Capacitor [capacitance=22µF package="100 mil [THT, electrolytic]"]
  SPKR1 = Loudspeaker
  D2 = Rectifier Diode [part_number=1N4001 package="300 mil [THT]"]
  C2 = Electrolytic Capacitor [capacitance=100µF package="100 mil [THT, electrolytic]"]
  C3 = Electrolytic Capacitor [capacitance=4.7µF package="100 mil [THT, electrolytic]"]
  S1 = Pushbutton [package="[THT]"]
  R1 = Resistor [tolerance=±5% resistance=2.2k package=THT]
  R2 = Resistor [tolerance=±5% resistance=1M package=THT]
  R3 = Resistor [tolerance=±5% resistance=1M package=THT]
  C4 = Ceramic Capacitor [capacitance=100nF package="100 mil [THT, multilayer]"]
  R4 = Resistor [tolerance=±5% resistance=10k package=THT]
  C5 = Ceramic Capacitor [capacitance=100nF package="100 mil [THT, multilayer]"]
  R5 = Resistor [tolerance=±5% resistance=1k package=THT]
  R6 = Resistor [tolerance=±5% resistance=100k package=THT]
  Q1 = NPN-Transistor [part_number=A42 package="TO92 [THT]"]

nets:
  N1: 9V.GND, D2.cathode, S1.Pin_1, S1.Pin_2, R1.Pin_1
  N2: 9V.VCC, Q5.C, C2.+, R2.Pin_0, R4.Pin_0, R5.Pin_0
  N3: Q2.E, Q3.E, Q4.C, SPKR1.pin2, C2.-, C3.+, S1.Pin_3, S1.Pin_4, R1.Pin_0
  N4: Q2.B, R3.Pin_1, C4.1
  N5: Q2.C, R3.Pin_0, R4.Pin_1, C5.0
  N6: Q3.B, C5.1, R6.Pin_0
  N7: Q3.C, Q4.B, D1.cathode
  N8: Q4.E, Q5.E, C1.+, R6.Pin_1
  N9: D1.anode, Q5.B, R5.Pin_1
  N10: C1.-, SPKR1.pin1
  N11: D2.anode, C3.-, Q1.B
  N12: R2.Pin_1, C4.0, Q1.E
