# Fritzing sketch Amplified (saved by Fritzing 0.9.2b)
breadboards: 1

parts:
  HS088 = female pin header, 5 pins [form="♀ (female)"]
  3V = LilyPad Coin Cell Battery Holder
  Q1 = NPN-Transistor [part_number=2N3904 package="TO92 [THT]"]
  S1 = Pushbutton [package="[THT]"]
  C1 = Ceramic Capacitor [capacitance=100nF package="100 mil [THT, multilayer]"]
  R1 = Resistor [tolerance=±5% resistance=10k package=THT]
  C2 = Electrolytic Capacitor [capacitance=47µF package="100 mil [THT, electrolytic]"]
  Q2 = NPN-Transistor [part_number=2N3904 package="TO92 [THT]"]
  R2 = Resistor [tolerance=±5% resistance=4.7k package=THT]
  R3 = Resistor [tolerance=±5% resistance=4.7k package=THT]
  R4 = Resistor [tolerance=±5% resistance=6.8k package=THT]
  Q3 = PNP-Transistor [part_number=2N3906 package="TO92 [THT]"]
  Q4 = NPN-Transistor [part_number=2N3904 package="TO92 [THT]"]
  C3 = Electrolytic Capacitor [capacitance=220µF package="100 mil [THT, electrolytic]"]
  SPKR1 = Loudspeaker
  R5 = Resistor [tolerance=±5% resistance=1k package=THT]
  D1 = Rectifier Diode [part_number=1N4148 package="300 mil [THT]"]
  D2 = Rectifier Diode [part_number=1N4148 package="300 mil [THT]"]
  R6 = Trimmer Potentiometer [maximum_resistance=10kΩ package=THT]

nets:
  3V: HS088.pin1, 3V.+, S1.Pin_1, S1.Pin_2, Q4.C, R5.Pin_0
  N1: HS088.pin2, C1.1
  N2: HS088.pin3, Q1.C, R6.leg2
  N3: HS088.pin4, Q1.B
  GND: HS088.pin5, 3V.-, Q1.E, R1.Pin_1, Q2.E, R4.Pin_1, Q3.C, SPKR1.pin2, R6.leg1
  N4: S1.Pin_3, S1.Pin_4, C1.0, R1.Pin_0
  N5: C2.-, Q2.B, R3.Pin_1, R4.Pin_0
  N6: C2.+, R6.wiper
  N7: Q2.C, Q3.B, D2.cathode
  N8: R2.Pin_0, Q3.E, Q4.E, C3.+
  N9: R2.Pin_1, R3.Pin_0
  N10: Q4.B, R5.Pin_1, D1.anode
  N11: C3.-, SPKR1.pin1
  N12: D1.cathode, D2.anode
