# Fritzing sketch PropPlane (saved by Fritzing 0.9.2b)
breadboards: 1

parts:
  IC1 = IC, DIP package, 28 pins [chip_label=SN76477]
  9V = Power plug
  R1 = Resistor [tolerance=±5% resistance=10k package=THT]
  R2 = Resistor [tolerance=±5% resistance=47k package=THT]
  C1 = Ceramic Capacitor [capacitance=1nF package="100 mil [THT, multilayer]"]
  C2 = Ceramic Capacitor [capacitance=47nF package="100 mil [THT, multilayer]"]
  R3 = Trimmer Potentiometer [maximum_resistance=500kΩ package=THT]
  R4 = Resistor [tolerance=±5% resistance=100k package=THT]
  R5 = Resistor [tolerance=±5% resistance=100k package=THT]
  Q1 = NPN-Transistor [part_number=2N3904 package="TO92 [THT]"]
  Q2 = PNP-Transistor [part_number=2N3906 package="TO92 [THT]"]
  R6 = Resistor [tolerance=±5% resistance=3.9k package=THT]
  SPKR1 = Loudspeaker
  C3 = Electrolytic Capacitor [capacitance=100µF package="100 mil [THT, electrolytic]"]
  R7 = Resistor [tolerance=±5% resistance=47k package=THT]

nets:
  GND: IC1.pin2, 9V.GND, R1.Pin_0, R2.Pin_0, C1.1, C2.0, R3.leg1, R3.wiper, R5.Pin_0, Q2.C, R6.Pin_0, SPKR1.pin2
  N1: IC1.pin4, R1.Pin_1
  N2: IC1.pin5, R2.Pin_1
  N3: IC1.pin6, C1.0
  N4: IC1.pin11, R5.Pin_1
  N5: IC1.pin12, R7.Pin_0
  N6: IC1.pin13, Q1.B, Q2.B, R6.Pin_1
  VCC: IC1.pin14, 9V.VCC, Q1.C
  N7: IC1.pin15, IC1.pin27, IC1.pin28
  N8: IC1.pin20, R4.Pin_0
  N9: IC1.pin21, C2.1
  N10: R3.leg2, R4.Pin_1
  N11: Q1.E, Q2.E, C3.+, R7.Pin_1
  N12: SPKR1.pin1, C3.-
