# Fritzing sketch GranularSynth (saved by Fritzing 0.9.2b)
breadboards: 1

parts:
  R1 = Rotary Potentiometer (Small) [maximum_resistance=10kΩ package=THT]
  R2 = Rotary Potentiometer (Small) [maximum_resistance=10kΩ package=THT]
  R3 = Rotary Potentiometer (Small) [maximum_resistance=10kΩ package=THT]
  R4 = Rotary Potentiometer (Small) [maximum_resistance=10kΩ package=THT]
  R5 = Rotary Potentiometer (Small) [maximum_resistance=10kΩ package=THT]
  J1 = Audio Jack (TRS) 3.5mm [package="PG203J [THT]"]
  U1 = atmega168 [package=dip]
  XTAL1 = Crystal [frequency="16 Mhz" package=THT]
  C1 = Ceramic Capacitor [capacitance=22pF package="100 mil [THT, multilayer]"]
  C2 = Ceramic Capacitor [capacitance=22pF package="100 mil [THT, multilayer]"]
  R6 = Resistor [tolerance=±5% resistance=470 package=THT]
  LED1 = LED - 3mm [color="Green (570nm)" package="3 mm [THT]"]
  R7 = Resistor [tolerance=±5% resistance=10k package=THT]
  ICSP = shrouded pin header, 6 pins [form="♂ (shrouded male)"]
  7V+ = Power plug
  U2 = Voltage Regulator - 5V [package="TO220 [THT]"]
  D1 = Rectifier Diode [part_number=1N4001 package="300 mil [THT]"]
  C3 = Electrolytic Capacitor [capacitance=100µF package="100 mil [THT, electrolytic]"]
  C4 = Electrolytic Capacitor [capacitance=100µF package="100 mil [THT, electrolytic]"]
  C5 = Ceramic Capacitor [capacitance=100nF package="100 mil [THT, multilayer]"]

nets:
  5V: R1.leg1, R2.leg1, R3.leg1, R4.leg1, R5.leg1, U1.VCC, U1.AVCC, R7.Pin_0, ICSP.pin6, U2.output_voltage, C4.+, C5.1
  OSC1-PITCH: R1.wiper, U1.A0
  GND: R1.leg2, R2.leg2, R3.leg2, R4.leg2, R5.leg2, J1.Sleeve, U1.GND, C1.0, C2.1, LED1.cathode, ICSP.pin4, 7V+.GND, U2.GND, C3.-, C4.-, C5.0
  OSC1-DELAY: R2.wiper, U1.A1
  OSC2-DELAY: R3.wiper, U1.A2
  OSC2-PITCH: R4.wiper, U1.A3
  FREQ: R5.wiper, U1.A4
  N1: J1.Tip, U1.D3_(PWM)
  RESET: U1.RESET, R7.Pin_1, ICSP.pin3
  N2: U1.XLAT1, XTAL1.pin_1, C2.0
  N3: U1.XLAT2, XTAL1.pin_0, C1.1
  MOSI: U1.D11_(PWM), ICSP.pin5
  MISO: U1.D12, ICSP.pin1
  SCK: U1.D13, R6.Pin_0, ICSP.pin2
  N4: R6.Pin_1, LED1.anode
  N5: 7V+.VCC, D1.anode
  N6: U2.input_voltage, D1.cathode, C3.+
