# Fritzing sketch GranularSynth_breadboard (saved by Fritzing 0.9.2b)
breadboards: 1

parts:
  Part1 = Arduino Uno (Rev3)
  R1 = Rotary Potentiometer (Small) [maximum_resistance=10kΩ package=THT]
  R2 = Rotary Potentiometer (Small) [maximum_resistance=10kΩ package=THT]
  R3 = Rotary Potentiometer (Small) [maximum_resistance=10kΩ package=THT]
  R4 = Rotary Potentiometer (Small) [maximum_resistance=10kΩ package=THT]
  R5 = Rotary Potentiometer (Small) [maximum_resistance=10kΩ package=THT]
  TRS1 = Audio Jack (TRS) 3.5mm [package="PG203J [THT]"]

nets:
  N1: Part1.A0, R1.wiper
  N2: Part1.A1, R2.wiper
  N3: Part1.A2, R3.wiper
  N4: Part1.A3, R4.wiper
  N5: Part1.A4/SDA, R5.wiper
  GND: Part1.GND, R1.leg2, R2.leg2, R3.leg2, R4.leg2, R5.leg2, TRS1.Sleeve
  N6: Part1.D3_PWM, TRS1.Tip
  5V: Part1.5V, R1.leg1, R2.leg1, R3.leg1, R4.leg1, R5.leg1
