# Fritzing sketch GreaterSimpleSoundEffects (saved by Fritzing 0.9.2b)
breadboards: 1

parts:
  IC1 = IC, DIP package, 16 pins [chip_label=CD4040 part_number=CD4040]
  3-15V = Power plug
  Q1 = NPN-Transistor [part_number=2N3904 package="TO92 [THT]"]
  Q2 = NPN-Transistor [part_number=2N3904 package="TO92 [THT]"]
  R1 = Resistor [tolerance=±5% resistance=5.6k package=THT]
  R2 = Resistor [tolerance=±5% resistance=12k package=THT]
  R3 = Resistor [tolerance=±5% resistance=22k package=THT]
  R4 = Resistor [tolerance=±5% resistance=47k package=THT]
  R5 = Resistor [tolerance=±5% resistance=100k package=THT]
  R6 = Resistor [tolerance=±5% resistance=220k package=THT]
  R7 = Resistor [tolerance=±5% resistance=470k package=THT]
  R8 = Resistor [tolerance=±5% resistance=820k package=THT]
  R9 = Resistor [tolerance=±5% resistance=820k package=THT]
  R10 = Resistor [tolerance=±5% resistance=5.6k package=THT]
  R11 = Resistor [tolerance=±5% resistance=12k package=THT]
  R12 = Resistor [tolerance=±5% resistance=22k package=THT]
  R13 = Resistor [tolerance=±5% resistance=47k package=THT]
  R14 = Resistor [tolerance=±5% resistance=820k package=THT]
  D1 = Rectifier Diode [part_number=1N4148 package="300 mil [THT]"]
  D2 = Rectifier Diode [part_number=1N4148 package="300 mil [THT]"]
  D3 = Rectifier Diode [part_number=1N4148 package="300 mil [THT]"]
  D4 = Rectifier Diode [part_number=1N4148 package="300 mil [THT]"]
  IC2 = IC, DIP package, 16 pins [chip_label=CD4049 part_number=CD4049]
  C1 = Ceramic Capacitor [capacitance=47nF package="100 mil [THT, multilayer]"]
  C2 = Electrolytic Capacitor [capacitance=100µF package="100 mil [THT, electrolytic]"]
  SPKR1 = Loudspeaker
  Q3 = NPN-Transistor [part_number=2N3904 package="TO92 [THT]"]
  R15 = Photocell (LDR) [part_number=5539 package=THT]
  IC3 = LM386 [part_number=LM386 package=dip08]

nets:
  Q12: IC1.pin1, R13.Pin_0
  Q6: IC1.pin2, R3.Pin_0
  Q5: IC1.pin3, R4.Pin_0
  Q7: IC1.pin4, R2.Pin_0
  Q4: IC1.pin5, R5.Pin_0
  Q3: IC1.pin6, R6.Pin_0
  Q2: IC1.pin7, R7.Pin_0
  GND: IC1.pin8, IC1.pin11, 3-15V.GND, IC2.pin8, SPKR1.pin1, IC3.GND
  Q1: IC1.pin9, R8.Pin_0
  P0: IC1.pin10, IC2.pin3, IC2.pin4, IC2.pin9, IC2.pin11, IC2.pin14, C1.1
  Q9: IC1.pin12, R10.Pin_0
  Q8: IC1.pin13, R1.Pin_0
  Q10: IC1.pin14, R11.Pin_0
  Q11: IC1.pin15, R12.Pin_0
  VDD: IC1.pin16, 3-15V.VCC, IC2.pin1, IC3.Vs
  N1: Q1.E, Q2.E, D1.anode, D4.anode
  N2: Q1.B, R9.Pin_1
  N3: Q1.C, Q2.C, D2.cathode, D3.cathode
  N4: Q2.B, R14.Pin_1
  N5: R1.Pin_1, R2.Pin_1, R3.Pin_1, R4.Pin_1, R5.Pin_1, R6.Pin_1, R7.Pin_1, R8.Pin_1, R9.Pin_0
  N6: R10.Pin_1, R11.Pin_1, R12.Pin_1, R13.Pin_1, R14.Pin_0
  N7: D1.cathode, D3.anode, IC2.pin7, C1.0, Q3.E, R15.pin_1
  N8: D2.anode, D4.cathode, IC2.pin5, IC2.pin6, Q3.C, R15.pin_0
  P1: IC2.pin2, IC2.pin10, IC2.pin12, IC2.pin15, IC3.+INPUT
  N9: C2.-, SPKR1.pin2
  N10: C2.+, IC3.Vout
  TOUCH: Q3.B

notes:
  TOUCH

custom parts:
  LM386: low voltage audio power amplifier
