# Fritzing sketch DelayKit (saved by Fritzing 0.9.2b)
breadboards: 1

parts:
  JDC = Power Jack [package=power_jack_pth_lock]
  IC3 = IC, DIP package, 16 pins [chip_label=PT2399]
  IC2 = TL072/TLE2072 Dual Op. Amp [part_number=TL072 package="DIP8 [THT]"]
  VR1 = Rotary Potentiometer (Small) [maximum_resistance=50kΩ part_number=DELAY package=THT]
  VR2 = Rotary Potentiometer (Small) [maximum_resistance=100kΩ part_number=VOLUME package=THT]
  VR3 = Rotary Potentiometer (Small) [maximum_resistance=20kΩ part_number=REPEAT package=THT]
  S1 = SWITCH-DPDT [package=ms]
  S1c = Toggle Switch [package=THT]
  D1 = Rectifier Diode [part_number=1N4004 package="300 mil [THT]"]
  C1 = Electrolytic Capacitor [capacitance=1µF package="100 mil [THT, electrolytic]"]
  C2 = Electrolytic Capacitor [capacitance=1µF package="100 mil [THT, electrolytic]"]
  C3 = Electrolytic Capacitor [capacitance=1µF package="100 mil [THT, electrolytic]"]
  C4 = Electrolytic Capacitor [capacitance=1µF package="100 mil [THT, electrolytic]"]
  C5 = Electrolytic Capacitor [capacitance=47µF package="100 mil [THT, electrolytic]"]
  C6 = Electrolytic Capacitor [capacitance=47µF package="100 mil [THT, electrolytic]"]
  C7 = Electrolytic Capacitor [capacitance=47µF package="100 mil [THT, electrolytic]"]
  R1 = Resistor [tolerance=±5% resistance=47 package=THT]
  R2 = Resistor [tolerance=±5% resistance=47 package=THT]
  R3 = Resistor [tolerance=±5% resistance=1k package=THT]
  R4 = Resistor [tolerance=±5% resistance=2.7k package=THT]
  R5 = Resistor [tolerance=±5% resistance=12k package=THT]
  R6 = Resistor [tolerance=±5% resistance=12k package=THT]
  R7 = Resistor [tolerance=±5% resistance=12k package=THT]
  R8 = Resistor [tolerance=±5% resistance=12k package=THT]
  R9 = Resistor [tolerance=±5% resistance=12k package=THT]
  R10 = Resistor [tolerance=±5% resistance=12k package=THT]
  R11 = Resistor [tolerance=±5% resistance=12k package=THT]
  R12 = Resistor [tolerance=±5% resistance=12k package=THT]
  R13 = Resistor [tolerance=±5% resistance=12k package=THT]
  R14 = Resistor [tolerance=±5% resistance=12k package=THT]
  R15 = Resistor [tolerance=±5% resistance=24k package=THT]
  R16 = Resistor [tolerance=±5% resistance=24k package=THT]
  R17 = Resistor [tolerance=±5% resistance=24k package=THT]
  R18 = Resistor [tolerance=±5% resistance=33k package=THT]
  R19 = Resistor [tolerance=±5% resistance=47k package=THT]
  R20 = Resistor [tolerance=±5% resistance=100k package=THT]
  R21 = Resistor [tolerance=±5% resistance=240k package=THT]
  R22 = Resistor [tolerance=±5% resistance=510k package=THT]
  R24 = Resistor [tolerance=±5% resistance=1M package=THT]
  C8 = Electrolytic Capacitor [capacitance=47µF package="100 mil [THT, electrolytic]"]
  C9 = Electrolytic Capacitor [capacitance=47µF package="100 mil [THT, electrolytic]"]
  C10 = Ceramic Capacitor [capacitance=5pF package="100 mil [THT, multilayer]"]
  C11 = Ceramic Capacitor [capacitance=47pF package="100 mil [THT, multilayer]"]
  C12 = Ceramic Capacitor [capacitance=500pF part_number="marked 560 pcb" package="100 mil [THT, multilayer]"]
  C14 = Ceramic Capacitor [capacitance=10nF package="100 mil [THT, multilayer]"]
  C13 = Ceramic Capacitor [capacitance=1nF package="100 mil [THT, multilayer]"]
  C15 = Ceramic Capacitor [capacitance=10nF package="100 mil [THT, multilayer]"]
  C16 = Ceramic Capacitor [capacitance=10nF package="100 mil [THT, multilayer]"]
  C18 = Ceramic Capacitor [capacitance=27nF part_number="marked 223 pcb" package="100 mil [THT, multilayer]"]
  C21 = Ceramic Capacitor [capacitance=82nF package="100 mil [THT, multilayer]"]
  C19 = Ceramic Capacitor [capacitance=82nF package="100 mil [THT, multilayer]"]
  C20 = Ceramic Capacitor [capacitance=82nF package="100 mil [THT, multilayer]"]
  C22 = Ceramic Capacitor [capacitance=100nF package="100 mil [THT, multilayer]"]
  C17 = Ceramic Capacitor [capacitance=10nF package="100 mil [THT, multilayer]"]
  C23 = Ceramic Capacitor [capacitance=100nF package="100 mil [THT, multilayer]"]
  C24 = Ceramic Capacitor [capacitance=100nF package="100 mil [THT, multilayer]"]
  C25 = Ceramic Capacitor [capacitance=100nF package="100 mil [THT, multilayer]"]
  IC1 = Voltage Regulator [part_number=78L05 package=to-92]
  LED1 = LED - 3mm [color="Red (633nm)" package="3 mm [THT]"]
  JIN = Power Jack [package=power_jack_pth_lock]
  JOUT = Power Jack [package=power_jack_pth_lock]
  VCC1 = Battery block 9V
  R23 = Resistor [tolerance=±5% resistance=510k package=THT]
  R25 = Resistor [tolerance=±5% resistance=1k package=THT]

nets:
  VIN: JDC.GND, R1.Pin_1, R5.Pin_0
  PWB: JDC.GNDBREAK, VCC1.+
  PWC: JDC.PWR, JIN.GNDBREAK, VCC1.-
  N1: IC3.pin1, C5.+, C6.+, C24.1, IC1.OUT
  N2: IC3.pin2, C9.+
  D2/GND/RE1/V1: IC3.pin3, IC3.pin4, IC2.Pin_4, VR1.wiper, VR2.leg1, VR3.leg1, S1.5, D1.anode, C5.-, C6.-, C7.-, R6.Pin_0, R20.Pin_0, R24.Pin_0, C8.-, C9.-, C14.1, C15.0, C16.0, C18.0, C22.0, C17.0, C23.0, C24.0, IC1.GND, JIN.GND, JOUT.GND
  N3: IC3.pin6, R3.Pin_1
  N4: IC3.pin7, C23.1
  N5: IC3.pin8, C22.1
  N6: IC3.pin9, C21.0
  N7: IC3.pin10, C21.1
  N8: IC3.pin11, C20.1
  N9: IC3.pin12, R9.Pin_0, C20.0
  N10: IC3.pin13, R13.Pin_0, C13.1
  N11: IC3.pin14, R4.Pin_0, R17.Pin_0, C13.0
  N12: IC3.pin15, R19.Pin_0, C12.0
  N13: IC3.pin16, R11.Pin_0, C12.1
  AOUT: IC2.Pin_1, C4.+, R16.Pin_0, C11.1
  AIN-: IC2.Pin_2, R15.Pin_1, R16.Pin_1, R18.Pin_1, C11.0
  AIN+: IC2.Pin_3, R25.Pin_1
  BIN+: IC2.Pin_5, R21.Pin_1
  BIN-: IC2.Pin_6, C10.1
  BOUT: IC2.Pin_7, C3.+, R15.Pin_0, C10.0, R23.Pin_0
  V5: IC2.Pin_8, R8.Pin_1, C8.+, IC1.IN
  D1: VR1.leg1, R3.Pin_0
  V2: VR2.wiper, C1.-
  V3: VR2.leg2
  RE2: VR3.wiper, R7.Pin_1
  RE3: VR3.leg2, C2.-
  N14: S1.1, R2.Pin_1
  S1ap: S1.2, R24.Pin_1, C19.1
  JIN-TIP: S1.3, S1c.L1, JIN.PWR
  N15: S1.4, R2.Pin_0
  LED-: S1.6, LED1.cathode
  JOUT-TIP: S1c.COM, JOUT.PWR
  N16: S1c.L2, C4.-, R20.Pin_1
  N17: D1.cathode, R1.Pin_0
  N18: C1.+, R18.Pin_0
  N19: C2.+, R4.Pin_1, C14.0
  N20: C3.-, R12.Pin_0
  N21: C7.+, R25.Pin_0
  LED+: R5.Pin_1, LED1.anode
  N22: R6.Pin_1, R8.Pin_0, R21.Pin_0
  N23: R7.Pin_0, C25.1
  N24: R9.Pin_1, R14.Pin_0, C17.1
  N25: R10.Pin_0, R11.Pin_1, R19.Pin_1, C15.1
  N26: R10.Pin_1, R12.Pin_1, C18.1, C25.0
  N27: R13.Pin_1, R14.Pin_1, R17.Pin_1, C16.1
  N28: R22.Pin_0, C19.0
  N29: R22.Pin_1, R23.Pin_1

notes:
  S1 & S1c actually represent a single 3PDT stomp switch
  I haven't bothered to layout the breadboard, as the kit includes a PCB

custom parts:
  TL072/TLE2072 Dual Op. Amp: The classic LM 358 Dual Operational Amplifier (Op-Amp). The analog swiss-army knife.
