# Fritzing sketch Goblin (saved by Fritzing 0.9.2b)
breadboards: 1

parts:
  IC1 = Dual Op-Amp [part_number=JRC4558D package=dip08]
  RA19-DRIVE = Rotary Potentiometer (Small) [maximum_resistance=500kΩ package=THT]
  JACK-IN = AMPHENOL - ACJS-MHDR [package=ACJS-MHDR]
  C1 = Ceramic Capacitor [capacitance=22nF package="100 mil [THT, multilayer]"]
  JACK-OUT = AMPHENOL - ACJS-MHDR [package=ACJS-MHDR]
  R9 = Resistor [tolerance=±5% resistance=3.3k package=THT]
  S1 = SWITCH-DPDT [package=gpi-152-3013]
  S1c = Toggle Switch [package=THT]
  C12 = Electrolytic Capacitor [capacitance=100µF package="100 mil [THT, electrolytic]"]
  R1 = Resistor [tolerance=±5% resistance=1k package=THT]
  9V = Power plug
  D5 = Rectifier Diode [part_number=1N4001 package="300 mil [THT]"]
  Q1 = NPN-Transistor [part_number=S9014 package="TO92 [THT]"]
  Q2 = NPN-Transistor [part_number=S9014 package="TO92 [THT]"]
  R2 = Resistor [tolerance=±5% resistance=560k package=THT]
  R6 = Resistor [tolerance=±5% resistance=4.7k package=THT]
  R10 = Resistor [tolerance=±5% resistance=10k package=THT]
  R9_2 = Resistor [tolerance=±5% resistance=10k package=THT]
  C7 = Electrolytic Capacitor [capacitance=47µF package="100 mil [THT, electrolytic]"]
  C3 = Ceramic Capacitor [capacitance=47nF package="100 mil [THT, multilayer]"]
  R3 = Resistor [tolerance=±5% resistance=10k package=THT]
  R5 = Resistor [tolerance=±5% resistance=10k package=THT]
  C2 = Ceramic Capacitor [capacitance=1µF package="100 mil [THT, multilayer]"]
  D2 = Rectifier Diode [part_number=1N4148 package="300 mil [THT]"]
  D1 = Rectifier Diode [part_number=1N4148 package="300 mil [THT]"]
  C4 = Ceramic Capacitor [capacitance=50pF package="100 mil [THT, multilayer]"]
  R16 = Resistor [tolerance=±5% resistance=10k package=THT]
  R8 = Resistor [tolerance=±5% resistance=1k package=THT]
  R7 = Resistor [tolerance=±5% resistance=51k package=THT]
  C5 = Ceramic Capacitor [capacitance=220nF package="100 mil [THT, multilayer]"]
  RA20-TONE = Rotary Potentiometer (Small) [maximum_resistance=20kΩ package=THT]
  C9 = Ceramic Capacitor [capacitance=220nF package="100 mil [THT, multilayer]"]
  R11 = Resistor [tolerance=±5% resistance=220 package=THT]
  R17 = Resistor [tolerance=±5% resistance=1k package=THT]
  C8 = Ceramic Capacitor [capacitance=1µF package="100 mil [THT, multilayer]"]
  R18 = Resistor [tolerance=±5% resistance=1k package=THT]
  RB21-VOL = Rotary Potentiometer (Small) [maximum_resistance=100kΩ package=THT]
  C10 = Ceramic Capacitor [capacitance=100nF package="100 mil [THT, multilayer]"]
  R12 = Resistor [tolerance=±5% resistance=560k package=THT]
  R14 = Resistor [tolerance=±5% resistance=10k package=THT]
  R15 = Resistor [tolerance=±5% resistance=100 package=THT]
  C11 = Electrolytic Capacitor [capacitance=10µF package="100 mil [THT, electrolytic]"]
  R13 = Resistor [tolerance=±5% resistance=10k package=THT]
  L1 = LED - 3mm [color="Red (660nm)" package="3 mm [THT]"]
  L2 = LED - 3mm [color="White (4500K)" package="3 mm [THT]"]
  R19 = Resistor [tolerance=±5% resistance=10k package=THT]

nets:
  N1: IC1.A_OUT, RA19-DRIVE.leg1, RA19-DRIVE.wiper, D2.cathode, D1.anode, C4.1, R8.Pin_0
  N2: IC1.A_-IN, C3.1, D2.anode, D1.cathode, C4.0, R7.Pin_1
  N3: IC1.A_+IN, R5.Pin_1, C2.1
  GND: IC1.A_V-, JACK-IN.Sleeve_(1), JACK-OUT.Sleeve_(4), S1c.L2, C12.-, 9V.GND, D5.anode, R10.Pin_0, C7.-, R3.Pin_0, C5.1, R11.Pin_1, R14.Pin_1, R13.Pin_1, L1.cathode, L2.cathode
  N4: IC1.B_+IN, R16.Pin_1, R8.Pin_1, C5.0, RA20-TONE.leg2
  N5: IC1.B_-IN, RA20-TONE.leg1, R17.Pin_0
  N6: IC1.B_OUT, R17.Pin_1, C8.0
  VCC: IC1.A_V+, S1c.L1, C12.+, 9V.VCC, D5.cathode, Q1.C, Q2.C, R9_2.Pin_1, R19.Pin_0
  N7: RA19-DRIVE.leg2, R7.Pin_0
  N8: JACK-IN.Tip_(3), S1.2
  FXin: C1.0, S1.1
  N9: C1.1, R1.Pin_0
  N10: JACK-OUT.Tip_(6), S1.5
  N11: R9.Pin_0, S1c.COM
  N12: R9.Pin_1, L1.anode
  FXout: S1.4, C11.-, R13.Pin_0
  N13: S1.3, S1.6
  N14: R1.Pin_1, Q1.B, R2.Pin_0
  N15: Q1.E, R3.Pin_1, C2.0
  N16: Q2.E, R14.Pin_0, R15.Pin_0
  N17: Q2.B, C10.1, R12.Pin_0
  AC_GND: R2.Pin_1, R6.Pin_0, R10.Pin_1, R9_2.Pin_0, C7.+, R5.Pin_0, R16.Pin_0, RB21-VOL.leg2, R12.Pin_1
  N18: R6.Pin_1, C3.0
  N19: RA20-TONE.wiper, C9.0
  N20: C9.1, R11.Pin_0
  N21: C8.1, R18.Pin_0
  N22: R18.Pin_1, RB21-VOL.leg1
  N23: RB21-VOL.wiper, C10.0
  N24: R15.Pin_1, C11.+
  N25: L2.anode, R19.Pin_1

notes:
  S1 & S1c actually represent a single 3PDT stomp switch
  9V - maybe wired as 9V jack with 9V battery bypass
  battery ground may be wired via input jack for switching
