# Fritzing sketch LaserHarpKit (saved by Fritzing 0.9.2b)
breadboards: 2

parts:
  DC01 = Power plug
  U1 = IC, DIP package, 40 pins [chip_label=AT89C52]
  D1 = LED - 3mm [color="Blue (430nm)" package="3 mm [THT]"]
  R1 = Resistor [tolerance=±5% resistance=1k package=THT]
  KG = SWITCH-DPDT [package=os]
  C6 = Electrolytic Capacitor [capacitance=10µF package="100 mil [THT, electrolytic]"]
  K1 = Pushbutton [package="[THT]"]
  K2 = Pushbutton [package="[THT]"]
  D2 = LED - 3mm [color="Blue (430nm)" package="3 mm [THT]"]
  D3 = LED - 3mm [color="Blue (430nm)" package="3 mm [THT]"]
  D4 = LED - 3mm [color="Blue (430nm)" package="3 mm [THT]"]
  D5 = LED - 3mm [color="Blue (430nm)" package="3 mm [THT]"]
  D6 = LED - 3mm [color="Blue (430nm)" package="3 mm [THT]"]
  R2 = Resistor [tolerance=±5% resistance=1k package=THT]
  R3 = Resistor [tolerance=±5% resistance=1k package=THT]
  R4 = Resistor [tolerance=±5% resistance=1k package=THT]
  R5 = Resistor [tolerance=±5% resistance=1k package=THT]
  R6 = Resistor [tolerance=±5% resistance=1k package=THT]
  D7 = LED - 3mm [color="Blue (430nm)" package="3 mm [THT]"]
  R7 = Resistor [tolerance=±5% resistance=1k package=THT]
  Y1 = Crystal [frequency="16 MHz" part_number=12MHZ package=THT]
  C4 = Ceramic Capacitor [capacitance=30pF package="100 mil [THT, multilayer]"]
  C3 = Ceramic Capacitor [capacitance=30pF package="100 mil [THT, multilayer]"]
  C5 = Electrolytic Capacitor [capacitance=10µF package="100 mil [THT, electrolytic]"]
  R15 = Resistor [tolerance=±5% resistance=10k package=THT]
  D8 = LED - 3mm [color="Blue (430nm)" package="3 mm [THT]"]
  D9 = LED - 3mm [color="Blue (430nm)" package="3 mm [THT]"]
  D10 = LED - 3mm [color="Blue (430nm)" package="3 mm [THT]"]
  R16 = Resistor [tolerance=±5% resistance=1k package=THT]
  R17 = Resistor [tolerance=±5% resistance=1k package=THT]
  R18 = Resistor [tolerance=±5% resistance=1k package=THT]
  Q1 = PNP-Transistor [part_number=8550 package="TO92 [THT]"]
  SPK = Piezo Speaker
  R19 = Resistor [tolerance=±5% resistance=1k package=THT]
  JG1 = LED - 5mm [color="Red (633nm)" part_number="Red Laser" package="5 mm [THT]"]
  JG2 = LED - 5mm [color="Red (633nm)" part_number="Red Laser" package="5 mm [THT]"]
  JG3 = LED - 5mm [color="Red (633nm)" part_number="Red Laser" package="5 mm [THT]"]
  JG4 = LED - 5mm [color="Red (633nm)" part_number="Red Laser" package="5 mm [THT]"]
  JG5 = LED - 5mm [color="Red (633nm)" part_number="Red Laser" package="5 mm [THT]"]
  JG6 = LED - 5mm [color="Red (633nm)" part_number="Red Laser" package="5 mm [THT]"]
  JG7 = LED - 5mm [color="Red (633nm)" part_number="Red Laser" package="5 mm [THT]"]
  R8 = Resistor [tolerance=±5% resistance=10k package=THT]
  GM1 = Photocell (LDR) [package=THT]
  R21 = Resistor [tolerance=±5% resistance=10k package=THT]
  GM2 = Photocell (LDR) [package=THT]
  R22 = Resistor [tolerance=±5% resistance=10k package=THT]
  R23 = Resistor [tolerance=±5% resistance=10k package=THT]
  R24 = Resistor [tolerance=±5% resistance=10k package=THT]
  R25 = Resistor [tolerance=±5% resistance=10k package=THT]
  R26 = Resistor [tolerance=±5% resistance=10k package=THT]
  GM3 = Photocell (LDR) [package=THT]
  GM4 = Photocell (LDR) [package=THT]
  GM5 = Photocell (LDR) [package=THT]
  GM6 = Photocell (LDR) [package=THT]
  GM7 = Photocell (LDR) [package=THT]

nets:
  GND: DC01.GND, U1.pin20, C6.-, K1.Pin_1, K1.Pin_2, K2.Pin_1, K2.Pin_2, C4.0, C3.0, R15.Pin_1, Q1.C, JG1.cathode, JG2.cathode, JG3.cathode, JG4.cathode, JG5.cathode, JG6.cathode, JG7.cathode, GM1.pin_1, GM2.pin_1, GM3.pin_1, GM4.pin_1, GM5.pin_1, GM6.pin_1, GM7.pin_1
  N1: DC01.VCC, KG.2
  N2: U1.pin1, D1.cathode
  N3: U1.pin2, D2.cathode
  N4: U1.pin3, D3.cathode
  N5: U1.pin4, D4.cathode
  N6: U1.pin5, D5.cathode
  N7: U1.pin6, D6.cathode
  N8: U1.pin7, D7.cathode
  RST: U1.pin9, C5.-, R15.Pin_0
  K1: U1.pin13, K1.Pin_3, K1.Pin_4
  SPK: U1.pin14, R19.Pin_1
  N9: U1.pin15, D8.cathode
  N10: U1.pin16, D9.cathode
  N11: U1.pin17, D10.cathode
  N12: U1.pin18, Y1.pin_0, C3.1
  N13: U1.pin19, Y1.pin_1, C4.1
  K2: U1.pin21, K2.Pin_3, K2.Pin_4
  N14: U1.pin22, R26.Pin_1, GM7.pin_0
  N15: U1.pin23, R25.Pin_1, GM6.pin_0
  N16: U1.pin24, R24.Pin_1, GM5.pin_0
  N17: U1.pin25, R23.Pin_1, GM4.pin_0
  N18: U1.pin26, R22.Pin_1, GM3.pin_0
  N19: U1.pin27, R21.Pin_1, GM2.pin_0
  N20: U1.pin28, R8.Pin_1, GM1.pin_0
  VCC: U1.pin40, R1.Pin_0, KG.3, C6.+, R2.Pin_0, R3.Pin_0, R4.Pin_0, R5.Pin_0, R6.Pin_0, R7.Pin_0, C5.+, R16.Pin_0, R17.Pin_0, R18.Pin_0, SPK.pin2, JG1.anode, JG2.anode, JG3.anode, JG4.anode, JG5.anode, JG6.anode, JG7.anode, R8.Pin_0, R21.Pin_0, R22.Pin_0, R23.Pin_0, R24.Pin_0, R25.Pin_0, R26.Pin_0
  N21: D1.anode, R1.Pin_1
  N22: D2.anode, R2.Pin_1
  N23: D3.anode, R3.Pin_1
  N24: D4.anode, R4.Pin_1
  N25: D5.anode, R5.Pin_1
  N26: D6.anode, R6.Pin_1
  N27: D7.anode, R7.Pin_1
  N28: D8.anode, R16.Pin_1
  N29: D9.anode, R17.Pin_1
  N30: D10.anode, R18.Pin_1
  N31: Q1.E, SPK.pin1
  N32: Q1.B, R19.Pin_0
