# Fritzing sketch WavePlayer (saved by Fritzing 0.9.2b)
breadboards: 1

parts:
  Part1 = Arduino Uno (Rev3)
  microSD1 = MicroSD Breakout
  PLAY = Pushbutton [package="[THT]"]
  J1 = Piezo Speaker
  R1 = Resistor [tolerance=±5% resistance=1k part_number=(optional) package=THT]

nets:
  N1: Part1.D9_PWM, R1.Pin_0
  N2: Part1.D10_PWM/SS, microSD1.CS
  N3: Part1.D11_PWM/MOSI, microSD1.DI
  N4: Part1.D12/MISO, microSD1.DO
  N5: Part1.D13/SCK, microSD1.CLK
  N6: Part1.D2, PLAY.Pin_1, PLAY.Pin_2
  VCC: Part1.5V, microSD1.5V
  GND: Part1.GND, microSD1.GND, PLAY.Pin_3, PLAY.Pin_4, J1.pin2
  N7: J1.pin1, R1.Pin_1

custom parts:
  MicroSD Breakout: 5V-ready microSD Breakout with Level Shifter
