# Fritzing sketch MotorizedMusicBox (saved by Fritzing 0.9.2b)
breadboards: 1

parts:
  VCC = Battery [part_number=1.5V]
  M1 = DC Motor
  S1 = Toggle Switch [package=THT]

nets:
  N1: VCC.-, M1.pin_2
  N2: VCC.+, S1.COM
  N3: M1.pin_1, S1.L2

notes:
  1.5V
