# Fritzing sketch SimpleSoundEffects2 (saved by Fritzing 0.9.2b)
breadboards: 1

parts:
  U3 = attiny85 [package=dip]
  5V = Power plug
  R1 = Trimmer Potentiometer [maximum_resistance=10kΩ package=THT]
  R2 = Resistor [tolerance=±5% resistance=10k package=THT]
  R3 = Resistor [tolerance=±5% resistance=5.6k package=THT]
  Q1 = NPN-Transistor [part_number=2N3904 package="TO92 [THT]"]
  SPKR1 = Loudspeaker
  R4 = Resistor [tolerance=±5% resistance=47 package=THT]

nets:
  N1: U3.Pin_1, R2.Pin_1
  N2: U3.Pin_3, R3.Pin_0
  GND: U3.Pin_4, 5V.GND, R1.leg2, Q1.E
  N3: U3.Pin_7, R1.wiper
  VCC: U3.Pin_8, 5V.VCC, R1.leg1, R2.Pin_0, R4.Pin_1
  N4: R3.Pin_1, Q1.B
  N5: Q1.C, SPKR1.pin2
  N6: SPKR1.pin1, R4.Pin_0
