# Fritzing sketch SimpleSoundEffects2_piezo (saved by Fritzing 0.9.2b)
breadboards: 1

parts:
  U3 = attiny85 [package=dip]
  5V = Power plug
  R1 = Trimmer Potentiometer [maximum_resistance=10kΩ package=THT]
  R2 = Resistor [tolerance=±5% resistance=10k package=THT]
  R3 = Resistor [tolerance=±5% resistance=5.6k package=THT]
  Q1 = NPN-Transistor [part_number=2N3904 package="TO92 [THT]"]
  R4 = Resistor [tolerance=±5% resistance=47 package=THT]
  PIEZO = Piezo Speaker
  R5 = Resistor [tolerance=±5% resistance=10k package=THT]

nets:
  N1: U3.Pin_1, R2.Pin_1
  N2: U3.Pin_3, R3.Pin_0
  GND: U3.Pin_4, 5V.GND, R1.leg2, Q1.E
  N3: U3.Pin_7, R1.wiper
  VCC: U3.Pin_8, 5V.VCC, R1.leg1, R2.Pin_0, R4.Pin_1
  N4: R3.Pin_1, Q1.B
  N5: Q1.C, PIEZO.pin1, R5.Pin_0
  N6: R4.Pin_0, PIEZO.pin2, R5.Pin_1
