# Fritzing sketch SYN6288Module (saved by Fritzing 0.9.2b)

parts:
  Part1 = Arduino Uno (Rev3)
  AUDIO_OUT = female pin header, 2 pins [form="♀ (female)"]
  J1 = female pin header, 5 pins [form="♀ (female)"]
  SPKR1 = Loudspeaker

nets:
  GND: Part1.GND, J1.pin4
  TXD: Part1.D0/RX, J1.pin3
  RXD: Part1.D1/TX, J1.pin2
  VDD: Part1.5V, J1.pin1
  N1: AUDIO_OUT.pin1, SPKR1.pin1
  N2: AUDIO_OUT.pin2, SPKR1.pin2
  BY: J1.pin5

notes:
  SYN6288 Module
