# Fritzing sketch AudioLevelIndicatorKit (saved by Fritzing 0.9.2b)
breadboards: 1

parts:
  IC1 = LM3915 [package=THT]
  LED1 = LED - 3mm [color="Yellow (595nm)" package="3 mm [THT]"]
  LED2 = LED - 3mm [color="Yellow (595nm)" package="3 mm [THT]"]
  LED3 = LED - 3mm [color="Yellow (595nm)" package="3 mm [THT]"]
  LED4 = LED - 3mm [color="Yellow (595nm)" package="3 mm [THT]"]
  LED5 = LED - 3mm [color="Yellow (595nm)" package="3 mm [THT]"]
  LED6 = LED - 3mm [color="Yellow (595nm)" package="3 mm [THT]"]
  LED7 = LED - 3mm [color="Yellow (595nm)" package="3 mm [THT]"]
  LED9 = LED - 3mm [color="Red (633nm)" package="3 mm [THT]"]
  LED8 = LED - 3mm [color="Yellow (595nm)" package="3 mm [THT]"]
  LED10 = LED - 3mm [color="Red (633nm)" package="3 mm [THT]"]
  VCC1 = Battery block 9V
  R9 = Resistor [tolerance=±5% resistance=20k package=THT]
  R2 = Resistor [tolerance=±5% resistance=100 package=THT]
  R5 = Resistor [tolerance=±5% resistance=1k package=THT]
  R8 = Resistor [tolerance=±5% resistance=1k package=THT]
  R1 = Resistor [tolerance=±5% resistance=1k package=THT]
  R3 = Resistor [tolerance=±5% resistance=10k package=THT]
  R7 = Resistor [tolerance=±5% resistance=10 package=THT]
  C1 = Ceramic Capacitor [capacitance=100nF package="100 mil [THT, multilayer]"]
  C2 = Ceramic Capacitor [capacitance=100nF package="100 mil [THT, multilayer]"]
  R4 = Trimmer Potentiometer [maximum_resistance=50kΩ package=THT]
  TRS1 = Audio Jack (TRS) 3.5mm [package="4Ucon 08780 [THT]"]
  R6 = Resistor [tolerance=±5% resistance=560 package=THT]
  S1 = Pushbutton [package=THT]

nets:
  N1: IC1.OUT1, LED1.cathode
  GND: IC1.V-, IC1.R_LO, IC1.REF_ADJ, VCC1.-, R5.Pin_0, R7.Pin_1, C1.0, C2.1, R4.leg1, R6.Pin_0
  vcc: IC1.V+, VCC1.+, R9.Pin_0, R2.Pin_0, C1.1, S1.leg0
  N2: IC1.SIG, R4.wiper
  N3: IC1.R_HIGH, R9.Pin_1, R6.Pin_1
  N4: IC1.REF_OUT, R5.Pin_1
  N5: IC1.MODE, S1.leg1
  N6: IC1.OUT10, R8.Pin_0
  N7: IC1.OUT9, R1.Pin_0
  N8: IC1.OUT8, LED8.cathode
  N9: IC1.OUT7, LED7.cathode
  N10: IC1.OUT6, LED6.cathode
  N11: IC1.OUT5, LED5.cathode
  N12: IC1.OUT4, LED4.cathode
  N13: IC1.OUT3, LED3.cathode
  N14: IC1.OUT2, LED2.cathode
  N15: LED1.anode, LED2.anode, LED3.anode, LED4.anode, LED5.anode, LED6.anode, LED7.anode, LED9.anode, LED8.anode, LED10.anode, R2.Pin_1, C2.0
  N16: LED9.cathode, R1.Pin_1
  N17: LED10.cathode, R8.Pin_1
  N18: R3.Pin_0, R4.leg2
  N19: R3.Pin_1, TRS1.Ring
  N20: R7.Pin_0, TRS1.Sleeve

custom parts:
  LM3915: Dot/Bar Display Driver
