# Fritzing sketch UsbLedVolumeIndicatorKit (saved by Fritzing 0.9.2b)
breadboards: 1

parts:
  K1 = Power plug [part_number=USB/5-12V]
  D23 = Rectifier Diode [part_number=1N5819 package="300 mil [THT]"]
  U1 = TL072/TLE2072 Dual Op. Amp [package="DIP8 [THT]"]
  U2 = TL072/TLE2072 Dual Op. Amp [package="DIP8 [THT]"]
  U3 = TL072/TLE2072 Dual Op. Amp [package="DIP8 [THT]"]
  MIC1 = Microphone
  U4 = TL072/TLE2072 Dual Op. Amp [package="DIP8 [THT]"]
  U5 = TL072/TLE2072 Dual Op. Amp [package="DIP8 [THT]"]
  U6 = TL072/TLE2072 Dual Op. Amp [package="DIP8 [THT]"]
  RP1 = Trimmer Potentiometer [maximum_resistance=500kΩ package=THT]
  C1 = Ceramic Capacitor [capacitance=100nF package="100 mil [THT, multilayer]"]
  R1 = Resistor [tolerance=±5% resistance=10k package=THT]
  C4 = Electrolytic Capacitor [capacitance=4.7µF package="100 mil [THT, electrolytic]"]
  C2 = Electrolytic Capacitor [capacitance=100µF package="100 mil [THT, electrolytic]"]
  R2 = Resistor [tolerance=±5% resistance=5.1k package=THT]
  R3 = Resistor [tolerance=±5% resistance=1M package=THT]
  R4 = Resistor [tolerance=±5% resistance=5.1k package=THT]
  D1 = Rectifier Diode [part_number=1N4001 package="300 mil [THT]"]
  C3 = Ceramic Capacitor [capacitance=100nF package="100 mil [THT, multilayer]"]
  R6 = Resistor [tolerance=±5% resistance=5.1k package=THT]
  D22 = Rectifier Diode [part_number=1N4001 package="300 mil [THT]"]
  R7 = Resistor [tolerance=±5% resistance=100 package=THT]
  R8 = Resistor [tolerance=±5% resistance=100 package=THT]
  R9 = Resistor [tolerance=±5% resistance=510 package=THT]
  R10 = Resistor [tolerance=±5% resistance=510 package=THT]
  R11 = Resistor [tolerance=±5% resistance=100 package=THT]
  R12 = Resistor [tolerance=±5% resistance=100 package=THT]
  R13 = Resistor [tolerance=±5% resistance=510 package=THT]
  R14 = Resistor [tolerance=±5% resistance=510 package=THT]
  R15 = Resistor [tolerance=±5% resistance=200 package=THT]
  R16 = Resistor [tolerance=±5% resistance=200 package=THT]
  R17 = Resistor [tolerance=±5% resistance=510 package=THT]
  R18 = Resistor [tolerance=±5% resistance=510 package=THT]
  R19 = Resistor [tolerance=±5% resistance=200 package=THT]
  R20 = Resistor [tolerance=±5% resistance=430 package=THT]
  R21 = Resistor [tolerance=±5% resistance=510 package=THT]
  R22 = Resistor [tolerance=±5% resistance=510 package=THT]
  R23 = Resistor [tolerance=±5% resistance=430 package=THT]
  R24 = Resistor [tolerance=±5% resistance=1k package=THT]
  R25 = Resistor [tolerance=±5% resistance=10k package=THT]
  R26 = Resistor [tolerance=±5% resistance=510 package=THT]
  R27 = Resistor [tolerance=±5% resistance=510 package=THT]
  R28 = Resistor [tolerance=±5% resistance=2k package=THT]
  D21 = LED - 5mm [color="Red (633nm)" package="5 mm [THT]"]
  D19 = LED - 5mm [color="Red (633nm)" package="5 mm [THT]"]
  D02 = LED - 5mm [color="Green (555nm)" package="5 mm [THT]"]
  D04 = LED - 5mm [color="Green (555nm)" package="5 mm [THT]"]
  D03 = LED - 5mm [color="Green (555nm)" package="5 mm [THT]"]
  D05 = LED - 5mm [color="Green (555nm)" package="5 mm [THT]"]
  D06 = LED - 5mm [color="Green (555nm)" package="5 mm [THT]"]
  D08 = LED - 5mm [color="Green (555nm)" package="5 mm [THT]"]
  D07 = LED - 5mm [color="Green (555nm)" package="5 mm [THT]"]
  D09 = LED - 5mm [color="Green (555nm)" package="5 mm [THT]"]
  D10 = LED - 5mm [color="Green (555nm)" package="5 mm [THT]"]
  D12 = LED - 5mm [color="Green (555nm)" package="5 mm [THT]"]
  D11 = LED - 5mm [color="Green (555nm)" package="5 mm [THT]"]
  D13 = LED - 5mm [color="Green (555nm)" package="5 mm [THT]"]
  D20 = LED - 5mm [color="Red (633nm)" package="5 mm [THT]"]
  D17 = LED - 5mm [color="Red (633nm)" package="5 mm [THT]"]
  D16 = LED - 5mm [color="Red (633nm)" package="5 mm [THT]"]
  D18 = LED - 5mm [color="Red (633nm)" package="5 mm [THT]"]
  D15 = LED - 5mm [color="Red (633nm)" package="5 mm [THT]"]
  D14 = LED - 5mm [color="Red (633nm)" package="5 mm [THT]"]
  R5 = Resistor [tolerance=±5% resistance=510 package=THT]

nets:
  GND: K1.GND, U1.Pin_4, U2.Pin_4, U3.Pin_4, MIC1.pin2, U4.Pin_4, U5.Pin_4, U6.Pin_4, C4.-, C2.-, R2.Pin_1, R4.Pin_1, R6.Pin_1, D22.cathode, R8.Pin_0, R25.Pin_0, D21.cathode, D19.cathode, D02.cathode, D04.cathode, D03.cathode, D05.cathode, D06.cathode, D08.cathode, D07.cathode, D09.cathode, D10.cathode, D12.cathode, D11.cathode, D13.cathode, D20.cathode, D17.cathode, D16.cathode, D18.cathode, D15.cathode, D14.cathode
  N1: K1.VCC, D23.anode
  VCC: D23.cathode, U2.Pin_8, U3.Pin_8, U4.Pin_8, U5.Pin_8, U6.Pin_8, R28.Pin_1, R5.Pin_1
  N2: U1.Pin_1, RP1.wiper, C3.1
  N3: U1.Pin_2, RP1.leg2, R4.Pin_0
  N4: U1.Pin_3, C1.1, R2.Pin_0, R3.Pin_1
  N5: U1.Pin_5, C3.0, R6.Pin_0
  AUDIO_REF: U1.Pin_6, U2.Pin_3, U2.Pin_5, U3.Pin_3, U3.Pin_5, U4.Pin_3, U4.Pin_5, U5.Pin_3, U5.Pin_5, U6.Pin_3, U6.Pin_5, C4.+, D1.cathode, R25.Pin_1
  N6: U1.Pin_7, D1.anode
  AVCC: U1.Pin_8, R1.Pin_1, C2.+, R3.Pin_0, R5.Pin_0
  N7: U2.Pin_1, R9.Pin_1
  U2aRef: U2.Pin_2, R7.Pin_0, R8.Pin_1
  U2bRef: U2.Pin_6, R7.Pin_1, R11.Pin_0
  N8: U2.Pin_7, R10.Pin_1
  N9: U3.Pin_1, R13.Pin_1
  U3aRef: U3.Pin_2, R11.Pin_1, R12.Pin_0
  U3bRef: U3.Pin_6, R12.Pin_1, R15.Pin_0
  N10: U3.Pin_7, R14.Pin_1
  N11: MIC1.pin1, C1.0, R1.Pin_0
  N12: U4.Pin_1, R17.Pin_1
  U4aRef: U4.Pin_2, R15.Pin_1, R16.Pin_0
  U4bRef: U4.Pin_6, R16.Pin_1, R19.Pin_0
  N13: U4.Pin_7, R18.Pin_1
  N14: U5.Pin_1, R21.Pin_1
  U5aRef: U5.Pin_2, R19.Pin_1, R20.Pin_0
  U5bRef: U5.Pin_6, R20.Pin_1, R23.Pin_0
  N15: U5.Pin_7, R22.Pin_1
  N16: U6.Pin_1, R26.Pin_1
  U6aRef: U6.Pin_2, R23.Pin_1, R24.Pin_0
  U6bRef: U6.Pin_6, D22.anode, R24.Pin_1, R28.Pin_0
  N17: U6.Pin_7, R27.Pin_1
  OUT_L1: R9.Pin_0, D02.anode, D04.anode
  OUT_L2: R10.Pin_0, D03.anode, D05.anode
  OUT_L3: R13.Pin_0, D06.anode, D08.anode
  OUT_L4: R14.Pin_0, D07.anode, D09.anode
  OUT_L5: R17.Pin_0, D10.anode, D12.anode
  OUT_L6: R18.Pin_0, D11.anode, D13.anode
  OUT_L7: R21.Pin_0, D16.anode, D14.anode
  OUT_L8: R22.Pin_0, D17.anode, D15.anode
  OUT_L9: R26.Pin_0, D20.anode, D18.anode
  OUT_L10: R27.Pin_0, D21.anode, D19.anode

notes:
  circuit not laid out for the breadboard
  non-inverting amp
  Vin(1+ RP1/R4)
  buffer
  electret audio input
  D23 provides basic reverse polarity protection
  Voltage divider ladder provides the sequence of voltage references
  8 comparator stages, each driving 2 LEDs
  <<< 6 green and 4 red LED stages LEFT
  6 green and 4 red LED stages RIGHT >>>

custom parts:
  TL072/TLE2072 Dual Op. Amp: The classic LM 358 Dual Operational Amplifier (Op-Amp). The analog swiss-army knife.
