# Fritzing sketch VoiceLevelIndicatorKit (saved by Fritzing 0.9.2b)
breadboards: 1

parts:
  MIC1 = Microphone
  C13 = Electrolytic Capacitor [capacitance=4.7µF package="100 mil [THT, electrolytic]"]
  R77 = Resistor [tolerance=±5% resistance=47k package=THT]
  R78 = Resistor [tolerance=±5% resistance=47k package=THT]
  Q37 = NPN-Transistor [part_number=S9013 package="TO92 [THT]"]
  R80 = Resistor [tolerance=±5% resistance=2k package=THT]
  R2 = Trimmer Potentiometer [maximum_resistance=50kΩ package=THT]
  R79 = Resistor [tolerance=±5% resistance=47k package=THT]
  C14 = Electrolytic Capacitor [capacitance=4.7µF package="100 mil [THT, electrolytic]"]
  Q38 = NPN-Transistor [part_number=S9013 package="TO92 [THT]"]
  R82 = Resistor [tolerance=±5% resistance=33k package=THT]
  R83 = Resistor [tolerance=±5% resistance=10k package=THT]
  9-15V = Power plug
  C15 = Electrolytic Capacitor [capacitance=4.7µF package="100 mil [THT, electrolytic]"]
  D1 = Rectifier Diode [part_number=1N4007 package="300 mil [THT]"]
  C16 = Electrolytic Capacitor [capacitance=220µF package="100 mil [THT, electrolytic]"]
  C17 = Electrolytic Capacitor [capacitance=220µF package="100 mil [THT, electrolytic]"]
  U1 = Voltage Regulator - 5V [part_number=L7806CV package="TO220 [THT]"]
  R26 = Trimmer Potentiometer [maximum_resistance=50kΩ package=THT]
  R52 = Resistor [tolerance=±5% resistance=10k package=THT]
  R55 = Resistor [tolerance=±5% resistance=4.7k package=THT]
  C9 = Ceramic Capacitor [capacitance=2.2nF package="100 mil [THT, multilayer]"]
  Q25 = NPN-Transistor [part_number=S9013 package="TO92 [THT]"]
  C10 = Ceramic Capacitor [capacitance=1nF package="100 mil [THT, multilayer]"]
  R60 = Resistor [tolerance=±5% resistance=100k package=THT]
  R60b = Resistor [tolerance=±5% resistance=100k package=THT]
  R56 = Resistor [tolerance=±5% resistance=4.7k package=THT]
  C11 = Ceramic Capacitor [capacitance=10nF package="100 mil [THT, multilayer]"]
  Q36 = PNP-Transistor [part_number=S9012 package="TO92 [THT]"]
  D41 = Rectifier Diode [part_number=1N4148 package="300 mil [THT]"]
  D42 = Rectifier Diode [part_number=1N4148 package="300 mil [THT]"]
  C12 = Electrolytic Capacitor [capacitance=4.7µF package="100 mil [THT, electrolytic]"]
  R61 = Resistor [tolerance=±5% resistance=47k package=THT]
  Q26 = NPN-Transistor [part_number=S9013 package="TO92 [THT]"]
  LED1 = LED - 5mm [color="Blue (525nm)" package="5 mm [THT]"]
  R63 = Resistor [tolerance=±5% resistance=560 package=THT]
  R64 = Resistor [tolerance=±5% resistance=560 package=THT]
  R62 = Resistor [tolerance=±5% resistance=47k package=THT]
  Q27 = NPN-Transistor [part_number=S9013 package="TO92 [THT]"]
  D43 = Rectifier Diode [part_number=1N4148 package="300 mil [THT]"]
  LED2 = LED - 5mm [color="Blue (525nm)" package="5 mm [THT]"]
  R73 = Resistor [tolerance=±5% resistance=33k package=THT]
  R65 = Resistor [tolerance=±5% resistance=560 package=THT]
  Q28 = NPN-Transistor [part_number=S9013 package="TO92 [THT]"]
  D44 = Rectifier Diode [part_number=1N4148 package="300 mil [THT]"]
  LED3 = LED - 5mm [color="Blue (525nm)" package="5 mm [THT]"]
  R74 = Resistor [tolerance=±5% resistance=33k package=THT]
  R66 = Resistor [tolerance=±5% resistance=560 package=THT]
  Q29 = NPN-Transistor [part_number=S9013 package="TO92 [THT]"]
  D45 = Rectifier Diode [part_number=1N4148 package="300 mil [THT]"]
  LED4 = LED - 5mm [color="Blue (525nm)" package="5 mm [THT]"]
  R53 = Resistor [tolerance=±5% resistance=10k package=THT]
  R67 = Resistor [tolerance=±5% resistance=560 package=THT]
  Q30 = NPN-Transistor [part_number=S9013 package="TO92 [THT]"]
  D46 = Rectifier Diode [part_number=1N4148 package="300 mil [THT]"]
  LED5 = LED - 5mm [color="Blue (525nm)" package="5 mm [THT]"]
  R54 = Resistor [tolerance=±5% resistance=10k package=THT]
  R68 = Resistor [tolerance=±5% resistance=560 package=THT]
  Q31 = NPN-Transistor [part_number=S9013 package="TO92 [THT]"]
  D47 = Rectifier Diode [part_number=1N4148 package="300 mil [THT]"]
  LED6 = LED - 5mm [color="Blue (525nm)" package="5 mm [THT]"]
  R57 = Resistor [tolerance=±5% resistance=4.7k package=THT]
  R69 = Resistor [tolerance=±5% resistance=560 package=THT]
  Q32 = NPN-Transistor [part_number=S9013 package="TO92 [THT]"]
  D48 = Rectifier Diode [part_number=1N4148 package="300 mil [THT]"]
  LED7 = LED - 5mm [color="Blue (525nm)" package="5 mm [THT]"]
  R58 = Resistor [tolerance=±5% resistance=4.7k package=THT]
  R70 = Resistor [tolerance=±5% resistance=560 package=THT]
  Q33 = NPN-Transistor [part_number=S9013 package="TO92 [THT]"]
  D49 = Rectifier Diode [part_number=1N4148 package="300 mil [THT]"]
  LED8 = LED - 5mm [color="Blue (525nm)" package="5 mm [THT]"]
  R75 = Resistor [tolerance=±5% resistance=2k package=THT]
  R71 = Resistor [tolerance=±5% resistance=560 package=THT]
  Q34 = NPN-Transistor [part_number=S9013 package="TO92 [THT]"]
  D50 = Rectifier Diode [part_number=1N4148 package="300 mil [THT]"]
  LED9 = LED - 5mm [color="Blue (525nm)" package="5 mm [THT]"]
  R76 = Resistor [tolerance=±5% resistance=2k package=THT]
  R72 = Resistor [tolerance=±5% resistance=560 package=THT]
  Q35 = NPN-Transistor [part_number=S9013 package="TO92 [THT]"]
  LED10 = LED - 5mm [color="Blue (525nm)" package="5 mm [THT]"]
  C18 = Electrolytic Capacitor [capacitance=4.7µF package="100 mil [THT, electrolytic]"]
  R45 = Resistor [tolerance=±5% resistance=560 package=THT]
  R43 = Resistor [tolerance=±5% resistance=560 package=THT]
  R33 = Resistor [tolerance=±5% resistance=4.7k package=THT]
  R87 = Resistor [tolerance=±5% resistance=4.7k package=THT]
  R88 = Resistor [tolerance=±5% resistance=10k package=THT]
  R44 = Resistor [tolerance=±5% resistance=560 package=THT]
  R39 = Resistor [tolerance=±5% resistance=560 package=THT]
  R47 = Resistor [tolerance=±5% resistance=560 package=THT]
  R37 = Resistor [tolerance=±5% resistance=47k package=THT]
  R51 = Resistor [tolerance=±5% resistance=2k package=THT]
  R50 = Resistor [tolerance=±5% resistance=2k package=THT]
  R95 = Resistor [tolerance=±5% resistance=100k package=THT]
  R96 = Resistor [tolerance=±5% resistance=10k package=THT]
  R49 = Resistor [tolerance=±5% resistance=33k package=THT]
  R31 = Resistor [tolerance=±5% resistance=4.7k package=THT]
  R34 = Resistor [tolerance=±5% resistance=4.7k package=THT]
  R41 = Resistor [tolerance=±5% resistance=560 package=THT]
  R36 = Resistor [tolerance=±5% resistance=47k package=THT]
  R30 = Resistor [tolerance=±5% resistance=10k package=THT]
  R48 = Resistor [tolerance=±5% resistance=33k package=THT]
  R46 = Resistor [tolerance=±5% resistance=560 package=THT]
  R38 = Resistor [tolerance=±5% resistance=560 package=THT]
  R42 = Resistor [tolerance=±5% resistance=560 package=THT]
  R40 = Resistor [tolerance=±5% resistance=560 package=THT]
  Q20 = NPN-Transistor [part_number=S9013 package="TO92 [THT]"]
  Q14 = NPN-Transistor [part_number=S9013 package="TO92 [THT]"]
  Q15 = NPN-Transistor [part_number=S9013 package="TO92 [THT]"]
  Q21 = NPN-Transistor [part_number=S9013 package="TO92 [THT]"]
  Q16 = NPN-Transistor [part_number=S9013 package="TO92 [THT]"]
  Q23 = NPN-Transistor [part_number=S9013 package="TO92 [THT]"]
  Q19 = NPN-Transistor [part_number=S9013 package="TO92 [THT]"]
  Q17 = NPN-Transistor [part_number=S9013 package="TO92 [THT]"]
  Q18 = NPN-Transistor [part_number=S9013 package="TO92 [THT]"]
  Q48 = NPN-Transistor [part_number=S9013 package="TO92 [THT]"]
  Q24 = NPN-Transistor [part_number=S9013 package="TO92 [THT]"]
  R27 = Trimmer Potentiometer [maximum_resistance=50kΩ package=THT]
  C5 = Ceramic Capacitor [capacitance=100nF package="100 mil [THT, multilayer]"]
  C7 = Ceramic Capacitor [capacitance=10nF package="100 mil [THT, multilayer]"]
  C8 = Ceramic Capacitor [capacitance=100nF package="100 mil [THT, multilayer]"]
  Q22 = PNP-Transistor [part_number=S9012 package="TO92 [THT]"]
  D21 = Rectifier Diode [part_number=1N4148 package="300 mil [THT]"]
  D26 = Rectifier Diode [part_number=1N4148 package="300 mil [THT]"]
  D25 = Rectifier Diode [part_number=1N4148 package="300 mil [THT]"]
  D23 = Rectifier Diode [part_number=1N4148 package="300 mil [THT]"]
  D22 = Rectifier Diode [part_number=1N4148 package="300 mil [THT]"]
  D29 = Rectifier Diode [part_number=1N4148 package="300 mil [THT]"]
  D24 = Rectifier Diode [part_number=1N4148 package="300 mil [THT]"]
  D28 = Rectifier Diode [part_number=1N4148 package="300 mil [THT]"]
  D27 = Rectifier Diode [part_number=1N4148 package="300 mil [THT]"]
  D30 = Rectifier Diode [part_number=1N4148 package="300 mil [THT]"]
  LED11 = LED - 5mm [color="Red (660nm)" package="5 mm [THT]"]
  LED12 = LED - 5mm [color="Red (660nm)" package="5 mm [THT]"]
  LED13 = LED - 5mm [color="Red (660nm)" package="5 mm [THT]"]
  LED14 = LED - 5mm [color="Red (660nm)" package="5 mm [THT]"]
  LED15 = LED - 5mm [color="Red (660nm)" package="5 mm [THT]"]
  LED16 = LED - 5mm [color="Red (660nm)" package="5 mm [THT]"]
  LED17 = LED - 5mm [color="Red (660nm)" package="5 mm [THT]"]
  LED18 = LED - 5mm [color="Red (660nm)" package="5 mm [THT]"]
  LED19 = LED - 5mm [color="Red (660nm)" package="5 mm [THT]"]
  LED20 = LED - 5mm [color="Red (660nm)" package="5 mm [THT]"]
  C22 = Electrolytic Capacitor [capacitance=4.7µF package="100 mil [THT, electrolytic]"]
  R109 = Resistor [tolerance=±5% resistance=560 package=THT]
  R110 = Resistor [tolerance=±5% resistance=560 package=THT]
  R111 = Resistor [tolerance=±5% resistance=4.7k package=THT]
  R8 = Resistor [tolerance=±5% resistance=560 package=THT]
  R113 = Resistor [tolerance=±5% resistance=47k package=THT]
  R114 = Resistor [tolerance=±5% resistance=560 package=THT]
  R3 = Resistor [tolerance=±5% resistance=4.7k package=THT]
  R116 = Resistor [tolerance=±5% resistance=560 package=THT]
  R117 = Resistor [tolerance=±5% resistance=560 package=THT]
  R118 = Resistor [tolerance=±5% resistance=33k package=THT]
  R119 = Resistor [tolerance=±5% resistance=10k package=THT]
  R1 = Resistor [tolerance=±5% resistance=10k package=THT]
  R121 = Resistor [tolerance=±5% resistance=47k package=THT]
  R122 = Resistor [tolerance=±5% resistance=4.7k package=THT]
  R5 = Resistor [tolerance=±5% resistance=100k package=THT]
  R124 = Resistor [tolerance=±5% resistance=560 package=THT]
  R125 = Resistor [tolerance=±5% resistance=560 package=THT]
  R126 = Resistor [tolerance=±5% resistance=10k package=THT]
  R127 = Resistor [tolerance=±5% resistance=33k package=THT]
  R7 = Resistor [tolerance=±5% resistance=560 package=THT]
  R4 = Resistor [tolerance=±5% resistance=4.7k package=THT]
  R130 = Resistor [tolerance=±5% resistance=2k package=THT]
  R6 = Resistor [tolerance=±5% resistance=560 package=THT]
  R132 = Resistor [tolerance=±5% resistance=2k package=THT]
  Q12 = NPN-Transistor [part_number=S9013 package="TO92 [THT]"]
  Q4 = NPN-Transistor [part_number=S9013 package="TO92 [THT]"]
  Q10 = NPN-Transistor [part_number=S9013 package="TO92 [THT]"]
  Q11 = NPN-Transistor [part_number=S9013 package="TO92 [THT]"]
  Q9 = NPN-Transistor [part_number=S9013 package="TO92 [THT]"]
  Q1 = NPN-Transistor [part_number=S9013 package="TO92 [THT]"]
  Q6 = NPN-Transistor [part_number=S9013 package="TO92 [THT]"]
  Q3 = NPN-Transistor [part_number=S9013 package="TO92 [THT]"]
  Q7 = NPN-Transistor [part_number=S9013 package="TO92 [THT]"]
  Q5 = NPN-Transistor [part_number=S9013 package="TO92 [THT]"]
  Q8 = NPN-Transistor [part_number=S9013 package="TO92 [THT]"]
  R81 = Trimmer Potentiometer [maximum_resistance=50kΩ package=THT]
  C2 = Ceramic Capacitor [capacitance=100nF package="100 mil [THT, multilayer]"]
  Q2 = PNP-Transistor [part_number=S9012 package="TO92 [THT]"]
  D61 = Rectifier Diode [part_number=1N4148 package="300 mil [THT]"]
  D62 = Rectifier Diode [part_number=1N4148 package="300 mil [THT]"]
  D1_2 = Rectifier Diode [part_number=1N4148 package="300 mil [THT]"]
  D64 = Rectifier Diode [part_number=1N4148 package="300 mil [THT]"]
  D65 = Rectifier Diode [part_number=1N4148 package="300 mil [THT]"]
  D66 = Rectifier Diode [part_number=1N4148 package="300 mil [THT]"]
  D67 = Rectifier Diode [part_number=1N4148 package="300 mil [THT]"]
  D68 = Rectifier Diode [part_number=1N4148 package="300 mil [THT]"]
  D69 = Rectifier Diode [part_number=1N4148 package="300 mil [THT]"]
  D70 = Rectifier Diode [part_number=1N4148 package="300 mil [THT]"]
  LED21 = LED - 5mm [color="Green (570nm)" package="5 mm [THT]"]
  LED22 = LED - 5mm [color="Green (570nm)" package="5 mm [THT]"]
  LED23 = LED - 5mm [color="Green (570nm)" package="5 mm [THT]"]
  LED24 = LED - 5mm [color="Green (570nm)" package="5 mm [THT]"]
  LED25 = LED - 5mm [color="Green (570nm)" package="5 mm [THT]"]
  LED26 = LED - 5mm [color="Green (570nm)" package="5 mm [THT]"]
  LED27 = LED - 5mm [color="Green (570nm)" package="5 mm [THT]"]
  LED28 = LED - 5mm [color="Green (565nm)" package="5 mm [THT]"]
  LED29 = LED - 5mm [color="Green (570nm)" package="5 mm [THT]"]
  LED30 = LED - 5mm [color="Green (570nm)" package="5 mm [THT]"]
  C1 = Electrolytic Capacitor [capacitance=4.7µF package="100 mil [THT, electrolytic]"]
  C2_2 = Electrolytic Capacitor [capacitance=4.7µF package="100 mil [THT, electrolytic]"]

nets:
  N1: MIC1.pin1, C13.+, R77.Pin_0
  GND: MIC1.pin2, Q37.E, R79.Pin_0, Q38.E, 9-15V.GND, C16.-, C17.-, U1.GND
  N2: C13.-, R78.Pin_0, Q37.B
  V6V: R77.Pin_1, R80.Pin_1, R83.Pin_1, C17.+, U1.output_voltage
  N3: R78.Pin_1, Q37.C, R80.Pin_0, R2.leg2
  N4: R2.leg1, R79.Pin_1
  N5: R2.wiper, C14.+
  N6: C14.-, Q38.B, R82.Pin_0
  N7: Q38.C, R82.Pin_1, R83.Pin_0, C15.+
  N8: 9-15V.VCC, D1.anode
  IN: C15.-, R26.leg2, R27.leg2, R81.leg2
  N9: D1.cathode, C16.+, U1.input_voltage
  N10: R26.leg1, R52.Pin_1
  N11: R26.wiper, R55.Pin_0
  N12: R52.Pin_0, Q25.E, C10.0, C12.-, Q26.E, Q27.E, Q28.E, Q29.E, Q30.E, Q31.E, Q32.E, Q33.E, Q34.E, Q35.E
  N13: R55.Pin_1, C9.1
  N14: C9.0, Q25.B, R60b.Pin_0
  N15: Q25.C, R60.Pin_1, R56.Pin_0, C11.1
  N16: C10.1, R60.Pin_0, R60b.Pin_1
  N17: R56.Pin_1, Q36.E, D41.cathode, LED1.anode, LED2.anode, LED3.anode, LED4.anode, LED5.anode, LED6.anode, LED7.anode, LED8.anode, LED9.anode, LED10.anode
  N18: C11.0, Q36.B, D41.anode
  N19: Q36.C, D42.anode, C12.+, R61.Pin_0
  N20: D42.cathode, R62.Pin_0, D43.anode
  N21: R61.Pin_1, Q26.B
  N22: Q26.C, R63.Pin_0
  N23: LED1.cathode, R63.Pin_1
  N24: R64.Pin_0, Q27.C
  N25: R64.Pin_1, LED2.cathode
  N26: R62.Pin_1, Q27.B
  N27: D43.cathode, R73.Pin_0, D44.anode
  N28: R73.Pin_1, Q28.B
  N29: R65.Pin_0, Q28.C
  N30: R65.Pin_1, LED3.cathode
  N31: D44.cathode, R74.Pin_0, D45.anode
  N32: R74.Pin_1, Q29.B
  N33: R66.Pin_0, Q29.C
  N34: R66.Pin_1, LED4.cathode
  N35: D45.cathode, R53.Pin_0, D46.anode
  N36: R53.Pin_1, Q30.B
  N37: R67.Pin_0, Q30.C
  N38: R67.Pin_1, LED5.cathode
  N39: D46.cathode, R54.Pin_0, D47.anode
  N40: R54.Pin_1, Q31.B
  N41: R68.Pin_0, Q31.C
  N42: R68.Pin_1, LED6.cathode
  N43: D47.cathode, R57.Pin_0, D48.anode
  N44: R57.Pin_1, Q32.B
  N45: R69.Pin_0, Q32.C
  N46: R69.Pin_1, LED7.cathode
  N47: D48.cathode, R58.Pin_0, D49.anode
  N48: R58.Pin_1, Q33.B
  N49: R70.Pin_0, Q33.C
  N50: R70.Pin_1, LED8.cathode
  N51: D49.cathode, R75.Pin_0, D50.anode
  N52: R75.Pin_1, Q34.B
  N53: R71.Pin_0, Q34.C
  N54: R71.Pin_1, LED9.cathode
  N55: D50.cathode, R76.Pin_0
  N56: R76.Pin_1, Q35.B
  N57: R72.Pin_0, Q35.C
  N58: R72.Pin_1, LED10.cathode
  N59: C18.-, R96.Pin_0, Q20.E, Q14.E, Q15.E, Q21.E, Q16.E, Q23.E, Q19.E, Q17.E, Q18.E, Q48.E, Q24.E
  N60: C18.+, R36.Pin_0, Q22.C, D22.anode
  N61: R45.Pin_0, Q21.C
  N62: R45.Pin_1, LED19.cathode
  N63: R43.Pin_0, Q19.C
  N64: R43.Pin_1, LED13.cathode
  N65: R33.Pin_0, D28.anode, D27.cathode
  N66: R33.Pin_1, Q20.B
  N67: R87.Pin_0, R95.Pin_1, Q48.C, C7.1, C8.1
  N68: R87.Pin_1, Q22.E, D21.cathode, LED11.anode, LED12.anode, LED13.anode, LED14.anode, LED15.anode, LED16.anode, LED17.anode, LED18.anode, LED19.anode, LED20.anode
  N69: R88.Pin_0, D26.cathode, D27.anode
  N70: R88.Pin_1, Q19.B
  N71: R44.Pin_0, Q20.C
  N72: R44.Pin_1, LED16.cathode
  N73: R39.Pin_0, Q15.C
  N74: R39.Pin_1, LED20.cathode
  N75: R47.Pin_0, Q24.C
  N76: R47.Pin_1, LED17.cathode
  N77: R37.Pin_0, D23.anode, D22.cathode
  N78: R37.Pin_1, Q15.B
  N79: R51.Pin_0, D30.cathode
  N80: R51.Pin_1, Q24.B
  N81: R50.Pin_0, D29.cathode, D30.anode
  N82: R50.Pin_1, Q23.B
  N83: R95.Pin_0, Q48.B, C5.0, C7.0
  N84: R96.Pin_1, R27.leg1
  N85: R49.Pin_0, D25.anode, D24.cathode
  N86: R49.Pin_1, Q17.B
  N87: R31.Pin_0, R27.wiper
  N88: R31.Pin_1, C5.1
  N89: R34.Pin_0, D29.anode, D28.cathode
  N90: R34.Pin_1, Q21.B
  N91: R41.Pin_0, Q17.C
  N92: R41.Pin_1, LED15.cathode
  N93: R36.Pin_1, Q14.B
  N94: R30.Pin_0, D26.anode, D25.cathode
  N95: R30.Pin_1, Q18.B
  N96: R48.Pin_0, D23.cathode, D24.anode
  N97: R48.Pin_1, Q16.B
  N98: R46.Pin_0, Q23.C
  N99: R46.Pin_1, LED18.cathode
  N100: R38.Pin_0, Q14.C
  N101: R38.Pin_1, LED11.cathode
  N102: R42.Pin_0, Q18.C
  N103: R42.Pin_1, LED12.cathode
  N104: R40.Pin_0, Q16.C
  N105: R40.Pin_1, LED14.cathode
  N106: C8.0, Q22.B, D21.anode
  N107: C22.-, R1.Pin_0, Q12.E, Q4.E, Q10.E, Q11.E, Q9.E, Q1.E, Q6.E, Q3.E, Q7.E, Q5.E, Q8.E
  N108: C22.+, R121.Pin_0, Q2.C, D67.anode
  N109: R109.Pin_0, Q6.C
  N110: R109.Pin_1, LED26.cathode
  N111: R110.Pin_0, Q12.C
  N112: R110.Pin_1, LED23.cathode
  N113: R111.Pin_0, D65.cathode, D66.anode
  N114: R111.Pin_1, Q9.B
  N115: R8.Pin_0, Q5.C
  N116: R8.Pin_1, LED24.cathode
  N117: R113.Pin_0, D67.cathode, D70.anode
  N118: R113.Pin_1, Q4.B
  N119: R114.Pin_0, Q10.C
  N120: R114.Pin_1, LED21.cathode
  N121: R3.Pin_0, R81.wiper
  N122: R3.Pin_1, C1.-
  N123: R116.Pin_0, Q8.C
  N124: R116.Pin_1, LED25.cathode
  N125: R117.Pin_0, Q7.C
  N126: R117.Pin_1, LED30.cathode
  N127: R118.Pin_0, D62.cathode, D69.anode
  N128: R118.Pin_1, Q6.B
  N129: R119.Pin_0, D65.anode, D68.cathode
  N130: R119.Pin_1, Q8.B
  N131: R1.Pin_1, R81.leg1
  N132: R121.Pin_1, Q3.B
  N133: R122.Pin_0, D64.anode, D66.cathode
  N134: R122.Pin_1, Q10.B
  N135: R5.Pin_0, Q1.B, C2.0, C1.+
  N136: R5.Pin_1, R4.Pin_0, Q1.C, C2.1, C2_2.-
  N137: R124.Pin_0, Q11.C
  N138: R124.Pin_1, LED29.cathode
  N139: R125.Pin_0, Q9.C
  N140: R125.Pin_1, LED28.cathode
  N141: R126.Pin_0, D68.anode, D69.cathode
  N142: R126.Pin_1, Q7.B
  N143: R127.Pin_0, D62.anode, D70.cathode
  N144: R127.Pin_1, Q5.B
  N145: R7.Pin_0, Q4.C
  N146: R7.Pin_1, LED27.cathode
  N147: R4.Pin_1, Q2.E, D1_2.cathode, LED21.anode, LED22.anode, LED23.anode, LED24.anode, LED25.anode, LED26.anode, LED27.anode, LED28.anode, LED29.anode, LED30.anode
  N148: R130.Pin_0, D61.cathode
  N149: R130.Pin_1, Q12.B
  N150: R6.Pin_0, Q3.C
  N151: R6.Pin_1, LED22.cathode
  N152: R132.Pin_0, D61.anode, D64.cathode
  N153: R132.Pin_1, Q11.B
  N154: Q2.B, D1_2.anode, C2_2.+

notes:
  I haven't bothered to layout the breadboard (since I'm using a PCB).
  See the schematic page for the circuit
