# Fritzing sketch 3x7 (saved by Fritzing 0.9.2b)
breadboards: 1

parts:
  R1 = Resistor [tolerance=±5% resistance=1k package=THT]
  LED1 = LED - 5mm [color="Red (633nm)" package="5 mm [THT]"]
  Ra1 = Resistor [tolerance=±5% resistance=680 package=THT]
  Ra2 = Resistor [tolerance=±5% resistance=470 package=THT]
  LED2 = LED - 5mm [color="Yellow (574nm)" package="5 mm [THT]"]
  LED3 = LED - 5mm [color="Red (633nm)" package="5 mm [THT]"]
  Ra3 = Resistor [tolerance=±5% resistance=680 package=THT]
  R2 = Resistor [tolerance=±5% resistance=1k package=THT]
  R3 = Resistor [tolerance=±5% resistance=1k package=THT]
  Q2 = Basic FET N-Channel [part_number=2N7000 package="TO220 [THT]"]
  Q3 = Basic FET N-Channel [part_number=2N7000 package="TO220 [THT]"]
  Q1 = Basic FET N-Channel [package="TO220 [THT]"]

nets:
  DIGIT_A_ENABLE -: R1.Pin_0, Q1.gate
  GND: R1.Pin_1, R2.Pin_1, R3.Pin_1, Q2.source, Q3.source, Q1.source
  N1: LED1.cathode, Q1.drain
  N2: LED1.anode, Ra1.Pin_1
  SEGMENT_ENABLE --: Ra1.Pin_0, Ra2.Pin_0, Ra3.Pin_0
  N3: Ra2.Pin_1, LED2.anode
  N4: LED2.cathode, Q2.drain
  N5: LED3.cathode, Q3.drain
  N6: LED3.anode, Ra3.Pin_1
  DIGIT_B_ENABLE -: R2.Pin_0, Q2.gate
  DIGIT_C_ENABLE -: R3.Pin_0, Q3.gate

notes:
  Digit "A" Enable
  Digit "B" Enable
  Digit "C" Enable
  Segment "a" Enable
  Schematic fragment - single segment control across 3 digits. Note: Ra1, Ra2 are 1kΩ in original kit, but swapped for 680Ω to equalise apparent brightness of read and yellow LEDs
  Circuit fragment - single segment control across 3 digits
