# Fritzing sketch LRThreeDigitDemo (saved by Fritzing 0.9.2b)
breadboards: 1

parts:
  3x8 = female pin header, 12 pins [form="♀ (female)"]
  TheCuttle = TheCuttle

nets:
  Seg_a: 3x8.pin1, TheCuttle.D11_(PWM)
  Seg_b: 3x8.pin2, TheCuttle.D10_(PWM)
  Seg_c: 3x8.pin3, TheCuttle.D9_(PWM)
  Seg_d: 3x8.pin4, TheCuttle.D8
  Seg_e: 3x8.pin5, TheCuttle.D7
  Seg_f: 3x8.pin6, TheCuttle.D6_(PWM)
  Seg_g: 3x8.pin7, TheCuttle.D5_(PWM)
  DigitC: 3x8.pin8, TheCuttle.D2
  DigitB: 3x8.pin9, TheCuttle.D3_(PWM)
  DigitA: 3x8.pin10, TheCuttle.D4
  GND: 3x8.pin11, 3x8.pin12, TheCuttle.GND#21

custom parts:
  TheCuttle: Boldport Cuttle Arduino-compatible Atmega328-based board
