# Fritzing sketch PomodoroTimer (saved by Fritzing 0.9.2b)
breadboards: 1

parts:
  U1 = atmega328 [package=dip]
  XTAL1 = Crystal [frequency="16 Mhz" package=THT]
  C1 = Ceramic Capacitor [capacitance=22pF package="100 mil [THT, multilayer]"]
  C2 = Ceramic Capacitor [capacitance=22pF package="100 mil [THT, multilayer]"]
  R1 = Resistor [tolerance=±5% resistance=10k package=THT]
  5V = Power plug
  3x9 = female pin header, 12 pins [form="♀ (female)"]
  S1 = Pushbutton [package="[THT]"]
  S2 = Pushbutton [package="[THT]"]

nets:
  N1: U1.RESET, R1.Pin_1
  N2: U1.D2, S1.Pin_1, S1.Pin_2
  N3: U1.D3_(PWM), S2.Pin_1, S2.Pin_2
  DigitA: U1.D4, 3x9.pin10
  vcc: U1.VCC, U1.AVCC, R1.Pin_0, 5V.VCC
  GND: U1.GND, C1.0, C2.1, 5V.GND, 3x9.pin11, 3x9.pin12, S1.Pin_3, S1.Pin_4, S2.Pin_3, S2.Pin_4
  N4: U1.XLAT1, XTAL1.pin_0, C1.1
  N5: U1.XLAT2, XTAL1.pin_1, C2.0
  DigitB: U1.D5_(PWM), 3x9.pin9
  DigitC: U1.D6_(PWM), 3x9.pin8
  Seg_g: U1.D7, 3x9.pin7
  Seg_f: U1.D8, 3x9.pin6
  Seg_e: U1.D9_(PWM), 3x9.pin5
  Seg_d: U1.D10_(PWM), 3x9.pin4
  Seg_c: U1.D11_(PWM), 3x9.pin3
  Seg_b: U1.D12, 3x9.pin2
  Seg_a: U1.D13, 3x9.pin1
