# Fritzing sketch RippleTester (saved by Fritzing 0.9.2b)
breadboards: 1

parts:
  IC1 = IC, DIP package, 16 pins [chip_label=CD4060]
  5V = Power plug
  C1 = Ceramic Capacitor [capacitance=100nF package="100 mil [THT, multilayer]"]
  R2 = Resistor [tolerance=±5% resistance=47k package=THT]
  R1 = Resistor [tolerance=±5% resistance=47k package=THT]
  IC2 = IC, DIP package, 16 pins [chip_label=CD4017 part_number=CD4017]
  3x7 = female pin header, 12 pins [form="♀ (female)"]

nets:
  D7: IC1.pin1, IC1.pin12, IC2.pin14
  Seg_c: IC1.pin4, 3x7.pin3
  Seg_b: IC1.pin5, 3x7.pin2
  Seg_d: IC1.pin6, 3x7.pin4
  Seg_a: IC1.pin7, 3x7.pin1
  GND: IC1.pin8, 5V.GND, IC2.pin8, IC2.pin13, 3x7.pin11, 3x7.pin12
  N1: IC1.pin9, C1.0
  N2: IC1.pin10, R1.Pin_0
  N3: IC1.pin11, R2.Pin_0
  Seg_f: IC1.pin13, 3x7.pin6
  Seg_e: IC1.pin14, 3x7.pin5
  Seg_g: IC1.pin15, 3x7.pin7
  VDD: IC1.pin16, 5V.VCC, IC2.pin16
  N4: C1.1, R2.Pin_1, R1.Pin_1
  DigitB: IC2.pin2, 3x7.pin9
  DigitA: IC2.pin3, 3x7.pin10
  DigitC: IC2.pin4, 3x7.pin8
  S3: IC2.pin7, IC2.pin15
