# Fritzing sketch Emergency (saved by Fritzing 0.9.2b)
breadboards: 2

parts:
  9V = Power plug
  5V = Power plug
  Q1 = 2N7000 FET N-Channel [part_number=2N7000 package=TO92]
  Q2 = NPN-Transistor [part_number=S9013 package="TO92 [THT]"]
  C1 = Electrolytic Capacitor [capacitance=330µF package="100 mil [THT, electrolytic]"]
  R1 = Resistor [tolerance=±5% resistance=1k package=THT]
  R2 = Resistor [tolerance=±5% resistance=220 package=THT]
  LED1 = LED - 3mm [color="Yellow (585nm)" package="3 mm [THT]"]
  C1_2 = Ceramic Capacitor [capacitance=100nF package="100 mil [THT, multilayer]"]
  R1_2 = Resistor [tolerance=±5% resistance=1k package=THT]
  LED1_2 = LED - 3mm [color="Yellow (585nm)" package="3 mm [THT]"]
  R2_2 = Resistor [tolerance=±5% resistance=220 package=THT]

nets:
  GND: 9V.GND, 5V.GND, Q1.source, C1.-, R2.Pin_0, C1_2.0
  N1: 9V.VCC, R1.Pin_0
  N2: 5V.VCC, C1_2.1, R1_2.Pin_0, R2_2.Pin_1
  N3: Q1.gate, R1_2.Pin_1
  N4: Q1.drain, LED1_2.cathode
  N5: Q2.E, C1.+, R1.Pin_1
  N6: Q2.C, LED1.anode
  N7: R2.Pin_1, LED1.cathode
  N8: LED1_2.anode, R2_2.Pin_0

notes:
  Original Circuit
  Revised Circuit

custom parts:
  2N7000 FET N-Channel: A 2N7000 MOSFET N-Channel Transistor
