# Fritzing sketch IxpandO (saved by Fritzing 0.9.2b)
breadboards: 1

parts:
  IC2 = IC, DIP package, 28 pins [chip_label=MCP23017]
  R1 = Resistor [tolerance=±5% resistance=4.7k package=THT]
  R2 = Resistor [tolerance=±5% resistance=4.7k package=THT]
  R3 = Resistor [tolerance=±5% resistance=4.7k package=THT]
  R4 = Resistor [tolerance=±5% resistance=4.7k package=THT]
  R5 = Resistor [tolerance=±5% resistance=4.7k package=THT]
  C1 = Ceramic Capacitor [capacitance=1µF package="100 mil [THT, multilayer]"]
  C2 = Ceramic Capacitor [capacitance=10µF package="100 mil [THT, multilayer]"]
  J1 = female pin header, 16 pins [form="♀ (female)"]
  J2 = female pin header, 8 pins [form="♀ (female)"]
  LED0 = LED - 5mm [color="Red (633nm)" package="5 mm [THT]"]
  R6 = Resistor [tolerance=±5% resistance=1k package=THT]
  LED1 = LED - 5mm [color="Red (633nm)" package="5 mm [THT]"]
  R7 = Resistor [tolerance=±5% resistance=1k package=THT]
  LED2 = LED - 5mm [color="Red (633nm)" package="5 mm [THT]"]
  LED3 = LED - 5mm [color="Red (633nm)" package="5 mm [THT]"]
  R8 = Resistor [tolerance=±5% resistance=1k package=THT]
  R9 = Resistor [tolerance=±5% resistance=1k package=THT]
  LED4 = LED - 5mm [color="Red (633nm)" package="5 mm [THT]"]
  LED5 = LED - 5mm [color="Red (633nm)" package="5 mm [THT]"]
  R10 = Resistor [tolerance=±5% resistance=1k package=THT]
  R11 = Resistor [tolerance=±5% resistance=1k package=THT]
  LED6 = LED - 5mm [color="Red (633nm)" package="5 mm [THT]"]
  LED7 = LED - 5mm [color="Red (633nm)" package="5 mm [THT]"]
  R12 = Resistor [tolerance=±5% resistance=1k package=THT]
  R13 = Resistor [tolerance=±5% resistance=1k package=THT]
  SW1 = DIP Switch 8 Position [package=dipswitch-08]
  B1 = TheCuttle

nets:
  GPB0: IC2.pin1, J1.pin1, LED0.anode
  GPB1: IC2.pin2, J1.pin2, LED1.anode
  GPB2: IC2.pin3, J1.pin3, LED2.anode
  GPB3: IC2.pin4, J1.pin4, LED3.anode
  GPB4: IC2.pin5, J1.pin5, LED4.anode
  GPB5: IC2.pin6, J1.pin6, LED5.anode
  GPB6: IC2.pin7, J1.pin7, LED6.anode
  GPB7: IC2.pin8, J1.pin8, LED7.anode
  VDD: IC2.pin9, R1.Pin_0, R2.Pin_0, R3.Pin_0, R4.Pin_0, R5.Pin_0, C1.0, C2.0, J2.pin6, J2.pin7, B1.VCC#6
  GND: IC2.pin10, IC2.pin15, IC2.pin16, IC2.pin17, C1.1, C2.1, J2.pin8, R6.Pin_1, R7.Pin_1, R8.Pin_1, R9.Pin_1, R10.Pin_1, R11.Pin_1, R12.Pin_1, R13.Pin_1, SW1.1, SW1.2, SW1.3, SW1.4, SW1.5, SW1.6, SW1.7, SW1.8, B1.GND#7
  SCK: IC2.pin12, R4.Pin_1, J2.pin4, B1.A5
  SDA: IC2.pin13, R5.Pin_1, J2.pin5, B1.A4
  RSTN: IC2.pin18, R1.Pin_1, J2.pin1
  INTB: IC2.pin19, R2.Pin_1, J2.pin2
  INTA: IC2.pin20, R3.Pin_1, J2.pin3, B1.D2
  GPA0: IC2.pin21, J1.pin16, SW1.16
  GPA1: IC2.pin22, J1.pin15, SW1.15
  GPA2: IC2.pin23, J1.pin14, SW1.14
  GPA3: IC2.pin24, J1.pin13, SW1.13
  GPA4: IC2.pin25, J1.pin12, SW1.12
  GPA5: IC2.pin26, J1.pin11, SW1.11
  GPA6: IC2.pin27, J1.pin10, SW1.10
  GPA7: IC2.pin28, J1.pin9, SW1.9
  N1: LED0.cathode, R6.Pin_0
  N2: LED1.cathode, R7.Pin_0
  N3: LED2.cathode, R8.Pin_0
  N4: LED3.cathode, R9.Pin_0
  N5: LED4.cathode, R10.Pin_0
  N6: LED5.cathode, R11.Pin_0
  N7: LED6.cathode, R13.Pin_0
  N8: LED7.cathode, R12.Pin_0

notes:
  peripheral option 1 - LEDs on Bank B
  peripheral option 2 - switches on Bank A
  optional controller (cuttle)
  not layed out - see IxpandO PCB

custom parts:
  TheCuttle: Boldport Cuttle Arduino-compatible Atmega328-based board
