# Fritzing sketch Juice (saved by Fritzing 0.9.2b)
breadboards: 1

parts:
  2_6-16V = Power plug
  LED1 = LED - 5mm [color="Red (633nm)" package="5 mm [THT]"]
  R6 = Resistor [tolerance=±5% resistance=1.2k package=THT]
  C1 = Ceramic Capacitor [capacitance=2.2µF package="100 mil [THT, multilayer]"]
  C2 = Ceramic Capacitor [capacitance=2.2µF package="100 mil [THT, multilayer]"]
  C3 = Electrolytic Capacitor [capacitance=10µF package="100 mil [THT, electrolytic]"]
  R1 = Resistor [tolerance=±5% resistance=1k package=THT]
  R2 = Resistor [tolerance=±5% resistance=3.3k package=THT]
  R3 = Resistor [tolerance=±5% resistance=1k package=THT]
  R4 = Resistor [tolerance=±5% resistance=5.6k package=THT]
  R5 = Resistor [tolerance=±5% resistance=1.2k package=THT]
  IC1 = IC, DIP package, 6 pins [chip_label=LDP]
  VO=1_47V = Pushbutton [package=THT]
  VO=3V = Pushbutton [package=THT]
  VO=4_53V = Pushbutton [package=THT]
  VR1 = Trimmer Potentiometer [maximum_resistance=20kΩ package=THT]
  VO=ADJ = Pushbutton [package=THT]
  LDO-OFF = Pushbutton [package=THT]

nets:
  GND: 2_6-16V.GND, R6.Pin_1, C1.0, C2.0, C3.-, R5.Pin_1, IC1.pin3, LDO-OFF.leg0
  N1: 2_6-16V.VCC, LED1.anode, C2.1, C3.+, R3.Pin_0, IC1.pin2
  N2: LED1.cathode, R6.Pin_0
  N3: C1.1, IC1.pin4, VO=1_47V.leg1, VO=3V.leg1, VO=4_53V.leg1, VO=ADJ.leg1
  N4: R1.Pin_0, VO=1_47V.leg0
  N5: R1.Pin_1, R2.Pin_1, R4.Pin_1, R5.Pin_0, IC1.pin5, VR1.leg2
  N6: R2.Pin_0, VO=3V.leg0
  N7: R3.Pin_1, IC1.pin1, LDO-OFF.leg1
  N8: R4.Pin_0, VO=4_53V.leg0
  N9: VR1.leg1, VR1.wiper, VO=ADJ.leg0

notes:
  breadboard not laid out - see schematic
