# Fritzing sketch Pease (saved by Fritzing 0.9.2b)
breadboards: 1

parts:
  IC1 = IC, DIP package, 8 pins [chip_label=LM331]
  R5 = Trimmer Potentiometer [maximum_resistance=5kΩ package=THT]
  Q4 = 2N7000 FET N-Channel [part_number=2N7000 package=TO92]
  LED1 = LED - 5mm [color="Green (555nm)" package="5 mm [THT]"]
  C1 = Ceramic Capacitor [capacitance=100nF package="100 mil [THT, multilayer]"]
  C2 = Ceramic Capacitor [capacitance=1µF package="100 mil [THT, multilayer]"]
  R4 = Resistor [tolerance=±5% resistance=5k package=THT]
  R3 = Resistor [tolerance=±5% resistance=3.3k package=THT]
  R6 = Resistor [tolerance=±5% resistance=220 package=THT]
  R2 = Resistor [tolerance=±5% resistance=10k package=THT]
  R1 = Resistor [tolerance=±5% resistance=1M package=THT]
  5-9V = Power plug
  S1 = Photocell (LDR) [part_number="20kΩ LDR" package=THT]

nets:
  N1: IC1.pin1, IC1.pin6, C2.1, R2.Pin_0
  N2: IC1.pin2, IC1.pin7, R4.Pin_0
  N3: IC1.pin3, Q4.gate, R3.Pin_1
  GND: IC1.pin4, R5.leg1, R5.wiper, Q4.source, C1.0, C2.0, 5-9V.GND, S1.pin_1
  N4: IC1.pin5, C1.1, R1.Pin_0
  Vs: IC1.pin8, R3.Pin_0, R6.Pin_0, R1.Pin_1, 5-9V.VCC
  N5: R5.leg2, R4.Pin_1
  N6: Q4.drain, LED1.cathode
  N7: LED1.anode, R6.Pin_1
  N8: R2.Pin_1, S1.pin_0

custom parts:
  2N7000 FET N-Channel: A 2N7000 MOSFET N-Channel Transistor
