# Fritzing sketch PissOff (saved by Fritzing 0.9.2b)
breadboards: 1

parts:
  IC2 = SO20W [chip_label=IC part_number=MKE04Z8VWJ4 package=SO(w)]
  Vbatt = 4 x AAA Battery Mount [part_number=3.5V-13.2V]
  IC1 = IC, DIP package, 8 pins [chip_label=IC part_number=TPA301DR]
  J1 = Piezo Speaker
  R21 = Resistor [tolerance=±5% resistance=47k package=THT]
  C1 = Ceramic Capacitor [capacitance=1µF package="100 mil [THT, multilayer]"]
  C6 = Ceramic Capacitor [capacitance=100nF package="100 mil [THT, multilayer]"]
  R1 = Resistor [tolerance=±5% resistance=1k package=THT]
  C2 = Ceramic Capacitor [capacitance=1µF package="100 mil [THT, multilayer]"]
  R5 = Resistor [tolerance=±5% resistance=47k package=THT]
  R2 = Resistor [tolerance=±5% resistance=8.2k package=THT]
  R3 = Resistor [tolerance=±5% resistance=8.2k package=THT]
  C3 = Ceramic Capacitor [capacitance=1µF package="100 mil [THT, multilayer]"]
  R9 = Resistor [tolerance=±5% resistance=220 package=THT]
  R11 = Resistor [tolerance=±5% resistance=220 package=THT]
  VR1 = Trimmer Potentiometer [maximum_resistance=50kΩ package=THT]
  R22 = Resistor [tolerance=±5% resistance=1k package=THT]
  R18 = Resistor [tolerance=±5% resistance=8.2k package=THT]
  R15 = Resistor [tolerance=±5% resistance=8.2k package=THT]
  R14 = Resistor [tolerance=±5% resistance=8.2k package=THT]
  R6 = Resistor [tolerance=±5% resistance=1k package=THT]
  R4 = Resistor [tolerance=±5% resistance=1k package=THT]
  R7 = Resistor [tolerance=±5% resistance=1k package=THT]
  R19 = Resistor [tolerance=±5% resistance=8.2k package=THT]
  R16 = Resistor [tolerance=±5% resistance=8.2k package=THT]
  R13 = Resistor [tolerance=±5% resistance=8.2k package=THT]
  R12 = Resistor [tolerance=±5% resistance=8.2k package=THT]
  R10 = Resistor [tolerance=±5% resistance=8.2k package=THT]
  R8 = Resistor [tolerance=±5% resistance=8.2k package=THT]
  IC3 = Voltage Regulator LDO [part_number=AP2210K-3.3TRG1 package=sot23-5]
  C5 = Ceramic Capacitor [capacitance=1µF package="100 mil [THT, multilayer]"]
  C7 = Ceramic Capacitor [capacitance=1µF package="100 mil [THT, multilayer]"]
  R20 = Resistor [tolerance=±5% resistance=47k package=THT]
  R24 = Resistor [tolerance=±5% resistance=47k package=THT]
  R25 = Resistor [tolerance=±5% resistance=47k package=THT]
  D1 = LTR-301 [package=ltr-301]
  D3 = smd LED [color="Orange (620nm)" package="0603 [SMD]"]
  R23 = Resistor [tolerance=±5% resistance=1k package=THT]
  IC4 = 2N7000 FET N-Channel [part_number=2N7000 package=TO92]
  R26 = Resistor [tolerance=±5% resistance=47k package=THT]
  R17 = Resistor [tolerance=±5% resistance=33 package=THT]
  D5 = smd LED [color="Infrared (940nm)" package="0603 [SMD]"]
  J9 = microSD Socket [package=usd-socket-pp]
  C4 = Ceramic Capacitor [capacitance=1µF package="100 mil [THT, multilayer]"]

nets:
  N1: IC2.1, R21.Pin_1
  SWD_DTO: IC2.2
  VCC: IC2.3, IC1.pin6, R21.Pin_0, C1.0, C6.1, R1.Pin_1, IC3.OUT, C5.1, D1.C, D3.anode, R26.Pin_1, R17.Pin_1, J9.VCC
  N2: IC2.4, C6.0
  DAC2: IC2.5, R16.Pin_0
  DAC1: IC2.6, R8.Pin_0
  SD_Chip_Select: IC2.7, J9.CS
  SD_Data_Out: IC2.8, J9.DO
  DAC6: IC2.9, R7.Pin_0
  DAC5: IC2.10, R4.Pin_0
  DAC4: IC2.11, R15.Pin_0, R14.Pin_0
  DAC3: IC2.12, R18.Pin_0
  SD_Data_In: IC2.13, J9.DI
  SD_Clock: IC2.14, J9.SCK
  Signal_TX: IC2.15
  Signal_RX: IC2.16
  AUDIO_Enable: IC2.17, IC1.pin1, R1.Pin_0
  Signal: IC2.18, IC4.gate, R26.Pin_0
  IR_input: IC2.19, R20.Pin_1, D1.E
  SWD_CLK: IC2.20
  GND: Vbatt.-, IC1.pin7, C1.1, C2.0, VR1.leg1, R22.Pin_0, IC3.GND, C5.0, C7.0, R25.Pin_0, IC4.source, J9.SHIELD, J9.GND, C4.0
  N3: Vbatt.+, IC3.IN, IC3.EN, C7.1
  N4: IC1.pin2, IC1.pin3, C2.1
  N5: IC1.pin4, R5.Pin_0, R2.Pin_1
  N6: IC1.pin5, J1.pin2, R5.Pin_1
  N7: IC1.pin8, J1.pin1
  N8: R2.Pin_0, R3.Pin_1
  N9: R3.Pin_0, C3.1
  AUDIO: C3.0, R9.Pin_1, R11.Pin_1, C4.1
  N10: R9.Pin_0, R11.Pin_0, VR1.wiper
  N11: VR1.leg2, R22.Pin_1, R18.Pin_1, R15.Pin_1, R14.Pin_1, R6.Pin_1, R7.Pin_1, R19.Pin_1, R13.Pin_1
  N12: R6.Pin_0, R4.Pin_1
  N13: R19.Pin_0, R16.Pin_1
  N14: R13.Pin_0, R12.Pin_1
  N15: R12.Pin_0, R10.Pin_1
  N16: R10.Pin_0, R8.Pin_1
  N17: R20.Pin_0, R24.Pin_1
  N18: R24.Pin_0, R25.Pin_1
  N19: D3.cathode, R23.Pin_1
  Signal_LED: R23.Pin_0, IC4.drain, D5.cathode
  N20: R17.Pin_0, D5.anode

notes:
  breadboard layout not provided (uses custom PCB)

custom parts:
  2N7000 FET N-Channel: A 2N7000 MOSFET N-Channel Transistor
