# Fritzing sketch SolarPendulum (saved by Fritzing 0.9.2b)
breadboards: 1

parts:
  PV1 = SOLAR-IXYS [package=solarbit-12x1]
  C1 = Electrolytic Capacitor [capacitance=2.2mF package="100 mil [THT, electrolytic]"]
  C2 = Electrolytic Capacitor [capacitance=1mF package="100 mil [THT, electrolytic]"]
  D1 = Rectifier Diode [part_number=1N5819 package="300 mil [THT]"]
  R1 = Resistor [tolerance=±5% resistance=100k package=THT]
  Q1 = NPN-Transistor [part_number=2N3904 package="TO92 [THT]"]
  Q2 = PNP-Transistor [part_number=2N3906 package="TO92 [THT]"]
  R2 = Resistor [tolerance=±5% resistance=100k package=THT]
  L1 = Inductor [package="400 mil [THT]"]

nets:
  GND: PV1.A, C1.-, C2.-, Q1.E, L1.pin_1
  N1: PV1.C, C1.+, D1.anode, Q2.E
  N2: C2.+, D1.cathode, R1.Pin_0
  N3: R1.Pin_1, Q1.B, R2.Pin_0
  N4: Q1.C, Q2.B
  N5: Q2.C, R2.Pin_1, L1.pin_0
