# Fritzing sketch ScopeTag (saved by Fritzing 0.9.2b)
breadboards: 1

parts:
  C5 = Ceramic Capacitor [capacitance=100nF package="100 mil [THT, multilayer]"]
  C6 = Ceramic Capacitor [capacitance=100nF package="100 mil [THT, multilayer]"]
  C3 = Ceramic Capacitor [capacitance=100nF package="100 mil [THT, multilayer]"]
  C7 = Ceramic Capacitor [capacitance=100nF package="100 mil [THT, multilayer]"]
  C1 = Ceramic Capacitor [capacitance=22pF package="100 mil [THT, multilayer]"]
  C2 = Ceramic Capacitor [capacitance=22pF package="100 mil [THT, multilayer]"]
  C4 = Electrolytic Capacitor [capacitance=10µF voltage=35V package="100 mil [THT, electrolytic]"]
  XTAL1 = Crystal [frequency="16 Mhz" package=THT]
  D1 = Rectifier Diode [part_number=1N4148 package="300 mil [THT]"]
  R1 = Resistor [tolerance=±5% resistance=10k package=THT]
  S1 = Pushbutton [package="[THT]"]
  U1 = atmega328 [package=dip]
  JP1 = Header 6 [package=1x06-smd]
  IC2 = IC, DIP package, 14 pins [chip_label=MCP42010]

nets:
  GND: C5.0, C6.0, C7.0, C1.0, C2.0, C4.-, S1.Pin_1, S1.Pin_2, U1.GND, JP1.6, IC2.pin4, IC2.pin5, IC2.pin10
  N1: C5.1, U1.AREF
  N2: C6.1, U1.AVCC
  N3: C3.0, D1.anode, R1.Pin_1, S1.Pin_3, S1.Pin_4, U1.RESET
  DTR: C3.1, JP1.1
  VCC: C7.1, C4.+, D1.cathode, R1.Pin_0, U1.VCC, JP1.4, IC2.pin7, IC2.pin8, IC2.pin11, IC2.pin12, IC2.pin14
  N4: C1.1, XTAL1.pin_1, U1.XLAT2
  N5: C2.1, XTAL1.pin_0, U1.XLAT1
  RX: U1.D0_(RX), JP1.3
  TX: U1.D1_(TX), JP1.2
  LATCH: U1.D9_(PWM), IC2.pin1
  DATA: U1.D11_(PWM), IC2.pin3
  CLOCK: U1.D13, IC2.pin2
  CTS: JP1.5
  CH2: IC2.pin6
  CH1: IC2.pin9

notes:
  CH1(X)
  CH2(Y)
