# Fritzing sketch TheGent (saved by Fritzing 0.9.2b)
breadboards: 1

parts:
  S1 = Toggle Switch [package=THT]
  D1 = LTR-301 [part_number=PT333-3C package=ltr-301]
  R1 = Resistor [tolerance=±5% resistance=390 package=THT]
  R2 = Resistor [tolerance=±5% resistance=390 package=THT]
  R3 = Resistor [tolerance=±5% resistance=390 package=THT]
  R4 = Resistor [tolerance=±5% resistance=390 package=THT]
  R5 = Resistor [tolerance=±5% resistance=390 package=THT]
  R6 = Resistor [tolerance=±5% resistance=390 package=THT]
  R7 = Resistor [tolerance=±5% resistance=390 package=THT]
  R8 = Resistor [tolerance=±5% resistance=390 package=THT]
  R9 = Resistor [tolerance=±5% resistance=820 package=THT]
  LED1 = LED - 5mm [color="Green (555nm)" package="5 mm [THT]"]
  LED2 = LED - 5mm [color="Orange (605nm)" package="5 mm [THT]"]
  LED3 = LED - 5mm [color="Green (555nm)" package="5 mm [THT]"]
  LED4 = LED - 5mm [color="Orange (605nm)" package="5 mm [THT]"]
  LED5 = LED - 5mm [color="Green (555nm)" package="5 mm [THT]"]
  Part1 = LilyPad Coin Cell Battery Holder
  Q1 = 2N7000 FET N-Channel [part_number=2N7000 package=TO92]
  R10 = Resistor [tolerance=±5% resistance=10k package=THT]

nets:
  N1: S1.L1, LED1.anode, LED2.anode, LED3.anode, LED4.anode, LED5.anode, R10.Pin_0
  N2: S1.COM, Part1.+
  N3: D1.C, Q1.gate, R10.Pin_1
  N4: D1.E, Part1.-, Q1.source
  N5: R1.Pin_0, LED1.cathode
  N6: R1.Pin_1, R2.Pin_0
  N7: R2.Pin_1, R4.Pin_1, R6.Pin_1, R8.Pin_1, R9.Pin_1, Q1.drain
  N8: R3.Pin_0, LED2.cathode
  N9: R3.Pin_1, R4.Pin_0
  N10: R5.Pin_0, LED3.cathode
  N11: R5.Pin_1, R6.Pin_0
  N12: R7.Pin_0, LED4.cathode
  N13: R7.Pin_1, R8.Pin_0
  N14: R9.Pin_0, LED5.cathode

custom parts:
  2N7000 FET N-Channel: A 2N7000 MOSFET N-Channel Transistor
