# Fritzing sketch TheLady (saved by Fritzing 0.9.2b)
breadboards: 1

parts:
  3V = Battery Holders [part_number=CR2032 package=battcon_20mm_4legs]
  R1 = Resistor [tolerance=±5% resistance=68 package=THT]
  LED1 = LED - 5mm [color="Red (633nm)" package="5 mm [THT]"]
  R2 = Resistor [tolerance=±5% resistance=68 package=THT]
  R3 = Resistor [tolerance=±5% resistance=68 package=THT]
  R4 = Resistor [tolerance=±5% resistance=68 package=THT]
  LED2 = LED - 5mm [color="Red (633nm)" package="5 mm [THT]"]
  R5 = Resistor [tolerance=±5% resistance=68 package=THT]
  R6 = Resistor [tolerance=±5% resistance=68 package=THT]
  LED3 = LED - 5mm [color="Red (633nm)" package="5 mm [THT]"]
  R7 = Resistor [tolerance=±5% resistance=68 package=THT]
  R8 = Resistor [tolerance=±5% resistance=68 package=THT]
  LED4 = LED - 5mm [color="Red (633nm)" package="5 mm [THT]"]
  R9 = Resistor [tolerance=±5% resistance=68 package=THT]
  R10 = Resistor [tolerance=±5% resistance=68 package=THT]
  LED5 = LED - 5mm [color="Red (633nm)" package="5 mm [THT]"]
  R11 = Resistor [tolerance=±5% resistance=68 package=THT]
  R12 = Resistor [tolerance=±5% resistance=68 package=THT]
  LED6 = LED - 5mm [color="Red (633nm)" package="5 mm [THT]"]
  S1 = Toggle Switch [package=THT]

nets:
  N1: 3V.+, S1.COM
  N2: 3V.-, LED1.cathode, LED2.cathode, LED3.cathode, LED4.cathode, LED5.cathode, LED6.cathode
  N3: R1.Pin_0, R3.Pin_0, R5.Pin_0, R7.Pin_0, R9.Pin_0, R11.Pin_0, S1.L1
  N4: R1.Pin_1, R2.Pin_0
  N5: LED1.anode, R2.Pin_1
  N6: R3.Pin_1, R4.Pin_0
  N7: R4.Pin_1, LED2.anode
  N8: R5.Pin_1, R6.Pin_0
  N9: R6.Pin_1, LED3.anode
  N10: R7.Pin_1, R8.Pin_0
  N11: R8.Pin_1, LED4.anode
  N12: R9.Pin_1, R10.Pin_0
  N13: R10.Pin_1, LED5.anode
  N14: R11.Pin_1, R12.Pin_0
  N15: R12.Pin_1, LED6.anode
