# Fritzing sketch Firecracker (saved by Fritzing 0.9.2b)
breadboards: 1

parts:
  B2 = female pin header, 8 pins [form="♀ (female)" part_number=TheMatrix]
  B1 = TheCuttle [part_number=TheCuttle]
  T1 = LM35 Temperature Sensor [package="TO92 [THT]"]

nets:
  VCC: B2.pin1, B2.pin2, B1.VCC#6, T1.+Vs
  GND: B2.pin3, B1.GND#7, T1.GND
  IRQ: B2.pin4
  SYNC: B2.pin5
  RSTN: B2.pin6
  SDA: B2.pin7, B1.A4
  SCL: B2.pin8, B1.A5
  TEMP: B1.A0, T1.Vout

notes:
  TheMatrix connector

custom parts:
  TheCuttle: Boldport Cuttle Arduino-compatible Atmega328-based board
