# Fritzing sketch GrandFinale (saved by Fritzing 1.0.1rc)
breadboards: 1

parts:
  B2 = female pin header, 8 pins [form="♀ (female)" part_number=TheMatrix]
  Part1 = Arduino Uno (Rev3)

nets:
  VCC: B2.pin1, B2.pin2, Part1.5V
  GND: B2.pin3, Part1.GND
  IRQ: B2.pin4
  SYNC: B2.pin5
  RSTN: B2.pin6
  SDA: B2.pin7, Part1.A4/SDA
  SCL: B2.pin8, Part1.A5/SCL

notes:
  TheMatrix connector
