# Fritzing sketch KeypadControl (saved by Fritzing 0.9.2b)
breadboards: 1

parts:
  KEYA = shrouded pin header, 10 pins [form="♂ (shrouded male)"]
  LED = shrouded pin header, 10 pins [form="♂ (shrouded male)"]
  KEYB = shrouded pin header, 6 pins [form="♂ (shrouded male)"]
  B3 = female pin header, 8 pins [form="♀ (female)" part_number=TheMatrix]
  B4 = TheCuttle

nets:
  R4: KEYA.pin2, B4.D9_(PWM)
  R2: KEYA.pin3, B4.D7
  L4: KEYA.pin4, B4.D5_(PWM)
  L2: KEYA.pin5, B4.D3_(PWM)
  L1: KEYA.pin6, B4.D2
  L3: KEYA.pin7, B4.D4
  R1: KEYA.pin8, B4.D6_(PWM)
  R3: KEYA.pin9, B4.D8
  D8: LED.pin2
  D6: LED.pin3
  D4: LED.pin4
  D2: LED.pin5
  D1: LED.pin6
  D3: LED.pin7
  D5: LED.pin8
  D7: LED.pin9
  GND: KEYB.pin1, B3.pin3, B4.GND#7
  S4: KEYB.pin2, B4.D13
  S2: KEYB.pin3, B4.D11_(PWM)
  S1: KEYB.pin4, B4.D10_(PWM)
  S3: KEYB.pin5, B4.D12
  VCC: KEYB.pin6, B3.pin1, B3.pin2, B4.VCC#6
  IRQ: B3.pin4
  SYNC: B3.pin5
  RSTN: B3.pin6
  SDA: B3.pin7, B4.A4
  SCL: B3.pin8, B4.A5

notes:
  These are the three connectors on the KeyboardMatrixModule
  This is The Matrix connector

custom parts:
  TheCuttle: Boldport Cuttle Arduino-compatible Atmega328-based board
