# Fritzing sketch LedTest (saved by Fritzing 0.9.2b)

parts:
  Part1 = Arduino Uno (Rev3)
  Matrix = female pin header, 8 pins [form="♀ (female)"]

nets:
  SDA: Part1.A4/SDA, Matrix.pin7
  SCL: Part1.A5/SCL, Matrix.pin8
  GND: Part1.GND, Matrix.pin3
  VCC: Part1.5V, Matrix.pin1, Matrix.pin2
  IRQ: Matrix.pin4
  SYNC: Matrix.pin5
  RSTN: Matrix.pin6
