# Fritzing sketch TheMatrix (saved by Fritzing 0.9.2b)
breadboards: 1

parts:
  IC1 = IC, DIP package, 28 pins [chip_label=AS1130]
  R1 = Resistor [tolerance=±5% resistance=4.7k package=THT]
  R2 = Resistor [tolerance=±5% resistance=4.7k package=THT]
  R3 = Resistor [tolerance=±5% resistance=4.7k package=THT]
  R4 = Resistor [tolerance=±5% resistance=4.7k package=THT]
  J1 = female pin header, 8 pins [form="♀ (female)"]
  C1 = Ceramic Capacitor [capacitance=100nF package="100 mil [THT, multilayer]"]
  C2 = Ceramic Capacitor [capacitance=10µF package="100 mil [THT, multilayer]"]
  LED1 = LED - 5mm [color="Red (633nm)" package="5 mm [THT]"]
  LED2 = LED - 5mm [color="Red (633nm)" package="5 mm [THT]"]
  LED3 = LED - 5mm [color="Red (633nm)" package="5 mm [THT]"]
  LED4 = LED - 5mm [color="Red (633nm)" package="5 mm [THT]"]
  LED5 = LED - 5mm [color="Red (633nm)" package="5 mm [THT]"]
  LED6 = LED - 5mm [color="Red (633nm)" package="5 mm [THT]"]
  LED7 = LED - 5mm [color="Red (633nm)" package="5 mm [THT]"]
  LED8 = LED - 5mm [color="Red (633nm)" package="5 mm [THT]"]
  LED9 = LED - 5mm [color="Red (633nm)" package="5 mm [THT]"]
  LED10 = LED - 5mm [color="Red (633nm)" package="5 mm [THT]"]
  LED11 = LED - 5mm [color="Red (633nm)" package="5 mm [THT]"]
  LED20 = LED - 5mm [color="Red (633nm)" package="5 mm [THT]"]
  LED19 = LED - 5mm [color="Red (633nm)" package="5 mm [THT]"]
  LED15 = LED - 5mm [color="Red (633nm)" package="5 mm [THT]"]
  LED14 = LED - 5mm [color="Red (633nm)" package="5 mm [THT]"]
  LED12 = LED - 5mm [color="Red (633nm)" package="5 mm [THT]"]
  LED16 = LED - 5mm [color="Red (633nm)" package="5 mm [THT]"]
  LED17 = LED - 5mm [color="Red (633nm)" package="5 mm [THT]"]
  LED13 = LED - 5mm [color="Red (633nm)" package="5 mm [THT]"]
  LED18 = LED - 5mm [color="Red (633nm)" package="5 mm [THT]"]
  R5 = Resistor [tolerance=±5% resistance=4.7k part_number=optional package=THT]
  LED21 = LED - 5mm [color="Red (633nm)" package="5 mm [THT]"]
  LED24 = LED - 5mm [color="Red (633nm)" package="5 mm [THT]"]
  LED31 = LED - 5mm [color="Red (633nm)" package="5 mm [THT]"]
  LED36 = LED - 5mm [color="Red (633nm)" package="5 mm [THT]"]
  LED37 = LED - 5mm [color="Red (633nm)" package="5 mm [THT]"]
  LED33 = LED - 5mm [color="Red (633nm)" package="5 mm [THT]"]
  LED27 = LED - 5mm [color="Red (633nm)" package="5 mm [THT]"]
  LED32 = LED - 5mm [color="Red (633nm)" package="5 mm [THT]"]
  LED34 = LED - 5mm [color="Red (633nm)" package="5 mm [THT]"]
  LED40 = LED - 5mm [color="Red (633nm)" package="5 mm [THT]"]
  LED26 = LED - 5mm [color="Red (633nm)" package="5 mm [THT]"]
  LED22 = LED - 5mm [color="Red (633nm)" package="5 mm [THT]"]
  LED29 = LED - 5mm [color="Red (633nm)" package="5 mm [THT]"]
  LED39 = LED - 5mm [color="Red (633nm)" package="5 mm [THT]"]
  LED25 = LED - 5mm [color="Red (633nm)" package="5 mm [THT]"]
  LED30 = LED - 5mm [color="Red (633nm)" package="5 mm [THT]"]
  LED28 = LED - 5mm [color="Red (633nm)" package="5 mm [THT]"]
  LED38 = LED - 5mm [color="Red (633nm)" package="5 mm [THT]"]
  LED35 = LED - 5mm [color="Red (633nm)" package="5 mm [THT]"]
  LED23 = LED - 5mm [color="Red (633nm)" package="5 mm [THT]"]
  LED56 = LED - 5mm [color="Red (633nm)" package="5 mm [THT]"]
  LED54 = LED - 5mm [color="Red (633nm)" package="5 mm [THT]"]
  LED55 = LED - 5mm [color="Red (633nm)" package="5 mm [THT]"]
  LED58 = LED - 5mm [color="Red (633nm)" package="5 mm [THT]"]
  LED43 = LED - 5mm [color="Red (633nm)" package="5 mm [THT]"]
  LED47 = LED - 5mm [color="Red (633nm)" package="5 mm [THT]"]
  LED59 = LED - 5mm [color="Red (633nm)" package="5 mm [THT]"]
  LED50 = LED - 5mm [color="Red (633nm)" package="5 mm [THT]"]
  LED41 = LED - 5mm [color="Red (633nm)" package="5 mm [THT]"]
  LED52 = LED - 5mm [color="Red (633nm)" package="5 mm [THT]"]
  LED57 = LED - 5mm [color="Red (633nm)" package="5 mm [THT]"]
  LED60 = LED - 5mm [color="Red (633nm)" package="5 mm [THT]"]
  LED42 = LED - 5mm [color="Red (633nm)" package="5 mm [THT]"]
  LED46 = LED - 5mm [color="Red (633nm)" package="5 mm [THT]"]
  LED51 = LED - 5mm [color="Red (633nm)" package="5 mm [THT]"]
  LED44 = LED - 5mm [color="Red (633nm)" package="5 mm [THT]"]
  LED53 = LED - 5mm [color="Red (633nm)" package="5 mm [THT]"]
  LED49 = LED - 5mm [color="Red (633nm)" package="5 mm [THT]"]
  LED45 = LED - 5mm [color="Red (633nm)" package="5 mm [THT]"]
  LED48 = LED - 5mm [color="Red (633nm)" package="5 mm [THT]"]
  LED68 = LED - 5mm [color="Red (633nm)" package="5 mm [THT]"]
  LED77 = LED - 5mm [color="Red (633nm)" package="5 mm [THT]"]
  LED79 = LED - 5mm [color="Red (633nm)" package="5 mm [THT]"]
  LED67 = LED - 5mm [color="Red (633nm)" package="5 mm [THT]"]
  LED80 = LED - 5mm [color="Red (633nm)" package="5 mm [THT]"]
  LED73 = LED - 5mm [color="Red (633nm)" package="5 mm [THT]"]
  LED78 = LED - 5mm [color="Red (633nm)" package="5 mm [THT]"]
  LED61 = LED - 5mm [color="Red (633nm)" package="5 mm [THT]"]
  LED70 = LED - 5mm [color="Red (633nm)" package="5 mm [THT]"]
  LED66 = LED - 5mm [color="Red (633nm)" package="5 mm [THT]"]
  LED63 = LED - 5mm [color="Red (633nm)" package="5 mm [THT]"]
  LED74 = LED - 5mm [color="Red (633nm)" package="5 mm [THT]"]
  LED64 = LED - 5mm [color="Red (633nm)" package="5 mm [THT]"]
  LED65 = LED - 5mm [color="Red (633nm)" package="5 mm [THT]"]
  LED75 = LED - 5mm [color="Red (633nm)" package="5 mm [THT]"]
  LED72 = LED - 5mm [color="Red (633nm)" package="5 mm [THT]"]
  LED71 = LED - 5mm [color="Red (633nm)" package="5 mm [THT]"]
  LED62 = LED - 5mm [color="Red (633nm)" package="5 mm [THT]"]
  LED76 = LED - 5mm [color="Red (633nm)" package="5 mm [THT]"]
  LED69 = LED - 5mm [color="Red (633nm)" package="5 mm [THT]"]
  LED100 = LED - 5mm [color="Red (633nm)" package="5 mm [THT]"]
  LED96 = LED - 5mm [color="Red (633nm)" package="5 mm [THT]"]
  LED99 = LED - 5mm [color="Red (633nm)" package="5 mm [THT]"]
  LED91 = LED - 5mm [color="Red (633nm)" package="5 mm [THT]"]
  LED84 = LED - 5mm [color="Red (633nm)" package="5 mm [THT]"]
  LED94 = LED - 5mm [color="Red (633nm)" package="5 mm [THT]"]
  LED86 = LED - 5mm [color="Red (633nm)" package="5 mm [THT]"]
  LED88 = LED - 5mm [color="Red (633nm)" package="5 mm [THT]"]
  LED89 = LED - 5mm [color="Red (633nm)" package="5 mm [THT]"]
  LED87 = LED - 5mm [color="Red (633nm)" package="5 mm [THT]"]
  LED93 = LED - 5mm [color="Red (633nm)" package="5 mm [THT]"]
  LED83 = LED - 5mm [color="Red (633nm)" package="5 mm [THT]"]
  LED81 = LED - 5mm [color="Red (633nm)" package="5 mm [THT]"]
  LED85 = LED - 5mm [color="Red (633nm)" package="5 mm [THT]"]
  LED97 = LED - 5mm [color="Red (633nm)" package="5 mm [THT]"]
  LED98 = LED - 5mm [color="Red (633nm)" package="5 mm [THT]"]
  LED90 = LED - 5mm [color="Red (633nm)" package="5 mm [THT]"]
  LED82 = LED - 5mm [color="Red (633nm)" package="5 mm [THT]"]
  LED92 = LED - 5mm [color="Red (633nm)" package="5 mm [THT]"]
  LED95 = LED - 5mm [color="Red (633nm)" package="5 mm [THT]"]
  LED118 = LED - 5mm [color="Red (633nm)" package="5 mm [THT]"]
  LED108 = LED - 5mm [color="Red (633nm)" package="5 mm [THT]"]
  LED111 = LED - 5mm [color="Red (633nm)" package="5 mm [THT]"]
  LED104 = LED - 5mm [color="Red (633nm)" package="5 mm [THT]"]
  LED120 = LED - 5mm [color="Red (633nm)" package="5 mm [THT]"]
  LED115 = LED - 5mm [color="Red (633nm)" package="5 mm [THT]"]
  LED112 = LED - 5mm [color="Red (633nm)" package="5 mm [THT]"]
  LED119 = LED - 5mm [color="Red (633nm)" package="5 mm [THT]"]
  LED105 = LED - 5mm [color="Red (633nm)" package="5 mm [THT]"]
  LED102 = LED - 5mm [color="Red (633nm)" package="5 mm [THT]"]
  LED106 = LED - 5mm [color="Red (633nm)" package="5 mm [THT]"]
  LED114 = LED - 5mm [color="Red (633nm)" package="5 mm [THT]"]
  LED101 = LED - 5mm [color="Red (633nm)" package="5 mm [THT]"]
  LED110 = LED - 5mm [color="Red (633nm)" package="5 mm [THT]"]
  LED107 = LED - 5mm [color="Red (633nm)" package="5 mm [THT]"]
  LED109 = LED - 5mm [color="Red (633nm)" package="5 mm [THT]"]
  LED103 = LED - 5mm [color="Red (633nm)" package="5 mm [THT]"]
  LED113 = LED - 5mm [color="Red (633nm)" package="5 mm [THT]"]
  LED117 = LED - 5mm [color="Red (633nm)" package="5 mm [THT]"]
  LED116 = LED - 5mm [color="Red (633nm)" package="5 mm [THT]"]

nets:
  GND: IC1.pin1, IC1.pin7, IC1.pin14, IC1.pin22, IC1.pin28, J1.pin3, C1.0, C2.0, R5.Pin_1
  CS6: IC1.pin2, LED4.anode, LED14.anode, LED24.anode, LED34.anode, LED56.cathode, LED54.cathode, LED55.cathode, LED58.cathode, LED59.cathode, LED52.cathode, LED57.cathode, LED60.cathode, LED51.cathode, LED44.anode, LED53.cathode, LED65.anode, LED75.anode, LED85.anode, LED95.anode, LED115.anode, LED105.anode
  VCC: IC1.pin3, IC1.pin10, IC1.pin18, IC1.pin19, IC1.pin26, R1.Pin_0, R2.Pin_0, R3.Pin_0, R4.Pin_0, J1.pin1, J1.pin2, C1.1, C2.1
  CS7: IC1.pin4, LED3.anode, LED13.anode, LED33.anode, LED23.anode, LED54.anode, LED43.cathode, LED47.cathode, LED50.cathode, LED41.cathode, LED42.cathode, LED46.cathode, LED44.cathode, LED49.cathode, LED45.cathode, LED48.cathode, LED74.anode, LED64.anode, LED84.anode, LED94.anode, LED104.anode, LED114.anode
  CS8: IC1.pin5, LED2.anode, LED12.anode, LED31.cathode, LED36.cathode, LED37.cathode, LED33.cathode, LED32.cathode, LED34.cathode, LED40.cathode, LED22.anode, LED39.cathode, LED38.cathode, LED35.cathode, LED43.anode, LED53.anode, LED73.anode, LED63.anode, LED93.anode, LED83.anode, LED103.anode, LED113.anode
  CS9: IC1.pin6, LED1.anode, LED11.anode, LED21.cathode, LED24.cathode, LED27.cathode, LED32.anode, LED26.cathode, LED22.cathode, LED29.cathode, LED25.cathode, LED30.cathode, LED28.cathode, LED23.cathode, LED52.anode, LED42.anode, LED72.anode, LED62.anode, LED82.anode, LED92.anode, LED112.anode, LED102.anode
  CS11: IC1.pin8, LED1.cathode, LED2.cathode, LED3.cathode, LED4.cathode, LED5.cathode, LED6.cathode, LED7.cathode, LED8.cathode, LED9.cathode, LED10.cathode
  CS10: IC1.pin9, LED11.cathode, LED20.cathode, LED19.cathode, LED15.cathode, LED14.cathode, LED12.cathode, LED16.cathode, LED17.cathode, LED13.cathode, LED18.cathode, LED21.anode, LED31.anode, LED41.anode, LED51.anode, LED61.anode, LED71.anode, LED91.anode, LED81.anode, LED111.anode, LED101.anode
  IRQ: IC1.pin11, R2.Pin_1, J1.pin4
  SYNC: IC1.pin12, J1.pin5
  RSTN: IC1.pin13, R1.Pin_1, J1.pin6
  SCL: IC1.pin15, R3.Pin_1, J1.pin8
  SDA: IC1.pin16, R4.Pin_1, J1.pin7
  N1: IC1.pin17, R5.Pin_0
  CS5: IC1.pin20, LED5.anode, LED15.anode, LED25.anode, LED35.anode, LED55.anode, LED45.anode, LED68.cathode, LED67.cathode, LED80.anode, LED61.cathode, LED70.cathode, LED66.cathode, LED63.cathode, LED64.cathode, LED65.cathode, LED62.cathode, LED69.cathode, LED100.anode, LED90.anode, LED120.anode, LED110.anode
  CS4: IC1.pin21, LED10.anode, LED20.anode, LED40.anode, LED30.anode, LED50.anode, LED60.anode, LED77.cathode, LED79.cathode, LED80.cathode, LED73.cathode, LED78.cathode, LED70.anode, LED74.cathode, LED75.cathode, LED72.cathode, LED71.cathode, LED76.cathode, LED99.anode, LED89.anode, LED119.anode, LED109.anode
  CS2: IC1.pin23, LED8.anode, LED18.anode, LED28.anode, LED38.anode, LED58.anode, LED48.anode, LED68.anode, LED78.anode, LED100.cathode, LED96.cathode, LED99.cathode, LED91.cathode, LED94.cathode, LED88.anode, LED93.cathode, LED97.cathode, LED98.cathode, LED92.cathode, LED95.cathode, LED107.anode, LED117.anode
  CS3: IC1.pin24, LED9.anode, LED19.anode, LED29.anode, LED39.anode, LED59.anode, LED49.anode, LED79.anode, LED69.anode, LED84.cathode, LED86.cathode, LED88.cathode, LED89.cathode, LED87.cathode, LED83.cathode, LED81.cathode, LED85.cathode, LED98.anode, LED90.cathode, LED82.cathode, LED118.anode, LED108.anode
  CS0: IC1.pin25, LED6.anode, LED16.anode, LED36.anode, LED26.anode, LED56.anode, LED46.anode, LED66.anode, LED76.anode, LED96.anode, LED86.anode, LED118.cathode, LED111.cathode, LED120.cathode, LED115.cathode, LED112.cathode, LED119.cathode, LED106.anode, LED114.cathode, LED113.cathode, LED117.cathode, LED116.cathode
  CS1: IC1.pin27, LED7.anode, LED17.anode, LED37.anode, LED27.anode, LED47.anode, LED57.anode, LED77.anode, LED67.anode, LED87.anode, LED97.anode, LED108.cathode, LED104.cathode, LED105.cathode, LED102.cathode, LED106.cathode, LED101.cathode, LED110.cathode, LED107.cathode, LED109.cathode, LED103.cathode, LED116.anode

notes:
  This is built on the Boldport Matrix PCB; breadboard layout not completed
