# Fritzing sketch TheMonarch (saved by Fritzing 0.9.2b)
breadboards: 1

parts:
  IC1 = 555 Timer [package="DIP8 [THT]"]
  IC3 = IC, DIP package, 20 pins [chip_label=74HC273]
  R1 = Resistor [tolerance=±5% resistance=10k package=THT]
  R2 = Resistor [tolerance=±5% resistance=10k package=THT]
  C1 = Ceramic Capacitor [capacitance=1µF package="100 mil [THT, multilayer]"]
  IC2 = IC, DIP package, 14 pins [chip_label=74HC86]
  C2 = Ceramic Capacitor [capacitance=1µF package="100 mil [THT, multilayer]"]
  Vbatt = LilyPad Coin Cell Battery Holder
  R3 = Resistor [tolerance=±5% resistance=10k package=THT]
  R4 = Resistor [tolerance=±5% resistance=560 package=THT]
  R5 = Resistor [tolerance=±5% resistance=560 package=THT]
  LED1 = LED - 5mm [color="Red (633nm)" package="5 mm [THT]"]
  R6 = Resistor [tolerance=±5% resistance=560 package=THT]
  R7 = Resistor [tolerance=±5% resistance=560 package=THT]
  LED2 = LED - 5mm [color="Red (633nm)" package="5 mm [THT]"]
  R8 = Resistor [tolerance=±5% resistance=560 package=THT]
  R9 = Resistor [tolerance=±5% resistance=560 package=THT]
  LED3 = LED - 5mm [color="Red (633nm)" package="5 mm [THT]"]
  R10 = Resistor [tolerance=±5% resistance=560 package=THT]
  R11 = Resistor [tolerance=±5% resistance=560 package=THT]
  LED4 = LED - 5mm [color="Red (633nm)" package="5 mm [THT]"]
  R12 = Resistor [tolerance=±5% resistance=560 package=THT]
  R13 = Resistor [tolerance=±5% resistance=560 package=THT]
  LED5 = LED - 5mm [color="Red (633nm)" package="5 mm [THT]"]
  R14 = Resistor [tolerance=±5% resistance=560 package=THT]
  R15 = Resistor [tolerance=±5% resistance=560 package=THT]
  LED6 = LED - 5mm [color="Red (633nm)" package="5 mm [THT]"]
  R16 = Resistor [tolerance=±5% resistance=560 package=THT]
  R17 = Resistor [tolerance=±5% resistance=560 package=THT]
  LED7 = LED - 5mm [color="Red (633nm)" package="5 mm [THT]"]
  R18 = Resistor [tolerance=±5% resistance=560 package=THT]
  R19 = Resistor [tolerance=±5% resistance=560 package=THT]
  LED8 = LED - 5mm [color="Red (633nm)" package="5 mm [THT]"]

nets:
  GND: IC1.Ground, IC3.pin10, C1.0, IC2.pin7, C2.0, Vbatt.-, R3.Pin_1, LED1.cathode, LED2.cathode, LED3.cathode, LED4.cathode, LED5.cathode, LED6.cathode, LED7.cathode, LED8.cathode
  N1: IC1.Trigger, IC1.Threshold, R2.Pin_1, C1.1
  CLK: IC1.Output, IC3.pin11
  N2: IC1.Reset, R3.Pin_0
  N3: IC1.Discharge, R1.Pin_1, R2.Pin_0
  3.3V: IC1.Vcc_Supply_Voltage, IC3.pin1, IC3.pin20, R1.Pin_0, IC2.pin14, C2.1, Vbatt.+
  OUT1: IC3.pin2, IC3.pin4, R4.Pin_1
  Y4: IC3.pin3, IC2.pin11
  OUT2: IC3.pin5, IC3.pin7, R6.Pin_1
  OUT3: IC3.pin6, IC3.pin8, R9.Pin_1
  OUT4: IC3.pin9, IC3.pin13, IC2.pin12, R11.Pin_1
  OUT5: IC3.pin12, IC3.pin14, R13.Pin_1
  OUT6: IC3.pin15, IC3.pin17, IC2.pin1, R14.Pin_1
  OUT7: IC3.pin16, IC3.pin18, IC2.pin4, R16.Pin_1
  OUT8: IC3.pin19, IC2.pin5, R19.Pin_1
  N4: IC2.pin2, IC2.pin6
  N5: IC2.pin3, IC2.pin13
  N6: R4.Pin_0, R5.Pin_1
  N7: R5.Pin_0, LED1.anode
  N8: R6.Pin_0, R7.Pin_1
  N9: R7.Pin_0, LED2.anode
  N10: R8.Pin_0, LED3.anode
  N11: R8.Pin_1, R9.Pin_0
  N12: R10.Pin_0, LED4.anode
  N13: R10.Pin_1, R11.Pin_0
  N14: R12.Pin_0, LED5.anode
  N15: R12.Pin_1, R13.Pin_0
  N16: R14.Pin_0, R15.Pin_1
  N17: R15.Pin_0, LED6.anode
  N18: R16.Pin_0, R17.Pin_1
  N19: R17.Pin_0, LED7.anode
  N20: R18.Pin_0, LED8.anode
  N21: R18.Pin_1, R19.Pin_0
