# Fritzing sketch Touchy (saved by Fritzing 0.9.2b)
breadboards: 1

parts:
  U1 = IC, DIP package, 24 pins [chip_label=EFM8SB1]
  C1 = Ceramic Capacitor [capacitance=1µF package="100 mil [THT, multilayer]"]
  C2 = Ceramic Capacitor [capacitance=100nF package="100 mil [THT, multilayer]"]
  VBB = Battery
  R1 = Resistor [tolerance=±5% resistance=1k package=THT]
  LED1 = LED - 5mm [color="Orange (605nm)" package="5 mm [THT]"]
  R2 = Resistor [tolerance=±5% resistance=1k package=THT]
  LED2 = LED - 5mm [color="Orange (605nm)" package="5 mm [THT]"]
  R3 = Resistor [tolerance=±5% resistance=1k package=THT]
  LED3 = LED - 5mm [color="Orange (605nm)" package="5 mm [THT]"]
  R4 = Resistor [tolerance=±5% resistance=1k package=THT]
  LED4 = LED - 5mm [color="Orange (605nm)" package="5 mm [THT]"]
  R5 = Resistor [tolerance=±5% resistance=1k package=THT]
  LED5 = LED - 5mm [color="Orange (605nm)" package="5 mm [THT]"]
  R6 = Resistor [tolerance=±5% resistance=1k package=THT]
  LED6 = LED - 5mm [color="Orange (605nm)" package="5 mm [THT]"]
  J1 = female pin header, 12 pins [form="♀ (female)"]

nets:
  CS3: U1.pin1
  CS4: U1.pin2
  P0.0: U1.pin3, R6.Pin_1, J1.pin12
  GND: U1.pin5, C1.1, C2.1, VBB.-, J1.pin1, J1.pin2
  Vbatt: U1.pin6, C1.0, C2.0, VBB.+, LED1.anode, LED2.anode, LED3.anode, LED4.anode, LED5.anode, LED6.anode
  RSTb: U1.pin9, J1.pin11
  P2.7: U1.pin10, R5.Pin_1, J1.pin10
  P1.7: U1.pin11, R3.Pin_1, J1.pin6
  P1.6: U1.pin12, R4.Pin_1, J1.pin7
  CS8: U1.pin14
  CS2: U1.pin15
  CS1: U1.pin16
  CS0: U1.pin17
  CS5: U1.pin18
  P1.0: U1.pin19, R2.Pin_1, J1.pin5
  P0.7: U1.pin20, R1.Pin_1, J1.pin4
  CS7: U1.pin21
  P0.5: U1.pin22, J1.pin9
  P0.4: U1.pin23, J1.pin8
  CS6: U1.pin24
  N1: R1.Pin_0, LED1.cathode
  N2: R2.Pin_0, LED2.cathode
  N3: R3.Pin_0, LED3.cathode
  N4: R4.Pin_0, LED4.cathode
  N5: R5.Pin_0, LED5.cathode
  N6: R6.Pin_0, LED6.cathode
  Vext: J1.pin3

notes:
  CS0-8 are the 9 capacitive touch pads
