# Fritzing sketch chirpy_ananas (saved by Fritzing 0.9.2b)
breadboards: 1

parts:
  Q1 = NPN-Transistor [part_number=BC547 package="TO92 [THT]"]
  R1 = Resistor [tolerance=±5% resistance=3.3k package=THT]
  Part1 = LilyPad Coin Cell Battery Holder
  R2 = Resistor [tolerance=±5% resistance=3.3k package=THT]
  C1 = Electrolytic Capacitor [capacitance=100µF package="100 mil [THT, electrolytic]"]
  LED1 = LED - 5mm [color="Yellow (595nm)" package="5 mm [THT]"]
  R3 = Resistor [tolerance=±5% resistance=3.3k package=THT]
  Q2 = NPN-Transistor [part_number=BC547 package="TO92 [THT]"]
  R4 = Resistor [tolerance=±5% resistance=3.3k package=THT]
  C2 = Electrolytic Capacitor [capacitance=100µF package="100 mil [THT, electrolytic]"]
  LED2 = LED - 5mm [color="Yellow (595nm)" package="5 mm [THT]"]
  R5 = Resistor [tolerance=±5% resistance=3.3k package=THT]
  Q3 = NPN-Transistor [part_number=BC547 package="TO92 [THT]"]
  R6 = Resistor [tolerance=±5% resistance=3.3k package=THT]
  C3 = Electrolytic Capacitor [capacitance=100µF package="100 mil [THT, electrolytic]"]
  LED3 = LED - 5mm [color="Yellow (595nm)" package="5 mm [THT]"]
  P1 = Piezo Speaker
  Q4 = PNP-Transistor [package="TO92 [THT]"]
  R7 = Trimmer Potentiometer [maximum_resistance=10kΩ package=THT]
  R8 = Resistor [tolerance=±5% resistance=3.3k package=THT]

nets:
  N1: Q1.E, LED1.anode
  N2: Q1.B, R6.Pin_1, C3.+
  N3: Q1.C, R1.Pin_1, R2.Pin_0
  V+: R1.Pin_0, Part1.+, R3.Pin_0, R5.Pin_0, Q4.E, R7.leg1
  GND: Part1.-, C1.-, LED1.cathode, C2.-, LED2.cathode, C3.-, LED3.cathode, P1.pin1, R7.leg2
  N4: R2.Pin_1, C1.+, Q2.B
  N5: R3.Pin_1, Q2.C, R4.Pin_0
  N6: Q2.E, LED2.anode
  N7: R4.Pin_1, C2.+, Q3.B
  A: R5.Pin_1, Q3.C, R6.Pin_0, R8.Pin_0
  N8: Q3.E, LED3.anode
  N9: P1.pin2, Q4.C
  N10: Q4.B, R7.wiper, R8.Pin_1

notes:
  annoying chirping customisation
