# Fritzing sketch binco (saved by Fritzing 0.9.2b)
breadboards: 1

parts:
  Part1 = LilyPad Coin Cell Battery Holder
  IC01 = 555 Timer [package="DIP8 [THT]"]
  IC00 = IC, DIP package, 16 pins [chip_label=74HC4020]
  R000 = Resistor [tolerance=±5% resistance=1.5k package=THT]
  S1 = Pushbutton [package=THT]
  C10 = Ceramic Capacitor [capacitance=1µF package="100 mil [THT, multilayer]"]
  C11 = Ceramic Capacitor [capacitance=1µF package="100 mil [THT, multilayer]"]
  R010 = Resistor [tolerance=±5% resistance=1.5k package=THT]
  R011 = Resistor [tolerance=±5% resistance=47k package=THT]
  S2 = Pushbutton [package=THT]
  S3 = Pushbutton [package=THT]
  R001 = Resistor [tolerance=±5% resistance=1.5k package=THT]
  C00 = Ceramic Capacitor [capacitance=1µF package="100 mil [THT, multilayer]"]
  S4 = Pushbutton [package=THT]
  R100 = Resistor [tolerance=±5% resistance=47k package=THT]
  R101 = Resistor [tolerance=±5% resistance=1.5k package=THT]
  LED1 = smd LED [color="Green (570nm)" package="1206 [SMD]"]
  R102 = Resistor [tolerance=±5% resistance=1.5k package=THT]
  LED2 = smd LED [color="Green (570nm)" package="1206 [SMD]"]
  R103 = Resistor [tolerance=±5% resistance=1.5k package=THT]
  LED3 = smd LED [color="Green (570nm)" package="1206 [SMD]"]
  R104 = Resistor [tolerance=±5% resistance=1.5k package=THT]
  LED4 = smd LED [color="Green (570nm)" package="1206 [SMD]"]
  R105 = Resistor [tolerance=±5% resistance=1.5k package=THT]
  LED5 = smd LED [color="Green (570nm)" package="1206 [SMD]"]
  R106 = Resistor [tolerance=±5% resistance=1.5k package=THT]
  LED6 = smd LED [color="Green (570nm)" package="1206 [SMD]"]
  R107 = Resistor [tolerance=±5% resistance=1.5k package=THT]
  LED7 = smd LED [color="Green (570nm)" package="1206 [SMD]"]
  R108 = Resistor [tolerance=±5% resistance=1.5k package=THT]
  LED8 = smd LED [color="Green (570nm)" package="1206 [SMD]"]
  R109 = Resistor [tolerance=±5% resistance=1.5k package=THT]
  LED9 = smd LED [color="Green (570nm)" package="1206 [SMD]"]
  R110 = Resistor [tolerance=±5% resistance=1.5k package=THT]
  LED10 = smd LED [color="Green (570nm)" package="1206 [SMD]"]
  R111 = Resistor [tolerance=±5% resistance=1.5k package=THT]
  LED11 = smd LED [color="Green (570nm)" package="1206 [SMD]"]

nets:
  GND: Part1.-, IC01.Ground, IC00.pin8, R000.Pin_1, C10.0, C11.0, C00.0, R100.Pin_1
  VBATT: Part1.+, IC01.Vcc_Supply_Voltage, IC00.pin16, S1.leg0, R001.Pin_0, C00.1
  N1: IC01.Trigger, IC01.Threshold, C11.1, R010.Pin_1, R011.Pin_1
  CLK: IC01.Output, IC00.pin10
  VDD: IC01.Reset, S1.leg1, C10.1, S4.leg0, R100.Pin_0, R101.Pin_0, R102.Pin_0, R103.Pin_0, R104.Pin_0, R105.Pin_0, R106.Pin_0, R107.Pin_0, R108.Pin_0, R109.Pin_0, R110.Pin_0, R111.Pin_0
  N2: IC01.Discharge, S2.leg0, S3.leg0, R001.Pin_1
  D9: IC00.pin1, LED9.cathode
  D10: IC00.pin2, LED10.cathode
  D11: IC00.pin3, LED11.cathode
  D3: IC00.pin4, LED3.cathode
  D2: IC00.pin5, LED2.cathode
  D4: IC00.pin6, LED4.cathode
  D1: IC00.pin7, LED1.cathode
  N3: IC00.pin11, R000.Pin_0, S4.leg1
  D6: IC00.pin12, LED6.cathode
  D5: IC00.pin13, LED5.cathode
  D7: IC00.pin14, LED7.cathode
  D8: IC00.pin15, LED8.cathode
  N4: R010.Pin_0, S2.leg1
  N5: R011.Pin_0, S3.leg1
  N6: R101.Pin_1, LED1.anode
  N7: R102.Pin_1, LED2.anode
  N8: R103.Pin_1, LED3.anode
  N9: R104.Pin_1, LED4.anode
  N10: R105.Pin_1, LED5.anode
  N11: R106.Pin_1, LED6.anode
  N12: R107.Pin_1, LED7.anode
  N13: R108.Pin_1, LED8.anode
  N14: R109.Pin_1, LED9.anode
  N15: R110.Pin_1, LED10.anode
  N16: R111.Pin_1, LED11.anode

notes:
  "count down" configuration
  not laid out - PCB provided
