# Fritzing sketch conehead (saved by Fritzing 0.9.2b)
breadboards: 1

parts:
  IC1 = Hex Inverter Schmitt Trigger SN74HC14 [package="DIP (Dual Inline)"]
  Part1 = LilyPad Coin Cell Battery Holder
  R6 = Resistor [tolerance=±5% resistance=4.7k package=THT]
  Q1 = LTR-301 [package=ltr-301]
  C_gate = Electrolytic Capacitor [capacitance=47µF package="100 mil [THT, electrolytic]"]
  C1 = Ceramic Capacitor [capacitance=100nF package="100 mil [THT, multilayer]"]
  S1 = Pushbutton [package=THT]
  D1 = Rectifier Diode [part_number=1N4148 package="300 mil [THT]"]
  C_carrier = Ceramic Capacitor [capacitance=10nF package="100 mil [THT, multilayer]"]
  R5 = Resistor [tolerance=±5% resistance=0 package=THT]
  SP1 = SPEAKER [package=pcb_mount_speaker]
  R7 = Resistor [tolerance=±5% resistance=4.7k package=THT]
  R9 = Resistor [tolerance=±5% resistance=4.7k package=THT]
  R8 = Resistor [tolerance=±5% resistance=4.7k package=THT]
  R11 = Resistor [tolerance=±5% resistance=4.7k package=THT]
  R10 = Resistor [tolerance=±5% resistance=4.7k package=THT]
  C2 = Ceramic Capacitor [capacitance=100nF package="100 mil [THT, multilayer]"]
  R1 = Resistor [tolerance=±5% resistance=4.7k package=THT]
  R2 = Resistor [tolerance=±5% resistance=4.7k package=THT]
  R3 = Resistor [tolerance=±5% resistance=4.7k package=THT]
  R4 = Resistor [tolerance=±5% resistance=4.7k package=THT]
  C_mod = Ceramic Capacitor [capacitance=1µF package="100 mil [THT, multilayer]"]
  R12 = Resistor [tolerance=±5% resistance=4.7k package=THT]
  R13 = Resistor [tolerance=±5% resistance=4.7k package=THT]

nets:
  GND: IC1.1A, IC1.2A, IC1.3A, IC1.GND, Part1.-, C_gate.-, C1.0, C_carrier.0, C2.0, C_mod.0
  N1: IC1.4Y, R5.Pin_0, R13.Pin_0
  N2: IC1.4A, D1.cathode, C_carrier.1, R1.Pin_1, R12.Pin_1
  N3: IC1.5Y, R2.Pin_0, R4.Pin_0
  N4: IC1.5A, R3.Pin_1, C_mod.1
  N5: IC1.6Y, R6.Pin_1, Q1.C, D1.anode
  N6: IC1.6A, C_gate.+, R7.Pin_0, R8.Pin_0, R10.Pin_0
  VCC: IC1.VCC, C1.1, S1.leg1
  N7: Part1.+, S1.leg0
  N8: R6.Pin_0, R7.Pin_1
  N9: Q1.E, R9.Pin_1, R11.Pin_1
  N10: R5.Pin_1, SP1.+
  N11: SP1.-, C2.1
  N12: R9.Pin_0, R8.Pin_1
  N13: R11.Pin_0, R10.Pin_1
  N14: R1.Pin_0, R2.Pin_1
  N15: R3.Pin_0, R4.Pin_1
  N16: R12.Pin_0, R13.Pin_1

notes:
  not laid out - see schematic
