# Fritzing sketch cordwood-three (saved by Fritzing 0.9.2b)

parts:
  C1 = Ceramic Capacitor [capacitance=1µF package="100 mil [THT, multilayer]"]
  R1 = Resistor [tolerance=±5% resistance=220 package=THT]
  R2 = Resistor [tolerance=±5% resistance=10k package=THT]
  Q1 = Basic FET N-Channel [package="DPak [SMD]"]
  LED1 = LED - 5mm [color="Green (570nm)" package="5 mm [THT]"]
  J1 = female pin header, 8 pins [form="♀ (female)"]
  R3 = Resistor [tolerance=±5% resistance=220 package=THT]
  R4 = Resistor [tolerance=±5% resistance=10k package=THT]
  Q2 = Basic FET N-Channel [package="DPak [SMD]"]
  LED2 = LED - 5mm [color="Green (570nm)" package="5 mm [THT]"]
  R5 = Resistor [tolerance=±5% resistance=220 package=THT]
  R6 = Resistor [tolerance=±5% resistance=10k package=THT]
  Q3 = Basic FET N-Channel [package="DPak [SMD]"]
  LED3 = LED - 5mm [color="Green (570nm)" package="5 mm [THT]"]
  R7 = Resistor [tolerance=±5% resistance=220 package=THT]
  R8 = Resistor [tolerance=±5% resistance=10k package=THT]
  Q4 = Basic FET N-Channel [package="DPak [SMD]"]
  LED4 = LED - 5mm [color="Green (570nm)" package="5 mm [THT]"]
  R9 = Resistor [tolerance=±5% resistance=220 package=THT]
  R10 = Resistor [tolerance=±5% resistance=10k package=THT]
  Q5 = Basic FET N-Channel [package="DPak [SMD]"]
  LED5 = LED - 5mm [color="Green (570nm)" package="5 mm [THT]"]
  R11 = Resistor [tolerance=±5% resistance=220 package=THT]
  R12 = Resistor [tolerance=±5% resistance=10k package=THT]
  Q6 = Basic FET N-Channel [package="DPak [SMD]"]
  LED6 = LED - 5mm [color="Green (570nm)" package="5 mm [THT]"]

nets:
  GND: C1.0, Q1.source, J1.pin5, Q2.source, Q3.source, Q4.source, Q5.source, Q6.source
  V+: C1.1, R1.Pin_0, R2.Pin_0, J1.pin4, R3.Pin_0, R4.Pin_0, R5.Pin_0, R6.Pin_0, R7.Pin_0, R8.Pin_0, R9.Pin_0, R10.Pin_0, R11.Pin_0, R12.Pin_0
  N1: R1.Pin_1, LED1.anode
  N2: R2.Pin_1, Q1.Gate, J1.pin1
  N3: Q1.drain, LED1.cathode
  N4: J1.pin2, R4.Pin_1, Q2.Gate
  N5: J1.pin3, R6.Pin_1, Q3.Gate
  N6: J1.pin6, R8.Pin_1, Q4.Gate
  N7: J1.pin7, R10.Pin_1, Q5.Gate
  N8: J1.pin8, R12.Pin_1, Q6.Gate
  N9: R3.Pin_1, LED2.anode
  N10: Q2.drain, LED2.cathode
  N11: R5.Pin_1, LED3.anode
  N12: Q3.drain, LED3.cathode
  N13: R7.Pin_1, LED4.anode
  N14: Q4.drain, LED4.cathode
  N15: R9.Pin_1, LED5.anode
  N16: Q5.drain, LED5.cathode
  N17: R11.Pin_1, LED6.anode
  N18: Q6.drain, LED6.cathode

notes:
  NB: I haven't bothered to layout a breadboard
