# Fritzing sketch FidgetCube (saved by Fritzing 0.9.2b)

parts:
  J2 = female pin header, 8 pins [form="♀ (female)"]
  J1 = female pin header, 2 pins [form="♀ (female)"]
  D1 = Zener Diode [part_number=1N4733 breakdown_voltage=5.1V package="Melf DO-213 AB [SMD]"]
  R1 = Resistor [tolerance=±5% resistance=22 package=THT]
  VCC1 = Battery block 9V
  S1 = Toggle Switch [package=THT]
  S2 = Pushbutton [package="[THT]"]

nets:
  N1: J2.pin8, S2.Pin_3, S2.Pin_4
  N2: J1.pin1, D1.cathode, R1.Pin_1
  GND: J1.pin2, D1.anode, VCC1.-, S2.Pin_1
  N3: R1.Pin_0, S1.L2
  N4: VCC1.+, S1.COM

notes:
  Cordwood Too Connectors
  etc.. pushbuttons for all controls on the Fidget Cube, wired to a Cordwood J2 connector
