# Fritzing sketch tuner (saved by Fritzing 0.9.2b)
breadboards: 3

parts:
  JP1 = Header 6 [package=1x06-smd]
  R1 = Resistor [tolerance=±5% resistance=150 package=THT]
  R2 = Resistor [tolerance=±5% resistance=150 package=THT]
  R3 = Resistor [tolerance=±5% resistance=150 package=THT]
  R4 = Resistor [tolerance=±5% resistance=10k package=THT]
  R5 = Resistor [tolerance=±5% resistance=10k package=THT]
  R6 = Resistor [tolerance=±5% resistance=10k package=THT]
  Q1 = 2N7000 FET N-Channel [part_number=2N7000 package=TO92]
  Q2 = 2N7000 FET N-Channel [part_number=2N7000 package=TO92]
  Q3 = 2N7000 FET N-Channel [part_number=2N7000 package=TO92]
  C1 = Ceramic Capacitor [capacitance=1µF package="100 mil [THT, multilayer]"]
  LED3 = LED - 5mm [color="Red (633nm)" package="5 mm [THT]"]
  LED6 = LED - 5mm [color="Red (633nm)" package="5 mm [THT]"]
  LED2 = LED - 5mm [color="Yellow (595nm)" package="5 mm [THT]"]
  LED5 = LED - 5mm [color="Yellow (595nm)" package="5 mm [THT]"]
  LED1 = LED - 5mm [color="Green (555nm)" package="5 mm [THT]"]
  LED4 = LED - 5mm [color="Green (555nm)" package="5 mm [THT]"]
  R7 = Resistor [tolerance=±5% resistance=150 package=THT]
  R8 = Resistor [tolerance=±5% resistance=150 package=THT]
  R9 = Resistor [tolerance=±5% resistance=150 package=THT]
  R11 = Resistor [tolerance=±5% resistance=10k package=THT]
  R12 = Resistor [tolerance=±5% resistance=10k package=THT]
  R10 = Resistor [tolerance=±5% resistance=10k package=THT]
  Q4 = 2N7000 FET N-Channel [part_number=2N7000 package=TO92]
  Q5 = 2N7000 FET N-Channel [part_number=2N7000 package=TO92]
  Q6 = 2N7000 FET N-Channel [part_number=2N7000 package=TO92]
  IC1 = LM386 [part_number=LM386 package=dip08]
  MIC1 = Microphone
  R13 = Resistor [tolerance=±5% resistance=10k package=THT]
  C2 = Ceramic Capacitor [capacitance=100nF package="100 mil [THT, multilayer]"]
  C3 = Electrolytic Capacitor [capacitance=10µF package="100 mil [THT, electrolytic]"]
  C4 = Electrolytic Capacitor [capacitance=10µF package="100 mil [THT, electrolytic]"]
  R14 = Resistor [tolerance=±5% resistance=22k package=THT]
  C5 = Electrolytic Capacitor [capacitance=220µF package="100 mil [THT, electrolytic]"]
  C6 = Ceramic Capacitor [capacitance=100nF package="100 mil [THT, multilayer]"]
  C7 = Electrolytic Capacitor [capacitance=220µF package="100 mil [THT, electrolytic]"]
  R15 = Resistor [tolerance=±5% resistance=22k package=THT]
  R16 = Resistor [tolerance=±5% resistance=2.2k package=THT]
  C8 = Ceramic Capacitor [capacitance=100nF package="100 mil [THT, multilayer]"]
  B1 = TheCuttle [part_number=TheCuttle]

nets:
  J1: JP1.1, R4.Pin_1, Q1.gate, B1.D2
  J2: JP1.2, R5.Pin_1, Q2.gate, B1.D3_(PWM)
  J3: JP1.3, R6.Pin_1, Q3.gate, B1.D4
  J4: JP1.4, R10.Pin_1, Q4.gate, B1.D5_(PWM)
  J5: JP1.5, R11.Pin_1, Q5.gate, B1.D6_(PWM)
  J6: JP1.6, R12.Pin_1, Q6.gate, B1.D7
  VDD: R1.Pin_0, R2.Pin_0, R3.Pin_0, R4.Pin_0, R5.Pin_0, R6.Pin_0, C1.0, R7.Pin_0, R8.Pin_0, R9.Pin_0, R11.Pin_0, R12.Pin_0, R10.Pin_0, IC1.Vs, R13.Pin_1, R14.Pin_0, C5.+, C6.1, B1.VCC#6
  N1: R1.Pin_1, LED1.anode
  N2: R2.Pin_1, LED2.anode
  N3: R3.Pin_1, LED3.anode
  N4: Q1.drain, LED1.cathode
  GND: Q1.source, Q2.source, Q3.source, C1.1, Q4.source, Q5.source, Q6.source, IC1.-INPUT, IC1.GND, MIC1.pin1, C4.-, C5.-, C6.0, R15.Pin_0, C8.0, B1.GND#7
  N5: Q2.drain, LED2.cathode
  N6: Q3.drain, LED3.cathode
  N7: LED6.cathode, Q6.drain
  N8: LED6.anode, R9.Pin_1
  N9: LED5.cathode, Q5.drain
  N10: LED5.anode, R8.Pin_1
  N11: LED4.cathode, Q4.drain
  N12: LED4.anode, R7.Pin_1
  N13: IC1.GAIN, C3.-, C3.+
  N14: IC1.+INPUT, C2.1
  N15: IC1.Vout, C7.+
  N16: IC1.BYPASS, C4.+
  N17: MIC1.pin2, R13.Pin_0, C2.0
  N18: R14.Pin_1, C7.-, R15.Pin_1, R16.Pin_0
  AIN: R16.Pin_1, C8.1, B1.A0

notes:
  Cordwood
  Electret Preamp

custom parts:
  2N7000 FET N-Channel: A 2N7000 MOSFET N-Channel Transistor
  LM386: low voltage audio power amplifier
  TheCuttle: Boldport Cuttle Arduino-compatible Atmega328-based board
