# Fritzing sketch krell (saved by Fritzing 0.9.2b)
breadboards: 1

parts:
  IC1 = IC, DIP package, 28 pins [chip_label=IC part_number=dsPIC33EP128MC202-I/SP]
  VCC1 = 4 x AAA Battery Mount
  PS1 = Toggle Switch [package=THT]
  C4 = Electrolytic Capacitor [capacitance=10µF package="100 mil [THT, electrolytic]"]
  REG1 = LD33 Low-Dropout Voltage Regulator [part_number=LP2950-33LPRE3]
  C3 = Electrolytic Capacitor [capacitance=10µF package="100 mil [THT, electrolytic]"]
  C5 = Ceramic Capacitor [capacitance=100nF package="100 mil [THT, multilayer]"]
  R9 = Resistor [tolerance=±5% resistance=10k package=THT]
  ICSP = female pin header, 5 pins [form="♀ (female)"]
  C2 = Ceramic Capacitor [capacitance=100nF package="100 mil [THT, multilayer]"]
  R6 = Resistor [tolerance=±5% resistance=1k package=THT]
  Q1 = PNP-Transistor [part_number=BC547C package="TO92 [THT]"]
  R8 = Resistor [tolerance=±5% resistance=1k package=THT]
  R7 = Resistor [tolerance=±5% resistance=100 package=THT]
  C7 = Ceramic Capacitor [capacitance=100nF package="100 mil [THT, multilayer]"]
  C1 = Electrolytic Capacitor [capacitance=220µF package="100 mil [THT, electrolytic]"]
  U1 = 2.5mm Audio Jack [package=stereojack2.5mm_smd]
  UART = female pin header, 2 pins [form="♀ (female)"]
  R1 = Resistor [tolerance=±5% resistance=1k package=THT]
  D1 = LED - 3mm [color="White (8000K)" package="3 mm [THT]"]
  R2 = Resistor [tolerance=±5% resistance=1k package=THT]
  D2 = LED - 3mm [color="White (8000K)" package="3 mm [THT]"]
  R3 = Resistor [tolerance=±5% resistance=1k package=THT]
  R4 = Resistor [tolerance=±5% resistance=1k package=THT]
  D3 = LED - 3mm [color="White (8000K)" package="3 mm [THT]"]
  D4 = LED - 3mm [color="White (8000K)" package="3 mm [THT]"]
  RP1 = Trimmer Potentiometer [maximum_resistance=47kΩ package=THT]
  RP2 = Trimmer Potentiometer [maximum_resistance=47kΩ package=THT]
  RP3 = Trimmer Potentiometer [maximum_resistance=47kΩ package=THT]
  RP4 = Trimmer Potentiometer [maximum_resistance=47kΩ package=THT]
  RP5 = Trimmer Potentiometer [maximum_resistance=47kΩ package=THT]
  RP6 = Trimmer Potentiometer [maximum_resistance=47kΩ package=THT]
  S1 = Pushbutton [package=THT]
  S2 = Pushbutton [package=THT]
  S3 = Pushbutton [package=THT]
  S4 = Pushbutton [package=THT]
  S5 = Pushbutton [package=THT]
  S6 = Pushbutton [package=THT]
  MIDI_EN = female pin header, 2 pins [form="♀ (female)"]

nets:
  MCLR: IC1.pin1, R9.Pin_1, ICSP.pin1
  VR6: IC1.pin2, RP6.wiper
  VR1: IC1.pin3, RP1.wiper
  VR2: IC1.pin4, RP2.wiper
  VR3: IC1.pin5, RP3.wiper
  VR4: IC1.pin6, RP4.wiper
  VR5: IC1.pin7, RP5.wiper
  GND: IC1.pin8, IC1.pin27, VCC1.-, C4.-, REG1.GND, C3.-, C5.0, ICSP.pin3, C2.0, R8.Pin_1, C7.0, U1.SLEEVE, D1.cathode, D2.cathode, D3.cathode, D4.cathode, RP1.leg1, RP2.leg1, RP3.leg1, RP4.leg1, RP5.leg1, RP6.leg1, S1.leg1, S2.leg1, S3.leg1, S4.leg1, S5.leg1, S6.leg1, MIDI_EN.pin2
  LED2: IC1.pin10, R2.Pin_0
  Tx: IC1.pin11, UART.pin2
  Msel: IC1.pin12, MIDI_EN.pin1
  VDD: IC1.pin13, IC1.pin28, REG1.Vout, C3.+, C5.1, R9.Pin_0, ICSP.pin2, C2.1, Q1.E, RP1.leg2, RP2.leg2, RP3.leg2, RP4.leg2, RP5.leg2, RP6.leg2
  SW6: IC1.pin14, ICSP.pin4, S6.leg0
  SW5: IC1.pin15, ICSP.pin5, S5.leg0
  SW4: IC1.pin16, S4.leg0
  SW3: IC1.pin17, S3.leg0
  SW2: IC1.pin18, S2.leg0
  LED4: IC1.pin21, R4.Pin_0
  LED3: IC1.pin22, R3.Pin_0
  Rx: IC1.pin23, UART.pin1
  LED1: IC1.pin24, R1.Pin_0
  PWM: IC1.pin25, R6.Pin_0
  SW1: IC1.pin26, S1.leg0
  N1: VCC1.+, PS1.COM
  N2: PS1.L2, C4.+, REG1.Vin
  N3: R6.Pin_1, Q1.B
  N4: Q1.C, R8.Pin_0, R7.Pin_0
  N5: R7.Pin_1, C7.1, C1.+
  N6: C1.-, U1.LEFT, U1.RIGHT
  N7: R1.Pin_1, D1.anode
  N8: R2.Pin_1, D2.anode
  N9: R3.Pin_1, D3.anode
  N10: R4.Pin_1, D4.anode

notes:
  not laid out - see schematic only
