# Fritzing sketch ligemdio (saved by Fritzing 0.9.2b)
breadboards: 1

parts:
  T1 = NPN-Transistor [part_number=PN2222ATA package="TO92 [THT]"]
  T2 = NPN-Transistor [part_number=PN2222ATA package="TO92 [THT]"]
  R1 = Resistor [tolerance=±5% resistance=33 package=THT]
  R2 = Resistor [tolerance=±5% resistance=1k package=THT]
  R5 = Resistor [tolerance=±5% resistance=1k package=THT]
  LED3 = LED - 5mm [color="Orange (620nm)" package="5 mm [THT]"]
  C1 = Electrolytic Capacitor [capacitance=3.3µF voltage=50V package="100 mil [THT, electrolytic]"]
  5V = Power plug
  DUT1 = LED - 5mm [color="Blue (525nm)" package="5 mm [THT]"]

nets:
  N1: T1.E, T2.B, R1.Pin_0
  N2: T1.B, T2.C, R2.Pin_1
  N3: T1.C, DUT1.cathode
  GND: T2.E, R1.Pin_1, LED3.cathode, C1.-, 5V.GND
  N4: R2.Pin_0, R5.Pin_0, C1.+, 5V.VCC, DUT1.anode
  N5: R5.Pin_1, LED3.anode
