# Fritzing sketch CuttleTalk (saved by Fritzing 0.9.2b)
breadboards: 1

parts:
  B1 = TheCuttle
  R1 = Resistor [tolerance=±5% resistance=220 package=THT]
  LED1 = LED - 5mm [color="White (8000K)" package="5 mm [THT]"]

nets:
  N1: B1.D11_(PWM), LED1.anode
  N2: B1.GND#21, R1.Pin_0
  N3: R1.Pin_1, LED1.cathode

custom parts:
  TheCuttle: Boldport Cuttle Arduino-compatible Atmega328-based board
