# Fritzing sketch pease-out-original (saved by Fritzing 0.9.2b)
breadboards: 1

parts:
  IC1 = IC, DIP package, 8 pins [chip_label=LM331]
  5-9V = Power plug
  RT1 = Trimmer Potentiometer [maximum_resistance=2MΩ package=THT]
  RT2 = Resistor [tolerance=±5% resistance=15k package=THT]
  C1 = Electrolytic Capacitor [capacitance=10µF package="100 mil [THT, electrolytic]"]
  CT1 = Ceramic Capacitor [capacitance=100nF package="100 mil [THT, multilayer]"]
  RS = Resistor [tolerance=±5% resistance=15k package=THT]
  CL = Ceramic Capacitor [capacitance=1µF package="100 mil [THT, multilayer]"]
  C2 = Ceramic Capacitor [capacitance=1µF package="100 mil [THT, multilayer]"]
  RL1 = Resistor [tolerance=±5% resistance=15k package=THT]
  RL2 = Resistor [tolerance=±5% resistance=15k package=THT]
  R2 = Resistor [tolerance=±5% resistance=15k package=THT]
  LED1 = LED - 5mm [color="Red (633nm)" package="5 mm [THT]"]
  R1 = Resistor [tolerance=±5% resistance=15k package=THT]
  Q1 = 2N7000 FET N-Channel [part_number=2N7000 package=TO92]

nets:
  THRES: IC1.pin1, IC1.pin6, CL.1, RL1.Pin_0
  COMP: IC1.pin2, IC1.pin7, RS.Pin_0
  FOUT: IC1.pin3, R1.Pin_1, Q1.gate
  GND: IC1.pin4, 5-9V.GND, C1.-, CT1.0, RS.Pin_1, CL.0, C2.0, RL2.Pin_1, Q1.source
  RC: IC1.pin5, RT2.Pin_1, CT1.1
  Vs: IC1.pin8, 5-9V.VCC, RT1.leg1, RT1.wiper, C1.+, C2.1, R2.Pin_0, R1.Pin_0
  N1: RT1.leg2, RT2.Pin_0
  N2: RL1.Pin_1, RL2.Pin_0
  N3: R2.Pin_1, LED1.anode
  N4: LED1.cathode, Q1.drain

custom parts:
  2N7000 FET N-Channel: A 2N7000 MOSFET N-Channel Transistor
