# Fritzing sketch pease-out (saved by Fritzing 0.9.2b)
breadboards: 1

parts:
  IC1 = IC, DIP package, 8 pins [chip_label=LM331]
  5-9V = Power plug
  RT2 = Resistor [tolerance=±5% resistance=15k package=THT]
  C1 = Electrolytic Capacitor [capacitance=10µF package="100 mil [THT, electrolytic]"]
  CT1 = Ceramic Capacitor [capacitance=10nF package="100 mil [THT, multilayer]"]
  RS = Resistor [tolerance=±5% resistance=15k package=THT]
  CL = Ceramic Capacitor [capacitance=100nF package="100 mil [THT, multilayer]"]
  C2 = Ceramic Capacitor [capacitance=1µF package="100 mil [THT, multilayer]"]
  RL1 = Resistor [tolerance=±5% resistance=15k package=THT]
  RL2 = Resistor [tolerance=±5% resistance=15k package=THT]
  Rp = Resistor [tolerance=±5% resistance=10k package=THT]
  R1 = Resistor [tolerance=±5% resistance=15k package=THT]
  J1 = Piezo Speaker
  Rv1 = Resistor [tolerance=±5% resistance=33k package=THT]
  Rv2 = Resistor [tolerance=±5% resistance=33k package=THT]
  Q1 = Basic FET N-Channel [package="TO220 [THT]"]

nets:
  THRES: IC1.pin1, IC1.pin6, CL.1, RL1.Pin_0
  N1: IC1.pin2, RS.Pin_0
  FOUT: IC1.pin3, R1.Pin_1, Q1.gate
  GND: IC1.pin4, 5-9V.GND, C1.-, CT1.0, RS.Pin_1, CL.0, C2.0, RL2.Pin_1, Rv2.Pin_1, Q1.source
  RC: IC1.pin5, RT2.Pin_1, CT1.1
  COMP: IC1.pin7, Rv1.Pin_1, Rv2.Pin_0
  Vs: IC1.pin8, 5-9V.VCC, RT2.Pin_0, C1.+, C2.1, Rp.Pin_0, R1.Pin_0, J1.pin2
  N2: RL1.Pin_1, RL2.Pin_0
  N3: Rp.Pin_1, J1.pin1, Q1.drain
  Vin: Rv1.Pin_0

notes:
  Vin
  Voltage Probe (0-5V)
