# Fritzing sketch pips (saved by Fritzing 0.9.2b)
breadboards: 1

parts:
  IC4 = IC, DIP package, 16 pins [chip_label=CD4060]
  R2 = Resistor [tolerance=±5% resistance=470k package=THT]
  R1 = Resistor [tolerance=±5% resistance=470k package=THT]
  R4 = Resistor [tolerance=±5% resistance=470k package=THT]
  R3 = Resistor [tolerance=±5% resistance=470k package=THT]
  R5 = Resistor [tolerance=±5% resistance=15k package=THT]
  R6 = Resistor [tolerance=±5% resistance=15k package=THT]
  R7 = Resistor [tolerance=±5% resistance=15k package=THT]
  R8 = Resistor [tolerance=±5% resistance=15k package=THT]
  R9 = Resistor [tolerance=±5% resistance=15k package=THT]
  C1 = Ceramic Capacitor [capacitance=100nF package="100 mil [THT, multilayer]"]
  Q1 = PNP-Transistor [package="TO92 [THT]"]
  Vbatt = Battery block 9V
  C2 = Ceramic Capacitor [capacitance=100nF package="100 mil [THT, multilayer]"]
  LED1 = LED - 5mm [color="Red (633nm)" package="5 mm [THT]"]
  LED2 = LED - 5mm [color="Red (633nm)" package="5 mm [THT]"]
  LED3 = LED - 5mm [color="Red (633nm)" package="5 mm [THT]"]
  LED4 = LED - 5mm [color="Red (633nm)" package="5 mm [THT]"]
  LED5 = LED - 5mm [color="Red (633nm)" package="5 mm [THT]"]
  LED6 = LED - 5mm [color="Red (633nm)" package="5 mm [THT]"]
  LED7 = LED - 5mm [color="Red (633nm)" package="5 mm [THT]"]
  S1 = Pushbutton [package="[THT]"]
  D1 = Rectifier Diode [part_number=1N4148 package="300 mil [THT]"]
  D2 = Rectifier Diode [part_number=1N4148 package="300 mil [THT]"]
  D3 = Rectifier Diode [part_number=1N4148 package="300 mil [THT]"]
  D4 = Rectifier Diode [part_number=1N4148 package="300 mil [THT]"]
  D5 = Rectifier Diode [part_number=1N4148 package="300 mil [THT]"]

nets:
  P7: IC4.pin4, R8.Pin_1, D3.cathode
  P2: IC4.pin5, R4.Pin_1, LED2.anode, D2.cathode, D5.cathode
  P3: IC4.pin7, R6.Pin_1, D1.anode, D4.cathode
  GND: IC4.pin8, Vbatt.-, C2.0, S1.Pin_1, S1.Pin_2
  N1: IC4.pin9, C1.0
  N2: IC4.pin10, R2.Pin_0, R1.Pin_0
  N3: IC4.pin11, R3.Pin_0, S1.Pin_3, S1.Pin_4
  N4: IC4.pin12, R9.Pin_1, D2.anode, D3.anode
  VCC: IC4.pin16, R9.Pin_0, Q1.E, Vbatt.+, C2.1, LED1.anode, LED4.anode
  N5: R2.Pin_1, R1.Pin_1, R3.Pin_1, C1.1
  N6: R4.Pin_0, Q1.B
  P7a: R5.Pin_0, Q1.C, LED7.anode, D1.cathode
  P1: R5.Pin_1, LED5.cathode
  N7: R6.Pin_0, LED3.cathode
  N8: R7.Pin_0, LED6.cathode
  N9: R7.Pin_1, D4.anode, D5.anode
  N10: R8.Pin_0, LED7.cathode
  N11: LED1.cathode, LED6.anode
  N12: LED2.cathode, LED5.anode
  N13: LED3.anode, LED4.cathode
