# Fritzing sketch stringy (saved by Fritzing 0.9.2b)
breadboards: 1

parts:
  IC2 = IC, DIP package, 8 pins [chip_label=PIC part_number=12F1840-I/P]
  IC1 = Voltage Regulator [part_number=78L05 package=to-92]
  C1 = Electrolytic Capacitor [capacitance=10µF package="100 mil [THT, electrolytic]"]
  C2 = Electrolytic Capacitor [capacitance=10µF package="100 mil [THT, electrolytic]"]
  C3 = Electrolytic Capacitor [capacitance=220µF package="100 mil [THT, electrolytic]"]
  LED1 = LED - 5mm [color="Blue (430nm)" package="5 mm [THT]"]
  R1 = Resistor [tolerance=±5% resistance=1k package=THT]
  VCC1 = Battery block 9V
  C4 = Ceramic Capacitor [capacitance=100nF package="100 mil [THT, multilayer]"]
  C5 = Ceramic Capacitor [capacitance=100nF package="100 mil [THT, multilayer]"]
  R2 = Resistor [tolerance=±5% resistance=1k package=THT]
  Q1 = NPN-Transistor [part_number=BC547B package="TO92 [THT]"]
  R3 = Resistor [tolerance=±5% resistance=1M package=THT]
  R4 = Resistor [tolerance=±5% resistance=1k package=THT]
  R5 = Resistor [tolerance=±5% resistance=47 package=THT]
  S1 = Pushbutton [package=THT]
  S2 = Pushbutton [package=THT]
  R6 = Resistor [tolerance=±5% resistance=1k package=THT]
  R7 = Resistor [tolerance=±5% resistance=1k package=THT]
  R8 = Resistor [tolerance=±5% resistance=1k package=THT]
  R9 = Resistor [tolerance=±5% resistance=1k package=THT]
  R10 = Resistor [tolerance=±5% resistance=1k package=THT]
  R11 = Resistor [tolerance=±5% resistance=1k package=THT]
  R12 = Resistor [tolerance=±5% resistance=1k package=THT]
  R13 = Resistor [tolerance=±5% resistance=1k package=THT]
  R14 = Resistor [tolerance=±5% resistance=1k package=THT]
  R15 = Resistor [tolerance=±5% resistance=1k package=THT]
  R16 = Resistor [tolerance=±5% resistance=1k package=THT]
  R17 = Resistor [tolerance=±5% resistance=1k package=THT]
  R18 = Resistor [tolerance=±5% resistance=1k package=THT]
  J1 = Audio Jack (TRS) 3.5mm [package="4Ucon 08780 [THT]"]

nets:
  VDD: IC2.pin1, IC1.OUT, C1.+, C5.1, Q1.C, R7.Pin_1
  N1: IC2.pin2, LED1.anode
  N2: IC2.pin3, S2.leg0
  N3: IC2.pin4, S1.leg0
  N4: IC2.pin5, R2.Pin_1
  plectrum: IC2.pin6, R3.Pin_1
  N5: IC2.pin7, R1.Pin_1
  GND: IC2.pin8, IC1.GND, C1.-, C2.-, R1.Pin_0, VCC1.-, C4.0, C5.0, R3.Pin_0, R5.Pin_0, S1.leg1, S2.leg1, R6.Pin_0, R18.Pin_0, J1.Sleeve
  N6: IC1.IN, C2.+, VCC1.+
  N7: C3.-, J1.Ring, J1.Tip
  N8: C3.+, C4.1, R4.Pin_0
  N9: LED1.cathode, R6.Pin_1
  N10: R2.Pin_0, Q1.B
  N11: Q1.E, R4.Pin_1, R5.Pin_1
  N12: R7.Pin_0, R8.Pin_1
  N13: R8.Pin_0, R9.Pin_1
  N14: R9.Pin_0, R10.Pin_1
  N15: R10.Pin_0, R11.Pin_1
  N16: R11.Pin_0, R12.Pin_1
  N17: R12.Pin_0, R13.Pin_1
  N18: R13.Pin_0, R14.Pin_1
  N19: R14.Pin_0, R15.Pin_1
  N20: R15.Pin_0, R16.Pin_1
  N21: R16.Pin_0, R17.Pin_1
  N22: R17.Pin_0, R18.Pin_1

notes:
  I haven't laid out the breadboard, as it is intended for the Boldport PCB
