# Fritzing sketch tap (saved by Fritzing 0.9.2b)
breadboards: 2

parts:
  5V = Power plug
  IC1 = IC, DIP package, 14 pins [chip_label=IC part_number=SN7400]
  IC2 = IC, DIP package, 14 pins [chip_label=IC part_number=SN7400]
  T2 = NPN-Transistor [package="TO92 [THT]"]
  T7 = NPN-Transistor [package="TO92 [THT]"]
  T8 = PNP-Transistor [package="TO92 [THT]"]
  T1 = NPN-Transistor [package="TO92 [THT]"]
  T4 = NPN-Transistor [package="TO92 [THT]"]
  T3 = NPN-Transistor [package="TO92 [THT]"]
  T6 = NPN-Transistor [package="TO92 [THT]"]
  T5 = NPN-Transistor [package="TO92 [THT]"]
  T9 = NPN-Transistor [package="TO92 [THT]"]
  T10 = NPN-Transistor [package="TO92 [THT]"]
  T11 = NPN-Transistor [package="TO92 [THT]"]
  T12 = NPN-Transistor [package="TO92 [THT]"]
  T13 = NPN-Transistor [package="TO92 [THT]"]
  T14 = NPN-Transistor [package="TO92 [THT]"]
  R1 = Resistor [tolerance=±5% resistance=100k package=THT]
  R2 = Resistor [tolerance=±5% resistance=100k package=THT]
  R3 = Resistor [tolerance=±5% resistance=100k package=THT]
  D1 = Rectifier Diode [part_number=1N4148 package="300 mil [THT]"]
  D2 = Rectifier Diode [part_number=1N4148 package="300 mil [THT]"]
  D3 = Rectifier Diode [part_number=1N4148 package="300 mil [THT]"]
  R4 = Resistor [tolerance=±5% resistance=10M package=THT]
  R5 = Resistor [tolerance=±5% resistance=10M package=THT]
  R6 = Resistor [tolerance=±5% resistance=10M package=THT]
  C3 = Ceramic Capacitor [capacitance=47nF package="100 mil [THT, multilayer]"]
  R7 = Resistor [tolerance=±5% resistance=10M package=THT]
  R8 = Resistor [tolerance=±5% resistance=1k package=THT]
  R9 = Resistor [tolerance=±5% resistance=27k package=THT]
  C1 = Ceramic Capacitor [capacitance=220pF package="100 mil [THT, multilayer]"]
  C2 = Ceramic Capacitor [capacitance=220pF package="100 mil [THT, multilayer]"]
  R10 = Resistor [tolerance=±5% resistance=27k package=THT]
  R11 = Resistor [tolerance=±5% resistance=27k package=THT]
  R12 = Resistor [tolerance=±5% resistance=27k package=THT]
  R13 = Resistor [tolerance=±5% resistance=27k package=THT]
  R14 = Resistor [tolerance=±5% resistance=27k package=THT]
  R15 = Resistor [tolerance=±5% resistance=27k package=THT]

nets:
  GND: 5V.GND, IC1.pin7, IC2.pin7, T7.E, T8.C, T1.E, T3.E, T5.E, T9.E, T10.E, T11.E, T12.E, T13.E, T14.E, C3.0, R8.Pin_0
  VCC: 5V.VCC, IC1.pin14, IC2.pin14, C3.1, C1.1
  RB: IC1.pin1, IC1.pin13, IC2.pin1, IC2.pin8, IC2.pin12
  Q1c: IC1.pin2, IC1.pin6, R11.Pin_0
  Q1: IC1.pin3, IC1.pin5, R10.Pin_0
  N1: IC1.pin4, T1.C, R1.Pin_0, D1.cathode
  Q2c: IC1.pin8, IC1.pin12, R13.Pin_0
  Q2: IC1.pin9, IC1.pin11, R12.Pin_0
  N2: IC1.pin10, T3.C, R2.Pin_0, D2.cathode
  Q3c: IC2.pin2, IC2.pin6, R15.Pin_0
  Q3: IC2.pin3, IC2.pin5, R14.Pin_0
  N3: IC2.pin4, T5.C, R3.Pin_0, D3.cathode
  N4: IC2.pin9, IC2.pin10, R8.Pin_1, C2.1
  N5: IC2.pin11, C2.0
  N6: IC2.pin13, T8.E
  N7: T2.E, T1.B
  N8: T2.B, R4.Pin_1
  N9: T2.C, R1.Pin_1
  N10: T7.B, R7.Pin_1
  N11: T7.C, T8.B, R9.Pin_1
  N12: T4.E, T3.B
  N13: T4.B, R5.Pin_1
  N14: T4.C, R2.Pin_1
  N15: T6.E, T5.B
  N16: T6.B, R6.Pin_1
  N17: T6.C, R3.Pin_1
  N18: T9.B, R10.Pin_1
  S1c: T9.C
  N19: T10.B, R11.Pin_1
  S1: T10.C
  N20: T11.B, R12.Pin_1
  S2c: T11.C
  N21: T12.B, R13.Pin_1
  S2: T12.C
  N22: T13.B, R14.Pin_1
  S3c: T13.C
  N23: T14.B, R15.Pin_1
  S3: T14.C
  CB: D1.anode, D2.anode, D3.anode, R9.Pin_0
  A: R4.Pin_0
  B: R5.Pin_0
  C: R6.Pin_0
  RESET: R7.Pin_0, C1.0

notes:
  A
  B
  C
  CB
  RB
  Q1
  Q1c
  Q2
  Q2c
  Q3
  Q3c
  S1c
  S1
  S2c
  S2
  S3c
  S3
