# Fritzing sketch whiteboard (saved by Fritzing 0.9.2b)
breadboards: 1
perfboards: 2

parts:
  IC3 = IC, DIP package, 16 pins [chip_label=CD4060]
  9-12V = Power plug
  oR2 = Resistor [tolerance=±5% resistance=10k package=THT]
  oR1 = Resistor [tolerance=±5% resistance=10k package=THT]
  oC1 = Electrolytic Capacitor [capacitance=1µF package="100 mil [THT, electrolytic]"]
  LED1 = LED - 3mm [color="White (4500K)" package="3 mm [THT]"]
  LED2 = LED - 3mm [color="White (4500K)" package="3 mm [THT]"]
  LED3 = LED - 3mm [color="White (4500K)" package="3 mm [THT]"]
  LED4 = LED - 3mm [color="White (4500K)" package="3 mm [THT]"]
  R3 = Resistor [tolerance=±5% resistance=1k package=THT]
  R4 = Resistor [tolerance=±5% resistance=1k package=THT]
  R5 = Resistor [tolerance=±5% resistance=1k package=THT]
  R6 = Resistor [tolerance=±5% resistance=1k package=THT]
  D1 = Rectifier Diode [part_number=1N4001 package="300 mil [THT]"]
  F1 = Resettable Fuse PTC [part_number=100mA package=ptc]
  U1 = Voltage Regulator [package=to220-adj]
  Co = Electrolytic Capacitor [capacitance=10µF package="100 mil [THT, electrolytic]"]
  Ci = Ceramic Capacitor [capacitance=100nF package="100 mil [THT, multilayer]"]
  TR = Trimmer Potentiometer [maximum_resistance=2kΩ package=THT]
  R1 = Resistor [tolerance=±5% resistance=220 package=THT]
  D2 = Rectifier Diode [part_number=1N4001 package="300 mil [THT]"]
  D3 = Rectifier Diode [part_number=1N4001 package="300 mil [THT]"]
  Ca = Electrolytic Capacitor [capacitance=10µF package="100 mil [THT, electrolytic]"]
  J1 = female pin header, 2 pins [form="♀ (female)"]
  J2 = female pin header, 2 pins [form="♀ (female)"]

nets:
  D2: IC3.pin4, R3.Pin_0
  D1: IC3.pin5, R5.Pin_0
  D3: IC3.pin6, R4.Pin_0
  D0: IC3.pin7, R6.Pin_0
  GND: IC3.pin8, 9-12V.GND, LED1.cathode, LED2.cathode, LED3.cathode, LED4.cathode, D1.anode, Co.-, Ci.0, TR.leg1, TR.wiper, Ca.-, J2.pin1, J2.pin2
  N1: IC3.pin9, oC1.-
  N2: IC3.pin10, oR1.Pin_0
  N3: IC3.pin11, oR2.Pin_0
  N4: IC3.pin12, IC3.pin14
  VCC: IC3.pin16, U1.OUT, Co.+, R1.Pin_1, D2.cathode, D3.anode, J1.pin1, J1.pin2
  Vbatt: 9-12V.VCC, F1.1
  N5: oR2.Pin_1, oR1.Pin_1, oC1.+
  N6: LED1.anode, R6.Pin_1
  N7: LED2.anode, R5.Pin_1
  N8: LED3.anode, R3.Pin_1
  N9: LED4.anode, R4.Pin_1
  N10: D1.cathode, F1.2, U1.IN, Ci.1, D3.cathode
  N11: U1.ADJ, TR.leg2, R1.Pin_0, D2.anode, Ca.+

notes:
  whiteboard Variable Power Supply
  Simple ripple counter
  whiteboard LED shroud
