# Fritzing sketch widlar (saved by Fritzing 0.9.2b)
breadboards: 1

parts:
  IC1 = IC, DIP package, 14 pins [chip_label=LM723]
  R2 = Resistor [tolerance=±5% resistance=2k package=THT]
  R1 = Resistor [tolerance=±5% resistance=1k package=THT]
  R3 = Resistor [tolerance=±5% resistance=3.9k package=THT]
  C1 = Ceramic Capacitor [capacitance=100pF package="100 mil [THT, multilayer]"]
  12V = Power plug
  RL = Resistor [tolerance=±5% resistance=560 package=THT]
  LED1 = LED - 3mm [color="Orange (620nm)" package="3 mm [THT]"]
  C2 = Electrolytic Capacitor [capacitance=100µF package="100 mil [THT, electrolytic]"]

nets:
  INV: IC1.pin4, R3.Pin_1, C1.1, C2.+
  NI: IC1.pin5, R2.Pin_0, R1.Pin_0
  N1: IC1.pin6, R1.Pin_1, C2.-
  GND: IC1.pin7, 12V.GND, RL.Pin_1
  OSC_OUT: IC1.pin10, R2.Pin_1, R3.Pin_0, LED1.anode
  VIN: IC1.pin11, IC1.pin12, 12V.VCC
  COMP: IC1.pin13, C1.0
  N2: RL.Pin_0, LED1.cathode

notes:
  Oscillator Output
