# Fritzing sketch DIYDevBoard (saved by Fritzing 0.9.2b)
breadboards: 1

parts:
  U1 = ESP8266 WiFi Module [part_number=ESP8266]
  Part1 = FTDI Basic Programmer
  R1 = Resistor [tolerance=±5% resistance=10k package=THT]
  BB1 = 4-Line Bi-Directional Level Shifter
  5-9V = Power plug
  C1 = Electrolytic Capacitor [capacitance=100µF package="100 mil [THT, electrolytic]"]
  U3 = Voltage Regulator - 3.3V [part_number=LD1117-3.3 package="TO220 [THT]"]
  C2 = Electrolytic Capacitor [capacitance=10µF package="100 mil [THT, electrolytic]"]
  SW1 = DIP SWITCH [package=dipswitch-02]
  R2 = Resistor [tolerance=±5% resistance=10k package=THT]
  R3 = Resistor [tolerance=±5% resistance=10k package=THT]

nets:
  N1: U1.RXD, BB1.A1
  V33: U1.VCC, R1.Pin_1, BB1.LV, C1.+, U3.output_voltage, C2.+, R2.Pin_1, R3.Pin_0
  N2: U1.GPIO_0, R1.Pin_0, SW1.4
  N3: U1.RST, SW1.3, R2.Pin_0
  N4: U1.CH_PD, R3.Pin_1
  GND: U1.GND, BB1.GND#6, 5-9V.GND, C1.-, U3.GND, C2.-, SW1.1, SW1.2
  N5: U1.TXD, BB1.A2
  N6: Part1.RXI, BB1.B2
  N7: Part1.TXO, BB1.B1
  N8: Part1.POWER, BB1.HV
  N9: Part1.GND, BB1.GND#16
  N10: 5-9V.VCC, U3.input_voltage

custom parts:
  ESP8266 WiFi Module: Generic WiFi Module based on the ESP8266 with onboard PCB antenna and UART communications
  4-Line Bi-Directional Level Shifter: 4-Channel Bi-Directional Level Shifter
