# Fritzing sketch DIYDevBoard (saved by Fritzing 0.9.2b)
breadboards: 2

parts:
  ESP1 = ESP 12E
  C2 = Electrolytic Capacitor [capacitance=470µF package="100 mil [THT, electrolytic]"]
  >4_5V = Power plug
  S2 = Pushbutton [part_number=reset package="[THT]"]
  R5 = Resistor [tolerance=±5% resistance=10k package=THT]
  R2 = Resistor [tolerance=±5% resistance=10k part_number=built-in package=THT]
  R1 = Resistor [tolerance=±5% resistance=10k part_number=built-in package=THT]
  R3 = Resistor [tolerance=±5% resistance=10k package=THT]
  S1 = Toggle Switch [part_number=run/prog package=THT]
  BB1 = 4-Line Bi-Directional Level Shifter
  Part2 = FTDI Basic Programmer
  R4 = Resistor [tolerance=±5% resistance=470 package=THT]
  U1 = V_REG_LD1117VXX [part_number=LD1117A package=78xxl]
  C1 = Electrolytic Capacitor [capacitance=10µF package="100 mil [THT, electrolytic]"]
  C3 = Ceramic Capacitor [capacitance=100nF package="100 mil [THT, multilayer]"]

nets:
  N1: ESP1.TX0, BB1.A1
  N2: ESP1.RX0, BB1.A2
  N3: ESP1.GPIO0, S1.COM
  N4: ESP1.GPIO15, R1.Pin_0
  GND: ESP1.GND, C2.-, >4_5V.GND, S2.Pin_3, S2.Pin_4, R1.Pin_1, BB1.GND, Part2.GND, R4.Pin_1, U1.GND, C1.-, C3.0
  3V3: ESP1.VCC, C2.+, R5.Pin_0, R2.Pin_0, R3.Pin_1, BB1.LV, U1.OUT, C3.1
  N5: ESP1.EN, R2.Pin_1
  N6: ESP1.RST, S2.Pin_1, S2.Pin_2, R5.Pin_1
  N7: >4_5V.VCC, U1.IN, C1.+
  N8: R3.Pin_0, S1.L2
  N9: S1.L1, R4.Pin_0
  N10: BB1.HV, Part2.POWER
  N11: BB1.B1, Part2.RXI
  N12: BB1.B2, Part2.TXO

custom parts:
  ESP 12E: ESP 12e module with spi interface and wifi connection
  4-Line Bi-Directional Level Shifter: 4-Channel Bi-Directional Level Shifter
