# Fritzing sketch Programming (saved by Fritzing 0.9.2b)
breadboards: 2

parts:
  ESP1 = ESP 12E
  LED1 = LED_BARGRAPH_10 [package=led_bargaph_10]
  R1 = Resistor [tolerance=±5% resistance=1k package=THT]
  C1 = Electrolytic Capacitor [capacitance=470µF package="100 mil [THT, electrolytic]"]
  3_3V = Power plug
  S1 = Pushbutton [package="[THT]"]
  R2 = Resistor [tolerance=±5% resistance=10k package=THT]
  R3 = Resistor [tolerance=±5% resistance=10k package=THT]
  R4 = Resistor [tolerance=±5% resistance=10k package=THT]
  R5 = Resistor [tolerance=±5% resistance=10k package=THT]
  S2 = Toggle Switch [package=THT]
  BB1 = 4-Line Bi-Directional Level Shifter
  Part2 = FTDI Basic Programmer

nets:
  N1: ESP1.TX0, BB1.A1
  N2: ESP1.RX0, BB1.A2
  GPIO5: ESP1.GPIO5, LED1.C_A
  GPIO4: ESP1.GPIO4, LED1.B_A
  N3: ESP1.GPIO0, S2.COM
  GPIO2: ESP1.GPIO2, LED1.A_A
  N4: ESP1.GPIO15, R4.Pin_0
  GND: ESP1.GND, R1.Pin_0, C1.-, 3_3V.GND, S1.Pin_3, S1.Pin_4, R4.Pin_1, S2.L1, BB1.GND, Part2.GND
  3V3: ESP1.VCC, C1.+, 3_3V.VCC, R2.Pin_0, R3.Pin_0, R5.Pin_1, BB1.LV
  GPIO13: ESP1.GPIO13, LED1.D_A
  GPIO12: ESP1.GPIO12, LED1.E_A
  GPIO14: ESP1.GPIO14, LED1.F_A
  GPIO16: ESP1.GPIO16, LED1.G_A
  N5: ESP1.EN, R3.Pin_1
  N6: ESP1.RST, S1.Pin_1, S1.Pin_2, R2.Pin_1
  N7: LED1.G_C, LED1.F_C, LED1.E_C, LED1.D_C, LED1.C_C, LED1.B_C, LED1.A_C, R1.Pin_1
  N8: R5.Pin_0, S2.L2
  N9: BB1.HV, Part2.POWER
  N10: BB1.B1, Part2.RXI
  N11: BB1.B2, Part2.TXO

custom parts:
  ESP 12E: ESP 12e module with spi interface and wifi connection
  4-Line Bi-Directional Level Shifter: 4-Channel Bi-Directional Level Shifter
