# Fritzing sketch RgbLedFiddler (saved by Fritzing 0.9.2b)
breadboards: 2

parts:
  LED1 = RGB LED - (4 legs) [package="5 mm [THT]"]
  ESP12 = ESP 12E
  R9 = Resistor [tolerance=±5% resistance=10k package=THT]
  R10 = Resistor [tolerance=±5% resistance=10k part_number=built-in package=THT]
  R11 = Resistor [tolerance=±5% resistance=10k part_number=built-in package=THT]
  4_5-9V = Power plug
  U1 = Voltage Regulator - 3.3V [part_number=LD1117-3.3 package="TO220 [THT]"]
  R1 = Resistor [tolerance=±5% resistance=1.5k package=THT]
  R2 = Resistor [tolerance=±5% resistance=1.2k package=THT]
  R3 = Resistor [tolerance=±5% resistance=680k package=THT]
  C1 = Electrolytic Capacitor [capacitance=10µF package="100 mil [THT, electrolytic]"]
  C2 = Electrolytic Capacitor [capacitance=470µF package="100 mil [THT, electrolytic]"]
  C3 = Ceramic Capacitor [capacitance=100nF package="100 mil [THT, multilayer]"]

nets:
  N1: LED1.red_cathode, R1.Pin_1
  Vcc: LED1.common_anode, ESP12.VCC, R9.Pin_0, R10.Pin_0, U1.output_voltage, C2.+, C3.1
  N2: LED1.green_cathode, R2.Pin_1
  N3: LED1.blue_cathode, R3.Pin_1
  N4: ESP12.GPIO15, R11.Pin_0
  GND: ESP12.GND, R11.Pin_1, 4_5-9V.GND, U1.GND, C1.-, C2.-, C3.0
  PWM_R: ESP12.GPIO13, R1.Pin_0
  PWM_G: ESP12.GPIO12, R2.Pin_0
  PWM_B: ESP12.GPIO14, R3.Pin_0
  N5: ESP12.EN, R10.Pin_1
  N6: ESP12.RST, R9.Pin_1
  N7: 4_5-9V.VCC, U1.input_voltage, C1.+

notes:
  Built-in to the ESP12 module adapter

custom parts:
  ESP 12E: ESP 12e module with spi interface and wifi connection
