# Fritzing sketch DHT11 (saved by Fritzing 0.9.2b)
breadboards: 1

parts:
  U1 = ESP8266 WiFi Module [part_number=ESP8266]
  Part1 = FTDI Basic Programmer
  R1 = Resistor [tolerance=±5% resistance=10k package=THT]
  BB1 = 4-Line Bi-Directional Level Shifter
  5-9V = Power plug
  C1 = Electrolytic Capacitor [capacitance=100µF package="100 mil [THT, electrolytic]"]
  U3 = Voltage Regulator - 3.3V [part_number=LD1117-3.3 package="TO220 [THT]"]
  C2 = Electrolytic Capacitor [capacitance=10µF package="100 mil [THT, electrolytic]"]
  SW1 = DIP SWITCH [package=dipswitch-02]
  R2 = Resistor [tolerance=±5% resistance=10k package=THT]
  R3 = Resistor [tolerance=±5% resistance=10k package=THT]
  J1 = female pin header, 6 pins [form="♀ (female)"]
  J2 = shrouded pin header, 8 pins [form="♂ (shrouded male)"]
  J3 = female pin header, 2 pins [form="♀ (female)"]
  DHT1 = DHT11 Humitidy and Temperature Sensor

nets:
  RxD: U1.RXD, BB1.A1, J2.pin5
  V33: U1.VCC, R1.Pin_1, BB1.LV, C1.+, U3.output_voltage, C2.+, R2.Pin_1, R3.Pin_0, J2.pin4, DHT1.VDD
  GPIO_0: U1.GPIO_0, R1.Pin_0, SW1.4, J2.pin6
  RSTn: U1.RST, SW1.3, R2.Pin_0, J2.pin3
  GPIO_2: U1.GPIO_2, J2.pin7, J3.pin1, DHT1.DATA
  CH_PD: U1.CH_PD, R3.Pin_1, J2.pin2
  GND: U1.GND, Part1.GND, BB1.GND, 5-9V.GND, C1.-, U3.GND, C2.-, SW1.1, SW1.2, J1.pin6, J2.pin8, J3.pin2, DHT1.GND
  TxD: U1.TXD, BB1.A2, J2.pin1
  B2: Part1.RXI, BB1.B2, J1.pin2
  B1: Part1.TXO, BB1.B1, J1.pin3
  HV: Part1.POWER, BB1.HV, J1.pin4
  N1: 5-9V.VCC, U3.input_voltage

notes:
  DIY Dev Board

custom parts:
  ESP8266 WiFi Module: Generic WiFi Module based on the ESP8266 with onboard PCB antenna and UART communications
  4-Line Bi-Directional Level Shifter: 4-Channel Bi-Directional Level Shifter
  DHT11 Humitidy and Temperature Sensor: DHT11 Humidity and Temperature Sensor
