# Fritzing sketch YouTubeFootSwitch (saved by Fritzing 0.9.2b)
breadboards: 2

parts:
  U2 = 74HC595 [package="DIP16 [THT]"]
  U3 = 74HC595 [package="DIP16 [THT]"]
  LED0 = RGB LED - (4 legs) [package="5 mm [THT]"]
  R1 = Resistor [tolerance=±5% resistance=680 package=THT]
  LED1 = RGB LED - (4 legs) [package="5 mm [THT]"]
  R2 = Resistor [tolerance=±5% resistance=680 package=THT]
  LED2 = RGB LED - (4 legs) [package="5 mm [THT]"]
  LED3 = RGB LED - (4 legs) [package="5 mm [THT]"]
  R3 = Resistor [tolerance=±5% resistance=680 package=THT]
  R4 = Resistor [tolerance=±5% resistance=680 package=THT]
  S0 = Pushbutton [package=THT]
  S1 = Pushbutton [package=THT]
  S2 = Pushbutton [package=THT]
  S3 = Pushbutton [package=THT]
  R5 = Resistor [tolerance=±5% resistance=10k package=THT]
  R6 = Resistor [tolerance=±5% resistance=10k package=THT]
  R7 = Resistor [tolerance=±5% resistance=10k package=THT]
  R8 = Resistor [tolerance=±5% resistance=10k package=THT]
  ESP2 = ESP 12E
  R9 = Resistor [tolerance=±5% resistance=10k package=THT]
  R10 = Resistor [tolerance=±5% resistance=10k part_number=built-in package=THT]
  R11 = Resistor [tolerance=±5% resistance=10k part_number=built-in package=THT]
  3_2-3_3V_Regulated = Power plug
  C1 = Ceramic Capacitor [capacitance=100nF package="100 mil [THT, multilayer]"]
  C2 = Electrolytic Capacitor [capacitance=47µF package="100 mil [THT, electrolytic]"]

nets:
  Q1R: U2.Q2, LED0.red_cathode
  Q1G: U2.Q3, LED0.green_cathode
  Q1B: U2.Q4, LED0.blue_cathode
  Q2R: U2.Q5, LED1.red_cathode
  Q2G: U2.Q6, LED1.green_cathode
  Q2B: U2.Q7, LED1.blue_cathode
  GND: U2.GND, U2.OE, U3.GND, U3.OE, R5.Pin_0, R6.Pin_0, R7.Pin_0, R8.Pin_0, ESP2.GND, R11.Pin_1, 3_2-3_3V_Regulated.GND, C1.0, C2.-
  CARRY: U2.Q7', U3.DS
  Vcc: U2.MR, U2.VCC, U3.MR, U3.VCC, R1.Pin_1, R2.Pin_1, R3.Pin_1, R4.Pin_1, S0.leg0, S1.leg0, S2.leg0, S3.leg0, ESP2.VCC, R9.Pin_0, R10.Pin_0, 3_2-3_3V_Regulated.VCC, C1.1, C2.+
  CLOCK: U2.SH_CP, U3.SH_CP, ESP2.GPIO5
  LATCH: U2.ST_CP, U3.ST_CP, ESP2.GPIO4
  DATA: U2.DS, ESP2.GPIO2
  Q3R: U3.Q2, LED2.red_cathode
  Q3G: U3.Q3, LED2.green_cathode
  Q3B: U3.Q4, LED2.blue_cathode
  Q4R: U3.Q5, LED3.red_cathode
  Q4G: U3.Q6, LED3.green_cathode
  Q4B: U3.Q7, LED3.blue_cathode
  N1: LED0.common_anode, R1.Pin_0
  N2: LED1.common_anode, R2.Pin_0
  N3: LED2.common_anode, R3.Pin_0
  N4: LED3.common_anode, R4.Pin_0
  SW0: S0.leg1, R5.Pin_1, ESP2.GPIO16
  SW1: S1.leg1, R6.Pin_1, ESP2.GPIO14
  SW2: S2.leg1, R7.Pin_1, ESP2.GPIO12
  SW3: S3.leg1, R8.Pin_1, ESP2.GPIO13
  N5: ESP2.GPIO15, R11.Pin_0
  N6: ESP2.EN, R10.Pin_1
  N7: ESP2.RST, R9.Pin_1

notes:
  Built-in to the ESP12 module adapter

custom parts:
  ESP 12E: ESP 12e module with spi interface and wifi connection
