# Fritzing sketch esp-12-temperature-logger (saved by Fritzing 1.0.1rc)
breadboards: 1

parts:
  DS1 = DS18B20 1-Wire Temperature Sensor [part_number=DS18B20]
  R1 = Resistor [tolerance=±5% power=0.25W resistance=4.7k package=THT]
  ESP-12_Adapter = IC, DIP package, 16 pins [chip_label="ESP12 Adapter"]
  U2 = V_REG_LD1117VXX [part_number=LD1117A package=78xxl]
  C4 = Ceramic Capacitor [capacitance=100nF voltage=35V package="100 mil [THT, multilayer]"]
  C5 = Electrolytic Capacitor [capacitance=10µF voltage=35V package="100 mil [THT, electrolytic]"]
  C6 = Electrolytic Capacitor [capacitance=470µF voltage=35V package="100 mil [THT, electrolytic]"]
  >4_5V1 = Power plug
  R2 = Resistor [tolerance=±5% power=0.25W resistance=10k package=THT]

nets:
  GND: DS1.GND, ESP-12_Adapter.pin9, U2.GND, C4.0, C5.-, C6.-, >4_5V1.GND
  TEMP: DS1.DQ, R1.Pin_1, ESP-12_Adapter.pin11
  3.3V: DS1.VDD, R1.Pin_0, ESP-12_Adapter.pin8, U2.OUT, C4.1, C6.+, R2.Pin_0
  N1: ESP-12_Adapter.pin1, R2.Pin_1
  N2: U2.IN, C5.+, >4_5V1.VCC
