# Fritzing sketch AMTransmitter (saved by Fritzing 0.9.2b)
breadboards: 1

parts:
  U1 = 555 Timer [package="SO8 [SMD]"]
  P1 = Trimmer Potentiometer [maximum_resistance=10kΩ package=THT]
  5V = Power plug
  ANT1 = Antenna
  C1 = Ceramic Capacitor [capacitance=1nF package="100 mil [THT, multilayer]"]
  U2 = 2.5mm Audio Jack [package=stereojack2.5mm_specia_pogopins]
  R2 = Resistor [tolerance=±5% resistance=1k package=THT]
  R1 = Resistor [tolerance=±5% resistance=220 package=THT]
  C2 = Ceramic Capacitor [capacitance=10nF package="100 mil [THT, multilayer]"]
  C3 = Ceramic Capacitor [capacitance=10nF package="100 mil [THT, multilayer]"]
  Q1 = NPN-Transistor [part_number=BC547 package="TO92 [THT]"]

nets:
  GND: U1.Pin_1, 5V.GND, C1.0, U2.SLEEVE, C2.1, C3.1
  N1: U1.Pin_2, U1.Pin_6, C1.1, R2.Pin_1
  N2: U1.Pin_3, U2.RIGHT, C3.0, Q1.B
  N3: U1.Pin_4, U1.Pin_8, 5V.VCC, R1.Pin_0, Q1.C
  N4: U1.Pin_5, C2.0
  N5: U1.Pin_7, P1.wiper, R1.Pin_1
  N6: P1.leg1, R2.Pin_0
  N7: ANT1.antenna_lead, Q1.E
