# Fritzing sketch AdjustablePulseGenerator (saved by Fritzing 0.9.2b)
breadboards: 1

parts:
  R3 = Resistor [tolerance=±5% resistance=1.5k package=THT]
  U1 = 555 Timer [package="SO8 [SMD]"]
  C5 = Electrolytic Capacitor [capacitance=100µF package="100 mil [THT, electrolytic]"]
  C6 = Electrolytic Capacitor [capacitance=100µF package="100 mil [THT, electrolytic]"]
  C4 = Electrolytic Capacitor [capacitance=1µF package="100 mil [THT, electrolytic]"]
  C3 = Ceramic Capacitor [capacitance=1nF package="100 mil [THT, multilayer]"]
  C2 = Ceramic Capacitor [capacitance=100nF package="100 mil [THT, multilayer]"]
  R1 = Trimmer Potentiometer [maximum_resistance=10kΩ package=THT]
  R2 = Trimmer Potentiometer [maximum_resistance=10kΩ package=THT]
  LED1 = LED - 5mm [color="Red (633nm)" package="5 mm [THT]"]
  C1 = Ceramic Capacitor [capacitance=100nF package="100 mil [THT, multilayer]"]
  5-15V = Power plug
  JP1 = Header 5x2 [package=2x5-ra]
  R4 = Resistor [tolerance=±5% resistance=220 package=THT]
  R5 = Resistor [tolerance=±5% resistance=220 package=THT]

nets:
  Vcc: R3.Pin_0, U1.Pin_4, U1.Pin_8, C6.+, 5-15V.VCC, R4.Pin_0
  N1: R3.Pin_1, LED1.anode
  GND: U1.Pin_1, C5.-, C6.-, C4.-, C3.0, C2.0, C1.1, 5-15V.GND
  N2: U1.Pin_2, U1.Pin_6, R2.leg2, JP1.2, JP1.4, JP1.6, JP1.8
  OUT: U1.Pin_3, LED1.cathode
  N3: U1.Pin_5, C1.0
  N4: U1.Pin_7, R1.leg2, R5.Pin_0
  N5: C5.+, JP1.1
  N6: C4.+, JP1.3
  N7: C3.1, JP1.7
  N8: C2.1, JP1.5
  N9: R1.leg1, R1.wiper, R4.Pin_1
  N10: R2.leg1, R2.wiper, R5.Pin_1
