# Fritzing sketch AircraftNavigationLights (saved by Fritzing 0.9.2b)
breadboards: 1

parts:
  9V = Power plug
  U1 = 555 Timer [package="DIP8 [THT]"]
  U2 = 555 Timer [package="DIP8 [THT]"]
  LED1 = LED - 3mm [color="White (4500K)" package="3 mm [THT]"]
  LED2 = LED - 3mm [color="White (4500K)" package="3 mm [THT]"]
  R1 = Resistor [tolerance=±5% resistance=470k package=THT]
  D1 = Rectifier Diode [part_number=1N4148 package="300 mil [THT]"]
  R2 = Resistor [tolerance=±5% resistance=2M package=THT]
  C1 = Electrolytic Capacitor [capacitance=2.2µF package="100 mil [THT, electrolytic]"]
  R3 = Resistor [tolerance=±5% resistance=1M package=THT]
  C2 = Ceramic Capacitor [capacitance=220nF package="100 mil [THT, multilayer]"]
  R4 = Resistor [tolerance=±5% resistance=470 package=THT]
  C3 = Ceramic Capacitor [capacitance=100nF package="100 mil [THT, multilayer]"]
  C4 = Ceramic Capacitor [capacitance=100nF package="100 mil [THT, multilayer]"]

nets:
  GND: 9V.GND, U1.Ground, U2.Ground, LED1.cathode, LED2.cathode, C1.-, C2.0, C3.0, C4.0
  VCC: 9V.VCC, U1.Reset, U1.Vcc_Supply_Voltage, U2.Vcc_Supply_Voltage
  N1: U1.Trigger, U1.Threshold, D1.cathode, R2.Pin_0, C1.+
  N2: U1.Output, U2.Reset, R1.Pin_1, R2.Pin_1
  N3: U1.Control_Voltage, C3.1
  N4: U2.Trigger, U2.Threshold, R3.Pin_0, C2.1
  N5: U2.Output, R3.Pin_1, R4.Pin_0
  N6: U2.Control_Voltage, C4.1
  N7: LED1.anode, LED2.anode, R4.Pin_1
  N8: R1.Pin_0, D1.anode
