# Fritzing sketch AstableOscillator (saved by Fritzing 0.9.2b)
breadboards: 1

parts:
  U1 = 555 Timer [package="SO8 [SMD]"]
  R3 = Resistor [tolerance=±5% resistance=1k package=THT]
  LED1 = LED - 5mm [color="Red (633nm)" package="5 mm [THT]"]
  R1 = Resistor [tolerance=±5% resistance=10k package=THT]
  R2 = Resistor [tolerance=±5% resistance=330k package=THT]
  C1 = Electrolytic Capacitor [capacitance=2.2µF package="100 mil [THT, electrolytic]"]
  C2 = Ceramic Capacitor [capacitance="100 nF" package="0603 [SMD, multilayer]"]
  Uno = Arduino Uno (Rev3)
  9V = Power plug

nets:
  GND: U1.Pin_1, LED1.cathode, C1.-, C2.1, Uno.GND, 9V.GND
  N1: U1.Pin_2, U1.Pin_6, R2.Pin_1, C1.+
  N2: U1.Pin_3, R3.Pin_0
  N3: U1.Pin_4, U1.Pin_8, R1.Pin_0, 9V.VCC
  N4: U1.Pin_5, C2.0
  N5: U1.Pin_7, R1.Pin_1, R2.Pin_0
  PROBEA: R3.Pin_1, LED1.anode, Uno.A0

notes:
  Note: alternatively, can power the board from +5V Arduino pin
