# Fritzing sketch Minimal (saved by Fritzing 1.0.7)
breadboards: 1

parts:
  U1 = 555 Timer [package="DIP8 [THT]"]
  Power = Power plug
  C1 = Electrolytic Capacitor [capacitance=1µF voltage=35V package="100 mil [THT, electrolytic]"]
  R1 = Resistor [tolerance=±5% power=0.25W resistance=10k package=THT]
  R2 = Resistor [tolerance=±5% power=0.25W resistance=220 package=THT]
  LED1 = LED - 3mm [color="Red (633nm)" current=0.030A package="3 mm [THT]"]

nets:
  GND: U1.Ground, Power.GND, C1.-, R2.Pin_0
  N1: U1.Trigger, U1.Threshold, C1.+, R1.Pin_0
  N2: U1.Output, R1.Pin_1, LED1.anode
  5V: U1.Reset, U1.Vcc_Supply_Voltage, Power.VCC
  N3: R2.Pin_1, LED1.cathode
