# Fritzing sketch BeatBot (saved by Fritzing 0.9.2b)
breadboards: 1

parts:
  9V = Power plug
  U1 = 555 Timer [package="DIP8 [THT]"]
  IC3 = IC, DIP package, 16 pins [chip_label=CD4017 part_number=CD4017]
  U2 = 555 Timer [package="DIP8 [THT]"]
  U3 = 555 Timer [package="DIP8 [THT]"]
  R1 = Resistor [tolerance=±5% resistance=10k package=THT]
  R2 = Trimmer Potentiometer [maximum_resistance=500kΩ package=THT]
  J1 = Piezo Speaker
  C1 = Ceramic Capacitor [capacitance=100nF package="100 mil [THT, multilayer]"]
  C2 = Electrolytic Capacitor [capacitance=2.2µF voltage=50V package="100 mil [THT, electrolytic]"]
  L1 = Solenoid
  D7 = Rectifier Diode [part_number=1N4001 package="300 mil [THT]"]
  C3 = Ceramic Capacitor [capacitance=220nF package="100 mil [THT, multilayer]"]
  R3 = Resistor [tolerance=±5% resistance=100k package=THT]
  D6 = Rectifier Diode [part_number=1N4148 package="300 mil [THT]"]
  R4 = Resistor [tolerance=±5% resistance=10k package=THT]
  S1 = Pushbutton [package=THT]
  D5 = Rectifier Diode [part_number=1N4148 package="300 mil [THT]"]
  D1 = Rectifier Diode [part_number=1N4148 package="300 mil [THT]"]
  D2 = Rectifier Diode [part_number=1N4148 package="300 mil [THT]"]
  D3 = Rectifier Diode [part_number=1N4148 package="300 mil [THT]"]
  R5 = Resistor [tolerance=±5% resistance=12k package=THT]
  R6 = Resistor [tolerance=±5% resistance=22k package=THT]
  R7 = Resistor [tolerance=±5% resistance=51k package=THT]
  C4 = Electrolytic Capacitor [capacitance=100µF voltage=50V package="100 mil [THT, electrolytic]"]
  R8 = Trimmer Potentiometer [maximum_resistance=2kΩ package=THT]
  Q1 = PNP-Transistor [part_number=2N3906 package="TO92 [THT]"]
  R9 = Resistor [tolerance=±5% resistance=22k package=THT]
  R10 = Resistor [tolerance=±5% resistance=20k package=THT]
  C5 = Electrolytic Capacitor [capacitance=10µF voltage=50V package="100 mil [THT, electrolytic]"]
  C6 = Ceramic Capacitor [capacitance=100nF package="100 mil [THT, multilayer]"]
  R11 = Resistor [tolerance=±5% resistance=10k package=THT]
  D8 = Rectifier Diode [part_number=1N4148 package="300 mil [THT]"]
  R12 = Resistor [tolerance=±5% resistance=1k package=THT]

nets:
  GND: 9V.GND, U1.Ground, IC3.pin8, IC3.pin13, U2.Ground, U3.Ground, J1.pin1, C1.0, C2.-, L1.pin1, D7.anode, C3.0, R4.Pin_1, C5.-, R11.Pin_1, D8.anode
  VCC: 9V.VCC, U1.Reset, U1.Vcc_Supply_Voltage, IC3.pin16, U2.Reset, U2.Vcc_Supply_Voltage, U3.Reset, U3.Vcc_Supply_Voltage, R1.Pin_0, C1.1, Q1.E, R9.Pin_1
  N1: U1.Trigger, U1.Threshold, R2.leg2, C2.+
  N2: U1.Output, IC3.pin14
  N3: U1.Discharge, R1.Pin_1, R2.leg1, R2.wiper
  N4: IC3.pin2, D2.anode
  N5: IC3.pin3, D1.anode, C6.0
  N6: IC3.pin4, S1.leg1, D3.anode
  N7: IC3.pin10, D6.anode
  N8: IC3.pin15, D6.cathode, R4.Pin_0, D5.cathode
  N9: U2.Trigger, U2.Threshold, C3.1, R3.Pin_1
  N10: U2.Output, R3.Pin_0, C4.+
  N11: U2.Control_Voltage, R5.Pin_1, R6.Pin_1, R7.Pin_1
  N12: U3.Trigger, R10.Pin_0, C5.+
  N13: U3.Output, R12.Pin_0
  N14: U3.Threshold, C6.1, R11.Pin_0, D8.cathode
  N15: U3.Discharge, R9.Pin_0, R10.Pin_1
  N16: J1.pin2, R8.leg1, R8.wiper
  N17: L1.pin2, D7.cathode, Q1.C
  N18: S1.leg0, D5.anode
  N19: D1.cathode, R5.Pin_0
  N20: D2.cathode, R6.Pin_0
  N21: D3.cathode, R7.Pin_0
  N22: C4.-, R8.leg2
  N23: Q1.B, R12.Pin_1
