# Fritzing sketch BipolarLedFlasher (saved by Fritzing 0.9.2b)
breadboards: 1

parts:
  U1 = 555 Timer [package="DIP8 [THT]"]
  R1 = Resistor [tolerance=±5% resistance=220 package=THT]
  R2 = Resistor [tolerance=±5% resistance=220 package=THT]
  LED1 = LED - 3mm [color="Red (633nm)" package="3 mm [THT]"]
  LED2 = LED - 3mm [color="Green (570nm)" package="3 mm [THT]"]
  VCC1 = Battery block 9V
  R3 = Resistor [tolerance=±5% resistance=33k package=THT]
  C1 = Electrolytic Capacitor [capacitance=10µF package="100 mil [THT, electrolytic]"]

nets:
  N1: U1.Ground, R2.Pin_1, VCC1.-, C1.-
  N2: U1.Trigger, U1.Threshold, R3.Pin_0, C1.+
  N3: U1.Output, LED1.cathode, LED2.anode, R3.Pin_1
  N4: U1.Reset, U1.Vcc_Supply_Voltage, R1.Pin_0, VCC1.+
  N5: R1.Pin_1, LED1.anode
  N6: R2.Pin_0, LED2.cathode
