# Fritzing sketch Bistable (saved by Fritzing 0.9.2b)
breadboards: 1

parts:
  5V = Power plug
  U1 = 555 Timer [package="DIP8 [THT]"]
  S1 = Toggle Switch [package=THT]
  R1 = Resistor [tolerance=±5% resistance=1k package=THT]
  R2 = Resistor [tolerance=±5% resistance=1k package=THT]
  C1 = Ceramic Capacitor [capacitance=100nF package="100 mil [THT, multilayer]"]
  LED1 = LED - 5mm [color="Red (633nm)" package="5 mm [THT]"]
  R3 = Resistor [tolerance=±5% resistance=220 package=THT]

nets:
  GND: 5V.GND, U1.Ground, U1.Threshold, S1.COM, C1.0, R3.Pin_0
  VCC: 5V.VCC, U1.Vcc_Supply_Voltage, R1.Pin_1, R2.Pin_1
  N1: U1.Trigger, S1.L2, R1.Pin_0
  OUT: U1.Output, LED1.anode
  N2: U1.Reset, S1.L1, R2.Pin_0
  N3: U1.Control_Voltage, C1.1
  N4: LED1.cathode, R3.Pin_1
