# Fritzing sketch BreadboardPWMGen (saved by Fritzing 1.0.1rc)
breadboards: 1

parts:
  U1 = 555 Timer [package="DIP8 [THT]"]
  R1 = Resistor [tolerance=±5% resistance=1k power=0.25W package=THT]
  R2 = Trimmer Potentiometer [maximum_resistance=50kΩ knob_status=50% power=0.5W package=THT]
  D1 = Rectifier Diode [part_number=1N4148 package="300 mil [THT]"]
  D2 = Rectifier Diode [part_number=1N4148 package="300 mil [THT]"]
  3-15V = Power plug
  C5 = Ceramic Capacitor [capacitance=1nF voltage=35V package="100 mil [THT, multilayer]"]
  C2 = Ceramic Capacitor [capacitance=100nF voltage=35V package="100 mil [THT, multilayer]"]
  R3 = Resistor [tolerance=±5% power=0.25W resistance=1k package=THT]
  LED1 = LED - 3mm [color="Red (633nm)" current=0.030A package="3 mm [THT]"]

nets:
  GND: U1.Ground, 3-15V.GND, C5.1, C2.1, R3.Pin_1
  N1: U1.Trigger, U1.Threshold, R2.wiper, C5.0
  CH1/OUT (PWM): U1.Output, LED1.anode
  VCC: U1.Reset, U1.Vcc_Supply_Voltage, R1.Pin_0, 3-15V.VCC
  N2: U1.Control_Voltage, C2.0
  N3: U1.Discharge, R1.Pin_1, D1.anode, D2.cathode
  N4: R2.leg1, D2.anode
  N5: R2.leg2, D1.cathode
  N6: R3.Pin_0, LED1.cathode
