# Fritzing sketch BreadboardPulseGen (saved by Fritzing 1.0.1rc)
breadboards: 1

parts:
  U1 = 555 Timer [package="DIP8 [THT]"]
  VR1 = Trimmer Potentiometer [maximum_resistance=100kΩ knob_status=50% power=0.5W package=THT]
  C1 = Electrolytic Capacitor [capacitance=10µF voltage=35V package="100 mil [THT, electrolytic]"]
  5V = Power plug
  VR2 = Trimmer Potentiometer [maximum_resistance=10kΩ knob_status=50% power=0.5W package=THT]
  C5 = Ceramic Capacitor [capacitance=100nF voltage=35V package="100 mil [THT, multilayer]"]
  R1 = Resistor [tolerance=±5% power=0.25W resistance=1k package=THT]
  R2 = Resistor [tolerance=±5% power=0.25W resistance=470 package=THT]
  LED1 = LED - 3mm [color="Red (633nm)" current=0.030A package="3 mm [THT]"]
  J1 = female pin header, 4 pins [form="♀ (female)"]
  C2 = Ceramic Capacitor [capacitance=1µF voltage=35V package="100 mil [THT, multilayer]"]
  J2 = female pin header, 4 pins [form="♀ (female)"]
  C3 = Ceramic Capacitor [capacitance=100nF voltage=35V package="100 mil [THT, multilayer]"]
  C4 = Ceramic Capacitor [capacitance=10nF voltage=35V package="100 mil [THT, multilayer]"]

nets:
  GND: U1.Ground, 5V.GND, VR2.leg1, C5.0, LED1.cathode, J1.pin4, J2.pin1, J2.pin2, J2.pin3, J2.pin4, C4.0
  N1: U1.Trigger, U1.Threshold, VR1.leg1, VR1.wiper, C1.+, C2.1, C3.1, C4.1
  OUT: U1.Output, R1.Pin_0, R2.Pin_0
  VCC: U1.Reset, U1.Vcc_Supply_Voltage, 5V.VCC, VR2.leg2
  N2: U1.Control_Voltage, VR2.wiper, C5.1
  N3: VR1.leg2, R1.Pin_1
  N4: C1.-, J1.pin1
  N5: R2.Pin_1, LED1.anode
  N6: J1.pin2, C2.0
  N7: J1.pin3, C3.0
