# Fritzing sketch CompactLEDFlasher (saved by Fritzing 1.0.1rc)
breadboards: 1

parts:
  U1 = 555 Timer [package="DIP8 [THT]"]
  Power = Power plug
  LED1 = LED - 3mm [color="Red (633nm)" current=0.030A package="3 mm [THT]"]
  R1 = Resistor [tolerance=±5% power=0.25W resistance=10M package=THT]
  R2 = Resistor [tolerance=±5% power=0.25W resistance=470 package=THT]
  C1 = Ceramic Capacitor [capacitance=100nF voltage=35V package="100 mil [THT, multilayer]"]

nets:
  GND: U1.Ground, Power.GND, C1.0
  N1: U1.Trigger, U1.Threshold, R1.Pin_0, C1.1
  OUT: U1.Output, R1.Pin_1
  5V: U1.Reset, U1.Vcc_Supply_Voltage, Power.VCC, LED1.anode
  N2: U1.Discharge, R2.Pin_1
  N3: LED1.cathode, R2.Pin_0
