# Fritzing sketch ContinuityTester (saved by Fritzing 0.9.2b)
breadboards: 1

parts:
  Q2 = Basic FET P-Channel [part_number=BS250 package="D2Pak [SMD]"]
  Q1 = Basic FET N-Channel [part_number=2N7000 package="DPak [SMD]"]
  3V = LilyPad Coin Cell Battery Holder
  J1 = Screw terminal - 2 pins [package=THT]
  R1 = Resistor [tolerance=±5% resistance=220 package=THT]
  R3 = Resistor [tolerance=±5% resistance=3.3M package=THT]
  R2 = Resistor [tolerance=±5% resistance=330 package=THT]
  U1 = 555 Timer [package="DIP8 [THT]"]
  C1 = Ceramic Capacitor [capacitance=10nF package="100 mil [THT, multilayer]"]
  R5 = Resistor [tolerance=±5% resistance=39k package=THT]
  C2 = Ceramic Capacitor [capacitance=100nF package="100 mil [THT, multilayer]"]
  J2 = Piezo Speaker
  Q3 = Basic FET N-Channel [part_number=2N7000 package="DPak [SMD]"]
  R6 = Resistor [tolerance=±5% resistance=10k package=THT]
  R4 = Resistor [tolerance=±5% resistance=220 package=THT]
  LED1 = LED - 3mm [color="Blue (430nm)" package="3 mm [THT]"]

nets:
  N1: Q2.Gate, Q1.drain, R3.Pin_0
  VCC: Q2.drain, U1.Reset, U1.Vcc_Supply_Voltage, J2.pin1, R6.Pin_1, LED1.anode
  Vbat: Q2.source, 3V.+, R1.Pin_0, R3.Pin_1
  N2: Q1.Gate, J1.pin2, R2.Pin_0
  GND: Q1.source, 3V.-, R2.Pin_1, U1.Ground, C1.1, C2.0, Q3.source, R4.Pin_0
  N3: J1.pin1, R1.Pin_1
  N4: U1.Trigger, U1.Threshold, C1.0, R5.Pin_0
  N5: U1.Output, R5.Pin_1, Q3.Gate
  N6: U1.Control_Voltage, C2.1
  N7: J2.pin2, Q3.drain, R6.Pin_0
  N8: R4.Pin_1, LED1.cathode

notes:
  Continuity probes
