# Fritzing sketch DelayOn (saved by Fritzing 1.0.1rc)
breadboards: 1

parts:
  U1 = 555 Timer [package="DIP8 [THT]"]
  Power = Power plug
  LED1 = LED - 3mm [color="Red (633nm)" current=0.030A package="3 mm [THT]"]
  R1 = Resistor [tolerance=±5% power=0.25W resistance=1k package=THT]
  R2 = 12mm Trimmer Potentiometer (Large) [maximum_resistance=1MΩ knob_status=50% power=0.5W package=THT]
  C1 = Electrolytic Capacitor [capacitance=100µF voltage=35V package="100 mil [THT, electrolytic]"]
  LED2 = LED - 3mm [color="Green (555nm)" current=0.030A package="3 mm [THT]"]
  R3 = Resistor [tolerance=±5% power=0.25W resistance=1k package=THT]

nets:
  GND: U1.Ground, Power.GND, R1.Pin_1, R2.wiper, R3.Pin_0
  N1: U1.Trigger, U1.Threshold, R2.leg2, C1.-
  N2: U1.Output, LED1.anode
  5V: U1.Reset, U1.Vcc_Supply_Voltage, Power.VCC, C1.+, LED2.anode
  N3: LED1.cathode, R1.Pin_0
  N4: LED2.cathode, R3.Pin_1
