# Fritzing sketch Dice (saved by Fritzing 0.9.2b)
breadboards: 1

parts:
  U1 = 555 Timer [package="SO8 [SMD]"]
  IC2 = IC, DIP package, 16 pins [chip_label=CD4017 part_number=CD4017]
  R1 = Resistor [tolerance=±5% resistance=10k package=THT]
  R2 = Resistor [tolerance=±5% resistance=1M package=THT]
  C1 = Electrolytic Capacitor [capacitance=1µF package="100 mil [THT, electrolytic]"]
  5-12V = Power plug
  C2 = Ceramic Capacitor [capacitance=100nF package="100 mil [THT, multilayer]"]
  LED1 = LED - 5mm [color="Red (633nm)" package="5 mm [THT]"]
  LED2 = LED - 5mm [color="Red (633nm)" package="5 mm [THT]"]
  LED3 = LED - 5mm [color="Red (633nm)" package="5 mm [THT]"]
  LED4 = LED - 5mm [color="Red (633nm)" package="5 mm [THT]"]
  LED5 = LED - 5mm [color="Red (633nm)" package="5 mm [THT]"]
  R5 = Resistor [tolerance=±5% resistance=1k package=THT]
  LED6 = LED - 5mm [color="Red (633nm)" package="5 mm [THT]"]
  R4 = Resistor [tolerance=±5% resistance=330 package=THT]
  R3 = Resistor [tolerance=±5% resistance=330 package=THT]
  LED7 = LED - 5mm [color="Red (633nm)" package="5 mm [THT]"]
  N3 = NPN-Transistor [part_number=2N3904 package="TO92 [THT]"]
  N1 = NPN-Transistor [part_number=2N3904 package="TO92 [THT]"]
  N2 = NPN-Transistor [part_number=2N3904 package="TO92 [THT]"]
  R10 = Resistor [tolerance=±5% resistance=10k package=THT]
  R11 = Resistor [tolerance=±5% resistance=10k package=THT]
  R12 = Resistor [tolerance=±5% resistance=10k package=THT]
  R13 = Resistor [tolerance=±5% resistance=10k package=THT]
  D1 = Rectifier Diode [part_number=1N4148 package="300 mil [THT]"]
  D2 = Rectifier Diode [part_number=1N4148 package="300 mil [THT]"]
  D3 = Rectifier Diode [part_number=1N4148 package="300 mil [THT]"]
  D4 = Rectifier Diode [part_number=1N4148 package="300 mil [THT]"]
  D5 = Rectifier Diode [part_number=1N4148 package="300 mil [THT]"]
  R14 = Resistor [tolerance=±5% resistance=1M package=THT]
  P2 = PNP-Transistor [part_number=2N3906 package="TO92 [THT]"]
  R15 = Resistor [tolerance=±5% resistance=1M package=THT]
  SW1 = Pushbutton [package="[THT]"]
  D5b = Rectifier Diode [part_number=1N4148 package="300 mil [THT]"]
  D4b = Rectifier Diode [part_number=1N4148 package="300 mil [THT]"]
  D1b = Rectifier Diode [part_number=1N4148 package="300 mil [THT]"]
  R16 = Resistor [tolerance=±5% resistance=330 package=THT]
  N4b = NPN-Transistor [part_number=2N3904 package="TO92 [THT]"]
  R17 = Resistor [tolerance=±5% resistance=10k package=THT]
  C4 = Electrolytic Capacitor [capacitance=1µF package="100 mil [THT, electrolytic]"]
  R18 = Resistor [tolerance=±5% resistance=10k package=THT]
  PF1 = Basic FET P-Channel [part_number=BS250 package="DPak [SMD]"]
  C5 = Electrolytic Capacitor [capacitance=47µF package="100 mil [THT, electrolytic]"]
  R19 = Resistor [tolerance=±5% resistance=330k package=THT]
  D6 = Rectifier Diode [part_number=1N4148 package="300 mil [THT]"]
  D7 = Rectifier Diode [part_number=1N4148 package="300 mil [THT]"]
  R20 = Resistor [tolerance=±5% resistance=330k package=THT]
  N4 = NPN-Transistor [part_number=2N3904 package="TO92 [THT]"]

nets:
  GND: U1.Pin_1, IC2.pin8, IC2.pin13, R2.Pin_1, 5-12V.GND, C2.0, LED6.cathode, N3.E, N1.E, N2.E, SW1.Pin_1, SW1.Pin_2, N4b.E, C4.-, C5.-
  N1: U1.Pin_2, U1.Pin_6, R2.Pin_0, C4.+, R18.Pin_1
  CLK: U1.Pin_3, IC2.pin14
  VCC: U1.Pin_4, U1.Pin_8, IC2.pin16, C1.+, R5.Pin_0, R4.Pin_0, R3.Pin_0, P2.E, R15.Pin_1, R17.Pin_1, PF1.drain, N4.C
  N2: U1.Pin_5, C2.1
  N3: U1.Pin_7, R1.Pin_1, R18.Pin_0
  Q5: IC2.pin1, D5.anode, D5b.anode
  Q1: IC2.pin2
  Q0: IC2.pin3, D1.anode, D1b.anode
  Q2: IC2.pin4, D2.anode
  Q6: IC2.pin5, IC2.pin15
  Q3: IC2.pin7, D3.anode
  Q4: IC2.pin10, D4.anode, D4b.anode
  N4: R1.Pin_0, P2.C
  N5: C1.-, R14.Pin_1, D7.anode
  VDD: 5-12V.VCC, PF1.source, R19.Pin_0
  N6: LED1.cathode, LED7.anode
  N7: LED1.anode, R3.Pin_1
  N8: LED2.cathode, LED6.anode
  N9: LED2.anode, R16.Pin_1
  N10: LED3.cathode, N2.C
  N11: LED3.anode, LED5.cathode
  N12: LED4.cathode, N3.C
  N13: LED4.anode, R5.Pin_1
  N14: LED5.anode, R4.Pin_1
  N15: LED7.cathode, N1.C
  N16: N3.B, R11.Pin_1
  N17: N1.B, R12.Pin_1
  N18: N2.B, R13.Pin_1
  S5: R10.Pin_0, D5.cathode
  N19: R10.Pin_1, N4b.B
  S0/S2/S5b: R11.Pin_0, D1.cathode, D2.cathode, D5b.cathode
  S0b/S3/S4b: R12.Pin_0, D3.cathode, D4b.cathode, D1b.cathode
  S4: R13.Pin_0, D4.cathode
  N20: R14.Pin_0, P2.B, R15.Pin_0
  N21: SW1.Pin_3, SW1.Pin_4, D6.cathode, D7.cathode
  N22: R16.Pin_0, N4.E
  N23: N4b.C, R17.Pin_0, N4.B
  N24: PF1.Gate, R19.Pin_1, R20.Pin_0
  N25: C5.+, D6.anode, R20.Pin_1
