# Fritzing sketch DigitalLogicClock (saved by Fritzing 0.9.2b)
breadboards: 1

parts:
  5V = Power plug
  IC1 = 555 Timer [package="DIP8 [THT]"]
  IC2 = 555 Timer [package="DIP8 [THT]"]
  IC3 = 555 Timer [package="DIP8 [THT]"]
  C2 = Ceramic Capacitor [capacitance=100nF package="100 mil [THT, multilayer]"]
  R1 = Resistor [tolerance=±5% resistance=470 package=THT]
  C1 = Electrolytic Capacitor [capacitance=10µF package="100 mil [THT, electrolytic]"]
  R2b = Trimmer Potentiometer [maximum_resistance=100kΩ package=THT]
  R2a = Resistor [tolerance=±5% resistance=1k package=THT]
  R2 = Resistor [tolerance=±5% resistance=10k package=THT]
  R3 = Resistor [tolerance=±5% resistance=1k package=THT]
  C3 = Electrolytic Capacitor [capacitance=10µF package="100 mil [THT, electrolytic]"]
  C4 = Ceramic Capacitor [capacitance=100nF package="100 mil [THT, multilayer]"]
  S1 = Pushbutton [package=THT]
  R4 = Resistor [tolerance=±5% resistance=1k package=THT]
  R5 = Resistor [tolerance=±5% resistance=1k package=THT]
  S2 = Toggle Switch [package=THT]
  C5 = Ceramic Capacitor [capacitance=100nF package="100 mil [THT, multilayer]"]
  IC4 = IC, DIP package, 14 pins [chip_label=IC part_number=74LS00]
  IC5 = IC, DIP package, 14 pins [chip_label=IC part_number=74LS00]
  S3 = Toggle Switch [package=THT]
  R6 = Resistor [tolerance=±5% resistance=10k package=THT]
  LED1 = LED - 5mm [color="Red (633nm)" package="5 mm [THT]"]
  R7 = Resistor [tolerance=±5% resistance=470 package=THT]

nets:
  GND: 5V.GND, IC1.Ground, IC2.Ground, IC3.Ground, IC3.Threshold, C2.0, C1.-, C3.-, C4.0, S1.leg0, S2.COM, C5.0, IC4.pin7, IC5.pin7, S3.L2, R7.Pin_0
  VCC: 5V.VCC, IC1.Reset, IC1.Vcc_Supply_Voltage, IC2.Reset, IC2.Vcc_Supply_Voltage, IC3.Vcc_Supply_Voltage, R1.Pin_0, R2.Pin_0, R3.Pin_0, R4.Pin_0, R5.Pin_0, IC4.pin14, IC5.pin14, R6.Pin_0
  N1: IC1.Trigger, IC1.Threshold, C1.+, R2b.leg1, R2b.wiper
  ASTABLE: IC1.Output, IC4.pin1
  N2: IC1.Control_Voltage, C2.1
  N3: IC1.Discharge, R1.Pin_1, R2a.Pin_0
  N4: IC2.Trigger, R3.Pin_1, S1.leg1
  MONOSTABLE: IC2.Output, IC4.pin9
  N5: IC2.Control_Voltage, C4.1
  N6: IC2.Threshold, IC2.Discharge, R2.Pin_1, C3.+
  N7: IC3.Trigger, R4.Pin_1, S2.L2
  SELECT: IC3.Output, IC4.pin2, IC4.pin12, IC4.pin13
  N8: IC3.Reset, R5.Pin_1, S2.L1
  N9: IC3.Control_Voltage, C5.1
  N10: R2b.leg2, R2a.Pin_1
  N11: IC4.pin3, IC4.pin4
  N12: IC4.pin5, IC4.pin8
  N13: IC4.pin6, IC5.pin5
  N14: IC4.pin10, IC4.pin11
  N15: IC5.pin1, IC5.pin2, S3.COM
  N16: IC5.pin3, IC5.pin4
  N17: IC5.pin6, IC5.pin9, IC5.pin10
  CLOCK_OUT: IC5.pin8, LED1.anode
  N18: S3.L1, R6.Pin_1
  N19: LED1.cathode, R7.Pin_1

notes:
  CLOCK_OUT
