# Fritzing sketch DoorbellKit (saved by Fritzing 0.9.2b)
breadboards: 1

parts:
  6V = Power plug
  U1 = 555 Timer [package="DIP8 [THT]"]
  D1 = Rectifier Diode [part_number=1N4148 package="300 mil [THT]"]
  D2 = Rectifier Diode [part_number=1N4148 package="300 mil [THT]"]
  R1 = Resistor [tolerance=±5% resistance=47k package=THT]
  R2 = Resistor [tolerance=±5% resistance=47k package=THT]
  R3 = Resistor [tolerance=±5% resistance=47k package=THT]
  R4 = Resistor [tolerance=±5% resistance=47k package=THT]
  C4 = Ceramic Capacitor [capacitance=100nF package="100 mil [THT, multilayer]"]
  C2 = Ceramic Capacitor [capacitance=100nF package="100 mil [THT, multilayer]"]
  C3 = Ceramic Capacitor [capacitance=100nF package="100 mil [THT, multilayer]"]
  C1 = Electrolytic Capacitor [capacitance=10µF package="100 mil [THT, electrolytic]"]
  C5 = Electrolytic Capacitor [capacitance=100µF package="100 mil [THT, electrolytic]"]
  SPKR1 = Loudspeaker
  S1 = Pushbutton [package="[THT]"]

nets:
  GND: 6V.GND, U1.Ground, R4.Pin_1, C4.0, C2.0, C3.0, C1.-, SPKR1.pin2
  VCC: 6V.VCC, U1.Vcc_Supply_Voltage, R1.Pin_1, C4.1, S1.Pin_3, S1.Pin_4
  CH1: U1.Trigger, U1.Threshold, R3.Pin_1, C2.1
  CH3: U1.Output, C5.+
  CH2: U1.Reset, D1.cathode, R4.Pin_0, C1.+
  N1: U1.Control_Voltage, C3.1
  N2: U1.Discharge, R2.Pin_0, R3.Pin_0
  N3: D1.anode, D2.anode, S1.Pin_1, S1.Pin_2
  N4: D2.cathode, R1.Pin_0, R2.Pin_1
  N5: C5.-, SPKR1.pin1
