# Fritzing sketch DoorbellKit2 (saved by Fritzing 1.0.1rc)
breadboards: 1

parts:
  Power = Power plug
  U1 = 555 Timer [package="DIP8 [THT]"]
  C1 = Ceramic Capacitor [capacitance=100nF voltage=35V package="100 mil [THT, multilayer]"]
  D1 = Rectifier Diode [part_number=1N4148 package="300 mil [THT]"]
  Q1 = NPN-Transistor [part_number=S9013 package="TO92 [THT]"]
  C2 = Ceramic Capacitor [capacitance=10nF voltage=35V package="100 mil [THT, multilayer]"]
  S1 = Pushbutton [package="[THT]"]
  R1 = Resistor [tolerance=±5% power=0.25W resistance=47k package=THT]
  D2 = Rectifier Diode [part_number=1N4001 package="300 mil [THT]"]
  R2 = Resistor [tolerance=±5% power=0.25W resistance=47k package=THT]
  R3 = Resistor [tolerance=±5% power=0.25W resistance=47k package=THT]
  R4 = Resistor [tolerance=±5% power=0.25W resistance=47k package=THT]
  D3 = Rectifier Diode [part_number=1N4001 package="300 mil [THT]"]
  C3 = Ceramic Capacitor [capacitance=100nF voltage=35V package="100 mil [THT, multilayer]"]
  C4 = Electrolytic Capacitor [capacitance=10µF voltage=35V package="100 mil [THT, electrolytic]"]
  SPKR1 = Loudspeaker

nets:
  GND: Power.GND, U1.Ground, C1.0, C2.1, R4.Pin_1, C3.0, C4.-, SPKR1.pin1
  5V: Power.VCC, U1.Vcc_Supply_Voltage, C1.1, Q1.C, S1.Pin_3, S1.Pin_4, R1.Pin_1
  N1: U1.Trigger, U1.Threshold, C2.0, R3.Pin_1
  N2: U1.Output, D1.anode
  RESET: U1.Reset, R4.Pin_0, D3.cathode, C4.+
  N3: U1.Control_Voltage, C3.1
  N4: U1.Discharge, R2.Pin_1, R3.Pin_0
  N5: D1.cathode, Q1.B
  N6: Q1.E, SPKR1.pin2
  N7: S1.Pin_1, S1.Pin_2, D2.anode, D3.anode
  N8: R1.Pin_0, D2.cathode, R2.Pin_0
