# Fritzing sketch DualModeVariableFrequencyOrDuty (saved by Fritzing 0.9.2b)
breadboards: 1

parts:
  S1 = Toggle Switch [package=THT]
  VR1 = Trimmer Potentiometer [maximum_resistance=50kΩ package=THT]
  U1 = 555 Timer [package="DIP8 [THT]"]
  C1 = Electrolytic Capacitor [capacitance=10µF package="100 mil [THT, electrolytic]"]
  R1 = Resistor [tolerance=±5% resistance=2k package=THT]
  Q1 = PNP-Transistor [part_number=2N3906 package="TO92 [THT]"]
  C2 = Ceramic Capacitor [capacitance=100nF package="100 mil [THT, multilayer]"]
  5V = Power plug
  Q2 = NPN-Transistor [part_number=2N3904 package="TO92 [THT]"]
  R2 = Resistor [tolerance=±5% resistance=2k package=THT]
  R3 = Resistor [tolerance=±5% resistance=10k package=THT]
  R4 = Resistor [tolerance=±5% resistance=6.8k package=THT]
  LED1 = LED - 3mm [color="Red (633nm)" package="3 mm [THT]"]
  R5 = Resistor [tolerance=±5% resistance=220 package=THT]

nets:
  N1: S1.L1, VR1.leg2
  N2: S1.COM, R2.Pin_0
  N3: S1.L2, VR1.leg1, R1.Pin_0
  N4: VR1.wiper, U1.Trigger, U1.Threshold, C1.+
  GND: U1.Ground, C1.-, C2.0, 5V.GND, R4.Pin_0, LED1.cathode
  OUT: U1.Output, Q2.B, R5.Pin_0
  VCC: U1.Reset, U1.Vcc_Supply_Voltage, Q1.E, 5V.VCC, R3.Pin_1
  N5: U1.Control_Voltage, C2.1
  N6: U1.Discharge, R1.Pin_1
  N7: Q1.B, Q2.C, R3.Pin_0
  N8: Q1.C, R2.Pin_1
  N9: Q2.E, R4.Pin_1
  N10: LED1.anode, R5.Pin_1
