# Fritzing sketch USBlinky (saved by Fritzing 0.9.2b)
breadboards: 1

parts:
  S1 = Toggle Switch [package=THT]
  VR1 = Trimmer Potentiometer [maximum_resistance=50kΩ package=THT]
  U1 = 555 Timer [package="DIP8 [THT]"]
  C1 = Electrolytic Capacitor [capacitance=10µF package="100 mil [THT, electrolytic]"]
  R1 = Resistor [tolerance=±5% resistance=2k package=THT]
  Q1 = PNP-Transistor [part_number=2N3906 package="TO92 [THT]"]
  C2 = Ceramic Capacitor [capacitance=100nF package="100 mil [THT, multilayer]"]
  5V = Power plug
  Q2 = NPN-Transistor [part_number=2N3904 package="TO92 [THT]"]
  R2 = Resistor [tolerance=±5% resistance=2k package=THT]
  R3 = Resistor [tolerance=±5% resistance=10k package=THT]
  R4 = Resistor [tolerance=±5% resistance=6.8k package=THT]
  LED1 = LED - 3mm [color="Blue (430nm)" package="3 mm [THT]"]
  R5 = Resistor [tolerance=±5% resistance=100 package=THT]
  LED2 = LED - 3mm [color="Blue (430nm)" package="3 mm [THT]"]
  LED3 = LED - 3mm [color="Blue (430nm)" package="3 mm [THT]"]
  LED4 = LED - 3mm [color="Blue (430nm)" package="3 mm [THT]"]
  R6 = Resistor [tolerance=±5% resistance=100 package=THT]
  R7 = Resistor [tolerance=±5% resistance=100 package=THT]
  R8 = Resistor [tolerance=±5% resistance=100 package=THT]
  Q3 = Basic FET N-Channel [part_number=2N7000 package="TO220 [THT]"]

nets:
  N1: S1.L1, VR1.leg2
  N2: S1.COM, R2.Pin_0
  N3: S1.L2, VR1.leg1, R1.Pin_0
  N4: VR1.wiper, U1.Trigger, U1.Threshold, C1.+
  GND: U1.Ground, C1.-, C2.0, 5V.GND, R4.Pin_0, Q3.source
  OUT: U1.Output, Q2.B, Q3.gate
  VCC: U1.Reset, U1.Vcc_Supply_Voltage, Q1.E, 5V.VCC, R3.Pin_1, R5.Pin_0, R6.Pin_0, R7.Pin_0, R8.Pin_0
  N5: U1.Control_Voltage, C2.1
  N6: U1.Discharge, R1.Pin_1
  N7: Q1.B, Q2.C, R3.Pin_0
  N8: Q1.C, R2.Pin_1
  N9: Q2.E, R4.Pin_1
  N10: LED1.cathode, LED2.cathode, LED3.cathode, LED4.cathode, Q3.drain
  N11: LED1.anode, R5.Pin_1
  N12: LED2.anode, R6.Pin_1
  N13: LED3.anode, R7.Pin_1
  N14: LED4.anode, R8.Pin_1
