# Fritzing sketch KnightRider (saved by Fritzing 0.9.2b)
breadboards: 1

parts:
  U1 = 555 Timer [package="SO8 [SMD]"]
  IC2 = IC, DIP package, 16 pins [chip_label=CD4017 part_number=CD4017]
  R1 = Resistor [tolerance=±5% resistance=1k package=THT]
  R2 = Resistor [tolerance=±5% resistance=68k package=THT]
  C1 = Electrolytic Capacitor [capacitance=1µF package="100 mil [THT, electrolytic]"]
  9V = Power plug
  C2 = Ceramic Capacitor [capacitance=100nF package="100 mil [THT, multilayer]"]
  LED1 = LED - 5mm [color="Red (633nm)" package="5 mm [THT]"]
  LED2 = LED - 5mm [color="Red (633nm)" package="5 mm [THT]"]
  LED3 = LED - 5mm [color="Red (633nm)" package="5 mm [THT]"]
  LED4 = LED - 5mm [color="Red (633nm)" package="5 mm [THT]"]
  LED5 = LED - 5mm [color="Red (633nm)" package="5 mm [THT]"]
  R7 = Resistor [tolerance=±5% resistance=220 package=THT]
  R6 = Resistor [tolerance=±5% resistance=220 package=THT]
  R5 = Resistor [tolerance=±5% resistance=220 package=THT]
  LED6 = LED - 5mm [color="Red (633nm)" package="5 mm [THT]"]
  R4 = Resistor [tolerance=±5% resistance=220 package=THT]
  R3 = Resistor [tolerance=±5% resistance=220 package=THT]
  R8 = Resistor [tolerance=±5% resistance=220 package=THT]
  D1 = Rectifier Diode [part_number=1N4148 package="300 mil [THT]"]
  D2 = Rectifier Diode [part_number=1N4148 package="300 mil [THT]"]
  D3 = Rectifier Diode [part_number=1N4148 package="300 mil [THT]"]
  D4 = Rectifier Diode [part_number=1N4148 package="300 mil [THT]"]
  D5 = Rectifier Diode [part_number=1N4148 package="300 mil [THT]"]
  D6 = Rectifier Diode [part_number=1N4148 package="300 mil [THT]"]
  D7 = Rectifier Diode [part_number=1N4148 package="300 mil [THT]"]
  D8 = Rectifier Diode [part_number=1N4148 package="300 mil [THT]"]

nets:
  GND: U1.Pin_1, IC2.pin8, IC2.pin13, IC2.pin15, C1.-, 9V.GND, C2.0, LED1.cathode, LED2.cathode, LED3.cathode, LED4.cathode, LED5.cathode, LED6.cathode
  N1: U1.Pin_2, U1.Pin_6, R2.Pin_1, C1.+
  CLK: U1.Pin_3, IC2.pin14
  N2: U1.Pin_4, U1.Pin_8, IC2.pin16, R1.Pin_0, 9V.VCC
  N3: U1.Pin_5, C2.1
  N4: U1.Pin_7, R1.Pin_1, R2.Pin_0
  Q5: IC2.pin1, R3.Pin_0
  Q1: IC2.pin2, D8.anode
  Q0: IC2.pin3, R8.Pin_0
  Q2: IC2.pin4, D6.anode
  Q6: IC2.pin5, D1.anode
  Q7: IC2.pin6, D3.anode
  Q3: IC2.pin7, D4.anode
  Q8: IC2.pin9, D5.anode
  Q4: IC2.pin10, D2.anode
  Q9: IC2.pin11, D7.anode
  N5: LED1.anode, R3.Pin_1
  N6: LED2.anode, R4.Pin_1
  N7: LED3.anode, R5.Pin_1
  N8: LED4.anode, R6.Pin_1
  N9: LED5.anode, R7.Pin_1
  N10: R7.Pin_0, D7.cathode, D8.cathode
  N11: R6.Pin_0, D5.cathode, D6.cathode
  N12: R5.Pin_0, D3.cathode, D4.cathode
  N13: LED6.anode, R8.Pin_1
  N14: R4.Pin_0, D1.cathode, D2.cathode
