# Fritzing sketch LaserRay (saved by Fritzing 0.9.2b)
breadboards: 1

parts:
  5V = Power plug
  U1 = 555 Timer [package="DIP8 [THT]"]
  LED1 = LED - 5mm [color="White (4500K)" package="5 mm [THT]"]
  R1 = Resistor [tolerance=±5% resistance=220k package=THT]
  C1 = Ceramic Capacitor [capacitance=100nF package="100 mil [THT, multilayer]"]
  C2 = Electrolytic Capacitor [capacitance=10µF package="100 mil [THT, electrolytic]"]
  R2 = Resistor [tolerance=±5% resistance=470 package=THT]
  R3 = Resistor [tolerance=±5% resistance=10k package=THT]
  R4 = Resistor [tolerance=±5% resistance=2.2k package=THT]
  J1 = Piezo Speaker
  JP1 = USB_MICROB_PLUG [package=micro-b-smt]
  S1 = Pushbutton [package=THT]

nets:
  GND: 5V.GND, U1.Ground, C1.1, R4.Pin_1, JP1.GND
  VCC: 5V.VCC, U1.Reset, U1.Vcc_Supply_Voltage, R3.Pin_0, J1.pin1, S1.leg1
  N1: U1.Trigger, U1.Threshold, R1.Pin_0, C1.0
  N2: U1.Output, R1.Pin_1, C2.+, R2.Pin_0
  N3: U1.Control_Voltage, LED1.anode
  N4: LED1.cathode, R2.Pin_1
  N5: C2.-, R3.Pin_1, R4.Pin_0, J1.pin2
  N6: JP1.VCC, S1.leg0
