# Fritzing sketch Latch (saved by Fritzing 0.9.2b)
breadboards: 1

parts:
  Power_(~5-12V) = Power plug
  U1 = 555 Timer [package="DIP8 [THT]"]
  R1 = Resistor [tolerance=±5% resistance=22k package=THT]
  R2 = Resistor [tolerance=±5% resistance=22k package=THT]
  R3 = Resistor [tolerance=±5% resistance=100k package=THT]
  C1 = Electrolytic Capacitor [capacitance=1µF package="100 mil [THT, electrolytic]"]
  S1 = Pushbutton [package="[THT]"]
  LED1 = LED - 5mm [color="Red (633nm)" package="5 mm [THT]"]
  RL = Resistor [tolerance=±5% resistance=1k package=THT]

nets:
  GND: Power_(~5-12V).GND, U1.Ground, R2.Pin_1, C1.-, RL.Pin_1
  VCC: Power_(~5-12V).VCC, U1.Reset, U1.Vcc_Supply_Voltage, R1.Pin_0
  N1: U1.Trigger, U1.Threshold, R1.Pin_1, R2.Pin_0, S1.Pin_3, S1.Pin_4
  N2: U1.Output, R3.Pin_1, LED1.anode
  N3: R3.Pin_0, C1.+, S1.Pin_1, S1.Pin_2
  N4: LED1.cathode, RL.Pin_0
