# Fritzing sketch LedCube (saved by Fritzing 1.0.7)
breadboards: 1

parts:
  U1 = 555 Timer [package="DIP8 [THT]"]
  12V = Power plug
  C1 = Electrolytic Capacitor [capacitance=10µF voltage=35V package="100 mil [THT, electrolytic]"]
  R2 = Resistor [tolerance=±5% power=0.25W resistance=10k package=THT]
  LED7a = LED - 3mm [color="White (8000K)" current=0.030A package="3 mm [THT]"]
  LED6a = LED - 3mm [color="White (8000K)" current=0.030A package="3 mm [THT]"]
  LED5a = LED - 3mm [color="White (8000K)" current=0.030A package="3 mm [THT]"]
  U2 = IC, DIP package, 16 pins [chip_label=CD4020]
  LED4a = LED - 3mm [color="White (8000K)" current=0.030A package="3 mm [THT]"]
  LED8a = LED - 3mm [color="White (8000K)" current=0.030A package="3 mm [THT]"]
  LED9a = LED - 3mm [color="White (8000K)" current=0.030A package="3 mm [THT]"]
  LED10a = LED - 3mm [color="White (8000K)" current=0.030A package="3 mm [THT]"]
  LED11a = LED - 3mm [color="White (8000K)" current=0.030A package="3 mm [THT]"]
  LED12a = LED - 3mm [color="White (8000K)" current=0.030A package="3 mm [THT]"]
  LED12b = LED - 3mm [color="White (8000K)" current=0.030A package="3 mm [THT]"]
  LED12c = LED - 3mm [color="White (8000K)" current=0.030A package="3 mm [THT]"]
  LED11b = LED - 3mm [color="White (8000K)" current=0.030A package="3 mm [THT]"]
  LED11c = LED - 3mm [color="White (8000K)" current=0.030A package="3 mm [THT]"]
  LED10b = LED - 3mm [color="White (8000K)" current=0.030A package="3 mm [THT]"]
  LED10c = LED - 3mm [color="White (8000K)" current=0.030A package="3 mm [THT]"]
  LED9b = LED - 3mm [color="White (8000K)" current=0.030A package="3 mm [THT]"]
  LED9c = LED - 3mm [color="White (8000K)" current=0.030A package="3 mm [THT]"]
  LED8b = LED - 3mm [color="White (8000K)" current=0.030A package="3 mm [THT]"]
  LED8c = LED - 3mm [color="White (8000K)" current=0.030A package="3 mm [THT]"]
  LED7b = LED - 3mm [color="White (8000K)" current=0.030A package="3 mm [THT]"]
  LED7c = LED - 3mm [color="White (8000K)" current=0.030A package="3 mm [THT]"]
  LED6b = LED - 3mm [color="White (8000K)" current=0.030A package="3 mm [THT]"]
  LED6c = LED - 3mm [color="White (8000K)" current=0.030A package="3 mm [THT]"]
  LED5b = LED - 3mm [color="White (8000K)" current=0.030A package="3 mm [THT]"]
  LED5c = LED - 3mm [color="White (8000K)" current=0.030A package="3 mm [THT]"]
  LED4b = LED - 3mm [color="White (8000K)" current=0.030A package="3 mm [THT]"]
  LED4c = LED - 3mm [color="White (8000K)" current=0.030A package="3 mm [THT]"]

nets:
  GND: U1.Ground, 12V.GND, C1.-, U2.pin8, U2.pin11, LED12c.cathode, LED11c.cathode, LED10c.cathode, LED9c.cathode, LED8c.cathode, LED7c.cathode, LED6c.cathode, LED5c.cathode, LED4c.cathode
  N1: U1.Trigger, U1.Threshold, C1.+, R2.Pin_0
  CLK: U1.Output, R2.Pin_1, U2.pin10
  VDD: U1.Reset, U1.Vcc_Supply_Voltage, 12V.VCC, U2.pin16
  N2: LED7a.cathode, LED7b.anode
  Q7: LED7a.anode, U2.pin6
  N3: LED6a.cathode, LED6b.anode
  Q6: LED6a.anode, U2.pin4
  N4: LED5a.cathode, LED5b.anode
  Q5: LED5a.anode, U2.pin5
  Q12: U2.pin1, LED12a.anode
  Q4: U2.pin7, LED4a.anode
  Q9: U2.pin12, LED9a.anode
  Q8: U2.pin13, LED8a.anode
  Q10: U2.pin14, LED10a.anode
  Q11: U2.pin15, LED11a.anode
  N5: LED4a.cathode, LED4b.anode
  N6: LED8a.cathode, LED8b.anode
  N7: LED9a.cathode, LED9b.anode
  N8: LED10a.cathode, LED10b.anode
  N9: LED11a.cathode, LED11b.anode
  N10: LED12a.cathode, LED12b.anode
  N11: LED12b.cathode, LED12c.anode
  N12: LED11b.cathode, LED11c.anode
  N13: LED10b.cathode, LED10c.anode
  N14: LED9b.cathode, LED9c.anode
  N15: LED8b.cathode, LED8c.anode
  N16: LED7b.cathode, LED7c.anode
  N17: LED6b.cathode, LED6c.anode
  N18: LED5b.cathode, LED5c.anode
  N19: LED4b.cathode, LED4c.anode
