# Fritzing sketch LongRunning-TLC556 (saved by Fritzing 0.9.2b)
breadboards: 1

parts:
  Part1 = Arduino Uno (Rev3)
  5V = Power plug
  R1 = Resistor [tolerance=±5% resistance=10M package=THT]
  R2 = Resistor [tolerance=±5% resistance=1G package=THT]
  R3 = Resistor [tolerance=±5% resistance=100k package=THT]
  C1 = Ceramic Capacitor [capacitance=470nF package="100 mil [THT, multilayer]"]
  C2 = Ceramic Capacitor [capacitance=470nF package="100 mil [THT, multilayer]"]
  RL2 = Resistor [tolerance=±5% resistance=1k package=THT]
  LL2 = LED - 5mm [color="Red (633nm)" package="5 mm [THT]"]
  C3 = Ceramic Capacitor [capacitance=100nF package="100 mil [THT, multilayer]"]
  RL1 = Resistor [tolerance=±5% resistance=1k package=THT]
  LL1 = LED - 5mm [color="Red (633nm)" package="5 mm [THT]"]
  D1 = Rectifier Diode [part_number=1N4148 package="300 mil [THT]"]
  C4 = Ceramic Capacitor [capacitance=100nF package="100 mil [THT, multilayer]"]
  R4 = Resistor [tolerance=±5% resistance=10k package=THT]
  R5 = Resistor [tolerance=±5% resistance=10k package=THT]
  U1 = 556 [package=dil14]

nets:
  GND: Part1.GND, 5V.GND, C1.0, C2.0, LL2.cathode, C3.0, LL1.cathode, U1.GND
  OUT2/TRIGGER: Part1.D2, RL2.Pin_0, U1.OUT2
  5V: 5V.VCC, R1.Pin_0, R3.Pin_0, C3.1, R4.Pin_0, R5.Pin_0, U1.RST, U1.RST2, U1.VCC
  DIS1: R1.Pin_1, R2.Pin_0, U1.DIS
  THR1/TRG1: R2.Pin_1, C1.1, U1.THR, U1.TRIG
  DIS2/THR2: R3.Pin_1, C2.1, U1.THR2, U1.DIS2
  N1: RL2.Pin_1, LL2.anode
  OUT1: RL1.Pin_0, D1.cathode, U1.OUT
  N2: RL1.Pin_1, LL1.anode
  N3: D1.anode, C4.0, R4.Pin_1
  TRG2: C4.1, R5.Pin_1, U1.TRIG2
