# Fritzing sketch LongRunning (saved by Fritzing 0.9.2b)
breadboards: 1

parts:
  Part1 = Arduino Uno (Rev3)
  U2 = 555 Timer [package="DIP8 [THT]"]
  5V = Power plug
  U1 = 555 Timer [package="DIP8 [THT]"]
  R1 = Resistor [tolerance=±5% resistance=10M package=THT]
  R2 = Resistor [tolerance=±5% resistance=1G package=THT]
  R3 = Resistor [tolerance=±5% resistance=100k package=THT]
  C1 = Ceramic Capacitor [capacitance=470nF package="100 mil [THT, multilayer]"]
  C2 = Ceramic Capacitor [capacitance=470nF package="100 mil [THT, multilayer]"]
  RL2 = Resistor [tolerance=±5% resistance=1k package=THT]
  LL2 = LED - 5mm [color="Red (633nm)" package="5 mm [THT]"]
  C3 = Ceramic Capacitor [capacitance=100nF package="100 mil [THT, multilayer]"]
  RL1 = Resistor [tolerance=±5% resistance=1k package=THT]
  LL1 = LED - 5mm [color="Red (633nm)" package="5 mm [THT]"]
  D1 = Rectifier Diode [part_number=1N4148 package="300 mil [THT]"]
  C4 = Ceramic Capacitor [capacitance=100nF package="100 mil [THT, multilayer]"]
  R4 = Resistor [tolerance=±5% resistance=10k package=THT]
  R5 = Resistor [tolerance=±5% resistance=10k package=THT]

nets:
  GND: Part1.GND, U2.Ground, 5V.GND, U1.Ground, C1.0, C2.0, LL2.cathode, C3.0, LL1.cathode
  TRIGGER: Part1.D2, U2.Output, RL2.Pin_0
  N1: U2.Trigger, C4.1, R5.Pin_1
  5V: U2.Reset, U2.Vcc_Supply_Voltage, 5V.VCC, U1.Reset, U1.Vcc_Supply_Voltage, R1.Pin_0, R3.Pin_0, C3.1, R4.Pin_0, R5.Pin_0
  N2: U2.Threshold, U2.Discharge, R3.Pin_1, C2.1
  N3: U1.Trigger, U1.Threshold, R2.Pin_1, C1.1
  N4: U1.Output, RL1.Pin_0, D1.cathode
  N5: U1.Discharge, R1.Pin_1, R2.Pin_0
  N6: RL2.Pin_1, LL2.anode
  N7: RL1.Pin_1, LL1.anode
  N8: D1.anode, C4.0, R4.Pin_1
