# Fritzing sketch ML555-async (saved by Fritzing 1.0.7)
breadboards: 1

parts:
  U1 = 555 Timer [part_number=ML555 package="DIP8 [THT]"]
  5V = Power plug
  R1 = Resistor [tolerance=±5% power=0.25W resistance=10k package=THT]
  R2 = Resistor [tolerance=±5% power=0.25W resistance=330k package=THT]
  C1 = Electrolytic Capacitor [capacitance=22µF voltage=35V package="100 mil [THT, electrolytic]"]
  LED1 = LED - 3mm [color="Red (633nm)" current=0.030A package="3 mm [THT]"]
  R3 = Resistor [tolerance=±5% power=0.25W resistance=1k package=THT]
  C2 = Ceramic Capacitor [capacitance=100nF voltage=35V package="100 mil [THT, multilayer]"]

nets:
  GND: U1.Ground, 5V.GND, C1.-, R3.Pin_1, C2.0
  N1: U1.Trigger, U1.Threshold, R2.Pin_1, C1.+
  N2: U1.Output, LED1.anode
  N3: U1.Reset, U1.Vcc_Supply_Voltage, 5V.VCC, R1.Pin_0
  N4: U1.Control_Voltage, C2.1
  N5: U1.Discharge, R1.Pin_1, R2.Pin_0
  N6: LED1.cathode, R3.Pin_0
