# Fritzing sketch ML555 (saved by Fritzing 1.0.7)
breadboards: 1

parts:
  Power = Power plug
  Q1 = NPN-Transistor [part_number=2N3904 package="TO92 [THT]"]
  Q2 = NPN-Transistor [part_number=2N3904 package="TO92 [THT]"]
  Q3 = NPN-Transistor [part_number=2N3904 package="TO92 [THT]"]
  Q4 = NPN-Transistor [part_number=2N3904 package="TO92 [THT]"]
  Q5 = PNP-Transistor [part_number=2N3906 package="TO92 [THT]"]
  Q6 = PNP-Transistor [part_number=2N3906 package="TO92 [THT]"]
  Q7 = PNP-Transistor [part_number=2N3906 package="TO92 [THT]"]
  Q8 = PNP-Transistor [part_number=2N3906 package="TO92 [THT]"]
  Q9 = PNP-Transistor [part_number=2N3906 package="TO92 [THT]"]
  Q10 = PNP-Transistor [part_number=2N3906 package="TO92 [THT]"]
  Q11 = PNP-Transistor [part_number=2N3906 package="TO92 [THT]"]
  Q12 = PNP-Transistor [part_number=2N3906 package="TO92 [THT]"]
  Q13 = PNP-Transistor [part_number=2N3906 package="TO92 [THT]"]
  Q14 = NPN-Transistor [part_number=2N3904 package="TO92 [THT]"]
  Q15 = NPN-Transistor [part_number=2N3904 package="TO92 [THT]"]
  Q16 = NPN-Transistor [part_number=2N3904 package="TO92 [THT]"]
  Q17 = NPN-Transistor [part_number=2N3904 package="TO92 [THT]"]
  Q18 = NPN-Transistor [part_number=2N3904 package="TO92 [THT]"]
  Q19B = PNP-Transistor [part_number=2N3906 package="TO92 [THT]"]
  Q19A = PNP-Transistor [part_number=2N3906 package="TO92 [THT]"]
  Q20 = NPN-Transistor [part_number=2N3904 package="TO92 [THT]"]
  Q21 = NPN-Transistor [part_number=2N3904 package="TO92 [THT]"]
  Q22 = NPN-Transistor [part_number=2N3904 package="TO92 [THT]"]
  Q23 = PNP-Transistor [part_number=2N3906 package="TO92 [THT]"]
  Q24 = NPN-Transistor [part_number=2N3904 package="TO92 [THT]"]
  Q25 = PNP-Transistor [part_number=2N3906 package="TO92 [THT]"]
  R1 = Resistor [tolerance=±5% power=0.25W resistance=4.7k package=THT]
  R2 = Resistor [tolerance=±5% power=0.25W resistance=820 package=THT]
  R3 = Resistor [tolerance=±5% power=0.25W resistance=4.7k package=THT]
  R4 = Resistor [tolerance=±5% power=0.25W resistance=1k package=THT]
  R5 = Resistor [tolerance=±5% power=0.25W resistance=10k package=THT]
  R6 = Resistor [tolerance=±5% power=0.25W resistance=100k package=THT]
  R7 = Resistor [tolerance=±5% power=0.25W resistance=4.7k package=THT]
  R8 = Resistor [tolerance=±5% power=0.25W resistance=4.7k package=THT]
  R9 = Resistor [tolerance=±5% power=0.25W resistance=4.7k package=THT]
  R10 = Resistor [tolerance=±5% power=0.25W resistance=15k package=THT]
  R11 = Resistor [tolerance=±5% power=0.25W resistance=4.7k package=THT]
  R12 = Resistor [tolerance=±5% power=0.25W resistance=6.8k package=THT]
  R13 = Resistor [tolerance=±5% power=0.25W resistance=3.9k package=THT]
  R14 = Resistor [tolerance=±5% power=0.25W resistance=220 package=THT]
  R15 = Resistor [tolerance=±5% power=0.25W resistance=4.7k package=THT]
  R16 = Resistor [tolerance=±5% power=0.25W resistance=100 package=THT]
  R17 = Resistor [tolerance=±5% power=0.25W resistance=100k package=THT]
  2_TRIG = Multimeter straight red probe
  1_GND = Multimeter straight black probe
  5_CONT = Multimeter straight red probe
  7_DISCH = Multimeter straight red probe
  4_RESET = Multimeter straight red probe
  3_OUT = Multimeter straight red probe
  6_THRES = Multimeter straight red probe
  8_VCC = Multimeter straight red probe

nets:
  GND: Power.GND, Q7.C, Q10.C, Q12.C, Q13.C, Q14.E, Q15.E, Q16.E, Q17.E, Q24.E, R5.Pin_1, R6.Pin_1, R9.Pin_1, R15.Pin_1, 1_GND.Probe_tip
  9V: Power.VCC, Q19B.E, Q19A.E, Q21.C, Q22.C, R1.Pin_0, R2.Pin_0, R3.Pin_0, R4.Pin_0, R7.Pin_0, R12.Pin_0, 8_VCC.Probe_tip
  N1: Q1.E, Q2.B
  N2: Q1.B, 6_THRES.Probe_tip
  N3: Q1.C, Q2.C, Q5.B, Q5.C, Q6.B
  N4: Q2.E, Q3.E, R5.Pin_0
  N5: Q3.B, Q4.E
  N6: Q3.C, Q4.C, Q7.B, Q8.B, Q8.C
  N7: Q4.B, R7.Pin_1, R8.Pin_0, 5_CONT.Probe_tip
  N8: Q5.E, R1.Pin_1
  N9: Q6.E, Q7.E, R2.Pin_1
  N10: Q6.C, Q15.C, Q16.B, R11.Pin_1
  N11: Q8.E, R3.Pin_1
  N12: Q9.E, R4.Pin_1
  N13: Q9.B, Q19B.B, Q19B.C, Q19A.B, R10.Pin_0
  N14: Q9.C, Q11.E, Q12.E
  N15: Q10.E, Q11.B
  N16: Q10.B, 2_TRIG.Probe_tip
  N17: Q11.C, Q15.B, R6.Pin_0
  N18: Q12.B, Q13.E
  N19: Q13.B, R8.Pin_1, R9.Pin_0
  N20: Q14.B, Q25.C, R16.Pin_1
  N21: Q14.C, 7_DISCH.Probe_tip
  N22: Q16.C, Q17.B, Q18.E
  N23: Q17.C, Q19A.C, Q20.B, R11.Pin_0
  N24: Q18.B, Q18.C, Q25.E, R10.Pin_1
  N25: Q20.E, R14.Pin_0, R15.Pin_0, R16.Pin_0
  N26: Q20.C, Q21.B, Q23.B, Q23.C, R12.Pin_1
  N27: Q21.E, Q22.B, R13.Pin_0
  N28: Q22.E, Q23.E, Q24.C, R13.Pin_1, 3_OUT.Probe_tip
  N29: Q24.B, R14.Pin_1
  N30: Q25.B, R17.Pin_0
  N31: R17.Pin_1, 4_RESET.Probe_tip

notes:
  1. GND
  2. TRIG
  3. OUT
  4. RESET
  5. CONT
  6. THRES
  7. DISCH
  8. VCC
