# Fritzing sketch MissingPulseDetector (saved by Fritzing 1.0.1rc)
breadboards: 1

parts:
  Power = Power plug
  U1 = 555 Timer [package="DIP8 [THT]"]
  U2 = 555 Timer [package="DIP8 [THT]"]
  R1 = Resistor [tolerance=±5% power=0.25W resistance=330k package=THT]
  R2 = Resistor [tolerance=±5% power=0.25W resistance=47k package=THT]
  C1 = Electrolytic Capacitor [capacitance=1µF voltage=35V package="100 mil [THT, electrolytic]"]
  R5 = Resistor [tolerance=±5% power=0.25W resistance=330k package=THT]
  U3 = 4011 4 x 2 Input NAND Gate, single part [part_number=4011 package="DIP (Dual Inline) [THT]"]
  S1 = Pushbutton [package="[THT]"]
  LED1 = LED - 3mm [color="Red (633nm)" current=0.030A package="3 mm [THT]"]
  R3 = Resistor [tolerance=±5% power=0.25W resistance=470 package=THT]
  R4 = Resistor [tolerance=±5% power=0.25W resistance=10k package=THT]
  C2 = Electrolytic Capacitor [capacitance=4.7µF voltage=35V package="100 mil [THT, electrolytic]"]
  Q1 = PNP-Transistor [part_number=2N3906 package="TO92 [THT]"]
  LED2 = LED - 3mm [color="Red (633nm)" current=0.030A package="3 mm [THT]"]
  R6 = Resistor [tolerance=±5% power=0.25W resistance=470 package=THT]

nets:
  GND: Power.GND, U1.Ground, U2.Ground, C1.-, U3.GND, S1.Pin_3, S1.Pin_4, R3.Pin_1, C2.-, Q1.C
  5V: Power.VCC, U1.Reset, U1.Vcc_Supply_Voltage, U2.Reset, U2.Vcc_Supply_Voltage, R1.Pin_0, R5.Pin_0, U3.VDD, R4.Pin_0, R6.Pin_1
  N1: U1.Trigger, U1.Threshold, R2.Pin_1, C1.+
  CH2/PULSE_GEN: U1.Output, U3.A1, U3.B1, LED1.anode
  N2: U1.Discharge, R1.Pin_1, R2.Pin_0
  CH3/SIGNAL: U2.Trigger, U3.Q2, Q1.B
  CH1: U2.Output, LED2.cathode
  N3: U2.Threshold, U2.Discharge, R5.Pin_1, C2.+, Q1.E
  N4: U3.Q1, U3.A2
  N5: U3.B2, S1.Pin_1, S1.Pin_2, R4.Pin_1
  N6: LED1.cathode, R3.Pin_0
  N7: LED2.anode, R6.Pin_0
