# Fritzing sketch Monostable (saved by Fritzing 0.9.2b)
breadboards: 1

parts:
  U1 = 555 Timer [package="DIP8 [THT]"]
  RL = Resistor [tolerance=±5% resistance=1k package=THT]
  LED1 = LED - 5mm [color="Red (633nm)" package="5 mm [THT]"]
  C2 = Ceramic Capacitor [capacitance=100nF package="100 mil [THT, multilayer]"]
  R1 = Resistor [tolerance=±5% resistance=22k package=THT]
  C1 = Electrolytic Capacitor [capacitance=47µF package="100 mil [THT, electrolytic]"]
  UNO = Arduino Uno (Rev3)
  R2 = Resistor [tolerance=±5% resistance=1k package=THT]

nets:
  N1: U1.Ground, LED1.cathode, C2.1, C1.-, UNO.GND
  N2: U1.Trigger, R2.Pin_0
  N3: U1.Output, RL.Pin_0
  N4: U1.Reset, U1.Vcc_Supply_Voltage, R1.Pin_0, UNO.5V
  N5: U1.Control_Voltage, C2.0
  N6: U1.Threshold, U1.Discharge, R1.Pin_1, C1.+
  PROBE: RL.Pin_1, LED1.anode, UNO.A0
  N7: UNO.D2, R2.Pin_1
