# Fritzing sketch NixiePowerSupply (saved by Fritzing 0.9.2b)
breadboards: 1

parts:
  U1 = 555 Timer [package="DIP8 [THT]"]
  R1 = Resistor [tolerance=±5% resistance=10k package=THT]
  C1 = Electrolytic Capacitor [capacitance=470µF voltage=16V package="100 mil [THT, electrolytic]"]
  VCC1 = Battery block 9V
  R2 = Resistor [tolerance=±5% resistance=33k package=THT]
  Q1 = NPN-Transistor [part_number=2N3904 package="TO92 [THT]"]
  R3 = Resistor [tolerance=±5% resistance=1k package=THT]
  R4 = Resistor [tolerance=±5% resistance=10k package=THT]
  C2 = Ceramic Capacitor [capacitance=2.2nF package="100 mil [THT, multilayer]"]
  L1 = Inductor [inductance=100µH package="400 mil [THT]"]
  D1 = Rectifier Diode [part_number=FR107 package="300 mil [THT]"]
  C3 = Electrolytic Capacitor [capacitance=1µF voltage=450V package="100 mil [THT, electrolytic]"]
  NIXIE = Screw terminal - 2 pins [package=THT]
  R5 = Resistor [tolerance=±5% resistance=220k package=THT]
  R6 = Trimmer Potentiometer [maximum_resistance=2kΩ package=THT]
  R7 = Resistor [tolerance=±5% resistance=470 package=THT]
  D2 = Rectifier Diode [part_number=1N4148 package="300 mil [THT]"]
  Q2 = PNP-Transistor [part_number=2N3906 package="TO92 [THT]"]
  R8 = Resistor [tolerance=±5% resistance=1k package=THT]
  Q3 = Basic FET N-Channel [part_number=IRF730 package="TO220 [THT]"]
  R9 = Resistor [tolerance=±5% resistance=1k package=THT]
  C4 = Ceramic Capacitor [capacitance=470pF package="100 mil [THT, multilayer]"]

nets:
  GND: U1.Ground, C1.-, VCC1.-, Q1.E, C2.0, C3.-, NIXIE.pin2, R7.Pin_0, Q2.C, R8.Pin_0, Q3.source, C4.0
  N1: U1.Trigger, U1.Threshold, R4.Pin_1, C2.1
  CH3: U1.Output, D2.anode, Q2.B, R8.Pin_1
  N2: U1.Reset, U1.Vcc_Supply_Voltage, C1.+, VCC1.+, R2.Pin_0, R3.Pin_1, L1.pin_1
  N3: U1.Control_Voltage, R2.Pin_1, Q1.C
  N4: U1.Discharge, R3.Pin_0, R4.Pin_0
  CH1: R1.Pin_0, NIXIE.pin1
  CH2: R1.Pin_1, D1.cathode, C3.+, R5.Pin_1
  N5: Q1.B, R6.wiper
  N6: L1.pin_0, D1.anode, Q3.drain, R9.Pin_1
  N7: R5.Pin_0, R6.leg2
  N8: R6.leg1, R7.Pin_1
  N9: D2.cathode, Q2.E, Q3.gate
  N10: R9.Pin_0, C4.1
