# Fritzing sketch PrecisionVariableFrequencyFixedDuty (saved by Fritzing 1.0.1rc)
breadboards: 1

parts:
  U1 = 555 Timer [package="DIP8 [THT]"]
  LED1 = LED - 5mm [color="Red (660nm)" current=0.030A package="5 mm [THT]"]
  R1 = Resistor [tolerance=±5% resistance=1.5k power=0.25W package=THT]
  VR1 = Trimmer Potentiometer [maximum_resistance=100kΩ knob_status=50% power=0.5W package=THT]
  C1 = Electrolytic Capacitor [capacitance=3.3µF package="100 mil [THT, electrolytic]"]
  5V = Power plug
  VR2 = Trimmer Potentiometer [maximum_resistance=10kΩ knob_status=50% power=0.5W package=THT]
  C2 = Ceramic Capacitor [capacitance=100nF package="100 mil [THT, multilayer]"]

nets:
  GND: U1.Ground, C1.-, 5V.GND, VR2.leg1, C2.0
  CH2: U1.Trigger, U1.Threshold, VR1.leg1, VR1.wiper, C1.+
  CH3: U1.Output, VR1.leg2
  VCC: U1.Reset, U1.Vcc_Supply_Voltage, R1.Pin_0, 5V.VCC, VR2.leg2
  CH4: U1.Control_Voltage, VR2.wiper, C2.1
  CH1: U1.Discharge, LED1.cathode
  N1: LED1.anode, R1.Pin_1
