# Fritzing sketch PwmMotorControl (saved by Fritzing 0.9.2b)
breadboards: 1

parts:
  U1 = 555 Timer [package="SO8 [SMD]"]
  R1 = Resistor [tolerance=±5% resistance=1k package=THT]
  C2 = Ceramic Capacitor [capacitance="100 nF" package="0603 [SMD, multilayer]"]
  5V = Power plug
  D1 = Rectifier Diode [part_number=1N4148 package="300 mil [THT]"]
  D2 = Rectifier Diode [part_number=1N4148 package="300 mil [THT]"]
  R2 = Trimmer Potentiometer [maximum_resistance=100kΩ package=THT]
  R3 = Resistor [tolerance=±5% resistance=470 package=THT]
  M1 = DC Motor
  D3 = Rectifier Diode [part_number=1N4001 package="300 mil [THT]"]
  Q1 = Basic FET N-Channel [part_number=2N7000 package="TO220 [THT]"]
  C1 = Ceramic Capacitor [capacitance=470nF package="100 mil [THT, multilayer]"]

nets:
  GND: U1.Pin_1, C2.1, 5V.GND, Q1.source, C1.1
  CH2: U1.Pin_2, U1.Pin_6, R2.wiper, C1.0
  N1: U1.Pin_3, R3.Pin_0
  VCC: U1.Pin_4, U1.Pin_8, R1.Pin_0, 5V.VCC, M1.pin_2, D3.cathode
  N2: U1.Pin_5, C2.0
  N3: U1.Pin_7, R1.Pin_1, D1.anode, D2.cathode
  N4: D1.cathode, R2.leg2
  N5: D2.anode, R2.leg1
  N6: R3.Pin_1, Q1.gate
  N7: M1.pin_1, D3.anode, Q1.drain
