# Fritzing sketch RouletteKit (saved by Fritzing 0.9.2b)
breadboards: 1

parts:
  U1 = 555 Timer [package="DIP8 [THT]"]
  IC1 = IC, DIP package, 16 pins [chip_label=CD4017 part_number=CD4017]
  VCC1 = Battery block 9V
  D1 = Rectifier Diode [part_number=1N4001 package="300 mil [THT]"]
  Q1 = NPN-Transistor [part_number=9014 package="TO92 [THT]"]
  C1 = Electrolytic Capacitor [capacitance=47µF package="100 mil [THT, electrolytic]"]
  R1 = Resistor [tolerance=±5% resistance=470k package=THT]
  S1 = Pushbutton [package="[THT]"]
  R2 = Resistor [tolerance=±5% resistance=10k package=THT]
  R3 = Resistor [tolerance=±5% resistance=470k package=THT]
  C2 = Electrolytic Capacitor [capacitance=1µF package="100 mil [THT, electrolytic]"]
  LED1 = LED - 3mm [color="Red (633nm)" package="3 mm [THT]"]
  LED2 = LED - 3mm [color="Red (633nm)" package="3 mm [THT]"]
  LED8 = LED - 3mm [color="Red (633nm)" package="3 mm [THT]"]
  LED9 = LED - 3mm [color="Red (633nm)" package="3 mm [THT]"]
  LED10 = LED - 3mm [color="Red (633nm)" package="3 mm [THT]"]
  LED4 = LED - 3mm [color="Red (633nm)" package="3 mm [THT]"]
  LED3 = LED - 3mm [color="Red (633nm)" package="3 mm [THT]"]
  LED5 = LED - 3mm [color="Red (633nm)" package="3 mm [THT]"]
  LED6 = LED - 3mm [color="Red (633nm)" package="3 mm [THT]"]
  LED7 = LED - 3mm [color="Red (633nm)" package="3 mm [THT]"]

nets:
  N1: U1.Ground, IC1.pin8, IC1.pin12, IC1.pin13, VCC1.-, C1.-, R1.Pin_0, R3.Pin_0, C2.-, LED1.cathode, LED2.cathode, LED8.cathode, LED9.cathode, LED10.cathode, LED4.cathode, LED3.cathode, LED5.cathode, LED6.cathode, LED7.cathode
  N2: U1.Trigger, U1.Threshold, U1.Discharge, R2.Pin_0, R3.Pin_1, C2.+
  N3: U1.Output, IC1.pin14
  N4: U1.Reset, U1.Vcc_Supply_Voltage, IC1.pin16, D1.cathode, Q1.C, S1.Pin_3, S1.Pin_4
  N5: IC1.pin1, LED6.anode
  N6: IC1.pin2, LED2.anode
  N7: IC1.pin3, LED1.anode
  N8: IC1.pin4, LED3.anode
  N9: IC1.pin5, LED7.anode
  N10: IC1.pin6, LED8.anode
  N11: IC1.pin7, LED4.anode
  N12: IC1.pin9, LED9.anode
  N13: IC1.pin10, LED5.anode
  N14: IC1.pin11, LED10.anode
  N15: VCC1.+, D1.anode
  N16: Q1.E, R2.Pin_1
  N17: Q1.B, C1.+, R1.Pin_1, S1.Pin_1, S1.Pin_2
