# Fritzing sketch SRLatch (saved by Fritzing 0.9.2b)
breadboards: 1

parts:
  5-9V = Power plug
  U1 = 555 Timer [package="DIP8 [THT]"]
  SET = Pushbutton [package="[THT]"]
  RESET = Pushbutton [package="[THT]"]
  R3 = Resistor [tolerance=±5% resistance=1k package=THT]
  R1 = Resistor [tolerance=±5% resistance=10k package=THT]
  R2 = Resistor [tolerance=±5% resistance=10k package=THT]
  LED1(Q) = LED - 3mm [color="Green (555nm)" package="3 mm [THT]"]

nets:
  GND: 5-9V.GND, U1.Ground, U1.Threshold, SET.Pin_3, SET.Pin_4, RESET.Pin_3, RESET.Pin_4, LED1(Q).cathode
  VCC: 5-9V.VCC, U1.Vcc_Supply_Voltage, R1.Pin_0, R2.Pin_0
  N1: U1.Trigger, SET.Pin_1, SET.Pin_2, R1.Pin_1
  N2: U1.Output, R3.Pin_0
  N3: U1.Reset, RESET.Pin_1, RESET.Pin_2, R2.Pin_1
  N4: R3.Pin_1, LED1(Q).anode
