# Fritzing sketch Simple555Tester (saved by Fritzing 1.0.1rc)
breadboards: 1

parts:
  U1 = 555 Timer [package="SO8 [SMD]"]
  R3 = Resistor [tolerance=±5% resistance=470 power=0.25W package=THT]
  R1 = Resistor [tolerance=±5% resistance=1k power=0.25W package=THT]
  R2 = Resistor [tolerance=±5% resistance=150k power=0.25W package=THT]
  C1 = Electrolytic Capacitor [capacitance=10µF voltage=35V package="100 mil [THT, electrolytic]"]
  C2 = Ceramic Capacitor [capacitance="100 nF" package="0603 [SMD, multilayer]"]
  5-9V = Power plug
  S1 = Pushbutton [package="[THT]"]
  D1 = LED - 3mm [color="Green (555nm)" current=0.030A package="3 mm [THT]"]
  D2 = LED - 3mm [color="Green (555nm)" current=0.030A package="3 mm [THT]"]
  R4 = Resistor [tolerance=±5% resistance=470 power=0.25W package=THT]
  S2 = SWITCH-SP3T [package=switch-sp3t-smd]

nets:
  GND: U1.Pin_1, C1.-, C2.1, 5-9V.GND, R4.Pin_1, S2.4
  N1: U1.Pin_2, U1.Pin_6, R2.Pin_1, C1.+
  N2: U1.Pin_3, D1.cathode, D2.anode
  5V: U1.Pin_4, U1.Pin_8, R3.Pin_0, R1.Pin_0, S1.Pin_3, S1.Pin_4, S2.1
  CONTROL: U1.Pin_5, C2.0, S2.3
  N3: U1.Pin_7, R1.Pin_1, R2.Pin_0
  N4: R3.Pin_1, D1.anode
  N5: 5-9V.VCC, S1.Pin_1, S1.Pin_2
  N6: D2.cathode, R4.Pin_0
