# Fritzing sketch SimpleChime (saved by Fritzing 0.9.0b)
breadboards: 1

parts:
  U2 = 555 Timer [package="SO8 [SMD]"]
  U1 = 555 Timer [package="SO8 [SMD]"]
  R5 = Trimmer Potentiometer [maximum_resistance=100kΩ package=THT]
  VCC = Battery block 9V
  C2 = Ceramic Capacitor [capacitance=10nF package="100 mil [THT, multilayer]"]
  C1 = Electrolytic Capacitor [capacitance=33µF package="100 mil [THT, electrolytic]"]
  R1 = Resistor [tolerance=±5% resistance=4.7k package=THT]
  C4 = Ceramic Capacitor [capacitance=10nF package="100 mil [THT, multilayer]"]
  R3 = Resistor [tolerance=±5% resistance=1k package=THT]
  C3 = Ceramic Capacitor [capacitance=100nF package="100 mil [THT, multilayer]"]
  R2 = Resistor [tolerance=±5% resistance=10k package=THT]
  K1 = Piezo Speaker
  C5 = Electrolytic Capacitor [capacitance=100µF package="100 mil [THT, electrolytic]"]
  R4 = Resistor [tolerance=±5% resistance=10k package=THT]
  S2 = Pushbutton [package="[THT]"]

nets:
  N1: U2.Pin_1, U1.Pin_1, VCC.-, C2.0, C1.-, C4.0, C3.0, R2.Pin_1, K1.pin1, S2.Pin_1, S2.Pin_2
  N2: U2.Pin_2, U2.Pin_6, R5.wiper, C3.1
  N3: U2.Pin_3, C5.+
  N4: U2.Pin_4, U1.Pin_3, R2.Pin_0
  N5: U2.Pin_5, C4.1
  N6: U2.Pin_7, R5.leg2, R3.Pin_1
  N7: U2.Pin_8, U1.Pin_4, U1.Pin_8, VCC.+, R1.Pin_0, R3.Pin_0, R4.Pin_0
  N8: U1.Pin_2, R1.Pin_1, S2.Pin_3, S2.Pin_4
  N9: U1.Pin_5, C2.1
  N10: U1.Pin_6, U1.Pin_7, C1.+, R4.Pin_1
  N11: K1.pin2, C5.-
