# Fritzing sketch SimpleSiren (saved by Fritzing 1.0.1rc)
breadboards: 1

parts:
  U2 = 555 Timer [package="SO8 [SMD]"]
  U1 = 555 Timer [package="SO8 [SMD]"]
  RV2 = Trimmer Potentiometer [maximum_resistance=100kΩ knob_status=50% power=0.5W package=THT]
  VCC = Battery block 9V
  C3 = Ceramic Capacitor [capacitance=10nF package="100 mil [THT, multilayer]"]
  C1 = Electrolytic Capacitor [capacitance=47µF voltage=35V package="100 mil [THT, electrolytic]"]
  R2 = Resistor [tolerance=±5% resistance=2k power=0.25W package=THT]
  C2 = Ceramic Capacitor [capacitance=100nF voltage=35V package="100 mil [THT, multilayer]"]
  K1 = Piezo Speaker
  C4 = Electrolytic Capacitor [capacitance=1µF voltage=35V package="100 mil [THT, electrolytic]"]
  R1 = Resistor [tolerance=±5% resistance=2k power=0.25W package=THT]
  S1 = Pushbutton [package="[THT]"]
  RV1 = Trimmer Potentiometer [maximum_resistance=100kΩ knob_status=50% power=0.5W package=THT]
  R3 = Resistor [tolerance=±5% resistance=1k power=0.25W package=THT]
  C5 = Electrolytic Capacitor [capacitance=100µF voltage=35V package="100 mil [THT, electrolytic]"]
  C6 = Ceramic Capacitor [capacitance=100nF voltage=35V package="100 mil [THT, multilayer]"]

nets:
  GND: U2.Pin_1, U1.Pin_1, VCC.-, C3.0, C1.-, C2.0, K1.pin1, C5.-, C6.0
  N1: U2.Pin_2, U2.Pin_6, RV2.wiper, C2.1
  N2: U2.Pin_3, C4.+
  N3: U2.Pin_4, U2.Pin_8, U1.Pin_4, U1.Pin_8, R2.Pin_0, R1.Pin_0, S1.Pin_3, S1.Pin_4
  N4: U2.Pin_5, R3.Pin_1
  N5: U2.Pin_7, RV2.leg2, R2.Pin_1
  N6: U1.Pin_2, U1.Pin_6, C1.+, RV1.wiper
  N7: U1.Pin_3, R3.Pin_0
  N8: U1.Pin_5, C3.1
  N9: U1.Pin_7, R1.Pin_1, RV1.leg2
  N10: VCC.+, S1.Pin_1, S1.Pin_2, C5.+, C6.1
  N11: K1.pin2, C4.-
