# Fritzing sketch SlowGlow (saved by Fritzing 0.9.2b)
breadboards: 1

parts:
  U1 = 555 Timer [package="SO8 [SMD]"]
  LED1 = LED - 5mm [color="White (8000K)" package="5 mm [THT]"]
  R1 = Resistor [tolerance=±5% resistance=4.7k package=THT]
  R2 = Resistor [tolerance=±5% resistance=330k package=THT]
  C1 = Electrolytic Capacitor [capacitance=4.7µF package="100 mil [THT, electrolytic]"]
  C2 = Ceramic Capacitor [capacitance="100 nF" package="0603 [SMD, multilayer]"]
  5V = Power plug
  D1 = Rectifier Diode [part_number=1N4148 package="300 mil [THT]"]
  R3 = Resistor [tolerance=±5% resistance=470 package=THT]
  C3 = Electrolytic Capacitor [capacitance=220µF package="100 mil [THT, electrolytic]"]
  R4 = Resistor [tolerance=±5% resistance=470 package=THT]

nets:
  GND: U1.Pin_1, C1.-, C2.1, 5V.GND, C3.-, R4.Pin_1
  N1: U1.Pin_2, U1.Pin_6, R2.Pin_1, C1.+
  N2: U1.Pin_3, D1.anode
  N3: U1.Pin_4, U1.Pin_8, R1.Pin_0, 5V.VCC
  N4: U1.Pin_5, C2.0
  N5: U1.Pin_7, R1.Pin_1, R2.Pin_0
  N6: LED1.cathode, R4.Pin_0
  N7: LED1.anode, R3.Pin_1, C3.+
  N8: D1.cathode, R3.Pin_0
