# Fritzing sketch SlowGlow2 (saved by Fritzing 1.0.1rc)
breadboards: 1

parts:
  Power = Power plug
  Q1 = NPN-Transistor [part_number=2N3904 package="TO92 [THT]"]
  R1 = Resistor [tolerance=±5% power=0.25W resistance=33k package=THT]
  R2 = Resistor [tolerance=±5% power=0.25W resistance=220 package=THT]
  LED1 = LED - 5mm [color="Red (633nm)" current=0.030A package="5 mm [THT]"]
  C1 = Electrolytic Capacitor [capacitance=0.1mF voltage=35V package="100 mil [THT, electrolytic]"]
  U1 = 555 Timer [package="DIP8 [THT]"]

nets:
  GND: Power.GND, R2.Pin_1, C1.-, U1.Ground
  5V: Power.VCC, Q1.C, U1.Reset, U1.Vcc_Supply_Voltage
  CH3: Q1.E, LED1.anode
  CH2: Q1.B, R1.Pin_1, C1.+, U1.Trigger, U1.Threshold
  CH1: R1.Pin_0, U1.Output
  N1: R2.Pin_0, LED1.cathode
