# Fritzing sketch TickTock (saved by Fritzing 1.0.1rc)
breadboards: 1

parts:
  U4 = IC, DIP package, 14 pins [chip_label=74LS73]
  Power = Power plug
  U1 = 555 Timer [package="DIP8 [THT]"]
  R2 = 12mm Trimmer Potentiometer (Large) [maximum_resistance=10kΩ knob_status=50% power=0.5W package=THT]
  U2 = 555 Timer [package="DIP8 [THT]"]
  U3 = 555 Timer [package="DIP8 [THT]"]
  Q1 = Basic FET N-Channel [part_number=2N7000 package="TO220 [THT]"]
  R1 = Resistor [tolerance=±5% power=0.25W resistance=2k package=THT]
  C1 = Electrolytic Capacitor [capacitance=10µF voltage=35V package="100 mil [THT, electrolytic]"]
  C2 = Ceramic Capacitor [capacitance=100nF voltage=35V package="100 mil [THT, multilayer]"]
  R3 = Resistor [tolerance=±5% power=0.25W resistance=4.7k package=THT]
  R4 = Resistor [tolerance=±5% power=0.25W resistance=10k package=THT]
  C3 = Electrolytic Capacitor [capacitance=10µF voltage=35V package="100 mil [THT, electrolytic]"]
  R5 = Resistor [tolerance=±5% power=0.25W resistance=1k package=THT]
  R6 = Resistor [tolerance=±5% power=0.25W resistance=47k package=THT]
  R7 = Resistor [tolerance=±5% power=0.25W resistance=10k package=THT]
  C4 = Ceramic Capacitor [capacitance=100nF voltage=35V package="100 mil [THT, multilayer]"]
  C5 = Electrolytic Capacitor [capacitance=10µF voltage=35V package="100 mil [THT, electrolytic]"]
  J1 = Piezo Speaker
  C6 = Electrolytic Capacitor [capacitance=100µF voltage=35V package="100 mil [THT, electrolytic]"]

nets:
  TICK: U4.pin1, U2.Output, U3.Control_Voltage
  5V: U4.pin2, U4.pin3, U4.pin4, U4.pin14, Power.VCC, U1.Reset, U1.Vcc_Supply_Voltage, U2.Reset, U2.Vcc_Supply_Voltage, U3.Reset, U3.Vcc_Supply_Voltage, R1.Pin_0, R3.Pin_0, R4.Pin_1, R5.Pin_0, C6.+
  GND: U4.pin11, Power.GND, U1.Ground, U2.Ground, U3.Ground, C1.-, C3.-, C4.0, J1.pin1, C6.-
  FNOTCH: U4.pin12, Q1.gate
  N1: U1.Trigger, U1.Threshold, R2.leg1, R2.wiper, C1.+
  CLOCK: U1.Output, C2.0
  N2: U1.Discharge, R2.leg2, R1.Pin_1
  N3: U2.Trigger, C2.1, R4.Pin_0
  N4: U2.Threshold, U2.Discharge, R3.Pin_1, C3.+
  N5: U3.Trigger, U3.Threshold, Q1.source, R7.Pin_0, C4.1
  AF: U3.Output, C5.+
  N6: U3.Discharge, R5.Pin_1, R6.Pin_1
  N7: Q1.drain, R6.Pin_0, R7.Pin_1
  N8: C5.-, J1.pin2
