# Fritzing sketch TouchSwitch (saved by Fritzing 0.9.2b)
breadboards: 1

parts:
  5-15V = Power plug
  U1 = 555 Timer [package="DIP8 [THT]"]
  R1 = Resistor [tolerance=±5% resistance=100k package=THT]
  C1 = Electrolytic Capacitor [capacitance=10µF package="100 mil [THT, electrolytic]"]
  C2 = Ceramic Capacitor [capacitance=10nF package="100 mil [THT, multilayer]"]
  R3 = Resistor [tolerance=±5% resistance=1k package=THT]
  LED1 = LED - 3mm [color="Green (555nm)" package="3 mm [THT]"]

nets:
  GND/TOUCH-: 5-15V.GND, U1.Ground, C1.-, C2.1, LED1.cathode
  N1: 5-15V.VCC, U1.Reset, U1.Vcc_Supply_Voltage, R1.Pin_0
  TOUCH+: U1.Trigger
  N2: U1.Output, R3.Pin_0
  N3: U1.Control_Voltage, C2.0
  N4: U1.Threshold, U1.Discharge, R1.Pin_1, C1.+
  N5: R3.Pin_1, LED1.anode

notes:
  Touch Pad
