# Fritzing sketch TriangleWaveGen (saved by Fritzing 0.9.0b)
breadboards: 1

parts:
  U1 = 555 Timer [package="SO8 [SMD]"]
  R1 = Resistor [tolerance=±5% resistance=1k package=THT]
  R2 = Resistor [tolerance=±5% resistance=22k package=THT]
  C1 = Electrolytic Capacitor [capacitance=33µF package="100 mil [THT, electrolytic]"]
  C2 = Ceramic Capacitor [capacitance="100 nF" package="0603 [SMD, multilayer]"]
  Uno = Arduino Uno (Rev3)
  R3a = Resistor [tolerance=±5% resistance=10k package=THT]
  C3a = Electrolytic Capacitor [capacitance=10µF package="100 mil [THT, electrolytic]"]
  R3b = Resistor [tolerance=±5% resistance=220 package=THT]
  C3b = Electrolytic Capacitor [capacitance=10µF package="100 mil [THT, electrolytic]"]

nets:
  N1: U1.Pin_1, C1.-, C2.0, Uno.GND, C3a.-, C3b.-
  N2: U1.Pin_2, U1.Pin_6, R2.Pin_1, C1.+
  N3: U1.Pin_3, Uno.A0, R3a.Pin_0
  N4: U1.Pin_4, U1.Pin_8, R1.Pin_0, Uno.5V
  N5: U1.Pin_5, C2.1
  N6: U1.Pin_7, R1.Pin_1, R2.Pin_0
  N7: Uno.A1, C3a.+, R3b.Pin_1, C3b.+
  N8: R3a.Pin_1, R3b.Pin_0
