# Fritzing sketch TwoToneDoorbell (saved by Fritzing 0.9.2b)
breadboards: 1

parts:
  U1 = 555 Timer [package="SO8 [SMD]"]
  VCC1 = Battery block 9V
  R1 = Resistor [tolerance=±5% resistance=47k package=THT]
  D1 = Rectifier Diode [part_number=1N4001 package="300 mil [THT]"]
  D2 = Rectifier Diode [part_number=1N4001 package="300 mil [THT]"]
  D3 = Rectifier Diode [part_number=1N4001 package="300 mil [THT]"]
  R5 = Resistor [tolerance=±5% resistance=220k package=THT]
  C4 = Electrolytic Capacitor [capacitance=10µF package="100 mil [THT, electrolytic]"]
  R2 = Resistor [tolerance=±5% resistance=47k package=THT]
  R3 = Resistor [tolerance=±5% resistance=47k package=THT]
  C1 = Ceramic Capacitor [capacitance=33nF package="100 mil [THT, multilayer]"]
  J1 = Piezo Speaker
  C3 = Electrolytic Capacitor [capacitance=100µF package="100 mil [THT, electrolytic]"]
  R4 = Resistor [tolerance=±5% resistance=22k package=THT]
  C2 = Electrolytic Capacitor [capacitance=10µF package="100 mil [THT, electrolytic]"]
  S1 = Pushbutton [package="[THT]"]
  C5 = Ceramic Capacitor [capacitance=100nF package="100 mil [THT, multilayer]"]
  C6 = Ceramic Capacitor [capacitance=100nF package="100 mil [THT, multilayer]"]
  Q2 = 2N7000 FET N-Channel [part_number=2N7000 package=TO92]

nets:
  N1: U1.Pin_1, C1.1, J1.pin1, R4.Pin_1, C2.-, Q2.drain
  N2: U1.Pin_2, U1.Pin_6, R3.Pin_1, C1.0
  N3: U1.Pin_3, C3.+
  N4: U1.Pin_4, D2.cathode, R4.Pin_0, C2.+
  N5: U1.Pin_5, C5.0
  N6: U1.Pin_7, R2.Pin_1, R3.Pin_0
  N7: U1.Pin_8, VCC1.+, R1.Pin_0, S1.Pin_1, S1.Pin_2, C6.1
  GND: VCC1.-, R5.Pin_1, C4.-, C5.1, C6.0, Q2.source
  N8: R1.Pin_1, D1.cathode, R2.Pin_0
  N9: D1.anode, D2.anode, D3.anode, S1.Pin_3, S1.Pin_4
  N10: D3.cathode, R5.Pin_0, C4.+, Q2.gate
  N11: J1.pin2, C3.-

custom parts:
  2N7000 FET N-Channel: A 2N7000 MOSFET N-Channel Transistor
