# Fritzing sketch UpsideDown (saved by Fritzing 1.0.7)
breadboards: 1

parts:
  U1 = 555 Timer [package="DIP8 [THT]"]
  Power = Power plug
  R2 = 12mm Trimmer Potentiometer (Large) [maximum_resistance=10kΩ knob_status=50% power=0.5W package=THT]
  D1 = Rectifier Diode [part_number=1N5819 package="300 mil [THT]"]
  R1 = Resistor [tolerance=±5% power=0.25W resistance=40k package=THT]
  LED1 = LED - 3mm [color="Red (633nm)" current=0.030A package="3 mm [THT]"]
  R3 = Resistor [tolerance=±5% power=0.25W resistance=1k package=THT]
  C1 = Ceramic Capacitor [capacitance=100nF voltage=35V package="100 mil [THT, multilayer]"]
  CH1 = Multimeter straight red probe
  CH2 = Multimeter straight red probe

nets:
  GND: U1.Ground, Power.GND, R1.Pin_0, LED1.cathode
  N1: U1.Trigger, U1.Threshold, D1.cathode, R1.Pin_1, C1.1, CH2.Probe_tip_2
  OUT: U1.Output, R2.wiper, R2.leg2, R3.Pin_0, CH1.Probe_tip_2
  9V: U1.Reset, U1.Vcc_Supply_Voltage, Power.VCC, C1.0
  N2: R2.leg1, D1.anode
  N3: LED1.anode, R3.Pin_1

notes:
  CH1
  CH2
