# Fritzing sketch ControlAdjust (saved by Fritzing 0.9.2b)
breadboards: 1

parts:
  U1 = 555 Timer [package="SO8 [SMD]"]
  R3 = Resistor [tolerance=±5% resistance=1k package=THT]
  R1 = Resistor [tolerance=±5% resistance=4.7k package=THT]
  5-9V = Power plug
  LED1 = LED - 3mm [color="Blue (430nm)" package="3 mm [THT]"]
  C1 = Electrolytic Capacitor [capacitance=1µF package="100 mil [THT, electrolytic]"]
  R6 = Trimmer Potentiometer [maximum_resistance=100kΩ package=THT]
  R2 = Resistor [tolerance=±5% resistance=47k package=THT]
  R4 = Resistor [tolerance=±5% resistance=4.7k package=THT]
  R5 = Resistor [tolerance=±5% resistance=4.7k package=THT]

nets:
  GND: U1.Pin_1, 5-9V.GND, LED1.cathode, C1.-, R5.Pin_1
  CH2: U1.Pin_2, U1.Pin_6, C1.+, R2.Pin_1
  CH1: U1.Pin_3, R3.Pin_0
  VCC: U1.Pin_4, U1.Pin_8, R1.Pin_0, 5-9V.VCC, R4.Pin_1
  N1: U1.Pin_5, R6.wiper
  N2: U1.Pin_7, R1.Pin_1, R2.Pin_0
  N3: R3.Pin_1, LED1.anode
  N4: R6.leg1, R4.Pin_0
  N5: R6.leg2, R5.Pin_0
