# Fritzing sketch DiodeSteering (saved by Fritzing 0.9.2b)
breadboards: 1

parts:
  U1 = 555 Timer [package="SO8 [SMD]"]
  R3 = Resistor [tolerance=±5% resistance=1k package=THT]
  R1 = Resistor [tolerance=±5% resistance=4.7k package=THT]
  C2 = Ceramic Capacitor [capacitance="100 nF" package="0603 [SMD, multilayer]"]
  5-9V = Power plug
  LED1 = LED - 3mm [color="Blue (430nm)" package="3 mm [THT]"]
  D1 = Rectifier Diode [part_number=1N4148 package="300 mil [THT]"]
  D2 = Rectifier Diode [part_number=1N4148 package="300 mil [THT]"]
  C1 = Electrolytic Capacitor [capacitance=1µF package="100 mil [THT, electrolytic]"]
  R2 = Trimmer Potentiometer [maximum_resistance=100kΩ package=THT]

nets:
  GND: U1.Pin_1, C2.1, 5-9V.GND, LED1.cathode, C1.-
  CH2: U1.Pin_2, U1.Pin_6, C1.+, R2.wiper
  CH1: U1.Pin_3, R3.Pin_0
  VCC: U1.Pin_4, U1.Pin_8, R1.Pin_0, 5-9V.VCC
  N1: U1.Pin_5, C2.0
  N2: U1.Pin_7, R1.Pin_1, D1.anode, D2.cathode
  N3: R3.Pin_1, LED1.anode
  N4: D1.cathode, R2.leg2
  N5: D2.anode, R2.leg1
