# Fritzing sketch VariableDutyCycle (saved by Fritzing 0.9.2b)
breadboards: 1

parts:
  U1 = 555 Timer [package="SO8 [SMD]"]
  R3 = Resistor [tolerance=±5% resistance=1k package=THT]
  R1 = Resistor [tolerance=±5% resistance=1k package=THT]
  R2 = Resistor [tolerance=±5% resistance=10k package=THT]
  C2 = Ceramic Capacitor [capacitance="100 nF" package="0603 [SMD, multilayer]"]
  5-9V = Power plug
  R2a = Rotary Potentiometer (Small) [maximum_resistance=50kΩ package=THT]
  R1a = Rotary Potentiometer (Small) [maximum_resistance=50kΩ package=THT]
  R2b = Resistor [tolerance=±5% resistance=50k package=THT]
  LED1 = LED - 3mm [color="Green (555nm)" package="3 mm [THT]"]
  C1 = Ceramic Capacitor [capacitance=10nF package="100 mil [THT, multilayer]"]

nets:
  GND: U1.Pin_1, C2.1, 5-9V.GND, LED1.cathode, C1.0
  N1: U1.Pin_2, U1.Pin_6, R2.Pin_1, C1.1
  N2: U1.Pin_3, R3.Pin_0
  N3: U1.Pin_4, U1.Pin_8, R1.Pin_0, 5-9V.VCC
  N4: U1.Pin_5, C2.0
  N5: U1.Pin_7, R2a.wiper, R1a.wiper, R2b.Pin_1
  PROBEA: R3.Pin_1, LED1.anode
  N6: R1.Pin_1, R1a.leg2
  N7: R2.Pin_0, R2a.leg1, R2b.Pin_0

notes:
  R1a and R2a are a linked dual-pole pot
