# Fritzing sketch VoltageControlledOscillator (saved by Fritzing 0.9.2b)
breadboards: 1

parts:
  U1 = 555 Timer [package="SO8 [SMD]"]
  R3 = Resistor [tolerance=±5% resistance=1k package=THT]
  LED1 = LED - 5mm [color="Red (633nm)" package="5 mm [THT]"]
  R1 = Resistor [tolerance=±5% resistance=10k package=THT]
  R2 = Resistor [tolerance=±5% resistance=330k package=THT]
  C2 = Ceramic Capacitor [capacitance="100 nF" package="0603 [SMD, multilayer]"]
  9V = Power plug
  C1 = Ceramic Capacitor [capacitance=100nF package="100 mil [THT, multilayer]"]
  RV = Trimmer Potentiometer [maximum_resistance=10kΩ package=THT]
  C3 = Ceramic Capacitor [capacitance=10nF package="100 mil [THT, multilayer]"]

nets:
  GND: U1.Pin_1, LED1.cathode, C2.1, 9V.GND, C1.0, RV.leg2, C3.1
  CH2(B): U1.Pin_2, U1.Pin_6, R2.Pin_1, C1.1
  CH1(Y): U1.Pin_3, R3.Pin_0
  VCC: U1.Pin_4, U1.Pin_8, R1.Pin_0, 9V.VCC, RV.leg1, C3.0
  CH3(R): U1.Pin_5, C2.0, RV.wiper
  N1: U1.Pin_7, R1.Pin_1, R2.Pin_0
  N2: R3.Pin_1, LED1.anode
