# Fritzing sketch VoltageDoublerChargePump (saved by Fritzing 0.9.2b)
breadboards: 1

parts:
  U1 = 555 Timer [part_number=NE555P package="SO8 [SMD]"]
  R1 = Resistor [tolerance=±5% resistance=10k package=THT]
  R2 = Resistor [tolerance=±5% resistance=47k package=THT]
  C2 = Ceramic Capacitor [capacitance="100 nF" package="0603 [SMD, multilayer]"]
  9V = Power plug
  C1 = Ceramic Capacitor [capacitance=1nF package="100 mil [THT, multilayer]"]
  CF = Electrolytic Capacitor [capacitance=1µF voltage=50V package="100 mil [THT, electrolytic]"]
  D1 = Rectifier Diode [part_number=1N5819 package="300 mil [THT]"]
  D2 = Rectifier Diode [part_number=1N5819 package="300 mil [THT]"]
  CL = Electrolytic Capacitor [capacitance=1µF voltage=50V package="100 mil [THT, electrolytic]"]
  RL = Resistor [tolerance=±5% resistance=10k package=THT]

nets:
  GND/PROBEB: U1.Pin_1, C2.1, 9V.GND, C1.0, CL.-, RL.Pin_1
  N1: U1.Pin_2, U1.Pin_6, R2.Pin_1, C1.1
  N2: U1.Pin_3, CF.-
  N3: U1.Pin_4, U1.Pin_8, R1.Pin_0, 9V.VCC, D1.anode
  N4: U1.Pin_5, C2.0
  N5: U1.Pin_7, R1.Pin_1, R2.Pin_0
  N6: CF.+, D1.cathode, D2.anode
  PROBEA: D2.cathode, CL.+, RL.Pin_0
