# Fritzing sketch RelaxationOscillator (saved by Fritzing 1.0.1rc)
breadboards: 1

parts:
  U1 = 74HC04_HEX_INVERTER [part_number=74HC04 package=dil14]
  5V = Power plug
  Q1 = Basic FET N-Channel [part_number=2N7000 package="TO220 [THT]"]
  R1 = Resistor [tolerance=±5% power=0.25W resistance=1k package=THT]
  C1 = Ceramic Capacitor [capacitance=100nF voltage=35V package="100 mil [THT, multilayer]"]
  R2 = Resistor [tolerance=±5% power=0.25W resistance=1k package=THT]
  LED1 = LED - 3mm [color="Red (633nm)" current=0.030A package="3 mm [THT]"]
  R3 = Resistor [tolerance=±5% power=0.25W resistance=470 package=THT]

nets:
  N1: U1.1A, U1.2Y, R1.Pin_1
  OUT: U1.1Y, C1.1, R2.Pin_0
  N2: U1.2A, R1.Pin_0, C1.0
  GND: U1.3A, U1.GND, U1.4A, U1.5A, U1.6A, 5V.GND, Q1.source
  VCC: U1.VCC, 5V.VCC, R3.Pin_1
  N3: Q1.gate, R2.Pin_1
  N4: Q1.drain, LED1.cathode
  N5: LED1.anode, R3.Pin_0
