# Fritzing sketch VoltageMultiplier (saved by Fritzing 1.0.1rc)
breadboards: 1

parts:
  IC1 = Hex Inverter Schmitt Trigger SN74HC14 [package="DIP (Dual Inline)"]
  5V = Power plug
  C1 = Ceramic Capacitor [capacitance=100nF voltage=35V package="100 mil [THT, multilayer]"]
  R1 = Resistor [tolerance=±5% power=0.25W resistance=1k package=THT]
  D1 = Rectifier Diode [part_number=1N4148 package="300 mil [THT]"]
  C2 = Ceramic Capacitor [capacitance=330nF voltage=35V package="100 mil [THT, multilayer]"]
  D2 = Rectifier Diode [part_number=1N4148 package="300 mil [THT]"]
  C3 = Ceramic Capacitor [capacitance=330nF voltage=35V package="100 mil [THT, multilayer]"]
  D3 = Rectifier Diode [part_number=1N4148 package="300 mil [THT]"]
  C4 = Ceramic Capacitor [capacitance=330nF voltage=35V package="100 mil [THT, multilayer]"]
  D4 = Rectifier Diode [part_number=1N4148 package="300 mil [THT]"]
  C5 = Ceramic Capacitor [capacitance=330nF voltage=35V package="100 mil [THT, multilayer]"]
  D5 = Rectifier Diode [part_number=1N4148 package="300 mil [THT]"]
  C6 = Electrolytic Capacitor [capacitance=33µF voltage=400V package="100 mil [THT, electrolytic]"]
  LED1 = LED - 3mm [color="Yellow (574nm)" current=0.030A package="3 mm [THT]"]
  R2 = Resistor [tolerance=±5% power=0.25W resistance=10k package=THT]

nets:
  N1: IC1.1A, C1.1, R1.Pin_0
  1Y: IC1.1Y, IC1.2A, R1.Pin_1, C2.0
  2Y: IC1.2Y, IC1.3A, C3.0
  3Y: IC1.3Y, IC1.6A, C4.0
  GND: IC1.GND, IC1.4A, IC1.5A, 5V.GND, C1.0, C6.-, R2.Pin_1
  6Y: IC1.6Y, C5.0
  VCC: IC1.VCC, 5V.VCC, D1.anode
  N2: D1.cathode, C2.1, D2.anode
  N3: D2.cathode, C3.1, D3.anode
  N4: D3.cathode, C4.1, D4.anode
  N5: D4.cathode, C5.1, D5.anode
  OUT: D5.cathode, C6.+, LED1.anode
  N6: LED1.cathode, R2.Pin_0
