# Fritzing sketch QuadNOR (saved by Fritzing 1.0.7)
breadboards: 1

parts:
  Part1 = Arduino Uno (Rev3)
  IC1 = 74LS02 [package=dil14]
  LED1 = LED - 3mm [color="Blue (430nm)" current=0.030A package="3 mm [THT]"]
  LED2 = LED - 3mm [color="Green (555nm)" current=0.030A package="3 mm [THT]"]
  LED3 = LED - 3mm [color="Yellow (595nm)" current=0.030A package="3 mm [THT]"]
  R1 = Resistor [tolerance=±5% resistance=1k power=0.25W package=THT]
  R2 = Resistor [tolerance=±5% resistance=1k power=0.25W package=THT]
  R3 = Resistor [tolerance=±5% resistance=1k power=0.25W package=THT]
  IC2 = IC, DIP package, 14 pins [chip_label=74LS08]
  5V = Power plug

nets:
  B1: Part1.D8, IC1.B1
  A1: Part1.D9_PWM, IC1.A1
  B2: Part1.D6_PWM, IC1.B2
  A2: Part1.D7, IC1.A2
  GND: Part1.GND, IC1.GND, R1.Pin_0, R2.Pin_0, R3.Pin_0, IC2.pin7, 5V.GND
  AB1: IC1.Y1, LED2.anode, IC2.pin1
  AB2: IC1.Y2, LED3.anode, IC2.pin2
  Vcc: IC1.VCC, IC2.pin14, 5V.VCC
  N1: LED1.cathode, R3.Pin_1
  Y1: LED1.anode, IC2.pin3
  N2: LED2.cathode, R2.Pin_1
  N3: LED3.cathode, R1.Pin_1

custom parts:
  74LS02: 74LS02 Quad 2-input NOR
