# Fritzing sketch SchmittOscillator (saved by Fritzing 1.0.1rc)
breadboards: 1

parts:
  R1 = Resistor [tolerance=±5% resistance=1k power=0.25W package=THT]
  5V = Power plug
  U1 = SN74LS14N [package="DIP14 [THT]"]
  C1 = Ceramic Capacitor [capacitance=100nF voltage=35V package="100 mil [THT, multilayer]"]
  R2 = Resistor [tolerance=±5% power=0.25W resistance=1k package=THT]
  R3 = Resistor [tolerance=±5% power=0.25W resistance=470 package=THT]
  Q2 = Basic FET N-Channel [package="DPak [SMD]"]
  LED1 = LED - 3mm [color="Red (633nm)" current=0.030A package="3 mm [THT]"]

nets:
  OUT: R1.Pin_0, U1.1Y, U1.2A
  IN: R1.Pin_1, U1.1A, C1.1
  GND: 5V.GND, U1.3A, U1.GND, U1.4A, U1.5A, U1.6A, C1.0, Q2.source
  VCC: 5V.VCC, U1.VCC, LED1.anode
  INDICATOR: U1.2Y, R2.Pin_0
  N1: R2.Pin_1, Q2.Gate
  N2: R3.Pin_0, Q2.drain
  N3: R3.Pin_1, LED1.cathode

notes:
  OUT
