# Fritzing sketch BinaryCounter (saved by Fritzing 1.0.1rc)
breadboards: 1

parts:
  IC2 = IC, DIP package, 16 pins [chip_label=74LS161]
  5V = Power plug
  R1 = Resistor [tolerance=±5% power=0.25W resistance=4.7k package=THT]
  LED1 = LED - 3mm [color="Red (633nm)" current=0.030A package="3 mm [THT]"]
  R2 = Resistor [tolerance=±5% power=0.25W resistance=1k package=THT]
  LED2 = LED - 3mm [color="Red (633nm)" current=0.030A package="3 mm [THT]"]
  R3 = Resistor [tolerance=±5% power=0.25W resistance=1k package=THT]
  LED3 = LED - 3mm [color="Red (633nm)" current=0.030A package="3 mm [THT]"]
  R4 = Resistor [tolerance=±5% power=0.25W resistance=1k package=THT]
  LED4 = LED - 3mm [color="Red (633nm)" current=0.030A package="3 mm [THT]"]
  R5 = Resistor [tolerance=±5% power=0.25W resistance=1k package=THT]

nets:
  N1: IC2.pin1, R1.Pin_0
  CLK: IC2.pin2
  5V: IC2.pin7, IC2.pin9, IC2.pin10, IC2.pin16, 5V.VCC, R1.Pin_1
  GND: IC2.pin8, 5V.GND, R2.Pin_0, R3.Pin_0, R4.Pin_0, R5.Pin_0
  N2: IC2.pin11, LED4.anode
  N3: IC2.pin12, LED3.anode
  N4: IC2.pin13, LED2.anode
  N5: IC2.pin14, LED1.anode
  N6: LED1.cathode, R2.Pin_1
  N7: LED2.cathode, R3.Pin_1
  N8: LED3.cathode, R4.Pin_1
  N9: LED4.cathode, R5.Pin_1

notes:
  CLK
