# Fritzing sketch FullCycle (saved by Fritzing 1.0.1rc)
breadboards: 1

parts:
  IC1 = IC, DIP package, 16 pins [chip_label=74LS161]
  5V = Power plug
  IC2 = IC, DIP package, 16 pins [chip_label=74LS47]
  R1 = Resistor [tolerance=±5% power=0.25W resistance=4.7k package=THT]
  7_Segment_CA = 7 Segment Display
  R2 = Resistor [tolerance=±5% power=0.25W resistance=220 package=THT]
  LED1 = LED - 3mm [color="Red (633nm)" current=0.030A package="3 mm [THT]"]
  R3 = Resistor [tolerance=±5% power=0.25W resistance=4.7k package=THT]
  12V = Power plug

nets:
  N1: IC1.pin1, R1.Pin_0
  CLK: IC1.pin2
  5V: IC1.pin7, IC1.pin9, IC1.pin10, IC1.pin16, 5V.VCC, IC2.pin3, IC2.pin16, R1.Pin_1
  GND: IC1.pin8, 5V.GND, IC2.pin8, R3.Pin_0, 12V.GND
  N2: IC1.pin11, IC2.pin6
  N3: IC1.pin12, IC2.pin2
  N4: IC1.pin13, IC2.pin1
  N5: IC1.pin14, IC2.pin7
  E: IC2.pin9, 7_Segment_CA.Segment_C
  D: IC2.pin10, 7_Segment_CA.Segment_D
  C: IC2.pin11, 7_Segment_CA.Segment_E
  B: IC2.pin12, 7_Segment_CA.Segment_F
  A: IC2.pin13, 7_Segment_CA.Segment_A
  G: IC2.pin14, 7_Segment_CA.Segment_G
  F: IC2.pin15, 7_Segment_CA.Segment_B
  N6: 7_Segment_CA.common_anode, R2.Pin_1
  12V: R2.Pin_0, LED1.anode, 12V.VCC
  N7: LED1.cathode, R3.Pin_1

notes:
  CLK
  5V
  12V
