# Fritzing sketch ClapSwitch (saved by Fritzing 1.0.1rc)
breadboards: 1

parts:
  U2 = IC, DIP package, 14 pins [chip_label=74LS74]
  U1 = 555 Timer [package="DIP8 [THT]"]
  Power = Power plug
  C1 = Electrolytic Capacitor [capacitance=4.7µF voltage=35V package="100 mil [THT, electrolytic]"]
  R1 = Resistor [tolerance=±5% power=0.25W resistance=10k package=THT]
  Q1 = NPN-Transistor [part_number=2N3904 package="TO92 [THT]"]
  MIC1 = Microphone
  R2 = Resistor [tolerance=±5% power=0.25W resistance=47k package=THT]
  R3 = Resistor [tolerance=±5% power=0.25W resistance=100k package=THT]
  C2 = Ceramic Capacitor [capacitance=100nF voltage=35V package="100 mil [THT, multilayer]"]
  LED1 = LED - 3mm [color="Red (633nm)" current=0.030A package="3 mm [THT]"]
  R4 = Resistor [tolerance=±5% power=0.25W resistance=1k package=THT]
  C3 = Electrolytic Capacitor [capacitance=10µF voltage=35V package="100 mil [THT, electrolytic]"]
  R5 = Resistor [tolerance=±5% power=0.25W resistance=1k package=THT]
  S1 = Pushbutton [package="[THT]"]
  R6 = Resistor [tolerance=±5% power=0.25W resistance=10k package=THT]

nets:
  N1: U2.pin1, S1.Pin_1, S1.Pin_2, R6.Pin_0
  N2: U2.pin2, U2.pin6
  PULSE: U2.pin3, U1.Output
  5V: U2.pin4, U2.pin14, U1.Reset, U1.Vcc_Supply_Voltage, Power.VCC, R1.Pin_1, R2.Pin_1, R3.Pin_1, R6.Pin_1
  INDICATOR: U2.pin5, LED1.anode
  GND: U2.pin7, U1.Ground, Power.GND, C1.-, Q1.E, MIC1.pin1, C2.1, R4.Pin_1, S1.Pin_3, S1.Pin_4
  TRIGGER: U1.Trigger, Q1.C, R2.Pin_0
  N3: U1.Control_Voltage, C2.0
  N4: U1.Threshold, U1.Discharge, C1.+, R3.Pin_0
  N5: R1.Pin_0, MIC1.pin2, C3.+
  N6: Q1.B, R5.Pin_1
  N7: LED1.cathode, R4.Pin_0
  N8: C3.-, R5.Pin_0
