# Fritzing sketch QuadLatch (saved by Fritzing 0.9.0b)
breadboards: 1

parts:
  IC1 = 74LS75 [package=dil16]
  R4 = Resistor [tolerance=±5% resistance=4.7k package=THT]
  LED4 = LED - 5mm [color="Red (633nm)" package="5 mm [THT]"]
  LED3 = LED - 5mm [color="Red (633nm)" package="5 mm [THT]"]
  LED2 = LED - 5mm [color="Red (633nm)" package="5 mm [THT]"]
  R3 = Resistor [tolerance=±5% resistance=4.7k package=THT]
  R2 = Resistor [tolerance=±5% resistance=4.7k package=THT]
  R1 = Resistor [tolerance=±5% resistance=4.7k package=THT]
  LED1 = LED - 5mm [color="Red (633nm)" package="5 mm [THT]"]
  Part1 = Arduino Uno (Rev3)

nets:
  N1: IC1.D1, Part1.D6_PWM
  N2: IC1.D2, Part1.D5_PWM
  N3: IC1.E3-4, IC1.E1-2, Part1.D2
  VCC: IC1.VCC, Part1.5V
  N4: IC1.D3, Part1.D4
  N5: IC1.D4, Part1.D3_PWM
  N6: IC1.Q4, LED4.anode, Part1.A3
  N7: IC1.Q3, LED3.anode, Part1.A2
  GND: IC1.GND, R4.Pin_1, R3.Pin_1, R2.Pin_1, R1.Pin_1, Part1.GND
  N8: IC1.Q2, LED2.anode, Part1.A1
  N9: IC1.Q1, LED1.anode, Part1.A0
  N10: R4.Pin_0, LED4.cathode
  N11: LED3.cathode, R3.Pin_0
  N12: LED2.cathode, R2.Pin_0
  N13: R1.Pin_0, LED1.cathode

custom parts:
  74LS75: 74LS75 Quad Latch, 4-bit latch
