# Fritzing sketch LTC2400_ADR4540_opax388_buffered (saved by Fritzing 0.9.2b)
breadboards: 1

parts:
  IC2 = IC, DIP package, 8 pins [chip_label=2400 part_number=LTC2400]
  R3 = Resistor [tolerance=±5% resistance=10k package=THT]
  R4 = Resistor [tolerance=±5% resistance=10k package=THT]
  Part1 = Arduino Uno (Rev3)
  C5 = Electrolytic Capacitor [capacitance=100µF package="100 mil [THT, electrolytic]"]
  C4 = Ceramic Capacitor [capacitance=10nF package="100 mil [THT, multilayer]"]
  L2 = Inductor [inductance=47µH package="400 mil [THT]"]
  C6 = Ceramic Capacitor [capacitance=100nF package="100 mil [THT, multilayer]"]
  IC3 = Dual Op-Amp [part_number=OPA2388 package=dip08]
  R6 = Resistor [tolerance=±5% resistance=1M package=THT]
  IC4 = Dual Op-Amp [part_number=OPA2388 package=dip08]
  R7 = Resistor [tolerance=±5% resistance=100k package=THT]
  C7 = Ceramic Capacitor [capacitance=10nF package="100 mil [THT, multilayer]"]
  C8 = Ceramic Capacitor [capacitance=10nF package="100 mil [THT, multilayer]"]
  IC1 = IC, DIP package, 8 pins [chip_label=4540 part_number=ADR4540]
  C9 = Ceramic Capacitor [capacitance=100nF package="100 mil [THT, multilayer]"]
  C10 = Electrolytic Capacitor [capacitance=1µF package="100 mil [THT, electrolytic]"]
  C11 = Ceramic Capacitor [capacitance=100nF package="100 mil [THT, multilayer]"]

nets:
  Vcc: IC2.pin1, IC2.pin8, R3.Pin_1, R4.Pin_1, C5.+, C4.1, L2.pin_1, C6.1, IC3.A_V+, IC4.A_V+, C7.1, C8.1, IC1.pin2, C10.+, C11.1
  VREF_BUFF: IC2.pin2, IC3.A_OUT, IC3.A_-IN
  VIN_BUFF: IC2.pin3, IC4.A_OUT, IC4.A_-IN
  GND: IC2.pin4, Part1.GND, C5.-, C4.0, C6.0, IC3.A_V-, IC4.A_V-, R7.Pin_1, C7.0, C8.0, IC1.pin4, C9.0, C10.-, C11.0
  CS: IC2.pin5, R4.Pin_0, Part1.D10_PWM/SS
  SDO: IC2.pin6, Part1.D12/MISO
  SCK: IC2.pin7, R3.Pin_0, Part1.D13/SCK
  N1: Part1.5V, L2.pin_0
  VREF: IC3.A_+IN, IC3.B_+IN, IC1.pin6, C9.1
  VREF_ALT: IC3.B_-IN, IC3.B_OUT
  N2: R6.Pin_0, IC4.A_+IN, R7.Pin_0
  VIN: R6.Pin_1

notes:
  VREF ALT
  VIN
