# Fritzing sketch LTC2400_baseline (saved by Fritzing 0.9.2b)
breadboards: 1

parts:
  IC2 = IC, DIP package, 8 pins [chip_label=2400 part_number=LTC2400]
  IC1 = IC, DIP package, 8 pins [chip_label=1019 part_number=LT1019]
  R5 = Resistor [tolerance=±5% resistance=5 package=THT]
  C2 = Electrolytic Capacitor [capacitance=2.2µF package="100 mil [THT, electrolytic]"]
  R3 = Resistor [tolerance=±5% resistance=10k package=THT]
  R4 = Resistor [tolerance=±5% resistance=10k package=THT]
  R2 = Resistor [tolerance=±5% resistance=100k package=THT]
  R1 = Resistor [tolerance=±5% resistance=1M package=THT]
  Part1 = Arduino Uno (Rev3)
  C4 = Electrolytic Capacitor [capacitance=100µF package="100 mil [THT, electrolytic]"]
  C1 = Ceramic Capacitor [capacitance=10nF package="100 mil [THT, multilayer]"]
  C3 = Ceramic Capacitor [capacitance=10nF package="100 mil [THT, multilayer]"]
  L1 = Inductor [inductance=47µH package="400 mil [THT]"]
  C5 = Ceramic Capacitor [capacitance=100nF package="100 mil [THT, multilayer]"]
  C6 = Electrolytic Capacitor [capacitance=10µF part_number=optional package="100 mil [THT, electrolytic]"]

nets:
  Vcc: IC2.pin1, IC2.pin8, IC1.pin2, R3.Pin_1, R4.Pin_1, C4.+, C1.1, C3.1, L1.pin_1, C5.1
  VREF: IC2.pin2, IC1.pin6, R5.Pin_0
  N1: IC2.pin3, R2.Pin_0, R1.Pin_1, C6.+
  GND: IC2.pin4, IC1.pin4, C2.-, R2.Pin_1, Part1.GND, C4.-, C1.0, C3.0, C5.0, C6.-
  CS: IC2.pin5, R4.Pin_0, Part1.D10_PWM/SS
  SDO: IC2.pin6, Part1.D12/MISO
  SCK: IC2.pin7, R3.Pin_0, Part1.D13/SCK
  N2: R5.Pin_1, C2.+
  VIN: R1.Pin_0
  N3: Part1.5V, L1.pin_0

notes:
  VIN (30V max)
