# Fritzing sketch LTC2400_buffered (saved by Fritzing 0.9.2b)
breadboards: 1

parts:
  IC2 = IC, DIP package, 8 pins [chip_label=2400 part_number=LTC2400]
  IC1 = IC, DIP package, 8 pins [chip_label=1019 part_number=LT1019]
  R5 = Resistor [tolerance=±5% resistance=5 package=THT]
  C2 = Electrolytic Capacitor [capacitance=2.2µF package="100 mil [THT, electrolytic]"]
  R3 = Resistor [tolerance=±5% resistance=10k package=THT]
  R4 = Resistor [tolerance=±5% resistance=10k package=THT]
  R2 = Resistor [tolerance=±5% resistance=100k package=THT]
  R1 = Resistor [tolerance=±5% resistance=1M package=THT]
  Part1 = Arduino Uno (Rev3)
  C5 = Electrolytic Capacitor [capacitance=100µF package="100 mil [THT, electrolytic]"]
  C3 = Ceramic Capacitor [capacitance=10nF package="100 mil [THT, multilayer]"]
  C4 = Ceramic Capacitor [capacitance=10nF package="100 mil [THT, multilayer]"]
  IC3 = LM324 [part_number=LMV324 package=dil16]
  L2 = Inductor [inductance=47µH package="400 mil [THT]"]
  C6 = Ceramic Capacitor [capacitance=100nF package="100 mil [THT, multilayer]"]

nets:
  Vcc: IC2.pin1, IC2.pin8, IC1.pin2, R3.Pin_1, R4.Pin_1, C5.+, C3.1, C4.1, IC3.V+, L2.pin_1, C6.1
  VREF: IC2.pin2, IC1.pin6, R5.Pin_0, IC3.IN1+, IC3.IN2+
  N1: IC2.pin3, R2.Pin_0, R1.Pin_1
  GND: IC2.pin4, IC1.pin4, C2.-, R2.Pin_1, Part1.GND, C5.-, C3.0, C4.0, IC3.GND, C6.0
  CS: IC2.pin5, R4.Pin_0, Part1.D10_PWM/SS
  SDO: IC2.pin6, Part1.D12/MISO
  SCK: IC2.pin7, R3.Pin_0, Part1.D13/SCK
  N2: R5.Pin_1, C2.+
  VIN: R1.Pin_0
  N3: Part1.5V, L2.pin_0
  VREF_BUFFERED: IC3.OUT1, IC3.IN1-
  VREF_ALT: IC3.IN2-, IC3.OUT2

notes:
  VIN (30V max)

custom parts:
  LM324: LM324 Quad OpAmp
