# Fritzing sketch AsyncJKCounter (saved by Fritzing 0.9.2b)
breadboards: 1

parts:
  IC1 = IC, DIP package, 14 pins [chip_label=74LS73]
  IC2 = IC, DIP package, 14 pins [chip_label=74LS73]
  5V = Power plug
  U1 = 555 Timer [package="DIP8 [THT]"]
  C1 = Ceramic Capacitor [capacitance=100nF package="100 mil [THT, multilayer]"]
  R1 = Resistor [tolerance=±5% resistance=1k package=THT]
  R2 = Resistor [tolerance=±5% resistance=12k package=THT]
  C2 = Electrolytic Capacitor [capacitance=47µF package="100 mil [THT, electrolytic]"]
  R3 = Resistor [tolerance=±5% resistance=1k package=THT]
  LED1 = LED - 3mm [color="Red (633nm)" package="3 mm [THT]"]
  R4 = Resistor [tolerance=±5% resistance=1k package=THT]
  R5 = Resistor [tolerance=±5% resistance=1k package=THT]
  R6 = Resistor [tolerance=±5% resistance=1k package=THT]
  LED2 = LED - 3mm [color="Red (633nm)" package="3 mm [THT]"]
  LED3 = LED - 3mm [color="Red (633nm)" package="3 mm [THT]"]
  LED4 = LED - 3mm [color="Red (633nm)" package="3 mm [THT]"]

nets:
  PULSE: IC1.pin1, U1.Output
  VCC: IC1.pin2, IC1.pin3, IC1.pin4, IC1.pin6, IC1.pin7, IC1.pin10, IC1.pin14, IC2.pin2, IC2.pin3, IC2.pin4, IC2.pin6, IC2.pin7, IC2.pin10, IC2.pin14, 5V.VCC, U1.Reset, U1.Vcc_Supply_Voltage, R1.Pin_0
  D0: IC1.pin5, IC1.pin12, R3.Pin_0
  D1: IC1.pin9, IC2.pin1, R4.Pin_0
  GND: IC1.pin11, IC2.pin11, 5V.GND, U1.Ground, C1.1, C2.-, LED1.cathode, LED2.cathode, LED3.cathode, LED4.cathode
  D2: IC2.pin5, IC2.pin12, R5.Pin_0
  D3: IC2.pin9, R6.Pin_0
  N1: U1.Trigger, U1.Threshold, R2.Pin_1, C2.+
  N2: U1.Control_Voltage, C1.0
  N3: U1.Discharge, R1.Pin_1, R2.Pin_0
  N4: R3.Pin_1, LED1.anode
  N5: R4.Pin_1, LED2.anode
  N6: R5.Pin_1, LED3.anode
  N7: R6.Pin_1, LED4.anode

notes:
  pulse generator
  4-digit output
  4-stage async counter
  power supply
