# Fritzing sketch GuitarHeadphoneAmp (saved by Fritzing 0.9.2b)
breadboards: 1

parts:
  VCC1 = Battery block 9V
  CPS2 = Electrolytic Capacitor [capacitance=100µF package="100 mil [THT, electrolytic]"]
  IC1 = LM386 [package=dip08]
  C4 = Electrolytic Capacitor [capacitance=100µF package="100 mil [THT, electrolytic]"]
  RPS1 = Resistor [tolerance=±5% resistance=1k package=THT]
  LED1 = LED - 3mm [color="Green (555nm)" package="3 mm [THT]"]
  R2 = Resistor [tolerance=±5% resistance=10 package=THT]
  C5 = Ceramic Capacitor [capacitance=100nF package="100 mil [THT, multilayer]"]
  JOUT = Audio Jack (TRS) 3.5mm [package="4Ucon 08780 [THT]"]
  C1 = Ceramic Capacitor [capacitance=100nF package="100 mil [THT, multilayer]"]
  C3 = Electrolytic Capacitor [capacitance=10µF package="100 mil [THT, electrolytic]"]
  CPS1 = Ceramic Capacitor [capacitance=100nF package="100 mil [THT, multilayer]"]
  C2 = Ceramic Capacitor [capacitance=1nF package="100 mil [THT, multilayer]"]
  R1 = Resistor [tolerance=±5% resistance=47k package=THT]
  R3 = Resistor [tolerance=±5% resistance=1k package=THT]
  JIN = AMPHENOL - ACJS-MHDR [package=ACJS-MHDR]

nets:
  GND: VCC1.-, CPS2.-, IC1.+INPUT, IC1.GND, LED1.cathode, C5.0, JOUT.Sleeve, CPS1.0, C2.0, R1.Pin_1, JIN.Sleeve_(1)
  N1: VCC1.+, CPS2.+, IC1.Vs, RPS1.Pin_0, CPS1.1
  N2: IC1.GAIN, C3.+, R3.Pin_1
  N3: IC1.-INPUT, C1.1, C2.1
  N4: IC1.Vout, C4.+, R2.Pin_0
  N5: C4.-, JOUT.Ring, JOUT.Tip
  N6: RPS1.Pin_1, LED1.anode
  N7: R2.Pin_1, C5.1
  N8: C1.0, R1.Pin_0, JIN.Tip_(3)
  N9: C3.-, R3.Pin_0

custom parts:
  LM386: low voltage audio power amplifier
