# Fritzing sketch TDA7297Kit (saved by Fritzing 0.9.2b)
breadboards: 1

parts:
  IC1 = IC, DIP package, 16 pins [chip_label=TDA7297]
  R1 = Resistor [tolerance=±5% resistance=47k package=THT]
  R2 = Resistor [tolerance=±5% resistance=47k package=THT]
  R3 = Resistor [tolerance=±5% resistance=4.7k package=THT]
  C1 = Electrolytic Capacitor [capacitance=3.3mF voltage=25V package="100 mil [THT, electrolytic]"]
  C2 = Ceramic Capacitor [capacitance=100nF package="100 mil [THT, multilayer]"]
  C4 = Ceramic Capacitor [capacitance=220nF package="100 mil [THT, multilayer]"]
  C3 = Ceramic Capacitor [capacitance=220nF package="100 mil [THT, multilayer]"]
  C5 = Electrolytic Capacitor [capacitance=10µF package="100 mil [THT, electrolytic]"]
  R4a = Rotary Potentiometer (Small) [maximum_resistance=50kΩ package=THT]
  LED1 = LED - 5mm [color="Red (633nm)" package="5 mm [THT]"]
  D1 = Rectifier Diode [part_number=1N4007 package="300 mil [THT]"]
  12V = Screw terminal - 2 pins [package=THT]
  SP1 = Screw terminal - 2 pins [package=THT]
  SP2 = Screw terminal - 2 pins [package=THT]
  TRS1 = Audio Jack (TRS) 3.5mm [package="PG203J [THT]"]
  R4b = Rotary Potentiometer (Small) [maximum_resistance=50kΩ package=THT]

nets:
  N1: IC1.pin1, SP1.pin1
  N2: IC1.pin2, SP1.pin2
  VCC: IC1.pin3, IC1.pin13, R1.Pin_0, R3.Pin_1, C1.-, C2.1, D1.cathode
  N3: IC1.pin4, C3.1
  N4: IC1.pin6, IC1.pin9, R1.Pin_1, R2.Pin_1, C2.0, C5.+
  N5: IC1.pin7, R2.Pin_0
  GND: IC1.pin8, C1.+, C5.-, R4a.leg2, LED1.cathode, 12V.pin2, TRS1.Sleeve, R4b.leg2
  N6: IC1.pin12, C4.1
  N7: IC1.pin14, SP2.pin2
  N8: IC1.pin15, SP2.pin1
  N9: R3.Pin_0, LED1.anode
  INR: C4.0, R4a.wiper
  INL: C3.0, R4b.wiper
  N10: R4a.leg1, TRS1.Ring
  N11: D1.anode, 12V.pin1
  N12: TRS1.Tip, R4b.leg1

notes:
  I haven't laid out the breadboard .. see the schematic only
