# Fritzing sketch WhiteNoiseGeneratorS9014 (saved by Fritzing 0.9.2b)
breadboards: 1

parts:
  Q1 = NPN-Transistor [part_number=S9014 package="TO92 [THT]"]
  Q2 = NPN-Transistor [part_number=S9014 package="TO92 [THT]"]
  Q3 = NPN-Transistor [part_number=S9014 package="TO92 [THT]"]
  Q4 = NPN-Transistor [part_number=S9014 package="TO92 [THT]"]
  R1 = Resistor [tolerance=±5% resistance=1M package=THT]
  12V = Power plug
  C1 = Ceramic Capacitor [capacitance=100nF package="100 mil [THT, multilayer]"]
  R2 = Resistor [tolerance=±5% resistance=1M package=THT]
  R3 = Resistor [tolerance=±5% resistance=100k package=THT]
  C2 = Ceramic Capacitor [capacitance=100nF package="100 mil [THT, multilayer]"]
  R4 = Resistor [tolerance=±5% resistance=100k package=THT]
  C3 = Ceramic Capacitor [capacitance=1nF package="100 mil [THT, multilayer]"]
  R5 = Resistor [tolerance=±5% resistance=10k package=THT]
  C4 = Electrolytic Capacitor [capacitance=10µF package="100 mil [THT, electrolytic]"]
  R6 = Trimmer Potentiometer [maximum_resistance=10kΩ package=THT]
  J1 = Screw terminal - 2 pins [package=THT]
  C5 = Electrolytic Capacitor [capacitance=10µF package="100 mil [THT, electrolytic]"]
  R7 = Resistor [tolerance=±5% resistance=100k package=THT]
  R8 = Resistor [tolerance=±5% resistance=470 package=THT]
  C6 = Electrolytic Capacitor [capacitance=100µF package="100 mil [THT, electrolytic]"]
  TRS1 = Audio Jack (TRS) 3.5mm [package="4Ucon 08780 [THT]"]

nets:
  N1: Q1.E, Q3.C, Q4.C, 12V.VCC, R3.Pin_1, R4.Pin_1, R7.Pin_1
  N2: Q1.B, R1.Pin_1, C1.0
  GND: Q2.E, R1.Pin_0, 12V.GND, C3.0, R5.Pin_1, R6.leg2, J1.pin1, R8.Pin_1, TRS1.Sleeve
  N3: Q2.B, C1.1, R2.Pin_1
  N4: Q2.C, R2.Pin_0, R3.Pin_0, C2.0
  N5: Q3.E, R5.Pin_0, C4.+
  N6: Q3.B, C2.1, R4.Pin_0, C3.1
  N7: Q4.E, R8.Pin_0, C6.+
  N8: Q4.B, C5.+, R7.Pin_0
  N9: C4.-, R6.leg1, J1.pin2
  N10: R6.wiper, C5.-
  N11: C6.-, TRS1.Ring, TRS1.Tip
