# Fritzing sketch CommonEmitterAmplifier (saved by Fritzing 0.9.2b)
breadboards: 1

parts:
  5V = Power plug
  Q1 = NPN-Transistor [part_number=2N3904 package="TO92 [THT]"]
  Rc = Resistor [tolerance=±5% resistance=470 package=THT]
  Re = Resistor [tolerance=±5% resistance=220 package=THT]
  R2 = Resistor [tolerance=±5% resistance=5k package=THT]
  C1 = Ceramic Capacitor [capacitance=100nF package="100 mil [THT, multilayer]"]
  R1a = Resistor [tolerance=±5% resistance=12k package=THT]
  R1b = Resistor [tolerance=±5% resistance=36.9k package=THT]
  J1 = female pin header, 4 pins [form="♀ (female)"]
  R1c = Resistor [tolerance=±5% resistance=80k package=THT]

nets:
  N1: 5V.GND, Re.Pin_0, R2.Pin_0
  N2: 5V.VCC, Rc.Pin_0, R1a.Pin_0, R1b.Pin_0, R1c.Pin_0
  N3: Q1.E, Re.Pin_1
  CH1:IN: Q1.B, R2.Pin_1, C1.0, J1.pin1
  CH2:OUT: Q1.C, Rc.Pin_1
  IN: C1.1
  N4: R1a.Pin_1, J1.pin4
  N5: R1b.Pin_1, J1.pin3
  N6: J1.pin2, R1c.Pin_1

notes:
  CH2: OUT
  CH1: IN
  0.8Vpp
  10kHz
  R1a,b,c - multiple resistors or pots for approx these resistances, switched in as R1 via jumper
