# Fritzing sketch Comparator (saved by Fritzing 0.9.2b)
breadboards: 1

parts:
  Q1 = PNP-Transistor [part_number=2N3906 package="TO92 [THT]"]
  Q2 = PNP-Transistor [part_number=2N3906 package="TO92 [THT]"]
  Q3 = NPN-Transistor [part_number=2N3904 package="TO92 [THT]"]
  Q4 = NPN-Transistor [part_number=2N3904 package="TO92 [THT]"]
  Q5 = NPN-Transistor [part_number=2N3904 package="TO92 [THT]"]
  Q6 = NPN-Transistor [part_number=2N3904 package="TO92 [THT]"]
  Q7 = PNP-Transistor [part_number=2N3906 package="TO92 [THT]"]
  Q8 = NPN-Transistor [part_number=2N3904 package="TO92 [THT]"]
  R1 = Trimmer Potentiometer [maximum_resistance=100kΩ package=THT]
  R2 = Trimmer Potentiometer [maximum_resistance=100kΩ package=THT]
  R3 = Resistor [tolerance=±5% resistance=10k package=THT]
  R4 = Resistor [tolerance=±5% resistance=10k package=THT]
  R5 = Resistor [tolerance=±5% resistance=2.2k package=THT]
  R6 = Resistor [tolerance=±5% resistance=2.2k package=THT]
  R7 = Resistor [tolerance=±5% resistance=1k package=THT]
  LED1 = LED - 3mm [color="Blue (430nm)" package="3 mm [THT]"]
  5-12V = Power plug
  JVi = female pin header, 2 pins [form="♀ (female)"]
  JVr = female pin header, 2 pins [form="♀ (female)"]
  J1 = female pin header, 5 pins [form="♀ (female)"]

nets:
  VCC: Q1.E, Q2.E, Q7.E, R1.leg1, R2.leg1, R3.Pin_0, R7.Pin_0, 5-12V.VCC, J1.pin5
  N1: Q1.B, Q1.C, Q2.B, Q3.C
  N2: Q2.C, Q4.C, R5.Pin_0
  N3: Q3.E, Q4.E, Q5.C
  Vi: Q3.B, JVi.pin1, J1.pin1
  Vr: Q4.B, JVr.pin1, J1.pin2
  GND: Q5.E, Q6.E, Q8.E, R1.leg2, R2.leg2, R4.Pin_1, 5-12V.GND, J1.pin4
  N4: Q5.B, Q6.B, Q6.C, R3.Pin_1
  N5: Q7.B, R5.Pin_1
  Vo: Q7.C, R4.Pin_0, R6.Pin_0, J1.pin3
  N6: Q8.B, R6.Pin_1
  N7: Q8.C, LED1.cathode
  N8: R1.wiper, JVi.pin2
  N9: R2.wiper, JVr.pin2
  N10: R7.Pin_1, LED1.anode
