# Fritzing sketch CurrentSink (saved by Fritzing 0.9.2b)
breadboards: 1

parts:
  VCC1 = Battery block 9V
  R1 = Resistor [tolerance=±5% resistance=20k package=THT]
  R2 = Resistor [tolerance=±5% resistance=2.2k package=THT]
  Q1 = NPN-Transistor [part_number=BC547 package="TO92 [THT]"]
  R3 = Resistor [tolerance=±5% resistance=1k package=THT]
  VR4 = Trimmer Potentiometer [maximum_resistance=10kΩ package=THT]
  LED1 = LED - 3mm [color="Green (555nm)" package="3 mm [THT]"]
  LED2 = LED - 3mm [color="Green (555nm)" package="3 mm [THT]"]
  LED3 = LED - 3mm [color="Green (555nm)" package="3 mm [THT]"]

nets:
  GND: VCC1.-, R2.Pin_1, R3.Pin_1
  Vcc: VCC1.+, R1.Pin_0, VR4.wiper
  N1: R1.Pin_1, R2.Pin_0, Q1.B
  N2: Q1.E, R3.Pin_0
  N3: Q1.C, LED3.cathode
  N4: VR4.leg2, LED1.anode
  N5: LED1.cathode, LED2.anode
  N6: LED2.cathode, LED3.anode
