# Fritzing sketch LongTailPair (saved by Fritzing 0.9.2b)
breadboards: 1

parts:
  Q1 = NPN-Transistor [part_number=S9013 package="TO92 [THT]"]
  Q2 = NPN-Transistor [part_number=S9013 package="TO92 [THT]"]
  RC1 = Resistor [tolerance=±5% resistance=10k package=THT]
  VRB1 = Trimmer Potentiometer [maximum_resistance=10kΩ package=THT]
  RC2 = Resistor [tolerance=±5% resistance=10k package=THT]
  VCC1 = Battery block 9V
  RE = Resistor [tolerance=±5% resistance=4.7k package=THT]
  RB1a = Resistor [tolerance=±5% resistance=10k package=THT]
  RB2a = Resistor [tolerance=±5% resistance=10k package=THT]
  RB1b = Resistor [tolerance=±5% resistance=10k package=THT]
  RB2b = Resistor [tolerance=±5% resistance=10k package=THT]
  VRB2 = Trimmer Potentiometer [maximum_resistance=10kΩ package=THT]
  RO1 = Resistor [tolerance=±5% resistance=1k package=THT]
  LED1 = LED - 3mm [color="Red (633nm)" package="3 mm [THT]"]
  LED2 = LED - 3mm [color="Green (555nm)" package="3 mm [THT]"]
  RMO1a = Resistor [tolerance=±5% resistance=1M package=THT]
  RMO1b = Resistor [tolerance=±5% resistance=1M package=THT]
  RMO2b = Resistor [tolerance=±5% resistance=1M package=THT]
  RMO2a = Resistor [tolerance=±5% resistance=1M package=THT]
  RMB1a = Resistor [tolerance=±5% resistance=1M package=THT]
  RMB1b = Resistor [tolerance=±5% resistance=1M package=THT]
  RMB2a = Resistor [tolerance=±5% resistance=1M package=THT]
  RMB2b = Resistor [tolerance=±5% resistance=1M package=THT]
  Part1 = Arduino Uno (Rev3)
  Rb1 = Resistor [tolerance=±5% resistance=4.7k package=THT]
  Rb2 = Resistor [tolerance=±5% resistance=4.7k package=THT]

nets:
  N1: Q1.E, Q2.E, RE.Pin_0
  B1: Q1.B, RMB1a.Pin_0, Rb1.Pin_0
  OUT1: Q1.C, RC1.Pin_1, RO1.Pin_0, RMO1a.Pin_0
  B2: Q2.B, RMB2a.Pin_0, Rb2.Pin_1
  OUT2: Q2.C, RC2.Pin_1, LED1.cathode, LED2.anode, RMO2a.Pin_0
  VCC: RC1.Pin_0, RC2.Pin_0, VCC1.+, RB1a.Pin_1, RB2a.Pin_1
  N2: VRB1.leg1, RB1b.Pin_0
  N3: VRB1.wiper, Rb1.Pin_1
  N4: VRB1.leg2, RB1a.Pin_0
  GND: VCC1.-, RE.Pin_1, RB1b.Pin_1, RB2b.Pin_1, RMO1b.Pin_1, RMO2b.Pin_1, RMB1b.Pin_1, RMB2b.Pin_1, Part1.GND
  N5: RB2a.Pin_0, VRB2.leg2
  N6: RB2b.Pin_0, VRB2.leg1
  N7: VRB2.wiper, Rb2.Pin_0
  N8: RO1.Pin_1, LED1.anode, LED2.cathode
  AO1: RMO1a.Pin_1, RMO1b.Pin_0, Part1.A0
  AO2: RMO2b.Pin_0, RMO2a.Pin_1, Part1.A1
  AB1: RMB1a.Pin_1, RMB1b.Pin_0, Part1.A2
  AB2: RMB2a.Pin_1, RMB2b.Pin_0, Part1.A3
