# Fritzing sketch Monostable (saved by Fritzing 0.9.2b)
breadboards: 1

parts:
  R1 = Resistor [tolerance=±5% resistance=10k package=THT]
  R2 = Resistor [tolerance=±5% resistance=100k package=THT]
  R3 = Resistor [tolerance=±5% resistance=10k package=THT]
  C1 = Electrolytic Capacitor [capacitance=10µF package="100 mil [THT, electrolytic]"]
  Q1 = NPN-Transistor [part_number=S9013 package="TO92 [THT]"]
  Q2 = NPN-Transistor [part_number=S9013 package="TO92 [THT]"]
  LED1 = LED - 5mm [color="Red (633nm)" package="5 mm [THT]"]
  R5 = Resistor [tolerance=±5% resistance=100k package=THT]
  R6 = Resistor [tolerance=±5% resistance=10k package=THT]
  S1 = Pushbutton [package="[THT]"]
  R4 = Resistor [tolerance=±5% resistance=10k package=THT]
  D1 = Rectifier Diode [part_number=1N4001 package="300 mil [THT]"]
  VCC = Power plug

nets:
  N1: R1.Pin_0, R2.Pin_0, R3.Pin_0, S1.Pin_3, S1.Pin_4, VCC.VCC
  N2: R1.Pin_1, C1.+, Q1.C
  N3: R2.Pin_1, C1.-, Q2.B
  OUT: R3.Pin_1, Q2.C, LED1.anode, R4.Pin_1
  GND: Q1.E, Q2.E, LED1.cathode, R5.Pin_1, VCC.GND
  N4: Q1.B, R4.Pin_0, D1.cathode
  N5: R5.Pin_0, R6.Pin_1, D1.anode
  IN: R6.Pin_0, S1.Pin_1, S1.Pin_2
