# Fritzing sketch MrBiJuT (saved by Fritzing 0.9.2b)
breadboards: 1

parts:
  IC3 = IC, DIP package, 14 pins [chip_label=CD4011]
  PS = Power plug [part_number=9V]
  LED1 = LED - 3mm [color="Red (633nm)" part_number="NPN indicator" package="3 mm [THT]"]
  LED2 = LED - 3mm [color="Yellow (585nm)" part_number="PNP indicator" package="3 mm [THT]"]
  R1 = Resistor [tolerance=±5% resistance=100 package=THT]
  R2 = Resistor [tolerance=±5% resistance=100 package=THT]
  R3 = Resistor [tolerance=±5% resistance=100 package=THT]
  D1 = Rectifier Diode [part_number=1N4148 package="300 mil [THT]"]
  D2 = Rectifier Diode [part_number=1N4148 package="300 mil [THT]"]
  D3 = Rectifier Diode [part_number=1N4148 package="300 mil [THT]"]
  D4 = Rectifier Diode [part_number=1N4148 package="300 mil [THT]"]
  PNP_DUT = PNP-Transistor [package="TO92 [THT]"]  # not connected
  NPN_DUT = NPN-Transistor [package="TO92 [THT]"]  # not connected

nets:
  OSC: IC3.pin1, IC3.pin2, IC3.pin11
  SIG+: IC3.pin3, IC3.pin5, IC3.pin6, R2.Pin_1, R3.Pin_0
  E PAD/SIG-: IC3.pin4, LED1.anode, LED2.cathode, R1.Pin_1
  GND: IC3.pin7, PS.GND
  N1: IC3.pin8, IC3.pin9
  N2: IC3.pin12, IC3.pin13
  VDD: IC3.pin14, PS.VCC
  N3: LED1.cathode, LED2.anode, R3.Pin_1, D1.cathode, D3.anode
  B PAD: R1.Pin_0, R2.Pin_0
  N4: D1.anode, D2.cathode, D3.cathode, D4.anode
  C PAD: D2.anode, D4.cathode

notes:
  E PAD
  B PAD
  C PAD
