# Fritzing sketch NegativeFeedbackAmplifier (saved by Fritzing 0.9.2b)
breadboards: 1

parts:
  INPUT = Screw terminal - 2 pins [package=THT]
  OUTPUT = Screw terminal - 2 pins [package=THT]
  12V = Power plug
  R1 = Resistor [tolerance=±5% resistance=10k package=THT]
  C1 = Electrolytic Capacitor [capacitance=10µF package="100 mil [THT, electrolytic]"]
  VRB1 = Trimmer Potentiometer [maximum_resistance=100kΩ package=THT]
  RB1 = Resistor [tolerance=±5% resistance=20k package=THT]
  RB2 = Resistor [tolerance=±5% resistance=20k package=THT]
  Q1 = NPN-Transistor [package="TO92 [THT]"]
  RF1 = Resistor [tolerance=±5% resistance=100 package=THT]
  RE1 = Resistor [tolerance=±5% resistance=1k package=THT]
  CE1 = Electrolytic Capacitor [capacitance=100µF package="100 mil [THT, electrolytic]"]
  RC1 = Resistor [tolerance=±5% resistance=2.4k package=THT]
  Q2 = NPN-Transistor [package="TO92 [THT]"]
  C2 = Electrolytic Capacitor [capacitance=10µF package="100 mil [THT, electrolytic]"]
  S1 = Toggle Switch [package=THT]
  S2 = Toggle Switch [package=THT]
  RB21 = Resistor [tolerance=±5% resistance=5.1k package=THT]
  VRB2 = Trimmer Potentiometer [maximum_resistance=47kΩ package=THT]
  RF2 = Resistor [tolerance=±5% resistance=1k package=THT]
  C3 = Electrolytic Capacitor [capacitance=22µF package="100 mil [THT, electrolytic]"]
  RB22 = Resistor [tolerance=±5% resistance=10k package=THT]
  RC2 = Resistor [tolerance=±5% resistance=2.4k package=THT]
  RE2 = Resistor [tolerance=±5% resistance=1k package=THT]
  CE2 = Electrolytic Capacitor [capacitance=100µF package="100 mil [THT, electrolytic]"]
  RL = Resistor [tolerance=±5% resistance=2.4k package=THT]
  C4 = Electrolytic Capacitor [capacitance=10µF package="100 mil [THT, electrolytic]"]
  RF2v = Trimmer Potentiometer [maximum_resistance=10kΩ package=THT]

nets:
  N1: INPUT.pin1, R1.Pin_0
  GND: INPUT.pin2, OUTPUT.pin2, 12V.GND, RB1.Pin_0, RE1.Pin_0, CE1.-, RB22.Pin_0, RE2.Pin_0, CE2.-, RL.Pin_0
  N2: OUTPUT.pin1, RL.Pin_1, C4.-
  VCC: 12V.VCC, VRB1.leg1, VRB1.wiper, RC1.Pin_1, VRB2.leg1, VRB2.wiper, RC2.Pin_1
  N3: R1.Pin_1, C1.-
  TP1: C1.+, RB1.Pin_1, RB2.Pin_0, Q1.B
  N4: VRB1.leg2, RB2.Pin_1
  TP3: Q1.E, RF1.Pin_1, S2.COM
  TP2: Q1.C, RC1.Pin_0, C2.+
  N5: RF1.Pin_0, RE1.Pin_1, CE1.+
  TP6: Q2.E, RE2.Pin_1, CE2.+
  TP4: Q2.B, S1.L2, RB21.Pin_0, RB22.Pin_1
  TP5: Q2.C, C3.+, RC2.Pin_0, C4.+
  N6: C2.-, S1.COM
  N7: S2.L2, RF2v.leg2
  N8: RB21.Pin_1, VRB2.leg2
  N9: RF2.Pin_0, RF2v.leg1, RF2v.wiper
  N10: RF2.Pin_1, C3.-
