# Fritzing sketch PhaseSplitter (saved by Fritzing 0.9.2b)
breadboards: 1

parts:
  Q1 = NPN-Transistor [part_number=2N3904 package="TO92 [THT]"]
  Rc = Resistor [tolerance=±5% resistance=4.7k package=THT]
  5-20V = Power plug
  Re = Resistor [tolerance=±5% resistance=4.7k package=THT]
  Rb1 = Resistor [tolerance=±5% resistance=4.7k package=THT]
  Rb2 = Resistor [tolerance=±5% resistance=56k package=THT]
  C1 = Ceramic Capacitor [capacitance=100nF package="100 mil [THT, multilayer]"]

nets:
  SIGNAL+: Q1.E, Re.Pin_0
  N1: Q1.B, Rb1.Pin_1, Rb2.Pin_0, C1.1
  SIGNAL-: Q1.C, Rc.Pin_1
  VCC: Rc.Pin_0, 5-20V.VCC, Rb1.Pin_0
  GND: 5-20V.GND, Re.Pin_1, Rb2.Pin_1
  SIGNAL: C1.0

notes:
  IN
  OUT INV
  OUT NON-INV
