# Fritzing sketch SawTooth (saved by Fritzing 0.9.2b)
breadboards: 1

parts:
  R1 = Resistor [tolerance=±5% resistance=1k package=THT]
  R2 = Resistor [tolerance=±5% resistance=10k package=THT]
  Q1 = PNP-Transistor [part_number=2N3906 package="TO92 [THT]"]
  Q3 = NPN-Transistor [part_number=2N3904 package="TO92 [THT]"]
  Q2 = PNP-Transistor [part_number=2N3906 package="TO92 [THT]"]
  C1 = Ceramic Capacitor [capacitance=10µF package="100 mil [THT, multilayer]"]
  VCC1 = Battery block 9V
  R3 = Resistor [tolerance=±5% resistance=4.7k package=THT]
  R4 = Resistor [tolerance=±5% resistance=10k package=THT]
  Part1 = Arduino Uno (Rev3)
  R5 = Resistor [tolerance=±5% resistance=1M package=THT]
  R6 = Resistor [tolerance=±5% resistance=1M package=THT]
  R7 = Resistor [tolerance=±5% resistance=10k package=THT]

nets:
  N1: R1.Pin_0, VCC1.+, R3.Pin_0, R7.Pin_0
  N2: R1.Pin_1, R2.Pin_0, Q1.B
  GND: R2.Pin_1, Q3.E, C1.0, VCC1.-, R4.Pin_1, Part1.GND, R6.Pin_1
  N3: Q1.E, R7.Pin_1
  Vout: Q1.C, Q2.E, C1.1, R5.Pin_0
  N4: Q3.B, Q2.C
  N5: Q3.C, Q2.B, R3.Pin_1, R4.Pin_0
  N6: Part1.A0, R5.Pin_1, R6.Pin_0
