# Fritzing sketch TwoStageCommonEmitterAmplifier (saved by Fritzing 0.9.2b)
breadboards: 1

parts:
  INPUT = Screw terminal - 2 pins [package=THT]
  OUTPUT = Screw terminal - 2 pins [package=THT]
  9V = Power plug
  C1 = Electrolytic Capacitor [capacitance=10µF package="100 mil [THT, electrolytic]"]
  RB1 = Resistor [tolerance=±5% resistance=3.6k package=THT]
  RB2 = Resistor [tolerance=±5% resistance=20k package=THT]
  Q1 = NPN-Transistor [package="TO92 [THT]"]
  RE1 = Resistor [tolerance=±5% resistance=100 package=THT]
  RE1b = Resistor [tolerance=±5% resistance=100 package=THT]
  CE1 = Electrolytic Capacitor [capacitance=100µF package="100 mil [THT, electrolytic]"]
  RC1 = Resistor [tolerance=±5% resistance=1k package=THT]
  Q2 = NPN-Transistor [package="TO92 [THT]"]
  C2 = Electrolytic Capacitor [capacitance=10µF package="100 mil [THT, electrolytic]"]
  RB21 = Resistor [tolerance=±5% resistance=20k package=THT]
  RB22 = Resistor [tolerance=±5% resistance=3.6k package=THT]
  RC2 = Resistor [tolerance=±5% resistance=1k package=THT]
  RE2b = Resistor [tolerance=±5% resistance=100 package=THT]
  CE2 = Electrolytic Capacitor [capacitance=100µF package="100 mil [THT, electrolytic]"]
  RL = Resistor [tolerance=±5% resistance=2.2k package=THT]
  C4 = Electrolytic Capacitor [capacitance=10µF package="100 mil [THT, electrolytic]"]
  RE2 = Resistor [tolerance=±5% resistance=100 package=THT]

nets:
  N1: INPUT.pin1, C1.-
  GND: INPUT.pin2, OUTPUT.pin2, 9V.GND, RB1.Pin_0, RE1b.Pin_0, CE1.-, RB22.Pin_0, RE2b.Pin_0, CE2.-, RL.Pin_0
  N2: OUTPUT.pin1, RL.Pin_1, C4.-
  VCC: 9V.VCC, RB2.Pin_1, RC1.Pin_1, RB21.Pin_1, RC2.Pin_1
  TP1: C1.+, RB1.Pin_1, RB2.Pin_0, Q1.B
  TP3: Q1.E, RE1.Pin_1
  TP2: Q1.C, RC1.Pin_0, C2.+
  N3: RE1.Pin_0, RE1b.Pin_1, CE1.+
  TP6: Q2.E, RE2.Pin_1
  TP4: Q2.B, C2.-, RB21.Pin_0, RB22.Pin_1
  TP5: Q2.C, RC2.Pin_0, C4.+
  N4: RE2b.Pin_1, CE2.+, RE2.Pin_0
