# Fritzing sketch Module3V (saved by Fritzing 1.0.1rc)
breadboards: 1

parts:
  Part5 = Arduino Pro Mini (3.3V)
  OLED2 = 128x32 I2C Monochrome OLED Display
  GY-BME280-3_3_Module = female pin header, 6 pins [form="♀ (female)"]

nets:
  3.3V: Part5.VCC, OLED2.3.3V, GY-BME280-3_3_Module.pin1
  GND: Part5.GND, OLED2.GND, GY-BME280-3_3_Module.pin2
  SDA: Part5.A4, OLED2.SDA, GY-BME280-3_3_Module.pin4
  SCL: Part5.A5, OLED2.SCL, GY-BME280-3_3_Module.pin3
  CSB: GY-BME280-3_3_Module.pin5
  SDO: GY-BME280-3_3_Module.pin6

notes:
  GY-BME280-3.3 Module
