# Fritzing sketch Module (saved by Fritzing 1.0.1rc)
breadboards: 1

parts:
  OLED2 = 128x32 I2C Monochrome OLED Display
  GY-68_BMP180_Module = female pin header, 4 pins [form="♀ (female)"]
  Part6 = Arduino Uno (Rev3)

nets:
  SDA: OLED2.SDA, GY-68_BMP180_Module.pin4, Part6.A4/SDA
  SCL: OLED2.SCL, GY-68_BMP180_Module.pin3, Part6.A5/SCL
  GND: OLED2.GND, GY-68_BMP180_Module.pin2, Part6.GND
  5V: OLED2.VIN, GY-68_BMP180_Module.pin1, Part6.5V

notes:
  GY-68 BMP180 Module
