# Fritzing sketch Module (saved by Fritzing 1.0.1rc)
breadboards: 1

parts:
  Part5 = Arduino Pro Mini (3.3V)
  OLED2 = 128x32 I2C Monochrome OLED Display
  GY-BMP280-3_3_Module = female pin header, 6 pins [form="♀ (female)"]

nets:
  3.3V: Part5.VCC, OLED2.3.3V, GY-BMP280-3_3_Module.pin1
  GND: Part5.GND, OLED2.GND, GY-BMP280-3_3_Module.pin2
  SDA: Part5.A4, OLED2.SDA, GY-BMP280-3_3_Module.pin4
  SCL: Part5.A5, OLED2.SCL, GY-BMP280-3_3_Module.pin3
  CSB: GY-BMP280-3_3_Module.pin5
  SDO: GY-BMP280-3_3_Module.pin6

notes:
  GY-BMP280-3.3 Module
