# Fritzing sketch BasicAND (saved by Fritzing 0.9.0b)
breadboards: 1

parts:
  Part1 = Arduino Uno (Rev3)
  LED1 = LED - 5mm [color="Red (633nm)" package="5 mm [THT]"]
  R3 = Resistor [tolerance=±5% resistance=4.7k package=THT]
  R1 = Resistor [tolerance=±5% resistance=1k package=THT]
  Q1 = NPN-Transistor [package="TO92 [THT]"]
  Q2 = NPN-Transistor [package="TO92 [THT]"]
  R2 = Resistor [tolerance=±5% resistance=1k package=THT]
  R4 = Resistor [tolerance=±5% resistance=10k package=THT]

nets:
  N1: Part1.A0, Part1.D8, R1.Pin_0
  N2: Part1.A1, Part1.D9_PWM, R2.Pin_0
  N3: Part1.A2, LED1.anode, Q2.E, R4.Pin_0
  N4: Part1.GND, R3.Pin_1, R4.Pin_1
  N5: Part1.5V, Q1.C
  N6: LED1.cathode, R3.Pin_0
  N7: R1.Pin_1, Q1.B
  N8: Q1.E, Q2.C
  N9: Q2.B, R2.Pin_1
