# Fritzing sketch BidirectionalLevelShifter (saved by Fritzing 0.9.2b)
breadboards: 1

parts:
  5V = Power plug
  3_3V = Power plug
  Q1 = Basic FET N-Channel [part_number=2N7000 package="TO220 [THT]"]
  R1 = Resistor [tolerance=±5% resistance=10k package=THT]
  R2 = Resistor [tolerance=±5% resistance=10k package=THT]
  S1 = Pushbutton [package="[THT]"]
  R3 = Resistor [tolerance=±5% resistance=220 package=THT]
  LED1 = LED - 3mm [color="Red (633nm)" package="3 mm [THT]"]

nets:
  GND: 5V.GND, 3_3V.GND, S1.Pin_1, S1.Pin_2, R3.Pin_1
  N1: 5V.VCC, R1.Pin_0
  N2: 3_3V.VCC, Q1.gate, R2.Pin_0
  HIGHV: Q1.drain, R1.Pin_1, S1.Pin_3, S1.Pin_4
  LOWV: Q1.source, R2.Pin_1, LED1.anode
  N3: R3.Pin_0, LED1.cathode
