# Fritzing sketch Modules (saved by Fritzing 1.0.1rc)
breadboards: 1

parts:
  5V = Power plug
  3_3V = Power plug
  BB1 = 4-Line Bi-Directional Level Shifter
  Q1 = Basic FET N-Channel [part_number=2N7000 package="TO220 [THT]"]
  Q2 = Basic FET N-Channel [part_number=2N7000 package="TO220 [THT]"]
  R1 = Resistor [tolerance=±5% power=0.25W resistance=4.7k package=THT]
  R2 = Resistor [tolerance=±5% power=0.25W resistance=1k package=THT]
  LED1 = LED - 3mm [color="Red (633nm)" current=0.030A package="3 mm [THT]"]
  LED2 = LED - 3mm [color="Red (633nm)" current=0.030A package="3 mm [THT]"]
  R3 = Resistor [tolerance=±5% power=0.25W resistance=1k package=THT]
  R4 = Resistor [tolerance=±5% power=0.25W resistance=4.7k package=THT]

nets:
  GND: 5V.GND, 3_3V.GND, BB1.GND, Q1.source, Q2.source
  HV: 5V.VCC, BB1.HV, R1.Pin_0, R2.Pin_0
  LV: 3_3V.VCC, BB1.LV, R3.Pin_0, R4.Pin_0
  CH1: BB1.A1, Q2.drain, LED2.cathode, R4.Pin_1
  CH4: BB1.A2
  CH2: BB1.B1
  CH3: BB1.B2, Q1.drain, R1.Pin_1, LED1.cathode
  SQUARE WAVE: Q1.gate, Q2.gate
  N1: R2.Pin_1, LED1.anode
  N2: LED2.anode, R3.Pin_1

notes:
  SQUARE WAVE
  CH1
  CH2
  CH3
  CH4

custom parts:
  4-Line Bi-Directional Level Shifter: 4-Channel Bi-Directional Level Shifter
