# Fritzing sketch BidirectionalLevelShifterModule (saved by Fritzing 0.9.2b)
breadboards: 1

parts:
  5V = Power plug
  3_3V = Power plug
  R1 = Resistor [tolerance=±5% resistance=10k package=THT]
  S1 = Pushbutton [package="[THT]"]
  R1_2 = Resistor [tolerance=±5% resistance=220 package=THT]
  LED1 = LED - 3mm [color="Red (633nm)" package="3 mm [THT]"]
  BB1 = 4-Line Bi-Directional Level Shifter

nets:
  GND: 5V.GND, 3_3V.GND, S1.Pin_1, S1.Pin_2, R1_2.Pin_1, BB1.GND
  N1: 5V.VCC, R1.Pin_0, BB1.HV
  N2: 3_3V.VCC, BB1.LV
  N3: R1.Pin_1, S1.Pin_3, S1.Pin_4, BB1.B4
  N4: R1_2.Pin_0, LED1.cathode
  N5: LED1.anode, BB1.A4

custom parts:
  4-Line Bi-Directional Level Shifter: 4-Channel Bi-Directional Level Shifter
