# Fritzing sketch LM386AudioAmp (saved by Fritzing 0.9.2b)
breadboards: 1

parts:
  IC1 = LM386 [package=dip08]
  C1 = Electrolytic Capacitor [capacitance=10µF package="100 mil [THT, electrolytic]"]
  C2 = Electrolytic Capacitor [capacitance=10µF package="100 mil [THT, electrolytic]"]
  AUDIO_OUT = Audio Jack (TRS) 3.5mm [package="4Ucon 08780 [THT]"]
  9V = Power plug
  R1 = Trimmer Potentiometer [maximum_resistance=10kΩ package=THT]
  C3 = Ceramic Capacitor [capacitance=47nF package="100 mil [THT, multilayer]"]
  R2 = Resistor [tolerance=±5% resistance=10 package=THT]
  C4 = Electrolytic Capacitor [capacitance=220µF package="100 mil [THT, electrolytic]"]
  C5 = Ceramic Capacitor [capacitance=100nF package="100 mil [THT, multilayer]"]
  R3 = Trimmer Potentiometer [maximum_resistance=10kΩ package=THT]

nets:
  N1: IC1.GAIN, C1.+, R1.leg2
  GND: IC1.-INPUT, IC1.GND, C2.-, AUDIO_OUT.Sleeve, 9V.GND, C3.0, C5.1, R3.leg2
  N2: IC1.+INPUT, R3.wiper
  N3: IC1.Vout, R2.Pin_0, C4.+
  N4: IC1.Vs, 9V.VCC, C5.0
  N5: IC1.BYPASS, C2.+
  N6: C1.-, R1.wiper
  N7: AUDIO_OUT.Ring, AUDIO_OUT.Tip, C4.-
  N8: C3.1, R2.Pin_1
  AUDIO_IN: R3.leg1

notes:
  Audio In

custom parts:
  LM386: low voltage audio power amplifier
