# Fritzing sketch PotModules (saved by Fritzing 0.9.2b)
breadboards: 1

parts:
  VR1 = Rotary Potentiometer (Small) [maximum_resistance=100kΩ package=THT]
  5V = Power plug
  LED1 = LED - 3mm [color="White (4500K)" package="3 mm [THT]"]
  R1 = Resistor [tolerance=±5% resistance=470 package=THT]
  VR2 = Rotary Potentiometer (Small) [maximum_resistance=10kΩ package=THT]
  LED2 = LED - 3mm [color="White (4500K)" package="3 mm [THT]"]
  Q1 = Basic FET N-Channel [package="D2Pak [SMD]"]

nets:
  GND: VR1.leg1, 5V.GND, LED2.cathode, Q1.source
  N1: VR1.wiper, Q1.Gate
  N2: VR1.leg2, 5V.VCC, R1.Pin_0, VR2.leg2
  N3: LED1.cathode, Q1.drain
  N4: LED1.anode, R1.Pin_1
  N5: VR2.leg1, VR2.wiper, LED2.anode

notes:
  potentiometer (voltage divider) mode
  variable resistor (rheostat) mode
