# Fritzing sketch SingleShotTrigger (saved by Fritzing 0.9.2b)
breadboards: 1

parts:
  U1 = 555 Timer [package="DIP8 [THT]"]
  R3 = Resistor [tolerance=±5% resistance=220 package=THT]
  C2 = Ceramic Capacitor [capacitance=100nF package="100 mil [THT, multilayer]"]
  R1 = Resistor [tolerance=±5% resistance=20k package=THT]
  C1 = Electrolytic Capacitor [capacitance=1µF package="100 mil [THT, electrolytic]"]
  5V = Power plug
  S1 = Pushbutton [package="[THT]"]
  R2 = Resistor [tolerance=±5% resistance=10k package=THT]
  IC2 = IC, DIP package, 16 pins [chip_label=CD4049 part_number=CD4049]
  LED1 = LED - 3mm [color="Green (555nm)" package="3 mm [THT]"]

nets:
  GND: U1.Ground, R3.Pin_1, C2.1, C1.-, 5V.GND, S1.Pin_3, S1.Pin_4, IC2.pin8
  N1: U1.Trigger, S1.Pin_1, S1.Pin_2, R2.Pin_0
  N2: U1.Output, IC2.pin9, IC2.pin11, LED1.anode
  VCC: U1.Reset, U1.Vcc_Supply_Voltage, R1.Pin_0, 5V.VCC, R2.Pin_1, IC2.pin1
  N3: U1.Control_Voltage, C2.0
  N4: U1.Threshold, U1.Discharge, R1.Pin_1, C1.+
  N5: R3.Pin_0, LED1.cathode
  -P: IC2.pin10
  N6: IC2.pin12, IC2.pin14
  P: IC2.pin15

notes:
  -P
  P
