# Fritzing sketch BreatheLamp (saved by Fritzing 0.9.2b)
breadboards: 1

parts:
  IC1 = LM324 [package=dil16]
  Q1 = NPN-Transistor [part_number=S8050 package="TO92 [THT]"]
  D1 = Rectifier Diode [part_number=1N4007 package="300 mil [THT]"]
  VCC1 = Battery block 9V
  R1 = Resistor [tolerance=±5% resistance=100 package=THT]
  R2 = Resistor [tolerance=±5% resistance=100 package=THT]
  R3 = Resistor [tolerance=±5% resistance=47k package=THT]
  R4 = Resistor [tolerance=±5% resistance=47k package=THT]
  C1 = Electrolytic Capacitor [capacitance=33µF package="100 mil [THT, electrolytic]"]
  R5 = Resistor [tolerance=±5% resistance=47k package=THT]
  R6 = Resistor [tolerance=±5% resistance=100k package=THT]
  R7 = Resistor [tolerance=±5% resistance=20k package=THT]
  R8 = Trimmer Potentiometer [maximum_resistance=20kΩ package=THT]
  LED1 = LED - 3mm [color="Red (633nm)" package="3 mm [THT]"]
  LED3 = LED - 3mm [color="Red (633nm)" package="3 mm [THT]"]
  LED2 = LED - 3mm [color="Red (633nm)" package="3 mm [THT]"]
  LED4 = LED - 3mm [color="Red (633nm)" package="3 mm [THT]"]
  LED7 = LED - 3mm [color="Red (633nm)" package="3 mm [THT]"]
  LED8 = LED - 3mm [color="Red (633nm)" package="3 mm [THT]"]
  LED5 = LED - 3mm [color="Red (633nm)" package="3 mm [THT]"]
  LED6 = LED - 3mm [color="Red (633nm)" package="3 mm [THT]"]

nets:
  OSC: IC1.OUT1, Q1.B, C1.+, R8.wiper
  N1: IC1.IN1-, C1.-, R5.Pin_1
  N2: IC1.IN1+, IC1.IN2-, R3.Pin_0, R4.Pin_1
  Vdd: IC1.V+, Q1.C, D1.cathode, R4.Pin_0
  N3: IC1.IN2+, R6.Pin_0, R7.Pin_0
  N4: IC1.OUT2, R5.Pin_0, R6.Pin_1
  GND: IC1.GND, VCC1.-, R3.Pin_1, LED2.cathode, LED4.cathode, LED8.cathode, LED6.cathode
  N5: Q1.E, R1.Pin_0, R2.Pin_0
  N6: D1.anode, VCC1.+
  N7: R1.Pin_1, LED1.anode, LED3.anode
  N8: R2.Pin_1, LED7.anode, LED5.anode
  N9: R7.Pin_1, R8.leg1
  N10: LED1.cathode, LED2.anode
  N11: LED3.cathode, LED4.anode
  N12: LED7.cathode, LED8.anode
  N13: LED5.cathode, LED6.anode

custom parts:
  LM324: LM324 Quad OpAmp
