# Fritzing sketch LogicProbe (saved by Fritzing 0.9.2b)
breadboards: 1

parts:
  D1 = LED - 3mm [color="Red (633nm)" package="3 mm [THT]"]
  D3 = LED - 3mm [color="Yellow (595nm)" package="3 mm [THT]"]
  R3 = Resistor [tolerance=±5% resistance=1k package=THT]
  R1 = Resistor [tolerance=±5% resistance=1k package=THT]
  5V = Power plug
  IC1 = IC, DIP package, 14 pins [chip_label=CD4001]
  D2 = LED - 3mm [color="Green (555nm)" package="3 mm [THT]"]
  R2 = Resistor [tolerance=±5% resistance=1k package=THT]
  R5 = Resistor [tolerance=±5% resistance=2.2M package=THT]
  R4 = Resistor [tolerance=±5% resistance=4.7M package=THT]
  C1 = Ceramic Capacitor [capacitance=100nF package="100 mil [THT, multilayer]"]

nets:
  N1: D1.cathode, IC1.pin3, IC1.pin6, D2.anode, R5.Pin_1
  N2: D1.anode, R1.Pin_1, D2.cathode, R2.Pin_1
  N3: D3.cathode, R3.Pin_1
  Vcc: D3.anode, R1.Pin_0, 5V.VCC, IC1.pin14, R4.Pin_0
  N4: R3.Pin_0, IC1.pin11
  GND: 5V.GND, IC1.pin7, R2.Pin_0
  INPUT: IC1.pin1, IC1.pin2, R5.Pin_0
  N5: IC1.pin4, C1.0
  N6: IC1.pin5, IC1.pin10, IC1.pin12, IC1.pin13
  N7: IC1.pin8, IC1.pin9, R4.Pin_1, C1.1

notes:
  INPUT
