# Fritzing sketch SRLatch (saved by Fritzing 0.9.2b)
breadboards: 1

parts:
  LED1(Q) = LED - 3mm [color="Green (555nm)" package="3 mm [THT]"]
  LED2(!Q) = LED - 3mm [color="Yellow (595nm)" package="3 mm [THT]"]
  R2 = Resistor [tolerance=±5% resistance=1k package=THT]
  R1 = Resistor [tolerance=±5% resistance=1k package=THT]
  RESET = Pushbutton [package="[THT]"]
  SET = Pushbutton [package="[THT]"]
  R3 = Resistor [tolerance=±5% resistance=10k package=THT]
  R4 = Resistor [tolerance=±5% resistance=10k package=THT]
  5V = Power plug
  IC1 = IC, DIP package, 14 pins [chip_label=CD4001]

nets:
  N1: LED1(Q).cathode, R1.Pin_1
  N2: LED1(Q).anode, IC1.pin3, IC1.pin5
  N3: LED2(!Q).cathode, R2.Pin_1
  N4: LED2(!Q).anode, IC1.pin2, IC1.pin4
  GND: R2.Pin_0, R1.Pin_0, R3.Pin_0, R4.Pin_0, 5V.GND, IC1.pin7
  N5: RESET.Pin_1, RESET.Pin_2, R3.Pin_1, IC1.pin6
  Vcc: RESET.Pin_3, RESET.Pin_4, SET.Pin_3, SET.Pin_4, 5V.VCC, IC1.pin14
  N6: SET.Pin_1, SET.Pin_2, R4.Pin_1, IC1.pin1

notes:
  Set
  Reset
