# Fritzing sketch SchmittOscillator (saved by Fritzing 1.0.1rc)
breadboards: 1

parts:
  R1 = Resistor [tolerance=±5% resistance=1k power=0.25W package=THT]
  5V = Power plug
  C1 = Ceramic Capacitor [capacitance=100nF voltage=35V package="100 mil [THT, multilayer]"]
  R2 = Resistor [tolerance=±5% power=0.25W resistance=1k package=THT]
  R3 = Resistor [tolerance=±5% power=0.25W resistance=470 package=THT]
  Q2 = Basic FET N-Channel [package="DPak [SMD]"]
  LED1 = LED - 3mm [color="Red (633nm)" current=0.030A package="3 mm [THT]"]
  U2 = IC, DIP package, 14 pins [chip_label=CD40106]

nets:
  OUT: R1.Pin_0, U2.pin2, U2.pin3
  IN: R1.Pin_1, C1.1, U2.pin1
  GND: 5V.GND, C1.0, Q2.source, U2.pin5, U2.pin7, U2.pin9, U2.pin11, U2.pin13
  VCC: 5V.VCC, LED1.anode, U2.pin14
  INDICATOR: R2.Pin_0, U2.pin4
  N1: R2.Pin_1, Q2.Gate
  N2: R3.Pin_0, Q2.drain
  N3: R3.Pin_1, LED1.cathode

notes:
  OUT
