# Fritzing sketch VoltageMultiplier (saved by Fritzing 1.0.1rc)
breadboards: 1

parts:
  5V = Power plug
  C1 = Ceramic Capacitor [capacitance=100nF voltage=35V package="100 mil [THT, multilayer]"]
  R1 = Resistor [tolerance=±5% power=0.25W resistance=1k package=THT]
  D1 = Rectifier Diode [part_number=1N4148 package="300 mil [THT]"]
  C2 = Ceramic Capacitor [capacitance=330nF voltage=35V package="100 mil [THT, multilayer]"]
  D2 = Rectifier Diode [part_number=1N4148 package="300 mil [THT]"]
  C3 = Ceramic Capacitor [capacitance=330nF voltage=35V package="100 mil [THT, multilayer]"]
  D3 = Rectifier Diode [part_number=1N4148 package="300 mil [THT]"]
  C4 = Ceramic Capacitor [capacitance=330nF voltage=35V package="100 mil [THT, multilayer]"]
  D4 = Rectifier Diode [part_number=1N4148 package="300 mil [THT]"]
  C5 = Ceramic Capacitor [capacitance=330nF voltage=35V package="100 mil [THT, multilayer]"]
  D5 = Rectifier Diode [part_number=1N4148 package="300 mil [THT]"]
  C6 = Electrolytic Capacitor [capacitance=33µF voltage=400V package="100 mil [THT, electrolytic]"]
  LED1 = LED - 3mm [color="Yellow (574nm)" current=0.030A package="3 mm [THT]"]
  R2 = Resistor [tolerance=±5% power=0.25W resistance=10k package=THT]
  U1 = IC, DIP package, 14 pins [chip_label=CD40106]

nets:
  GND: 5V.GND, C1.0, C6.-, R2.Pin_1, U1.pin7, U1.pin11
  VCC: 5V.VCC, D1.anode, U1.pin14
  N1: C1.1, R1.Pin_0, U1.pin1
  1Y: R1.Pin_1, U1.pin2, U1.pin13
  N2: D1.cathode, C2.1, D2.anode
  6Y: C2.0, U1.pin3, U1.pin12
  N3: D2.cathode, C3.1, D3.anode
  2Y: C3.0, U1.pin4, U1.pin5
  N4: D3.cathode, C4.1, D4.anode
  3Y: C4.0, U1.pin6, U1.pin9
  N5: D4.cathode, C5.1, D5.anode
  4Y: C5.0, U1.pin8
  OUT: D5.cathode, C6.+, LED1.anode
  N6: LED1.cathode, R2.Pin_0
