# Fritzing sketch SRLatch (saved by Fritzing 1.0.1rc)
breadboards: 1

parts:
  U4 = 4011 4 x 2 Input NAND Gate, single part [part_number=4011 package="DIP (Dual Inline) [THT]"]
  Power = Power plug
  Set = Pushbutton [package="[THT]"]
  R1 = Resistor [tolerance=±5% power=0.25W resistance=10k package=THT]
  Reset = Pushbutton [package="[THT]"]
  R2 = Resistor [tolerance=±5% power=0.25W resistance=10k package=THT]
  R3 = Resistor [tolerance=±5% power=0.25W resistance=470 package=THT]
  LED1 = LED - 3mm [color="Green (555nm)" current=0.030A package="3 mm [THT]"]
  LED2 = LED - 3mm [color="Red (633nm)" current=0.030A package="3 mm [THT]"]
  R4 = Resistor [tolerance=±5% power=0.25W resistance=470 package=THT]

nets:
  N1: U4.A1, Set.Pin_1, Set.Pin_2, R1.Pin_0
  5V/Enable: U4.B1, U4.A2, U4.VDD, Power.VCC, Set.Pin_3, Set.Pin_4, Reset.Pin_3, Reset.Pin_4
  N2: U4.Q1, U4.B4
  N3: U4.Q2, U4.A3
  N4: U4.B2, Reset.Pin_1, Reset.Pin_2, R2.Pin_0
  GND: U4.GND, Power.GND, R1.Pin_1, R2.Pin_1, R3.Pin_0, R4.Pin_0
  Q: U4.B3, U4.Q4, LED1.anode
  ~Q: U4.Q3, U4.A4, LED2.anode
  N5: R3.Pin_1, LED1.cathode
  N6: LED2.cathode, R4.Pin_1

notes:
  SET
  RESET
