# Fritzing sketch ToggleTouchSwitch (saved by Fritzing 1.0.1rc)
breadboards: 1

parts:
  U2 = TOUCH [package=touch1]
  U1 = 4011 4 x 2 Input NAND Gate, single part [part_number=4011 package="DIP (Dual Inline) [THT]"]
  5V = Power plug
  R1 = Resistor [tolerance=±5% power=0.25W resistance=4.7M package=THT]
  R3 = Resistor [tolerance=±5% power=0.25W resistance=1k package=THT]
  LED1 = LED - 3mm [color="Green (555nm)" current=0.030A package="3 mm [THT]"]
  R4 = Resistor [tolerance=±5% power=0.25W resistance=4.7M package=THT]
  C1 = Ceramic Capacitor [capacitance=100nF voltage=35V package="100 mil [THT, multilayer]"]

nets:
  N1: U2.T1, U1.A1, U1.B1, R1.Pin_1
  N2: U2.T2, R4.Pin_0, C1.1
  N3: U1.Q1, U1.A2, U1.B2, R4.Pin_1
  OUT: U1.Q2, R1.Pin_0, LED1.anode
  GND: U1.GND, 5V.GND, R3.Pin_1, C1.0
  VCC: U1.VDD, 5V.VCC
  N4: R3.Pin_0, LED1.cathode
