# Fritzing sketch TouchSwitch (saved by Fritzing 1.0.1rc)
breadboards: 1

parts:
  U2 = TOUCH [package=touch1]
  U1 = 4011 4 x 2 Input NAND Gate, single part [part_number=4011 package="DIP (Dual Inline) [THT]"]
  5V = Power plug
  U3 = TOUCH [package=touch1]
  R1 = Resistor [tolerance=±5% power=0.25W resistance=10M package=THT]
  R2 = Resistor [tolerance=±5% power=0.25W resistance=10M package=THT]
  R3 = Resistor [tolerance=±5% power=0.25W resistance=1k package=THT]
  LED1 = LED - 3mm [color="Red (633nm)" current=0.030A package="3 mm [THT]"]

nets:
  N1: U2.T1, U1.A1, R1.Pin_1
  GND: U2.T2, U1.GND, 5V.GND, U3.T2, R3.Pin_1
  N2: U1.B1, U1.Q2
  OUT: U1.Q1, U1.A2, LED1.anode
  N3: U1.B2, U3.T1, R2.Pin_1
  VCC: U1.VDD, 5V.VCC, R1.Pin_0, R2.Pin_0
  N4: R3.Pin_0, LED1.cathode
