# Fritzing sketch LedChaser (saved by Fritzing 1.0.1rc)
breadboards: 1

parts:
  U1 = 555 Timer [package="DIP8 [THT]"]
  3-5V = Power plug
  C1 = Electrolytic Capacitor [capacitance=10µF voltage=35V package="100 mil [THT, electrolytic]"]
  R1 = Resistor [tolerance=±5% resistance=2k power=0.25W package=THT]
  RL2 = Resistor [tolerance=±5% resistance=220 power=0.25W package=THT]
  U2 = IC, DIP package, 16 pins [chip_label=CD4017 part_number=CD4017]
  S1 = Toggle Switch [package=THT]
  LED0 = LED - 3mm [color="Red (633nm)" current=0.030A package="3 mm [THT]"]
  R2 = Resistor [tolerance=±5% power=0.25W resistance=47k package=THT]
  LED1 = LED - 3mm [color="Red (633nm)" current=0.030A package="3 mm [THT]"]
  RL2_2 = Resistor [tolerance=±5% resistance=220 power=0.25W package=THT]
  LED2 = LED - 3mm [color="Red (633nm)" current=0.030A package="3 mm [THT]"]
  RL3 = Resistor [tolerance=±5% resistance=220 power=0.25W package=THT]
  LED3 = LED - 3mm [color="Red (633nm)" current=0.030A package="3 mm [THT]"]
  RL4 = Resistor [tolerance=±5% resistance=220 power=0.25W package=THT]
  LED4 = LED - 3mm [color="Red (633nm)" current=0.030A package="3 mm [THT]"]
  RL5 = Resistor [tolerance=±5% resistance=220 power=0.25W package=THT]
  LED5 = LED - 3mm [color="Red (633nm)" current=0.030A package="3 mm [THT]"]
  RL6 = Resistor [tolerance=±5% resistance=220 power=0.25W package=THT]
  LED6 = LED - 3mm [color="Red (633nm)" current=0.030A package="3 mm [THT]"]
  RL7 = Resistor [tolerance=±5% resistance=220 power=0.25W package=THT]
  LED7 = LED - 3mm [color="Red (633nm)" current=0.030A package="3 mm [THT]"]
  RL8 = Resistor [tolerance=±5% resistance=220 power=0.25W package=THT]
  LED8 = LED - 3mm [color="Red (633nm)" current=0.030A package="3 mm [THT]"]
  RL9 = Resistor [tolerance=±5% resistance=220 power=0.25W package=THT]
  LED9 = LED - 3mm [color="Red (633nm)" current=0.030A package="3 mm [THT]"]
  RL10 = Resistor [tolerance=±5% resistance=220 power=0.25W package=THT]

nets:
  GND: U1.Ground, 3-5V.GND, C1.-, RL2.Pin_1, U2.pin8, U2.pin13, U2.pin15, RL2_2.Pin_1, RL3.Pin_1, RL4.Pin_1, RL5.Pin_1, RL6.Pin_1, RL7.Pin_1, RL8.Pin_1, RL9.Pin_1, RL10.Pin_1
  N1: U1.Trigger, U1.Threshold, C1.+, R2.Pin_1
  CLK: U1.Output, U2.pin14
  VCC: U1.Reset, U1.Vcc_Supply_Voltage, R1.Pin_1, U2.pin16, S1.L2
  N2: U1.Discharge, R1.Pin_0, R2.Pin_0
  N3: 3-5V.VCC, S1.COM
  N4: RL2.Pin_0, LED0.cathode
  L5: U2.pin1, LED5.anode
  L1: U2.pin2, LED1.anode
  L0: U2.pin3, LED0.anode
  L2: U2.pin4, LED2.anode
  L6: U2.pin5, LED6.anode
  L7: U2.pin6, LED7.anode
  L3: U2.pin7, LED3.anode
  L8: U2.pin9, LED8.anode
  L4: U2.pin10, LED4.anode
  L9: U2.pin11, LED9.anode
  N5: LED1.cathode, RL2_2.Pin_0
  N6: LED2.cathode, RL3.Pin_0
  N7: LED3.cathode, RL4.Pin_0
  N8: LED4.cathode, RL5.Pin_0
  N9: LED5.cathode, RL6.Pin_0
  N10: LED6.cathode, RL7.Pin_0
  N11: LED7.cathode, RL8.Pin_0
  N12: LED8.cathode, RL9.Pin_0
  N13: LED9.cathode, RL10.Pin_0
