# Fritzing sketch Counter (saved by Fritzing 1.0.7)
breadboards: 1

parts:
  U1 = 555 Timer [package="DIP8 [THT]"]
  3-5V = Power plug
  C1 = Electrolytic Capacitor [capacitance=10µF voltage=35V package="100 mil [THT, electrolytic]"]
  R1 = Resistor [tolerance=±5% resistance=2k power=0.25W package=THT]
  S1 = Toggle Switch [package=THT]
  R2 = Resistor [tolerance=±5% power=0.25W resistance=47k package=THT]
  LED7 = LED - 3mm [color="Red (633nm)" current=0.030A package="3 mm [THT]"]
  RL7 = Resistor [tolerance=±5% resistance=220 power=0.25W package=THT]
  LED6 = LED - 3mm [color="Red (633nm)" current=0.030A package="3 mm [THT]"]
  RL6 = Resistor [tolerance=±5% resistance=220 power=0.25W package=THT]
  LED5 = LED - 3mm [color="Red (633nm)" current=0.030A package="3 mm [THT]"]
  RL5 = Resistor [tolerance=±5% resistance=220 power=0.25W package=THT]
  LED1 = LED - 3mm [color="Green (555nm)" current=0.030A package="3 mm [THT]"]
  RL1 = Resistor [tolerance=±5% resistance=220 power=0.25W package=THT]
  S2 = Pushbutton [package="[THT]"]
  R3 = Resistor [tolerance=±5% power=0.25W resistance=4.7k package=THT]
  U2 = IC, DIP package, 16 pins [chip_label=CD4020]
  LED4 = LED - 3mm [color="Red (633nm)" current=0.030A package="3 mm [THT]"]
  RL4 = Resistor [tolerance=±5% power=0.25W resistance=220 package=THT]
  RL8 = Resistor [tolerance=±5% resistance=220 power=0.25W package=THT]
  LED8 = LED - 3mm [color="Red (633nm)" current=0.030A package="3 mm [THT]"]
  RL9 = Resistor [tolerance=±5% resistance=220 power=0.25W package=THT]
  LED9 = LED - 3mm [color="Red (633nm)" current=0.030A package="3 mm [THT]"]
  RL10 = Resistor [tolerance=±5% resistance=220 power=0.25W package=THT]
  LED10 = LED - 3mm [color="Red (633nm)" current=0.030A package="3 mm [THT]"]
  RL11 = Resistor [tolerance=±5% resistance=220 power=0.25W package=THT]
  LED11 = LED - 3mm [color="Red (633nm)" current=0.030A package="3 mm [THT]"]
  RL12 = Resistor [tolerance=±5% resistance=220 power=0.25W package=THT]
  LED12 = LED - 3mm [color="Red (633nm)" current=0.030A package="3 mm [THT]"]
  RL13 = Resistor [tolerance=±5% resistance=220 power=0.25W package=THT]
  LED13 = LED - 3mm [color="Red (633nm)" current=0.030A package="3 mm [THT]"]
  RL14 = Resistor [tolerance=±5% resistance=220 power=0.25W package=THT]
  LED14 = LED - 3mm [color="Red (633nm)" current=0.030A package="3 mm [THT]"]

nets:
  GND: U1.Ground, 3-5V.GND, C1.-, RL7.Pin_1, RL6.Pin_1, RL5.Pin_1, RL1.Pin_1, R3.Pin_1, U2.pin8, RL4.Pin_1, RL8.Pin_1, RL9.Pin_1, RL10.Pin_1, RL11.Pin_1, RL12.Pin_1, RL13.Pin_1, RL14.Pin_1
  N1: U1.Trigger, U1.Threshold, C1.+, R2.Pin_1
  CLK: U1.Output, U2.pin10
  VDD: U1.Reset, U1.Vcc_Supply_Voltage, R1.Pin_1, S1.L2, S2.Pin_3, S2.Pin_4, U2.pin16
  N2: U1.Discharge, R1.Pin_0, R2.Pin_0
  N3: 3-5V.VCC, S1.COM
  N4: LED7.cathode, RL7.Pin_0
  Q7: LED7.anode, U2.pin6
  N5: LED6.cathode, RL6.Pin_0
  Q6: LED6.anode, U2.pin4
  N6: LED5.cathode, RL5.Pin_0
  Q5: LED5.anode, U2.pin5
  N7: LED1.cathode, RL1.Pin_0
  Q1: LED1.anode, U2.pin9
  N8: S2.Pin_1, S2.Pin_2, R3.Pin_0, U2.pin11
  Q12: U2.pin1, LED12.anode
  Q13: U2.pin2, LED13.anode
  Q14: U2.pin3, LED14.anode
  Q4: U2.pin7, LED4.anode
  Q9: U2.pin12, LED9.anode
  Q8: U2.pin13, LED8.anode
  Q10: U2.pin14, LED10.anode
  Q11: U2.pin15, LED11.anode
  N9: LED4.cathode, RL4.Pin_0
  N10: RL8.Pin_0, LED8.cathode
  N11: RL9.Pin_0, LED9.cathode
  N12: RL10.Pin_0, LED10.cathode
  N13: RL11.Pin_0, LED11.cathode
  N14: RL12.Pin_0, LED12.cathode
  N15: RL13.Pin_0, LED13.cathode
  N16: RL14.Pin_0, LED14.cathode
