# Fritzing sketch Counter (saved by Fritzing 1.0.7)
breadboards: 1

parts:
  U1 = 555 Timer [package="DIP8 [THT]"]
  3-5V = Power plug
  C1 = Electrolytic Capacitor [capacitance=10µF voltage=35V package="100 mil [THT, electrolytic]"]
  R1 = Resistor [tolerance=±5% resistance=2k power=0.25W package=THT]
  S1 = Toggle Switch [package=THT]
  R2 = Resistor [tolerance=±5% power=0.25W resistance=47k package=THT]
  LED7 = LED - 3mm [color="Red (633nm)" current=0.030A package="3 mm [THT]"]
  RL7 = Resistor [tolerance=±5% resistance=220 power=0.25W package=THT]
  LED6 = LED - 3mm [color="Red (633nm)" current=0.030A package="3 mm [THT]"]
  RL6 = Resistor [tolerance=±5% resistance=220 power=0.25W package=THT]
  LED5 = LED - 3mm [color="Red (633nm)" current=0.030A package="3 mm [THT]"]
  RL5 = Resistor [tolerance=±5% resistance=220 power=0.25W package=THT]
  LED4 = LED - 3mm [color="Red (633nm)" current=0.030A package="3 mm [THT]"]
  RL4 = Resistor [tolerance=±5% resistance=220 power=0.25W package=THT]
  LED3 = LED - 3mm [color="Red (633nm)" current=0.030A package="3 mm [THT]"]
  RL3 = Resistor [tolerance=±5% resistance=220 power=0.25W package=THT]
  LED2 = LED - 3mm [color="Red (633nm)" current=0.030A package="3 mm [THT]"]
  RL2 = Resistor [tolerance=±5% resistance=220 power=0.25W package=THT]
  LED1 = LED - 3mm [color="Red (633nm)" current=0.030A package="3 mm [THT]"]
  RL1 = Resistor [tolerance=±5% resistance=220 power=0.25W package=THT]
  U2 = IC, DIP package, 14 pins [chip_label=CD4024 part_number=CD4024]
  S2 = Pushbutton [package="[THT]"]
  R3 = Resistor [tolerance=±5% power=0.25W resistance=4.7k package=THT]

nets:
  GND: U1.Ground, 3-5V.GND, C1.-, RL7.Pin_1, RL6.Pin_1, RL5.Pin_1, RL4.Pin_1, RL3.Pin_1, RL2.Pin_1, RL1.Pin_1, U2.pin7, R3.Pin_1
  N1: U1.Trigger, U1.Threshold, C1.+, R2.Pin_1
  CLK: U1.Output, U2.pin1
  VDD: U1.Reset, U1.Vcc_Supply_Voltage, R1.Pin_1, S1.L2, U2.pin14, S2.Pin_3, S2.Pin_4
  N2: U1.Discharge, R1.Pin_0, R2.Pin_0
  N3: 3-5V.VCC, S1.COM
  N4: LED7.cathode, RL7.Pin_0
  Q7: LED7.anode, U2.pin3
  N5: LED6.cathode, RL6.Pin_0
  Q6: LED6.anode, U2.pin4
  N6: LED5.cathode, RL5.Pin_0
  Q5: LED5.anode, U2.pin5
  N7: LED4.cathode, RL4.Pin_0
  Q4: LED4.anode, U2.pin6
  N8: LED3.cathode, RL3.Pin_0
  Q3: LED3.anode, U2.pin9
  N9: LED2.cathode, RL2.Pin_0
  Q2: LED2.anode, U2.pin11
  N10: LED1.cathode, RL1.Pin_0
  Q1: LED1.anode, U2.pin12
  N11: U2.pin2, S2.Pin_1, S2.Pin_2, R3.Pin_0
