# Fritzing sketch ShiftRegister (saved by Fritzing 1.0.1rc)
breadboards: 1

parts:
  Part1 = Arduino Uno (Rev3)
  IC2 = IC, DIP package, 16 pins [chip_label=CD4027]
  IC1 = IC, DIP package, 14 pins [chip_label=CD4069BE]
  R1 = Resistor [tolerance=±5% power=0.25W resistance=10k package=THT]
  S1-RESET = Pushbutton [package="[THT]"]
  IC3 = IC, DIP package, 16 pins [chip_label=CD4027]
  LED1 = LED - 3mm [color="Red (633nm)" current=0.030A package="3 mm [THT]"]
  R2 = Resistor [tolerance=±5% power=0.25W resistance=470 package=THT]
  LED2 = LED - 3mm [color="Red (633nm)" current=0.030A package="3 mm [THT]"]
  R3 = Resistor [tolerance=±5% power=0.25W resistance=470 package=THT]
  LED3 = LED - 3mm [color="Red (633nm)" current=0.030A package="3 mm [THT]"]
  R4 = Resistor [tolerance=±5% power=0.25W resistance=470 package=THT]
  LED4 = LED - 3mm [color="Red (633nm)" current=0.030A package="3 mm [THT]"]
  R5 = Resistor [tolerance=±5% power=0.25W resistance=470 package=THT]
  S2-CLK = Pushbutton [package="[THT]"]
  R6 = Resistor [tolerance=±5% power=0.25W resistance=10k package=THT]
  C1 = Ceramic Capacitor [capacitance=100nF voltage=35V package="100 mil [THT, multilayer]"]
  S3-DATA = Toggle Switch [package=THT]
  R7 = Resistor [tolerance=±5% power=0.25W resistance=10k package=THT]
  R8 = Resistor [tolerance=±5% power=0.25W resistance=470 package=THT]
  LED5 = LED - 3mm [color="Green (555nm)" current=0.030A package="3 mm [THT]"]
  D1 = Rectifier Diode [part_number=1N4148 package="300 mil [THT]"]
  D2 = Rectifier Diode [part_number=1N4148 package="300 mil [THT]"]
  5V = Power plug

nets:
  DATA-A: Part1.D4, D2.anode
  CLK: Part1.D5_PWM, IC2.pin3, IC2.pin13, IC3.pin3, IC3.pin13, S2-CLK.Pin_1, S2-CLK.Pin_2, R6.Pin_1, C1.1
  RESET: Part1.D6_PWM, IC2.pin4, IC2.pin12, R1.Pin_0, S1-RESET.Pin_1, S1-RESET.Pin_2, IC3.pin4, IC3.pin12
  GND: Part1.GND, IC2.pin7, IC2.pin8, IC2.pin9, IC1.pin7, R1.Pin_1, IC3.pin7, IC3.pin8, IC3.pin9, R2.Pin_0, R3.Pin_0, R4.Pin_0, R5.Pin_0, R6.Pin_0, C1.0, R7.Pin_0, R8.Pin_0, 5V.GND
  Q2: IC2.pin1, IC3.pin10, LED2.anode
  ~Q2: IC2.pin2, IC3.pin11
  ~Q1: IC2.pin5, IC2.pin14
  Q1: IC2.pin6, IC2.pin15, LED1.anode
  DATA: IC2.pin10, IC1.pin9, S3-DATA.COM, R7.Pin_1, LED5.anode, D2.cathode
  ~DATA: IC2.pin11, IC1.pin8
  VDD: IC2.pin16, IC1.pin14, S1-RESET.Pin_3, S1-RESET.Pin_4, IC3.pin16, S2-CLK.Pin_3, S2-CLK.Pin_4, D1.anode, 5V.VCC
  Q4: IC3.pin1, LED4.anode
  ~Q4: IC3.pin2
  ~Q3: IC3.pin5, IC3.pin14
  Q3: IC3.pin6, IC3.pin15, LED3.anode
  N1: LED1.cathode, R2.Pin_1
  N2: LED2.cathode, R3.Pin_1
  N3: LED3.cathode, R4.Pin_1
  N4: LED4.cathode, R5.Pin_1
  N5: S3-DATA.L2, D1.cathode
  N6: R8.Pin_1, LED5.cathode
