# Fritzing sketch QuadExclusiveInterlock (saved by Fritzing 1.0.1rc)
breadboards: 1

parts:
  IC1 = IC, DIP package, 16 pins [chip_label=CD4028]
  5V = Power plug
  R1 = Resistor [tolerance=±5% power=0.25W resistance=10k package=THT]
  R2 = Resistor [tolerance=±5% power=0.25W resistance=10k package=THT]
  LED1 = LED - 3mm [color="Green (555nm)" current=0.030A package="3 mm [THT]"]
  LED2 = LED - 3mm [color="Green (555nm)" current=0.030A package="3 mm [THT]"]
  LED3 = LED - 3mm [color="Green (555nm)" current=0.030A package="3 mm [THT]"]
  LED4 = LED - 3mm [color="Green (555nm)" current=0.030A package="3 mm [THT]"]
  R3 = Resistor [tolerance=±5% power=0.25W resistance=470 package=THT]
  R4 = Resistor [tolerance=±5% power=0.25W resistance=470 package=THT]
  R5 = Resistor [tolerance=±5% power=0.25W resistance=470 package=THT]
  R6 = Resistor [tolerance=±5% power=0.25W resistance=470 package=THT]
  T1 = Basic FET N-Channel [part_number=2N7000 package="TO220 [THT]"]
  LED5 = LED - 3mm [color="Red (633nm)" current=0.030A package="3 mm [THT]"]
  R7 = Resistor [tolerance=±5% power=0.25W resistance=470 package=THT]
  LED6 = LED - 3mm [color="Red (633nm)" current=0.030A package="3 mm [THT]"]
  R8 = Resistor [tolerance=±5% power=0.25W resistance=470 package=THT]
  R9 = Resistor [tolerance=±5% power=0.25W resistance=10k package=THT]
  T2 = Basic FET N-Channel [part_number=2N7000 package="TO220 [THT]"]
  R10 = Resistor [tolerance=±5% power=0.25W resistance=10k package=THT]
  LED7 = LED - 3mm [color="Red (633nm)" current=0.030A package="3 mm [THT]"]
  R11 = Resistor [tolerance=±5% power=0.25W resistance=470 package=THT]
  R12 = Resistor [tolerance=±5% power=0.25W resistance=10k package=THT]
  R13 = Resistor [tolerance=±5% power=0.25W resistance=10k package=THT]
  T3 = Basic FET N-Channel [part_number=2N7000 package="TO220 [THT]"]
  LED8 = LED - 3mm [color="Red (633nm)" current=0.030A package="3 mm [THT]"]
  R14 = Resistor [tolerance=±5% power=0.25W resistance=470 package=THT]
  R15 = Resistor [tolerance=±5% power=0.25W resistance=10k package=THT]
  R16 = Resistor [tolerance=±5% power=0.25W resistance=10k package=THT]
  T4 = Basic FET N-Channel [part_number=2N7000 package="TO220 [THT]"]
  S1 = Toggle Switch [package=THT]
  S2 = Toggle Switch [package=THT]
  S3 = Toggle Switch [package=THT]
  S4 = Toggle Switch [package=THT]

nets:
  Q4: IC1.pin1, R12.Pin_1, R13.Pin_0
  Q2: IC1.pin2, R9.Pin_1, R10.Pin_0
  GND: IC1.pin8, 5V.GND, R3.Pin_0, R4.Pin_0, R5.Pin_0, R6.Pin_0, T1.source, T2.source, T3.source, T4.source, S1.L1, S2.L1, S3.L1, S4.L1
  Q8: IC1.pin9, R15.Pin_0, R16.Pin_1
  A: IC1.pin10, R1.Pin_0, LED1.anode, S1.COM
  D: IC1.pin11, LED4.anode, R16.Pin_0, S4.COM
  C: IC1.pin12, LED3.anode, R12.Pin_0, S3.COM
  B: IC1.pin13, LED2.anode, R9.Pin_0, S2.COM
  Q1: IC1.pin14, R1.Pin_1, R2.Pin_0
  VCC: IC1.pin16, 5V.VCC, R7.Pin_0, R8.Pin_0, R11.Pin_0, R14.Pin_0, S1.L2, S2.L2, S3.L2, S4.L2
  N1: R2.Pin_1, T1.gate
  N2: LED1.cathode, R3.Pin_1
  N3: LED2.cathode, R4.Pin_1
  N4: LED3.cathode, R5.Pin_1
  N5: LED4.cathode, R6.Pin_1
  N6: T1.drain, LED5.cathode
  N7: LED5.anode, R7.Pin_1
  N8: LED6.cathode, T2.drain
  N9: LED6.anode, R8.Pin_1
  N10: T2.gate, R10.Pin_1
  N11: LED7.cathode, T3.drain
  N12: LED7.anode, R11.Pin_1
  N13: R13.Pin_1, T3.gate
  N14: LED8.cathode, T4.drain
  N15: LED8.anode, R14.Pin_1
  N16: R15.Pin_1, T4.gate
