# Fritzing sketch Counter (saved by Fritzing 1.0.1rc)
breadboards: 1

parts:
  5V = Power plug
  IC1 = IC, DIP package, 16 pins [chip_label=CD4029 part_number=CD4029]
  BIN/DEC = Toggle Switch [package=THT]
  LED1 = LED - 3mm [color="Red (633nm)" current=0.030A package="3 mm [THT]"]
  LED2 = LED - 3mm [color="Red (633nm)" current=0.030A package="3 mm [THT]"]
  LED3 = LED - 3mm [color="Red (633nm)" current=0.030A package="3 mm [THT]"]
  LED4 = LED - 3mm [color="Red (633nm)" current=0.030A package="3 mm [THT]"]
  R1 = Resistor [tolerance=±5% power=0.25W resistance=1k package=THT]
  R2 = Resistor [tolerance=±5% power=0.25W resistance=1k package=THT]
  R3 = Resistor [tolerance=±5% power=0.25W resistance=1k package=THT]
  R4 = Resistor [tolerance=±5% power=0.25W resistance=1k package=THT]
  CLK = female pin header, 1 pin [form="♀ (female)"]
  R5 = Resistor [tolerance=±5% power=0.25W resistance=10k package=THT]
  CLEAR = Pushbutton [package="[THT]"]

nets:
  GND: 5V.GND, IC1.pin3, IC1.pin4, IC1.pin5, IC1.pin8, IC1.pin12, IC1.pin13, BIN/DEC.L2, R1.Pin_1, R2.Pin_1, R3.Pin_1, R4.Pin_1, R5.Pin_1
  5V: 5V.VCC, IC1.pin10, IC1.pin16, BIN/DEC.L1, CLEAR.Pin_3, CLEAR.Pin_4
  N1: IC1.pin1, R5.Pin_0, CLEAR.Pin_1, CLEAR.Pin_2
  Q4: IC1.pin2, LED4.anode
  Q1: IC1.pin6, LED1.anode
  N2: IC1.pin9, BIN/DEC.COM
  Q2: IC1.pin11, LED2.anode
  Q3: IC1.pin14, LED3.anode
  N3: IC1.pin15, CLK.pin1
  N4: LED1.cathode, R1.Pin_0
  N5: LED2.cathode, R2.Pin_0
  N6: LED3.cathode, R3.Pin_0
  N7: LED4.cathode, R4.Pin_0

notes:
  CLK
