# Fritzing sketch MainsLinkedPLL (saved by Fritzing 0.9.2b)
breadboards: 1

parts:
  IC1 = IC, DIP package, 16 pins [chip_label=CD4046]
  R1 = Resistor [tolerance=±5% resistance=100k package=THT]
  RL = Resistor [tolerance=±5% resistance=1k package=THT]
  IC3 = IC, DIP package, 14 pins [chip_label=CD4011]
  U1 = Optocoupler [package=THT]
  C1 = Ceramic Capacitor [capacitance=100nF package="100 mil [THT, multilayer]"]
  LED1 = LED - 3mm [color="White (4500K)" package="3 mm [THT]"]
  R3 = Resistor [tolerance=±5% resistance=1M package=THT]
  R4 = Resistor [tolerance=±5% resistance=220k package=THT]
  C2 = Electrolytic Capacitor [capacitance=2.2µF package="100 mil [THT, electrolytic]"]
  R5 = Resistor [tolerance=±5% resistance=10k package=THT]
  12VAC = Screw terminal - 2 pins [package=THT]
  240VAC = Screw terminal - 2 pins [package=THT]
  D1 = Rectifier Diode [part_number=1N4148 package="300 mil [THT]"]
  R9 = Resistor [tolerance=±5% resistance=10k package=THT]
  R6 = Resistor [tolerance=±5% resistance=68k package=THT]
  R8 = Resistor [tolerance=±5% resistance=68k package=THT]
  R7 = Resistor [tolerance=±5% resistance=68k package=THT]
  C3 = Electrolytic Capacitor [capacitance=1µF package="100 mil [THT, electrolytic]"]
  C4 = Ceramic Capacitor [capacitance=100nF package="100 mil [THT, multilayer]"]
  C5 = Ceramic Capacitor [capacitance=10nF package="100 mil [THT, multilayer]"]
  5V = Power plug

nets:
  VCO_OUT: IC1.pin3, IC1.pin4, IC3.pin12, IC3.pin13
  GND: IC1.pin5, IC1.pin8, R1.Pin_1, RL.Pin_1, IC3.pin1, IC3.pin2, IC3.pin5, IC3.pin6, IC3.pin7, IC3.pin8, IC3.pin9, U1.Pin_4, R4.Pin_1, C3.-, C4.0, C5.0, 5V.GND
  N1: IC1.pin6, C1.1
  N2: IC1.pin7, C1.0
  N3: IC1.pin9, R3.Pin_1, C2.+
  N4: IC1.pin11, R1.Pin_0
  N5: IC1.pin13, R3.Pin_0
  PulseIn: IC1.pin14, U1.Pin_5, R5.Pin_0
  VDD: IC1.pin16, IC3.pin14, R5.Pin_1, C3.+, C4.1, C5.1, 5V.VCC
  N6: RL.Pin_0, LED1.cathode
  PulseOut: IC3.pin11, LED1.anode
  N7: U1.Pin_1, D1.cathode, R9.Pin_0, R6.Pin_1
  N8: U1.Pin_2, 12VAC.pin2, 240VAC.pin2, D1.anode
  N9: R4.Pin_0, C2.-
  N10: 12VAC.pin1, R9.Pin_1
  N11: 240VAC.pin1, R8.Pin_0
  N12: R6.Pin_0, R7.Pin_0
  N13: R8.Pin_1, R7.Pin_1

notes:
  12 VAC
  240 VAC
  Sync Pulse
  Raw Pulse
  240VAC Pulse Detector (12VAC for testing)
