# Fritzing sketch RampGenerator (saved by Fritzing 0.9.2b)
breadboards: 1

parts:
  IC1 = IC, DIP package, 16 pins [chip_label=CD4046]
  5-12V = Power plug
  R1 = Resistor [tolerance=±5% resistance=10k package=THT]
  VR1 = Trimmer Potentiometer [maximum_resistance=10kΩ package=THT]
  Q1 = NPN-Transistor [part_number=2N3904 package="TO92 [THT]"]
  R4 = Resistor [tolerance=±5% resistance=1k package=THT]
  R2 = Resistor [tolerance=±5% resistance=12k package=THT]
  R3 = Resistor [tolerance=±5% resistance=4.7k package=THT]
  C1 = Ceramic Capacitor [capacitance=10pF package="100 mil [THT, multilayer]"]
  C2 = Ceramic Capacitor [capacitance=1nF package="100 mil [THT, multilayer]"]
  C3 = Ceramic Capacitor [capacitance=100nF package="100 mil [THT, multilayer]"]
  C4 = Electrolytic Capacitor [capacitance=10µF package="100 mil [THT, electrolytic]"]

nets:
  GND: IC1.pin3, IC1.pin5, IC1.pin8, IC1.pin14, 5-12V.GND, R1.Pin_1, Q1.E, R3.Pin_1, C1.1, C2.0, C3.0, C4.-
  VCO_OUT: IC1.pin4, R4.Pin_0
  CH1/CXa: IC1.pin6, Q1.C, C2.1
  N1: IC1.pin7, C1.0
  N2: IC1.pin9, VR1.wiper
  N3: IC1.pin11, R1.Pin_0
  VDD: IC1.pin16, 5-12V.VCC, R2.Pin_1, C3.1, C4.+
  N4: VR1.leg1, R2.Pin_0
  N5: VR1.leg2, R3.Pin_0
  N6: Q1.B, R4.Pin_1

notes:
  CH1
