# Fritzing sketch VCO (saved by Fritzing 0.9.2b)
breadboards: 1

parts:
  IC1 = IC, DIP package, 16 pins [chip_label=CD4046]
  9V = Power plug
  C1 = Electrolytic Capacitor [capacitance=4.7µF package="100 mil [THT, electrolytic]"]
  R1 = Resistor [tolerance=±5% resistance=68k package=THT]
  R2 = Resistor [tolerance=±5% resistance=1M package=THT]
  VR1 = Trimmer Potentiometer [maximum_resistance=100kΩ package=THT]
  LED1 = LED - 5mm [color="Red (633nm)" package="5 mm [THT]"]
  RL = Resistor [tolerance=±5% resistance=1k package=THT]
  Q1 = 2N7000 FET N-Channel [part_number=2N7000 package=TO92]

nets:
  VCO_OUT: IC1.pin3, IC1.pin4, Q1.gate
  GND: IC1.pin5, IC1.pin8, 9V.GND, R1.Pin_1, R2.Pin_1, VR1.leg2, Q1.source
  N1: IC1.pin6, C1.-
  N2: IC1.pin7, C1.+
  N3: IC1.pin9, VR1.wiper
  N4: IC1.pin11, R1.Pin_0
  N5: IC1.pin12, R2.Pin_0
  VDD: IC1.pin16, 9V.VCC, VR1.leg1, LED1.anode
  N6: LED1.cathode, RL.Pin_1
  N7: RL.Pin_0, Q1.drain

custom parts:
  2N7000 FET N-Channel: A 2N7000 MOSFET N-Channel Transistor
