# Fritzing sketch AstableOscillator (saved by Fritzing 0.9.2b)
breadboards: 1

parts:
  IC1 = IC, DIP package, 14 pins [chip_label=CD4047]
  R1 = Resistor [tolerance=±5% resistance=220k package=THT]
  LED1 = LED - 5mm [color="Red (633nm)" package="5 mm [THT]"]
  3-15V = Power plug
  R2 = Resistor [tolerance=±5% resistance=1k package=THT]
  C2 = Electrolytic Capacitor [capacitance=1µF package="100 mil [THT, electrolytic]"]

nets:
  N1: IC1.pin1, C2.-
  N2: IC1.pin2, R1.Pin_0
  N3: IC1.pin3, R1.Pin_1, C2.+
  VCC: IC1.pin4, IC1.pin5, IC1.pin6, IC1.pin14, 3-15V.VCC
  GND: IC1.pin7, IC1.pin8, IC1.pin9, IC1.pin12, LED1.cathode, 3-15V.GND
  N4: IC1.pin10, R2.Pin_0
  N5: LED1.anode, R2.Pin_1
