# Fritzing sketch RelaxationOscillator (saved by Fritzing 1.0.1rc)
breadboards: 1

parts:
  IC1 = IC, DIP package, 16 pins [chip_label=CD4049 part_number=CD4049]
  Power = Power plug
  R1 = Resistor [tolerance=±5% power=0.25W resistance=6.8k package=THT]
  C1 = Ceramic Capacitor [capacitance=100nF voltage=35V package="100 mil [THT, multilayer]"]
  LED1 = LED - 3mm [color="Red (633nm)" current=0.030A package="3 mm [THT]"]
  R2 = Resistor [tolerance=±5% power=0.25W resistance=68k package=THT]
  R3 = Resistor [tolerance=±5% power=0.25W resistance=470 package=THT]

nets:
  5V: IC1.pin1, Power.VCC
  GND: IC1.pin3, IC1.pin5, IC1.pin7, IC1.pin8, Power.GND, R3.Pin_0
  N1: IC1.pin9, R2.Pin_0
  N2: IC1.pin10, IC1.pin11, R1.Pin_1
  OUT: IC1.pin12, IC1.pin14, C1.0
  N3: IC1.pin15, LED1.anode
  N4: R1.Pin_0, C1.1, R2.Pin_1
  N5: LED1.cathode, R3.Pin_1
