# Fritzing sketch VoltageDoubler (saved by Fritzing 1.0.1rc)
breadboards: 1

parts:
  IC1 = IC, DIP package, 16 pins [chip_label=CD4049 part_number=CD4049]
  Power = Power plug
  R1 = Resistor [tolerance=±5% power=0.25W resistance=6.8k package=THT]
  C1 = Ceramic Capacitor [capacitance=100nF voltage=35V package="100 mil [THT, multilayer]"]
  LED1 = LED - 3mm [color="Yellow (585nm)" current=0.030A package="3 mm [THT]"]
  R2 = Resistor [tolerance=±5% power=0.25W resistance=68k package=THT]
  R3 = Resistor [tolerance=±5% power=0.25W resistance=10k package=THT]
  D1 = Rectifier Diode [part_number=1N4007 package="300 mil [THT]"]
  C2 = Electrolytic Capacitor [capacitance=47µF voltage=400V package="100 mil [THT, electrolytic]"]
  D2 = Rectifier Diode [part_number=1N4007 package="300 mil [THT]"]
  C3 = Electrolytic Capacitor [capacitance=47µF voltage=400V package="100 mil [THT, electrolytic]"]

nets:
  12V: IC1.pin1, Power.VCC, D1.anode
  OUT: IC1.pin2, IC1.pin4, IC1.pin6, IC1.pin15, C2.-
  OSC: IC1.pin3, IC1.pin5, IC1.pin7, IC1.pin12, IC1.pin14, C1.0
  GND: IC1.pin8, Power.GND, R3.Pin_0, C3.-
  N1: IC1.pin9, R2.Pin_0
  N2: IC1.pin10, IC1.pin11, R1.Pin_1
  N3: R1.Pin_0, C1.1, R2.Pin_1
  N4: LED1.cathode, R3.Pin_1
  VOUT: LED1.anode, D2.cathode, C3.+
  N5: D1.cathode, C2.+, D2.anode
