# Fritzing sketch CrystalOscillator (saved by Fritzing 0.9.2b)
breadboards: 1

parts:
  IC3 = IC, DIP package, 16 pins [chip_label=CD4060]
  5V = Power plug
  C1 = Ceramic Capacitor [capacitance=10pF package="100 mil [THT, multilayer]"]
  R2 = Resistor [tolerance=±5% resistance=10M package=THT]
  R1 = Resistor [tolerance=±5% resistance=330k package=THT]
  XTAL1 = Crystal [frequency="32 kHz" package=THT]
  C2 = Ceramic Capacitor [capacitance=40pF package="100 mil [THT, multilayer]"]

nets:
  CH1/D7: IC3.pin1
  D2: IC3.pin4
  D1: IC3.pin5
  D3: IC3.pin6
  D0: IC3.pin7
  GND: IC3.pin8, IC3.pin12, 5V.GND, C1.1, C2.1
  CH2: IC3.pin10, R2.Pin_1, R1.Pin_0
  N1: IC3.pin11, C1.0, R2.Pin_0, XTAL1.pin_0
  D5: IC3.pin13
  D4: IC3.pin14
  D6: IC3.pin15
  VDD: IC3.pin16, 5V.VCC
  N2: R1.Pin_1, XTAL1.pin_1, C2.0
