# Fritzing sketch MusicLightKit (saved by Fritzing 0.9.2b)
breadboards: 1

parts:
  IC2 = IC, DIP package, 16 pins [chip_label=CD4060]
  R1 = Resistor [tolerance=±5% resistance=1.5M package=THT]
  C1 = Electrolytic Capacitor [capacitance=1µF package="100 mil [THT, electrolytic]"]
  R2 = Resistor [tolerance=±5% resistance=10k package=THT]
  R3 = Trimmer Potentiometer [maximum_resistance=200kΩ package=THT]
  5V = Power plug
  S1 = Toggle Switch [package=THT]
  Q2 = PNP-Transistor [part_number=S9012 package="TO92 [THT]"]
  R4 = Resistor [tolerance=±5% resistance=220k package=THT]
  D2 = Rectifier Diode [part_number=1N4148 package="300 mil [THT]"]
  D3 = Rectifier Diode [part_number=1N4148 package="300 mil [THT]"]
  D4 = Rectifier Diode [part_number=1N4148 package="300 mil [THT]"]
  LED1 = LED - 5mm [color="Red (633nm)" package="5 mm [THT]"]
  LED2 = LED - 5mm [color="Red (633nm)" package="5 mm [THT]"]
  LED3 = LED - 5mm [color="Red (633nm)" package="5 mm [THT]"]
  LED4 = LED - 5mm [color="Red (633nm)" package="5 mm [THT]"]
  R5 = Resistor [tolerance=±5% resistance=200 package=THT]
  R6 = Resistor [tolerance=±5% resistance=200 package=THT]
  R7 = Resistor [tolerance=±5% resistance=200 package=THT]
  R8 = Resistor [tolerance=±5% resistance=200 package=THT]
  Q3 = PNP-Transistor [part_number=S9012 package="TO92 [THT]"]
  LED5 = LED - 5mm [color="Yellow (595nm)" package="5 mm [THT]"]
  LED6 = LED - 5mm [color="Yellow (595nm)" package="5 mm [THT]"]
  LED7 = LED - 5mm [color="Yellow (595nm)" package="5 mm [THT]"]
  LED8 = LED - 5mm [color="Yellow (595nm)" package="5 mm [THT]"]
  R9 = Resistor [tolerance=±5% resistance=200 package=THT]
  R10 = Resistor [tolerance=±5% resistance=200 package=THT]
  R11 = Resistor [tolerance=±5% resistance=200 package=THT]
  R12 = Resistor [tolerance=±5% resistance=200 package=THT]
  Q4 = PNP-Transistor [part_number=S9012 package="TO92 [THT]"]
  LED9 = LED - 5mm [color="Green (570nm)" package="5 mm [THT]"]
  LED10 = LED - 5mm [color="Green (570nm)" package="5 mm [THT]"]
  LED11 = LED - 5mm [color="Green (570nm)" package="5 mm [THT]"]
  LED12 = LED - 5mm [color="Green (570nm)" package="5 mm [THT]"]
  R13 = Resistor [tolerance=±5% resistance=200 package=THT]
  R14 = Resistor [tolerance=±5% resistance=200 package=THT]
  R15 = Resistor [tolerance=±5% resistance=200 package=THT]
  R16 = Resistor [tolerance=±5% resistance=200 package=THT]

nets:
  PULSE2: IC2.pin4, D2.cathode, Q4.B
  PULSE1: IC2.pin5, D3.cathode, Q3.B
  PULSE3: IC2.pin6, Q2.B, D4.cathode
  GND: IC2.pin8, 5V.GND, Q2.C, Q3.C, Q4.C
  N1: IC2.pin9, C1.+
  N2: IC2.pin10, R2.Pin_0
  N3: IC2.pin11, R1.Pin_0
  VDD: IC2.pin16, S1.L2, R4.Pin_0, R5.Pin_1, R6.Pin_1, R7.Pin_1, R8.Pin_1, R9.Pin_1, R10.Pin_1, R11.Pin_1, R12.Pin_1, R13.Pin_1, R14.Pin_1, R15.Pin_1, R16.Pin_1
  N4: R1.Pin_1, C1.-, R3.leg2
  N5: R2.Pin_1, R3.leg1, R3.wiper
  N6: 5V.VCC, S1.COM
  N7: Q2.E, LED1.cathode, LED2.cathode, LED3.cathode, LED4.cathode
  N8: R4.Pin_1, D2.anode, D3.anode, D4.anode
  N9: LED1.anode, R5.Pin_0
  N10: LED2.anode, R6.Pin_0
  N11: LED3.anode, R7.Pin_0
  N12: LED4.anode, R8.Pin_0
  N13: Q3.E, LED5.cathode, LED6.cathode, LED7.cathode, LED8.cathode
  N14: LED5.anode, R9.Pin_0
  N15: LED6.anode, R11.Pin_0
  N16: LED7.anode, R12.Pin_0
  N17: LED8.anode, R10.Pin_0
  N18: Q4.E, LED9.cathode, LED10.cathode, LED11.cathode, LED12.cathode
  N19: LED9.anode, R13.Pin_0
  N20: LED10.anode, R16.Pin_0
  N21: LED11.anode, R14.Pin_0
  N22: LED12.anode, R15.Pin_0
