# Fritzing sketch RCOscillator (saved by Fritzing 0.9.2b)
breadboards: 1

parts:
  IC3 = IC, DIP package, 16 pins [chip_label=CD4060]
  5V = Power plug
  C1 = Ceramic Capacitor [capacitance=1nF package="100 mil [THT, multilayer]"]
  R2 = Resistor [tolerance=±5% resistance=10k package=THT]
  R1 = Resistor [tolerance=±5% resistance=10k package=THT]

nets:
  CH1/D7: IC3.pin1
  D2: IC3.pin4
  D1: IC3.pin5
  D3: IC3.pin6
  D0: IC3.pin7
  GND: IC3.pin8, IC3.pin12, 5V.GND
  N1: IC3.pin9, C1.0
  N2: IC3.pin10, R1.Pin_0
  N3: IC3.pin11, R2.Pin_0
  D5: IC3.pin13
  D4: IC3.pin14
  D6: IC3.pin15
  VDD: IC3.pin16, 5V.VCC
  CH2: C1.1, R2.Pin_1, R1.Pin_1
