# Fritzing sketch HiZAmplifier (saved by Fritzing 1.0.1rc)
breadboards: 1

parts:
  IC1 = IC, DIP package, 14 pins [chip_label=TC4069UBP]
  Power = Power plug
  R1 = Resistor [tolerance=±5% power=0.25W resistance=1M package=THT]
  R2 = Resistor [tolerance=±5% power=0.25W resistance=10M package=THT]
  C1 = Ceramic Capacitor [capacitance=100nF voltage=35V package="100 mil [THT, multilayer]"]

nets:
  N1: IC1.pin1, R1.Pin_1, R2.Pin_0
  SIGNAL_OUT: IC1.pin2, R2.Pin_1
  GND: IC1.pin7, Power.GND
  VDD: IC1.pin14, Power.VCC
  N2: R1.Pin_0, C1.1
  SIGNAL_IN: C1.0

notes:
  SIGNAL IN
  SIGNAL OUT
