# Fritzing sketch LogicProbe (saved by Fritzing 0.9.2b)
breadboards: 1

parts:
  D1 = LED - 3mm [color="Red (633nm)" package="3 mm [THT]"]
  D3 = LED - 3mm [color="Yellow (595nm)" package="3 mm [THT]"]
  R3 = Resistor [tolerance=±5% resistance=1k package=THT]
  R1 = Resistor [tolerance=±5% resistance=1k package=THT]
  5V = Power plug
  D2 = LED - 3mm [color="Green (555nm)" package="3 mm [THT]"]
  R2 = Resistor [tolerance=±5% resistance=1k package=THT]
  R4 = Resistor [tolerance=±5% resistance=1M package=THT]
  C1 = Ceramic Capacitor [capacitance=100nF package="100 mil [THT, multilayer]"]
  U3 = IC, DIP package, 14 pins [chip_label=CD4069BE]
  D4 = Rectifier Diode [part_number=1N4148 package="300 mil [THT]"]

nets:
  N1: D1.cathode, D2.anode, U3.pin2, U3.pin13, D4.cathode
  N2: D1.anode, R1.Pin_1
  N3: D3.cathode, R3.Pin_1
  Vcc: D3.anode, R1.Pin_0, 5V.VCC, R4.Pin_0, U3.pin14
  N4: R3.Pin_0, U3.pin8
  GND: 5V.GND, R2.Pin_0, U3.pin7
  N5: D2.cathode, R2.Pin_1
  N6: R4.Pin_1, C1.1, U3.pin11
  N7: C1.0, U3.pin12
  INPUT: U3.pin1
  N8: U3.pin9, U3.pin10, D4.anode

notes:
  INPUT
