# Fritzing sketch PushButtonLatch (saved by Fritzing 1.0.1rc)
breadboards: 1

parts:
  D1 = LED - 3mm [color="Red (633nm)" current=0.030A package="3 mm [THT]"]
  R1 = Resistor [tolerance=±5% resistance=220 power=0.25W package=THT]
  3-9V = Power plug
  D2 = LED - 3mm [color="Green (555nm)" current=0.030A package="3 mm [THT]"]
  R2 = Resistor [tolerance=±5% resistance=220 power=0.25W package=THT]
  IC1 = IC, DIP package, 14 pins [chip_label=CD4069BE]
  S1 = Pushbutton [package="[THT]"]
  R3 = Resistor [tolerance=±5% power=0.25W resistance=10k package=THT]
  R4 = Resistor [tolerance=±5% power=0.25W resistance=1M package=THT]
  C1 = Ceramic Capacitor [capacitance=1nF voltage=35V package="100 mil [THT, multilayer]"]
  R5 = Resistor [tolerance=±5% power=0.25W resistance=100k package=THT]
  C2 = Electrolytic Capacitor [capacitance=1µF voltage=35V package="100 mil [THT, electrolytic]"]
  R6 = Resistor [tolerance=±5% power=0.25W resistance=1M package=THT]

nets:
  Q: D1.cathode, IC1.pin4, R3.Pin_0
  N1: D1.anode, R1.Pin_1
  Vcc: R1.Pin_0, 3-9V.VCC, R2.Pin_1, IC1.pin14
  GND: 3-9V.GND, IC1.pin5, IC1.pin7, IC1.pin9, IC1.pin11, IC1.pin13, C2.-, R6.Pin_1
  nQ: D2.cathode, IC1.pin2, IC1.pin3, R5.Pin_0
  N2: D2.anode, R2.Pin_0
  N3: IC1.pin1, R3.Pin_1, R4.Pin_1, C1.1
  N4: S1.Pin_1, S1.Pin_2, R4.Pin_0, C1.0
  N5: S1.Pin_3, S1.Pin_4, R5.Pin_1, C2.+, R6.Pin_0
