# Fritzing sketch Oscillator (saved by Fritzing 0.9.2b)
breadboards: 1

parts:
  IC1 = IC, DIP package, 14 pins [chip_label=CD4070]
  3-15V = Power plug
  R1 = Resistor [tolerance=±5% resistance=1k package=THT]
  C1 = Ceramic Capacitor [capacitance=10nF package="100 mil [THT, multilayer]"]
  R2 = Resistor [tolerance=±5% resistance=1k package=THT]
  IC2 = IC, DIP package, 14 pins [chip_label=CD4069]
  R3 = Resistor [tolerance=±5% resistance=100k package=THT]
  C2 = Variable Capacitor [capacitance=100nF max_capacitance=120pF min_capacitance=40pF voltage=35V]

nets:
  VCC: IC1.pin1, IC1.pin5, IC1.pin9, IC1.pin14, 3-15V.VCC, IC2.pin14
  N1: IC1.pin2, R1.Pin_0, C1.0
  SIG1: IC1.pin3, R1.Pin_1, IC2.pin1
  SIG2: IC1.pin4, R2.Pin_0, IC2.pin3
  N2: IC1.pin6, R2.Pin_1
  GND: IC1.pin7, 3-15V.GND, C1.1, IC2.pin7
  N3: IC1.pin8, R3.Pin_1, C2.0
  SIG3: IC1.pin10, IC2.pin5, R3.Pin_0, C2.2
  OUT1: IC2.pin2
  OUT2: IC2.pin4
  OUT3: IC2.pin6
