# Fritzing sketch CMOSInverterOscillator (saved by Fritzing 0.9.2b)
breadboards: 1

parts:
  U2 = IC, DIP package, 14 pins [chip_label=CD4069BE]
  R1 = Trimmer Potentiometer [maximum_resistance=100kΩ package=THT]
  C1 = Electrolytic Capacitor [capacitance=10µF voltage=25V package="100 mil [THT, electrolytic]"]
  R2 = Resistor [tolerance=±5% resistance=100k package=THT]
  R3 = Resistor [tolerance=±5% resistance=1k package=THT]
  D1 = LED - 5mm [color="Yellow (574nm)" package="5 mm [THT]"]
  5V = Power plug

nets:
  N1: U2.pin1, R2.Pin_1
  N2: U2.pin2, U2.pin3, R1.leg2
  N3: U2.pin4, U2.pin13, C1.+
  GND: U2.pin7, D1.cathode, 5V.GND
  CH1: U2.pin12, R3.Pin_1
  VCC: U2.pin14, 5V.VCC
  N4: R1.leg1, R1.wiper, C1.-, R2.Pin_0
  N5: R3.Pin_0, D1.anode
