# Fritzing sketch simple_LED_capacitor_circuit (saved by Fritzing 0.9.0b)
breadboards: 1

parts:
  C1 = Electrolytic Capacitor [capacitance=1mF package="100 mil [THT, electrolytic]"]
  Power_plug1 = Power plug
  D1 = Rectifier Diode [part_number=1N4001 package="300 mil [THT]"]
  S1 = Pushbutton [package="[THT]"]
  R1 = Resistor [tolerance=±5% resistance=470 package=THT]
  LED1 = LED - 5mm [color="Red (633nm)" package="5 mm [THT]"]

nets:
  N1: C1.-, Power_plug1.GND, LED1.cathode
  N2: C1.+, S1.Pin_3, S1.Pin_4, R1.Pin_1
  N3: Power_plug1.VCC, D1.anode
  N4: D1.cathode, S1.Pin_1, S1.Pin_2
  N5: R1.Pin_0, LED1.anode
