# Fritzing sketch xCapacitorial (saved by Fritzing 0.9.0b)
breadboards: 1

parts:
  C1 = Electrolytic Capacitor [capacitance=1mF package="100 mil [THT, electrolytic]"]
  D1 = Rectifier Diode [part_number=1N4001 package="300 mil [THT]"]
  R1 = Resistor [tolerance=±5% resistance=470 package=THT]
  LED1 = LED - 5mm [color="Red (633nm)" package="5 mm [THT]"]
  Part1 = Arduino Uno (Rev3)

nets:
  N1: C1.-, LED1.cathode, Part1.GND
  N2: C1.+, D1.cathode, R1.Pin_1, Part1.A0
  N3: D1.anode, Part1.D8
  N4: R1.Pin_0, LED1.anode
