# Fritzing sketch ClapSwitchKit (saved by Fritzing 0.9.2b)
breadboards: 1

parts:
  MIC1 = Microphone
  R2 = Resistor [tolerance=±5% resistance=360k package=THT]
  C2 = Electrolytic Capacitor [capacitance=33µF package="100 mil [THT, electrolytic]"]
  R1 = Resistor [tolerance=±5% resistance=7.5k package=THT]
  R3 = Resistor [tolerance=±5% resistance=75k package=THT]
  C3 = Ceramic Capacitor [capacitance=22nF package="100 mil [THT, multilayer]"]
  C1 = Electrolytic Capacitor [capacitance=1µF package="100 mil [THT, electrolytic]"]
  Q1 = NPN-Transistor [part_number=S8050 package="TO92 [THT]"]
  Q2 = NPN-Transistor [part_number=S8050 package="TO92 [THT]"]
  C4 = Ceramic Capacitor [capacitance=10nF package="100 mil [THT, multilayer]"]
  R4 = Resistor [tolerance=±5% resistance=3.9k package=THT]
  R5 = Resistor [tolerance=±5% resistance=6.2k package=THT]
  R6 = Resistor [tolerance=±5% resistance=240 package=THT]
  R7 = Resistor [tolerance=±5% resistance=3.9k package=THT]
  R8 = Resistor [tolerance=±5% resistance=7.5k package=THT]
  Q3 = NPN-Transistor [part_number=S8050 package="TO92 [THT]"]
  Q4 = NPN-Transistor [part_number=S8050 package="TO92 [THT]"]
  R9 = Resistor [tolerance=±5% resistance=7.5k package=THT]
  R10 = Resistor [tolerance=±5% resistance=3.9k package=THT]
  R11 = Resistor [tolerance=±5% resistance=3.9k package=THT]
  D1 = Rectifier Diode [part_number=1N4148 package="300 mil [THT]"]
  D2 = Rectifier Diode [part_number=1N4148 package="300 mil [THT]"]
  C5 = Ceramic Capacitor [capacitance=47nF package="100 mil [THT, multilayer]"]
  C6 = Ceramic Capacitor [capacitance=47nF package="100 mil [THT, multilayer]"]
  R12 = Resistor [tolerance=±5% resistance=3.9k package=THT]
  D3 = Rectifier Diode [part_number=1N4148 package="300 mil [THT]"]
  D4 = Rectifier Diode [part_number=1N4148 package="300 mil [THT]"]
  Q5 = NPN-Transistor [part_number=S8050 package="TO92 [THT]"]
  R13 = Resistor [tolerance=±5% resistance=26k package=THT]
  R14 = Resistor [tolerance=±5% resistance=110 package=THT]
  Q7 = NPN-Transistor [part_number=S8050 package="TO92 [THT]"]
  R15 = Resistor [tolerance=±5% resistance=240 package=THT]
  R16 = Resistor [tolerance=±5% resistance=240 package=THT]
  LED1 = LED - 5mm [color="Green (555nm)" package="5 mm [THT]"]
  LED2 = LED - 5mm [color="Red (633nm)" package="5 mm [THT]"]
  R17 = Resistor [tolerance=±5% resistance=240 package=THT]
  C7 = Electrolytic Capacitor [capacitance=47µF package="100 mil [THT, electrolytic]"]
  3V = Power plug
  Q6 = PNP-Transistor [part_number=S8550 package="TO92 [THT]"]

nets:
  N1: MIC1.pin1, R1.Pin_0, C1.+
  N2: MIC1.pin2, R2.Pin_0, C2.+, R4.Pin_0, R5.Pin_0, R6.Pin_0
  N3: R2.Pin_1, R3.Pin_0, C1.-, Q1.B
  GND: C2.-, R1.Pin_1, Q1.E, Q2.E, C4.0, Q3.E, Q4.E, Q7.E, R17.Pin_1, C7.-, 3V.GND
  N4: R3.Pin_1, C3.0
  N5: C3.1, Q2.C, R5.Pin_1, C5.0, C6.0
  N6: Q1.C, Q2.B, C4.1, R4.Pin_1
  N7: R6.Pin_1, R7.Pin_0, R11.Pin_0, Q5.C, R13.Pin_0, R16.Pin_0, C7.+, 3V.VCC, Q6.E
  N8: R7.Pin_1, R8.Pin_0, Q3.C, R10.Pin_0
  N9: R8.Pin_1, Q4.B, D2.anode
  N10: Q3.B, R9.Pin_1, D1.anode
  N11: Q4.C, R9.Pin_0, R11.Pin_1, R12.Pin_0, D3.cathode
  N12: R10.Pin_1, D1.cathode, C5.1
  N13: D2.cathode, C6.1, R12.Pin_1, D4.cathode
  N14: D3.anode, R15.Pin_0
  N15: D4.anode, Q5.B, R13.Pin_1
  N16: Q5.E, R14.Pin_0
  N17: R14.Pin_1, Q7.B
  N18: Q7.C, LED1.cathode, LED2.anode, Q6.C
  N19: R15.Pin_1, Q6.B
  N20: R16.Pin_1, LED1.anode
  N21: LED2.cathode, R17.Pin_0
