# Fritzing sketch ClapSwitchKit2 (saved by Fritzing 0.9.2b)
breadboards: 1

parts:
  MIC1 = Microphone
  R2 = Resistor [tolerance=±5% resistance=470k package=THT]
  C4 = Electrolytic Capacitor [capacitance=47µF package="100 mil [THT, electrolytic]"]
  R1 = Resistor [tolerance=±5% resistance=2.2k package=THT]
  R3 = Resistor [tolerance=±5% resistance=47k package=THT]
  Q1 = NPN-Transistor [part_number=S9013 package="TO92 [THT]"]
  Q2 = NPN-Transistor [part_number=S9013 package="TO92 [THT]"]
  C3 = Ceramic Capacitor [capacitance=10nF package="100 mil [THT, multilayer]"]
  R4 = Resistor [tolerance=±5% resistance=4.7k package=THT]
  R6 = Resistor [tolerance=±5% resistance=4.7k package=THT]
  R7 = Resistor [tolerance=±5% resistance=470 package=THT]
  R9 = Resistor [tolerance=±5% resistance=2.2k package=THT]
  R10 = Resistor [tolerance=±5% resistance=10k package=THT]
  Q3 = NPN-Transistor [part_number=S9013 package="TO92 [THT]"]
  Q4 = NPN-Transistor [part_number=S9013 package="TO92 [THT]"]
  R11 = Resistor [tolerance=±5% resistance=10k package=THT]
  R8 = Resistor [tolerance=±5% resistance=10k package=THT]
  R12 = Resistor [tolerance=±5% resistance=2.2k package=THT]
  D1 = Rectifier Diode [part_number=1N4148 package="300 mil [THT]"]
  D2 = Rectifier Diode [part_number=1N4148 package="300 mil [THT]"]
  C5 = Ceramic Capacitor [capacitance=100nF package="100 mil [THT, multilayer]"]
  C6 = Ceramic Capacitor [capacitance=100nF package="100 mil [THT, multilayer]"]
  R13 = Resistor [tolerance=±5% resistance=10k package=THT]
  R14 = Resistor [tolerance=±5% resistance=1k package=THT]
  5V = Power plug
  C1 = Ceramic Capacitor [capacitance=100nF package="100 mil [THT, multilayer]"]
  C2 = Electrolytic Capacitor [capacitance=1µF package="100 mil [THT, electrolytic]"]
  R5 = Resistor [tolerance=±5% resistance=10k package=THT]
  LED1 = LED - 3mm [color="Red (633nm)" package="3 mm [THT]"]
  JP1 = Header 2 [package=jst-2-smd]

nets:
  N1: MIC1.pin1, R1.Pin_0, C1.1
  N2: MIC1.pin2, R2.Pin_0, C4.+, R4.Pin_0, R6.Pin_0, R7.Pin_0
  CH2: R2.Pin_1, R3.Pin_0, Q1.B, C1.0
  GND: C4.-, R1.Pin_1, Q1.E, Q2.E, C3.0, Q3.E, Q4.E, 5V.GND
  N3: R3.Pin_1, C2.-
  N4: Q1.C, C3.1, R4.Pin_1, R5.Pin_1
  N5: Q2.B, R5.Pin_0
  N6: Q2.C, R6.Pin_1, C5.0, C6.0, C2.+
  N7: R7.Pin_1, R9.Pin_0, R12.Pin_0, R14.Pin_0, 5V.VCC, JP1.1
  N8: R9.Pin_1, R10.Pin_0, Q3.C, R8.Pin_0
  N9: R10.Pin_1, Q4.B, D2.anode
  N10: Q3.B, R11.Pin_1, D1.anode
  CH1: Q4.C, R11.Pin_0, R12.Pin_1, R13.Pin_0, LED1.cathode, JP1.2
  N11: R8.Pin_1, D1.cathode, C5.1
  N12: D2.cathode, C6.1, R13.Pin_1
  N13: R14.Pin_1, LED1.anode
