# Fritzing sketch ColpittsOscillator (saved by Fritzing 0.9.2b)
breadboards: 1

parts:
  5V = Power plug
  R3 = Resistor [tolerance=±5% resistance=10k package=THT]
  R2 = Resistor [tolerance=±5% resistance=10k package=THT]
  C3 = Ceramic Capacitor [capacitance=100nF package="100 mil [THT, multilayer]"]
  Q1 = NPN-Transistor [part_number=2N3904 package="TO92 [THT]"]
  L1 = Inductor [inductance=1mH package="400 mil [THT]"]
  C1 = Ceramic Capacitor [capacitance=100nF package="100 mil [THT, multilayer]"]
  C2 = Ceramic Capacitor [capacitance=100nF package="100 mil [THT, multilayer]"]
  R1 = Resistor [tolerance=±5% resistance=2.2k package=THT]

nets:
  N1: 5V.GND, R2.Pin_0, C3.1, C2.1, R1.Pin_0
  N2: 5V.VCC, R3.Pin_0, L1.pin_0
  N3: R3.Pin_1, R2.Pin_1, C3.0, Q1.B
  TP1: Q1.E, C1.1, C2.0, R1.Pin_1
  Vout: Q1.C, L1.pin_1, C1.0
