# Fritzing sketch Comparator741 (saved by Fritzing 0.9.0b)
breadboards: 1

parts:
  Part1 = Arduino Uno (Rev3)
  IC1 = LM741 [package=dip08]
  R1 = Resistor [tolerance=±5% resistance=22k package=THT]
  C1 = Electrolytic Capacitor [capacitance=10µF package="100 mil [THT, electrolytic]"]
  R3 = Resistor [tolerance=±5% resistance=22k package=THT]
  R2 = Resistor [tolerance=±5% resistance=22k package=THT]
  R4 = Resistor [tolerance=±5% resistance=1k package=THT]
  LED1 = LED - 5mm [color="Red (633nm)" package="5 mm [THT]"]

nets:
  N1: Part1.A0, IC1.-INPUT, R1.Pin_1, C1.+
  N2: Part1.A1, IC1.OUTPUT, R4.Pin_0
  N3: Part1.D10_PWM/SS, R1.Pin_0
  N4: Part1.5V, IC1.V+, R2.Pin_1
  N5: Part1.GND, IC1.V-, C1.-, R3.Pin_1, LED1.cathode
  N6: IC1.+OFFSET, IC1.NC
  N7: IC1.+INPUT, R3.Pin_0, R2.Pin_0
  N8: R4.Pin_1, LED1.anode

custom parts:
  LM741: General Purpose Operational Amplifier
