# Fritzing sketch CrystalTester (saved by Fritzing 0.9.2b)
breadboards: 1

parts:
  9-15V = Power plug
  XTAL1 = Crystal [frequency="16 Mhz" package=THT]
  R1 = Resistor [tolerance=±5% resistance=4.7k package=THT]
  C1 = Ceramic Capacitor [capacitance=10nF package="100 mil [THT, multilayer]"]
  Q1 = NPN-Transistor [part_number=2N3904 package="TO92 [THT]"]
  Q2 = NPN-Transistor [part_number=2N3904 package="TO92 [THT]"]
  R2 = Resistor [tolerance=±5% resistance=22k package=THT]
  C2 = Ceramic Capacitor [capacitance=100nF package="100 mil [THT, multilayer]"]
  R4 = Resistor [tolerance=±5% resistance=1k package=THT]
  R5 = Resistor [tolerance=±5% resistance=1k package=THT]
  R3 = Resistor [tolerance=±5% resistance=100 package=THT]
  R6 = Resistor [tolerance=±5% resistance=470 package=THT]
  C3 = Ceramic Capacitor [capacitance=100pF package="100 mil [THT, multilayer]"]
  C4 = Ceramic Capacitor [capacitance=100pF package="100 mil [THT, multilayer]"]

nets:
  GND/PAD_B: 9-15V.GND, XTAL1.pin_1, C1.0, R2.Pin_0, R4.Pin_0, R6.Pin_0, C4.0
  N1: 9-15V.VCC, R1.Pin_0, C1.1, Q2.C, R3.Pin_0
  PAD_A: XTAL1.pin_0, R1.Pin_1, Q1.B, R2.Pin_1, C3.1
  N2: Q1.E, R4.Pin_1, R5.Pin_1, C3.0, C4.1
  N3: Q1.C, R3.Pin_1
  N4: Q2.E, C2.0, R6.Pin_1
  N5: Q2.B, R5.Pin_0
  OUT: C2.1
