# Fritzing sketch DarlingtonTouchSwitch (saved by Fritzing 0.9.2b)
breadboards: 1

parts:
  3_3-9V = Power plug
  Q1 = NPN-Transistor [part_number=2N3904 package="TO92 [THT]"]
  Q2 = NPN-Transistor [part_number=2N3904 package="TO92 [THT]"]
  R1 = Resistor [tolerance=±5% resistance=100k package=THT]
  R2 = Resistor [tolerance=±5% resistance=1k package=THT]
  LED1 = LED - 3mm [color="White (8000K)" package="3 mm [THT]"]

nets:
  GND: 3_3-9V.GND, Q2.E
  touch+: 3_3-9V.VCC, LED1.anode
  N1: Q1.E, Q2.B
  N2: Q1.B, R1.Pin_0
  N3: Q1.C, Q2.C, R2.Pin_0
  touch-: R1.Pin_1
  N4: R2.Pin_1, LED1.cathode

notes:
  touch-pad
