# Fritzing sketch AcLineDetector (saved by Fritzing 0.9.2b)
breadboards: 1

parts:
  Q3 = NPN-Transistor [part_number=2N3904 package="TO92 [THT]"]
  Q2 = NPN-Transistor [part_number=2N3904 package="TO92 [THT]"]
  Q1 = NPN-Transistor [part_number=2N3904 package="TO92 [THT]"]
  VCC = Battery
  LED1 = LED - 5mm [color="Green (570nm)" package="5 mm [THT]"]
  PIEZO = Piezo Speaker
  ANT1 = Antenna

nets:
  GND: Q3.E, VCC.-
  N1: Q3.B, Q2.E
  N2: Q3.C, LED1.cathode, PIEZO.pin2
  N3: Q2.B, Q1.E
  N4: Q2.C, Q1.C, VCC.+, LED1.anode, PIEZO.pin1
  N5: Q1.B, ANT1.antenna_lead
