# Fritzing sketch PeakDetector (saved by Fritzing 0.9.2b)
breadboards: 1

parts:
  D1 = Rectifier Diode [part_number=1N4007 package="300 mil [THT]"]
  R1 = Resistor [tolerance=±5% resistance=100k package=THT]
  C1 = Electrolytic Capacitor [capacitance=10µF package="100 mil [THT, electrolytic]"]
  Part1 = Arduino Uno (Rev3)
  OA1 = LM741 [part_number=LM741 package=dip08]

nets:
  PEAK_SIGNAL: D1.cathode, R1.Pin_1, C1.+, Part1.A1, OA1.-INPUT
  N1: D1.anode, OA1.OUTPUT
  GND: R1.Pin_0, C1.-, Part1.GND, OA1.V-
  SIGNAL_IN: Part1.A0, OA1.+INPUT
  VCC: Part1.5V, OA1.V+
  N2: OA1.+OFFSET, OA1.NC

custom parts:
  LM741: General Purpose Operational Amplifier
