# Fritzing sketch TS3A5018 (saved by Fritzing 0.9.2b)
breadboards: 1

parts:
  Part1 = Arduino Uno (Rev3)
  IC1 = IC, DIP package, 16 pins [chip_label=TS3A5018]
  IC2 = 555 Timer [package="DIP8 [THT]"]
  C1 = Ceramic Capacitor [capacitance=100nF package="100 mil [THT, multilayer]"]
  R1 = Resistor [tolerance=±5% resistance=1k package=THT]
  R2 = Resistor [tolerance=±5% resistance=1k package=THT]
  C2 = Electrolytic Capacitor [capacitance=1µF package="100 mil [THT, electrolytic]"]
  C3 = Electrolytic Capacitor [capacitance=2.2µF package="100 mil [THT, electrolytic]"]
  LED1 = LED - 5mm [color="Red (633nm)" package="5 mm [THT]"]
  R3 = Resistor [tolerance=±5% resistance=220 package=THT]
  LED2 = LED - 5mm [color="Green (555nm)" package="5 mm [THT]"]
  R4 = Resistor [tolerance=±5% resistance=2.2k package=THT]
  R5 = Resistor [tolerance=±5% resistance=4.7k package=THT]

nets:
  GND: Part1.GND, IC1.pin8, IC1.pin15, IC2.Ground, C1.0, C2.-, C3.-, LED1.cathode, LED2.cathode, R5.Pin_1
  N1: Part1.D2, R4.Pin_0
  VCC: Part1.3V3, IC1.pin16, IC2.Reset, IC2.Vcc_Supply_Voltage, R1.Pin_0
  SIGNAL: IC1.pin1, R4.Pin_1, R5.Pin_0
  N2: IC1.pin2, LED1.anode
  N3: IC1.pin3, LED2.anode
  N4: IC1.pin4, R3.Pin_1
  N5: IC1.pin12, IC2.Trigger, IC2.Threshold, R2.Pin_1
  N6: IC1.pin13, C3.+
  N7: IC1.pin14, C2.+
  N8: IC2.Output, R3.Pin_0
  N9: IC2.Control_Voltage, C1.1
  N10: IC2.Discharge, R1.Pin_1, R2.Pin_0
