# Fritzing sketch 4bitSynchronousCounter (saved by Fritzing 0.9.2b)
breadboards: 1

parts:
  IC1 = IC, DIP package, 16 pins [chip_label=74LS161]
  IC2 = IC, DIP package, 20 pins [chip_label=74LS245]
  R1 = Resistor [tolerance=±5% resistance=220 package=THT]
  LED1 = LED - 5mm [color="Red (633nm)" package="5 mm [THT]"]
  5V = Power plug
  LED2 = LED - 5mm [color="Red (633nm)" package="5 mm [THT]"]
  LED3 = LED - 5mm [color="Red (633nm)" package="5 mm [THT]"]
  LED4 = LED - 5mm [color="Red (633nm)" package="5 mm [THT]"]
  R2 = Resistor [tolerance=±5% resistance=220 package=THT]
  R3 = Resistor [tolerance=±5% resistance=220 package=THT]
  R4 = Resistor [tolerance=±5% resistance=220 package=THT]
  J1 = female pin header, 5 pins [form="♀ (female)"]

nets:
  -CLR: IC1.pin1, J1.pin5
  CLK: IC1.pin2, J1.pin4
  BUS7: IC1.pin3, IC2.pin9
  BUS6: IC1.pin4, IC2.pin8
  BUS5: IC1.pin5, IC2.pin7
  BUS4: IC1.pin6, IC2.pin6
  CE: IC1.pin7, IC1.pin10, J1.pin1
  GND: IC1.pin8, IC2.pin1, IC2.pin10, IC2.pin15, IC2.pin16, IC2.pin17, IC2.pin18, R1.Pin_0, 5V.GND, R2.Pin_0, R3.Pin_0, R4.Pin_0
  -J: IC1.pin9, J1.pin3
  N1: IC1.pin11, IC2.pin14, LED4.anode
  N2: IC1.pin12, IC2.pin13, LED3.anode
  N3: IC1.pin13, IC2.pin12, LED2.anode
  N4: IC1.pin14, IC2.pin11, LED1.anode
  VCC: IC1.pin16, IC2.pin20, 5V.VCC
  BUS0: IC2.pin2
  BUS1: IC2.pin3
  BUS2: IC2.pin4
  BUS3: IC2.pin5
  -CO: IC2.pin19, J1.pin2
  N5: R1.Pin_1, LED1.cathode
  N6: LED2.cathode, R2.Pin_1
  N7: LED3.cathode, R3.Pin_1
  N8: LED4.cathode, R4.Pin_1

notes:
  CE | -CO | -J | CLK | -CLR
