# Fritzing sketch DLatch (saved by Fritzing 0.9.2b)
breadboards: 1

parts:
  IC1 = IC, DIP package, 14 pins [chip_label=74LS00 part_number=74LS00]
  5V = Power plug
  S2 = SWITCH-DPDT [package=os]
  LED3 = LED - 5mm [color="Green (560nm)" package="5 mm [THT]"]
  LED4 = LED - 5mm [color="Blue (470nm)" package="5 mm [THT]"]
  LED1 = LED - 3mm [color="Red (633nm)" package="3 mm [THT]"]
  LED2 = LED - 3mm [color="Green (555nm)" package="3 mm [THT]"]
  R1 = Resistor [tolerance=±5% resistance=470 package=THT]
  R2 = Resistor [tolerance=±5% resistance=470 package=THT]
  R4 = Resistor [tolerance=±5% resistance=470 package=THT]
  R3 = Resistor [tolerance=±5% resistance=470 package=THT]
  S1 = Pushbutton [package="[THT]"]
  R5 = Resistor [tolerance=±5% resistance=1k package=THT]

nets:
  N1: IC1.pin1, IC1.pin10, IC1.pin11
  -Q: IC1.pin2, IC1.pin6, LED4.anode
  Q: IC1.pin3, IC1.pin4, LED3.anode
  N2: IC1.pin5, IC1.pin8
  GND: IC1.pin7, 5V.GND, S2.4, R1.Pin_0, R2.Pin_0, R4.Pin_0, R3.Pin_0, R5.Pin_0
  EN: IC1.pin9, IC1.pin12, S2.5, LED2.anode
  D: IC1.pin13, LED1.anode, S1.Pin_1, S1.Pin_2, R5.Pin_1
  Vcc: IC1.pin14, 5V.VCC, S2.6, S1.Pin_3, S1.Pin_4
  N3: LED3.cathode, R3.Pin_1
  N4: LED4.cathode, R4.Pin_1
  N5: LED1.cathode, R1.Pin_1
  N6: LED2.cathode, R2.Pin_1
