# Fritzing sketch PushPullOutputDriver (saved by Fritzing 1.0.1rc)
breadboards: 1

parts:
  Part1 = Arduino Uno (Rev3)
  Q1 = Basic FET P-Channel [part_number=BS250 package="TO220 [THT]"]
  Q2 = Basic FET N-Channel [part_number=2N7000 package="D2Pak [SMD]"]
  Power = Power plug
  R1 = Resistor [tolerance=±5% power=0.25W resistance=10k package=THT]
  R2 = Resistor [tolerance=±5% power=0.25W resistance=220 package=THT]
  R3 = Resistor [tolerance=±5% power=0.25W resistance=220 package=THT]
  LED1 = LED - 3mm [color="Red (633nm)" current=0.030A package="3 mm [THT]"]
  LED2 = LED - 3mm [color="Green (565nm)" current=0.030A package="3 mm [THT]"]

nets:
  TEST_SIGNAL: Part1.D9_PWM, Q1.gate, Q2.Gate, R1.Pin_0
  GND: Part1.GND, Q2.source, Power.GND, R1.Pin_1, R3.Pin_1
  OUTPUT: Q1.drain, Q2.drain, LED1.anode, LED2.cathode
  5V: Q1.source, Power.VCC, R2.Pin_0
  N1: R2.Pin_1, LED2.anode
  N2: R3.Pin_0, LED1.cathode
