# Fritzing sketch SRLatch (saved by Fritzing 0.9.0b)
breadboards: 1

parts:
  O1_R1 = Resistor [tolerance=±5% resistance=220 package=THT]
  O2_R1 = Resistor [tolerance=±5% resistance=220 package=THT]
  R1a = Resistor [tolerance=±5% resistance=1k package=THT]
  R2a = Resistor [tolerance=±5% resistance=1k package=THT]
  O2_LED = LED - 3mm [color="Red (633nm)" package="3 mm [THT]"]
  VCC1 = Battery block 9V
  Q1 = NPN-Transistor [part_number=S9013 package="TO92 [THT]"]
  Q2 = NPN-Transistor [part_number=S9013 package="TO92 [THT]"]
  R1b = Resistor [tolerance=±5% resistance=10k package=THT]
  O1_LED = LED - 3mm [color="Green (555nm)" package="3 mm [THT]"]
  R2b = Resistor [tolerance=±5% resistance=10k package=THT]
  R_R1 = Resistor [tolerance=±5% resistance=10k package=THT]
  S_R1 = Resistor [tolerance=±5% resistance=10k package=THT]
  S1_RESET = Pushbutton [package="[THT]"]
  S2_SET = Pushbutton [package="[THT]"]
  S_R2 = Resistor [tolerance=±5% resistance=100k package=THT]
  R_R2 = Resistor [tolerance=±5% resistance=100k package=THT]

nets:
  Out1: O1_R1.Pin_0, R1a.Pin_1, Q1.C, R1b.Pin_0
  N1: O1_R1.Pin_1, O1_LED.anode
  Out2: O2_R1.Pin_0, R2a.Pin_1, Q2.C, R2b.Pin_1
  N2: O2_R1.Pin_1, O2_LED.anode
  VCC: R1a.Pin_0, R2a.Pin_0, VCC1.+, S1_RESET.Pin_1, S1_RESET.Pin_2, S2_SET.Pin_1, S2_SET.Pin_2
  GND: O2_LED.cathode, VCC1.-, Q1.E, Q2.E, O1_LED.cathode, S_R2.Pin_0, R_R2.Pin_0
  N3: Q1.B, R2b.Pin_0, R_R1.Pin_1
  N4: Q2.B, R1b.Pin_1, S_R1.Pin_0
  RESET: R_R1.Pin_0, S1_RESET.Pin_3, S1_RESET.Pin_4, R_R2.Pin_1
  SET: S_R1.Pin_1, S2_SET.Pin_3, S2_SET.Pin_4, S_R2.Pin_1

notes:
  SET
  RESET
  OUT1
  OUT2
