# Fritzing sketch SRLatchFlipper (saved by Fritzing 0.9.0b)
breadboards: 1

parts:
  O1_R1 = Resistor [tolerance=±5% resistance=220 package=THT]
  O2_R1 = Resistor [tolerance=±5% resistance=220 package=THT]
  R1a = Resistor [tolerance=±5% resistance=1k package=THT]
  R2a = Resistor [tolerance=±5% resistance=1k package=THT]
  O2_LED = LED - 3mm [color="Red (633nm)" package="3 mm [THT]"]
  Q1 = NPN-Transistor [part_number=S9013 package="TO92 [THT]"]
  Q2 = NPN-Transistor [part_number=S9013 package="TO92 [THT]"]
  R1b = Resistor [tolerance=±5% resistance=10k package=THT]
  O1_LED = LED - 3mm [color="Green (555nm)" package="3 mm [THT]"]
  R2b = Resistor [tolerance=±5% resistance=10k package=THT]
  R_R1 = Resistor [tolerance=±5% resistance=10k package=THT]
  S_R1 = Resistor [tolerance=±5% resistance=10k package=THT]
  Part1 = Arduino Uno (Rev3)

nets:
  Out1: O1_R1.Pin_0, R1a.Pin_1, Q1.C, R1b.Pin_0, Part1.A0
  N1: O1_R1.Pin_1, O1_LED.anode
  Out2: O2_R1.Pin_0, R2a.Pin_1, Q2.C, R2b.Pin_1, Part1.A1
  N2: O2_R1.Pin_1, O2_LED.anode
  VCC: R1a.Pin_0, R2a.Pin_0, Part1.5V
  GND: O2_LED.cathode, Q1.E, Q2.E, O1_LED.cathode, Part1.GND
  N3: Q1.B, R2b.Pin_0, R_R1.Pin_1
  N4: Q2.B, R1b.Pin_1, S_R1.Pin_0
  RESET: R_R1.Pin_0, Part1.D7
  SET: S_R1.Pin_1, Part1.D6_PWM

notes:
  SET
  RESET
  OUT1
  OUT2
