# Fritzing sketch SRLatchWithNandGates (saved by Fritzing 0.9.2b)
breadboards: 1

parts:
  IC1 = IC, DIP package, 14 pins [chip_label=74LS00 part_number=74LS00]
  5V = Power plug
  S1 = SWITCH-DPDT [package=os]
  S2 = SWITCH-DPDT [package=os]
  LED3 = LED - 5mm [color="Green (565nm)" package="5 mm [THT]"]
  LED4 = LED - 5mm [color="Red (633nm)" package="5 mm [THT]"]
  LED1 = LED - 3mm [color="Red (633nm)" package="3 mm [THT]"]
  LED2 = LED - 3mm [color="Red (633nm)" package="3 mm [THT]"]
  R1 = Resistor [tolerance=±5% resistance=1k package=THT]
  R2 = Resistor [tolerance=±5% resistance=1k package=THT]
  R4 = Resistor [tolerance=±5% resistance=1k package=THT]
  R3 = Resistor [tolerance=±5% resistance=1k package=THT]

nets:
  S: IC1.pin1, S1.5, LED1.anode
  -Q: IC1.pin2, IC1.pin6, LED4.anode
  Q: IC1.pin3, IC1.pin4, LED3.anode
  R: IC1.pin5, S2.5, LED2.anode
  GND: IC1.pin7, 5V.GND, S1.4, S2.4, R1.Pin_0, R2.Pin_0, R4.Pin_0, R3.Pin_0
  Vcc: IC1.pin14, 5V.VCC, S1.6, S2.6
  N1: LED3.cathode, R3.Pin_1
  N2: LED4.cathode, R4.Pin_1
  N3: LED1.cathode, R1.Pin_1
  N4: LED2.cathode, R2.Pin_1
