# Fritzing sketch SRLatchWithNorGates (saved by Fritzing 0.9.2b)
breadboards: 1

parts:
  IC1 = 74LS02 [package=dil14]
  LED1(Q) = LED - 3mm [color="Green (555nm)" package="3 mm [THT]"]
  LED2(!Q) = LED - 3mm [color="Yellow (595nm)" package="3 mm [THT]"]
  R2 = Resistor [tolerance=±5% resistance=1k package=THT]
  R1 = Resistor [tolerance=±5% resistance=1k package=THT]
  RESET = Pushbutton [package="[THT]"]
  SET = Pushbutton [package="[THT]"]
  R3 = Resistor [tolerance=±5% resistance=10k package=THT]
  R4 = Resistor [tolerance=±5% resistance=10k package=THT]
  5V = Power plug

nets:
  N1: IC1.Y1, IC1.A2, LED1(Q).anode
  N2: IC1.A1, SET.Pin_1, SET.Pin_2, R4.Pin_1
  N3: IC1.B1, IC1.Y2, LED2(!Q).anode
  N4: IC1.B2, RESET.Pin_1, RESET.Pin_2, R3.Pin_1
  GND: IC1.GND, R2.Pin_0, R1.Pin_0, R3.Pin_0, R4.Pin_0, 5V.GND
  Vcc: IC1.VCC, RESET.Pin_3, RESET.Pin_4, SET.Pin_3, SET.Pin_4, 5V.VCC
  N5: LED1(Q).cathode, R1.Pin_1
  N6: LED2(!Q).cathode, R2.Pin_1

notes:
  Set
  Reset

custom parts:
  74LS02: 74LS02 Quad 2-input NOR
