# Fritzing sketch SyncJKCounter (saved by Fritzing 0.9.2b)
breadboards: 2

parts:
  IC1 = IC, DIP package, 14 pins [chip_label=74LS73]
  IC2 = IC, DIP package, 14 pins [chip_label=74LS73]
  5V = Power plug
  U1 = 555 Timer [package="DIP8 [THT]"]
  C1 = Ceramic Capacitor [capacitance=100nF package="100 mil [THT, multilayer]"]
  R1 = Resistor [tolerance=±5% resistance=1k package=THT]
  R2 = Resistor [tolerance=±5% resistance=12k package=THT]
  C2 = Electrolytic Capacitor [capacitance=47µF package="100 mil [THT, electrolytic]"]
  R3 = Resistor [tolerance=±5% resistance=1k package=THT]
  LED1 = LED - 3mm [color="Red (633nm)" package="3 mm [THT]"]
  R4 = Resistor [tolerance=±5% resistance=1k package=THT]
  R5 = Resistor [tolerance=±5% resistance=1k package=THT]
  R6 = Resistor [tolerance=±5% resistance=1k package=THT]
  LED2 = LED - 3mm [color="Red (633nm)" package="3 mm [THT]"]
  LED3 = LED - 3mm [color="Red (633nm)" package="3 mm [THT]"]
  LED4 = LED - 3mm [color="Red (633nm)" package="3 mm [THT]"]
  R7 = Resistor [tolerance=±5% resistance=1k package=THT]
  R8 = Resistor [tolerance=±5% resistance=1k package=THT]
  R9 = Resistor [tolerance=±5% resistance=1k package=THT]
  R10 = Resistor [tolerance=±5% resistance=1k package=THT]
  LED5 = LED - 3mm [color="Red (633nm)" package="3 mm [THT]"]
  LED6 = LED - 3mm [color="Red (633nm)" package="3 mm [THT]"]
  LED7 = LED - 3mm [color="Red (633nm)" package="3 mm [THT]"]
  LED8 = LED - 3mm [color="Red (633nm)" package="3 mm [THT]"]
  IC3 = IC, DIP package, 14 pins [chip_label=74LS73]
  IC4 = IC, DIP package, 14 pins [chip_label=74LS73]
  IC5 = IC, DIP package, 14 pins [chip_label=74LS08]
  IC6 = IC, DIP package, 14 pins [chip_label=74LS08]

nets:
  PULSE: IC1.pin1, IC1.pin5, IC2.pin1, IC2.pin5, U1.Output, IC3.pin1, IC3.pin5, IC4.pin1, IC4.pin5
  VCC: IC1.pin2, IC1.pin3, IC1.pin4, IC1.pin6, IC1.pin14, IC2.pin2, IC2.pin4, IC2.pin6, 5V.VCC, U1.Reset, U1.Vcc_Supply_Voltage, R1.Pin_0, IC3.pin2, IC3.pin4, IC3.pin6, IC4.pin2, IC4.pin4, IC4.pin6, IC5.pin14, IC6.pin14
  Q0: IC1.pin7, IC1.pin10, IC1.pin12, R3.Pin_0, IC5.pin1
  Q1: IC1.pin9, R4.Pin_0, IC5.pin2
  GND: IC1.pin11, IC2.pin11, 5V.GND, U1.Ground, C1.1, C2.-, LED1.cathode, LED2.cathode, LED3.cathode, LED4.cathode, LED5.cathode, LED6.cathode, LED7.cathode, LED8.cathode, IC3.pin11, IC4.pin11, IC5.pin7, IC6.pin7
  Y1: IC2.pin3, IC2.pin14, IC5.pin3, IC5.pin4
  Y2: IC2.pin7, IC2.pin10, IC5.pin6, IC6.pin2
  Q3: IC2.pin9, R6.Pin_0, IC6.pin1
  Q2: IC2.pin12, R5.Pin_0, IC5.pin5
  N1: U1.Trigger, U1.Threshold, R2.Pin_1, C2.+
  N2: U1.Control_Voltage, C1.0
  N3: U1.Discharge, R1.Pin_1, R2.Pin_0
  N4: R3.Pin_1, LED1.anode
  N5: R4.Pin_1, LED2.anode
  N6: R5.Pin_1, LED3.anode
  N7: R6.Pin_1, LED4.anode
  Q4: R7.Pin_0, IC3.pin12, IC6.pin5
  N8: R7.Pin_1, LED5.anode
  Q5: R8.Pin_0, IC3.pin9, IC6.pin13
  N9: R8.Pin_1, LED6.anode
  Q6: R9.Pin_0, IC4.pin12, IC6.pin9
  N10: R9.Pin_1, LED7.anode
  Q7: R10.Pin_0, IC4.pin9
  N11: R10.Pin_1, LED8.anode
  Y3: IC3.pin3, IC3.pin14, IC6.pin3, IC6.pin4
  Y4: IC3.pin7, IC3.pin10, IC6.pin6, IC6.pin12
  Y5: IC4.pin3, IC4.pin14, IC6.pin10, IC6.pin11
  Y6: IC4.pin7, IC4.pin10, IC6.pin8

notes:
  pulse generator (optional)
