# Fritzing sketch XorWithNandGates (saved by Fritzing 0.9.2b)
breadboards: 1

parts:
  Part1 = Arduino Uno (Rev3)
  IC1 = IC, DIP package, 14 pins [chip_label=74LS132]

nets:
  A: Part1.A0, Part1.D5_PWM, IC1.pin1, IC1.pin13
  B: Part1.A1, Part1.D6_PWM, IC1.pin2, IC1.pin10
  OUT: Part1.A2, IC1.pin6
  GND: Part1.GND, IC1.pin7
  VCC: Part1.5V, IC1.pin14
  N1: IC1.pin3, IC1.pin9, IC1.pin12
  N2: IC1.pin4, IC1.pin11
  N3: IC1.pin5, IC1.pin8
