# Fritzing sketch M62429 (saved by Fritzing 0.9.2b)
breadboards: 1

parts:
  Part1 = Arduino Uno (Rev3)
  IC1 = IC, DIP package, 8 pins [chip_label=M62429 part_number=M62429]
  SIGNAL_1kHz/1V = Header 2 [package=jst-2-smd]
  C1 = Ceramic Capacitor [capacitance=100nF package="100 mil [THT, multilayer]"]

nets:
  CLOCK: Part1.D8, IC1.pin5
  DATA: Part1.D7, IC1.pin4
  VCC: Part1.5V, IC1.pin6
  GND: Part1.GND, IC1.pin3, SIGNAL_1kHz/1V.1
  N1: IC1.pin1, IC1.pin8, C1.0
  CH1: IC1.pin2
  CH2: IC1.pin7
  N2: SIGNAL_1kHz/1V.2, C1.1

notes:
  CH1 LEFT
  CH2 RIGHT
  1kHz 1V
