# Fritzing sketch MCP4017 (saved by Fritzing 0.9.2b)
breadboards: 1

parts:
  Part1 = Arduino Uno (Rev3)
  IC1 = IC, DIP package, 6 pins [chip_label=MCP4017]
  R1 = Resistor [tolerance=±5% resistance=10 package=THT]
  R2 = Resistor [tolerance=±5% resistance=10 package=THT]
  R3 = Resistor [tolerance=±5% resistance=10 package=THT]

nets:
  SDA: Part1.A4/SDA, IC1.pin4, R1.Pin_0
  SCL: Part1.A5/SCL, IC1.pin3, R2.Pin_0
  GND/VSS: Part1.GND, IC1.pin2, IC1.pin5
  VDD: Part1.5V, IC1.pin1, R1.Pin_1, R2.Pin_1, R3.Pin_1
  CH1: IC1.pin6, R3.Pin_0

notes:
  CH1
