# Fritzing sketch AND (saved by Fritzing 0.9.2b)
breadboards: 1

parts:
  D1 = Rectifier Diode [part_number=1N4001 package="300 mil [THT]"]
  D2 = Rectifier Diode [part_number=1N4001 package="300 mil [THT]"]
  R1 = Resistor [tolerance=±5% resistance=1k package=THT]
  S1 = Pushbutton [package="[THT]"]
  S2 = Pushbutton [package="[THT]"]
  Part1 = Arduino Uno (Rev3)
  LED1 = LED - 3mm [color="Green (555nm)" package="3 mm [THT]"]
  R2 = Resistor [tolerance=±5% resistance=1k package=THT]
  R3 = Resistor [tolerance=±5% resistance=1k package=THT]
  R4 = Resistor [tolerance=±5% resistance=1k package=THT]

nets:
  A: D1.cathode, S1.Pin_1, S1.Pin_2, Part1.A0, R4.Pin_1
  OUT: D1.anode, D2.anode, R1.Pin_0, Part1.A2, R2.Pin_1
  B: D2.cathode, S2.Pin_3, S2.Pin_4, Part1.A1, R3.Pin_0
  N1: R1.Pin_1, LED1.anode
  GND: S1.Pin_3, S1.Pin_4, S2.Pin_1, S2.Pin_2, Part1.GND, LED1.cathode
  VCC: Part1.5V, R2.Pin_0, R3.Pin_1, R4.Pin_0
