# Fritzing sketch Lcd3Digit (saved by Fritzing 0.9.2b)
breadboards: 1

parts:
  U1 = atmega328 [package=dip]
  XTAL1 = Crystal [frequency="16 Mhz" package=THT]
  C1 = Ceramic Capacitor [capacitance=22pF package="100 mil [THT, multilayer]"]
  C2 = Ceramic Capacitor [capacitance=22pF package="100 mil [THT, multilayer]"]
  R1 = Resistor [tolerance=±5% resistance=10k package=THT]
  3V = Power plug
  RESET = Pushbutton [package="[THT]"]
  IC1 = IC, DIP package, 10 pins [chip_label=LCD3D]
  R2 = Resistor [tolerance=±5% resistance=100k package=THT]
  R3 = Resistor [tolerance=±5% resistance=100k package=THT]
  R4 = Resistor [tolerance=±5% resistance=100k package=THT]
  R5 = Resistor [tolerance=±5% resistance=100k package=THT]
  R6 = Resistor [tolerance=±5% resistance=100k package=THT]
  R7 = Resistor [tolerance=±5% resistance=100k package=THT]
  R8 = Resistor [tolerance=±5% resistance=100k package=THT]
  R9 = Resistor [tolerance=±5% resistance=100k package=THT]

nets:
  N1: U1.RESET, R1.Pin_1, RESET.Pin_1, RESET.Pin_2
  vcc: U1.VCC, U1.AVCC, R1.Pin_0, 3V.VCC, R2.Pin_0, R4.Pin_0, R6.Pin_0, R8.Pin_0
  GND: U1.GND, C1.0, C2.1, 3V.GND, RESET.Pin_3, RESET.Pin_4, R3.Pin_0, R5.Pin_0, R7.Pin_0, R9.Pin_0
  N2: U1.XLAT1, XTAL1.pin_1, C2.0
  N3: U1.XLAT2, XTAL1.pin_0, C1.1
  COM1: U1.D8, IC1.pin10, R2.Pin_1, R3.Pin_1
  COM2: U1.D9_(PWM), IC1.pin9, R4.Pin_1, R5.Pin_1
  COM3: U1.D10_(PWM), IC1.pin8, R6.Pin_1, R7.Pin_1
  COM4: U1.D11_(PWM), IC1.pin7, R8.Pin_1, R9.Pin_1
  SEG1: U1.A0, IC1.pin1
  SEG2: U1.A1, IC1.pin2
  SEG3: U1.A2, IC1.pin3
  SEG4: U1.A3, IC1.pin4
  SEG5: U1.A4, IC1.pin5
  SEG6: U1.A5, IC1.pin6
