# Fritzing sketch SimpleResistiveUsbLoad (saved by Fritzing 0.9.2b)
breadboards: 1

parts:
  R1 = Resistor [tolerance=±5% resistance=4.7k package=THT]
  LED3 = LED - 3mm [color="Red (633nm)" package="3 mm [THT]"]
  J1 = USB Connectors [package=usb-a-h]
  R1_2 = Resistor [tolerance=±5% resistance=4.7 power=10W package=THT]
  R3 = Resistor [tolerance=±5% resistance=2.2 power=10W package=THT]
  S2 = Toggle Switch [package=THT]
  S1 = Toggle Switch [package=THT]
  LED1 = LED - 3mm [color="Red (633nm)" package="3 mm [THT]"]
  LED2 = LED - 3mm [color="Red (633nm)" package="3 mm [THT]"]

nets:
  VBUS: R1.Pin_0, J1.VBUS, R1_2.Pin_1, R3.Pin_0
  N1: R1.Pin_1, LED3.anode, LED1.anode, LED2.anode
  GND: LED3.cathode, J1.GND, S2.L1, S2.COM, S1.L1, S1.COM
  N2: R1_2.Pin_0, S1.L2, LED1.cathode
  N3: R3.Pin_1, S2.L2, LED2.cathode
