# Fritzing sketch MobileRFDetectorKit (saved by Fritzing 0.9.0b)
breadboards: 1

parts:
  D1 = Rectifier Diode [part_number=1SS86 package="300 mil [THT]"]
  ANT1 = Antenna
  LED1 = LED - 5mm [color="Green (570nm)" package="5 mm [THT]"]
  R1 = Resistor [tolerance=±5% resistance=220 package=THT]
  3V-12V = Power plug
  R2 = Resistor [tolerance=±5% resistance=10k package=THT]
  R3 = Resistor [tolerance=±5% resistance=1M package=THT]
  R4 = Resistor [tolerance=±5% resistance=10k package=THT]
  C1 = Ceramic Capacitor [capacitance=10nF package="100 mil [THT, multilayer]"]
  R5 = Resistor [tolerance=±5% resistance=1M package=THT]
  R6 = Resistor [tolerance=±5% resistance=470k package=THT]
  L1 = Inductor [package="400 mil [THT]"]
  C2 = Ceramic Capacitor [capacitance=10nF package="100 mil [THT, multilayer]"]
  Q3 = NPN-Transistor [part_number=S8050 package="TO92 [THT]"]
  Q2 = NPN-Transistor [part_number=S8050 package="TO92 [THT]"]
  Q1 = NPN-Transistor [part_number=S8050 package="TO92 [THT]"]

nets:
  N1: D1.cathode, ANT1.antenna_lead, L1.pin_1
  N2: D1.anode, C2.1
  N3: LED1.cathode, Q1.C
  N4: LED1.anode, R1.Pin_1
  N5: R1.Pin_0, 3V-12V.VCC, R2.Pin_0, R3.Pin_0, R4.Pin_0
  N6: 3V-12V.GND, R6.Pin_1, L1.pin_0, Q3.E, Q2.E, Q1.E
  N7: R2.Pin_1, Q2.C, Q1.B
  N8: R3.Pin_1, C1.1, Q2.B
  N9: R4.Pin_1, C1.0, R5.Pin_0, Q3.C
  N10: R5.Pin_1, R6.Pin_0, C2.0, Q3.B
