# Fritzing sketch RFDetectorProbe (saved by Fritzing 0.9.2b)
breadboards: 1

parts:
  R1 = Resistor [tolerance=±5% resistance=1k package=THT]
  5-9V = Power plug
  LED1 = LED - 3mm [color="Green (555nm)" package="3 mm [THT]"]
  Q1 = NPN-Transistor [part_number=2N3904 package="TO92 [THT]"]
  R2 = Resistor [tolerance=±5% resistance=22k package=THT]
  C2 = Ceramic Capacitor [capacitance=1nF package="100 mil [THT, multilayer]"]
  D1 = Rectifier Diode [part_number=1N60P package="300 mil [THT]"]
  D2 = Rectifier Diode [part_number=1N60P package="300 mil [THT]"]
  C1 = Ceramic Capacitor [capacitance=1nF package="100 mil [THT, multilayer]"]
  ANT1 = Antenna

nets:
  N1: R1.Pin_0, 5-9V.VCC
  N2: R1.Pin_1, LED1.anode
  GND: 5-9V.GND, Q1.E, C2.1, D1.anode
  N3: LED1.cathode, Q1.C
  N4: Q1.B, R2.Pin_1
  N5: R2.Pin_0, C2.0, D2.cathode
  N6: D1.cathode, D2.anode, C1.1
  ANTENNA_OUT: C1.0, ANT1.antenna_lead

notes:
  this is the probe to an antenna or other circuit element that should be carrying RF signals
