# Fritzing sketch 555FallingEdgeDetector (saved by Fritzing 0.9.2b)
breadboards: 1

parts:
  5V = Power plug
  S1 = Pushbutton [package="[THT]"]
  U1 = 555 Timer [package="DIP8 [THT]"]
  C1 = Ceramic Capacitor [capacitance=100nF package="100 mil [THT, multilayer]"]
  R1 = Resistor [tolerance=±5% resistance=10k package=THT]
  LED1 = LED - 3mm [color="Blue (430nm)" package="3 mm [THT]"]
  R2 = Resistor [tolerance=±5% resistance=1k package=THT]
  R3 = Resistor [tolerance=±5% resistance=10k package=THT]
  D1 = Rectifier Diode [part_number=1N4148 package="300 mil [THT]"]
  R4 = Resistor [tolerance=±5% resistance=22k package=THT]
  R5 = Resistor [tolerance=±5% resistance=22k package=THT]
  C2 = Electrolytic Capacitor [capacitance=10µF package="100 mil [THT, electrolytic]"]
  Q1 = PNP-Transistor [part_number=2N3906 package="TO92 [THT]"]
  R6 = Resistor [tolerance=±5% resistance=10k package=THT]
  R7 = Resistor [tolerance=±5% resistance=1k package=THT]

nets:
  GND: 5V.GND, S1.Pin_3, S1.Pin_4, U1.Ground, R3.Pin_0, D1.anode, C2.-, R6.Pin_0
  VCC: 5V.VCC, U1.Reset, U1.Vcc_Supply_Voltage, R1.Pin_1, LED1.anode, R4.Pin_1, Q1.E
  N1: S1.Pin_1, S1.Pin_2, R1.Pin_0, R7.Pin_0
  N2: U1.Trigger, R5.Pin_0, C2.+
  N3: U1.Output, R2.Pin_0
  N4: U1.Threshold, C1.1, R3.Pin_1, D1.cathode
  N5: U1.Discharge, R4.Pin_0, R5.Pin_1
  N6: C1.0, Q1.C, R6.Pin_1
  N7: LED1.cathode, R2.Pin_1
  N8: Q1.B, R7.Pin_1
