# Fritzing sketch XorRcEdgeDetector (saved by Fritzing 0.9.2b)
breadboards: 1

parts:
  5V = Power plug
  IC1 = IC, DIP package, 14 pins [chip_label=74LS86]
  S1 = Pushbutton [package="[THT]"]
  R1 = Resistor [tolerance=±5% resistance=10k package=THT]
  LED1 = LED - 3mm [color="Blue (430nm)" package="3 mm [THT]"]
  R2 = Resistor [tolerance=±5% resistance=1k package=THT]
  R3 = Resistor [tolerance=±5% resistance=10k package=THT]
  C1 = Electrolytic Capacitor [capacitance=1µF package="100 mil [THT, electrolytic]"]

nets:
  GND: 5V.GND, IC1.pin7, R1.Pin_0, LED1.cathode, C1.-
  VCC: 5V.VCC, IC1.pin14, S1.Pin_3, S1.Pin_4
  N1: IC1.pin8, R2.Pin_0
  N2: IC1.pin9, R3.Pin_1, C1.+
  N3: IC1.pin10, S1.Pin_1, S1.Pin_2, R1.Pin_1, R3.Pin_0
  N4: LED1.anode, R2.Pin_1
