# Fritzing sketch SoundLevelTrigger (saved by Fritzing 0.9.2b)
breadboards: 1

parts:
  5V = Power plug
  MIC1 = Microphone
  R1 = Resistor [tolerance=±5% resistance=10k package=THT]
  U1 = TL072/TLE2072 Dual Op. Amp [part_number=TL072 package="DIP8 [THT]"]
  C1 = Electrolytic Capacitor [capacitance=1µF package="100 mil [THT, electrolytic]"]
  R2 = Resistor [tolerance=±5% resistance=2.2k package=THT]
  R3 = Resistor [tolerance=±5% resistance=560k package=THT]
  R4 = Trimmer Potentiometer [maximum_resistance=100kΩ package=THT]
  U2 = SN74LS14N [package="DIP14 [THT]"]
  R5 = Resistor [tolerance=±5% resistance=4.7k package=THT]
  C2 = Electrolytic Capacitor [capacitance=10µF package="100 mil [THT, electrolytic]"]

nets:
  GND: 5V.GND, MIC1.pin2, U1.Pin_3, U1.Pin_4, R4.leg1, U2.GND, R5.Pin_0, C2.-
  VCC: 5V.VCC, R1.Pin_0, U1.Pin_8, R4.leg2, U2.VCC
  N1: MIC1.pin1, R1.Pin_1, C1.+
  CH2: U1.Pin_1, U1.Pin_5, R3.Pin_1
  N2: U1.Pin_2, R2.Pin_1, R3.Pin_0
  N3: U1.Pin_6, R4.wiper
  N4: U1.Pin_7, U2.6A, R5.Pin_1, C2.+
  CH3: C1.-, R2.Pin_0
  CH1/OUTPUT: U2.5Y
  N5: U2.5A, U2.6Y

notes:
  Output

custom parts:
  TL072/TLE2072 Dual Op. Amp: The classic LM 358 Dual Operational Amplifier (Op-Amp). The analog swiss-army knife.
