# Fritzing sketch SingleStageTransmitterKit2 (saved by Fritzing 0.9.2b)
breadboards: 1

parts:
  S1 = Toggle Switch [package=THT]
  C1 = Ceramic Capacitor [capacitance=100nF package="100 mil [THT, multilayer]"]
  R1 = Resistor [tolerance=±5% resistance=2.2k package=THT]
  MIC1 = Microphone
  R2 = Resistor [tolerance=±5% resistance=22k package=THT]
  C3 = Ceramic Capacitor [capacitance=10nF package="100 mil [THT, multilayer]"]
  R3 = Resistor [tolerance=±5% resistance=220 package=THT]
  Q1 = NPN-Transistor [part_number=S9018 package="TO92 [THT]"]
  L1 = Inductor [part_number=5T inductance=64nH package="400 mil [THT]"]
  C5 = Ceramic Capacitor [capacitance=10pF package="100 mil [THT, multilayer]"]
  C7 = Ceramic Capacitor [capacitance=30pF package="100 mil [THT, multilayer]"]
  ANT1 = Antenna
  C6 = Ceramic Capacitor [capacitance=100nF package="100 mil [THT, multilayer]"]
  C4 = Ceramic Capacitor [capacitance=47pF package="100 mil [THT, multilayer]"]
  C6_2 = Ceramic Capacitor [capacitance=30pF package="100 mil [THT, multilayer]"]
  VCC = Battery [part_number=CR2032]

nets:
  +9V: S1.L1, C1.0, R1.Pin_0, R2.Pin_0, L1.pin_0, C4.0
  N1: S1.COM, VCC.+
  GND: C1.1, MIC1.pin1, C3.1, R3.Pin_1, C6_2.1, VCC.-
  N2: R1.Pin_1, MIC1.pin2, C6.1
  N3: R2.Pin_1, C3.0, Q1.B, C6.0
  N4: R3.Pin_0, Q1.E, C5.1, C6_2.0
  N5: Q1.C, L1.pin_1, C5.0, C7.1, C4.1
  ANT: C7.0, ANT1.antenna_lead
