# Fritzing sketch FireflyKit (saved by Fritzing 1.0.1rc)
breadboards: 1

parts:
  Part1 = LilyPad Coin Cell Battery Holder
  S1 = Toggle Switch [package=THT]
  R2 = Resistor [tolerance=±5% power=0.25W resistance=430 package=THT]
  R3 = Resistor [tolerance=±5% power=0.25W resistance=430 package=THT]
  Q1 = NPN-Transistor [part_number=S8550 package="TO92 [THT]"]
  Q2 = NPN-Transistor [part_number=S8550 package="TO92 [THT]"]
  Q3 = NPN-Transistor [part_number=S9014 package="TO92 [THT]"]
  R1 = Photocell (LDR) [power=0.25W dark_resistance_@0.01lx=300kΩ light_resistance_@100lx=400Ω luminance=10lx package=THT]
  R4 = Photocell (LDR) [power=0.25W dark_resistance_@0.01lx=300kΩ light_resistance_@100lx=400Ω luminance=10lx package=THT]
  M1 = Vibration Motor- ROB-08449 [package=vibe-motor-10mm]
  M2 = Vibration Motor- ROB-08449 [package=vibe-motor-10mm]
  R5 = Resistor [tolerance=±5% power=0.25W resistance=100 package=THT]
  R6 = Resistor [tolerance=±5% power=0.25W resistance=3.3k package=THT]
  R7 = Resistor [tolerance=±5% power=0.25W resistance=1.5k package=THT]
  R8 = 12mm Trimmer Potentiometer (Large) [maximum_resistance=10kΩ knob_status=50% power=0.5W package=THT]
  C1 = Electrolytic Capacitor [capacitance=100µF voltage=35V package="100 mil [THT, electrolytic]"]
  U2 = LM358 [part_number=LM358 package=dip08]
  R9 = Resistor [tolerance=±5% power=0.25W resistance=10k package=THT]
  R10 = Resistor [tolerance=±5% power=0.25W resistance=10k package=THT]
  R11 = Resistor [tolerance=±5% power=0.25W resistance=100 package=THT]
  LED = LED - 3mm [color="Blue (525nm)" current=0.030A package="3 mm [THT]"]

nets:
  GND: Part1.-, R1.pin_0, R4.pin_0, M1.-, M2.-, R7.Pin_1, U2.G$1_V-, R11.Pin_1
  N1: Part1.+, S1.COM
  3V: S1.L2, R2.Pin_0, R3.Pin_0, Q1.C, Q2.C, R5.Pin_0, R6.Pin_0
  N2: R2.Pin_1, Q1.B, R1.pin_1
  N3: R3.Pin_1, Q2.B, R4.pin_1
  N4: Q1.E, M1.+
  N5: Q2.E, M2.+
  N6: Q3.E, R11.Pin_0
  N7: Q3.B, R8.leg2, C1.+, U2.G$1_OUT
  N8: Q3.C, LED.cathode
  N9: R5.Pin_1, U2.G$1_V+, LED.anode
  N10: R6.Pin_1, R7.Pin_0, U2.G$1_-IN, U2.G$2_-IN
  N11: R8.leg1, R8.wiper, U2.G$2_+IN, R10.Pin_0
  N12: C1.-, U2.G$1_+IN, R9.Pin_0
  N13: U2.G$2_OUT, R9.Pin_1, R10.Pin_1
