# Fritzing sketch FrequencyCounter (saved by Fritzing 0.9.2b)
breadboards: 3

parts:
  R1 = Resistor [tolerance=±5% resistance=220 package=THT]
  7_Segment = 7 Segment Display
  R2 = Resistor [tolerance=±5% resistance=220 package=THT]
  R3 = Resistor [tolerance=±5% resistance=220 package=THT]
  R4 = Resistor [tolerance=±5% resistance=220 package=THT]
  R5 = Resistor [tolerance=±5% resistance=220 package=THT]
  R6 = Resistor [tolerance=±5% resistance=220 package=THT]
  R7 = Resistor [tolerance=±5% resistance=220 package=THT]
  IC1 = IC, DIP package, 16 pins [chip_label=CD4026]
  IC2 = IC, DIP package, 16 pins [chip_label=CD4026]
  7_Segment1 = 7 Segment Display
  R8 = Resistor [tolerance=±5% resistance=220 package=THT]
  R9 = Resistor [tolerance=±5% resistance=220 package=THT]
  R10 = Resistor [tolerance=±5% resistance=220 package=THT]
  R11 = Resistor [tolerance=±5% resistance=220 package=THT]
  R12 = Resistor [tolerance=±5% resistance=220 package=THT]
  R13 = Resistor [tolerance=±5% resistance=220 package=THT]
  R14 = Resistor [tolerance=±5% resistance=220 package=THT]
  5V = Power plug
  IC3 = IC, DIP package, 14 pins [chip_label=CD4047]
  C3 = Ceramic Capacitor [capacitance=1nF package="100 mil [THT, multilayer]"]
  R15 = Resistor [tolerance=±5% resistance=440k package=THT]
  R16 = Trimmer Potentiometer [maximum_resistance=20kΩ package=THT]
  C4 = Ceramic Capacitor [capacitance=200pF package="100 mil [THT, multilayer]"]
  R17 = Resistor [tolerance=±5% resistance=10k package=THT]
  D3 = Rectifier Diode [part_number=1N4148 package="300 mil [THT]"]
  IC4 = IC, DIP package, 8 pins [chip_label=NE5534P]
  C5 = Ceramic Capacitor [capacitance=10nF package="100 mil [THT, multilayer]"]
  R18 = Trimmer Potentiometer [maximum_resistance=20kΩ package=THT]
  R19 = Resistor [tolerance=±5% resistance=1k package=THT]
  R20 = Resistor [tolerance=±5% resistance=1k package=THT]
  R21 = Resistor [tolerance=±5% resistance=10k package=THT]
  R22 = Resistor [tolerance=±5% resistance=10k package=THT]
  R23 = Resistor [tolerance=±5% resistance=1k package=THT]
  INPUT = Screw terminal - 2 pins [package=THT]

nets:
  A: R1.Pin_0, IC1.pin10
  N1: R1.Pin_1, 7_Segment.Segment_A
  N2: 7_Segment.Segment_E, R5.Pin_1
  N3: 7_Segment.Segment_D, R4.Pin_1
  GND: 7_Segment.common_cathode, IC1.pin8, IC2.pin8, 7_Segment1.common_cathode, 5V.GND, IC3.pin7, IC3.pin8, IC3.pin9, IC3.pin12, R17.Pin_1, D3.anode, IC4.pin4, R20.Pin_0, R21.Pin_1, INPUT.pin2
  N4: 7_Segment.Segment_C, R3.Pin_1
  N5: 7_Segment.Segment_B, R2.Pin_1
  N6: 7_Segment.Segment_F, R6.Pin_1
  N7: 7_Segment.Segment_G, R7.Pin_1
  B: R2.Pin_0, IC1.pin12
  C: R3.Pin_0, IC1.pin13
  D: R4.Pin_0, IC1.pin9
  E: R5.Pin_0, IC1.pin11
  F: R6.Pin_0, IC1.pin6
  G: R7.Pin_0, IC1.pin7
  SIGNAL: IC1.pin1, IC4.pin6
  EN: IC1.pin2, IC1.pin3, IC2.pin2, IC2.pin3, IC3.pin11
  N8: IC1.pin5, IC2.pin1
  RESET: IC1.pin15, IC2.pin15, C4.1, R17.Pin_0, D3.cathode
  VDD: IC1.pin16, IC2.pin16, 5V.VCC, IC3.pin4, IC3.pin5, IC3.pin6, IC3.pin14, IC4.pin7, R19.Pin_0, R22.Pin_1, R23.Pin_1
  F2: IC2.pin6, R13.Pin_1
  G2: IC2.pin7, R14.Pin_1
  D2: IC2.pin9, R11.Pin_1
  A2: IC2.pin10, R8.Pin_0
  E2: IC2.pin11, R12.Pin_1
  B2: IC2.pin12, R9.Pin_0
  C2: IC2.pin13, R10.Pin_0
  N9: 7_Segment1.Segment_E, R12.Pin_0
  N10: 7_Segment1.Segment_D, R11.Pin_0
  N11: 7_Segment1.Segment_C, R10.Pin_1
  N12: 7_Segment1.Segment_DP, R23.Pin_0
  N13: 7_Segment1.Segment_B, R9.Pin_1
  N14: 7_Segment1.Segment_A, R8.Pin_1
  N15: 7_Segment1.Segment_F, R13.Pin_0
  N16: 7_Segment1.Segment_G, R14.Pin_0
  N17: IC3.pin1, C3.0
  N18: IC3.pin2, R15.Pin_1
  N19: IC3.pin3, C3.1, R16.wiper
  N20: IC3.pin10, C4.0
  N21: R15.Pin_0, R16.leg2
  N22: IC4.pin2, R18.wiper
  N23: IC4.pin3, C5.0, R21.Pin_0, R22.Pin_0
  N24: C5.1, INPUT.pin1
  N25: R18.leg1, R19.Pin_1
  N26: R18.leg2, R20.Pin_1

notes:
  this pattern repeated for another 3 digits (without the DP enabled)
