# Fritzing sketch FunctionGenerator324 (saved by Fritzing 0.9.0b)
breadboards: 1

parts:
  Part1 = Arduino Uno (Rev3)
  R1 = Resistor [tolerance=±5% resistance=20k package=THT]
  R2 = Resistor [tolerance=±5% resistance=20k package=THT]
  R3 = Resistor [tolerance=±5% resistance=20k package=THT]
  C1 = Electrolytic Capacitor [capacitance=33µF package="100 mil [THT, electrolytic]"]
  IC1 = LM324 [package=dil16]
  R22 = Resistor [tolerance=±5% resistance=22k package=THT]
  R21 = Resistor [tolerance=±5% resistance=22k package=THT]
  R20 = Resistor [tolerance=±5% resistance=20k package=THT]
  R23 = Resistor [tolerance=±5% resistance=100k package=THT]
  C2 = Electrolytic Capacitor [capacitance=33µF package="100 mil [THT, electrolytic]"]
  R30 = Resistor [tolerance=±5% resistance=20k package=THT]
  R31 = Resistor [tolerance=±5% resistance=20k package=THT]
  R32 = Resistor [tolerance=±5% resistance=20k package=THT]
  C3 = Electrolytic Capacitor [capacitance=10µF package="100 mil [THT, electrolytic]"]
  R33 = Resistor [tolerance=±5% resistance=20k package=THT]
  R40 = Resistor [tolerance=±5% resistance=20k package=THT]
  R43 = Resistor [tolerance=±5% resistance=20k package=THT]
  LED1 = LED - 3mm [color="Green (555nm)" package="3 mm [THT]"]
  R17 = Resistor [tolerance=±5% resistance=220 package=THT]
  R41 = Resistor [tolerance=±5% resistance=20k package=THT]
  R42 = Resistor [tolerance=±5% resistance=20k package=THT]
  R4 = Trimmer Potentiometer [maximum_resistance=20kΩ package=THT]

nets:
  OUT1: Part1.A0, R3.Pin_1, IC1.OUT1, R20.Pin_1, LED1.anode, R4.leg2
  OUT2: Part1.A1, IC1.OUT2, R23.Pin_1, C2.-, R30.Pin_1
  OUT3: Part1.A2, IC1.OUT3, C3.-, R33.Pin_1, R40.Pin_0
  OUT4: Part1.A3, IC1.OUT4, R43.Pin_1
  VCC: Part1.5V, R1.Pin_1, IC1.V+, R21.Pin_1, R31.Pin_0, R41.Pin_0
  GND: Part1.GND, R2.Pin_1, C1.-, IC1.GND, R22.Pin_1, R32.Pin_0, R17.Pin_1, R42.Pin_0
  N1: R1.Pin_0, R2.Pin_0, R3.Pin_0, IC1.IN1+
  N2: C1.+, IC1.IN1-, R4.wiper
  N3: IC1.IN2+, R22.Pin_0, R21.Pin_0
  N4: IC1.IN2-, R20.Pin_0, R23.Pin_0, C2.+
  N5: IC1.IN3-, R30.Pin_0, C3.+, R33.Pin_0
  N6: IC1.IN3+, R31.Pin_1, R32.Pin_1
  N7: IC1.IN4+, R41.Pin_1, R42.Pin_1
  N8: IC1.IN4-, R40.Pin_1, R43.Pin_0
  N9: LED1.cathode, R17.Pin_0

custom parts:
  LM324: LM324 Quad OpAmp
