# Fritzing sketch PPTCPerformance (saved by Fritzing 0.9.2b)
breadboards: 2

parts:
  5V1A = Power plug
  R1 = Resistor [tolerance=±5% resistance=4.7 power=10W package=THT]
  F1 = Resettable Fuse PTC [part_number=200mA package=0603]
  4V1_5A = Power plug
  R2 = Resistor [tolerance=±5% resistance=2.2 power=10W package=THT]
  F2 = Resettable Fuse PTC [part_number=500mA package=0603]

nets:
  N1: 5V1A.GND, R1.Pin_1
  N2: 5V1A.VCC, F1.1
  N3: R1.Pin_0, F1.2
  N4: 4V1_5A.GND, R2.Pin_1
  N5: 4V1_5A.VCC, F2.1
  N6: R2.Pin_0, F2.2

notes:
  200mA PolyFuse Test
  500mA PolyFuse Test
