# Fritzing sketch GeneralCurveTracer (saved by Fritzing 0.9.2b)
breadboards: 1

parts:
  9V = Power plug
  C2 = Ceramic Capacitor [capacitance=4.7nF package="100 mil [THT, multilayer]"]
  C3 = Ceramic Capacitor [capacitance=4.7nF package="100 mil [THT, multilayer]"]
  C1 = Ceramic Capacitor [capacitance=4.7nF package="100 mil [THT, multilayer]"]
  R1 = Resistor [tolerance=±5% resistance=4.7k package=THT]
  R2 = Resistor [tolerance=±5% resistance=3M package=THT]
  Q1 = NPN-Transistor [part_number=2N3904 package="TO92 [THT]"]
  R3 = Resistor [tolerance=±5% resistance=10k package=THT]
  R4 = Resistor [tolerance=±5% resistance=10k package=THT]
  R5 = Resistor [tolerance=±5% resistance=8.2k package=THT]
  R6 = Resistor [tolerance=±5% resistance=1k package=THT]
  S1 = SWITCH-DPDT [package=ayz0202]
  DUT2 = Rectifier Diode [part_number=1N4001 package="300 mil [THT]"]
  DUT1 = Rectifier Diode [part_number=1N4001 package="300 mil [THT]"]
  C4 = Ceramic Capacitor [capacitance=1µF package="100 mil [THT, multilayer]"]

nets:
  GND: 9V.GND, Q1.E, R3.Pin_1, R4.Pin_1, R6.Pin_1
  N1: 9V.VCC, R1.Pin_0
  N2: C2.0, C3.1, R4.Pin_0
  N3: C2.1, C1.1, R3.Pin_0
  N4: C3.0, R2.Pin_1, Q1.B
  N5: C1.0, R1.Pin_1, R2.Pin_0, Q1.C, C4.1
  N6: R5.Pin_0, C4.0
  X: R5.Pin_1, S1.2
  Y: R6.Pin_0, S1.5
  N7: S1.1, DUT1.anode
  N8: S1.3, DUT2.anode
  N9: S1.4, DUT1.cathode
  N10: S1.6, DUT2.cathode

notes:
  X (CH1)
  Y (CH2)
