# Fritzing sketch BazzFuss (saved by Fritzing 0.9.2b)
breadboards: 1

parts:
  INPUT_JACK_6_35MM = AMPHENOL - ACJS-MHDR [package=ACJS-MHDR]
  OUTPUT_JACK_6_35MM = AMPHENOL - ACJS-MHDR [package=ACJS-MHDR]
  VCC1 = Battery block 9V
  D1 = Rectifier Diode [part_number=1N4148 package="300 mil [THT]"]
  C1 = Electrolytic Capacitor [capacitance=4.7µF package="100 mil [THT, electrolytic]"]
  R1 = Resistor [tolerance=±5% resistance=100k package=THT]
  Q1 = NPN-Transistor [part_number=S9013 package="TO92 [THT]"]
  R2 = Rotary Potentiometer (Small) [maximum_resistance=100kΩ package=THT]
  C2 = Ceramic Capacitor [capacitance=100nF package="100 mil [THT, multilayer]"]
  Q2 = NPN-Transistor [part_number=S9013 package="TO92 [THT]"]

nets:
  N1: INPUT_JACK_6_35MM.Sleeve_(1), VCC1.-
  GND: INPUT_JACK_6_35MM.Sleeve_(4), OUTPUT_JACK_6_35MM.Sleeve_(1), R2.leg2, Q2.E
  N2: INPUT_JACK_6_35MM.Tip_(6), C1.-
  N3: OUTPUT_JACK_6_35MM.Tip_(3), R2.wiper
  N4: VCC1.+, R1.Pin_0
  N5: D1.cathode, C1.+, Q1.B
  N6: D1.anode, R1.Pin_1, Q1.C, C2.1, Q2.C
  N7: Q1.E, Q2.B
  N8: R2.leg1, C2.0
