# Fritzing sketch HallEffectSwitch (saved by Fritzing 0.9.2b)
breadboards: 1

parts:
  U1 = HALL-EFFECT [part_number=44E/938 package=sc70]
  LED1 = LED - 5mm [color="Red (633nm)" package="5 mm [THT]"]
  R1 = Resistor [tolerance=±5% resistance=1k package=THT]
  5V = Power plug

nets:
  GND: U1.GND, 5V.GND
  VCC: U1.VCC, R1.Pin_0, 5V.VCC
  N1: U1.OUT, LED1.cathode
  N2: LED1.anode, R1.Pin_1
