# Fritzing sketch HourglassKit (saved by Fritzing 1.0.1rc)
breadboards: 1

parts:
  DC1 = Power plug
  C1 = Ceramic Capacitor [capacitance=330nF voltage=35V package="100 mil [THT, multilayer]"]
  S1 = Toggle Switch [package=THT]
  U1 = IC, DIP package, 16 pins [chip_label=STC15W204S]
  S2 = Pushbutton [package="[THT]"]
  ISP = female pin header, 4 pins [form="♀ (female)"]
  L11 = LED - 3mm [color="Blue (430nm)" current=0.030A package="3 mm [THT]"]
  L12 = LED - 3mm [color="Blue (430nm)" current=0.030A package="3 mm [THT]"]
  L13 = LED - 3mm [color="Blue (430nm)" current=0.030A package="3 mm [THT]"]
  L14 = LED - 3mm [color="Blue (430nm)" current=0.030A package="3 mm [THT]"]
  L15 = LED - 3mm [color="Blue (430nm)" current=0.030A package="3 mm [THT]"]
  L16 = LED - 3mm [color="Blue (430nm)" current=0.030A package="3 mm [THT]"]
  L17 = LED - 3mm [color="Blue (430nm)" current=0.030A package="3 mm [THT]"]
  L18 = LED - 3mm [color="Blue (430nm)" current=0.030A package="3 mm [THT]"]
  L19 = LED - 3mm [color="Blue (430nm)" current=0.030A package="3 mm [THT]"]
  L20 = LED - 3mm [color="Blue (430nm)" current=0.030A package="3 mm [THT]"]
  L1 = LED - 3mm [color="Blue (430nm)" current=0.030A package="3 mm [THT]"]
  L5 = LED - 3mm [color="Blue (430nm)" current=0.030A package="3 mm [THT]"]
  L2 = LED - 3mm [color="Blue (430nm)" current=0.030A package="3 mm [THT]"]
  L3 = LED - 3mm [color="Blue (430nm)" current=0.030A package="3 mm [THT]"]
  L4 = LED - 3mm [color="Blue (430nm)" current=0.030A package="3 mm [THT]"]
  L9 = LED - 3mm [color="Blue (430nm)" current=0.030A package="3 mm [THT]"]
  L7 = LED - 3mm [color="Blue (430nm)" current=0.030A package="3 mm [THT]"]
  L6 = LED - 3mm [color="Blue (430nm)" current=0.030A package="3 mm [THT]"]
  L8 = LED - 3mm [color="Blue (430nm)" current=0.030A package="3 mm [THT]"]
  L10 = LED - 3mm [color="Blue (430nm)" current=0.030A package="3 mm [THT]"]
  L40 = LED - 3mm [color="Blue (430nm)" current=0.030A package="3 mm [THT]"]
  L39 = LED - 3mm [color="Blue (430nm)" current=0.030A package="3 mm [THT]"]
  L38 = LED - 3mm [color="Blue (430nm)" current=0.030A package="3 mm [THT]"]
  L37 = LED - 3mm [color="Blue (430nm)" current=0.030A package="3 mm [THT]"]
  L36 = LED - 3mm [color="Blue (430nm)" current=0.030A package="3 mm [THT]"]
  L30 = LED - 3mm [color="Blue (430nm)" current=0.030A package="3 mm [THT]"]
  L28 = LED - 3mm [color="Blue (430nm)" current=0.030A package="3 mm [THT]"]
  L29 = LED - 3mm [color="Blue (430nm)" current=0.030A package="3 mm [THT]"]
  L26 = LED - 3mm [color="Blue (430nm)" current=0.030A package="3 mm [THT]"]
  L27 = LED - 3mm [color="Blue (430nm)" current=0.030A package="3 mm [THT]"]
  L21 = LED - 3mm [color="Blue (430nm)" current=0.030A package="3 mm [THT]"]
  L31 = LED - 3mm [color="Blue (430nm)" current=0.030A package="3 mm [THT]"]
  L22 = LED - 3mm [color="Blue (430nm)" current=0.030A package="3 mm [THT]"]
  L23 = LED - 3mm [color="Blue (430nm)" current=0.030A package="3 mm [THT]"]
  L24 = LED - 3mm [color="Blue (430nm)" current=0.030A package="3 mm [THT]"]
  L25 = LED - 3mm [color="Blue (430nm)" current=0.030A package="3 mm [THT]"]
  L41 = LED - 3mm [color="Blue (430nm)" current=0.030A package="3 mm [THT]"]
  L42 = LED - 3mm [color="Blue (430nm)" current=0.030A package="3 mm [THT]"]
  L43 = LED - 3mm [color="Blue (430nm)" current=0.030A package="3 mm [THT]"]
  L44 = LED - 3mm [color="Blue (430nm)" current=0.030A package="3 mm [THT]"]
  L46 = LED - 3mm [color="Blue (430nm)" current=0.030A package="3 mm [THT]"]
  L41_2 = LED - 3mm [color="Blue (430nm)" current=0.030A package="3 mm [THT]"]
  L42_2 = LED - 3mm [color="Blue (430nm)" current=0.030A package="3 mm [THT]"]
  L43_2 = LED - 3mm [color="Blue (430nm)" current=0.030A package="3 mm [THT]"]
  L44_2 = LED - 3mm [color="Blue (430nm)" current=0.030A package="3 mm [THT]"]
  L45 = LED - 3mm [color="Blue (430nm)" current=0.030A package="3 mm [THT]"]
  L47 = LED - 3mm [color="Blue (430nm)" current=0.030A package="3 mm [THT]"]
  L48 = LED - 3mm [color="Blue (430nm)" current=0.030A package="3 mm [THT]"]
  L49 = LED - 3mm [color="Blue (430nm)" current=0.030A package="3 mm [THT]"]
  L50 = LED - 3mm [color="Blue (430nm)" current=0.030A package="3 mm [THT]"]
  L51 = LED - 3mm [color="Blue (430nm)" current=0.030A package="3 mm [THT]"]
  L56 = LED - 3mm [color="Blue (430nm)" current=0.030A package="3 mm [THT]"]
  L57 = LED - 3mm [color="Blue (430nm)" current=0.030A package="3 mm [THT]"]
  L52 = LED - 3mm [color="Blue (430nm)" current=0.030A package="3 mm [THT]"]
  L53 = LED - 3mm [color="Blue (430nm)" current=0.030A package="3 mm [THT]"]
  L54 = LED - 3mm [color="Blue (430nm)" current=0.030A package="3 mm [THT]"]
  L55 = LED - 3mm [color="Blue (430nm)" current=0.030A package="3 mm [THT]"]

nets:
  GND: DC1.GND, C1.0, U1.pin8, S2.Pin_1, S2.Pin_2, ISP.pin4
  N1: DC1.VCC, S1.COM
  VCC: C1.1, S1.L1, U1.pin6, ISP.pin1
  P12: U1.pin1, L30.anode, L28.anode, L29.anode, L26.anode, L27.anode, L21.cathode, L22.cathode, L23.cathode, L24.cathode, L25.cathode
  P13: U1.pin2, L40.anode, L39.anode, L38.anode, L37.anode, L36.anode, L31.cathode, L41.cathode, L42.cathode, L43.cathode, L44.cathode
  P14: U1.pin3, L46.anode, L41_2.cathode, L42_2.cathode, L43_2.cathode, L44_2.cathode, L45.cathode, L47.anode, L48.anode, L49.anode, L50.anode
  P15: U1.pin4, L51.cathode, L56.anode, L57.anode, L52.cathode, L53.cathode, L54.cathode, L55.cathode
  P54: U1.pin5
  P55: U1.pin7
  P30/RXD: U1.pin9, ISP.pin2, L11.anode, L16.cathode, L1.anode, L6.cathode, L36.cathode, L26.cathode, L21.anode, L31.anode, L46.cathode, L41_2.anode, L51.anode, L56.cathode
  P31/TXD: U1.pin10, ISP.pin3, L12.anode, L17.cathode, L2.anode, L7.cathode, L37.cathode, L27.cathode, L22.anode, L41.anode, L42_2.anode, L47.cathode, L57.cathode, L52.anode
  P32: U1.pin11, S2.Pin_3, S2.Pin_4
  P33: U1.pin12, L13.anode, L18.cathode, L3.anode, L8.cathode, L38.cathode, L28.cathode, L23.anode, L42.anode, L43_2.anode, L48.cathode, L53.anode
  P36: U1.pin13, L14.anode, L19.cathode, L4.anode, L9.cathode, L39.cathode, L29.cathode, L24.anode, L43.anode, L44_2.anode, L49.cathode, L54.anode
  P37: U1.pin14, L15.anode, L20.cathode, L5.anode, L10.cathode, L40.cathode, L30.cathode, L25.anode, L44.anode, L45.anode, L50.cathode, L55.anode
  P10: U1.pin15, L1.cathode, L5.cathode, L2.cathode, L3.cathode, L4.cathode, L9.anode, L7.anode, L6.anode, L8.anode, L10.anode
  P11: U1.pin16, L11.cathode, L12.cathode, L13.cathode, L14.cathode, L15.cathode, L16.anode, L17.anode, L18.anode, L19.anode, L20.anode
