# Fritzing sketch ICL7660 (saved by Fritzing 1.0.1rc)
breadboards: 1

parts:
  IC1 = IC, DIP package, 8 pins [chip_label=7660 part_number=ICL7660]
  Power = Power plug
  C1 = Electrolytic Capacitor [capacitance=10µF voltage=35V package="100 mil [THT, electrolytic]"]
  C2 = Electrolytic Capacitor [capacitance=10µF voltage=35V package="100 mil [THT, electrolytic]"]
  IC2 = IC, DIP package, 8 pins [chip_label=UA741]
  C3 = Ceramic Capacitor [capacitance=100nF voltage=35V package="100 mil [THT, multilayer]"]
  R = Resistor [tolerance=±5% power=0.25W resistance=10k package=THT]
  R2 = Resistor [tolerance=±5% power=0.25W resistance=10k package=THT]
  R1 = Resistor [tolerance=±5% power=0.25W resistance=10k package=THT]
  C4 = Electrolytic Capacitor [capacitance=10µF voltage=35V package="100 mil [THT, electrolytic]"]

nets:
  N1: IC1.pin2, C1.+
  GND: IC1.pin3, Power.GND, C2.+, C3.0, R2.Pin_0, C4.-
  N2: IC1.pin4, C1.-
  V-: IC1.pin5, C2.-, IC2.pin4
  V+: IC1.pin8, Power.VCC, IC2.pin7, C4.+
  N3: IC2.pin2, C3.1, R.Pin_0
  N4: IC2.pin3, R2.Pin_1, R1.Pin_0
  OSC_OUT: IC2.pin6, R.Pin_1, R1.Pin_1

notes:
  -5V Rail
  +5V Rail
  Demo application - OpAmp Oscillator
  Demo Application
