# Fritzing sketch fc-51-basic-test (saved by Fritzing 1.0.1rc)
breadboards: 1

parts:
  M1 = fc-51 [package=THT]
  5V = Power plug
  Q1 = Basic FET N-Channel [part_number=2N7000 package="TO220 [THT]"]
  R1 = Resistor [tolerance=±5% power=0.25W resistance=1k package=THT]
  LED1 = LED - 3mm [color="Red (633nm)" current=0.030A package="3 mm [THT]"]
  CH1 = Multimeter straight red probe

nets:
  N1: M1.pin1, Q1.gate, CH1.Probe_tip, CH1.Probe_tip_2
  GND: M1.pin2, 5V.GND, Q1.source
  5V: M1.pin3, 5V.VCC, R1.Pin_0
  N2: Q1.drain, LED1.cathode
  N3: R1.Pin_1, LED1.anode

notes:
  CH1
