# Fritzing sketch fc-51-sensor-module (saved by Fritzing 1.0.1rc)
breadboards: 1

parts:
  Part1 = Arduino Uno (Rev3)
  M1 = fc-51 [package=THT]
  CH1 = Multimeter straight red probe
  CH2 = Multimeter straight red probe

nets:
  N1: Part1.D13/SCK, CH2.Probe_tip_2
  N2: Part1.D2, M1.pin1, CH1.Probe_tip_2
  0V: Part1.5V, M1.pin3
  GND: Part1.GND, M1.pin2

notes:
  CH1
  CH2
