# Fritzing sketch ir-photodiodes (saved by Fritzing 1.0.1rc)
breadboards: 1

parts:
  IR-RX = S1133 Si Photodiode [package="8mm Ceramic [THT]"]
  IR-TX = LED - 5mm [color="Infrared (940nm)" current=0.030A package="5 mm [THT]"]
  5V = Power plug
  R1 = Resistor [tolerance=±5% power=0.25W resistance=1k package=THT]
  R2 = Resistor [tolerance=±5% power=0.25W resistance=3.3k package=THT]

nets:
  5V: IR-RX.cathode, 5V.VCC
  CH2: IR-RX.anode, R2.Pin_1
  GND: IR-TX.cathode, 5V.GND, R2.Pin_0
  N1: IR-TX.anode, R1.Pin_1
  CH1/SQUARE_WAVE: R1.Pin_0

notes:
  SQUARE_WAVE IN (CH1)
  DETECTED VOLTAGE (CH2)
