# Fritzing sketch LCResonator (saved by Fritzing 0.9.2b)
breadboards: 1

parts:
  Q1 = 2N7000 FET N-Channel [part_number=J310 package=TO92]
  Q2 = 2N7000 FET N-Channel [part_number=J310 package=TO92]
  9V = Power plug
  R2 = Resistor [tolerance=±5% resistance=2.2k package=THT]
  C3 = Ceramic Capacitor [capacitance=47nF package="100 mil [THT, multilayer]"]
  R3 = Resistor [tolerance=±5% resistance=1k package=THT]
  C2 = Ceramic Capacitor [capacitance=33pF package="100 mil [THT, multilayer]"]
  R1 = Resistor [tolerance=±5% resistance=10k package=THT]
  C1 = Ceramic Capacitor [capacitance=50pF part_number="calibration cap" package="100 mil [THT, multilayer]"]

nets:
  L+: Q1.gate, C2.0, C1.1
  N1: Q1.drain, 9V.VCC, R1.Pin_0
  N2: Q1.source, Q2.source, R2.Pin_0, C3.0
  GND: Q2.gate, 9V.GND, R2.Pin_1, C1.0
  N3: Q2.drain, C2.1, R1.Pin_1
  N4: C3.1, R3.Pin_0
  OUT: R3.Pin_1

custom parts:
  2N7000 FET N-Channel: A 2N7000 MOSFET N-Channel Transistor
