# Fritzing sketch DataSlicer (saved by Fritzing 0.9.2b)
breadboards: 1

parts:
  U1 = LM358 [part_number=LM358 package=dip08]
  5V = Power plug
  R1 = Photocell (LDR) [package=THT]
  R2 = Resistor [tolerance=±5% resistance=10k package=THT]
  R3 = Resistor [tolerance=±5% resistance=100 package=THT]
  R4 = Resistor [tolerance=±5% resistance=100k package=THT]
  R5 = Trimmer Potentiometer [maximum_resistance=1MΩ package=THT]
  LED1 = LED - 5mm [color="Red (633nm)" package="5 mm [THT]"]
  R6 = Resistor [tolerance=±5% resistance=470 package=THT]
  C1 = Electrolytic Capacitor [capacitance=1µF package="100 mil [THT, electrolytic]"]

nets:
  N1: U1.G$1_OUT, LED1.anode
  N2: U1.G$1_-IN, R1.pin_1, R2.Pin_0, R3.Pin_0
  N3: U1.G$1_+IN, R3.Pin_1, R4.Pin_0, C1.+
  GND: U1.G$1_V-, 5V.GND, R2.Pin_1, R5.leg1, R5.wiper, R6.Pin_1, C1.-
  5V: U1.G$1_V+, 5V.VCC, R1.pin_0
  N4: R4.Pin_1, R5.leg2
  N5: LED1.cathode, R6.Pin_0
