# Fritzing sketch DifferentialComparator (saved by Fritzing 0.9.2b)
breadboards: 1

parts:
  U1 = LM358 [part_number=LM358 package=dip08]
  5V = Power plug
  R1 = Photocell (LDR) [package=THT]
  R2 = Resistor [tolerance=±5% resistance=10k package=THT]
  R3 = Resistor [tolerance=±5% resistance=1k package=THT]
  C1 = Ceramic Capacitor [capacitance=100nF package="100 mil [THT, multilayer]"]
  R4 = Resistor [tolerance=±5% resistance=100k package=THT]
  R5 = Trimmer Potentiometer [maximum_resistance=10kΩ package=THT]
  LED1 = LED - 5mm [color="Red (633nm)" package="5 mm [THT]"]
  R6 = Resistor [tolerance=±5% resistance=470 package=THT]
  R7 = Resistor [tolerance=±5% resistance=100k package=THT]

nets:
  N1: U1.G$1_OUT, U1.G$2_+IN, R7.Pin_1
  N2: U1.G$1_-IN, C1.1, R7.Pin_0
  GND: U1.G$1_+IN, U1.G$1_V-, 5V.GND, R2.Pin_1, R5.leg1, R5.wiper, R6.Pin_1
  N3: U1.G$2_-IN, R4.Pin_1, R5.leg2
  N4: U1.G$2_OUT, LED1.anode
  5V: U1.G$1_V+, 5V.VCC, R1.pin_0, R4.Pin_0
  N5: R1.pin_1, R2.Pin_0, R3.Pin_0
  N6: R3.Pin_1, C1.0
  N7: LED1.cathode, R6.Pin_0
