# Fritzing sketch LDRComparator (saved by Fritzing 0.9.0b)
breadboards: 1

parts:
  R1 = Photocell (LDR) [package=THT]
  Part1 = Arduino Uno (Rev3)
  R2 = Rotary Potentiometer (Small) [maximum_resistance=50kΩ package=THT]
  R3 = Resistor [tolerance=±5% resistance=4.7k package=THT]
  R4 = Resistor [tolerance=±5% resistance=4.7k package=THT]
  LED1 = LED - 5mm [color="Red (633nm)" package="5 mm [THT]"]
  R5 = Resistor [tolerance=±5% resistance=4.7k package=THT]
  IC1 = LM324 [package=dil16]

nets:
  N1: R1.pin_0, Part1.5V, R2.leg2, IC1.V+
  N2: R1.pin_1, Part1.A0, R4.Pin_0, IC1.IN1-
  N3: Part1.D7, LED1.anode, IC1.OUT1
  GND: Part1.GND, R3.Pin_1, R4.Pin_1, R5.Pin_1, IC1.GND
  N4: R2.wiper, R3.Pin_0, IC1.IN1+
  N5: LED1.cathode, R5.Pin_0

custom parts:
  LM324: LM324 Quad OpAmp
