# Fritzing sketch LDRStereoTripDetector (saved by Fritzing 0.9.0b)
breadboards: 1

parts:
  R1 = Photocell (LDR) [package=THT]
  R3 = Resistor [tolerance=±5% resistance=4.7k package=THT]
  R4 = Resistor [tolerance=±5% resistance=4.7k package=THT]
  LED1 = LED - 5mm [color="Red (633nm)" package="5 mm [THT]"]
  R5 = Resistor [tolerance=±5% resistance=1k package=THT]
  R2 = Trimmer Potentiometer [maximum_resistance=50kΩ package=THT]
  R6 = Resistor [tolerance=±5% resistance=1k package=THT]
  LED2 = LED - 5mm [color="Red (633nm)" package="5 mm [THT]"]
  R7 = Photocell (LDR) [package=THT]
  R8 = Trimmer Potentiometer [maximum_resistance=50kΩ package=THT]
  R9 = Resistor [tolerance=±5% resistance=4.7k package=THT]
  R10 = Resistor [tolerance=±5% resistance=4.7k package=THT]
  IC1 = LM324 [part_number=LM324N package=dil16]
  VCC1 = 4 x AAA Battery Mount

nets:
  N1: R1.pin_0, R2.leg2, R7.pin_0, R8.leg2, IC1.V+, VCC1.+
  N2: R1.pin_1, R4.Pin_0, IC1.IN1-
  N3: R3.Pin_0, R2.wiper, IC1.IN1+
  GND: R3.Pin_1, R4.Pin_1, LED1.cathode, LED2.cathode, R9.Pin_1, R10.Pin_1, IC1.GND, VCC1.-
  N4: LED1.anode, R5.Pin_1
  N5: R5.Pin_0, IC1.OUT1
  N6: R6.Pin_0, IC1.OUT2
  N7: R6.Pin_1, LED2.anode
  N8: R7.pin_1, R10.Pin_0, IC1.IN2-
  N9: R8.wiper, R9.Pin_0, IC1.IN2+

custom parts:
  LM324: LM324 Quad OpAmp
