# Fritzing sketch ACBulb (saved by Fritzing 0.9.0b)

parts:
  JACK1 = 2.1mm Barrel Jack with Terminal Block
  C1 = Ceramic Capacitor [capacitance=0.68µF package="100 mil [THT, multilayer]"]
  R1 = Resistor [tolerance=±5% resistance=390k package=THT]
  R2 = Resistor [tolerance=±5% resistance=390k package=THT]
  C2 = Electrolytic Capacitor [capacitance=4.7µF package="100 mil [THT, electrolytic]"]
  D1 = Rectifier Diode [part_number=1N4001 package="300 mil [THT]"]
  D2 = Rectifier Diode [part_number=1N4001 package="300 mil [THT]"]
  D3 = Rectifier Diode [part_number=1N4001 package="300 mil [THT]"]
  D4 = Rectifier Diode [part_number=1N4001 package="300 mil [THT]"]
  R3 = Resistor [tolerance=±5% resistance=100 package=THT]
  LED1_x_38 = LED - 3mm [color="White (4500K)" package="3 mm [THT]"]

nets:
  N1: JACK1.POS, C1.0, R1.Pin_0
  N2: JACK1.NEG, D2.cathode, D4.anode
  N3: C1.1, R1.Pin_1, D1.anode, D3.cathode
  N4: R2.Pin_0, C2.+, D1.cathode, D4.cathode, R3.Pin_0
  N5: R2.Pin_1, C2.-, D2.anode, D3.anode, LED1_x_38.cathode
  N6: R3.Pin_1, LED1_x_38.anode

notes:
  Mains AC (230V 50Hz)
