# Fritzing sketch CandleEmulator (saved by Fritzing 0.9.2b)
breadboards: 1

parts:
  Part1 = Arduino Uno (Rev3)
  LED1 = LED - 5mm [color="Yellow (595nm)" package="5 mm [THT]"]
  R1 = Resistor [tolerance=±5% resistance=220 package=THT]

nets:
  N1: Part1.D11_PWM/MOSI, R1.Pin_0
  GND: Part1.GND, LED1.cathode
  N2: LED1.anode, R1.Pin_1
