# Fritzing sketch CandleLED (saved by Fritzing 1.0.1rc)
breadboards: 1

parts:
  CandleLED = LED - 5mm [color="Red (633nm)" current=0.030A package="5 mm [THT]"]
  CR2032 = Battery Holders [package=battcom_20mm_pth]

nets:
  GND: CandleLED.cathode, CR2032.-
  N1: CandleLED.anode, CR2032.+
