# Fritzing sketch DecorativeFlashingLED (saved by Fritzing 1.0.1rc)
breadboards: 1

parts:
  RGBFastFlashLED = LED - 5mm [color="Red (633nm)" current=0.030A package="5 mm [THT]"]
  LR41x3(4_5V) = FKIT-COIN_CELL [package=fkit-lir2450-h]
  S1 = SPST Switch [package=switch-spdt-smd]

nets:
  GND: RGBFastFlashLED.cathode, LR41x3(4_5V).NEG
  N1: RGBFastFlashLED.anode, S1.S
  N2: LR41x3(4_5V).POS, S1.P

notes:
  LR41x3
