# Fritzing sketch 555PWM (saved by Fritzing 0.9.2b)
breadboards: 1

parts:
  U1 = 555 Timer [package="DIP8 [THT]"]
  R1 = Resistor [tolerance=±5% resistance=1k package=THT]
  R2 = Trimmer Potentiometer [maximum_resistance=50kΩ package=THT]
  C1 = Ceramic Capacitor [capacitance=100nF package="100 mil [THT, multilayer]"]
  D1 = Rectifier Diode [part_number=1N4148 package="300 mil [THT]"]
  D2 = Rectifier Diode [part_number=1N4148 package="300 mil [THT]"]
  C2 = Ceramic Capacitor [capacitance=100nF package="100 mil [THT, multilayer]"]
  R3 = Resistor [tolerance=±5% resistance=1k package=THT]
  Q1 = Basic FET N-Channel [package="TO220 [THT]"]
  LEDLoad1 = LED - 5mm [color="Red (633nm)" package="5 mm [THT]"]
  LEDLoad2 = LED - 5mm [color="Red (633nm)" package="5 mm [THT]"]
  LEDLoad3 = LED - 5mm [color="Red (633nm)" package="5 mm [THT]"]
  RLoad = Resistor [tolerance=±5% resistance=160 package=THT]
  12V = Power plug

nets:
  GND: U1.Ground, C1.0, C2.1, Q1.source, 12V.GND
  N1: U1.Trigger, U1.Threshold, R2.wiper, C1.1
  N2: U1.Output, R3.Pin_0
  VCC: U1.Reset, U1.Vcc_Supply_Voltage, R1.Pin_0, RLoad.Pin_1, 12V.VCC
  N3: U1.Control_Voltage, C2.0
  N4: U1.Discharge, R1.Pin_1, D1.anode, D2.cathode
  N5: R2.leg1, D2.anode
  N6: R2.leg2, D1.cathode
  N7: R3.Pin_1, Q1.gate
  N8: Q1.drain, LEDLoad3.cathode
  N9: LEDLoad1.cathode, LEDLoad2.anode
  N10: LEDLoad1.anode, RLoad.Pin_0
  N11: LEDLoad2.cathode, LEDLoad3.anode
