# Fritzing sketch FlashingLED (saved by Fritzing 1.0.1rc)
breadboards: 1

parts:
  RedFlash1 = LED - 5mm [color="White (6500K)" current=0.030A package="5 mm [THT]"]
  RedFlash2 = LED - 5mm [color="White (6500K)" current=0.030A package="5 mm [THT]"]
  RedFlash3 = LED - 5mm [color="White (6500K)" current=0.030A package="5 mm [THT]"]
  RGBSlowFlash1 = LED - 5mm [color="White (6500K)" current=0.030A package="5 mm [THT]"]
  RGBSlowFlash2 = LED - 5mm [color="White (6500K)" current=0.030A package="5 mm [THT]"]
  RGBSlowFlash3 = LED - 5mm [color="White (6500K)" current=0.030A package="5 mm [THT]"]
  RGBFastFlash1 = LED - 5mm [color="White (6500K)" current=0.030A package="5 mm [THT]"]
  RGBFastFlash2 = LED - 5mm [color="White (6500K)" current=0.030A package="5 mm [THT]"]
  RGBFastFlash3 = LED - 5mm [color="White (6500K)" current=0.030A package="5 mm [THT]"]
  3V~40mA = Power plug

nets:
  GND: RedFlash1.cathode, RedFlash2.cathode, RedFlash3.cathode, RGBSlowFlash1.cathode, RGBSlowFlash2.cathode, RGBSlowFlash3.cathode, RGBFastFlash1.cathode, RGBFastFlash2.cathode, RGBFastFlash3.cathode, 3V~40mA.GND
  N1: RedFlash1.anode, RedFlash2.anode, RedFlash3.anode, RGBSlowFlash1.anode, RGBSlowFlash2.anode, RGBSlowFlash3.anode, RGBFastFlash1.anode, RGBFastFlash2.anode, RGBFastFlash3.anode, 3V~40mA.VCC

notes:
  Red Flash
  RGB Slow Flash
  RGB
  Fast Flash
