# Fritzing sketch FluorescentRingReplacement (saved by Fritzing 0.9.2b)
breadboards: 1

parts:
  CX = Ceramic Capacitor [capacitance=0.1µF voltage=275V package="100 mil [THT, multilayer]"]
  J1 = Screw terminal - 2 pins [package=THT]
  J2 = Screw terminal - 2 pins [package=THT]
  IC1 = IC, DIP package, 4 pins [chip_label=MB10]
  IC2 = IC, DIP package, 8 pins [chip_label=WS3441 part_number=WS3441]
  C1 = Electrolytic Capacitor [capacitance=6.8µF voltage=0.4kV package="100 mil [THT, electrolytic]"]
  R1 = Resistor [tolerance=±5% resistance=330k package=THT]
  R2 = Resistor [tolerance=±5% resistance=330k package=THT]
  C3 = Ceramic Capacitor [capacitance=860nF package="100 mil [THT, multilayer]"]
  R3 = Resistor [tolerance=±5% resistance=30k package=THT]
  R4 = Resistor [tolerance=±5% resistance=2 package=THT]
  R5 = Resistor [tolerance=±5% resistance=2 package=THT]
  D1 = Rectifier Diode [part_number=ES1J package="300 mil [THT]"]
  L1 = Inductors [package=sru5028]
  C2 = Electrolytic Capacitor [capacitance=3.3µF voltage=0.25kV package="100 mil [THT, electrolytic]"]
  R6 = Resistor [tolerance=±5% resistance=150k package=THT]

nets:
  N1: CX.0, J1.pin1, IC1.pin1
  N2: CX.1, J1.pin2, IC1.pin2
  N3: J2.pin1, IC1.pin3, C1.+, R1.Pin_0, D1.cathode, C2.+, R6.Pin_0
  N4: J2.pin2, L1.2, C2.-, R6.Pin_1
  N5: IC1.pin4, IC2.pin1, IC2.pin3, C1.-, C3.0, R3.Pin_0, R4.Pin_0, R5.Pin_0
  N6: IC2.pin2, R3.Pin_1
  N7: IC2.pin4, R2.Pin_1, C3.1
  N8: IC2.pin5, IC2.pin6, D1.anode, L1.1
  N9: IC2.pin7, IC2.pin8, R4.Pin_1, R5.Pin_1
  N10: R1.Pin_1, R2.Pin_0
