# Fritzing sketch HPDL1414 (saved by Fritzing 0.9.2b)
breadboards: 1

parts:
  Part1 = Arduino Uno (Rev3)
  IC1 = IC, DIP package, 12 pins [chip_label=DL1414]

nets:
  WR: Part1.A0, IC1.pin3
  A0: Part1.A1, IC1.pin5
  A1: Part1.A2, IC1.pin4
  D5: Part1.D8, IC1.pin12
  GND: Part1.GND, IC1.pin7
  D0: Part1.D2, IC1.pin8
  D1: Part1.D3_PWM, IC1.pin9
  D2: Part1.D4, IC1.pin10
  D3: Part1.D5_PWM, IC1.pin11
  D4: Part1.D6_PWM, IC1.pin2
  D6: Part1.D7, IC1.pin1
  VDD: Part1.5V, IC1.pin6
