# Fritzing sketch LED8x8Module (saved by Fritzing 0.9.2b)
breadboards: 3

parts:
  Part1 = Arduino Uno (Rev3)
  U1 = MAX7219 [part_number=MAX7219 package=dil24]
  R1 = Resistor [tolerance=±5% resistance=10k package=THT]
  C1 = Ceramic Capacitor [capacitance=100nF package="100 mil [THT, multilayer]"]
  LED8x8 = LBT2088AH [part_number=1088AS]

nets:
  CS: Part1.D10_PWM/SS, U1.LOAD
  MOSI: Part1.D11_PWM/MOSI, U1.DIN
  SCK: Part1.D13/SCK, U1.CLK
  GND: Part1.GND, U1.GND, U1.GND2, C1.0
  VCC: Part1.5V, U1.VCC, R1.Pin_0, C1.1
  DIG0: U1.DIG0, LED8x8.pin_9
  DIG4: U1.DIG4, LED8x8.pin1
  DIG6: U1.DIG6, LED8x8.pin2
  DIG2: U1.DIG2, LED8x8.pin_8
  DIG3: U1.DIG3, LED8x8.pin_12
  DIG7: U1.DIG7, LED8x8.pin_5
  DIG5: U1.DIG5, LED8x8.pin_7
  DIG1: U1.DIG1, LED8x8.pin_14
  SEGA: U1.SEGA, LED8x8.pin_3
  SEGF: U1.SEGF, LED8x8.pin_15
  SEGB: U1.SEGB, LED8x8.pin_4
  SEGG: U1.SEGG, LED8x8.pin_16
  N1: U1.ISET, R1.Pin_1
  SEGC: U1.SEGC, LED8x8.pin_10
  SEGE: U1.SEGE, LED8x8.pin_11
  SEGDP: U1.SEGDP, LED8x8.pin_13
  SEGD: U1.SEGD, LED8x8.pin_6
