# Fritzing sketch LEDBreadboardModules (saved by Fritzing 1.0.1rc)
breadboards: 1

parts:
  U1 = 555 Timer [package="DIP8 [THT]"]
  LED_Module = female pin header, 9 pins [form="♀ (female)"]
  Power = Power plug
  R1 = Resistor [tolerance=±5% power=0.25W resistance=1k package=THT]
  R2 = Resistor [tolerance=±5% power=0.25W resistance=47k package=THT]
  C1 = Electrolytic Capacitor [capacitance=22µF voltage=35V package="100 mil [THT, electrolytic]"]

nets:
  COM/GND: U1.Ground, LED_Module.pin9, Power.GND, C1.-
  N1: U1.Trigger, U1.Threshold, R2.Pin_1, C1.+
  D1/D2/D3/D4/D5/D6/D7/D8: U1.Output, LED_Module.pin1, LED_Module.pin2, LED_Module.pin3, LED_Module.pin4, LED_Module.pin5, LED_Module.pin6, LED_Module.pin7, LED_Module.pin8
  5V: U1.Reset, U1.Vcc_Supply_Voltage, Power.VCC, R1.Pin_0
  N2: U1.Discharge, R1.Pin_1, R2.Pin_0

notes:
  LED Module
