# Fritzing sketch CurrentRegulator (saved by Fritzing 0.9.2b)
breadboards: 1

parts:
  12V = Power plug
  Q1 = PNP-Transistor [part_number=2N3906 package="TO92 [THT]"]
  R1 = Trimmer Potentiometer [maximum_resistance=1kΩ package=THT]
  R2 = Resistor [tolerance=±5% resistance=10k package=THT]
  C1 = Electrolytic Capacitor [capacitance=100µF package="100 mil [THT, electrolytic]"]
  C2 = Ceramic Capacitor [capacitance=100nF package="100 mil [THT, multilayer]"]
  R3 = Resistor [tolerance=±5% resistance=10 package=THT]
  Q2 = NPN-Transistor [part_number=A42 package="TO92 [THT]"]
  R4 = Resistor [tolerance=±5% resistance=10 package=THT]
  LEDLoad3 = LED - 5mm [color="Red (633nm)" package="5 mm [THT]"]
  RLoad = Resistor [tolerance=±5% resistance=160 package=THT]
  D1 = Schottky Diode [part_number=1N5819 package="300 mil [THT]"]
  R5 = Resistor [tolerance=±5% resistance=10 package=THT]
  R6 = Resistor [tolerance=±5% resistance=10 package=THT]
  LEDLoad1 = LED - 5mm [color="Red (633nm)" package="5 mm [THT]"]
  LEDLoad2 = LED - 5mm [color="Red (633nm)" package="5 mm [THT]"]

nets:
  GND: 12V.GND, R2.Pin_1, C2.0, RLoad.Pin_0
  VCC: 12V.VCC, C1.+, C2.1, R3.Pin_1, R4.Pin_1, D1.anode, R5.Pin_1, R6.Pin_1
  N1: Q1.E, R3.Pin_0, Q2.C, R4.Pin_0, R5.Pin_0, R6.Pin_0
  N2: Q1.B, R1.wiper
  N3: Q1.C, Q2.B
  N4: R1.leg1, D1.cathode
  N5: R1.leg2, R2.Pin_0, C1.-
  N6: Q2.E, LEDLoad1.anode
  N7: LEDLoad3.cathode, RLoad.Pin_1
  N8: LEDLoad3.anode, LEDLoad2.cathode
  N9: LEDLoad1.cathode, LEDLoad2.anode
