# Fritzing sketch xLEDStrobeKit (saved by Fritzing 0.9.2b)
breadboards: 1

parts:
  LED1 = LED - 5mm [color="White (4500K)" package="5 mm [THT]"]
  LED2 = LED - 5mm [color="White (4500K)" package="5 mm [THT]"]
  LED3 = LED - 5mm [color="White (4500K)" package="5 mm [THT]"]
  LED4 = LED - 5mm [color="White (4500K)" package="5 mm [THT]"]
  LED5 = LED - 5mm [color="White (4500K)" package="5 mm [THT]"]
  LED6 = LED - 5mm [color="White (4500K)" package="5 mm [THT]"]
  LED7 = LED - 5mm [color="White (4500K)" package="5 mm [THT]"]
  LED8 = LED - 5mm [color="White (4500K)" package="5 mm [THT]"]
  LED9 = LED - 5mm [color="White (4500K)" package="5 mm [THT]"]
  LED10 = LED - 5mm [color="White (4500K)" package="5 mm [THT]"]
  LED11 = LED - 5mm [color="White (4500K)" package="5 mm [THT]"]
  LED12 = LED - 5mm [color="White (4500K)" package="5 mm [THT]"]
  LED13 = LED - 5mm [color="White (4500K)" package="5 mm [THT]"]
  LED14 = LED - 5mm [color="White (4500K)" package="5 mm [THT]"]
  LED15 = LED - 5mm [color="White (4500K)" package="5 mm [THT]"]
  LED16 = LED - 5mm [color="White (4500K)" package="5 mm [THT]"]
  R1 = Resistor [tolerance=±5% resistance=330 part_number="was 27Ω" package=THT]
  R2 = Resistor [tolerance=±5% resistance=27 package=THT]
  R3 = Resistor [tolerance=±5% resistance=220 part_number="was 27Ω" package=THT]
  LED17 = LED - 5mm [color="Blue (505nm)" package="5 mm [THT]"]
  LED18 = LED - 5mm [color="Blue (505nm)" package="5 mm [THT]"]
  LED19 = LED - 5mm [color="Blue (505nm)" package="5 mm [THT]"]
  LED20 = LED - 5mm [color="Blue (505nm)" package="5 mm [THT]"]
  LED21 = LED - 5mm [color="Blue (505nm)" package="5 mm [THT]"]
  LED22 = LED - 5mm [color="Blue (505nm)" package="5 mm [THT]"]
  LED23 = LED - 5mm [color="Blue (505nm)" package="5 mm [THT]"]
  LED24 = LED - 5mm [color="Blue (505nm)" package="5 mm [THT]"]
  LED25 = LED - 5mm [color="Blue (505nm)" package="5 mm [THT]"]
  LED26 = LED - 5mm [color="Blue (505nm)" package="5 mm [THT]"]
  LED27 = LED - 5mm [color="Blue (505nm)" package="5 mm [THT]"]
  LED28 = LED - 5mm [color="Blue (505nm)" package="5 mm [THT]"]
  LED29 = LED - 5mm [color="Blue (505nm)" package="5 mm [THT]"]
  LED30 = LED - 5mm [color="Blue (505nm)" package="5 mm [THT]"]
  LED31 = LED - 5mm [color="Blue (505nm)" package="5 mm [THT]"]
  LED32 = LED - 5mm [color="Blue (505nm)" package="5 mm [THT]"]
  LED33 = LED - 5mm [color="Red (660nm)" package="5 mm [THT]"]
  LED34 = LED - 5mm [color="Red (660nm)" package="5 mm [THT]"]
  LED35 = LED - 5mm [color="Red (660nm)" package="5 mm [THT]"]
  LED36 = LED - 5mm [color="Red (660nm)" package="5 mm [THT]"]
  LED37 = LED - 5mm [color="Red (660nm)" package="5 mm [THT]"]
  LED38 = LED - 5mm [color="Red (660nm)" package="5 mm [THT]"]
  LED39 = LED - 5mm [color="Red (660nm)" package="5 mm [THT]"]
  LED40 = LED - 5mm [color="Red (660nm)" package="5 mm [THT]"]
  LED41 = LED - 5mm [color="Red (660nm)" package="5 mm [THT]"]
  LED42 = LED - 5mm [color="Red (660nm)" package="5 mm [THT]"]
  LED43 = LED - 5mm [color="Red (660nm)" package="5 mm [THT]"]
  LED44 = LED - 5mm [color="Red (660nm)" package="5 mm [THT]"]
  LED45 = LED - 5mm [color="Red (660nm)" package="5 mm [THT]"]
  LED46 = LED - 5mm [color="Red (660nm)" package="5 mm [THT]"]
  LED47 = LED - 5mm [color="Red (660nm)" package="5 mm [THT]"]
  LED48 = LED - 5mm [color="Red (660nm)" package="5 mm [THT]"]
  Q1 = NPN-Transistor [part_number=S8050 package="TO92 [THT]"]
  Q2 = NPN-Transistor [part_number=S8050 package="TO92 [THT]"]
  Q3 = NPN-Transistor [part_number=S8050 package="TO92 [THT]"]
  12V = Power plug
  U1 = 555 Timer [package="DIP8 [THT]"]
  IC2 = IC, DIP package, 16 pins [chip_label=CD4017 part_number=CD4017]
  R4 = Resistor [tolerance=±5% resistance=10k package=THT]
  R5 = Resistor [tolerance=±5% resistance=10k package=THT]
  R6 = Resistor [tolerance=±5% resistance=10k package=THT]
  R7 = Resistor [tolerance=±5% resistance=2.2k package=THT]
  R8 = Resistor [tolerance=±5% resistance=2.2k package=THT]
  D1 = Rectifier Diode [part_number=1N4148 package="300 mil [THT]"]
  D2 = Rectifier Diode [part_number=1N4148 package="300 mil [THT]"]
  D3 = Rectifier Diode [part_number=1N4148 package="300 mil [THT]"]
  D4 = Rectifier Diode [part_number=1N4148 package="300 mil [THT]"]
  D5 = Rectifier Diode [part_number=1N4148 package="300 mil [THT]"]
  D6 = Rectifier Diode [part_number=1N4148 package="300 mil [THT]"]
  D7 = Rectifier Diode [part_number=1N4148 package="300 mil [THT]"]
  C1 = Ceramic Capacitor [capacitance=100nF package="100 mil [THT, multilayer]"]
  C2 = Electrolytic Capacitor [capacitance=10µF package="100 mil [THT, electrolytic]"]
  R9 = Trimmer Potentiometer [maximum_resistance=50kΩ package=THT]

nets:
  N1: LED1.cathode, LED2.anode
  N2: LED1.anode, LED5.anode, LED9.anode, LED13.anode, R1.Pin_1
  N3: LED2.cathode, LED3.anode
  N4: LED3.cathode, LED4.anode
  SINK_WHITE: LED4.cathode, LED6.cathode, LED10.cathode, LED14.cathode, Q1.C
  N5: LED5.cathode, LED7.anode
  N6: LED6.anode, LED8.cathode
  N7: LED7.cathode, LED8.anode
  N8: LED9.cathode, LED11.anode
  N9: LED10.anode, LED12.cathode
  N10: LED11.cathode, LED12.anode
  N11: LED13.cathode, LED15.anode
  N12: LED14.anode, LED16.cathode
  N13: LED15.cathode, LED16.anode
  VCC: R1.Pin_0, R2.Pin_0, R3.Pin_0, 12V.VCC, U1.Reset, U1.Vcc_Supply_Voltage, IC2.pin16, R7.Pin_1, C1.1
  N14: R2.Pin_1, LED17.anode, LED22.anode, LED25.anode, LED32.anode
  N15: R3.Pin_1, LED33.anode, LED39.anode, LED41.anode, LED47.anode
  N16: LED17.cathode, LED18.anode
  N17: LED18.cathode, LED19.anode
  N18: LED19.cathode, LED20.anode
  SINK_BLUE: LED20.cathode, LED24.cathode, LED27.cathode, LED30.cathode, Q3.C
  N19: LED21.cathode, LED24.anode
  N20: LED21.anode, LED23.cathode
  N21: LED22.cathode, LED23.anode
  N22: LED25.cathode, LED26.anode
  N23: LED26.cathode, LED28.anode
  N24: LED27.anode, LED28.cathode
  N25: LED29.cathode, LED30.anode
  N26: LED29.anode, LED31.cathode
  N27: LED31.anode, LED32.cathode
  N28: LED33.cathode, LED34.anode
  N29: LED34.cathode, LED35.anode
  N30: LED35.cathode, LED36.anode
  SINK_RED: LED36.cathode, LED40.cathode, LED44.cathode, LED45.cathode, Q2.C
  N31: LED37.cathode, LED40.anode
  N32: LED38.anode, LED39.cathode
  N33: LED41.cathode, LED43.anode
  N34: LED42.cathode, LED44.anode
  N35: LED42.anode, LED43.cathode
  N36: LED45.anode, LED48.cathode
  N37: LED46.cathode, LED48.anode
  N38: LED46.anode, LED47.cathode
  GND: Q1.E, Q2.E, Q3.E, 12V.GND, U1.Ground, IC2.pin8, IC2.pin13, IC2.pin15, C1.0, C2.-
  N39: Q1.B, R4.Pin_1
  N40: Q2.B, R5.Pin_1
  N41: Q3.B, R6.Pin_1
  N42: U1.Trigger, U1.Threshold, C2.+, R9.leg1, R9.wiper
  CLOCK: U1.Output, IC2.pin14
  N43: U1.Discharge, R7.Pin_0, R8.Pin_1
  Q0: IC2.pin3, D1.anode
  Q2: IC2.pin4, D2.anode
  Q6: IC2.pin5, D4.anode
  Q8: IC2.pin9, D5.anode, D6.anode, D7.anode
  Q4: IC2.pin10, D3.anode
  CTL_WHITE: R4.Pin_0, D1.cathode, D2.cathode, D5.cathode
  CTL_RED: R5.Pin_0, D3.cathode, D4.cathode, D6.cathode
  CTL_BLUE: R6.Pin_0, D7.cathode
  N44: R8.Pin_0, R9.leg2

notes:
  I haven't laid out the breadboard. See the schematic tab for circuit.
