# Fritzing sketch NonInverting (saved by Fritzing 0.9.0b)
breadboards: 1

parts:
  Part1 = Arduino Uno (Rev3)
  IC2 = IC, DIP package, 14 pins [chip_label=LM324N]
  IC1 = 555 Timer [package="SO8 [SMD]"]
  R1 = Resistor [tolerance=±5% resistance=1k package=THT]
  R2 = Resistor [tolerance=±5% resistance=330k package=THT]
  C1 = Electrolytic Capacitor [capacitance=1µF package="100 mil [THT, electrolytic]"]
  C2 = Ceramic Capacitor [capacitance=100nF package="100 mil [THT, multilayer]"]
  R3 = Resistor [tolerance=±5% resistance=10k package=THT]
  R4 = Resistor [tolerance=±5% resistance=220 package=THT]
  Ra2 = Resistor [tolerance=±5% resistance=10k package=THT]
  Ra1 = Resistor [tolerance=±5% resistance=10k package=THT]

nets:
  N1: Part1.A0, IC2.pin3, R3.Pin_1, R4.Pin_0
  N2: Part1.A1, IC2.pin1, Ra2.Pin_0
  N3: Part1.5V, IC2.pin4, IC1.Pin_4, IC1.Pin_8, R1.Pin_0
  N4: Part1.GND, IC2.pin11, IC1.Pin_1, C1.-, C2.0, R4.Pin_1, Ra1.Pin_1
  N5: IC2.pin2, Ra2.Pin_1, Ra1.Pin_0
  N6: IC1.Pin_2, IC1.Pin_6, R2.Pin_1, C1.+
  N7: IC1.Pin_3, R3.Pin_0
  N8: IC1.Pin_5, C2.1
  N9: IC1.Pin_7, R1.Pin_1, R2.Pin_0
