# Fritzing sketch SplitterBuffer (saved by Fritzing 0.9.2b)
breadboards: 1

parts:
  5-15V = Power plug
  IC1 = LM324 [package=dil16]
  R1 = Resistor [tolerance=±5% resistance=10k package=THT]
  R2 = Resistor [tolerance=±5% resistance=1k package=THT]
  R3 = Trimmer Potentiometer [maximum_resistance=10kΩ package=THT]

nets:
  GND: 5-15V.GND, IC1.GND, R1.Pin_1, R2.Pin_1
  VCC: 5-15V.VCC, IC1.V+
  CH2: IC1.OUT1, IC1.IN1-, R1.Pin_0
  CH1/FG: IC1.IN1+, IC1.IN2+
  CH3: IC1.IN2-, IC1.OUT2, R3.leg1
  N1: R2.Pin_0, R3.wiper

custom parts:
  LM324: LM324 Quad OpAmp
