# Fritzing sketch NonInvertingComparatorWithFeedback (saved by Fritzing 1.0.1rc)
breadboards: 1

parts:
  IC1 = IC, DIP package, 14 pins [chip_label=LM339 part_number=LM339]
  5V = Power plug
  Rvref = 6mm Trimmer Potentiometer [maximum_resistance=500kΩ knob_status=50% power=0.5W package=THT]
  D1 = Rectifier Diode [part_number=1N4148 package="300 mil [THT]"]
  D2 = Rectifier Diode [part_number=1N4148 package="300 mil [THT]"]
  Rfb = 6mm Trimmer Potentiometer [maximum_resistance=500kΩ knob_status=50% power=0.5W package=THT]
  Rin = Resistor [tolerance=±5% power=0.25W resistance=10k package=THT]
  INPUT1 = female pin header, 1 pin [form="♀ (female)"]
  R1pullup = Resistor [tolerance=±5% power=0.25W resistance=1k package=THT]
  LED1 = LED - 3mm [color="Red (633nm)" current=0.030A package="3 mm [THT]"]
  CH2 = Multimeter straight red probe
  CH1 = Multimeter straight red probe
  CH4 = Multimeter straight red probe
  CH3 = Multimeter straight red probe
  C1* = Ceramic Capacitor [capacitance=10pF voltage=35V package="100 mil [THT, multilayer]"]
  C2** = Ceramic Capacitor [capacitance=100pF voltage=35V package="100 mil [THT, multilayer]"]

nets:
  GND: IC1.pin1, IC1.pin6, IC1.pin7, IC1.pin8, IC1.pin9, IC1.pin10, IC1.pin11, IC1.pin12, IC1.pin13, IC1.pin14, 5V.GND, Rvref.leg1, D1.anode, D2.anode, LED1.cathode, C2**.1
  OUTPUT1: IC1.pin2, Rfb.leg1, Rfb.wiper, R1pullup.Pin_1, LED1.anode, CH2.Probe_tip, CH2.Probe_tip_2, C1*.0
  5V: IC1.pin3, 5V.VCC, Rvref.leg2, R1pullup.Pin_0
  IN1: IC1.pin4, D2.cathode, Rfb.leg2, Rin.Pin_1, CH3.Probe_tip, CH3.Probe_tip_2, C1*.1, C2**.0
  Vref: IC1.pin5, Rvref.wiper, D1.cathode, CH4.Probe_tip, CH4.Probe_tip_2
  N1: Rin.Pin_0, INPUT1.pin1, CH1.Probe_tip_2
