# Fritzing sketch SquareWaveOscillator (saved by Fritzing 1.0.1rc)
breadboards: 1

parts:
  U1 = LM393 [package=so08]
  Power = Power plug
  R1 = Resistor [tolerance=±5% power=0.25W resistance=4.7k package=THT]
  C1 = Ceramic Capacitor [capacitance=100nF voltage=35V package="100 mil [THT, multilayer]"]
  R2 = Resistor [tolerance=±5% power=0.25W resistance=100k package=THT]
  R3 = Resistor [tolerance=±5% power=0.25W resistance=100k package=THT]
  R4 = Resistor [tolerance=±5% power=0.25W resistance=100k package=THT]
  R5 = Resistor [tolerance=±5% power=0.25W resistance=100k package=THT]
  Q1 = Basic FET N-Channel [part_number=2N7000 package="D2Pak [SMD]"]
  R6 = Resistor [tolerance=±5% power=0.25W resistance=1k package=THT]
  LED1 = LED - 3mm [color="Green (555nm)" current=0.030A package="3 mm [THT]"]
  CH1 = Multimeter straight red probe

nets:
  N1: U1.G1_OUT, R1.Pin_0, R2.Pin_1, R3.Pin_1, Q1.Gate, CH1.Probe_tip, CH1.Probe_tip_2
  N2: U1.G1_-IN, C1.1, R2.Pin_0
  N3: U1.G1_+IN, R3.Pin_0, R4.Pin_1, R5.Pin_0
  GND: U1.G1_V-, Power.GND, C1.0, R5.Pin_1, Q1.source
  5V: U1.G1_V+, Power.VCC, R1.Pin_1, R4.Pin_0, R6.Pin_0
  N4: Q1.drain, LED1.cathode
  N5: R6.Pin_1, LED1.anode

notes:
  CH1
