# Fritzing sketch LowVoltageRegulator (saved by Fritzing 0.9.2b)
breadboards: 1

parts:
  IC1 = IC, DIP package, 14 pins [chip_label=LM723]
  R1 = Resistor [tolerance=±5% resistance=2k package=THT]
  R2 = Resistor [tolerance=±5% resistance=4.7k package=THT]
  R3 = Resistor [tolerance=±5% resistance=1.4k package=THT]
  C1 = Ceramic Capacitor [capacitance=100pF package="100 mil [THT, multilayer]"]
  Cref = Ceramic Capacitor [capacitance=100nF package="100 mil [THT, multilayer]"]
  12V = Power plug
  Rsc = Resistor [tolerance=±5% resistance=10 package=THT]
  RL = Resistor [tolerance=±5% resistance=220 package=THT]
  LED1 = LED - 5mm [color="Red (633nm)" package="5 mm [THT]"]

nets:
  N1: IC1.pin2, IC1.pin10, Rsc.Pin_1
  REGULATED_OUT: IC1.pin3, R3.Pin_1, Rsc.Pin_0, LED1.anode
  N2: IC1.pin4, R3.Pin_0, C1.1
  N3: IC1.pin5, R1.Pin_1, R2.Pin_0, Cref.0
  Vref: IC1.pin6, R1.Pin_0
  GND: IC1.pin7, R2.Pin_1, Cref.1, 12V.GND, RL.Pin_1
  VIN: IC1.pin11, IC1.pin12, 12V.VCC
  N4: IC1.pin13, C1.0
  N5: RL.Pin_0, LED1.cathode

notes:
  Regulated Output
