# Fritzing sketch QX5252JouleThief (saved by Fritzing 0.9.2b)
breadboards: 1

parts:
  L1 = Inductor [inductance=100µH package="400 mil [THT]"]
  IC1 = IC, DIP package, 4 pins [chip_label=IC part_number=QX5252]
  LED1 = smd LED [color="Blue (430nm)" package="0805 [SMD]"]
  BAT = Battery [part_number="AG8 1.55V"]

nets:
  N1: L1.pin_0, IC1.pin2, BAT.+
  N2: L1.pin_1, IC1.pin4, LED1.anode
  GND: IC1.pin3, LED1.cathode, BAT.-
