# Fritzing sketch QX5252SolarNightLight (saved by Fritzing 0.9.2b)
breadboards: 1

parts:
  L1 = Inductor [inductance=100µH package="400 mil [THT]"]
  IC1 = IC, DIP package, 4 pins [chip_label=IC part_number=QX5252]
  LED1 = smd LED [color="White (8000K)" package="0805 [SMD]"]
  BAT = Battery [part_number="HR03 1.2V"]
  PVC1 = SOLAR-IXYS [package=solarbit-12x1]

nets:
  N1: L1.pin_0, IC1.pin2, BAT.+
  N2: L1.pin_1, IC1.pin4, LED1.anode
  N3: IC1.pin1, PVC1.C
  GND: IC1.pin3, LED1.cathode, BAT.-, PVC1.A
