# Fritzing sketch LittleGem (saved by Fritzing 0.9.2b)
breadboards: 1

parts:
  VCC1 = Battery block 9V
  D1 = Rectifier Diode [part_number=1N4001 package="300 mil [THT]"]
  C1 = Electrolytic Capacitor [capacitance=100µF package="100 mil [THT, electrolytic]"]
  IC1 = LM386 [package=dip08]
  R1 = Trimmer Potentiometer [maximum_resistance=5kΩ package=THT]
  C2 = Electrolytic Capacitor [capacitance=220µF package="100 mil [THT, electrolytic]"]
  R2 = Trimmer Potentiometer [maximum_resistance=50Ω package=THT]
  R3 = Resistor [tolerance=±5% resistance=1k package=THT]
  LED1 = LED - 3mm [color="Green (555nm)" package="3 mm [THT]"]
  R4 = Resistor [tolerance=±5% resistance=10 package=THT]
  C3 = Ceramic Capacitor [capacitance=47nF package="100 mil [THT, multilayer]"]
  JIN = Audio Jack (TRS) 3.5mm [package="4Ucon 08780 [THT]"]
  C4 = Ceramic Capacitor [capacitance=10nF package="100 mil [THT, multilayer]"]
  SPKR1 = Loudspeaker
  R5 = Resistor [tolerance=±5% resistance=22 package=THT]

nets:
  GND: VCC1.-, C1.-, IC1.+INPUT, IC1.GND, R2.leg2, LED1.cathode, C3.0, JIN.Sleeve, SPKR1.pin2, R5.Pin_1
  N1: VCC1.+, D1.anode
  N2: D1.cathode, C1.+, IC1.Vs, R3.Pin_0
  N3: IC1.GAIN, R1.wiper, R1.leg2
  N4: IC1.-INPUT, C4.1
  N5: IC1.Vout, C2.+, R4.Pin_0
  N6: C2.-, R2.leg1, R5.Pin_0
  N7: R2.wiper, SPKR1.pin1
  N8: R3.Pin_1, LED1.anode
  N9: R4.Pin_1, C3.1
  N10: JIN.Tip, C4.0

custom parts:
  LM386: low voltage audio power amplifier
