# Fritzing sketch LowVoltageGlowingLEDs (saved by Fritzing 0.9.2b)
breadboards: 1

parts:
  R1 = Resistor [tolerance=±5% resistance=22k package=THT]
  R2 = Resistor [tolerance=±5% resistance=10k package=THT]
  C1 = Ceramic Capacitor [capacitance=10nF package="100 mil [THT, multilayer]"]
  L1 = Inductor [inductance=1mH package="400 mil [THT]"]
  U1 = Battery Holders [part_number="1.5V AAA" package=battery-aaa]
  Q1 = NPN-Transistor [part_number=2N3904 package="TO92 [THT]"]
  Q2 = NPN-Transistor [part_number=2N3904 package="TO92 [THT]"]
  D1 = Rectifier Diode [part_number=1N5819 package="300 mil [THT]"]
  C2 = Ceramic Capacitor [capacitance=100nF package="100 mil [THT, multilayer]"]
  Q3 = NPN-Transistor [part_number=S9013 package="TO92 [THT]"]
  Q4 = NPN-Transistor [part_number=S9013 package="TO92 [THT]"]
  LED1 = LED - 3mm [color="Yellow (574nm)" package="3 mm [THT]"]
  LED2 = LED - 3mm [color="Yellow (574nm)" package="3 mm [THT]"]
  R3 = Resistor [tolerance=±5% resistance=100k package=THT]
  C3 = Electrolytic Capacitor [capacitance=100µF package="100 mil [THT, electrolytic]"]
  R4 = Resistor [tolerance=±5% resistance=100k package=THT]
  C4 = Electrolytic Capacitor [capacitance=100µF package="100 mil [THT, electrolytic]"]
  C5 = Electrolytic Capacitor [capacitance=22µF package="100 mil [THT, electrolytic]"]
  C6 = Electrolytic Capacitor [capacitance=22µF package="100 mil [THT, electrolytic]"]

nets:
  Vss: R1.Pin_0, R2.Pin_0, L1.pin_0, U1.+
  N1: R1.Pin_1, C1.1, Q1.B
  N2: R2.Pin_1, Q1.C, Q2.B
  N3: C1.0, L1.pin_1, Q2.C, D1.anode
  GND: U1.-, Q1.E, Q2.E, C2.0, Q3.E, Q4.E
  Vg: D1.cathode, C2.1, LED1.anode, LED2.anode, R3.Pin_0, R4.Pin_0
  TP1: Q3.B, R4.Pin_1, C4.+, C5.+
  TP2: Q3.C, LED1.cathode, C3.-, C5.-
  N4: Q4.B, R3.Pin_1, C3.+, C6.+
  N5: Q4.C, LED2.cathode, C4.-, C6.-

notes:
  Yes seriously .. powered by just a 1.5V AA or AA cell
