# Fritzing sketch Chaser (saved by Fritzing 0.9.2b)
breadboards: 1

parts:
  IC1 = IC, DIP package, 20 pins [chip_label=MCP2200]
  S1 = Pushbutton [package="[THT]"]
  LED1 = LED - 5mm [color="Red (633nm)" package="5 mm [THT]"]
  R1 = Resistor [tolerance=±5% resistance=1k package=THT]
  LED2 = LED - 5mm [color="Red (633nm)" package="5 mm [THT]"]
  LED3 = LED - 5mm [color="Red (633nm)" package="5 mm [THT]"]
  LED4 = LED - 5mm [color="Red (633nm)" package="5 mm [THT]"]
  LED6 = LED - 5mm [color="Red (633nm)" package="5 mm [THT]"]
  LED7 = LED - 5mm [color="Red (633nm)" package="5 mm [THT]"]
  R2 = Resistor [tolerance=±5% resistance=1k package=THT]
  R3 = Resistor [tolerance=±5% resistance=1k package=THT]
  R4 = Resistor [tolerance=±5% resistance=1k package=THT]
  R5 = Resistor [tolerance=±5% resistance=1k package=THT]
  R6 = Resistor [tolerance=±5% resistance=1k package=THT]
  R7 = Resistor [tolerance=±5% resistance=1k package=THT]
  R8 = Resistor [tolerance=±5% resistance=10k package=THT]
  C1 = Ceramic Capacitor [capacitance=100nF package="100 mil [THT, multilayer]"]
  LED5 = LED - 5mm [color="Red (633nm)" package="5 mm [THT]"]

nets:
  VDD: IC1.pin1, R1.Pin_0, R2.Pin_0, R3.Pin_0, R4.Pin_0, R5.Pin_0, R6.Pin_0, R7.Pin_0, R8.Pin_0
  GP7: IC1.pin5, LED7.cathode
  GP6: IC1.pin6, LED6.cathode
  GP5: IC1.pin7, LED5.cathode
  GP4: IC1.pin8, LED4.cathode
  GP3: IC1.pin9, LED3.cathode
  GP2: IC1.pin14, LED2.cathode
  GP1: IC1.pin15, LED1.cathode
  N1: IC1.pin16, S1.Pin_3, S1.Pin_4, R8.Pin_1, C1.1
  GND: IC1.pin20, S1.Pin_1, S1.Pin_2, C1.0
  N2: LED1.anode, R1.Pin_1
  N3: LED2.anode, R2.Pin_1
  N4: LED3.anode, R3.Pin_1
  N5: LED4.anode, R4.Pin_1
  N6: LED6.anode, R6.Pin_1
  N7: LED7.anode, R7.Pin_1
  N8: R5.Pin_1, LED5.anode

notes:
  not showing MCP2200 support circuits and USB connection
