# Fritzing sketch DevKit (saved by Fritzing 0.9.2b)
breadboards: 1

parts:
  Part1 = Arduino Uno (Rev3)
  IC1 = IC, DIP package, 20 pins [chip_label=MCP2200]

nets:
  N1: Part1.D0/RX, IC1.pin10
  N2: Part1.D1/TX, IC1.pin11
  GND: Part1.GND, IC1.pin20

notes:
  not showing MCP2200 support circuits and USB connection
