# Fritzing sketch MCP23S17 (saved by Fritzing 0.9.2b)
breadboards: 1

parts:
  Part1 = Arduino Uno (Rev3)
  IC1 = IC, DIP package, 28 pins [chip_label=MCP23S17]
  LED1 = LED - 5mm [color="Green (570nm)" package="5 mm [THT]"]
  LED2 = LED - 5mm [color="Red (633nm)" package="5 mm [THT]"]
  R1 = Resistor [tolerance=±5% resistance=1k package=THT]
  R2 = Resistor [tolerance=±5% resistance=1k package=THT]
  R3 = Resistor [tolerance=±5% resistance=10k package=THT]
  S1 = Pushbutton [package=THT]
  LED3 = LED - 5mm [color="Yellow (595nm)" package="5 mm [THT]"]
  R4 = Resistor [tolerance=±5% resistance=1k package=THT]

nets:
  MOSI: Part1.D11_PWM/MOSI, IC1.pin13
  MISO: Part1.D12/MISO, IC1.pin14
  SCK: Part1.D13/SCK, IC1.pin12
  GND: Part1.GND, IC1.pin10, IC1.pin15, IC1.pin16, IC1.pin17, R1.Pin_1, R2.Pin_1, S1.leg0, R4.Pin_1
  INTA: Part1.D2, IC1.pin20
  CS: Part1.D7, IC1.pin11
  VDD: Part1.5V, IC1.pin9, IC1.pin18, R3.Pin_0
  OUT3: IC1.pin2, LED3.anode
  OUT2: IC1.pin5, LED2.anode
  IN1: IC1.pin22, R3.Pin_1, S1.leg1
  OUT1: IC1.pin24, LED1.anode
  N1: LED1.cathode, R1.Pin_0
  N2: LED2.cathode, R2.Pin_0
  N3: LED3.cathode, R4.Pin_0

notes:
  slave address 0100000
