# Fritzing sketch Buffer (saved by Fritzing 1.0.1rc)
breadboards: 1

parts:
  R1 = Resistor [tolerance=±5% power=0.25W resistance=10k package=THT]
  Vout = female pin header, 1 pin [form="♀ (female)"]
  Vin = female pin header, 1 pin [form="♀ (female)"]
  IC1 = IC, DIP package, 8 pins [chip_label=MCP601 part_number=MCP601]
  5V = Power plug

nets:
  CH2: R1.Pin_0, Vout.pin1, IC1.pin2, IC1.pin6
  GND: R1.Pin_1, IC1.pin4, 5V.GND
  CH1: Vin.pin1, IC1.pin3
  5V: IC1.pin7, 5V.VCC

notes:
  SIGNAL Generator In/
  CH1
  Vout/CH2
