# Fritzing sketch LightDetector (saved by Fritzing 1.0.1rc)
breadboards: 1

parts:
  IC2 = IC, DIP package, 8 pins [chip_label=MCP601 part_number=MCP601]
  5V = Power plug
  R1 = Resistor [tolerance=±5% power=0.25W resistance=100k package=THT]
  C1 = Ceramic Capacitor [capacitance=10nF voltage=35V package="100 mil [THT, multilayer]"]
  P1 = S1133 Si Photodiode [part_number=2CU84 package="8mm Ceramic [THT]"]
  LED1 = LED - 3mm [color="Red (633nm)" current=0.030A package="3 mm [THT]"]
  R2 = Resistor [tolerance=±5% power=0.25W resistance=1k package=THT]

nets:
  N1: IC2.pin2, R1.Pin_0, C1.0, P1.cathode
  GND: IC2.pin3, IC2.pin4, 5V.GND, P1.anode, LED1.cathode
  OUT: IC2.pin6, R1.Pin_1, C1.1, R2.Pin_0
  VDD: IC2.pin7, 5V.VCC
  N2: LED1.anode, R2.Pin_1
