# Fritzing sketch InvertingAmplifier (saved by Fritzing 0.9.2b)
breadboards: 2

parts:
  Q1 = NPN-Transistor [part_number=2N3904 package="TO92 [THT]"]
  Q2 = NPN-Transistor [part_number=2N3904 package="TO92 [THT]"]
  Q3 = PNP-Transistor [part_number=2N3906 package="TO92 [THT]"]
  Q4 = PNP-Transistor [part_number=2N3906 package="TO92 [THT]"]
  Q5 = NPN-Transistor [part_number=2N3904 package="TO92 [THT]"]
  Q6 = NPN-Transistor [part_number=2N3904 package="TO92 [THT]"]
  Q7 = NPN-Transistor [part_number=2N3904 package="TO92 [THT]"]
  Q8 = PNP-Transistor [part_number=2N3906 package="TO92 [THT]"]
  Q9 = PNP-Transistor [part_number=2N3906 package="TO92 [THT]"]
  Q10 = NPN-Transistor [part_number=2N3904 package="TO92 [THT]"]
  Q11 = NPN-Transistor [part_number=2N3904 package="TO92 [THT]"]
  Q12 = PNP-Transistor [part_number=2N3906 package="TO92 [THT]"]
  Q13 = PNP-Transistor [part_number=2N3906 package="TO92 [THT]"]
  Q14 = NPN-Transistor [part_number=2N3904 package="TO92 [THT]"]
  Q15 = NPN-Transistor [part_number=2N3904 package="TO92 [THT]"]
  Q16 = NPN-Transistor [part_number=2N3904 package="TO92 [THT]"]
  Q17 = NPN-Transistor [part_number=2N3904 package="TO92 [THT]"]
  Q18 = NPN-Transistor [part_number=2N3904 package="TO92 [THT]"]
  Q20 = PNP-Transistor [part_number=2N3906 package="TO92 [THT]"]
  Q22 = NPN-Transistor [part_number=2N3904 package="TO92 [THT]"]
  D1 = Schottky Diode [part_number=1N5817 package="300 mil [THT]"]
  D2 = Schottky Diode [part_number=1N5817 package="300 mil [THT]"]
  R1 = Resistor [tolerance=±5% resistance=1k package=THT]
  R2 = Resistor [tolerance=±5% resistance=1k package=THT]
  R3 = Resistor [tolerance=±5% resistance=51k package=THT]
  R4 = Resistor [tolerance=±5% resistance=4.7k package=THT]
  R5 = Resistor [tolerance=±5% resistance=39k part_number=act:33kΩ+5kΩ+1kΩ package=THT]
  R7 = Resistor [tolerance=±5% resistance=4.7k package=THT]
  R8 = Resistor [tolerance=±5% resistance=7.5k part_number=act:6.8kΩ+680Ω package=THT]
  R9 = Resistor [tolerance=±5% resistance=24 part_number=act:47Ω||47Ω package=THT]
  R10 = Resistor [tolerance=±5% resistance=51 part_number=act:100Ω||100Ω package=THT]
  R11 = Resistor [tolerance=±5% resistance=51 part_number=act:100Ω||100Ω package=THT]
  R12 = Resistor [tolerance=±5% resistance=51k package=THT]
  C1 = Ceramic Capacitor [capacitance=33pF package="100 mil [THT, multilayer]"]
  5-15V = Power plug
  LED1 = LED - 3mm [color="Green (555nm)" package="3 mm [THT]"]
  RL = Resistor [tolerance=±5% resistance=1k package=THT]
  R16 = Trimmer Potentiometer [maximum_resistance=10kΩ package=THT]
  Rf = Resistor [tolerance=±5% resistance=20k package=THT]
  Rin = Resistor [tolerance=±5% resistance=10k package=THT]
  Rd1 = Resistor [tolerance=±5% resistance=10k package=THT]
  Rd2 = Resistor [tolerance=±5% resistance=10k package=THT]

nets:
  N1: Q1.E, D1.anode
  J3_IN+: Q1.B, Rd1.Pin_0, Rd2.Pin_0
  N2: Q1.C, Q2.C, Q8.B, Q8.C, Q9.B
  N3: Q2.E, D2.anode
  J2_IN-: Q2.B, Rf.Pin_0, Rin.Pin_0
  N4: Q3.E, D1.cathode
  N5: Q3.B, Q4.B, Q9.C, Q10.C
  N6: Q3.C, Q5.C, Q7.B
  N7: Q4.E, D2.cathode
  N8: Q4.C, Q6.C, Q16.B, Q22.C, C1.0
  J1_OFFSET: Q5.E, R1.Pin_0
  N9: Q5.B, Q6.B, Q7.E, R3.Pin_0
  J5_OFFSET: Q6.E, R2.Pin_0
  J7_VCC+/VCC: Q7.C, Q8.E, Q9.E, Q12.E, Q13.E, Q14.C, 5-15V.VCC, R16.leg2, Rd1.Pin_1
  N10: Q10.E, R4.Pin_0
  N11: Q10.B, Q11.B, Q11.C, R5.Pin_1
  GND/J4_VCC-: Q11.E, Q20.C, Q22.E, R1.Pin_1, R2.Pin_1, R3.Pin_1, R4.Pin_1, R11.Pin_1, R12.Pin_1, 5-15V.GND, RL.Pin_0, R16.leg1, Rd2.Pin_1
  N12: Q12.B, Q12.C, Q13.B, R5.Pin_0
  N13: Q13.C, Q14.B, Q15.C, Q18.C, R7.Pin_0, C1.1
  N14: Q14.E, Q15.B, R9.Pin_0
  CH2/J6_OUT: Q15.E, R9.Pin_1, R10.Pin_0, LED1.anode, Rf.Pin_1
  N15: Q16.E, Q17.B, R12.Pin_0
  N16: Q16.C, Q17.C, Q18.E, Q20.B, R8.Pin_1
  N17: Q17.E, Q22.B, R11.Pin_0
  N18: Q18.B, R7.Pin_1, R8.Pin_0
  N19: Q20.E, R10.Pin_1
  N20: LED1.cathode, RL.Pin_1
  CH1/FG: R16.wiper, Rin.Pin_1

notes:
  Differential Amplifier
  Bias Generator
  Gain Stage
  Output Stage
  OUT
  IN+
  IN-
  Power Supply
  Inverting Amplifier Circuit
