# Fritzing sketch MeLEDy (saved by Fritzing 0.9.0b)
circuit board: 6cm x 4cm
breadboards: 1

parts:
  C1 = Electrolytic Capacitor [capacitance=47µF package="100 mil [THT, electrolytic]"]
  R1 = Resistor [tolerance=±5% resistance=4.7k package=THT]
  R2 = Resistor [tolerance=±5% resistance=1M package=THT]
  C2 = Electrolytic Capacitor [capacitance=1µF package="100 mil [THT, electrolytic]"]
  MIC1 = Microphone
  R3 = Resistor [tolerance=±5% resistance=10k package=THT]
  Q1 = NPN-Transistor [part_number=S9014 package="TO92 [THT]"]
  Q2 = NPN-Transistor [part_number=S9014 package="TO92 [THT]"]
  LED1 = LED - 3mm [color="Red (633nm)" package="3 mm [THT]"]
  LED2 = LED - 3mm [color="Red (633nm)" package="3 mm [THT]"]
  LED3 = LED - 3mm [color="Red (633nm)" package="3 mm [THT]"]
  LED4 = LED - 3mm [color="Red (633nm)" package="3 mm [THT]"]
  LED5 = LED - 3mm [color="Red (633nm)" package="3 mm [THT]"]
  S1 = SWITCH-DPDT [package=ayz0202]
  Vcc_(3-5V) = Battery
  R4 = Resistor [tolerance=±5% resistance=220 package=THT]
  LED6 = LED - 3mm [color="Green (555nm)" package="3 mm [THT]"]

nets:
  N1: C1.-, MIC1.pin1, Q1.E, Q2.E, Vcc_(3-5V).-, LED6.cathode
  N2: C1.+, R1.Pin_0, R2.Pin_0, R3.Pin_0, LED1.anode, LED2.anode, LED3.anode, LED4.anode, LED5.anode, S1.6, R4.Pin_0
  N3: R1.Pin_1, C2.+, MIC1.pin2
  N4: R2.Pin_1, C2.-, Q1.B
  N5: R3.Pin_1, Q1.C, Q2.B
  N6: Q2.C, LED1.cathode, LED2.cathode, LED3.cathode, LED4.cathode, LED5.cathode
  N7: S1.5, Vcc_(3-5V).+
  N8: R4.Pin_1, LED6.anode
