# Fritzing sketch VoltmeterAmmeterModule (saved by Fritzing 0.9.2b)
breadboards: 1

parts:
  R1 = Resistor [tolerance=±5% resistance=50 power=5W package=THT]
  R2 = Resistor [tolerance=±5% resistance=50 power=5W package=THT]
  R3 = Resistor [tolerance=±5% resistance=50 power=5W package=THT]
  R4 = Resistor [tolerance=±5% resistance=50 power=5W package=THT]
  R5 = Resistor [tolerance=±5% resistance=50 power=5W package=THT]
  Load_Power = Power plug
  Module_Power = Battery block 9V [part_number=4.5-30V]

nets:
  Load+: R1.Pin_0, R2.Pin_0, R3.Pin_0, R4.Pin_0, R5.Pin_0, Load_Power.VCC
  Load-IN: R1.Pin_1, R2.Pin_1, R3.Pin_1, R4.Pin_1, R5.Pin_1
  GND/Load-OUT/Module-: Load_Power.GND, Module_Power.-
  Module+: Module_Power.+

notes:
  Module Power 4.5-30V
  Module Load Connection
