# Fritzing sketch VoltmeterModule (saved by Fritzing 0.9.2b)
breadboards: 1

parts:
  R1 = Trimmer Potentiometer [maximum_resistance=10kΩ package=THT]
  4_5-30V = Power plug
  METER2 = 7-Segment Panel Ammeter

nets:
  Vcc: R1.leg1, 4_5-30V.VCC, METER2.V+
  N1: R1.wiper, METER2.LOAD-
  GND: R1.leg2, 4_5-30V.GND, METER2.GND

notes:
  3-wire Voltmeter (common ground)

custom parts:
  7-Segment Panel Ammeter: 7-Segment Panel Ammeter (0 to 9.99A)
