# Fritzing sketch MinimalLCOscillator (saved by Fritzing 0.9.2b)
breadboards: 1

parts:
  5V = Power plug
  L1 = Inductor [inductance=150µH package="400 mil [THT]"]
  C1 = Ceramic Capacitor [capacitance=47pF package="100 mil [THT, multilayer]"]
  C2 = Ceramic Capacitor [capacitance=100nF package="100 mil [THT, multilayer]"]
  Q1 = 2N7000 FET N-Channel [part_number=J201 package=TO92]
  R1 = Resistor [tolerance=±5% resistance=4.7k package=THT]

nets:
  GND: 5V.GND, L1.pin_0, R1.Pin_1
  N1: 5V.VCC, Q1.drain
  N2: L1.pin_1, C1.0, Q1.gate
  N3: C1.1, C2.1, Q1.source, R1.Pin_0
  SIGNAL: C2.0

custom parts:
  2N7000 FET N-Channel: A 2N7000 MOSFET N-Channel Transistor
