# Fritzing sketch Monostable122 (saved by Fritzing 0.9.0b)
breadboards: 1

parts:
  IC1 = 74LS122 [package=dil14]
  S1 = Pushbutton [package="[THT]"]
  R1 = Resistor [tolerance=±5% resistance=1k package=THT]
  C1 = Ceramic Capacitor [capacitance=100nF package="100 mil [THT, multilayer]"]
  R2 = Resistor [tolerance=±5% resistance=100k package=THT]
  C2 = Electrolytic Capacitor [capacitance=33µF package="100 mil [THT, electrolytic]"]
  LED1 = LED - 3mm [color="Red (633nm)" package="3 mm [THT]"]
  LED2 = LED - 3mm [color="Green (555nm)" package="3 mm [THT]"]
  5V = Power plug
  R3 = Resistor [tolerance=±5% resistance=1k package=THT]

nets:
  GND: IC1.A1, IC1.A2, IC1.GND, IC1.Cext, R1.Pin_1, C1.1, C2.-, 5V.GND, R3.Pin_0
  N1: IC1.B1, S1.Pin_1, S1.Pin_2, R1.Pin_0
  Vcc: IC1.B2, IC1.CLR, IC1.VCC, S1.Pin_3, S1.Pin_4, C1.0, R2.Pin_0, 5V.VCC
  N2: IC1.-Q, LED1.anode
  N3: IC1.Q, LED2.anode
  N4: IC1.Rext/Cext, R2.Pin_1, C2.+
  N5: LED1.cathode, LED2.cathode, R3.Pin_1

custom parts:
  74LS122: 74LS122 Monostable
