# Fritzing sketch MusicBoxKit (saved by Fritzing 0.9.2b)
breadboards: 1

parts:
  Part1 = Arduino Uno (Rev3)
  IC1 = IC, DIP package, 14 pins [chip_label=CD4066]
  IC2 = IC, DIP package, 14 pins [chip_label=CD4011]
  D1 = Rectifier Diode [part_number=1N4007 package="300 mil [THT]"]
  D2 = Rectifier Diode [part_number=1N4148 package="300 mil [THT]"]
  D3 = Rectifier Diode [part_number=1N4148 package="300 mil [THT]"]
  R1 = Resistor [tolerance=±5% resistance=270k package=THT]
  R2 = Resistor [tolerance=±5% resistance=620k package=THT]
  R3 = Resistor [tolerance=±5% resistance=150k package=THT]
  R4 = Resistor [tolerance=±5% resistance=62k package=THT]
  R5 = Resistor [tolerance=±5% resistance=270k package=THT]
  R6 = Resistor [tolerance=±5% resistance=150k package=THT]
  R7 = Resistor [tolerance=±5% resistance=150k package=THT]
  R8 = Resistor [tolerance=±5% resistance=150k package=THT]
  R9 = Resistor [tolerance=±5% resistance=150k package=THT]
  IC3 = IC, DIP package, 10 pins [chip_label=MusicBox]
  Q1 = NPN-Transistor [part_number=S8050 package="TO92 [THT]"]
  J1 = Piezo Speaker
  Q5 = MOSFET-NCHANNEL [part_number=2N7000 package=to-92]
  U1 = SWITCH_SPDT [package=kps-1290]
  U2 = SWITCH_SPDT [package=kps-1290]
  U3 = SWITCH_SPDT [package=kps-1290]
  U4 = SWITCH_SPDT [package=kps-1290]
  R10 = Resistor [tolerance=±5% resistance=1k package=THT]
  LED1 = LED - 5mm [color="Red (660nm)" package="5 mm [THT]"]
  LED2 = LED - 5mm [color="Green (570nm)" package="5 mm [THT]"]
  LED3 = LED - 5mm [color="Green (570nm)" package="5 mm [THT]"]
  LED4 = LED - 5mm [color="Green (570nm)" package="5 mm [THT]"]
  R11 = Resistor [tolerance=±5% resistance=1k package=THT]
  R12 = Resistor [tolerance=±5% resistance=1k package=THT]
  R13 = Resistor [tolerance=±5% resistance=1k package=THT]
  LED5 = LED - 5mm [color="Green (570nm)" package="5 mm [THT]"]
  R14 = Resistor [tolerance=±5% resistance=1k package=THT]

nets:
  MASTER_ON: Part1.D8, Q5.G, LED1.anode
  GND: Part1.GND, Q5.S, R10.Pin_1, R11.Pin_1, R12.Pin_1, R13.Pin_1, R14.Pin_1
  A: Part1.D4, IC1.pin13, IC2.pin13, R6.Pin_0, U1.S, LED2.anode
  B: Part1.D5_PWM, IC1.pin5, IC2.pin12, R7.Pin_0, U2.S, LED3.anode
  C: Part1.D6_PWM, IC2.pin1, IC2.pin5, IC2.pin6, D3.anode, R8.Pin_0, U3.S, LED4.anode
  D: Part1.D7, IC2.pin2, D2.anode, R9.Pin_0, U4.S, LED5.anode
  5V: Part1.5V, D1.anode
  N1: IC1.pin1, R4.Pin_0
  N2: IC1.pin2, IC1.pin3
  N3: IC1.pin4, R5.Pin_0
  CTRLC: IC1.pin6, IC2.pin11
  GNDA: IC1.pin7, IC2.pin7, R3.Pin_1, R6.Pin_1, R7.Pin_1, R8.Pin_1, R9.Pin_1, IC3.pin2, Q1.E, Q5.D
  N4: IC1.pin8, R2.Pin_1, IC3.pin8
  N5: IC1.pin9, R1.Pin_0, R2.Pin_0
  N6: IC1.pin10, IC3.pin6
  N7: IC1.pin11, IC2.pin4
  N8: IC1.pin12, IC2.pin3
  VB: IC1.pin14, IC2.pin14, D1.cathode, IC3.pin7, J1.pin1, U1.P, U2.P, U3.P, U4.P
  N9: IC2.pin8, IC2.pin9, D2.cathode, D3.cathode, R3.Pin_0
  N10: IC2.pin10, IC3.pin1
  N11: R1.Pin_1, R4.Pin_1, R5.Pin_1, IC3.pin9
  N12: IC3.pin4, Q1.B
  N13: Q1.C, J1.pin2
  N14: R10.Pin_0, LED1.cathode
  N15: LED2.cathode, R11.Pin_0
  N16: LED3.cathode, R12.Pin_0
  N17: LED4.cathode, R13.Pin_0
  N18: LED5.cathode, R14.Pin_0

notes:
  lazy - haven't laid out the breadboard (as most is a kit). See schematic page for actual circuit
  Music Box Module
