# Fritzing sketch NOR7402 (saved by Fritzing 0.9.0b)
breadboards: 1

parts:
  Part1 = Arduino Uno (Rev3)
  LED2 = LED - 3mm [color="Green (555nm)" package="3 mm [THT]"]
  R2 = Resistor [tolerance=±5% resistance=1k package=THT]
  IC1 = 74LS02 [package=dil14]

nets:
  A0: Part1.A0, LED2.anode, IC1.Y1
  N1: Part1.D8, IC1.B1
  N2: Part1.D9_PWM, IC1.A1
  Vcc: Part1.5V, IC1.VCC
  GND: Part1.GND, R2.Pin_0, IC1.GND
  N3: LED2.cathode, R2.Pin_1

custom parts:
  74LS02: 74LS02 Quad 2-input NOR
