# Fritzing sketch NORGateOscillator (saved by Fritzing 0.9.2b)
breadboards: 1

parts:
  Part1 = Arduino Uno (Rev3)
  LED2 = LED - 3mm [color="Green (555nm)" package="3 mm [THT]"]
  R2 = Resistor [tolerance=±5% resistance=1k package=THT]
  IC1 = 74LS02 [package=dil14]
  C1 = Electrolytic Capacitor [capacitance=10µF package="100 mil [THT, electrolytic]"]
  R3 = Resistor [tolerance=±5% resistance=47k package=THT]
  R4 = Trimmer Potentiometer [maximum_resistance=50kΩ package=THT]
  R5 = Resistor [tolerance=±5% resistance=2.2k package=THT]
  C2 = Ceramic Capacitor [capacitance=100nF package="100 mil [THT, multilayer]"]

nets:
  A0: Part1.A0, IC1.Y1, IC1.A2, IC1.B2, R5.Pin_1
  A1: Part1.A1, LED2.anode, IC1.Y2, C1.+, C2.0
  A2: Part1.A2, IC1.A1, IC1.B1, R3.Pin_0
  GND: Part1.GND, R2.Pin_0, IC1.GND, C2.1
  Vcc: Part1.5V, IC1.VCC
  N1: LED2.cathode, R2.Pin_1
  N2: C1.-, R3.Pin_1, R4.leg2
  N3: R4.leg1, R4.wiper, R5.Pin_0

custom parts:
  74LS02: 74LS02 Quad 2-input NOR
