# Fritzing sketch MUX (saved by Fritzing 1.0.1rc)
breadboards: 1

parts:
  Part1 = Arduino Uno (Rev3)
  U2 = 4011 4 x 2 Input NAND Gate, single part [part_number=4011 package="DIP (Dual Inline) [THT]"]
  LED1 = LED - 3mm [color="Yellow (585nm)" current=0.030A package="3 mm [THT]"]
  LED2 = LED - 3mm [color="Blue (430nm)" current=0.030A package="3 mm [THT]"]
  LED4 = LED - 3mm [color="Green (555nm)" current=0.030A package="3 mm [THT]"]
  R1 = Resistor [tolerance=±5% power=0.25W resistance=470 package=THT]
  R2 = Resistor [tolerance=±5% power=0.25W resistance=470 package=THT]
  R4 = Resistor [tolerance=±5% power=0.25W resistance=470 package=THT]
  CH4 = Multimeter straight red probe
  CH2 = Multimeter straight red probe
  CH1 = Multimeter straight red probe
  R3 = Resistor [tolerance=±5% power=0.25W resistance=470 package=THT]
  LED3 = LED - 3mm [color="Red (633nm)" current=0.030A package="3 mm [THT]"]
  CH3 = Multimeter straight red probe

nets:
  A: Part1.D2, U2.A1, LED1.anode, CH1.Probe_tip, CH1.Probe_tip_2
  B: Part1.D3_PWM, U2.B4, LED2.anode, CH2.Probe_tip, CH2.Probe_tip_2
  S: Part1.D4, U2.A2, U2.B2, U2.A4, LED3.anode, CH3.Probe_tip, CH3.Probe_tip_2
  5V: Part1.5V, U2.VDD
  GND: Part1.GND, U2.GND, R1.Pin_0, R2.Pin_0, R4.Pin_0, R3.Pin_0
  N1: U2.B1, U2.Q2
  N2: U2.Q1, U2.A3
  N3: U2.B3, U2.Q4
  Q: U2.Q3, LED4.anode, CH4.Probe_tip, CH4.Probe_tip_2
  N4: LED1.cathode, R1.Pin_1
  N5: LED2.cathode, R2.Pin_1
  N6: LED4.cathode, R4.Pin_1
  N7: R3.Pin_1, LED3.cathode

notes:
  Input A (CH1)
  Input B (CH2)
  Output Q (CH4)
  SELECT (CH3)
