# Fritzing sketch NOT (saved by Fritzing 1.0.1rc)
breadboards: 1

parts:
  Part1 = Arduino Uno (Rev3)
  U2 = 4011 4 x 2 Input NAND Gate, single part [part_number=4011 package="DIP (Dual Inline) [THT]"]
  LED1 = LED - 3mm [color="Yellow (585nm)" current=0.030A package="3 mm [THT]"]
  LED3 = LED - 3mm [color="Red (633nm)" current=0.030A package="3 mm [THT]"]
  R1 = Resistor [tolerance=±5% power=0.25W resistance=470 package=THT]
  R3 = Resistor [tolerance=±5% power=0.25W resistance=470 package=THT]
  CH3 = Multimeter straight red probe
  CH1 = Multimeter straight red probe

nets:
  A: Part1.D2, U2.A1, U2.B1, LED1.anode, CH1.Probe_tip, CH1.Probe_tip_2
  5V: Part1.5V, U2.VDD
  GND: Part1.GND, U2.A2, U2.B2, U2.GND, U2.A3, U2.B3, U2.A4, U2.B4, R1.Pin_0, R3.Pin_0
  Q: U2.Q1, LED3.anode, CH3.Probe_tip, CH3.Probe_tip_2
  N1: LED1.cathode, R1.Pin_1
  N2: LED3.cathode, R3.Pin_1

notes:
  Input A (CH1)
  Output Q (CH3)
