# Fritzing sketch TransconductanceSingleSupply (saved by Fritzing 0.9.2b)
breadboards: 1

parts:
  IC1 = LM741 [part_number=LM741 package=dip08]
  PS1 = Power plug [part_number=9V]
  R3 = Trimmer Potentiometer [maximum_resistance=10kΩ package=THT]
  R2 = Resistor [tolerance=±5% resistance=4.7k package=THT]
  LED1 = LED - 5mm [color="Blue (525nm)" package="5 mm [THT]"]
  R1 = Resistor [tolerance=±5% resistance=1k package=THT]
  D1 = Rectifier Diode [part_number=1N4148 package="300 mil [THT]"]
  D2 = Rectifier Diode [part_number=1N4148 package="300 mil [THT]"]
  D3 = Rectifier Diode [part_number=1N4148 package="300 mil [THT]"]
  D4 = Rectifier Diode [part_number=1N4148 package="300 mil [THT]"]

nets:
  N1: IC1.+OFFSET, IC1.NC
  CH2: IC1.-INPUT, R2.Pin_0, LED1.cathode
  CH1: IC1.+INPUT, R3.wiper
  GND: IC1.V-, PS1.GND, D1.cathode
  CH3/OUTPUT: IC1.OUTPUT, R1.Pin_1
  VCC: IC1.V+, PS1.VCC, R3.leg2
  CH4/VGND: R3.leg1, R2.Pin_1, D4.anode
  N2: LED1.anode, R1.Pin_0
  N3: D1.anode, D2.cathode
  N4: D2.anode, D3.cathode
  N5: D3.anode, D4.cathode

custom parts:
  LM741: General Purpose Operational Amplifier
