# Fritzing sketch TwinTeeOscillator (saved by Fritzing 0.9.2b)
breadboards: 1

parts:
  5-9V = Power plug
  R3 = Resistor [tolerance=±5% resistance=10k package=THT]
  R2 = Trimmer Potentiometer [maximum_resistance=50kΩ package=THT]
  R4 = Resistor [tolerance=±5% resistance=1k package=THT]
  R1a = Resistor [tolerance=±5% resistance=4.7k package=THT]
  R1b = Resistor [tolerance=±5% resistance=4.7k package=THT]
  C2 = Ceramic Capacitor [capacitance=20nF package="100 mil [THT, multilayer]"]
  C1a = Ceramic Capacitor [capacitance=10nF package="100 mil [THT, multilayer]"]
  C1b = Ceramic Capacitor [capacitance=10nF package="100 mil [THT, multilayer]"]
  U2 = TL072/TLE2072 Dual Op. Amp [part_number=TL072 package="DIP8 [THT]"]
  RR2 = Resistor [tolerance=±5% resistance=10k package=THT]
  RR1 = Resistor [tolerance=±5% resistance=10k package=THT]

nets:
  GND: 5-9V.GND, U2.Pin_4, RR2.Pin_1
  VCC: 5-9V.VCC, U2.Pin_8, RR1.Pin_1
  OUTPUT: R3.Pin_0, R1b.Pin_0, C1b.1, U2.Pin_1
  N1: R3.Pin_1, R4.Pin_0, U2.Pin_3
  AC_GND: R2.leg1, R2.wiper, R4.Pin_1, C2.0, U2.Pin_6, U2.Pin_7
  N2: R2.leg2, C1a.1, C1b.0
  N3: R1a.Pin_0, R1b.Pin_1, C2.1
  N4: R1a.Pin_1, C1a.0, U2.Pin_2
  N5: U2.Pin_5, RR2.Pin_0, RR1.Pin_0

notes:
  Output

custom parts:
  TL072/TLE2072 Dual Op. Amp: The classic LM 358 Dual Operational Amplifier (Op-Amp). The analog swiss-army knife.
