# Fritzing sketch OpAmpTimer (saved by Fritzing 0.9.2b)
breadboards: 1

parts:
  C1 = Electrolytic Capacitor [capacitance=47µF package="100 mil [THT, electrolytic]"]
  OA1 = LM741 [part_number=LM741 package=dip08]
  5V = Power plug
  S1 = Pushbutton [package="[THT]"]
  R1 = Resistor [tolerance=±5% resistance=10k package=THT]
  R2 = Resistor [tolerance=±5% resistance=10k package=THT]
  R3 = Resistor [tolerance=±5% resistance=1k package=THT]
  LED1 = LED - 3mm [color="Green (555nm)" package="3 mm [THT]"]
  R4 = Trimmer Potentiometer [maximum_resistance=50kΩ package=THT]
  R5 = Resistor [tolerance=±5% resistance=1k package=THT]
  Part1 = Arduino Uno (Rev3)

nets:
  GND: C1.-, OA1.V-, 5V.GND, S1.Pin_3, S1.Pin_4, R2.Pin_1, R3.Pin_1, Part1.GND
  INPUT: C1.+, OA1.-INPUT, S1.Pin_1, S1.Pin_2, R5.Pin_0, Part1.A0
  N1: OA1.+OFFSET, OA1.NC
  N2: OA1.+INPUT, R1.Pin_1, R2.Pin_0
  OUTPUT: OA1.OUTPUT, LED1.anode, Part1.A1
  N3: OA1.V+, 5V.VCC, R1.Pin_0, R4.wiper
  N4: R3.Pin_0, LED1.cathode
  N5: R4.leg1, R5.Pin_1

custom parts:
  LM741: General Purpose Operational Amplifier
