# Fritzing sketch 3DU5C (saved by Fritzing 1.0.1rc)
breadboards: 1

parts:
  5V = Power plug
  R1 = Resistor [tolerance=±5% power=0.25W resistance=3.3k package=THT]
  Q1 = LTR-301 [part_number=3DU5C package=ltr-301]
  METER3 = 7-Segment Panel Ammeter

nets:
  GND: 5V.GND, R1.Pin_0, METER3.GND
  5V: 5V.VCC, Q1.C, METER3.V+
  N1: R1.Pin_1, Q1.E, METER3.LOAD-

notes:
  3-wire Voltmeter (common ground)

custom parts:
  7-Segment Panel Ammeter: 7-Segment Panel Ammeter (0 to 9.99A)
