# Fritzing sketch AstableOpamp (saved by Fritzing 0.9.0b)
breadboards: 1

parts:
  Part1 = Arduino Uno (Rev3)
  R1 = Resistor [tolerance=±5% resistance=10k package=THT]
  R2 = Resistor [tolerance=±5% resistance=10k package=THT]
  R3 = Resistor [tolerance=±5% resistance=10k package=THT]
  R4 = Resistor [tolerance=±5% resistance=4.7k package=THT]
  C1 = Electrolytic Capacitor [capacitance=100µF package="100 mil [THT, electrolytic]"]
  R5 = Resistor [tolerance=±5% resistance=1k package=THT]
  LED1 = LED - 5mm [color="Red (633nm)" package="5 mm [THT]"]
  U1 = LMV324 [package=so014]

nets:
  N1: Part1.A0, R5.Pin_0, LED1.cathode
  N2: Part1.A1, R4.Pin_1, C1.+, U1.G$1_-IN
  N3: Part1.5V, R1.Pin_1, U1.G$1_+V
  N4: Part1.GND, R2.Pin_1, C1.-, R5.Pin_1, U1.G$1_-V
  N5: R1.Pin_0, R2.Pin_0, R3.Pin_0, U1.G$1_+IN
  N6: R3.Pin_1, R4.Pin_0, LED1.anode, U1.G$1_OUT
