# Fritzing sketch BaxandallOscillator (saved by Fritzing 1.0.7)
breadboards: 1

parts:
  Q1 = Basic FET N-Channel [part_number=IRF610 package="TO220 [THT]"]
  Power_In = Power plug
  L1 = Inductor [inductance=100µH package="400 mil [THT]"]
  L2a = Inductor [package="400 mil [THT]"]
  L2b = Inductor [package="400 mil [THT]"]
  L2c = Inductor [package="400 mil [THT]"]
  Q2 = Basic FET N-Channel [part_number=IRF610 package="TO220 [THT]"]
  D1 = Schottky Diode [part_number=BAT85 package="300 mil [THT]"]
  D2 = Schottky Diode [part_number=BAT85 package="300 mil [THT]"]
  R1 = Resistor [tolerance=±5% power=0.25W resistance=4.7k package=THT]
  R2 = Resistor [tolerance=±5% power=0.25W resistance=4.7k package=THT]
  R3 = Resistor [tolerance=±5% power=0.25W resistance=100k package=THT]
  LED1 = LED - 3mm [color="White (6500K)" current=0.030A package="3 mm [THT]"]
  LED2 = LED - 3mm [color="White (6500K)" current=0.030A package="3 mm [THT]"]
  C1 = Ceramic Capacitor [capacitance=1nF voltage=35V package="100 mil [THT, multilayer]"]

nets:
  N1: Q1.gate, D1.anode, R2.Pin_1
  CH1: Q1.drain, L2a.pin_0, D2.cathode, C1.1
  GND: Q1.source, Power_In.GND, Q2.source
  5V: Power_In.VCC, L1.pin_1, R1.Pin_0, R2.Pin_0
  N2: L1.pin_0, L2a.pin_1, L2b.pin_0
  CH2: L2b.pin_1, Q2.drain, D1.cathode, C1.0
  N3: L2c.pin_0, R3.Pin_0
  N4: L2c.pin_1, LED1.cathode, LED2.anode
  N5: Q2.gate, D2.anode, R1.Pin_1
  N6: R3.Pin_1, LED1.anode, LED2.cathode

notes:
  Inductors represent 12-0-12 to 240VAC transformer
