# Fritzing sketch CMOSOscillators (saved by Fritzing 0.9.2b)
breadboards: 1

parts:
  5V = Power plug
  IC1 = IC, DIP package, 14 pins [chip_label=NCH060C part_number=NCH060C]

nets:
  GND: 5V.GND, IC1.pin7
  VCC: 5V.VCC, IC1.pin14
  CH1: IC1.pin8

notes:
  OUT (CH1)
