# Fritzing sketch CommonEmitterHartley (saved by Fritzing 0.9.2b)
breadboards: 1

parts:
  L1 = Inductor [inductance=2µH package="400 mil [THT]"]
  L2 = Inductor [inductance=10µH package="400 mil [THT]"]
  C1 = Ceramic Capacitor [capacitance=1nF package="100 mil [THT, multilayer]"]
  C2 = Ceramic Capacitor [capacitance=100nF package="100 mil [THT, multilayer]"]
  Q1 = NPN-Transistor [part_number=2N3904 package="TO92 [THT]"]
  C3 = Ceramic Capacitor [capacitance=100nF package="100 mil [THT, multilayer]"]
  R1 = Resistor [tolerance=±5% resistance=10k package=THT]
  R2 = Resistor [tolerance=±5% resistance=1k package=THT]
  R3 = Resistor [tolerance=±5% resistance=22 package=THT]
  C4 = Ceramic Capacitor [capacitance=100nF package="100 mil [THT, multilayer]"]
  C5 = Electrolytic Capacitor [capacitance=10µF package="100 mil [THT, electrolytic]"]
  VCC1 = Battery block 9V

nets:
  N1: L1.pin_0, C1.1, R1.Pin_0, C5.+, VCC1.+
  N2: L1.pin_1, L2.pin_0, C2.1
  N3: L2.pin_1, C1.0, Q1.C, C3.1
  N4: C2.0, Q1.E, R3.Pin_0
  N5: Q1.B, R1.Pin_1, R2.Pin_0, C4.1
  OUT: C3.0
  GND: R2.Pin_1, R3.Pin_1, C4.0, C5.-, VCC1.-

notes:
  CH1/OUT
