# Fritzing sketch ComparatorRelaxation (saved by Fritzing 0.9.2b)
breadboards: 1

parts:
  U1 = LM358 [part_number=LM358 package=dip08]
  5V = Power plug
  R1 = Resistor [tolerance=±5% resistance=10k package=THT]
  R2 = Resistor [tolerance=±5% resistance=10k package=THT]
  R3 = Resistor [tolerance=±5% resistance=100k package=THT]
  R4 = Resistor [tolerance=±5% resistance=100k package=THT]
  R5 = Resistor [tolerance=±5% resistance=100k package=THT]
  C1 = Ceramic Capacitor [capacitance=100nF package="100 mil [THT, multilayer]"]

nets:
  VREF: U1.G$1_OUT, U1.G$1_-IN, R3.Pin_0, C1.1
  N1: U1.G$1_+IN, R1.Pin_1, R2.Pin_1
  GND: U1.G$1_V-, 5V.GND, R1.Pin_0
  CH3: U1.G$2_+IN, R3.Pin_1, R5.Pin_0
  CH2: U1.G$2_-IN, R4.Pin_0, C1.0
  CH1-OUT: U1.G$2_OUT, R4.Pin_1, R5.Pin_1
  VCC: U1.G$1_V+, 5V.VCC, R2.Pin_0
