# Fritzing sketch CrystalLocked1khzOscillator (saved by Fritzing 0.9.2b)
breadboards: 1

parts:
  IC1 = IC, DIP package, 16 pins [chip_label=CD4060]
  5V = Power plug
  C1 = Ceramic Capacitor [capacitance=22pF package="100 mil [THT, multilayer]"]
  R2 = Resistor [tolerance=±5% resistance=10M package=THT]
  R1 = Resistor [tolerance=±5% resistance=100 package=THT]
  X1 = Crystal [frequency="4 MHz" part_number=4.096MHz package=THT]
  C2 = Ceramic Capacitor [capacitance=22pF package="100 mil [THT, multilayer]"]
  C3 = Ceramic Capacitor [capacitance=100nF package="100 mil [THT, multilayer]"]
  IC2 = LM324 [part_number=TL074 package=dil16]
  VR1 = Trimmer Potentiometer [maximum_resistance=10kΩ package=THT]
  VR2 = Trimmer Potentiometer [maximum_resistance=10kΩ package=THT]
  VR3 = Trimmer Potentiometer [maximum_resistance=100kΩ package=THT]
  R9 = Resistor [tolerance=±5% resistance=100k package=THT]
  R10 = Resistor [tolerance=±5% resistance=68k package=THT]
  R7 = Resistor [tolerance=±5% resistance=47k package=THT]
  R8 = Resistor [tolerance=±5% resistance=47k package=THT]
  C10 = Electrolytic Capacitor [capacitance=1µF package="100 mil [THT, electrolytic]"]
  D1 = Rectifier Diode [part_number=1N4148 package="300 mil [THT]"]
  C9 = Ceramic Capacitor [capacitance=33nF package="100 mil [THT, multilayer]"]
  C8 = Ceramic Capacitor [capacitance=33nF package="100 mil [THT, multilayer]"]
  R11 = Resistor [tolerance=±5% resistance=3k package=THT]
  R13 = Resistor [tolerance=±5% resistance=10k package=THT]
  R12 = Resistor [tolerance=±5% resistance=4.7k package=THT]
  R14 = Resistor [tolerance=±5% resistance=10k package=THT]
  R15 = Resistor [tolerance=±5% resistance=4.7k package=THT]
  R3 = Resistor [tolerance=±5% resistance=15k package=THT]
  C4 = Ceramic Capacitor [capacitance=10nF package="100 mil [THT, multilayer]"]
  R4 = Resistor [tolerance=±5% resistance=15k package=THT]
  C5 = Ceramic Capacitor [capacitance=10nF package="100 mil [THT, multilayer]"]
  C6 = Ceramic Capacitor [capacitance=10nF package="100 mil [THT, multilayer]"]
  R5 = Resistor [tolerance=±5% resistance=15k package=THT]
  R6 = Resistor [tolerance=±5% resistance=15k package=THT]
  C7 = Ceramic Capacitor [capacitance=10nF package="100 mil [THT, multilayer]"]
  C11 = Ceramic Capacitor [capacitance=100nF package="100 mil [THT, multilayer]"]
  Q1 = 2N7000 FET N-Channel [part_number=2N7000 package=TO92]

nets:
  PULSE: IC1.pin1, R3.Pin_0
  GND: IC1.pin8, IC1.pin12, 5V.GND, C1.1, C2.1, C3.0, IC2.GND, R8.Pin_1, C4.0, C5.0, C6.0, C11.0
  N1: IC1.pin10, R1.Pin_0
  N2: IC1.pin11, C1.0, R2.Pin_0, X1.pin_0
  VDD: IC1.pin16, 5V.VCC, C3.1, IC2.V+, R7.Pin_1, C11.1
  N3: R2.Pin_1, R1.Pin_1, X1.pin_1, C2.0
  SIN_OUT: IC2.OUT1, IC2.IN1-, IC2.IN4+
  SIN: IC2.IN1+, IC2.OUT3, VR2.leg1, VR2.wiper, R9.Pin_0, D1.cathode, R15.Pin_1
  N4: IC2.IN2+, R7.Pin_0, R8.Pin_0
  VG: IC2.IN2-, IC2.OUT2, VR3.leg1, C10.+, C9.1, R11.Pin_1, Q1.source
  N5: IC2.IN3-, R9.Pin_1, R10.Pin_0
  N6: IC2.IN3+, C9.0, C8.0, R13.Pin_0, R12.Pin_1
  SQUARE_OUT: IC2.IN4-, IC2.OUT4
  SP: VR1.leg1, VR1.wiper, R11.Pin_0, R12.Pin_0, C7.0
  N7: VR1.leg2, R13.Pin_1
  N8: VR2.leg2, R14.Pin_0
  N9: VR3.wiper, Q1.gate
  N10: VR3.leg2, C10.-, D1.anode
  N11: R10.Pin_1, Q1.drain
  N12: C8.1, R14.Pin_1, R15.Pin_0
  N13: R3.Pin_1, C4.1, R4.Pin_0
  N14: R4.Pin_1, C5.1, R5.Pin_0
  N15: C6.1, R5.Pin_1, R6.Pin_0
  N16: R6.Pin_1, C7.1

notes:
  SIN OUT
  SQ OUT
  PULSE OUT

custom parts:
  LM324: LM324 Quad OpAmp
  2N7000 FET N-Channel: A 2N7000 MOSFET N-Channel Transistor
