# Fritzing sketch CrystalLocked455kHzModulated (saved by Fritzing 0.9.2b)
breadboards: 1

parts:
  C6 = Electrolytic Capacitor [capacitance=100µF package="100 mil [THT, electrolytic]"]
  VCC = Power plug
  Q1 = NPN-Transistor [part_number=2N3904 package="TO92 [THT]"]
  Q2 = NPN-Transistor [part_number=2N3904 package="TO92 [THT]"]
  R3 = Resistor [tolerance=±5% resistance=1.5k package=THT]
  R4 = Resistor [tolerance=±5% resistance=470 package=THT]
  R5 = Resistor [tolerance=±5% resistance=1k package=THT]
  R2 = Resistor [tolerance=±5% resistance=33k package=THT]
  R1 = Resistor [tolerance=±5% resistance=33k package=THT]
  C2 = Ceramic Capacitor [capacitance=22nF package="100 mil [THT, multilayer]"]
  C1 = Ceramic Capacitor [capacitance=22nF package="100 mil [THT, multilayer]"]
  R6 = Resistor [tolerance=±5% resistance=22k package=THT]
  R7 = Resistor [tolerance=±5% resistance=10M package=THT]
  C4 = Ceramic Capacitor [capacitance=68pF package="100 mil [THT, multilayer]"]
  C3 = Ceramic Capacitor [capacitance=68pF package="100 mil [THT, multilayer]"]
  C5 = Ceramic Capacitor [capacitance=27pF package="100 mil [THT, multilayer]"]
  Y1 = CRYSTAL [part_number=455kHz package=hc49up]
  Q3 = NPN-Transistor [part_number=2N3904 package="TO92 [THT]"]
  S1 = Toggle Switch [package=THT]
  R8 = Resistor [tolerance=±5% resistance=1.2k package=THT]
  LED1 = LED - 3mm [color="Green (555nm)" package="3 mm [THT]"]

nets:
  GND: C6.-, VCC.GND, Q1.E, Q2.E, C4.1, C3.0, Q3.E, LED1.cathode
  N1: C6.+, R3.Pin_0, R4.Pin_0, R2.Pin_0, R1.Pin_0, S1.COM, R8.Pin_1
  N2: VCC.VCC, S1.L2
  N3: Q1.B, R2.Pin_1, C2.0
  N4: Q1.C, R3.Pin_1, C1.0
  N5: Q2.B, R1.Pin_1, C1.1
  N6: Q2.C, R5.Pin_1, C2.1
  N7: R4.Pin_1, R5.Pin_0, R6.Pin_1
  N8: R6.Pin_0, R7.Pin_0, C4.0, C5.1, Y1.1, Q3.C
  N9: R7.Pin_1, C3.1, Y1.2, Q3.B
  PROBE: C5.0
  N10: R8.Pin_0, LED1.anode

notes:
  Probe
