# Fritzing sketch CrystalLocked4MHzCD4001 (saved by Fritzing 0.9.2b)
breadboards: 1

parts:
  IC3 = IC, DIP package, 14 pins [chip_label=CD4001]
  XTAL1 = Crystal [frequency="4 MHz" package=THT]
  C1 = Ceramic Capacitor [capacitance=30pF package="100 mil [THT, multilayer]"]
  C2 = Ceramic Capacitor [capacitance=30pF package="100 mil [THT, multilayer]"]
  5V = Power plug
  R1 = Resistor [tolerance=±5% resistance=4.7M package=THT]

nets:
  N1: IC3.pin1, XTAL1.pin_0, C1.1, R1.Pin_0
  GND: IC3.pin2, IC3.pin5, IC3.pin7, IC3.pin8, IC3.pin9, IC3.pin12, IC3.pin13, C1.0, C2.0, 5V.GND
  CH2: IC3.pin3, IC3.pin6, XTAL1.pin_1, C2.1, R1.Pin_1
  CH1: IC3.pin4
  VCC: IC3.pin14, 5V.VCC

notes:
  CH1
  CH2
