# Fritzing sketch HighFrequencyOpAmpOscillators (saved by Fritzing 0.9.2b)
breadboards: 1

parts:
  9V = Power plug
  C1 = Ceramic Capacitor [capacitance=100pF package="100 mil [THT, multilayer]"]
  R2 = Resistor [tolerance=±5% resistance=10k package=THT]
  R3 = Trimmer Potentiometer [maximum_resistance=10kΩ package=THT]
  R4 = Resistor [tolerance=±5% resistance=1k package=THT]
  R1 = Resistor [tolerance=±5% resistance=10k package=THT]
  C2 = Ceramic Capacitor [capacitance=1nF package="100 mil [THT, multilayer]"]
  R5 = Resistor [tolerance=±5% resistance=15k package=THT]
  IC1 = LM324 [package=dil16]
  C3 = Ceramic Capacitor [capacitance=100nF package="100 mil [THT, multilayer]"]
  C4 = Ceramic Capacitor [capacitance=10nF package="100 mil [THT, multilayer]"]
  IC2 = LM741 [part_number=UA741CN package=dip08]
  R6 = Trimmer Potentiometer [maximum_resistance=10kΩ package=THT]
  C5 = Ceramic Capacitor [capacitance=100pF package="100 mil [THT, multilayer]"]
  R7 = Resistor [tolerance=±5% resistance=15k package=THT]
  R8 = Resistor [tolerance=±5% resistance=10k package=THT]
  R9 = Resistor [tolerance=±5% resistance=10k package=THT]
  C6 = Ceramic Capacitor [capacitance=1nF package="100 mil [THT, multilayer]"]
  R10 = Resistor [tolerance=±5% resistance=1k package=THT]
  U1 = TL072/TLE2072 Dual Op. Amp [part_number=TL072CP package="DIP8 [THT]"]
  R11 = Trimmer Potentiometer [maximum_resistance=10kΩ package=THT]
  R12 = Resistor [tolerance=±5% resistance=1k package=THT]
  R13 = Resistor [tolerance=±5% resistance=15k package=THT]
  C7 = Ceramic Capacitor [capacitance=100pF package="100 mil [THT, multilayer]"]
  C8 = Ceramic Capacitor [capacitance=1nF package="100 mil [THT, multilayer]"]
  R14 = Resistor [tolerance=±5% resistance=10k package=THT]
  R15 = Resistor [tolerance=±5% resistance=10k package=THT]
  IC3 = LM324 [part_number=LF347N package=dil16]
  R16 = Trimmer Potentiometer [maximum_resistance=10kΩ package=THT]
  C9 = Ceramic Capacitor [capacitance=1nF package="100 mil [THT, multilayer]"]
  R17 = Resistor [tolerance=±5% resistance=1k package=THT]
  C10 = Ceramic Capacitor [capacitance=20pF package="100 mil [THT, multilayer]"]
  R18 = Resistor [tolerance=±5% resistance=15k package=THT]
  R19 = Resistor [tolerance=±5% resistance=10k package=THT]
  R20 = Resistor [tolerance=±5% resistance=10k package=THT]
  IC4 = LM741 [part_number=NE5534P package=dip08]
  R21 = Trimmer Potentiometer [maximum_resistance=10kΩ package=THT]
  R22 = Resistor [tolerance=±5% resistance=1k package=THT]
  C11 = Ceramic Capacitor [capacitance=1nF package="100 mil [THT, multilayer]"]
  R23 = Resistor [tolerance=±5% resistance=10k package=THT]
  R24 = Resistor [tolerance=±5% resistance=15k package=THT]
  R25 = Resistor [tolerance=±5% resistance=10k package=THT]
  C12 = Ceramic Capacitor [capacitance=20pF package="100 mil [THT, multilayer]"]

nets:
  GND: 9V.GND, C1.0, R2.Pin_1, IC1.GND, C3.1, C4.1, IC2.V-, C5.0, R8.Pin_1, U1.Pin_4, C7.0, R14.Pin_1, IC3.GND, C10.0, R19.Pin_1, IC4.V-, R25.Pin_1, C12.0
  VCC: 9V.VCC, R5.Pin_0, IC1.V+, C3.0, C4.0, IC2.V+, R7.Pin_0, U1.Pin_8, R13.Pin_0, IC3.V+, R18.Pin_0, IC4.V+, R24.Pin_0
  N1: C1.1, R3.leg2, IC1.IN4-
  N2: R2.Pin_0, R1.Pin_1, R5.Pin_1, IC1.IN4+
  N3: R3.wiper, R4.Pin_1
  N4: R4.Pin_0, R1.Pin_0, C2.1, IC1.OUT4
  OUT1: C2.0
  N5: IC2.+OFFSET, IC2.NC
  N6: IC2.-INPUT, R6.leg2, C5.1
  N7: IC2.+INPUT, R7.Pin_1, R8.Pin_0, R9.Pin_0
  N8: IC2.OUTPUT, R9.Pin_1, C6.1, R10.Pin_1
  N9: R6.wiper, R10.Pin_0
  OUT2: C6.0
  N10: U1.Pin_5, R13.Pin_1, R14.Pin_0, R15.Pin_1
  N11: U1.Pin_6, R11.leg2, C7.1
  N12: U1.Pin_7, R12.Pin_0, C8.1, R15.Pin_0
  N13: R11.wiper, R12.Pin_1
  OUT3: C8.0
  N14: IC3.IN4+, R18.Pin_1, R19.Pin_0, R20.Pin_1
  N15: IC3.IN4-, R16.leg2, C10.1
  N16: IC3.OUT4, C9.1, R17.Pin_0, R20.Pin_0
  N17: R16.wiper, R17.Pin_1
  OUT4: C9.0
  N18: IC4.+OFFSET, IC4.NC
  N19: IC4.-INPUT, R21.leg2, C12.1
  N20: IC4.+INPUT, R23.Pin_0, R24.Pin_1, R25.Pin_0
  N21: IC4.OUTPUT, R22.Pin_1, C11.1, R23.Pin_1
  N22: R21.wiper, R22.Pin_0
  OUT5: C11.0

notes:
  LM324N Oscillator
  Power Supply
  LF347N Oscillator
  NE5534P Oscillator
  UA741CN Oscillator

custom parts:
  LM324: LM324 Quad OpAmp
  LM741: General Purpose Operational Amplifier
  TL072/TLE2072 Dual Op. Amp: The classic LM 358 Dual Operational Amplifier (Op-Amp). The analog swiss-army knife.
