# Fritzing sketch LdrLedRing (saved by Fritzing 0.9.2b)
breadboards: 1

parts:
  Part1 = LilyPad Coin Cell Battery Holder
  R1 = Resistor [tolerance=±5% resistance=1k package=THT]
  LDR1 = Photocell (LDR) [package=THT]
  C1 = Electrolytic Capacitor [capacitance=220µF package="100 mil [THT, electrolytic]"]
  LED1 = LED - 3mm [color="White (8000K)" package="3 mm [THT]"]
  LDR2 = Photocell (LDR) [package=THT]
  R2 = Resistor [tolerance=±5% resistance=1k package=THT]
  C2 = Electrolytic Capacitor [capacitance=220µF package="100 mil [THT, electrolytic]"]
  LED2 = LED - 3mm [color="White (8000K)" package="3 mm [THT]"]
  LDR3 = Photocell (LDR) [package=THT]
  R3 = Resistor [tolerance=±5% resistance=1k package=THT]
  C3 = Electrolytic Capacitor [capacitance=220µF package="100 mil [THT, electrolytic]"]
  LED3 = LED - 3mm [color="White (8000K)" package="3 mm [THT]"]

nets:
  GND: Part1.-, LDR1.pin_1, C1.-, LED1.cathode, LDR2.pin_1, C2.-, LED2.cathode, LDR3.pin_1, C3.-, LED3.cathode
  3V: Part1.+, R1.Pin_0, R2.Pin_0, R3.Pin_0
  N1: R1.Pin_1, LDR1.pin_0, C1.+, LED1.anode
  N2: LDR2.pin_0, R2.Pin_1, C2.+, LED2.anode
  N3: LDR3.pin_0, R3.Pin_1, C3.+, LED3.anode
