# Fritzing sketch PierceGateOscillator (saved by Fritzing 0.9.2b)
breadboards: 1

parts:
  5V = Power plug
  XTAL1 = Crystal [frequency="4 MHz" part_number=4.27MHz package=THT]
  Rs = Resistor [tolerance=±5% resistance=4.7k package=THT]
  Rf = Resistor [tolerance=±5% resistance=2.2k package=THT]
  C1 = Ceramic Capacitor [capacitance=33µF package="100 mil [THT, multilayer]"]
  C3 = Ceramic Capacitor [capacitance=100nF package="100 mil [THT, multilayer]"]
  C2 = Ceramic Capacitor [capacitance=33pF package="100 mil [THT, multilayer]"]
  XXXXXXX = Hex Inverter Schmitt Trigger SN74HC14 [part_number=...74LS14 package="DIP (Dual Inline)"]
  C4 = Ceramic Capacitor [capacitance=100nF package="100 mil [THT, multilayer]"]

nets:
  GND: 5V.GND, C1.0, C2.0, XXXXXXX.GND, C4.1
  VCC: 5V.VCC, XXXXXXX.VCC, C4.0
  N1: XTAL1.pin_0, Rf.Pin_0, C1.1, XXXXXXX.1A
  N2: XTAL1.pin_1, Rs.Pin_1, C2.1
  N3: Rs.Pin_0, Rf.Pin_1, XXXXXXX.1Y, XXXXXXX.2A
  CH1: C3.0
  N4: C3.1, XXXXXXX.2Y

notes:
  CH1
