# Fritzing sketch PierceOscillator (saved by Fritzing 0.9.2b)
breadboards: 1

parts:
  5V = Power plug
  XTAL1 = Crystal [frequency="16 Mhz" part_number=DUT package=THT]
  R1 = Resistor [tolerance=±5% resistance=1k package=THT]
  R2 = Resistor [tolerance=±5% resistance=100k package=THT]
  Q1 = NPN-Transistor [part_number=2N3904 package="TO92 [THT]"]
  C1 = Ceramic Capacitor [capacitance=22pF package="100 mil [THT, multilayer]"]
  C2 = Ceramic Capacitor [capacitance=100nF package="100 mil [THT, multilayer]"]

nets:
  GND: 5V.GND, Q1.E, C1.0
  N1: 5V.VCC, R1.Pin_0
  N2: XTAL1.pin_0, R1.Pin_1, R2.Pin_0, Q1.C, C1.1, C2.1
  N3: XTAL1.pin_1, R2.Pin_1, Q1.B
  CH1: C2.0
