# Fritzing sketch ProgrammableFrequencyReference (saved by Fritzing 0.9.2b)
breadboards: 1

parts:
  IC2 = IC, DIP package, 16 pins [chip_label=CD4040 part_number=CD4040]
  IC3 = IC, DIP package, 14 pins [chip_label=CD4001]
  IC4 = IC, DIP package, 14 pins [chip_label=74LS73]
  XTAL1 = Crystal [frequency="4 MHz" package=THT]
  R1 = Resistor [tolerance=±5% resistance=4.7M package=THT]
  C1 = Ceramic Capacitor [capacitance=33pF package="100 mil [THT, multilayer]"]
  C2 = Ceramic Capacitor [capacitance=33pF package="100 mil [THT, multilayer]"]
  5V = Power plug
  C3 = Ceramic Capacitor [capacitance=100nF package="100 mil [THT, multilayer]"]
  C4 = Ceramic Capacitor [capacitance=100nF package="100 mil [THT, multilayer]"]
  R2 = Resistor [tolerance=±5% resistance=4.7k package=THT]
  D1 = Rectifier Diode [part_number=1N4001 package="300 mil [THT]"]
  D2 = Rectifier Diode [part_number=1N4001 package="300 mil [THT]"]
  D3 = Rectifier Diode [part_number=1N4001 package="300 mil [THT]"]
  D4 = Rectifier Diode [part_number=1N4001 package="300 mil [THT]"]
  D5 = Rectifier Diode [part_number=1N4001 package="300 mil [THT]"]
  D6 = Rectifier Diode [part_number=1N4001 package="300 mil [THT]"]
  D7 = Rectifier Diode [part_number=1N4001 package="300 mil [THT]"]
  D8 = Rectifier Diode [part_number=1N4001 package="300 mil [THT]"]
  D9 = Rectifier Diode [part_number=1N4001 package="300 mil [THT]"]
  D10 = Rectifier Diode [part_number=1N4001 package="300 mil [THT]"]
  D11 = Rectifier Diode [part_number=1N4001 package="300 mil [THT]"]
  D12 = Rectifier Diode [part_number=1N4001 package="300 mil [THT]"]
  SW1 = DIP Switch 8 Position [package=dipswitch-08]
  SW2 = DIP SWITCH [package=dipswitch-02]
  SW3 = DIP SWITCH [package=dipswitch-02]

nets:
  Q12: IC2.pin1, D12.cathode
  Q6: IC2.pin2, D6.cathode
  Q5: IC2.pin3, D5.cathode
  Q7: IC2.pin4, D7.cathode
  Q4: IC2.pin5, D4.cathode
  Q3: IC2.pin6, D3.cathode
  Q2: IC2.pin7, D2.cathode
  GND: IC2.pin8, IC3.pin2, IC3.pin5, IC3.pin7, IC3.pin8, IC3.pin12, IC3.pin13, IC4.pin11, C1.0, C2.0, 5V.GND, C3.1, C4.1
  Q1: IC2.pin9, D1.cathode
  CLK: IC2.pin10, IC3.pin4, IC3.pin9
  RST: IC2.pin11, IC4.pin5, IC4.pin12
  Q9: IC2.pin12, D9.cathode
  Q8: IC2.pin13, D8.cathode
  Q10: IC2.pin14, D10.cathode
  Q11: IC2.pin15, D11.cathode
  VCC: IC2.pin16, IC3.pin14, IC4.pin2, IC4.pin3, IC4.pin4, IC4.pin6, IC4.pin7, IC4.pin10, 5V.VCC, C3.0, C4.0, R2.Pin_0
  N1: IC3.pin1, XTAL1.pin_0, R1.Pin_0, C1.1
  N2: IC3.pin3, IC3.pin6, XTAL1.pin_1, R1.Pin_1, C2.1
  !CLK: IC3.pin10, IC4.pin1
  OUT: IC4.pin9
  J: IC4.pin14, R2.Pin_1, SW1.9, SW1.10, SW1.11, SW1.12, SW1.13, SW1.14, SW1.15, SW1.16, SW2.3, SW2.4, SW3.3, SW3.4
  N3: D1.anode, SW1.1
  N4: D2.anode, SW1.2
  N5: D3.anode, SW1.3
  N6: D4.anode, SW1.4
  N7: D5.anode, SW1.5
  N8: D6.anode, SW1.6
  N9: D7.anode, SW1.7
  N10: D8.anode, SW1.8
  N11: D9.anode, SW2.1
  N12: D10.anode, SW2.2
  N13: D11.anode, SW3.1
  N14: D12.anode, SW3.2

notes:
  OUT
