# Fritzing sketch RCPhaseShiftBJT (saved by Fritzing 0.9.2b)
breadboards: 1

parts:
  Q1 = NPN-Transistor [part_number=2N3904 package="TO92 [THT]"]
  Re = Resistor [tolerance=±5% resistance=360 package=THT]
  C3 = Ceramic Capacitor [capacitance=10nF package="100 mil [THT, multilayer]"]
  Ce = Electrolytic Capacitor [capacitance=100µF package="100 mil [THT, electrolytic]"]
  C2 = Ceramic Capacitor [capacitance=10nF package="100 mil [THT, multilayer]"]
  C1 = Ceramic Capacitor [capacitance=10nF package="100 mil [THT, multilayer]"]
  R2 = Resistor [tolerance=±5% resistance=10k package=THT]
  9V = Power plug
  R1 = Resistor [tolerance=±5% resistance=10k package=THT]
  R3 = Resistor [tolerance=±5% resistance=10k package=THT]
  Rb = Resistor [tolerance=±5% resistance=100k package=THT]
  C4 = Electrolytic Capacitor [capacitance=10µF package="100 mil [THT, electrolytic]"]
  Rc = Resistor [tolerance=±5% resistance=4.7k package=THT]
  C5 = Ceramic Capacitor [capacitance=10nF package="100 mil [THT, multilayer]"]

nets:
  N1: Q1.E, Re.Pin_1, Ce.+
  N2: Q1.B, C3.1, R3.Pin_1, Rb.Pin_0
  N3: Q1.C, C1.0, C4.+, Rc.Pin_0
  GND: Re.Pin_0, Ce.-, 9V.GND, R3.Pin_0, C5.0
  N4: C3.0, C2.1, R2.Pin_0
  N5: C2.0, C1.1, R1.Pin_0
  N6: R2.Pin_1, 9V.VCC, R1.Pin_1, Rb.Pin_1, Rc.Pin_1, C5.1
  OUT: C4.-

notes:
  OUT
