# Fritzing sketch RingOscillator (saved by Fritzing 0.9.2b)
breadboards: 1

parts:
  5V = Power plug
  IC1 = Hex Inverter Schmitt Trigger SN74HC14 [package="DIP (Dual Inline)"]
  R1 = Resistor [tolerance=±5% resistance=1k package=THT]
  C1 = Ceramic Capacitor [capacitance=100pF package="100 mil [THT, multilayer]"]
  C2 = Ceramic Capacitor [capacitance=100nF package="100 mil [THT, multilayer]"]

nets:
  GND: 5V.GND, IC1.GND, C1.1
  VCC: 5V.VCC, IC1.VCC
  N1: IC1.1A, R1.Pin_1, C1.0, C2.0
  N2: IC1.1Y, IC1.2A
  N3: IC1.2Y, IC1.3A
  N4: IC1.3Y, R1.Pin_0
  OUT: C2.1
