# Fritzing sketch SchmittCrystalLockedOscillator (saved by Fritzing 0.9.2b)
breadboards: 1

parts:
  IC1 = Hex Inverter Schmitt Trigger SN74HC14 [package="DIP (Dual Inline)"]
  5V = Power plug
  XTAL1 = Crystal [frequency="4 MHz" package=THT]
  R1 = Resistor [tolerance=±5% resistance=51k package=THT]
  C1 = Ceramic Capacitor [capacitance=20pF package="100 mil [THT, multilayer]"]
  C2 = Ceramic Capacitor [capacitance=20pF package="100 mil [THT, multilayer]"]

nets:
  N1: IC1.1A, XTAL1.pin_0, C1.1
  N2: IC1.1Y, IC1.2A, XTAL1.pin_1, R1.Pin_0, C2.1
  N3: IC1.2Y, R1.Pin_1
  GND: IC1.3Y, IC1.GND, IC1.4Y, IC1.5Y, IC1.6Y, 5V.GND, C1.0, C2.0
  VCC: IC1.VCC, 5V.VCC
