# Fritzing sketch SchmittOscillator (saved by Fritzing 1.0.1rc)
breadboards: 1

parts:
  R1 = Resistor [tolerance=±5% resistance=1k power=0.25W package=THT]
  Part1 = Arduino Uno (Rev3)
  C1 = Electrolytic Capacitor [capacitance=470µF voltage=35V package="100 mil [THT, electrolytic]"]
  LED1 = LED - 5mm [color="Red (633nm)" current=0.030A package="5 mm [THT]"]
  R2 = Resistor [tolerance=±5% resistance=1k power=0.25W package=THT]
  R3 = Resistor [tolerance=±5% resistance=1k power=0.25W package=THT]
  Q2 = NPN-Transistor [package="TO92 [THT]"]
  U1 = SN74LS14N [package="DIP14 [THT]"]

nets:
  OUT: R1.Pin_0, Part1.A1, R3.Pin_0, U1.1Y
  IN: R1.Pin_1, Part1.A0, C1.+, U1.1A
  VCC: Part1.5V, R2.Pin_0, U1.VCC
  GND: Part1.GND, C1.-, Q2.E, U1.2A, U1.3A, U1.GND, U1.4A, U1.5A, U1.6A
  N1: LED1.cathode, Q2.C
  N2: LED1.anode, R2.Pin_1
  N3: R3.Pin_1, Q2.B
