# Fritzing sketch WatsonLedRing (saved by Fritzing 0.9.2b)
breadboards: 1

parts:
  5V = Power plug
  LED1 = LED - 5mm [color="Blue (430nm)" package="5 mm [THT]"]
  LED2 = LED - 5mm [color="Blue (430nm)" package="5 mm [THT]"]
  LED3 = LED - 5mm [color="Blue (430nm)" package="5 mm [THT]"]
  R1 = Resistor [tolerance=±5% resistance=220 package=THT]
  R2 = Resistor [tolerance=±5% resistance=220 package=THT]
  R3 = Resistor [tolerance=±5% resistance=220 package=THT]
  R5 = Resistor [tolerance=±5% resistance=1M package=THT]
  R6 = Resistor [tolerance=±5% resistance=1M package=THT]
  R4 = Resistor [tolerance=±5% resistance=1M package=THT]
  C1 = Ceramic Capacitor [capacitance=100nF package="100 mil [THT, multilayer]"]
  C2 = Ceramic Capacitor [capacitance=100nF package="100 mil [THT, multilayer]"]
  C3 = Ceramic Capacitor [capacitance=100nF package="100 mil [THT, multilayer]"]
  Q1 = Basic FET N-Channel [part_number=2N7000 package="D2Pak [SMD]"]
  Q2 = Basic FET N-Channel [part_number=2N7000 package="D2Pak [SMD]"]
  Q3 = Basic FET N-Channel [part_number=2N7000 package="D2Pak [SMD]"]

nets:
  GND: 5V.GND, C1.1, C2.1, C3.1, Q1.source, Q2.source, Q3.source
  N1: 5V.VCC, R1.Pin_0, R2.Pin_0, R3.Pin_0
  N2: LED1.cathode, R5.Pin_0, Q1.drain
  N3: LED1.anode, R1.Pin_1
  N4: LED2.cathode, R6.Pin_0, Q2.drain
  N5: LED2.anode, R2.Pin_1
  N6: LED3.cathode, R4.Pin_0, Q3.drain
  N7: LED3.anode, R3.Pin_1
  N8: R5.Pin_1, C2.0, Q2.Gate
  N9: R6.Pin_1, C3.0, Q3.Gate
  N10: R4.Pin_1, C1.0, Q1.Gate
