# Fritzing sketch WatsonLedRing3V (saved by Fritzing 0.9.2b)
breadboards: 1

parts:
  3V = Power plug
  R1 = Resistor [tolerance=±5% resistance=220 package=THT]
  R2 = Resistor [tolerance=±5% resistance=220 package=THT]
  R3 = Resistor [tolerance=±5% resistance=220 package=THT]
  R5 = Resistor [tolerance=±5% resistance=1M package=THT]
  R6 = Resistor [tolerance=±5% resistance=1M package=THT]
  R4 = Resistor [tolerance=±5% resistance=1M package=THT]
  C1 = Ceramic Capacitor [capacitance=100nF package="100 mil [THT, multilayer]"]
  C2 = Ceramic Capacitor [capacitance=100nF package="100 mil [THT, multilayer]"]
  C3 = Ceramic Capacitor [capacitance=100nF package="100 mil [THT, multilayer]"]
  Q1 = Basic FET N-Channel [part_number=2N7000 package="D2Pak [SMD]"]
  Q2 = Basic FET N-Channel [part_number=2N7000 package="D2Pak [SMD]"]
  Q3 = Basic FET N-Channel [part_number=2N7000 package="D2Pak [SMD]"]
  LED1 = LED - 3mm [color="Green (555nm)" package="3 mm [THT]"]
  LED2 = LED - 3mm [color="Green (555nm)" package="3 mm [THT]"]
  LED3 = LED - 3mm [color="Green (555nm)" package="3 mm [THT]"]
  R7 = Resistor [tolerance=±5% resistance=22k package=THT]
  R8 = Resistor [tolerance=±5% resistance=22k package=THT]
  R9 = Resistor [tolerance=±5% resistance=22k package=THT]

nets:
  GND: 3V.GND, C1.1, C2.1, C3.1, Q1.source, Q2.source, Q3.source
  N1: 3V.VCC, R1.Pin_0, R2.Pin_0, R3.Pin_0
  N2: R1.Pin_1, LED1.anode, R7.Pin_0
  N3: R2.Pin_1, LED2.anode, R8.Pin_0
  N4: R3.Pin_1, LED3.anode, R9.Pin_0
  N5: R5.Pin_0, Q1.drain, LED1.cathode, R7.Pin_1
  N6: R5.Pin_1, C2.0, Q2.Gate
  N7: R6.Pin_0, Q2.drain, LED2.cathode, R8.Pin_1
  N8: R6.Pin_1, C3.0, Q3.Gate
  N9: R4.Pin_0, Q3.drain, LED3.cathode, R9.Pin_1
  N10: R4.Pin_1, C1.0, Q1.Gate
