# Fritzing sketch GeneralPurposeHighSideController (saved by Fritzing 1.0.1rc)
breadboards: 1

parts:
  U1 = 555 Timer [package="DIP8 [THT]"]
  R1 = Resistor [tolerance=±5% resistance=1k power=0.25W package=THT]
  R2 = Trimmer Potentiometer [maximum_resistance=100kΩ knob_status=50% power=0.5W package=THT]
  C1 = Ceramic Capacitor [capacitance=10nF package="100 mil [THT, multilayer]"]
  D1 = Rectifier Diode [part_number=1N4148 package="300 mil [THT]"]
  D2 = Rectifier Diode [part_number=1N4148 package="300 mil [THT]"]
  C2 = Ceramic Capacitor [capacitance=100nF package="100 mil [THT, multilayer]"]
  R3 = Resistor [tolerance=±5% resistance=1k power=0.25W package=THT]
  Q1 = Basic FET N-Channel [part_number=2N7000 package="TO220 [THT]"]
  RLoad = Resistor [tolerance=±5% resistance=10k power=0.25W package=THT]
  5-15V = Power plug
  Q2 = Basic FET P-Channel [part_number=IRF9540 package="DPak [SMD]"]
  R4 = Resistor [tolerance=±5% resistance=1k power=0.25W package=THT]
  C3 = Electrolytic Capacitor [capacitance=220µF package="100 mil [THT, electrolytic]"]
  C4 = Ceramic Capacitor [capacitance=100nF package="100 mil [THT, multilayer]"]
  C5 = Ceramic Capacitor [capacitance=1nF package="100 mil [THT, multilayer]"]
  S1 = Toggle Switch [package=THT]
  U2 = SWITCH_SPDT [package=kps-1290]
  R5 = Resistor [tolerance=±5% resistance=2.2k power=0.25W package=THT]
  LED1 = LED - 3mm [color="Green (570nm)" current=0.030A package="3 mm [THT]"]

nets:
  GND/OUT (GND): U1.Ground, C1.0, C2.1, Q1.source, RLoad.Pin_0, 5-15V.GND, C3.-, C4.1, C5.0, LED1.cathode
  N1: U1.Trigger, U1.Threshold, R2.wiper, S1.COM
  N2: U1.Output, R3.Pin_0
  VCC: U1.Reset, U1.Vcc_Supply_Voltage, R1.Pin_0, Q2.source, R4.Pin_0, C3.+, C4.0, U2.O, R5.Pin_0
  N3: U1.Control_Voltage, C2.0
  N4: U1.Discharge, R1.Pin_1, D1.anode, D2.cathode
  N5: R2.leg1, D2.anode
  N6: R2.leg2, D1.cathode
  N7: C1.1, S1.L1
  OUT (PWM): R3.Pin_1, Q1.gate
  N8: Q1.drain, Q2.Gate, R4.Pin_1
  OUT (V+): RLoad.Pin_1, Q2.drain
  N9: 5-15V.VCC, U2.P
  N10: C5.1, S1.L2
  N11: R5.Pin_1, LED1.anode
