# Fritzing sketch MotorControlModule (saved by Fritzing 1.0.1rc)
breadboards: 1

parts:
  U1 = 555 Timer [package="SO8 [SMD]"]
  R1 = Resistor [tolerance=±5% resistance=4.6k power=0.25W package=THT]
  D1 = Rectifier Diode [part_number=1N4148 package="300 mil [THT]"]
  D2 = Rectifier Diode [part_number=1N4148 package="300 mil [THT]"]
  C1 = Ceramic Capacitor [capacitance=100nF voltage=35V package="100 mil [THT, multilayer]"]
  R2 = Resistor [tolerance=±5% power=0.25W resistance=2.3k package=THT]
  Power = Screw terminal - 2 pins [package=THT]
  R3 = Dial Potentiometer with switch [knob_status=50% power=0.5W]
  D3 = Rectifier Diode [part_number=1N4148 package="300 mil [THT]"]
  R7 = Resistor [tolerance=±5% power=0.25W resistance=330 package=THT]
  Q1 = MOSFET-NCHANNEL [part_number=P0903BDG package=to220v]
  R8 = Resistor [tolerance=±5% resistance=4.6k power=0.25W package=THT]
  Output = Screw terminal - 2 pins [package=THT]
  D4 = Rectifier Diode [part_number=1N4001 package="300 mil [THT]"]

nets:
  GND/POWER-: U1.Pin_1, C1.0, Power.pin2, D3.anode, Q1.S, R8.Pin_1
  N1: U1.Pin_2, U1.Pin_6, C1.1, R3.wiper
  N2: U1.Pin_3, Q1.G, R8.Pin_0
  N3: U1.Pin_4, U1.Pin_8, R1.Pin_0, D3.cathode, R7.Pin_0
  N4: U1.Pin_7, R1.Pin_1, D2.anode, R2.Pin_1
  N5: D1.cathode, R2.Pin_0
  N6: D1.anode, R3.leg2
  N7: D2.cathode, R3.leg1
  OUTPUT+/POWER+: Power.pin1, R3.switch_leg1, Output.pin1
  VCC: R3.switch_leg2, R7.Pin_1, D4.cathode
  OUTPUT-: Q1.D, Output.pin2, D4.anode

notes:
  OUTPUT
  POWER
