# Fritzing sketch OpAmpDriver (saved by Fritzing 0.9.2b)
breadboards: 1

parts:
  5V = Power plug
  J1 = Piezo Speaker
  IC1 = Dual Op-Amp [part_number=TL072 package=dip08]
  R1 = Resistor [tolerance=±5% resistance=220k package=THT]
  R2 = Resistor [tolerance=±5% resistance=220k package=THT]
  R3 = Resistor [tolerance=±5% resistance=220k package=THT]
  R4 = Resistor [tolerance=±5% resistance=20k package=THT]
  C1 = Ceramic Capacitor [capacitance=10nF package="100 mil [THT, multilayer]"]
  R5 = Resistor [tolerance=±5% resistance=150 package=THT]
  R6 = Resistor [tolerance=±5% resistance=10k package=THT]
  S1 = Pushbutton [package="[THT]"]
  Q1 = Basic FET N-Channel [part_number=2N7000 package="TO220 [THT]"]

nets:
  GND: 5V.GND, J1.pin1, IC1.A_V-, R3.Pin_0, C1.0, S1.Pin_1, S1.Pin_2, Q1.source
  5V: 5V.VCC, IC1.A_V+, R2.Pin_1, R6.Pin_1
  N1: J1.pin2, R5.Pin_0
  N2: IC1.B_+IN, R1.Pin_0, R2.Pin_0, R3.Pin_1, Q1.drain
  N3: IC1.B_-IN, R4.Pin_0, C1.1
  N4: IC1.B_OUT, R1.Pin_1, R4.Pin_1, R5.Pin_1
  N5: R6.Pin_0, S1.Pin_3, S1.Pin_4, Q1.gate
