# Fritzing sketch PiezoBuzzers (saved by Fritzing 0.9.2b)
breadboards: 1

parts:
  5V = Power plug
  U1 = 555 Timer [package="DIP8 [THT]"]
  R1 = Resistor [tolerance=±5% resistance=1k package=THT]
  C1 = Ceramic Capacitor [capacitance=100nF package="100 mil [THT, multilayer]"]
  R2 = Rotary Potentiometer (Small) [maximum_resistance=100kΩ package=THT]
  C2 = Ceramic Capacitor [capacitance=47nF package="100 mil [THT, multilayer]"]
  Piezo = Piezo Speaker
  R3 = Resistor [tolerance=±5% resistance=10k package=THT]
  R4 = Resistor [tolerance=±5% resistance=2.2k package=THT]
  Q1 = Basic FET N-Channel [part_number=2N7000 package="TO220 [THT]"]

nets:
  GND: 5V.GND, U1.Ground, C1.1, C2.1, Q1.source
  VSS: 5V.VCC, U1.Reset, U1.Vcc_Supply_Voltage, R1.Pin_0, Piezo.pin2, R3.Pin_0
  N1: U1.Trigger, U1.Threshold, R2.leg1, C2.0
  N2: U1.Output, Q1.gate
  N3: U1.Control_Voltage, C1.0
  N4: U1.Discharge, R1.Pin_1, R2.wiper
  N5: Piezo.pin1, R3.Pin_1, R4.Pin_0
  N6: R4.Pin_1, Q1.drain

notes:
  Piezo Sensor
