# Fritzing sketch PolarityTester (saved by Fritzing 0.9.2b)
breadboards: 1

parts:
  U2 = IC, DIP package, 14 pins [chip_label=CD4069BE]
  5V = Power plug
  R1 = Resistor [tolerance=±5% resistance=1k package=THT]
  D9 = LED - 5mm [color="Green (570nm)" package="5 mm [THT]"]
  D10 = LED - 5mm [color="Red (660nm)" package="5 mm [THT]"]

nets:
  POLARITY_TEST: U2.pin5, U2.pin11
  N1: U2.pin6, R1.Pin_1
  GND: U2.pin7, 5V.GND
  N2: U2.pin8, D9.cathode, D10.anode
  N3: U2.pin9, U2.pin10
  Vcc: U2.pin14, 5V.VCC
  N4: R1.Pin_0, D9.anode, D10.cathode
