# Fritzing sketch 220VInverter (saved by Fritzing 1.0.1rc)
breadboards: 1

parts:
  NE1 = Neon Lamp [package=0.100"]
  R1 = Resistor [tolerance=±5% power=0.25W resistance=150k package=THT]
  220V_DC_Module = Power plug

nets:
  N1: NE1.1, R1.Pin_1
  N2: NE1.2, 220V_DC_Module.VCC
  N3: R1.Pin_0, 220V_DC_Module.GND

notes:
  220V DC Module Output
