# Fritzing sketch Any2AnyPowerPack (saved by Fritzing 0.9.2b)
breadboards: 1

parts:
  J1 = Power Jack [part_number="any polarity" package=power_jack_pth_lock]
  D1 = Rectifier Diode [part_number=1N5819 package="300 mil [THT]"]
  D2 = Rectifier Diode [part_number=1N5819 package="300 mil [THT]"]
  D3 = Rectifier Diode [part_number=1N5819 package="300 mil [THT]"]
  D4 = Rectifier Diode [part_number=1N5819 package="300 mil [THT]"]
  R1 = Resistor [tolerance=±5% resistance=1k package=THT]
  SW1 = SWITCH_SPDT [package=kps-1290]
  LED1 = LED - 3mm [color="Orange (620nm)" package="3 mm [THT]"]
  J2 = Screw terminal - 2 pins [part_number="centre-positive plug" package=THT]
  Battery = Battery block 9V
  J3 = Screw terminal - 2 pins [part_number="centre-negative plug" package=THT]

nets:
  N1: J1.GND, D2.cathode, D4.anode
  N2: J1.GNDBREAK, Battery.-
  N3: J1.PWR, SW1.P, Battery.+
  P+: D1.cathode, D4.cathode, R1.Pin_0, J2.pin1, J3.pin2
  N4: D1.anode, D3.cathode, SW1.S
  P-: D2.anode, D3.anode, LED1.cathode, J2.pin2, J3.pin1
  N5: R1.Pin_1, LED1.anode
