# Fritzing sketch BBBreakout (saved by Fritzing 0.9.2b)
breadboards: 1

parts:
  LED1 = LED - 3mm [color="Blue (430nm)" package="3 mm [THT]"]
  R1 = Resistor [tolerance=±5% resistance=2.2k package=THT]
  Terminal_Block = Screw terminal - 2 pins [package=THT]
  XH2_54 = female pin header, 2 pins [form="♀ (female)"]
  DCJack = Power plug

nets:
  N1: LED1.cathode, R1.Pin_1
  VCC: LED1.anode, Terminal_Block.pin1, XH2_54.pin1, DCJack.VCC
  GND: R1.Pin_0, Terminal_Block.pin2, XH2_54.pin2, DCJack.GND
