# Fritzing sketch Breadboard5V (saved by Fritzing 0.9.0b)
breadboards: 1

parts:
  C1 = Electrolytic Capacitor [capacitance=100µF package="100 mil [THT, electrolytic]"]
  C2 = Ceramic Capacitor [capacitance=100nF package="100 mil [THT, multilayer]"]
  C3 = Electrolytic Capacitor [capacitance=100µF package="100 mil [THT, electrolytic]"]
  R1 = Resistor [tolerance=±5% resistance=1k package=THT]
  U1 = Voltage Regulator - 5V [package="TO220 [THT]"]
  LED1 = LED - 3mm [color="Green (570nm)" package="3 mm [THT]"]
  S1 = Pushbutton [package=THT]
  VCC1 = Battery block 9V

nets:
  GND: C1.-, C2.1, C3.-, R1.Pin_0, U1.GND, VCC1.-
  N1: C1.+, U1.input_voltage, S1.leg1
  N2: C2.0, C3.+, U1.output_voltage, LED1.anode
  N3: R1.Pin_1, LED1.cathode
  N4: S1.leg0, VCC1.+
