# Fritzing sketch BridgeDoubler (saved by Fritzing 0.9.2b)
breadboards: 1

parts:
  12VAC = Power plug
  D1 = Rectifier Diode [part_number=1N5819 package="300 mil [THT]"]
  D2 = Rectifier Diode [part_number=1N5819 package="300 mil [THT]"]
  D3 = Rectifier Diode [part_number=1N5819 package="300 mil [THT]"]
  D4 = Rectifier Diode [part_number=1N5819 package="300 mil [THT]"]
  C1 = Electrolytic Capacitor [capacitance=100µF voltage=25V package="100 mil [THT, electrolytic]"]
  C2 = Electrolytic Capacitor [capacitance=100µF voltage=25V package="100 mil [THT, electrolytic]"]
  RL = Resistor [tolerance=±5% resistance=10k package=THT]

nets:
  N1: 12VAC.GND, D3.cathode, D4.anode, C1.+, C2.-
  CH1: 12VAC.VCC, D1.cathode, D2.anode
  CH3: D1.anode, D3.anode, C1.-, RL.Pin_0
  CH2: D2.cathode, D4.cathode, C2.+, RL.Pin_1
