# Fritzing sketch CapacitiveDropper (saved by Fritzing 0.9.2b)
breadboards: 1

parts:
  12VAC = Power plug
  R2 = Resistor [tolerance=±5% resistance=100 package=THT]
  R1 = Resistor [tolerance=±5% resistance=220k package=THT]
  C1 = Ceramic Capacitor [capacitance=100nF package="100 mil [THT, multilayer]"]
  D1 = Rectifier Diode [part_number=1N4007 package="300 mil [THT]"]
  D2 = Rectifier Diode [part_number=1N4007 package="300 mil [THT]"]
  D3 = Rectifier Diode [part_number=1N4007 package="300 mil [THT]"]
  D4 = Rectifier Diode [part_number=1N4007 package="300 mil [THT]"]
  C2 = Electrolytic Capacitor [capacitance=220µF package="100 mil [THT, electrolytic]"]
  R3 = Resistor [tolerance=±5% resistance=100k package=THT]
  R4 = Resistor [tolerance=±5% resistance=100 package=THT]
  LED1 = LED - 3mm [color="Blue (430nm)" package="3 mm [THT]"]
  LED2 = LED - 3mm [color="Blue (430nm)" package="3 mm [THT]"]
  LED3 = LED - 3mm [color="Blue (430nm)" package="3 mm [THT]"]

nets:
  N1: 12VAC.GND, R2.Pin_1
  N2: 12VAC.VCC, R1.Pin_1, C1.0
  N3: R2.Pin_0, D1.cathode, D2.anode
  N4: R1.Pin_0, C1.1, D3.cathode, D4.anode
  GND: D1.anode, D3.anode, C2.-, R3.Pin_0, LED3.cathode
  N5: D2.cathode, D4.cathode, C2.+, R3.Pin_1, R4.Pin_0
  N6: R4.Pin_1, LED1.anode
  N7: LED1.cathode, LED2.anode
  N8: LED2.cathode, LED3.anode
