# Fritzing sketch OnePinThreeV (saved by Fritzing 1.0.1rc)
breadboards: 1

parts:
  D1 = Rectifier Diode [part_number=1N4148 package="300 mil [THT]"]
  D2 = Rectifier Diode [part_number=1N4148 package="300 mil [THT]"]
  D3 = Rectifier Diode [part_number=1N4148 package="300 mil [THT]"]
  D4 = Rectifier Diode [part_number=1N4148 package="300 mil [THT]"]
  C1 = Ceramic Capacitor [capacitance=1µF voltage=25V package="100 mil [THT, multilayer]"]
  C2 = Ceramic Capacitor [capacitance=1µF voltage=25V package="100 mil [THT, multilayer]"]
  C3 = Ceramic Capacitor [capacitance=1µF voltage=25V package="100 mil [THT, multilayer]"]
  C6 = Ceramic Capacitor [capacitance=1µF voltage=25V package="100 mil [THT, multilayer]"]
  Rz = Resistor [tolerance=±5% resistance=220 power=0.25W package=THT]
  D7 = Zener Diode [part_number=1N4742 breakdown_voltage=12V package="300 mil [THT]"]
  Part4 = Arduino Uno (Rev3)
  D5 = Rectifier Diode [part_number=1N4148 package="300 mil [THT]"]
  D6 = Rectifier Diode [part_number=1N4148 package="300 mil [THT]"]
  C4 = Ceramic Capacitor [capacitance=1µF voltage=25V package="100 mil [THT, multilayer]"]
  C5 = Ceramic Capacitor [capacitance=1µF voltage=25V package="100 mil [THT, multilayer]"]
  RL = Resistor [tolerance=±5% resistance=10k power=0.25W package=THT]
  Q1 = Basic FET P-Channel [part_number=BS250 package="TO220 [THT]"]
  LED1 = LED - 3mm [color="Green (565nm)" current=0.030A package="3 mm [THT]"]
  Q2 = Basic FET N-Channel [part_number=2N7000 package="D2Pak [SMD]"]
  D9 = Rectifier Diode [part_number=1N5819 package="300 mil [THT]"]
  D8 = Rectifier Diode [part_number=1N4148 package="300 mil [THT]"]
  R1 = Resistor [tolerance=±5% power=0.25W resistance=10k package=THT]
  C7 = Ceramic Capacitor [capacitance=10nF voltage=35V package="100 mil [THT, multilayer]"]
  Q3 = Basic FET N-Channel [part_number=2N7000 package="D2Pak [SMD]"]
  R1_2 = Resistor [tolerance=±5% resistance=10k power=0.25W package=THT]
  F1 = Resettable Fuse PTC [part_number=200mA package=ptc]
  R2 = Resistor [tolerance=±5% power=0.25W resistance=1k package=THT]
  LED2 = LED - 3mm [color="Red (633nm)" current=0.030A package="3 mm [THT]"]

nets:
  N1: D1.cathode, D2.anode, C1.1
  VON: D1.anode, Q1.drain, D9.anode
  N2: D2.cathode, D3.anode, C2.1
  N3: D3.cathode, D4.anode, C3.1
  N4: D4.cathode, D5.anode, C4.1
  CH1/PUMP_A: C1.0, C3.0, Part4.D11_PWM/MOSI, C5.0, D8.anode
  GND: C2.0, C6.0, D7.anode, Part4.GND, C4.0, RL.Pin_0, Q2.source, R1.Pin_1, C7.0, Q3.source, LED2.cathode
  CH3: C6.1, Rz.Pin_0, D6.cathode
  CH2/VHIGH/VOUT: Rz.Pin_1, D7.cathode, LED1.anode, Q2.drain, D9.cathode
  N5: Part4.5V, F1.1
  N6: D5.cathode, D6.anode, C5.1
  N7: RL.Pin_1, LED1.cathode
  N8: Q1.gate, Q2.Gate, Q3.drain, R1_2.Pin_0
  VCC: Q1.source, R1_2.Pin_1, F1.2, R2.Pin_0
  N9: D8.cathode, R1.Pin_0, C7.1, Q3.Gate
  N10: R2.Pin_1, LED2.anode

notes:
  CH2
  CH1
  CH3
