# Fritzing sketch LM2662Inverter (saved by Fritzing 0.9.2b)
breadboards: 1

parts:
  5V = Power plug
  IC1 = LM2662 [part_number=LM2662MX package=dip08]
  C1 = Electrolytic Capacitor [capacitance=47µF package="100 mil [THT, electrolytic]"]
  C2 = Electrolytic Capacitor [capacitance=47µF package="100 mil [THT, electrolytic]"]
  R1 = Resistor [tolerance=±5% resistance=1k package=THT]
  LED1 = LED - 5mm [color="Blue (430nm)" package="5 mm [THT]"]

nets:
  GND: 5V.GND, IC1.GND, IC1.LV, C2.+, LED1.anode
  N1: 5V.VCC, IC1.FC, IC1.V+
  N2: IC1.CAP+, C1.+
  N3: IC1.CAP-, C1.-
  VOUT: IC1.OUT, C2.-, R1.Pin_0
  N4: R1.Pin_1, LED1.cathode

custom parts:
  LM2662: LM2662 in DIP8 compatible packaging
