# Fritzing sketch AMS1117 (saved by Fritzing 0.9.2b)
breadboards: 1

parts:
  4_5-15V = Power plug
  C1 = Tantalum Capacitor [capacitance=22µF package="100 mil [THT, tantalum]"]
  RL = Resistor [tolerance=±5% resistance=10k package=THT]
  IC1 = Voltage Regulator AMS1117 [package=sot223]

nets:
  GND: 4_5-15V.GND, C1.-, RL.Pin_1, IC1.GND
  N1: 4_5-15V.VCC, IC1.IN
  N2: C1.+, RL.Pin_0, IC1.OUT
