# Fritzing sketch LM317CC (saved by Fritzing 0.9.2b)
breadboards: 1

parts:
  VCC1 = Battery block 9V
  R1 = Resistor [tolerance=±5% resistance=470 package=THT]
  C1 = Electrolytic Capacitor [capacitance=10µF package="100 mil [THT, electrolytic]"]
  C2 = Electrolytic Capacitor [capacitance=10µF package="100 mil [THT, electrolytic]"]
  LED1 = LED - 3mm [color="Green (555nm)" package="3 mm [THT]"]
  LED2 = LED - 3mm [color="Green (555nm)" package="3 mm [THT]"]
  LED3 = LED - 3mm [color="Green (555nm)" package="3 mm [THT]"]
  S1 = Pushbutton [package=THT]
  S2 = Pushbutton [package=THT]
  S3 = Pushbutton [package=THT]
  U2 = Voltage Regulator - Variable [part_number=LM317 package="TO220 [THT]"]

nets:
  GND: VCC1.-, C1.-, C2.-, LED3.cathode, S3.leg1
  N1: VCC1.+, C1.+, U2.IN
  N2: R1.Pin_0, U2.OUT
  N3: R1.Pin_1, C2.+, S1.leg1, U2.ADJ
  N4: LED1.cathode, LED2.anode, S2.leg0
  N5: LED1.anode, S1.leg0
  N6: LED2.cathode, LED3.anode, S2.leg1, S3.leg0
