# Fritzing sketch LM7805 (saved by Fritzing 0.9.0b)
breadboards: 1

parts:
  9V = BC9VPC [package=bc9vpc]
  C1 = Electrolytic Capacitor [capacitance=0.1mF package="100 mil [THT, electrolytic]"]
  C2 = Ceramic Capacitor [capacitance=100nF package="100 mil [THT, multilayer]"]
  C3 = Electrolytic Capacitor [capacitance=0.1mF package="100 mil [THT, electrolytic]"]
  LED1 = LED - 5mm [color="Red (633nm)" package="5 mm [THT]"]
  R1 = Resistor [tolerance=±5% resistance=4.7k package=THT]
  U1 = Voltage Regulator - 5V [package="TO220 [THT]"]
  Part1 = Arduino Uno (Rev3)
  Rd1 = Resistor [tolerance=±5% resistance=4.7k package=THT]
  Rd2 = Resistor [tolerance=±5% resistance=4.7k package=THT]

nets:
  N1: 9V.V+, C1.+, U1.input_voltage
  GND: 9V.V-, C1.-, C2.1, C3.-, R1.Pin_0, U1.GND, Part1.GND, Rd2.Pin_0
  N2: C2.0, C3.+, LED1.anode, U1.output_voltage, Rd1.Pin_1
  N3: LED1.cathode, R1.Pin_1
  N4: Part1.A0, Rd1.Pin_0, Rd2.Pin_1
