# Fritzing sketch PowerSupply317Kit (saved by Fritzing 0.9.2b)
breadboards: 1

parts:
  U2 = IC, DIP package, 14 pins [chip_label=CD4069BE]
  220-12V_AC = Transformer [package=transformer]
  P1 = Screw terminal - 2 pins [package=THT]
  P2 = screw terminal, 3 pins
  220V_AC = Power plug
  D1 = Rectifier Diode [part_number=1N4148 package="300 mil [THT]"]
  D2 = Rectifier Diode [part_number=1N4148 package="300 mil [THT]"]
  D3 = Rectifier Diode [part_number=1N4007 package="300 mil [THT]"]
  D4 = Rectifier Diode [part_number=1N4007 package="300 mil [THT]"]
  D5 = Rectifier Diode [part_number=1N4007 package="300 mil [THT]"]
  D6 = Rectifier Diode [part_number=1N4007 package="300 mil [THT]"]
  C4 = Electrolytic Capacitor [capacitance=1mF voltage=35V package="100 mil [THT, electrolytic]"]
  C3 = Ceramic Capacitor [capacitance=100nF package="100 mil [THT, multilayer]"]
  U1 = Voltage Regulator - Variable [part_number=LM317T package="TO220 [THT]"]
  R1 = Resistor [tolerance=±5% resistance=240 package=THT]
  R5 = Trimmer Potentiometer [maximum_resistance=100kΩ package=THT]
  RP1 = Rotary Potentiometer (Small) [maximum_resistance=5kΩ package=THT]
  C5 = Electrolytic Capacitor [capacitance=10µF voltage=25V package="100 mil [THT, electrolytic]"]
  C1 = Electrolytic Capacitor [capacitance=1mF voltage=35V package="100 mil [THT, electrolytic]"]
  C2 = Ceramic Capacitor [capacitance=100nF package="100 mil [THT, multilayer]"]
  R2 = Resistor [tolerance=±5% resistance=1k package=THT]
  D7 = LED - 5mm [color="Blue (430nm)" package="5 mm [THT]"]
  LS1 = Piezo Speaker
  Q1 = NPN-Transistor [part_number=S9014 package="TO92 [THT]"]
  R6 = Resistor [tolerance=±5% resistance=10k package=THT]
  C6 = Electrolytic Capacitor [capacitance=10µF voltage=25V package="100 mil [THT, electrolytic]"]
  R4 = Resistor [tolerance=±5% resistance=100k package=THT]
  R3 = Resistor [tolerance=±5% resistance=1k package=THT]
  D8 = LED - 5mm [color="Yellow (574nm)" package="5 mm [THT]"]
  R0 = Resistor [tolerance=±5% resistance=1k package=THT]
  D9 = LED - 5mm [color="Green (570nm)" package="5 mm [THT]"]
  D10 = LED - 5mm [color="Red (660nm)" package="5 mm [THT]"]
  METER1 = 7-Segment Panel Ammeter

nets:
  N1: U2.pin1, R4.Pin_1
  N2: U2.pin2, U2.pin3, R5.leg2
  N3: U2.pin4, U2.pin13, C6.+
  POLARITY_TEST: U2.pin5, U2.pin11, P2.pin3
  N4: U2.pin6, R0.Pin_1
  GND: U2.pin7, P1.pin2, D5.anode, D6.anode, C4.-, C3.0, RP1.leg1, RP1.wiper, C5.-, C1.-, C2.0, D7.cathode, Q1.E, D8.cathode, METER1.GND
  N5: U2.pin8, D9.cathode, D10.anode
  N6: U2.pin9, U2.pin10
  CLK_OUT: U2.pin12, P2.pin2, R3.Pin_1
  Vo: U2.pin14, P1.pin1, D1.anode, D2.cathode, U1.OUT, R1.Pin_1, C1.+, C2.1, R2.Pin_1, LS1.pin1, METER1.LOAD-
  N7: 220-12V_AC.1, 220V_AC.VCC
  N8: 220-12V_AC.2, 220V_AC.GND
  N9: 220-12V_AC.3, D4.anode, D6.cathode
  N10: 220-12V_AC.4, D3.anode, D5.cathode
  PIEZO_IN: P2.pin1, R6.Pin_0
  Vdc: D1.cathode, D3.cathode, D4.cathode, C4.+, C3.1, U1.IN, METER1.V+
  N11: D2.anode, U1.ADJ, R1.Pin_0, RP1.leg2, C5.+
  N12: R5.leg1, R5.wiper, C6.-, R4.Pin_0
  N13: R2.Pin_0, D7.anode
  N14: LS1.pin2, Q1.C
  N15: Q1.B, R6.Pin_1
  N16: R3.Pin_0, D8.anode
  N17: R0.Pin_0, D9.anode, D10.cathode

notes:
  220V AC to 1.25-12V DC
  Utility Functions
  ignore the breadboard - I haven't tried to lay this out correctly, as it's a dangerous idea to build a mains power supply on a breadboard!
  See the schematic page only.
  Voltmeter
  3-wire Digital Voltmeter

custom parts:
  7-Segment Panel Ammeter: 7-Segment Panel Ammeter (0 to 9.99A)
