# Fritzing sketch BoostBuckConverterModule (saved by Fritzing 1.0.1rc)
breadboards: 1

parts:
  Power_In = Power plug
  Module_Power_In = female pin header, 2 pins [form="♀ (female)"]
  Module_Power_Out = female pin header, 2 pins [form="♀ (female)"]
  METER3 = 7-Segment Panel Ammeter
  R1 = Resistor [tolerance=±5% power=2W resistance=100 package=THT]
  VR1 = Rotary Potentiometer (Small) [maximum_resistance=10kΩ knob_status=50% power=0.5W package=THT]

nets:
  GND/VIN-/VOUT-: Power_In.GND, Module_Power_In.pin2, Module_Power_Out.pin2, METER3.GND, R1.Pin_1, VR1.leg2
  VIN+: Power_In.VCC, Module_Power_In.pin1, METER3.V+
  VOUT+: Module_Power_Out.pin1, METER3.LOAD-, VR1.leg1
  N1: R1.Pin_0, VR1.wiper

notes:
  Module Power In
  Module Power Out
  Test Load(s)

custom parts:
  7-Segment Panel Ammeter: 7-Segment Panel Ammeter (0 to 9.99A)
