# Fritzing sketch LM2596SModule2 (saved by Fritzing 1.0.1rc)
breadboards: 1

parts:
  5V = Power plug
  IC1 = IC, DIP package, 4 pins [chip_label=SMPS]
  LED1 = LED - 5mm [color="Blue (430nm)" current=0.030A package="5 mm [THT]"]
  LED2 = LED - 5mm [color="Blue (430nm)" current=0.030A package="5 mm [THT]"]

nets:
  N1: 5V.GND, IC1.pin1
  N2: 5V.VCC, IC1.pin4
  GND: IC1.pin2, LED1.cathode, LED2.cathode
  CH1: IC1.pin3, LED1.anode, LED2.anode
