# Fritzing sketch XL4015Module2 (saved by Fritzing 1.0.1rc)
breadboards: 1

parts:
  Power = Power plug
  IC1 = IC, DIP package, 8 pins [chip_label=SMPS]
  Rload = Resistor [tolerance=±5% power=5W resistance=10 package=THT]
  J1 = female pin header, 3 pins [form="♀ (female)"]
  Part1 = FTDI Basic Programmer

nets:
  GND: Power.GND, IC1.pin1, J1.pin1, Part1.GND
  N1: Power.VCC, IC1.pin8
  RXD: IC1.pin2, J1.pin2, Part1.TXO
  TXD: IC1.pin3, J1.pin3, Part1.RXI
  OUT-: IC1.pin4, Rload.Pin_1
  N2: IC1.pin5, Rload.Pin_0
