# Fritzing sketch BuckConverter (saved by Fritzing 0.9.2b)
breadboards: 1

parts:
  J1 = Screw terminal - 2 pins [package=THT]
  Rsc = Resistor [tolerance=±5% resistance=0.25 package=THT]
  R1 = Resistor [tolerance=±5% resistance=2k package=THT]
  R2 = Resistor [tolerance=±5% resistance=6.8k package=THT]
  U1 = IC, DIP package, 8 pins [chip_label=34063 part_number=MC34063AP]
  Rl = Resistor [tolerance=±5% resistance=1k package=THT]
  Ct = Ceramic Capacitor [capacitance=630pF package="100 mil [THT, multilayer]"]
  D1 = Rectifier Diode [part_number=1N5819 package="300 mil [THT]"]
  Co = Electrolytic Capacitor [capacitance=47µF package="100 mil [THT, electrolytic]"]
  L1 = Inductor [inductance=47µH package="400 mil [THT]"]
  C4 = Electrolytic Capacitor [capacitance=100µF package="100 mil [THT, electrolytic]"]
  Vin = Power plug
  LED1 = LED - 3mm [color="Green (555nm)" package="3 mm [THT]"]

nets:
  VOUT: J1.pin1, R2.Pin_1, Co.+, L1.pin_1, LED1.anode
  GND: J1.pin2, R1.Pin_1, U1.pin4, Rl.Pin_1, Ct.0, D1.anode, Co.-, C4.-, Vin.GND
  VIN: Rsc.Pin_0, U1.pin6, C4.+, Vin.VCC
  N1: Rsc.Pin_1, U1.pin1, U1.pin7, U1.pin8
  N2: R1.Pin_0, R2.Pin_0, U1.pin5
  N3: U1.pin2, D1.cathode, L1.pin_0
  N4: U1.pin3, Ct.1
  N5: Rl.Pin_0, LED1.cathode
