# Fritzing sketch ModuleKit (saved by Fritzing 0.9.2b)
breadboards: 1

parts:
  J1 = Screw terminal - 2 pins [package=THT]
  J2 = Screw terminal - 2 pins [package=THT]
  C4 = Ceramic Capacitor [capacitance=100nF package="100 mil [THT, multilayer]"]
  R1 = Resistor [tolerance=±5% resistance=200 package=THT]
  R2 = Resistor [tolerance=±5% resistance=1 package=THT]
  R3 = Resistor [tolerance=±5% resistance=10k package=THT]
  R4 = Resistor [tolerance=±5% resistance=1.2k package=THT]
  U1 = IC, DIP package, 8 pins [chip_label=34063 part_number=MC34063AP1]
  R5 = Resistor [tolerance=±5% resistance=4.7k package=THT]
  C2 = Ceramic Capacitor [capacitance=100nF package="100 mil [THT, multilayer]"]
  C3 = Ceramic Capacitor [capacitance=100pF package="100 mil [THT, multilayer]"]
  D1 = Rectifier Diode [part_number=1N5819 package="300 mil [THT]"]
  D2 = LED - 5mm [color="Red (633nm)" package="5 mm [THT]"]
  C1 = Electrolytic Capacitor [capacitance=47µF package="100 mil [THT, electrolytic]"]
  L1 = Inductor [inductance=150µH package="400 mil [THT]"]

nets:
  OUT+: J1.pin1, D1.cathode, C1.+
  GND/IN-/OUT-: J1.pin2, J2.pin2, C4.0, R4.Pin_0, U1.pin2, U1.pin4, C2.0, C3.0, D2.cathode, C1.-
  IN+: J2.pin1, C4.1, R2.Pin_0, U1.pin6
  N1: R1.Pin_0, L1.pin_0
  N2: R1.Pin_1, U1.pin8
  N3: R2.Pin_1, U1.pin7
  N4: R3.Pin_0, R5.Pin_0, C2.1
  N5: R3.Pin_1, R4.Pin_1, U1.pin5
  N6: U1.pin1, D1.anode, L1.pin_1
  N7: U1.pin3, C3.1
  N8: R5.Pin_1, D2.anode
