# Fritzing sketch Breadboarded (saved by Fritzing 0.9.2b)
breadboards: 1

parts:
  IC1 = IC, DIP package, 6 pins [chip_label=MT3608]
  5V = Power plug
  D1 = Rectifier Diode [part_number=1N5819 package="300 mil [THT]"]
  L1 = Inductor [inductance=22µH package="400 mil [THT]"]
  R2 = Resistor [tolerance=±5% resistance=2.2k package=THT]
  C1 = Ceramic Capacitor [capacitance=22µF package="100 mil [THT, multilayer]"]
  C2 = Ceramic Capacitor [capacitance=22µF package="100 mil [THT, multilayer]"]
  R1 = Trimmer Potentiometer [maximum_resistance=100kΩ package=THT]
  LED1 = LED - 3mm [color="Red (633nm)" package="3 mm [THT]"]
  RL = Resistor [tolerance=±5% resistance=10k package=THT]
  METER1 = 7-Segment Panel Voltmeter

nets:
  N1: IC1.pin1, D1.anode, L1.pin_0
  GND: IC1.pin2, 5V.GND, R2.Pin_1, C1.0, C2.0, RL.Pin_0, METER1.V-
  N2: IC1.pin3, R2.Pin_0, R1.leg2
  N3: IC1.pin4, IC1.pin5, 5V.VCC, L1.pin_1, C1.1
  VOUT: D1.cathode, C2.1, R1.leg1, R1.wiper, LED1.anode, METER1.V+
  N4: LED1.cathode, RL.Pin_1

notes:
  VOUT
  VIN

custom parts:
  7-Segment Panel Voltmeter: 7-Segment Panel Voltmeter (4.5 - 30V)
