# Fritzing sketch WirelessLedModule (saved by Fritzing 0.9.2b)
breadboards: 1

parts:
  IC1 = IC, DIP package, 8 pins [chip_label=XKT-511]
  3-12V = Power plug
  R1 = Resistor [tolerance=±5% resistance=200k package=THT]
  C1 = Ceramic Capacitor [capacitance=100nF package="100 mil [THT, multilayer]"]
  R2 = Resistor [tolerance=±5% resistance=900M package=THT]
  C2 = Ceramic Capacitor [capacitance=100nF package="100 mil [THT, multilayer]"]
  L1 = Inductor [package="400 mil [THT]"]

nets:
  N1: IC1.pin1, R2.Pin_1
  N2: IC1.pin2, R1.Pin_1, R2.Pin_0
  GND: IC1.pin3, IC1.pin4, 3-12V.GND, C1.0
  N3: IC1.pin5, C2.0, L1.pin_1
  N4: IC1.pin7, IC1.pin8, 3-12V.VCC, R1.Pin_0, C1.1, C2.1, L1.pin_0

notes:
  Note: rough redraw of the module circuit. Component values TBC
  XKT-511 Transmitting Module
