# Fritzing sketch ZenerDropper (saved by Fritzing 1.0.1rc)
breadboards: 1

parts:
  D1 = Zener Diode [part_number=1N4728 breakdown_voltage=3.3 package="Melf DO-213 AB [SMD]"]
  R1 = Resistor [tolerance=±5% power=0.25W resistance=1k package=THT]
  Vout = female pin header, 1 pin [form="♀ (female)"]
  SIGNAL = female pin header, 1 pin [form="♀ (female)"]
  Power = Power plug
  U2 = LM 358 Dual Op-Amp [part_number=LM358 package="DIP8 [THT]"]

nets:
  CH1/Vin: D1.cathode, U2.connector5, U2.connector6
  CH2: D1.anode, R1.Pin_0, Vout.pin1
  GND: R1.Pin_1, Power.GND, U2.connector3
  CH3: SIGNAL.pin1, U2.connector4
  12V: Power.VCC, U2.connector7

notes:
  SIGNAL Generator In/
  CH3
  Vout/CH2
  Vin/CH1
