# Fritzing sketch pp3power (saved by Fritzing 1.0.1rc)
breadboards: 1

parts:
  J1 = Screw terminal - 2 pins [package=THT]
  Rsc = Resistor [tolerance=±5% resistance=1 power=0.25W package=THT]
  R1 = Resistor [tolerance=±5% resistance=12k power=0.25W package=THT]
  R2 = Resistor [tolerance=±5% resistance=20k power=0.25W package=THT]
  U1 = IC, DIP package, 8 pins [chip_label=34063 part_number=MC34063AP]
  Rl = Resistor [tolerance=±5% resistance=1k power=0.25W package=THT]
  Ct = Ceramic Capacitor [capacitance=630pF voltage=35V package="100 mil [THT, multilayer]"]
  D1 = Rectifier Diode [part_number=1N5819 package="300 mil [THT]"]
  Co = Electrolytic Capacitor [capacitance=10µF voltage=35V package="100 mil [THT, electrolytic]"]
  L1 = Inductor [inductance=330µH package="400 mil [THT]"]
  C4 = Electrolytic Capacitor [capacitance=100µF package="100 mil [THT, electrolytic]"]
  Vin = Power plug
  LED1 = LED - 3mm [color="Green (555nm)" current=0.030A package="3 mm [THT]"]
  J2 = female pin header, 2 pins [form="♀ (female)"]
  R2b = Resistor [tolerance=±5% resistance=33k power=0.25W package=THT]
  R2c = Resistor [tolerance=±5% resistance=33k power=0.25W package=THT]

nets:
  VOUT: J1.pin1, Co.+, L1.pin_1, LED1.anode, J2.pin1, R2b.Pin_1, R2c.Pin_1
  GND: J1.pin2, R1.Pin_1, U1.pin4, Rl.Pin_1, Ct.0, D1.anode, Co.-, C4.-, Vin.GND
  VIN: Rsc.Pin_0, U1.pin6, C4.+, Vin.VCC
  N1: Rsc.Pin_1, U1.pin1, U1.pin7, U1.pin8
  N2: R1.Pin_0, R2.Pin_0, U1.pin5
  N3: R2.Pin_1, J2.pin2, R2b.Pin_0, R2c.Pin_0
  N4: U1.pin2, D1.cathode, L1.pin_0
  N5: U1.pin3, Ct.1
  N6: Rl.Pin_0, LED1.cathode
