# Fritzing sketch Power317 (saved by Fritzing 0.9.0b)
breadboards: 1

parts:
  LM317 = Voltage Regulator - Variable [package="TO220 [THT]"]
  R1 = Resistor [tolerance=±5% resistance=220 package=THT]
  LED1 = LED - 5mm [color="Red (633nm)" package="5 mm [THT]"]
  RL = Resistor [tolerance=±5% resistance=4.7k package=THT]
  VCC1 = Battery block 9V
  R2 = Resistor [tolerance=±5% resistance=100 package=THT]
  Part1 = Arduino Uno (Rev3)
  Rd1 = Resistor [tolerance=±5% resistance=4.7k package=THT]
  Rd2 = Resistor [tolerance=±5% resistance=4.7k package=THT]
  R3 = Trimmer Potentiometer [maximum_resistance=10kΩ package=THT]

nets:
  N1: LM317.ADJ, R1.Pin_0, R2.Pin_1
  N2: LM317.OUT, R1.Pin_1, LED1.anode, Rd1.Pin_1
  N3: LM317.IN, VCC1.+
  N4: LED1.cathode, RL.Pin_1
  N5: RL.Pin_0, VCC1.-, Part1.GND, Rd2.Pin_0, R3.leg1
  N6: R2.Pin_0, R3.wiper
  N7: Part1.A0, Rd1.Pin_0, Rd2.Pin_1
