# Fritzing sketch PowerLD1117 (saved by Fritzing 0.9.2b)
breadboards: 1

parts:
  U1 = Voltage Regulator - 3.3V [part_number=LD1117-33 package="TO220 [THT]"]
  4_5-18V = Power plug
  C1 = Electrolytic Capacitor [capacitance=10µF package="100 mil [THT, electrolytic]"]
  C2 = Electrolytic Capacitor [capacitance=100µF package="100 mil [THT, electrolytic]"]
  RL = Resistor [tolerance=±5% resistance=10k package=THT]

nets:
  N1: U1.input_voltage, 4_5-18V.VCC, C1.+
  GND: U1.GND, 4_5-18V.GND, C1.-, C2.-, RL.Pin_1
  N2: U1.output_voltage, C2.+, RL.Pin_0
