# Fritzing sketch PowerMB102 (saved by Fritzing 0.9.0b)
breadboards: 1

parts:
  LED1 = LED - 5mm [color="Red (633nm)" package="5 mm [THT]"]
  R1 = Resistor [tolerance=±5% resistance=4.7k package=THT]
  Part1 = Arduino Uno (Rev3)
  Rd1 = Resistor [tolerance=±5% resistance=4.7k package=THT]
  Rd2 = Resistor [tolerance=±5% resistance=4.7k package=THT]
  5V = Power plug
  3_3V = Power plug
  LED2 = LED - 5mm [color="Red (633nm)" package="5 mm [THT]"]
  R2 = Resistor [tolerance=±5% resistance=4.7k package=THT]
  Rd3 = Resistor [tolerance=±5% resistance=4.7k package=THT]
  Rd4 = Resistor [tolerance=±5% resistance=4.7k package=THT]

nets:
  GND: LED1.cathode, Part1.GND, Rd2.Pin_0, 5V.GND, 3_3V.GND, LED2.cathode, Rd4.Pin_1
  N1: LED1.anode, R1.Pin_1
  N2: R1.Pin_0, Rd1.Pin_1, 5V.VCC
  N3: Part1.A0, Rd1.Pin_0, Rd2.Pin_1
  N4: Part1.A1, Rd3.Pin_0, Rd4.Pin_0
  N5: 3_3V.VCC, R2.Pin_0, Rd3.Pin_1
  N6: LED2.anode, R2.Pin_1

notes:
  5V supply selected
  3.3V supply selected
