# Fritzing sketch QuadNOR (saved by Fritzing 0.9.0b)
breadboards: 1

parts:
  Part1 = Arduino Uno (Rev3)
  IC1 = 74LS02 [package=dil14]
  LED1 = LED - 3mm [color="Blue (430nm)" package="3 mm [THT]"]
  LED2 = LED - 3mm [color="Green (555nm)" package="3 mm [THT]"]
  LED3 = LED - 3mm [color="Yellow (595nm)" package="3 mm [THT]"]
  R1 = Resistor [tolerance=±5% resistance=1k package=THT]
  R2 = Resistor [tolerance=±5% resistance=1k package=THT]
  R3 = Resistor [tolerance=±5% resistance=1k package=THT]

nets:
  N1: Part1.D8, IC1.B1
  N2: Part1.D9_PWM, IC1.A1
  GND: Part1.GND, IC1.GND, R1.Pin_0, R2.Pin_0, R3.Pin_1
  N3: Part1.D6_PWM, IC1.B2
  N4: Part1.D7, IC1.A2
  Vcc: Part1.5V, IC1.VCC
  N5: IC1.Y1, IC1.B4, LED2.anode
  N6: IC1.Y2, IC1.A4, LED3.anode
  N7: IC1.Y4, LED1.anode
  N8: LED1.cathode, R3.Pin_0
  N9: LED2.cathode, R2.Pin_1
  N10: LED3.cathode, R1.Pin_1

custom parts:
  74LS02: 74LS02 Quad 2-input NOR
