# Fritzing sketch CurrentSource50uA (saved by Fritzing 1.0.1rc)
breadboards: 1

parts:
  IC1 = IC, DIP package, 8 pins [chip_label=REF200 part_number=REF200]
  5V = Power plug
  IC2 = LM2662 [part_number=LM2662MX package=dip08]
  C2 = Electrolytic Capacitor [capacitance=47µF voltage=35V package="100 mil [THT, electrolytic]"]
  C3 = Electrolytic Capacitor [capacitance=47µF voltage=35V package="100 mil [THT, electrolytic]"]
  AM1 = Multimeter (DC Current)

nets:
  Cout+: IC1.pin1, IC1.pin4, AM1.A_Probe
  Vs-: IC1.pin2, IC2.OUT, C3.-
  N1: IC1.pin3, IC1.pin7
  GND: IC1.pin5, 5V.GND, IC2.GND, IC2.LV, C3.+, AM1.COM_Probe
  Vs+: IC1.pin8, 5V.VCC, IC2.FC, IC2.V+
  N2: IC2.CAP+, C2.+
  N3: IC2.CAP-, C2.-

custom parts:
  LM2662: LM2662 in DIP8 compatible packaging
