# Fritzing sketch RSFlipFlop_NORLatch (saved by Fritzing 0.9.0b)
breadboards: 1

parts:
  IC1 = 74LS02 [package=dil14]
  LED1 = LED - 3mm [color="Green (555nm)" package="3 mm [THT]"]
  LED2 = LED - 3mm [color="Yellow (595nm)" package="3 mm [THT]"]
  R2 = Resistor [tolerance=±5% resistance=1k package=THT]
  R1 = Resistor [tolerance=±5% resistance=1k package=THT]
  S1 = Pushbutton [package="[THT]"]
  S2 = Pushbutton [package="[THT]"]
  R3 = Resistor [tolerance=±5% resistance=10k package=THT]
  R4 = Resistor [tolerance=±5% resistance=10k package=THT]
  5V = Power plug

nets:
  N1: IC1.Y1, IC1.A2, LED1.anode
  N2: IC1.A1, S2.Pin_1, S2.Pin_2, R4.Pin_1
  N3: IC1.B1, IC1.Y2, LED2.anode
  N4: IC1.B2, S1.Pin_3, S1.Pin_4, R3.Pin_1
  GND: IC1.GND, R2.Pin_0, R1.Pin_0, R3.Pin_0, R4.Pin_0, 5V.GND
  Vcc: IC1.VCC, S1.Pin_1, S1.Pin_2, S2.Pin_3, S2.Pin_4, 5V.VCC
  N5: LED1.cathode, R1.Pin_1
  N6: LED2.cathode, R2.Pin_1

custom parts:
  74LS02: 74LS02 Quad 2-input NOR
