# Fritzing sketch RelaxationJouleThief (saved by Fritzing 0.9.2b)
breadboards: 1

parts:
  R1 = Resistor [tolerance=±5% resistance=22k package=THT]
  R2 = Resistor [tolerance=±5% resistance=10k package=THT]
  C1 = Ceramic Capacitor [capacitance=10nF package="100 mil [THT, multilayer]"]
  L1 = Inductor [inductance=1mH package="400 mil [THT]"]
  U1 = Battery Holders [part_number="1.5V AAA" package=battery-aaa]
  LED1 = LED - 3mm [color="Red (633nm)" package="3 mm [THT]"]
  Q1 = NPN-Transistor [part_number=2N3904 package="TO92 [THT]"]
  Q2 = NPN-Transistor [part_number=2N3904 package="TO92 [THT]"]
  LED2 = LED - 3mm [color="Red (633nm)" package="3 mm [THT]"]

nets:
  CH4: R1.Pin_0, R2.Pin_0, L1.pin_0, U1.+, LED2.anode
  CH2: R1.Pin_1, C1.1, Q1.B
  CH3: R2.Pin_1, Q1.C, Q2.B
  CH1: C1.0, L1.pin_1, LED1.anode, Q2.C
  GND: U1.-, LED1.cathode, Q1.E, Q2.E, LED2.cathode

notes:
  this LED won't light as the forward voltage is higher than the battery
  This LED does light up
