# Fritzing sketch NAND (saved by Fritzing 0.9.2b)
breadboards: 1

parts:
  Part1 = Arduino Uno (Rev3)
  QB = NPN-Transistor [part_number=2N3904 package="TO92 [THT]"]
  RbB = Resistor [tolerance=±5% resistance=10k package=THT]
  LED1 = LED - 3mm [color="Green (555nm)" package="3 mm [THT]"]
  R1 = Resistor [tolerance=±5% resistance=1k package=THT]
  QA = NPN-Transistor [part_number=2N3904 package="TO92 [THT]"]
  RbA = Resistor [tolerance=±5% resistance=10k package=THT]
  Rp = Resistor [tolerance=±5% resistance=4.7k package=THT]

nets:
  A: Part1.A0, Part1.D7, RbA.Pin_0
  B: Part1.A1, Part1.D6_PWM, RbB.Pin_0
  OUT: Part1.A2, QB.C, R1.Pin_0, Rp.Pin_0
  N1: Part1.5V, Rp.Pin_1
  GND: Part1.GND, LED1.cathode, QA.E
  N2: QB.E, QA.C
  N3: QB.B, RbB.Pin_1
  N4: LED1.anode, R1.Pin_1
  N5: QA.B, RbA.Pin_1
