# Fritzing sketch NOT (saved by Fritzing 0.9.2b)
breadboards: 1

parts:
  Part1 = Arduino Uno (Rev3)
  Q2 = NPN-Transistor [part_number=2N3904 package="TO92 [THT]"]
  Rc = Resistor [tolerance=±5% resistance=4.7k package=THT]
  Rb = Resistor [tolerance=±5% resistance=10k package=THT]
  LED1 = LED - 3mm [color="Green (555nm)" package="3 mm [THT]"]
  R1 = Resistor [tolerance=±5% resistance=1k package=THT]

nets:
  A: Part1.A0, Part1.D6_PWM, Rb.Pin_0
  OUT: Part1.A1, Q2.C, Rc.Pin_1, R1.Pin_0
  N1: Part1.5V, Rc.Pin_0
  GND: Part1.GND, Q2.E, LED1.cathode
  N2: Q2.B, Rb.Pin_1
  N3: LED1.anode, R1.Pin_1
