# Fritzing sketch XOR (saved by Fritzing 0.9.2b)
breadboards: 1

parts:
  Part1 = Arduino Uno (Rev3)
  LED1 = LED - 3mm [color="Green (555nm)" package="3 mm [THT]"]
  R1 = Resistor [tolerance=±5% resistance=1k package=THT]
  Q1 = PNP-Transistor [part_number=2N3906 package="TO92 [THT]"]
  D1 = Rectifier Diode [part_number=1N4148 package="300 mil [THT]"]
  D2 = Rectifier Diode [part_number=1N4148 package="300 mil [THT]"]
  Rp = Resistor [tolerance=±5% resistance=10k package=THT]
  D3 = Rectifier Diode [part_number=1N4148 package="300 mil [THT]"]
  D4 = Rectifier Diode [part_number=1N4148 package="300 mil [THT]"]
  R2 = Resistor [tolerance=±5% resistance=10k package=THT]

nets:
  A: Part1.A0, Part1.D7, D3.anode, D4.cathode
  B: Part1.A1, Part1.D6_PWM, D1.cathode, D2.anode
  OUT: Part1.A2, R1.Pin_0, Q1.C, Rp.Pin_0
  GND: Part1.GND, LED1.cathode, Rp.Pin_1
  N1: LED1.anode, R1.Pin_1
  N2: Q1.E, D2.cathode, D3.cathode
  N3: Q1.B, R2.Pin_1
  N4: D1.anode, D4.anode, R2.Pin_0
