# Fritzing sketch RgbLedGlow (saved by Fritzing 0.9.2b)
breadboards: 1

parts:
  U1 = LM 358 Dual Op-Amp [part_number=LM358 package="SO 08 [SMD]"]
  R3 = Resistor [tolerance=±5% resistance=100k package=THT]
  R4 = Resistor [tolerance=±5% resistance=47k package=THT]
  R5 = Trimmer Potentiometer [maximum_resistance=100kΩ package=THT]
  C1 = Electrolytic Capacitor [capacitance=100µF package="100 mil [THT, electrolytic]"]
  R6 = Resistor [tolerance=±5% resistance=22k package=THT]
  5-12V = Power plug
  Q1 = PNP-Transistor [part_number=2N3906 package="TO92 [THT]"]
  LED1 = RGB LED - (4 legs) [package="5 mm [THT]"]
  R7 = Resistor [tolerance=±5% resistance=10k package=THT]
  R8 = Resistor [tolerance=±5% resistance=680 package=THT]
  Q2 = PNP-Transistor [part_number=2N3906 package="TO92 [THT]"]
  R9 = Resistor [tolerance=±5% resistance=10k package=THT]
  R10 = Resistor [tolerance=±5% resistance=680 package=THT]
  Q3 = PNP-Transistor [part_number=2N3906 package="TO92 [THT]"]
  R11 = Resistor [tolerance=±5% resistance=10k package=THT]
  R12 = Resistor [tolerance=±5% resistance=680 package=THT]
  U2 = LM 358 Dual Op-Amp [part_number=LM358 package="SO 08 [SMD]"]
  R13 = Resistor [tolerance=±5% resistance=100k package=THT]
  R14 = Resistor [tolerance=±5% resistance=47k package=THT]
  C2 = Electrolytic Capacitor [capacitance=100µF package="100 mil [THT, electrolytic]"]
  R15 = Resistor [tolerance=±5% resistance=22k package=THT]
  U3 = LM 358 Dual Op-Amp [part_number=LM358 package="SO 08 [SMD]"]
  R16 = Resistor [tolerance=±5% resistance=100k package=THT]
  R17 = Resistor [tolerance=±5% resistance=47k package=THT]
  C3 = Electrolytic Capacitor [capacitance=100µF package="100 mil [THT, electrolytic]"]
  R18 = Resistor [tolerance=±5% resistance=22k package=THT]
  Q4 = PNP-Transistor [part_number=2N3906 package="TO92 [THT]"]
  Q5 = PNP-Transistor [part_number=2N3906 package="TO92 [THT]"]
  Q6 = PNP-Transistor [part_number=2N3906 package="TO92 [THT]"]
  LED2 = RGB LED - (4 legs) [package="5 mm [THT]"]
  R19 = Resistor [tolerance=±5% resistance=10k package=THT]
  R20 = Resistor [tolerance=±5% resistance=10k package=THT]
  R21 = Resistor [tolerance=±5% resistance=10k package=THT]
  R22 = Resistor [tolerance=±5% resistance=360 package=THT]
  R23 = Resistor [tolerance=±5% resistance=360 package=THT]
  R24 = Resistor [tolerance=±5% resistance=360 package=THT]

nets:
  OSCG: U1.connector0, R4.Pin_1, C1.+, R9.Pin_0, R20.Pin_0
  N1: U1.connector1, C1.-, R6.Pin_1
  VREF: U1.connector2, U1.connector5, R5.wiper, U2.connector2, U2.connector5, U3.connector2, U3.connector5
  GND: U1.connector3, R5.leg2, 5-12V.GND, R8.Pin_1, R10.Pin_1, R12.Pin_1, U2.connector3, U3.connector3, R22.Pin_1, R23.Pin_1, R24.Pin_1
  N2: U1.connector4, R3.Pin_0, R4.Pin_0
  N3: U1.connector6, R3.Pin_1, R6.Pin_0
  VCC: U1.connector7, R5.leg1, 5-12V.VCC, LED1.common_anode, U2.connector7, U3.connector7, LED2.common_anode
  N4: Q1.E, LED1.red_cathode
  N5: Q1.B, R7.Pin_1
  N6: Q1.C, R8.Pin_0
  N7: LED1.green_cathode, Q2.E
  N8: LED1.blue_cathode, Q3.E
  OSCR: R7.Pin_0, U2.connector0, R14.Pin_1, C2.+, R21.Pin_0
  N9: Q2.B, R9.Pin_1
  N10: Q2.C, R10.Pin_0
  N11: Q3.B, R11.Pin_1
  N12: Q3.C, R12.Pin_0
  OSCB: R11.Pin_0, U3.connector0, R17.Pin_1, C3.+, R19.Pin_0
  N13: U2.connector1, C2.-, R15.Pin_1
  N14: U2.connector4, R13.Pin_0, R14.Pin_0
  N15: U2.connector6, R13.Pin_1, R15.Pin_0
  N16: U3.connector1, C3.-, R18.Pin_1
  N17: U3.connector4, R16.Pin_0, R17.Pin_0
  N18: U3.connector6, R16.Pin_1, R18.Pin_0
  N19: Q4.E, R22.Pin_0
  N20: Q4.B, R19.Pin_1
  N21: Q4.C, LED2.blue_cathode
  N22: Q5.E, R23.Pin_0
  N23: Q5.B, R20.Pin_1
  N24: Q5.C, LED2.green_cathode
  N25: Q6.E, R24.Pin_0
  N26: Q6.B, R21.Pin_1
  N27: Q6.C, LED2.red_cathode

notes:
  PNP Orientation 1: conventional. bright but limited glow transition
  PNP Orientation 2: arse-about. lower current but expanded glow transition
  PNP Option #1
  PNP Option #2
