# Fritzing sketch RingCounter (saved by Fritzing 0.9.2b)
breadboards: 1

parts:
  U1 = 555 Timer [package="DIP8 [THT]"]
  IC1 = IC, DIP package, 16 pins [chip_label=CD4017 part_number=CD4017]
  VCC = Power plug
  C1 = Electrolytic Capacitor [capacitance=1µF package="100 mil [THT, electrolytic]"]
  R1 = Trimmer Potentiometer [maximum_resistance=50kΩ package=THT]
  R2 = Resistor [tolerance=±5% resistance=10k package=THT]
  R3 = Resistor [tolerance=±5% resistance=2.2k package=THT]
  C2 = Electrolytic Capacitor [capacitance=1µF package="100 mil [THT, electrolytic]"]
  LED1 = LED - 5mm [color="Red (633nm)" package="5 mm [THT]"]
  LED2 = LED - 5mm [color="Red (633nm)" package="5 mm [THT]"]
  LED3 = LED - 5mm [color="Red (633nm)" package="5 mm [THT]"]
  LED4 = LED - 5mm [color="Red (633nm)" package="5 mm [THT]"]
  LED5 = LED - 5mm [color="Red (633nm)" package="5 mm [THT]"]
  LED6 = LED - 5mm [color="Red (633nm)" package="5 mm [THT]"]
  LED7 = LED - 5mm [color="Red (633nm)" package="5 mm [THT]"]
  LED8 = LED - 5mm [color="Red (633nm)" package="5 mm [THT]"]
  LED9 = LED - 5mm [color="Red (633nm)" package="5 mm [THT]"]
  LED10 = LED - 5mm [color="Red (633nm)" package="5 mm [THT]"]
  R4 = Resistor [tolerance=±5% resistance=1k package=THT]
  R5 = Resistor [tolerance=±5% resistance=1k package=THT]
  R6 = Resistor [tolerance=±5% resistance=1k package=THT]
  R7 = Resistor [tolerance=±5% resistance=1k package=THT]
  R8 = Resistor [tolerance=±5% resistance=1k package=THT]
  R9 = Resistor [tolerance=±5% resistance=1k package=THT]
  R10 = Resistor [tolerance=±5% resistance=1k package=THT]
  R11 = Resistor [tolerance=±5% resistance=1k package=THT]
  R12 = Resistor [tolerance=±5% resistance=1k package=THT]
  R13 = Resistor [tolerance=±5% resistance=1k package=THT]

nets:
  GND: U1.Ground, IC1.pin8, IC1.pin13, IC1.pin15, VCC.GND, C1.-, C2.-, R4.Pin_1, R5.Pin_1, R6.Pin_1, R7.Pin_1, R8.Pin_1, R9.Pin_1, R10.Pin_1, R11.Pin_1, R12.Pin_1, R13.Pin_1
  N1: U1.Trigger, U1.Threshold, C1.+, R1.wiper
  N2: U1.Output, IC1.pin14
  N3: U1.Reset, U1.Vcc_Supply_Voltage, IC1.pin16, VCC.VCC, R3.Pin_1, C2.+
  N4: U1.Discharge, R2.Pin_1, R3.Pin_0
  Q5: IC1.pin1, LED6.anode
  Q1: IC1.pin2, LED2.anode
  Q0: IC1.pin3, LED1.anode
  Q2: IC1.pin4, LED3.anode
  Q6: IC1.pin5, LED7.anode
  Q7: IC1.pin6, LED8.anode
  Q3: IC1.pin7, LED4.anode
  Q8: IC1.pin9, LED9.anode
  Q4: IC1.pin10, LED5.anode
  Q9: IC1.pin11, LED10.anode
  N5: R1.leg2, R2.Pin_0
  N6: LED1.cathode, R4.Pin_0
  N7: LED2.cathode, R5.Pin_0
  N8: LED3.cathode, R6.Pin_0
  N9: LED4.cathode, R7.Pin_0
  N10: LED5.cathode, R8.Pin_0
  N11: LED6.cathode, R9.Pin_0
  N12: LED7.cathode, R10.Pin_0
  N13: LED8.cathode, R11.Pin_0
  N14: LED9.cathode, R12.Pin_0
  N15: LED10.cathode, R13.Pin_0
