# Fritzing sketch IncrementalTester (saved by Fritzing 0.9.2b)
breadboards: 1

parts:
  RE1 = Rotary Encoder [package=THT]
  IC1 = IC, DIP package, 16 pins [chip_label=74LS173]
  R1 = Resistor [tolerance=±5% resistance=10k package=THT]
  5V = Power plug
  R2 = Resistor [tolerance=±5% resistance=10k package=THT]
  C1 = Ceramic Capacitor [capacitance=100nF package="100 mil [THT, multilayer]"]
  C2 = Ceramic Capacitor [capacitance=100nF package="100 mil [THT, multilayer]"]
  LED1 = LED - 3mm [color="Red (633nm)" package="3 mm [THT]"]
  R3 = Resistor [tolerance=±5% resistance=1k package=THT]
  LED2 = LED - 3mm [color="Green (570nm)" package="3 mm [THT]"]
  R4 = Resistor [tolerance=±5% resistance=1k package=THT]

nets:
  A: RE1.EncoderPinA, IC1.pin7, R2.Pin_1, C2.1
  GND: RE1.EncoderPinC, IC1.pin1, IC1.pin2, IC1.pin8, IC1.pin9, IC1.pin10, IC1.pin11, IC1.pin12, IC1.pin15, 5V.GND, C1.1, C2.0, R3.Pin_0
  B: RE1.EncoderPinB, IC1.pin13, IC1.pin14, R1.Pin_1, C1.0
  N1: IC1.pin3, LED2.cathode
  N2: IC1.pin4, LED1.anode
  VCC: IC1.pin16, R1.Pin_0, 5V.VCC, R2.Pin_0, R4.Pin_0
  N3: LED1.cathode, R3.Pin_1
  N4: LED2.anode, R4.Pin_1
