# Fritzing sketch SCRLatch (saved by Fritzing 0.9.2b)
breadboards: 1

parts:
  T1 = SCR [part_number=BT169D package=to-92]
  5V = Power plug
  LED1 = LED - 5mm [color="Blue (525nm)" package="5 mm [THT]"]
  R1 = Resistor [tolerance=±5% resistance=100 package=THT]
  R2 = Resistor [tolerance=±5% resistance=10k package=THT]
  S2_N/O_TRIGGER = Pushbutton [package="[THT]"]
  S1_N/C_"RESET" = Toggle Switch [package=THT]
  R3 = Resistor [tolerance=±5% resistance=1M package=THT]

nets:
  GND: T1.k, 5V.GND, R3.Pin_0
  N1: T1.g, R2.Pin_1
  CH2_PROBE: T1.a, LED1.cathode
  VCC: 5V.VCC, S2_N/O_TRIGGER.Pin_1, S2_N/O_TRIGGER.Pin_2, S1_N/C_"RESET".COM
  N2: LED1.anode, R1.Pin_1
  N3: R1.Pin_0, S1_N/C_"RESET".L1
  CH1_PROBE: R2.Pin_0, S2_N/O_TRIGGER.Pin_3, S2_N/O_TRIGGER.Pin_4, R3.Pin_1

custom parts:
  SCR: Low-power generic SCR package
