# Fritzing sketch Star (saved by Fritzing 0.9.2b)
breadboards: 1

parts:
  4-6V = Power plug
  R1 = Resistor [tolerance=±5% resistance=47k package=THT]
  U1 = LM 358 Dual Op-Amp [package="DIP8 [THT]"]
  R2 = Resistor [tolerance=±5% resistance=47k package=THT]
  LED1-20 = LED - 5mm [color="Red (633nm)" package="5 mm [THT]"]
  R3 = Resistor [tolerance=±5% resistance=100k package=THT]
  Q1 = NPN-Transistor [part_number=8050 package="TO92 [THT]"]
  R4 = Resistor [tolerance=±5% resistance=47k package=THT]
  R5 = Resistor [tolerance=±5% resistance=22 package=THT]
  R6 = Resistor [tolerance=±5% resistance=33k package=THT]
  C1 = Electrolytic Capacitor [capacitance=47µF package="100 mil [THT, electrolytic]"]

nets:
  GND: 4-6V.GND, U1.connector3, R2.Pin_0, LED1-20.cathode
  N1: 4-6V.VCC, R1.Pin_0, U1.connector7, Q1.C
  N2: R1.Pin_1, U1.connector2, U1.connector5, R2.Pin_1
  N3: U1.connector0, Q1.B, R6.Pin_1, C1.+
  N4: U1.connector1, R4.Pin_1, C1.-
  N5: U1.connector4, R3.Pin_1, R6.Pin_0
  N6: U1.connector6, R3.Pin_0, R4.Pin_0
  N7: LED1-20.anode, R5.Pin_1
  N8: Q1.E, R5.Pin_0
