# Fritzing sketch SchmittInverter (saved by Fritzing 0.9.2b)
breadboards: 1

parts:
  IC1 = Hex Inverter Schmitt Trigger SN74HC14 [package="DIP (Dual Inline)"]
  R1 = Resistor [tolerance=±5% resistance=1k package=THT]
  Part1 = Arduino Uno (Rev3)

nets:
  N1: IC1.1A, R1.Pin_0, Part1.A0
  N2: IC1.1Y, Part1.A1
  GND: IC1.2A, IC1.3A, IC1.GND, IC1.4A, IC1.5A, IC1.6A, Part1.GND
  VCC: IC1.VCC, Part1.5V
  PULSE: R1.Pin_1, Part1.D8
