# Fritzing sketch schmitt_oscillator (saved by Fritzing 0.9.0b)
breadboards: 1

parts:
  IC1 = Hex Inverter Schmitt Trigger SN74HC14 [package="DIP (Dual Inline)"]
  R1 = Resistor [tolerance=±5% resistance=1k package=THT]
  Part1 = Arduino Uno (Rev3)
  C1 = Electrolytic Capacitor [capacitance=0.47mF package="100 mil [THT, electrolytic]"]
  LED1 = LED - 5mm [color="Red (633nm)" package="5 mm [THT]"]
  R2 = Resistor [tolerance=±5% resistance=1k package=THT]
  R3 = Resistor [tolerance=±5% resistance=1k package=THT]
  Q1 = TRANSISTOR_NPN_2 [package=to-92]

nets:
  N1: IC1.1A, R1.Pin_1, Part1.A0, C1.+
  N2: IC1.1Y, R1.Pin_0, Part1.A1, R3.Pin_0
  GND: IC1.2A, IC1.3A, IC1.GND, IC1.4A, IC1.5A, IC1.6A, Part1.GND, C1.-, LED1.cathode
  VCC: IC1.VCC, Part1.5V, R2.Pin_0
  N3: LED1.anode, Q1.E
  N4: R2.Pin_1, Q1.C
  N5: R3.Pin_1, Q1.B
