# Fritzing sketch BasicDiscrete (saved by Fritzing 0.9.2b)
breadboards: 1

parts:
  5V = Power plug
  Q1 = NPN-Transistor [part_number=2N3904 package="TO92 [THT]"]
  Q2 = NPN-Transistor [part_number=2N3904 package="TO92 [THT]"]
  R1 = Resistor [tolerance=±5% resistance=1.8k package=THT]
  R2 = Resistor [tolerance=±5% resistance=1k package=THT]
  R3 = Resistor [tolerance=±5% resistance=100 package=THT]
  R4 = Resistor [tolerance=±5% resistance=10k package=THT]

nets:
  GND: 5V.GND, R3.Pin_0
  N1: 5V.VCC, R1.Pin_1, R2.Pin_1
  N2: Q1.E, Q2.E, R3.Pin_1
  IN: Q1.B
  N3: Q1.C, R1.Pin_0, R4.Pin_0
  N4: Q2.B, R4.Pin_1
  OUT: Q2.C, R2.Pin_0

notes:
  IN
  OUT
