# Fritzing sketch PowerOkIndicator (saved by Fritzing 0.9.2b)
breadboards: 1

parts:
  D1 = Rectifier Diode [part_number=1N4148 package="300 mil [THT]"]
  5V = Power plug
  IC1 = Hex Inverter Schmitt Trigger SN74HC14 [package="DIP (Dual Inline)"]
  R1 = Resistor [tolerance=±5% resistance=1k package=THT]
  R2 = Resistor [tolerance=±5% resistance=1M package=THT]
  C1 = Electrolytic Capacitor [capacitance=1µF package="100 mil [THT, electrolytic]"]
  R3 = Resistor [tolerance=±5% resistance=470 package=THT]
  LED1 = LED - 3mm [color="White (4500K)" package="3 mm [THT]"]
  S2 = Toggle Switch [package=THT]

nets:
  CH1: D1.cathode, R2.Pin_0, S2.COM
  CH2: D1.anode, IC1.1A, R2.Pin_1, C1.+
  GND: 5V.GND, IC1.GND, C1.-, R3.Pin_0, S2.L2
  VCC: 5V.VCC, IC1.VCC, R1.Pin_0
  N1: IC1.1Y, IC1.2A
  CH3: IC1.2Y, LED1.anode
  N2: R1.Pin_1, S2.L1
  N3: R3.Pin_1, LED1.cathode

notes:
  CH1
  CH2
  CH3
