# Fritzing sketch SwitchDebouncer (saved by Fritzing 0.9.2b)
breadboards: 1

parts:
  5V = Power plug
  IC1 = Hex Inverter Schmitt Trigger SN74HC14 [package="DIP (Dual Inline)"]
  R2 = Resistor [tolerance=±5% resistance=10k package=THT]
  R1 = Resistor [tolerance=±5% resistance=100k package=THT]
  C1 = Electrolytic Capacitor [capacitance=1µF package="100 mil [THT, electrolytic]"]
  R3 = Resistor [tolerance=±5% resistance=470 package=THT]
  LED1 = LED - 3mm [color="White (4500K)" package="3 mm [THT]"]
  S1 = Pushbutton [package="[THT]"]

nets:
  GND: 5V.GND, IC1.GND, C1.-, R3.Pin_0, S1.Pin_3, S1.Pin_4
  VCC: 5V.VCC, IC1.VCC, R1.Pin_1
  CH2: IC1.1A, R2.Pin_0, R1.Pin_0, C1.+
  N1: IC1.1Y, IC1.2A
  CH3: IC1.2Y, LED1.anode
  CH1: R2.Pin_1, S1.Pin_1, S1.Pin_2
  N2: R3.Pin_1, LED1.cathode

notes:
  CH1
  CH2
