# Fritzing sketch RS232TTLModule (saved by Fritzing 0.9.2b)
breadboards: 1

parts:
  IC1 = IC, DIP package, 16 pins [chip_label=MAX3232CSE]
  C1 = Ceramic Capacitor [capacitance=100nF package="100 mil [THT, multilayer]"]
  USB5V = Power plug
  J2 = DB9 Connector [package=db9]
  J1 = female pin header, 4 pins [form="♀ (female)"]
  R1 = Resistor [tolerance=±5% resistance=1k package=THT]
  LED1 = LED - 3mm [color="Red (633nm)" package="3 mm [THT]"]
  C2 = Ceramic Capacitor [capacitance=100nF package="100 mil [THT, multilayer]"]
  C3 = Ceramic Capacitor [capacitance=100nF package="100 mil [THT, multilayer]"]
  C4 = Ceramic Capacitor [capacitance=100nF package="100 mil [THT, multilayer]"]
  C5 = Ceramic Capacitor [capacitance=100nF package="100 mil [THT, multilayer]"]

nets:
  N1: IC1.pin1, C1.1
  N2: IC1.pin2, C2.0
  N3: IC1.pin3, C1.0
  N4: IC1.pin4, C4.1
  N5: IC1.pin5, C4.0
  N6: IC1.pin6, C3.1
  TXD: IC1.pin11, J1.pin3
  RXD: IC1.pin12, J1.pin2
  N7: IC1.pin13, J2.3
  N8: IC1.pin14, J2.2
  GND: IC1.pin15, USB5V.GND, J2.5, J1.pin4, R1.Pin_0, C3.0, C5.0
  VCC: IC1.pin16, USB5V.VCC, J1.pin1, LED1.anode, C2.1, C5.1
  N9: R1.Pin_1, LED1.cathode
