# Fritzing sketch UsbToRJ45 (saved by Fritzing 0.9.2b)
breadboards: 1

parts:
  IC2 = IC, DIP package, 16 pins [chip_label=CH340G]
  JP2 = USB_MICROB_PLUG [package=micro-b-th]
  C4 = Ceramic Capacitor [capacitance=100nF package="100 mil [THT, multilayer]"]
  C3 = Ceramic Capacitor [capacitance=10nF package="100 mil [THT, multilayer]"]
  XTAL2 = Crystal [frequency="8 MHz" part_number=12MHz package=THT]
  C1 = Ceramic Capacitor [capacitance=22pF package="100 mil [THT, multilayer]"]
  C2 = Ceramic Capacitor [capacitance=22pF package="100 mil [THT, multilayer]"]
  LED1 = LED - 3mm [color="Red (633nm)" package="3 mm [THT]"]
  R1 = Resistor [tolerance=±5% resistance=2.2k package=THT]
  IC3 = IC, DIP package, 16 pins [chip_label=MAX3232ESE]
  C5 = Ceramic Capacitor [capacitance=100nF package="100 mil [THT, multilayer]"]
  C6 = Ceramic Capacitor [capacitance=100nF package="100 mil [THT, multilayer]"]
  C7 = Ceramic Capacitor [capacitance=100nF package="100 mil [THT, multilayer]"]
  C8 = Ceramic Capacitor [capacitance=100nF package="100 mil [THT, multilayer]"]
  C9 = Ceramic Capacitor [capacitance=100nF package="100 mil [THT, multilayer]"]
  LED2 = LED - 3mm [color="Orange (605nm)" package="3 mm [THT]"]
  R2 = Resistor [tolerance=±5% resistance=2.2k package=THT]
  LED3 = LED - 3mm [color="Blue (430nm)" package="3 mm [THT]"]
  R3 = Resistor [tolerance=±5% resistance=2.2k package=THT]
  U1 = RJ45 Jack [package=rj45-8]
  J4 = shrouded pin header, 10 pins [form="♂ (shrouded male)"]

nets:
  GND: IC2.pin1, JP2.GND, C4.0, C3.0, C1.0, C2.1, R1.Pin_0, IC3.pin15, C5.1, C8.0, C9.0, U1.4, J4.pin5
  TXD: IC2.pin2, IC3.pin10, R3.Pin_0
  RXD: IC2.pin3, IC3.pin9, R2.Pin_0
  N1: IC2.pin4, C3.1
  N2: IC2.pin5, JP2.D+
  N3: IC2.pin6, JP2.D-
  N4: IC2.pin7, XTAL2.pin_0, C1.1
  N5: IC2.pin8, XTAL2.pin_1, C2.0
  vcc: IC2.pin16, JP2.VCC, C4.1, LED1.anode, IC3.pin16, C9.1, LED2.anode, LED3.anode
  N6: LED1.cathode, R1.Pin_1
  N7: IC3.pin1, C6.1
  N8: IC3.pin2, C5.0
  N9: IC3.pin3, C6.0
  N10: IC3.pin4, C7.1
  N11: IC3.pin5, C7.0
  N12: IC3.pin6, C8.1
  TXOUT: IC3.pin7, U1.6, J4.pin2
  RXIN: IC3.pin8, U1.3, J4.pin3
  N13: LED2.cathode, R2.Pin_1
  N14: LED3.cathode, R3.Pin_1
  CTS/RTS: U1.1, U1.8
  DSR/DTR: U1.2, U1.7

notes:
  CH340G USB-Serial Interface
  MAX3232 TTL-RS232 Module
  IDC to RJ45M Connector (null modem)
