# Fritzing sketch CH340GProtoboard (saved by Fritzing 0.9.2b)
breadboards: 1

parts:
  IC2 = IC, DIP package, 16 pins [chip_label=CH340G]
  JP2 = USB_MICROB_PLUG [package=micro-b-th]
  C3 = Ceramic Capacitor [capacitance=100nF package="100 mil [THT, multilayer]"]
  R4 = Resistor [tolerance=±5% resistance=910 package=THT]
  R5 = Resistor [tolerance=±5% resistance=910 package=THT]
  C4 = Ceramic Capacitor [capacitance=10nF package="100 mil [THT, multilayer]"]
  XTAL2 = Crystal [frequency="8 MHz" part_number=12MHz package=THT]
  C1 = Ceramic Capacitor [capacitance=22pF package="100 mil [THT, multilayer]"]
  C2 = Ceramic Capacitor [capacitance=22pF package="100 mil [THT, multilayer]"]
  LED1 = LED - 3mm [color="Red (633nm)" package="3 mm [THT]"]
  R1 = Resistor [tolerance=±5% resistance=2.7k package=THT]
  LED3 = LED - 3mm [color="Blue (430nm)" package="3 mm [THT]"]
  LED2 = LED - 3mm [color="Green (570nm)" package="3 mm [THT]"]
  R2 = Resistor [tolerance=±5% resistance=2.7k package=THT]
  R3 = Resistor [tolerance=±5% resistance=2.7k package=THT]
  F1 = Resettable Fuse PTC [part_number=500mA package=ptc-1206]
  J1 = female pin header, 6 pins [form="♀ (female)"]

nets:
  GND: IC2.pin1, JP2.GND, C3.0, C4.0, C1.0, C2.1, R1.Pin_0, J1.pin6
  TXD: IC2.pin2, R5.Pin_0, LED3.cathode
  RXD: IC2.pin3, R4.Pin_0, LED2.cathode
  N1: IC2.pin4, C4.1
  N2: IC2.pin5, JP2.D+
  N3: IC2.pin6, JP2.D-
  N4: IC2.pin7, XTAL2.pin_0, C1.1
  N5: IC2.pin8, XTAL2.pin_1, C2.0
  CTS: IC2.pin9, J1.pin5
  DTR: IC2.pin13, J1.pin1
  vcc: IC2.pin16, C3.1, LED1.anode, R2.Pin_0, R3.Pin_0, F1.2, J1.pin4
  N6: JP2.VCC, F1.1
  TX: R4.Pin_1, J1.pin2
  RX: R5.Pin_1, J1.pin3
  N7: LED1.cathode, R1.Pin_1
  N8: LED3.anode, R3.Pin_1
  N9: LED2.anode, R2.Pin_1
