# Fritzing sketch UsbUartCH340G (saved by Fritzing 0.9.2b)
breadboards: 2

parts:
  U1 = atmega328 [package=dip]
  XTAL1 = Crystal [frequency="16 Mhz" package=THT]
  C1 = Ceramic Capacitor [capacitance=22pF package="100 mil [THT, multilayer]"]
  C2 = Ceramic Capacitor [capacitance=22pF package="100 mil [THT, multilayer]"]
  R1 = Resistor [tolerance=±5% resistance=10k package=THT]
  RESET = Pushbutton [package="[THT]"]
  R2 = Resistor [tolerance=±5% resistance=1k package=THT]
  LED1 = LED - 3mm [color="Blue (430nm)" package="3 mm [THT]"]
  C3 = Ceramic Capacitor [capacitance=100nF package="100 mil [THT, multilayer]"]
  IC2 = IC, DIP package, 16 pins [chip_label=CH340G]
  JP2 = USB_MICROB_PLUG [package=micro-b-th]
  C4 = Ceramic Capacitor [capacitance=100nF package="100 mil [THT, multilayer]"]
  C5 = Ceramic Capacitor [capacitance=100nF package="100 mil [THT, multilayer]"]
  R3 = Resistor [tolerance=±5% resistance=1k package=THT]
  R4 = Resistor [tolerance=±5% resistance=1k package=THT]
  C6 = Ceramic Capacitor [capacitance=10nF package="100 mil [THT, multilayer]"]
  XTAL2 = Crystal [frequency="8 MHz" part_number=12MHz package=THT]
  C7 = Ceramic Capacitor [capacitance=22pF package="100 mil [THT, multilayer]"]
  C8 = Ceramic Capacitor [capacitance=22pF package="100 mil [THT, multilayer]"]
  LED2 = LED - 3mm [color="Red (633nm)" package="3 mm [THT]"]
  R5 = Resistor [tolerance=±5% resistance=2.2k package=THT]
  LED3 = LED - 3mm [color="Blue (430nm)" package="3 mm [THT]"]
  LED4 = LED - 3mm [color="Yellow (595nm)" package="3 mm [THT]"]
  R6 = Resistor [tolerance=±5% resistance=2.2k package=THT]
  R7 = Resistor [tolerance=±5% resistance=2.2k package=THT]

nets:
  N1: U1.RESET, R1.Pin_1, RESET.Pin_1, RESET.Pin_2, C3.0
  TXD: U1.D0_(RX), R3.Pin_0, LED3.cathode
  RXD: U1.D1_(TX), R4.Pin_0, LED4.cathode
  vcc: U1.VCC, U1.AVCC, R1.Pin_0, IC2.pin16, JP2.VCC, C4.1, C5.1, LED2.anode, R6.Pin_0, R7.Pin_0
  GND: U1.GND, C1.0, C2.1, RESET.Pin_3, RESET.Pin_4, LED1.cathode, IC2.pin1, JP2.GND, C4.0, C5.0, C6.0, C7.0, C8.1, R5.Pin_0
  N2: U1.XLAT1, XTAL1.pin_0, C1.1
  N3: U1.XLAT2, XTAL1.pin_1, C2.0
  N4: U1.D13, R2.Pin_0
  N5: R2.Pin_1, LED1.anode
  DTR: C3.1, IC2.pin13
  N6: IC2.pin2, R3.Pin_1
  N7: IC2.pin3, R4.Pin_1
  N8: IC2.pin4, C6.1
  N9: IC2.pin5, JP2.D+
  N10: IC2.pin6, JP2.D-
  N11: IC2.pin7, XTAL2.pin_0, C7.1
  N12: IC2.pin8, XTAL2.pin_1, C8.0
  N13: LED2.cathode, R5.Pin_1
  N14: LED3.anode, R7.Pin_1
  N15: LED4.anode, R6.Pin_1

notes:
  ATmega328 Target on Breadboard
  CH340G USB-Serial Interface
