# Fritzing sketch SimplePeakDetector (saved by Fritzing 0.9.2b)
breadboards: 1

parts:
  D1 = Rectifier Diode [part_number=1N4007 package="300 mil [THT]"]
  R1 = Resistor [tolerance=±5% resistance=100k package=THT]
  C1 = Electrolytic Capacitor [capacitance=10µF package="100 mil [THT, electrolytic]"]
  Part1 = Arduino Uno (Rev3)

nets:
  PEAK_SIGNAL: D1.cathode, R1.Pin_1, C1.+, Part1.A1
  SIGNAL_IN: D1.anode, Part1.A0
  GND: R1.Pin_0, C1.-, Part1.GND
