# Fritzing sketch SimplestNAND (saved by Fritzing 0.9.0b)
breadboards: 1

parts:
  Part1 = Arduino Uno (Rev3)
  R3 = Resistor [tolerance=±5% resistance=4.7k package=THT]
  R1 = Resistor [tolerance=±5% resistance=10k package=THT]
  Q1 = NPN-Transistor [package="TO92 [THT]"]
  Q2 = NPN-Transistor [package="TO92 [THT]"]
  R2 = Resistor [tolerance=±5% resistance=10k package=THT]
  LED1 = LED - 5mm [color="Red (633nm)" package="5 mm [THT]"]

nets:
  N1: Part1.A0, Part1.D8, R1.Pin_0
  N2: Part1.A1, Part1.D9_PWM, R2.Pin_0
  N3: Part1.A2, R3.Pin_1, Q1.C, LED1.anode
  N4: Part1.GND, Q2.E, LED1.cathode
  N5: Part1.5V, R3.Pin_0
  N6: R1.Pin_1, Q1.B
  N7: Q1.E, Q2.C
  N8: Q2.B, R2.Pin_1
