# Fritzing sketch SolenoidDIY (saved by Fritzing 0.9.2b)
breadboards: 1

parts:
  L1 = Inductor [package="400 mil [THT]"]
  9V1A = Power plug
  Part1 = Arduino Uno (Rev3)
  Q1 = Basic FET N-Channel [part_number=IRF540N package="DPak [SMD]"]
  R1 = Resistor [tolerance=±5% resistance=2.2k package=THT]
  LED1 = LED - 5mm [color="Blue (430nm)" package="5 mm [THT]"]
  D1 = Rectifier Diode [part_number=1N4001 package="300 mil [THT]"]

nets:
  N1: L1.pin_0, Q1.drain, LED1.cathode, D1.anode
  N2: L1.pin_1, 9V1A.VCC, R1.Pin_0, D1.cathode
  GND: 9V1A.GND, Part1.GND, Q1.source
  N3: Part1.D6_PWM, Q1.Gate
  N4: R1.Pin_1, LED1.anode
