# Fritzing sketch StairStepGenerator (saved by Fritzing 0.9.2b)
breadboards: 1

parts:
  Q1 = NPN-Transistor [part_number=2N3904 package="TO92 [THT]"]
  Q2 = NPN-Transistor [part_number=2N3904 package="TO92 [THT]"]
  D1 = Rectifier Diode [part_number=1N4148 package="300 mil [THT]"]
  D2 = Rectifier Diode [part_number=1N4148 package="300 mil [THT]"]
  R1 = Resistor [tolerance=±5% resistance=39.8k part_number=6.8+33 package=THT]
  R2 = Resistor [tolerance=±5% resistance=4.7k package=THT]
  C1 = Ceramic Capacitor [capacitance=10nF package="100 mil [THT, multilayer]"]
  5V = Power plug
  R3 = Resistor [tolerance=±5% resistance=10k package=THT]
  C2 = Ceramic Capacitor [capacitance=10nF package="100 mil [THT, multilayer]"]
  D3 = Rectifier Diode [part_number=1N4148 package="300 mil [THT]"]
  D4 = Rectifier Diode [part_number=1N4148 package="300 mil [THT]"]
  R4 = Resistor [tolerance=±5% resistance=33k package=THT]
  R5 = Resistor [tolerance=±5% resistance=2.2k package=THT]
  R6 = Resistor [tolerance=±5% resistance=33k package=THT]
  R7 = Resistor [tolerance=±5% resistance=33k package=THT]
  R8 = Resistor [tolerance=±5% resistance=15k part_number=10+10|10 package=THT]
  R9 = Resistor [tolerance=±5% resistance=6.8k package=THT]
  R10 = Resistor [tolerance=±5% resistance=6.8k package=THT]
  R11 = Resistor [tolerance=±5% resistance=10k package=THT]
  R12 = Resistor [tolerance=±5% resistance=10k package=THT]
  R13 = Resistor [tolerance=±5% resistance=10k package=THT]
  R14 = Resistor [tolerance=±5% resistance=10k package=THT]
  C3 = Ceramic Capacitor [capacitance=100nF package="100 mil [THT, multilayer]"]
  U1 = 555 Timer [package="SO8 [SMD]"]
  C4 = Ceramic Capacitor [capacitance=100nF package="100 mil [THT, multilayer]"]
  U2 = LMV324 [part_number=LMV324 package=so014]

nets:
  GND: Q1.E, Q2.E, C1.0, 5V.GND, C2.0, R7.Pin_1, R9.Pin_1, R12.Pin_1, C3.1, U1.Pin_1, C4.1, U2.G$1_-V
  N1: Q1.B, Q2.B, R10.Pin_1
  N2: Q1.C, R3.Pin_1, U1.Pin_4
  N3: Q2.C, R13.Pin_1, R14.Pin_1, C3.0, U2.G$4_+IN
  N4: D1.cathode, D2.anode, C1.1, U1.Pin_2, U1.Pin_6
  N5: D1.anode, R1.Pin_0, R2.Pin_1, U1.Pin_7
  N6: D2.cathode, R1.Pin_1
  VCC: R2.Pin_0, 5V.VCC, R3.Pin_0, R6.Pin_0, U1.Pin_8, U2.G$1_+V
  N7: C2.1, U1.Pin_5
  N8: D3.cathode, R4.Pin_1
  N9: D3.anode, D4.cathode, C4.0, U2.G$1_-IN
  N10: D4.anode, R5.Pin_1
  CH2: R4.Pin_0, R5.Pin_0, R8.Pin_0, R9.Pin_0, R10.Pin_0, U2.G$1_OUT
  N11: R6.Pin_1, R7.Pin_0, R8.Pin_1, U2.G$1_+IN
  CH3/OUTPUT: R11.Pin_0, R13.Pin_0, U2.G$4_OUT
  N12: R11.Pin_1, R12.Pin_0, U2.G$4_-IN
  CH1: R14.Pin_0, U1.Pin_3
