# Fritzing sketch StayCreative (saved by Fritzing 0.9.2b)
breadboards: 1

parts:
  5-9V = Power plug
  MIC1 = Microphone
  C1 = Ceramic Capacitor [capacitance=1µF package="100 mil [THT, multilayer]"]
  R1 = Resistor [tolerance=±5% resistance=22k package=THT]
  R2 = Resistor [tolerance=±5% resistance=22k package=THT]
  R3 = Trimmer Potentiometer [maximum_resistance=100kΩ package=THT]
  U1 = TL072/TLE2072 Dual Op. Amp [part_number=LM358 package="DIP8 [THT]"]
  R4 = Resistor [tolerance=±5% resistance=1k package=THT]
  R5 = Resistor [tolerance=±5% resistance=330k package=THT]
  LED1 = LED - 3mm [color="Blue (430nm)" package="3 mm [THT]"]
  LED2 = LED - 3mm [color="Blue (430nm)" package="3 mm [THT]"]
  Q1 = MOSFET-NCHANNEL [part_number=2N7000 package=to220v]
  IC2 = IC, DIP package, 4 pins [chip_label=SMPS]

nets:
  GND: 5-9V.GND, MIC1.pin2, R2.Pin_1, R3.leg1, U1.Pin_4, R4.Pin_1, Q1.S, IC2.pin1, IC2.pin2
  VCC: 5-9V.VCC, R1.Pin_0, U1.Pin_8, IC2.pin4
  N1: MIC1.pin1, C1.1, R1.Pin_1
  N2: C1.0, R2.Pin_0, R3.leg2
  N3: R3.wiper, U1.Pin_3
  N4: U1.Pin_1, R5.Pin_1, Q1.G
  N5: U1.Pin_2, R4.Pin_0, R5.Pin_0
  N6: LED1.cathode, LED2.cathode, Q1.D
  3V: LED1.anode, LED2.anode, IC2.pin3

notes:
  LEDx65

custom parts:
  TL072/TLE2072 Dual Op. Amp: The classic LM 358 Dual Operational Amplifier (Op-Amp). The analog swiss-army knife.
