# Fritzing sketch SubtractionLoopCounterKit (saved by Fritzing 0.9.2b)
breadboards: 1

parts:
  IC1 = IC, DIP package, 14 pins [chip_label=CD4011]
  IC2 = IC, DIP package, 14 pins [chip_label=CD4011]
  IC3 = IC, DIP package, 16 pins [chip_label=74HC192]
  IC4 = IC, DIP package, 16 pins [chip_label=CD4511]
  C2 = Ceramic Capacitor [capacitance=100nF package="100 mil [THT, multilayer]"]
  R8 = Resistor [tolerance=±5% resistance=390k package=THT]
  RP1 = Trimmer Potentiometer [maximum_resistance=3.3MΩ package=THT]
  R9 = Resistor [tolerance=±5% resistance=10k package=THT]
  S1 = Pushbutton [package=THT]
  LED0 = 7 Segment Display
  R1 = Resistor [tolerance=±5% resistance=560 package=THT]
  R2 = Resistor [tolerance=±5% resistance=560 package=THT]
  R3 = Resistor [tolerance=±5% resistance=560 package=THT]
  R4 = Resistor [tolerance=±5% resistance=560 package=THT]
  R5 = Resistor [tolerance=±5% resistance=560 package=THT]
  R6 = Resistor [tolerance=±5% resistance=560 package=THT]
  R7 = Resistor [tolerance=±5% resistance=560 package=THT]
  S2 = Pushbutton [package=THT]
  R10 = Resistor [tolerance=±5% resistance=10k package=THT]
  S3 = Pushbutton [package=THT]
  R11 = Resistor [tolerance=±5% resistance=10k package=THT]
  R12 = Resistor [tolerance=±5% resistance=10k package=THT]
  S4 = Pushbutton [package=THT]
  R13 = Resistor [tolerance=±5% resistance=10k package=THT]
  S5 = Pushbutton [package=THT]
  R14 = Resistor [tolerance=±5% resistance=10k package=THT]
  S6 = Pushbutton [package=THT]
  5V = Power plug
  R0 = Resistor [tolerance=±5% resistance=1k package=THT]
  LED1 = LED - 3mm [color="Red (633nm)" package="3 mm [THT]"]
  C1 = Ceramic Capacitor [capacitance=100nF package="100 mil [THT, multilayer]"]
  C3 = Ceramic Capacitor [capacitance=100nF package="100 mil [THT, multilayer]"]
  C4 = Ceramic Capacitor [capacitance=100nF package="100 mil [THT, multilayer]"]
  C5 = Ceramic Capacitor [capacitance=100nF package="100 mil [THT, multilayer]"]

nets:
  Q0: IC1.pin1, IC3.pin3, IC4.pin7
  Q3: IC1.pin2, IC3.pin7, IC4.pin6
  NOT9: IC1.pin3, IC1.pin5, IC1.pin6
  IS9: IC1.pin4, IC2.pin8
  GND: IC1.pin7, IC2.pin7, IC3.pin8, IC4.pin5, IC4.pin8, RP1.leg1, RP1.wiper, S1.leg0, LED0.common_cathode#3, R10.Pin_1, S3.leg0, S4.leg0, S5.leg0, S6.leg0, 5V.GND, LED1.cathode, C1.0, C3.0, C4.0, C5.0
  P3: IC1.pin8, IC3.pin9, R14.Pin_1, S6.leg1
  P0: IC1.pin9, IC3.pin15, S3.leg1, R11.Pin_1
  PSET: IC1.pin10, IC2.pin9
  CLKBUFFERED/TP1: IC1.pin11, IC2.pin13
  CLKSW: IC1.pin12, IC1.pin13, IC2.pin1, IC2.pin2, IC2.pin4
  VCC: IC1.pin14, IC2.pin14, IC3.pin16, IC4.pin3, IC4.pin4, IC4.pin16, R9.Pin_0, S2.leg1, R11.Pin_0, R12.Pin_0, R13.Pin_0, R14.Pin_0, 5V.VCC, R0.Pin_1, C1.1, C3.1, C4.1, C5.1
  N1: IC2.pin3, C2.1
  N2: IC2.pin5, IC2.pin6, C2.0, R8.Pin_1
  PL: IC2.pin10, IC3.pin11
  CLK/TP2: IC2.pin11, IC3.pin4
  N3: IC2.pin12, R9.Pin_1, S1.leg1
  P1: IC3.pin1, R12.Pin_1, S4.leg1
  Q1: IC3.pin2, IC4.pin1
  Q2: IC3.pin6, IC4.pin2
  P2: IC3.pin10, R13.Pin_1, S5.leg1
  N4: IC3.pin14, S2.leg0, R10.Pin_0
  N5: IC4.pin9, R5.Pin_0
  N6: IC4.pin10, R4.Pin_0
  N7: IC4.pin11, R3.Pin_0
  N8: IC4.pin12, R2.Pin_0
  N9: IC4.pin13, R1.Pin_0
  N10: IC4.pin14, R7.Pin_0
  N11: IC4.pin15, R6.Pin_0
  N12: R8.Pin_0, RP1.leg2
  N13: LED0.Segment_A#1, R7.Pin_1
  N14: LED0.Segment_F, R6.Pin_1
  N15: LED0.Segment_E, R5.Pin_1
  N16: LED0.Segment_D, R4.Pin_1
  N17: LED0.Segment_C, R3.Pin_1
  N18: LED0.Segment_B, R2.Pin_1
  N19: LED0.Segment_A#10, R1.Pin_1
  N20: R0.Pin_0, LED1.anode
