# Fritzing sketch BasicBuckAvrControl (saved by Fritzing 0.9.2b)
breadboards: 1

parts:
  Part1 = Arduino Uno (Rev3)
  R3 = Trimmer Potentiometer [maximum_resistance=10kΩ package=THT]
  Q1 = NPN-Transistor [part_number=2N3904 package="TO92 [THT]"]
  R2 = Resistor [tolerance=±5% resistance=1k package=THT]
  R1 = Resistor [tolerance=±5% resistance=1k package=THT]
  9V = Power plug
  L1 = Inductor [inductance=1mH package="400 mil [THT]"]
  D1 = Rectifier Diode [part_number=1N5819 package="300 mil [THT]"]
  C1 = Electrolytic Capacitor [capacitance=47µF package="100 mil [THT, electrolytic]"]
  Rload = Resistor [tolerance=±5% resistance=50 power=5W package=THT]
  Q2 = Basic FET P-Channel [part_number=IRF9540N package="DPak [SMD]"]

nets:
  N1: Part1.A0, R3.wiper
  N2: Part1.D9_PWM, R2.Pin_0
  GND: Part1.GND, R3.leg1, Q1.E, 9V.GND, D1.anode, C1.-, Rload.Pin_1
  Vcc: Part1.5V, R3.leg2
  CH1: Q1.B, R2.Pin_1
  N3: Q1.C, R1.Pin_1, Q2.Gate
  Vhi: R1.Pin_0, 9V.VCC, Q2.source
  CH2: L1.pin_0, D1.cathode, Q2.drain
  CH3: L1.pin_1, C1.+, Rload.Pin_0
