# Fritzing sketch BasicInvertingBuckBoostAvrControl (saved by Fritzing 0.9.2b)
breadboards: 1

parts:
  U3 = attiny85 [package=dip]
  U4 = LM 358 Dual Op-Amp [part_number=LMC6482AIN package="DIP8 [THT]"]
  U5 = Voltage Regulator - 5V [part_number=L7805 package="TO220 [THT]"]
  12V = Power plug
  C1 = Ceramic Capacitor [capacitance=100nF package="100 mil [THT, multilayer]"]
  C2 = Ceramic Capacitor [capacitance=100nF package="100 mil [THT, multilayer]"]
  C3 = Electrolytic Capacitor [capacitance=100µF package="100 mil [THT, electrolytic]"]
  L1 = Inductor [inductance=33µH package="400 mil [THT]"]
  D1 = Schottky Diode [part_number=1N5819 package="300 mil [THT]"]
  C4 = Electrolytic Capacitor [capacitance=220µF package="100 mil [THT, electrolytic]"]
  Q1 = Basic FET N-Channel [part_number=IRF3205 package="TO220 [THT]"]
  R1 = Resistor [tolerance=±5% resistance=10 package=THT]
  R2 = Resistor [tolerance=±5% resistance=10k package=THT]
  R3 = Resistor [tolerance=±5% resistance=100k package=THT]
  R4 = Resistor [tolerance=±5% resistance=100k package=THT]
  R6 = Resistor [tolerance=±5% resistance=22k package=THT]
  R7 = Resistor [tolerance=±5% resistance=22k package=THT]
  R8 = Resistor [tolerance=±5% resistance=10k package=THT]
  R9 = Trimmer Potentiometer [maximum_resistance=100kΩ package=THT]
  C5 = Electrolytic Capacitor [capacitance=470µF package="100 mil [THT, electrolytic]"]

nets:
  N1: U3.Pin_1, R8.Pin_1
  FB: U3.Pin_2, U4.connector0, R7.Pin_1
  GND: U3.Pin_4, U4.connector3, U5.GND, 12V.GND, C1.0, C2.0, C3.-, Q1.source, R2.Pin_1, R6.Pin_1, R9.leg2, C5.-
  PWM: U3.Pin_6, R1.Pin_0
  VSET: U3.Pin_7, R9.wiper
  VCC: U3.Pin_8, U4.connector7, U5.output_voltage, C2.1, C3.+, R8.Pin_0, R9.leg1, C5.+
  N2: U4.connector1, R3.Pin_1, R7.Pin_0
  N3: U4.connector2, R4.Pin_1, R6.Pin_0
  VIN: U5.input_voltage, 12V.VCC, C1.1, L1.pin_0, D1.cathode
  OUT+: L1.pin_1, C4.+, Q1.drain, R4.Pin_0
  OUT-: D1.anode, C4.-, R3.Pin_0
  N4: Q1.gate, R1.Pin_1, R2.Pin_0

notes:
  OUT+
  OUT-
