# Fritzing sketch SwitchNFET (saved by Fritzing 0.9.0b)
breadboards: 1

parts:
  Q1 = 2N7000 FET N-Channel [part_number=2N7000 package=TO92]
  VCC1 = Battery block 9V
  R1 = Resistor [tolerance=±5% resistance=220k package=THT]
  C1 = Electrolytic Capacitor [capacitance=10µF package="100 mil [THT, electrolytic]"]
  R2 = Resistor [tolerance=±5% resistance=1k package=THT]
  LED1 = LED - 3mm [color="Blue (430nm)" package="3 mm [THT]"]
  S1 = Pushbutton [package="[THT]"]

nets:
  N1: Q1.gate, R1.Pin_0, C1.+, S1.Pin_1, S1.Pin_2
  N2: Q1.drain, LED1.cathode
  N3: Q1.source, VCC1.-, R1.Pin_1, C1.-
  N4: VCC1.+, R2.Pin_0, S1.Pin_3, S1.Pin_4
  N5: R2.Pin_1, LED1.anode

custom parts:
  2N7000 FET N-Channel: A 2N7000 MOSFET N-Channel Transistor
