# Fritzing sketch SwitchNJFET (saved by Fritzing 0.9.2b)
breadboards: 1

parts:
  Q1 = 2N7000 FET N-Channel [part_number=J201 package=TO92]
  VCC1 = Battery block 9V
  Rd = Resistor [tolerance=±5% resistance=1k package=THT]
  LED1 = LED - 3mm [color="Blue (430nm)" package="3 mm [THT]"]
  Part1 = Arduino Uno (Rev3)
  Rg = Resistor [tolerance=±5% resistance=1M package=THT]

nets:
  N1: Q1.gate, Part1.GND
  N2: Q1.drain, LED1.cathode
  N3: Q1.source, VCC1.-, Rg.Pin_1
  N4: VCC1.+, Rd.Pin_0
  N5: Rd.Pin_1, LED1.anode
  N6: Part1.D6_PWM, Rg.Pin_0

custom parts:
  2N7000 FET N-Channel: A 2N7000 MOSFET N-Channel Transistor
