# Fritzing sketch SwitchNPN (saved by Fritzing 0.9.2b)
breadboards: 1

parts:
  Part1 = Arduino Uno (Rev3)
  Q1 = NPN-Transistor [part_number=BC547 package="TO92 [THT]"]
  DL = LED - 5mm [color="Red (633nm)" package="5 mm [THT]"]
  RL = Resistor [tolerance=±5% resistance=1k package=THT]
  Rb = Resistor [tolerance=±5% resistance=330k package=THT]
  C1 = Ceramic Capacitor [capacitance=10nF package="100 mil [THT, multilayer]"]

nets:
  PROBEA: Part1.A0, Q1.C, DL.cathode, C1.1
  GND: Part1.GND, Q1.E, C1.0
  N1: Part1.D7, Rb.Pin_0
  VCC: Part1.5V, RL.Pin_0
  N2: Q1.B, Rb.Pin_1
  N3: DL.anode, RL.Pin_1
