# Fritzing sketch SwitchPFET (saved by Fritzing 0.9.2b)
breadboards: 1

parts:
  VCC1 = Battery block 9V
  R1 = Resistor [tolerance=±5% resistance=220k package=THT]
  C1 = Electrolytic Capacitor [capacitance=10µF package="100 mil [THT, electrolytic]"]
  R2 = Resistor [tolerance=±5% resistance=1k package=THT]
  LED1 = LED - 3mm [color="Red (633nm)" package="3 mm [THT]"]
  S1 = Pushbutton [package="[THT]"]
  Q1 = Basic FET P-Channel [part_number=BS250 package="D2Pak [SMD]"]

nets:
  N1: VCC1.-, R1.Pin_1, C1.-, LED1.cathode
  N2: VCC1.+, S1.Pin_3, S1.Pin_4, Q1.source
  N3: R1.Pin_0, C1.+, S1.Pin_1, S1.Pin_2, Q1.Gate
  N4: R2.Pin_0, Q1.drain
  N5: R2.Pin_1, LED1.anode
