# Fritzing sketch SwitchPJFET (saved by Fritzing 0.9.2b)
breadboards: 1

parts:
  Part1 = Arduino Uno (Rev3)
  Rd = Resistor [tolerance=±5% resistance=1k package=THT]
  LED1 = LED - 5mm [color="Green (555nm)" package="5 mm [THT]"]
  Rs = Resistor [tolerance=±5% resistance=0 package=THT]
  Rg = Resistor [tolerance=±5% resistance=1M package=THT]
  VDD = Battery block 9V
  Q1 = Basic FET P-Channel [part_number="J175 p-JFET" package="TO220 [THT]"]

nets:
  N1: Part1.GND, Rs.Pin_1, VDD.+
  N2: Part1.D6_PWM, Rg.Pin_1
  N3: Rd.Pin_0, LED1.anode
  N4: Rd.Pin_1, Q1.drain
  N5: LED1.cathode, VDD.-
  N6: Rs.Pin_0, Q1.source
  N7: Rg.Pin_0, Q1.gate
