# Fritzing sketch SwitchPNP (saved by Fritzing 0.9.0b)
breadboards: 1

parts:
  Part1 = Arduino Uno (Rev3)
  DL = LED - 5mm [color="Red (633nm)" package="5 mm [THT]"]
  RL = Resistor [tolerance=±5% resistance=1k package=THT]
  Rb = Resistor [tolerance=±5% resistance=330k package=THT]
  C1 = Ceramic Capacitor [capacitance=10nF package="100 mil [THT, multilayer]"]
  Q1 = PNP-Transistor [part_number=BC557 package="TO92 [THT]"]

nets:
  N1: Part1.A0, RL.Pin_0, C1.0, Q1.C
  N2: Part1.D7, Rb.Pin_0
  N3: Part1.5V, C1.1, Q1.E
  N4: Part1.GND, DL.cathode
  N5: DL.anode, RL.Pin_1
  N6: Rb.Pin_1, Q1.B
