# Fritzing sketch SwitchPowerNFET (saved by Fritzing 0.9.2b)
breadboards: 1

parts:
  Q1 = Basic FET N-Channel [part_number=IRF3205 package="TO220 [THT]"]
  12V = Power plug
  Part1 = Arduino Uno (Rev3)
  LED4 = LED - 5mm [color="Blue (430nm)" part_number=Vf~3V package="5 mm [THT]"]
  LED5 = LED - 5mm [color="Blue (430nm)" part_number=Vf~3V package="5 mm [THT]"]
  LED6 = LED - 5mm [color="Blue (430nm)" part_number=Vf~3V package="5 mm [THT]"]
  LED7 = LED - 5mm [color="Blue (430nm)" part_number=Vf~3V package="5 mm [THT]"]
  R1 = Resistor [tolerance=±5% resistance=1k package=THT]

nets:
  N1: Q1.gate, Part1.D7
  N2: Q1.drain, LED7.cathode
  GND: Q1.source, 12V.GND, Part1.GND
  N3: 12V.VCC, R1.Pin_0
  N4: LED4.cathode, LED5.anode
  N5: LED4.anode, R1.Pin_1
  N6: LED5.cathode, LED6.anode
  N7: LED6.cathode, LED7.anode
