# Fritzing sketch SwitchSoftLatch (saved by Fritzing 0.9.2b)
breadboards: 1

parts:
  R1 = Resistor [tolerance=±5% resistance=100k package=THT]
  C1 = Electrolytic Capacitor [capacitance=22µF package="100 mil [THT, electrolytic]"]
  RL = Resistor [tolerance=±5% resistance=1k package=THT]
  LED1 = LED - 3mm [color="Red (633nm)" package="3 mm [THT]"]
  Q1 = Basic FET P-Channel [part_number=BS250 package="D2Pak [SMD]"]
  Q2 = NPN-Transistor [part_number=2N3904 package="TO92 [THT]"]
  5V = Power plug
  R2 = Resistor [tolerance=±5% resistance=100k package=THT]
  Q3 = NPN-Transistor [part_number=2N3904 package="TO92 [THT]"]
  R4 = Resistor [tolerance=±5% resistance=1M package=THT]
  R3 = Resistor [tolerance=±5% resistance=100k package=THT]
  S1 = Pushbutton [package="[THT]"]

nets:
  N1: R1.Pin_0, Q1.source, 5V.VCC, R3.Pin_0
  N2: R1.Pin_1, Q1.Gate, Q2.C
  GND: C1.-, RL.Pin_1, Q2.E, 5V.GND, Q3.E
  N3: C1.+, Q3.B, R4.Pin_1
  N4: RL.Pin_0, LED1.cathode
  N5: LED1.anode, Q1.drain, R2.Pin_0, R4.Pin_0
  N6: Q2.B, R2.Pin_1, S1.Pin_3, S1.Pin_4
  N7: Q3.C, R3.Pin_1, S1.Pin_1, S1.Pin_2
