# Fritzing sketch DPDT (saved by Fritzing 0.9.2b)
breadboards: 1

parts:
  5-9V = Power plug
  S1 = SWITCH-DPDT [package=os]
  LED1 = LED - 3mm [color="Red (633nm)" package="3 mm [THT]"]
  LED2 = LED - 3mm [color="Red (633nm)" package="3 mm [THT]"]
  LED3 = LED - 3mm [color="Yellow (595nm)" package="3 mm [THT]"]
  LED4 = LED - 3mm [color="Yellow (595nm)" package="3 mm [THT]"]
  R1 = Resistor [tolerance=±5% resistance=1k package=THT]
  R2 = Resistor [tolerance=±5% resistance=1k package=THT]

nets:
  GND: 5-9V.GND, LED1.cathode, LED3.cathode, R2.Pin_1
  VCC: 5-9V.VCC, LED2.anode, LED4.anode, R1.Pin_0
  N1: S1.1, LED1.anode
  N2: S1.2, R1.Pin_1
  N3: S1.3, LED3.anode
  N4: S1.4, LED2.cathode
  N5: S1.5, R2.Pin_0
  N6: S1.6, LED4.cathode
