# Fritzing sketch MomentaryDPDT (saved by Fritzing 1.0.7)
breadboards: 1

parts:
  S1 = SWITCH-DPDT [package=os]
  Power = Power plug
  R1 = Resistor [tolerance=±5% power=0.25W resistance=1k package=THT]
  LED1 = LED - 3mm [color="Yellow (595nm)" current=0.030A package="3 mm [THT]"]
  R2 = Resistor [tolerance=±5% power=0.25W resistance=1k package=THT]
  LED2 = LED - 3mm [color="Red (660nm)" current=30mA package="3 mm [THT]"]

nets:
  5V: S1.1, S1.6, Power.VCC
  N1: S1.2, R1.Pin_0, LED2.cathode
  GND: S1.3, S1.4, Power.GND
  N2: S1.5, LED1.cathode, R2.Pin_1
  N3: R1.Pin_1, LED1.anode
  N4: R2.Pin_0, LED2.anode
