# Fritzing sketch SingleStageDelay (saved by Fritzing 0.9.2b)
breadboards: 1

parts:
  S1 = SWITCH-DPDT [package=mss22]
  Q1 = NPN-Transistor [part_number=2N3904 package="TO92 [THT]"]
  5V = Power plug
  C1 = Electrolytic Capacitor [capacitance=1µF package="100 mil [THT, electrolytic]"]
  R1 = Resistor [tolerance=±5% resistance=1M package=THT]
  R2 = Resistor [tolerance=±5% resistance=2.2 package=THT]
  LED1 = LED - 3mm [color="Red (633nm)" package="3 mm [THT]"]
  R3 = Resistor [tolerance=±5% resistance=1M package=THT]
  R4 = Resistor [tolerance=±5% resistance=2.2 package=THT]
  LED2 = LED - 3mm [color="Red (633nm)" package="3 mm [THT]"]
  C2 = Electrolytic Capacitor [capacitance=1µF package="100 mil [THT, electrolytic]"]
  Q2 = Basic FET N-Channel [part_number=2N7000 package="TO220 [THT]"]

nets:
  5V: S1.2, S1.5, 5V.VCC, R2.Pin_0, R4.Pin_0
  CH4: S1.3, C1.+, R1.Pin_0
  CH2: S1.6, R3.Pin_1, C2.+, Q2.gate
  GND: Q1.E, 5V.GND, C1.-, R3.Pin_0, C2.-, Q2.source
  N1: Q1.B, R1.Pin_1
  CH3: Q1.C, LED1.cathode
  N2: R2.Pin_1, LED1.anode
  N3: R4.Pin_1, LED2.anode
  CH1: LED2.cathode, Q2.drain
