# Fritzing sketch TTLBufferDriver (saved by Fritzing 0.9.2b)
breadboards: 1

parts:
  Part1 = Arduino Uno (Rev3)
  QB = NPN-Transistor [part_number=2N3904 package="TO92 [THT]"]
  RbB = Resistor [tolerance=±5% resistance=10k package=THT]
  LED1 = LED - 3mm [color="Green (555nm)" package="3 mm [THT]"]
  RL = Resistor [tolerance=±5% resistance=1k package=THT]
  QA = NPN-Transistor [part_number=2N3904 package="TO92 [THT]"]
  RbA = Resistor [tolerance=±5% resistance=10k package=THT]
  Rp = Resistor [tolerance=±5% resistance=10k package=THT]
  IC1 = LM324 [package=dil16]
  Rd1 = Resistor [tolerance=±5% resistance=100k package=THT]
  Rd2 = Resistor [tolerance=±5% resistance=100k package=THT]

nets:
  A: Part1.A0, Part1.D7, RbA.Pin_0
  B: Part1.A1, Part1.D6_PWM, RbB.Pin_0
  TTL_OUT: Part1.A2, QA.E, Rp.Pin_1, IC1.IN1+
  BUFF_OUT: Part1.A3, RL.Pin_0, IC1.OUT1
  VCC: Part1.5V, QB.C, IC1.V+, Rd1.Pin_0
  GND: Part1.GND, LED1.cathode, Rp.Pin_0, IC1.GND, Rd2.Pin_0
  N1: QB.E, QA.C
  N2: QB.B, RbB.Pin_1
  N3: LED1.anode, RL.Pin_1
  N4: QA.B, RbA.Pin_1
  N5: IC1.IN1-, Rd1.Pin_1, Rd2.Pin_1

custom parts:
  LM324: LM324 Quad OpAmp
