# Fritzing sketch LM35 (saved by Fritzing 0.9.2b)
breadboards: 1

parts:
  Nokia_5110_LCD_Module2 = Nokia5110LCDModule
  Part2 = Arduino Prototyping Shield
  T1 = LM35 Temperature Sensor [package="TO92 [THT]"]

nets:
  Vcc: Nokia_5110_LCD_Module2.Vcc, Part2.+5V, Part2.N$167, Part2.N$168, T1.+Vs
  GND: Nokia_5110_LCD_Module2.Grnd, Part2.GND, Part2.N$155, Part2.N$156, T1.GND
  SCE: Nokia_5110_LCD_Module2.SCE, Part2.D9, Part2.N$135, Part2.N$143
  RST: Nokia_5110_LCD_Module2.RST, Part2.D10, Part2.N$131, Part2.N$132
  DC: Nokia_5110_LCD_Module2.D/C, Part2.D8, Part2.N$119, Part2.N$120
  DN: Nokia_5110_LCD_Module2.6_DN_(MOSI), Part2.D11, Part2.N$106, Part2.N$107
  SCLK: Nokia_5110_LCD_Module2.SCLK, Part2.D13, Part2.N$94, Part2.N$95
  N1: Nokia_5110_LCD_Module2.LED, Part2.N$82, Part2.N$83
  N2: Part2.A0, T1.Vout

custom parts:
  : Nokia 5110 LCD with 8 pin. It's a 45mm*45mm module part. Description: The Nokia 5110 is a basic graphic LCD screen for lots of applications. It was originally intended for as a cell phone screen. This one is mounted on an easy to solder PCB. It uses the PCD8544 controller. The PCD8544 is a low power CMOS LCD controller/driver, designed to drive a graphic display of 48 rows and 84 columns. All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
