# Fritzing sketch MusicalKit (saved by Fritzing 0.9.2b)
breadboards: 1

parts:
  14V-24V = Power plug
  Q2 = Basic FET N-Channel [part_number=80NF70 package="DPak [SMD]"]
  Q1 = npn-Powertransistor [part_number=BD243C package="TO220 [THT]"]
  R1 = Resistor [tolerance=±5% resistance=10k package=THT]
  R4 = Resistor [tolerance=±5% resistance=10k package=THT]
  R3 = Resistor [tolerance=±5% resistance=2k package=THT]
  R5 = Resistor [tolerance=±5% resistance=2k package=THT]
  D1 = LED - 3mm [color="Red (633nm)" package="3 mm [THT]"]
  D2 = LED - 3mm [color="Blue (430nm)" package="3 mm [THT]"]
  C2 = Ceramic Capacitor [capacitance=1µF package="100 mil [THT, multilayer]"]
  C1 = Electrolytic Capacitor [capacitance=10µF package="100 mil [THT, electrolytic]"]
  L1 = Inductor [package="400 mil [THT]"]
  L2 = Inductor [package="400 mil [THT]"]
  U1 = AUDIO-JACK2 [package=audio-jack-3.5mm-smd]

nets:
  GND: 14V-24V.GND, Q1.emitter, D1.cathode, D2.cathode, C2.0
  VCC: 14V-24V.VCC, Q2.drain, R3.Pin_0
  N1: Q2.Gate, R1.Pin_0, R3.Pin_1, C1.-
  J1: Q2.source, R1.Pin_1, R4.Pin_0, R5.Pin_0, C2.1, L1.pin_0, U1.RING, U1.TIP
  J3: Q1.base, R4.Pin_1, D1.anode, L2.pin_1
  J2: Q1.collector, L1.pin_1
  N2: R5.Pin_1, D2.anode
  N3: C1.+, U1.SLEEVE
  arc: L2.pin_0
