# Fritzing sketch RgbNightLight (saved by Fritzing 0.9.2b)
breadboards: 1

parts:
  L1 = Inductor [part_number="10 turns (left)" package="400 mil [THT]"]
  Q1 = NPN-Transistor [part_number=2N3904 package="TO92 [THT]"]
  LED1 = LED - 5mm [color="White (8000K)" part_number="RGB Slow Flash" package="5 mm [THT]"]
  R1 = Resistor [tolerance=±5% resistance=1k package=THT]
  L2 = Inductor [part_number="10 turns (right)" package="400 mil [THT]"]
  D1 = Rectifier Diode [part_number=1N5819 package="300 mil [THT]"]
  C1 = Ceramic Capacitor [capacitance=1µF package="100 mil [THT, multilayer]"]
  1_5V = Battery Holders [part_number=CR1216 package=battcon_12mm]

nets:
  N1: L1.pin_0, R1.Pin_1
  N2: L1.pin_1, Q1.B
  N3: Q1.E, LED1.cathode, C1.0, 1_5V.-
  N4: Q1.C, L2.pin_0, D1.anode
  N5: LED1.anode, D1.cathode, C1.1
  N6: R1.Pin_0, L2.pin_1, 1_5V.+
