# Fritzing sketch ToroidJouleThief (saved by Fritzing 0.9.2b)
breadboards: 1

parts:
  L1 = Inductor [part_number="10 turns (left)" package="400 mil [THT]"]
  Q1 = NPN-Transistor [part_number=2N5551 package="TO92 [THT]"]
  LED1 = LED - 5mm [color="White (8000K)" package="5 mm [THT]"]
  0_3-1_5V = Battery Holders [package=battery-aaa]
  R1 = Resistor [tolerance=±5% resistance=1k package=THT]
  L2 = Inductor [part_number="10 turns (right)" package="400 mil [THT]"]

nets:
  N1: L1.pin_0, R1.Pin_1
  N2: L1.pin_1, Q1.B
  N3: Q1.E, LED1.cathode, 0_3-1_5V.-
  N4: Q1.C, LED1.anode, L2.pin_0
  N5: 0_3-1_5V.+, R1.Pin_0, L2.pin_1
