# Fritzing sketch TransistorCurveTracer (saved by Fritzing 0.9.2b)
breadboards: 1

parts:
  Q1 = NPN-Transistor [part_number=2N3904 package="TO92 [THT]"]
  Q2 = NPN-Transistor [part_number=2N3904 package="TO92 [THT]"]
  D1 = Rectifier Diode [part_number=1N4148 package="300 mil [THT]"]
  D2 = Rectifier Diode [part_number=1N4148 package="300 mil [THT]"]
  R2 = Resistor [tolerance=±5% resistance=4.7k package=THT]
  C1 = Ceramic Capacitor [capacitance=10nF package="100 mil [THT, multilayer]"]
  5V = Power plug
  R3 = Resistor [tolerance=±5% resistance=10k package=THT]
  C2 = Ceramic Capacitor [capacitance=10nF package="100 mil [THT, multilayer]"]
  D3 = Rectifier Diode [part_number=1N4148 package="300 mil [THT]"]
  D4 = Rectifier Diode [part_number=1N4148 package="300 mil [THT]"]
  R5 = Resistor [tolerance=±5% resistance=2.2k package=THT]
  R6 = Resistor [tolerance=±5% resistance=33k package=THT]
  R7 = Resistor [tolerance=±5% resistance=33k package=THT]
  R8 = Resistor [tolerance=±5% resistance=22k package=THT]
  R9 = Resistor [tolerance=±5% resistance=6.8k package=THT]
  R10 = Resistor [tolerance=±5% resistance=6.8k package=THT]
  R11 = Resistor [tolerance=±5% resistance=10k package=THT]
  R12 = Resistor [tolerance=±5% resistance=10k package=THT]
  R13 = Resistor [tolerance=±5% resistance=10k package=THT]
  R14 = Resistor [tolerance=±5% resistance=10k package=THT]
  C3 = Ceramic Capacitor [capacitance=100nF package="100 mil [THT, multilayer]"]
  U1 = 555 Timer [package="SO8 [SMD]"]
  C4 = Ceramic Capacitor [capacitance=100nF package="100 mil [THT, multilayer]"]
  U2 = LMV324 [part_number=TL074 package=so014]
  Q3 = NPN-Transistor [part_number=2N3904 package="TO92 [THT]"]
  R15 = Resistor [tolerance=±5% resistance=3.3k package=THT]
  C5 = Ceramic Capacitor [capacitance=10nF package="100 mil [THT, multilayer]"]
  R16 = Resistor [tolerance=±5% resistance=100k package=THT]
  R17 = Resistor [tolerance=±5% resistance=4.7k package=THT]
  R18 = Resistor [tolerance=±5% resistance=10k package=THT]
  Q4 = PNP-Transistor [part_number=2N3906 package="TO92 [THT]"]
  Q5 = PNP-Transistor [part_number=2N3906 package="TO92 [THT]"]
  Q6 = NPN-Transistor [part_number=DUT package="TO92 [THT]"]
  R19 = Resistor [tolerance=±5% resistance=220 package=THT]
  R20 = Resistor [tolerance=±5% resistance=470 package=THT]
  R1 = Trimmer Potentiometer [maximum_resistance=50kΩ package=THT]
  R4 = Trimmer Potentiometer [maximum_resistance=50kΩ package=THT]
  R21 = Trimmer Potentiometer [maximum_resistance=50kΩ package=THT]

nets:
  GND: Q1.E, Q2.E, C1.0, 5V.GND, C2.0, R7.Pin_1, R9.Pin_1, R12.Pin_1, C3.1, U1.Pin_1, C4.1, U2.G$1_-V, Q3.E, C5.0, R17.Pin_0, Q6.E, R19.Pin_1
  N1: Q1.B, Q2.B, R10.Pin_1
  N2: Q1.C, R3.Pin_1, U1.Pin_4
  PULSE: Q2.C, R13.Pin_1, R14.Pin_1, C3.0, U2.G$4_+IN
  N3: D1.cathode, D2.anode, C1.1, U1.Pin_2, U1.Pin_6
  N4: D1.anode, R2.Pin_1, U1.Pin_7, R1.leg1
  N5: D2.cathode, R1.wiper
  VCC: R2.Pin_0, 5V.VCC, R3.Pin_0, R6.Pin_0, U1.Pin_8, U2.G$1_+V, R16.Pin_1
  N6: C2.1, U1.Pin_5
  N7: D3.cathode, R4.leg2
  N8: D3.anode, D4.cathode, C4.0, U2.G$1_-IN
  N9: D4.anode, R5.Pin_1
  RESET: R5.Pin_0, R8.Pin_0, R9.Pin_0, R10.Pin_0, U2.G$1_OUT, R4.wiper
  N10: R6.Pin_1, R7.Pin_0, R8.Pin_1, U2.G$1_+IN
  STEP: R11.Pin_0, R13.Pin_0, U2.G$4_OUT, R21.leg2
  N11: R11.Pin_1, R12.Pin_0, U2.G$4_-IN
  N12: R14.Pin_0, U1.Pin_3, R15.Pin_0
  N13: U2.G$3_OUT, R18.Pin_1, Q4.E, Q5.E
  N14: U2.G$3_-IN, R17.Pin_1, R18.Pin_0
  SIGNAL: U2.G$3_+IN, Q3.C, C5.1, R16.Pin_0
  N15: Q3.B, R15.Pin_1
  X-CH1: Q4.B, Q4.C, Q5.B, Q6.C
  Y-CH2: Q5.C, R19.Pin_0
  N16: Q6.B, R20.Pin_1
  N17: R20.Pin_0, R21.wiper
