# Fritzing sketch TransistorTester (saved by Fritzing 0.9.0b)
breadboards: 1

parts:
  LCD1 = LCD screen
  Part1 = Arduino Uno (Rev3)
  R1 = Resistor [tolerance=±5% resistance=220 package=THT]
  VR1 = Rotary Potentiometer (Small) [maximum_resistance=50kΩ package=THT]
  QTEST = NPN-Transistor [package="TO92 [THT]"]
  R2 = Resistor [tolerance=±5% resistance=1k package=THT]
  R3 = Resistor [tolerance=±5% resistance=1k package=THT]
  R4 = Resistor [tolerance=±5% resistance=1k package=THT]

nets:
  VSS: LCD1.VSS, LCD1.R/W, LCD1.LED-, Part1.GND, VR1.leg1
  VDD: LCD1.VDD, Part1.5V, R1.Pin_0, VR1.leg2
  N1: LCD1.V0, VR1.wiper
  N2: LCD1.RS, Part1.D6_PWM
  N3: LCD1.E, Part1.D7
  N4: LCD1.DB4, Part1.D9_PWM
  N5: LCD1.DB5, Part1.D10_PWM/SS
  N6: LCD1.DB6, Part1.D11_PWM/MOSI
  N7: LCD1.DB7, Part1.D12/MISO
  N8: LCD1.LED+, R1.Pin_1
  TestC: Part1.A0, QTEST.C, R4.Pin_0
  TestB: Part1.A1, QTEST.B, R3.Pin_0
  TestE: Part1.A2, QTEST.E, R2.Pin_0
  N9: Part1.D3_PWM, R4.Pin_1
  N10: Part1.D4, R3.Pin_1
  N11: Part1.D5_PWM, R2.Pin_1
