# Fritzing sketch TriacDimmer (saved by Fritzing 0.9.2b)
breadboards: 1

parts:
  T1 = TRIAC [part_number=BTA12-600 package=to-92]
  12V_AC_50Hz = Power plug
  R1 = Resistor [tolerance=±5% resistance=220 package=THT]
  R2 = Rotary Potentiometer (Small) [maximum_resistance=10kΩ package=THT]
  C1 = Ceramic Capacitor [capacitance=1nF part_number=mylar package="100 mil [THT, multilayer]"]
  D1 = Rectifier Diode [part_number=1N4007 package="300 mil [THT]"]
  D2 = Rectifier Diode [part_number=1N4007 package="300 mil [THT]"]
  12V_AC_LAMP_Socket = 2.1mm Barrel Jack with Terminal Block

nets:
  N1: T1.M1, 12V_AC_LAMP_Socket.POS
  N2: T1.G, D1.cathode, D2.anode
  N3: T1.M2, 12V_AC_50Hz.VCC, R1.Pin_1
  N4: 12V_AC_50Hz.GND, C1.0, 12V_AC_LAMP_Socket.NEG
  N5: R1.Pin_0, R2.leg1, R2.wiper
  N6: R2.leg2, C1.1, D1.anode, D2.cathode
