# Fritzing sketch PiezoPolarityTester (saved by Fritzing 1.0.7)
breadboards: 1

parts:
  LED1 = LED - 3mm [color="Red (633nm)" current=0.030A package="3 mm [THT]"]
  LED2 = LED - 3mm [color="Red (633nm)" current=0.030A package="3 mm [THT]"]
  R1 = Resistor [tolerance=±5% power=0.25W resistance=1k package=THT]
  R2 = Resistor [tolerance=±5% power=0.25W resistance=1k package=THT]
  TestPads = female pin header, 2 pins [form="♀ (female)"]
  Part2 = Arduino Nano (Rev3.0) (ICSP)

nets:
  N1: LED1.cathode, R1.Pin_0
  N2: LED1.anode, Part2.D2
  N3: LED2.cathode, R2.Pin_0
  N4: LED2.anode, Part2.D3
  GND: R1.Pin_1, R2.Pin_1, TestPads.pin1, Part2.GND
  N5: TestPads.pin2, Part2.A0
