# Fritzing sketch UltrasonicAlarm (saved by Fritzing 0.9.2b)
breadboards: 1

parts:
  IC1 = Hex Inverter Schmitt Trigger SN74HC14 [part_number=74LS14 package="DIP (Dual Inline)"]
  Part3 = SRF05 Ultrasonic Rangefinder
  IC2 = 555 Timer [package="DIP8 [THT]"]
  5V = Power plug
  R1 = Resistor [tolerance=±5% resistance=1.2k package=THT]
  D1 = Rectifier Diode [part_number=1N5819 package="300 mil [THT]"]
  R2 = Resistor [tolerance=±5% resistance=220 package=THT]
  C2 = Ceramic Capacitor [capacitance=1nF package="100 mil [THT, multilayer]"]
  D2 = Rectifier Diode [part_number=1N4148 package="300 mil [THT]"]
  R3 = Resistor [tolerance=±5% resistance=100k package=THT]
  R4 = Resistor [tolerance=±5% resistance=10k package=THT]
  R5 = Trimmer Potentiometer [maximum_resistance=100kΩ package=THT]
  IC3 = IC, DIP package, 14 pins [chip_label=CD4070]
  Q1 = Basic FET N-Channel [part_number=2N7000 package="TO220 [THT]"]
  R8 = Resistor [tolerance=±5% resistance=100 package=THT]
  R7 = Resistor [tolerance=±5% resistance=1k package=THT]
  C4 = Ceramic Capacitor [capacitance=100nF package="100 mil [THT, multilayer]"]
  LED1 = LED - 5mm [color="Red (633nm)" package="5 mm [THT]"]
  J1 = Piezo Speaker
  R9 = Resistor [tolerance=±5% resistance=470 package=THT]
  C3 = Ceramic Capacitor [capacitance=100nF package="100 mil [THT, multilayer]"]
  C1 = Electrolytic Capacitor [capacitance=10µF package="100 mil [THT, electrolytic]"]

nets:
  N1: IC1.1A, R1.Pin_0, R2.Pin_1, C1.+
  TRIG: IC1.1Y, Part3.Trig, R1.Pin_1, D1.anode
  GND: IC1.GND, Part3.GND, IC2.Ground, 5V.GND, IC3.pin7, Q1.source, C4.1, C3.0, C1.-
  N2: IC1.4Y, C2.0
  ECHO: IC1.4A, Part3.Echo, IC3.pin1
  VCC: IC1.VCC, Part3.VCC, IC2.Reset, IC2.Vcc_Supply_Voltage, 5V.VCC, D2.cathode, R3.Pin_1, R5.leg1, R5.wiper, IC3.pin14, J1.pin2, R9.Pin_1
  N3: IC2.Trigger, C2.1, D2.anode, R3.Pin_0
  N4: IC2.Output, IC3.pin2
  N5: IC2.Threshold, IC2.Discharge, R4.Pin_0, C3.1
  N6: D1.cathode, R2.Pin_0
  N7: R4.Pin_1, R5.leg2
  N8: IC3.pin3, R7.Pin_0
  N9: Q1.gate, R8.Pin_0
  N10: Q1.drain, LED1.cathode, J1.pin1
  N11: R8.Pin_1, R7.Pin_1, C4.0
  N12: LED1.anode, R9.Pin_0
