# Fritzing sketch VariableSawtoothGenerator (saved by Fritzing 0.9.2b)
breadboards: 1

parts:
  D1 = Rectifier Diode [part_number=1N4148 package="300 mil [THT]"]
  D2 = Rectifier Diode [part_number=1N4148 package="300 mil [THT]"]
  Q1 = PNP-Transistor [part_number=2N3906 package="TO92 [THT]"]
  R1 = Resistor [tolerance=±5% resistance=1k package=THT]
  D3 = Rectifier Diode [part_number=1N4148 package="300 mil [THT]"]
  D4 = Rectifier Diode [part_number=1N4148 package="300 mil [THT]"]
  Q2 = NPN-Transistor [part_number=2N3904 package="TO92 [THT]"]
  R2 = Resistor [tolerance=±5% resistance=220 package=THT]
  R3 = Resistor [tolerance=±5% resistance=220 package=THT]
  R4 = Trimmer Potentiometer [maximum_resistance=1kΩ package=THT]
  R5 = Trimmer Potentiometer [maximum_resistance=1kΩ package=THT]
  D5 = Rectifier Diode [part_number=1N4148 package="300 mil [THT]"]
  D6 = Rectifier Diode [part_number=1N4148 package="300 mil [THT]"]
  D7 = Rectifier Diode [part_number=1N4148 package="300 mil [THT]"]
  D8 = Rectifier Diode [part_number=1N4148 package="300 mil [THT]"]
  IC1 = LM324 [package=dil16]
  C1 = Ceramic Capacitor [capacitance=100nF package="100 mil [THT, multilayer]"]
  5-15V = Power plug
  R6 = Resistor [tolerance=±5% resistance=4.7k package=THT]
  R7 = Resistor [tolerance=±5% resistance=4.7k package=THT]
  R8 = Resistor [tolerance=±5% resistance=4.7k package=THT]

nets:
  N1: D1.cathode, D2.anode
  VCC: D1.anode, R4.leg1, R4.wiper, IC1.V+, 5-15V.VCC, R7.Pin_1
  N2: D2.cathode, Q1.B, R1.Pin_1
  N3: Q1.E, R2.Pin_0
  P3: Q1.C, D5.anode, D6.anode
  N4: R1.Pin_0, D3.anode, Q2.B
  N5: D3.cathode, D4.anode
  GND: D4.cathode, R5.leg1, R5.wiper, IC1.GND, C1.0, 5-15V.GND, R6.Pin_1
  N6: Q2.E, R3.Pin_0
  N7: Q2.C, D7.cathode, D8.cathode
  N8: R2.Pin_1, R4.leg2
  N9: R3.Pin_1, R5.leg2
  SQUAREOUT: D5.cathode, D7.anode, IC1.OUT1, R8.Pin_1
  N10: D6.cathode, D8.anode, IC1.IN1-, IC1.IN2+, C1.1
  P4: IC1.IN1+, R6.Pin_0, R7.Pin_0, R8.Pin_0
  SAWOUT: IC1.IN2-, IC1.OUT2

custom parts:
  LM324: LM324 Quad OpAmp
