# Fritzing sketch VoltageControlledOscillator (saved by Fritzing 0.9.2b)
breadboards: 1

parts:
  C1 = Ceramic Capacitor [capacitance=10nF package="100 mil [THT, multilayer]"]
  R1 = Resistor [tolerance=±5% resistance=100k package=THT]
  D1 = Rectifier Diode [part_number=KV1471 package="300 mil [THT]"]
  D2 = Rectifier Diode [part_number=KV1471 package="300 mil [THT]"]
  R2 = Resistor [tolerance=±5% resistance=100k package=THT]
  C2 = Ceramic Capacitor [capacitance=33pF package="100 mil [THT, multilayer]"]
  C3 = Ceramic Capacitor [capacitance=33pF package="100 mil [THT, multilayer]"]
  L1 = Inductor [inductance=10µH package="400 mil [THT]"]
  C4 = Ceramic Capacitor [capacitance=100pF package="100 mil [THT, multilayer]"]
  R3 = Resistor [tolerance=±5% resistance=100k package=THT]
  C5 = Ceramic Capacitor [capacitance=220pF package="100 mil [THT, multilayer]"]
  C6 = Ceramic Capacitor [capacitance=220pF package="100 mil [THT, multilayer]"]
  R4 = Resistor [tolerance=±5% resistance=2.2k package=THT]
  Q1 = MOSFET-NCHANNEL [part_number=J310 package=to220v]
  5V = Power plug
  Q2 = MOSFET-NCHANNEL [part_number=J310 package=to220v]
  C7 = Ceramic Capacitor [capacitance=10pF package="100 mil [THT, multilayer]"]
  R5 = Resistor [tolerance=±5% resistance=100k package=THT]
  R6 = Resistor [tolerance=±5% resistance=1k package=THT]
  C8 = Ceramic Capacitor [capacitance=100nF package="100 mil [THT, multilayer]"]
  R7 = Resistor [tolerance=±5% resistance=22 package=THT]
  R8 = Resistor [tolerance=±5% resistance=22 package=THT]
  C9 = Ceramic Capacitor [capacitance=100nF package="100 mil [THT, multilayer]"]
  C10 = Ceramic Capacitor [capacitance=100nF package="100 mil [THT, multilayer]"]
  R9 = Trimmer Potentiometer [maximum_resistance=100kΩ package=THT]

nets:
  GND: C1.0, D1.anode, R2.Pin_1, C2.0, L1.pin_1, R3.Pin_1, C6.0, R4.Pin_1, 5V.GND, R5.Pin_1, R6.Pin_1, C9.0, C10.0, R9.leg2
  Vcontrol: C1.1, R1.Pin_0, R9.wiper
  N1: R1.Pin_1, D1.cathode, D2.cathode
  N2: D2.anode, R2.Pin_0, C3.1
  N3: C2.1, C3.0, L1.pin_0, C4.1
  N4: C4.0, R3.Pin_0, C5.1, Q1.G
  N5: C5.0, C6.1, R4.Pin_0, Q1.S, C7.1
  N6: Q1.D, R7.Pin_1, C9.1
  VDD: 5V.VCC, R7.Pin_0, R8.Pin_0, R9.leg1
  N7: Q2.G, C7.0, R5.Pin_0
  N8: Q2.D, R8.Pin_1, C10.1
  N9: Q2.S, R6.Pin_0, C8.1
  Vout: C8.0

notes:
  Vcontrol
  Vout
  R9 optional 0-5V control input - or replaced with a direct 0-12V variable power source
