# Fritzing sketch ADR4540 (saved by Fritzing 0.9.2b)
breadboards: 1

parts:
  Part1 = Arduino Uno (Rev3)
  IC1 = IC, DIP package, 8 pins [chip_label=4540 part_number=ADR4540]
  R4 = Trimmer Potentiometer [maximum_resistance=10kΩ package=THT]
  C2 = Ceramic Capacitor [capacitance=100nF package="100 mil [THT, multilayer]"]
  Nokia_5110_LCD_Module3 = Nokia5110LCDModule
  C3 = Electrolytic Capacitor [capacitance=1µF package="100 mil [THT, electrolytic]"]
  C4 = Ceramic Capacitor [capacitance=100nF package="100 mil [THT, multilayer]"]

nets:
  VTEST: Part1.A0, R4.wiper
  DC: Part1.D8, Nokia_5110_LCD_Module3.D/C
  SCE: Part1.D9_PWM, Nokia_5110_LCD_Module3.SCE
  RST: Part1.D10_PWM/SS, Nokia_5110_LCD_Module3.RST
  DN: Part1.D11_PWM/MOSI, Nokia_5110_LCD_Module3.6_DN_(MOSI)
  SCLK: Part1.D13/SCK, Nokia_5110_LCD_Module3.SCLK
  GND: Part1.GND, IC1.pin4, R4.leg2, C2.0, Nokia_5110_LCD_Module3.Grnd, C3.-, C4.0
  VREF: Part1.AREF, IC1.pin6, C4.1
  5V: Part1.5V, IC1.pin2, R4.leg1, C2.1, Nokia_5110_LCD_Module3.Vcc, C3.+

custom parts:
  : Nokia 5110 LCD with 8 pin. It's a 45mm*45mm module part. Description: The Nokia 5110 is a basic graphic LCD screen for lots of applications. It was originally intended for as a cell phone screen. This one is mounted on an easy to solder PCB. It uses the PCD8544 controller. The PCD8544 is a low power CMOS LCD controller/driver, designed to drive a graphic display of 48 rows and 84 columns. All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
