# Fritzing sketch WatsonLedRing (saved by Fritzing 0.9.2b)
breadboards: 1

parts:
  5V = Power plug
  LED1 = LED - 5mm [color="Blue (430nm)" package="5 mm [THT]"]
  LED2 = LED - 5mm [color="Blue (430nm)" package="5 mm [THT]"]
  LED3 = LED - 5mm [color="Blue (430nm)" package="5 mm [THT]"]
  Q1 = 2N7000 FET N-Channel [part_number=2N7000 package=TO92]
  R1 = Resistor [tolerance=±5% resistance=220 package=THT]
  R2 = Resistor [tolerance=±5% resistance=220 package=THT]
  R3 = Resistor [tolerance=±5% resistance=220 package=THT]
  Q2 = 2N7000 FET N-Channel [part_number=2N7000 package=TO92]
  Q3 = 2N7000 FET N-Channel [part_number=2N7000 package=TO92]
  R4 = Resistor [tolerance=±5% resistance=1M package=THT]
  R5 = Resistor [tolerance=±5% resistance=1M package=THT]
  R6 = Resistor [tolerance=±5% resistance=1M package=THT]
  C1 = Ceramic Capacitor [capacitance=100nF package="100 mil [THT, multilayer]"]
  C2 = Ceramic Capacitor [capacitance=100nF package="100 mil [THT, multilayer]"]
  C3 = Ceramic Capacitor [capacitance=100nF package="100 mil [THT, multilayer]"]

nets:
  GND: 5V.GND, Q1.source, Q2.source, Q3.source, C1.1, C2.1, C3.1
  N1: 5V.VCC, LED1.anode, LED2.anode, LED3.anode
  N2: LED1.cathode, R1.Pin_0
  N3: LED2.cathode, R2.Pin_0
  N4: LED3.cathode, R3.Pin_0
  N5: Q1.gate, R6.Pin_1, C1.0
  N6: Q1.drain, R1.Pin_1, R4.Pin_0
  N7: R2.Pin_1, Q2.drain, R5.Pin_0
  N8: R3.Pin_1, Q3.drain, R6.Pin_0
  N9: Q2.gate, R4.Pin_1, C2.0
  N10: Q3.gate, R5.Pin_1, C3.0

custom parts:
  2N7000 FET N-Channel: A 2N7000 MOSFET N-Channel Transistor
