# Fritzing sketch WeevilEyeKit (saved by Fritzing 0.9.2b)
breadboards: 1

parts:
  Part2 = LilyPad Coin Cell Battery Holder
  Q1 = NPN-Transistor [part_number=2N3904 package="TO92 [THT]"]
  R4 = Photocell (LDR) [package=THT]
  LED1 = LED - 5mm [color="Red (633nm)" package="5 mm [THT]"]
  LED2 = LED - 5mm [color="Red (633nm)" package="5 mm [THT]"]
  R3 = Resistor [tolerance=±5% resistance=47k package=THT]
  R1 = Resistor [tolerance=±5% resistance=220 package=THT]
  R2 = Resistor [tolerance=±5% resistance=220 package=THT]

nets:
  GND: Part2.-, Q1.E, R4.pin_1
  3V: Part2.+, LED1.anode, LED2.anode, R3.Pin_0
  N1: Q1.B, R4.pin_0, R3.Pin_1
  N2: Q1.C, R1.Pin_1, R2.Pin_1
  N3: LED1.cathode, R1.Pin_0
  N4: LED2.cathode, R2.Pin_0
