# Fritzing sketch WienBridgeAudioToneGenerator (saved by Fritzing 0.9.2b)
breadboards: 1

parts:
  IC1 = LM324 [package=dil16]
  R1 = Resistor [tolerance=±5% resistance=10k package=THT]
  R2 = Resistor [tolerance=±5% resistance=10k package=THT]
  R3 = Resistor [tolerance=±5% resistance=100k package=THT]
  R4 = Resistor [tolerance=±5% resistance=47k package=THT]
  C1 = Ceramic Capacitor [capacitance=10nF package="100 mil [THT, multilayer]"]
  C2 = Ceramic Capacitor [capacitance=10nF package="100 mil [THT, multilayer]"]
  5-9V = Power plug
  C3 = Ceramic Capacitor [capacitance=1µF package="100 mil [THT, multilayer]"]
  R5 = Resistor [tolerance=±5% resistance=100k package=THT]
  R6 = Resistor [tolerance=±5% resistance=100k package=THT]
  D1 = Rectifier Diode [part_number=1N4148 package="300 mil [THT]"]
  D2 = Rectifier Diode [part_number=1N4148 package="300 mil [THT]"]
  D3 = Rectifier Diode [part_number=1N4148 package="300 mil [THT]"]
  D4 = Rectifier Diode [part_number=1N4148 package="300 mil [THT]"]
  R7 = Trimmer Potentiometer [maximum_resistance=1kΩ package=THT]
  SPKR1 = Loudspeaker
  LED1 = LED - 3mm [color="Green (555nm)" package="3 mm [THT]"]
  R8 = Resistor [tolerance=±5% resistance=1k package=THT]

nets:
  N1: IC1.OUT1, IC1.IN2+, R2.Pin_1, R3.Pin_0, D1.anode, D4.cathode
  N2: IC1.IN1-, R3.Pin_1, R4.Pin_1, D2.cathode, D3.anode
  CH2: IC1.IN1+, R1.Pin_0, C1.0, C2.0
  VCC: IC1.V+, 5-9V.VCC, R5.Pin_0, R8.Pin_0
  N3: IC1.IN2-, IC1.OUT2, C3.1
  GND: IC1.GND, 5-9V.GND, R6.Pin_0, SPKR1.pin2, LED1.cathode
  N4: IC1.IN4+, R5.Pin_1, R6.Pin_1
  CH3/VGND: IC1.IN4-, IC1.OUT4, R1.Pin_1, R4.Pin_0, C1.1
  N5: R2.Pin_0, C2.1
  N6: C3.0, R7.leg2
  N7: D1.cathode, D2.anode
  N8: D3.cathode, D4.anode
  OUT_CH1: R7.wiper, SPKR1.pin1
  N9: LED1.anode, R8.Pin_1

custom parts:
  LM324: LM324 Quad OpAmp
