# Fritzing sketch WindBellKit (saved by Fritzing 1.0.1rc)
breadboards: 1

parts:
  R1 = Resistor [tolerance=±5% resistance=150k power=0.25W package=THT]
  R2 = Resistor [tolerance=±5% resistance=150k power=0.25W package=THT]
  C1 = Electrolytic Capacitor [capacitance=10µF voltage=35V package="100 mil [THT, electrolytic]"]
  C2 = Electrolytic Capacitor [capacitance=10µF voltage=35V package="100 mil [THT, electrolytic]"]
  Q1 = NPN-Transistor [part_number=S9013 package="TO92 [THT]"]
  Q2 = NPN-Transistor [part_number=S9013 package="TO92 [THT]"]
  5V_(USB) = Power plug
  R3 = Resistor [tolerance=±5% resistance=510 power=0.25W package=THT]
  D1 = LED - 3mm [color="Blue (430nm)" current=0.030A package="3 mm [THT]"]
  D2 = LED - 3mm [color="Blue (430nm)" current=0.030A package="3 mm [THT]"]
  D3 = LED - 3mm [color="Blue (430nm)" current=0.030A package="3 mm [THT]"]
  D4 = LED - 3mm [color="Blue (430nm)" current=0.030A package="3 mm [THT]"]
  R4 = Resistor [tolerance=±5% resistance=510 power=0.25W package=THT]
  D5 = LED - 3mm [color="Blue (430nm)" current=0.030A package="3 mm [THT]"]
  D6 = LED - 3mm [color="Blue (430nm)" current=0.030A package="3 mm [THT]"]
  D7 = LED - 3mm [color="Blue (430nm)" current=0.030A package="3 mm [THT]"]
  D8 = LED - 3mm [color="Blue (430nm)" current=0.030A package="3 mm [THT]"]
  R5 = Resistor [tolerance=±5% resistance=510 power=0.25W package=THT]
  D9 = LED - 3mm [color="Blue (430nm)" current=0.030A package="3 mm [THT]"]
  D10 = LED - 3mm [color="Blue (430nm)" current=0.030A package="3 mm [THT]"]
  D11 = LED - 3mm [color="Blue (430nm)" current=0.030A package="3 mm [THT]"]
  D12 = LED - 3mm [color="Blue (430nm)" current=0.030A package="3 mm [THT]"]
  R6 = Resistor [tolerance=±5% resistance=510 power=0.25W package=THT]
  D13 = LED - 3mm [color="Red (633nm)" current=0.030A package="3 mm [THT]"]
  D14 = LED - 3mm [color="Red (633nm)" current=0.030A package="3 mm [THT]"]
  D15 = LED - 3mm [color="Red (633nm)" current=0.030A package="3 mm [THT]"]
  D16 = LED - 3mm [color="Red (633nm)" current=0.030A package="3 mm [THT]"]
  R7 = Resistor [tolerance=±5% resistance=510 power=0.25W package=THT]
  D17 = LED - 3mm [color="Red (633nm)" current=0.030A package="3 mm [THT]"]
  D18 = LED - 3mm [color="Red (633nm)" current=0.030A package="3 mm [THT]"]
  D19 = LED - 3mm [color="Red (633nm)" current=0.030A package="3 mm [THT]"]
  D20 = LED - 3mm [color="Red (633nm)" current=0.030A package="3 mm [THT]"]
  R8 = Resistor [tolerance=±5% resistance=510 power=0.25W package=THT]
  D21 = LED - 3mm [color="Green (555nm)" current=0.030A package="3 mm [THT]"]
  D22 = LED - 3mm [color="Green (555nm)" current=0.030A package="3 mm [THT]"]
  D23 = LED - 3mm [color="Green (555nm)" current=0.030A package="3 mm [THT]"]

nets:
  5V/A1/B1: R1.Pin_0, R2.Pin_0, 5V_(USB).VCC, R3.Pin_0, R4.Pin_0, R5.Pin_0, R6.Pin_0, R7.Pin_0, R8.Pin_0
  N1: R1.Pin_1, C1.+, Q2.B
  N2: R2.Pin_1, C2.+, Q1.B
  A2: C1.-, Q1.C, D1.cathode, D2.cathode, D3.cathode, D4.cathode, D17.cathode, D18.cathode, D19.cathode, D20.cathode
  B2: C2.-, Q2.C, D5.cathode, D6.cathode, D7.cathode, D8.cathode, D13.cathode, D14.cathode, D15.cathode, D16.cathode
  GND: Q1.E, Q2.E, 5V_(USB).GND, D9.cathode, D10.cathode, D11.cathode, D12.cathode, D21.cathode, D22.cathode, D23.cathode
  N3: R3.Pin_1, D1.anode, D2.anode, D3.anode, D4.anode
  N4: R4.Pin_1, D5.anode, D6.anode, D7.anode, D8.anode
  N5: R5.Pin_1, D9.anode, D10.anode, D11.anode, D12.anode
  N6: R6.Pin_1, D13.anode, D14.anode, D15.anode, D16.anode
  N7: R7.Pin_1, D17.anode, D18.anode, D19.anode, D20.anode
  N8: R8.Pin_1, D21.anode, D22.anode, D23.anode

notes:
  7x blocks of 4 Blue LEDs on the A1-A2 connection
  7x blocks of 4 Blue LEDs on the B1-B2 connection
  7x blocks of 4 Blue LEDs on A1-A2 connection
  7x blocks of 4 Blue LEDs on B1-B2 connection
  4x blocks of 4 Blue LEDs always on
  x4 blocks of 4 Blue LEDs always on
  4 Red LEDs on B1-B2 connection
  4 Red LEDs on A1-A2 connection
  4 Red LEDs on the B1-B2 connection
  4 Red LEDs on the A1-A2 connection
  3x Green LEDs always on
  3 Green LEDs always on
