# Fritzing sketch BeepLogicProbe (saved by Fritzing 0.9.2b)
breadboards: 1

parts:
  IC2 = IC, DIP package, 16 pins [chip_label=CD4040 part_number=CD4040]
  IC4 = IC, DIP package, 16 pins [chip_label=CD4049 part_number=CD4049]
  IC3 = IC, DIP package, 14 pins [chip_label=CD4093]
  IC1 = LM 358 Dual Op-Amp [part_number=LM358 package="SO 08 [SMD]"]
  R1 = Resistor [tolerance=±5% resistance=1M package=THT]
  R2 = Resistor [tolerance=±5% resistance=1M package=THT]
  5-13V = Power plug
  R3 = Resistor [tolerance=±5% resistance=100k package=THT]
  R4 = Resistor [tolerance=±5% resistance=47k package=THT]
  R5 = Resistor [tolerance=±5% resistance=47k package=THT]
  R6 = Resistor [tolerance=±5% resistance=100k package=THT]
  R7 = Resistor [tolerance=±5% resistance=220 package=THT]
  LED1 = LED - 3mm [color="Green (555nm)" package="3 mm [THT]"]
  LED2 = LED - 3mm [color="Red (633nm)" package="3 mm [THT]"]
  R8 = Resistor [tolerance=±5% resistance=220 package=THT]
  R9 = Resistor [tolerance=±5% resistance=220 package=THT]
  LED3 = LED - 3mm [color="Orange (605nm)" package="3 mm [THT]"]
  C1 = Ceramic Capacitor [capacitance=82pF voltage=16V package="100 mil [THT, multilayer]"]
  R10 = Resistor [tolerance=±5% resistance=10k package=THT]
  VHFSEL = Toggle Switch [package=THT]
  C2 = Ceramic Capacitor [capacitance=470nF package="100 mil [THT, multilayer]"]
  C3 = Ceramic Capacitor [capacitance=330nF package="100 mil [THT, multilayer]"]
  R11 = Resistor [tolerance=±5% resistance=10k package=THT]
  R12 = Resistor [tolerance=±5% resistance=1k package=THT]
  C4 = Electrolytic Capacitor [capacitance=4.7µF package="100 mil [THT, electrolytic]"]
  C5 = Electrolytic Capacitor [capacitance=4.7µF package="100 mil [THT, electrolytic]"]
  C6 = Electrolytic Capacitor [capacitance=4.7µF package="100 mil [THT, electrolytic]"]
  PIEZO = Piezo Speaker

nets:
  GND: IC2.pin8, IC2.pin11, IC4.pin8, IC3.pin7, IC1.connector3, R2.Pin_0, 5-13V.GND, R3.Pin_1, R5.Pin_0, R7.Pin_0, LED3.cathode, C2.0, C3.1, PIEZO.pin1
  N1: IC2.pin10, R10.Pin_1
  N2: IC2.pin13, R9.Pin_0
  Q10: IC2.pin14, VHFSEL.L1
  Q11: IC2.pin15, VHFSEL.L2
  VCC: IC2.pin16, IC4.pin1, IC3.pin2, IC3.pin14, IC1.connector7, R1.Pin_0, 5-13V.VCC, R4.Pin_1, R6.Pin_0, R8.Pin_0
  N3: IC4.pin2, IC4.pin15, C5.+
  N4: IC4.pin3, IC4.pin14, VHFSEL.COM
  N5: IC4.pin4, IC4.pin6, C6.+
  OCS_LO: IC4.pin5, IC4.pin7, IC3.pin11, R11.Pin_1
  OCS_HI: IC4.pin9, IC4.pin11, IC3.pin10, R12.Pin_0
  N6: IC4.pin10, IC4.pin12, C4.+
  VLOW: IC3.pin1, IC1.connector0, LED2.cathode
  N7: IC3.pin3, IC3.pin12
  N8: IC3.pin8, C3.0, R12.Pin_1
  VHI: IC3.pin9, IC1.connector6, LED1.anode
  N9: IC3.pin13, C2.1, R11.Pin_0
  N10: IC1.connector1, R5.Pin_1, R6.Pin_1
  PROBE/VIN: IC1.connector2, IC1.connector4, R1.Pin_1, R2.Pin_1, C1.1
  N11: IC1.connector5, R3.Pin_0, R4.Pin_0
  N12: R7.Pin_1, LED1.cathode
  N13: LED2.anode, R8.Pin_1
  N14: R9.Pin_1, LED3.anode
  N15: C1.0, R10.Pin_0
  N16: C4.-, C5.-, C6.-, PIEZO.pin2

notes:
  PROBE
