# Fritzing sketch ComponentTesterKit (saved by Fritzing 0.9.2b)
breadboards: 1

parts:
  U1 = atmega328 [package=dip]
  LED1 = LED - 3mm [color="Red (633nm)" package="3 mm [THT]"]
  Q1 = NPN-Transistor [part_number=S9014 package="TO92 [THT]"]
  C1 = Ceramic Capacitor [capacitance=100nF package="100 mil [THT, multilayer]"]
  IC2 = NPN-Transistor [part_number=7550 package="TO92 [THT]"]
  Q2 = NPN-Transistor [part_number=S9014 package="TO92 [THT]"]
  C2 = Ceramic Capacitor [capacitance=10nF package="100 mil [THT, multilayer]"]
  C3 = Ceramic Capacitor [capacitance=22pF package="100 mil [THT, multilayer]"]
  C4 = Ceramic Capacitor [capacitance=22pF package="100 mil [THT, multilayer]"]
  C5 = Ceramic Capacitor [capacitance=100nF package="100 mil [THT, multilayer]"]
  C6 = Ceramic Capacitor [capacitance=100nF package="100 mil [THT, multilayer]"]
  C7 = Ceramic Capacitor [capacitance=100nF package="100 mil [THT, multilayer]"]
  R1 = Resistor [tolerance=±5% resistance=220 package=THT]
  R2 = Resistor [tolerance=±5% resistance=10k package=THT]
  R3 = Resistor [tolerance=±5% resistance=10k package=THT]
  R4 = Resistor [tolerance=±5% resistance=10k package=THT]
  C8 = Electrolytic Capacitor [capacitance=10µF package="100 mil [THT, electrolytic]"]
  XTAL1 = Crystal [frequency="8 MHz" package=THT]
  C9 = Ceramic Capacitor [capacitance=100nF package="100 mil [THT, multilayer]"]
  C10 = Electrolytic Capacitor [capacitance=10µF package="100 mil [THT, electrolytic]"]
  R5 = Resistor [tolerance=±5% resistance=3.3k package=THT]
  R6 = Resistor [tolerance=±5% resistance=33k package=THT]
  R7 = Resistor [tolerance=±5% resistance=10k package=THT]
  R8 = Resistor [tolerance=±5% resistance=3.3k package=THT]
  R9 = Resistor [tolerance=±5% resistance=680 package=THT]
  R10 = Resistor [tolerance=±5% resistance=470k package=THT]
  R11 = Resistor [tolerance=±5% resistance=680 package=THT]
  R12 = Resistor [tolerance=±5% resistance=470k package=THT]
  R14 = Resistor [tolerance=±5% resistance=470k package=THT]
  R13 = Resistor [tolerance=±5% resistance=680 package=THT]
  C11 = Ceramic Capacitor [capacitance=1nF package="100 mil [THT, multilayer]"]
  IC3 = NPN-Transistor [part_number=TL431 package="TO92 [THT]"]
  R15 = Resistor [tolerance=±5% resistance=1k package=THT]
  R16 = Resistor [tolerance=±5% resistance=1k package=THT]
  R17 = Resistor [tolerance=±5% resistance=10k package=THT]
  R18 = Resistor [tolerance=±5% resistance=2.2k package=THT]
  D1 = VARISTOR [part_number="P6KE6V8 bidirectional diode" package=0603-res]
  C12 = Ceramic Capacitor [capacitance=100nF package="100 mil [THT, multilayer]"]
  9V = Power plug
  R19 = Resistor [tolerance=±5% resistance=180k package=THT]
  R20 = Resistor [tolerance=±5% resistance=20k package=THT]
  R21 = Resistor [tolerance=±5% resistance=100k package=THT]
  R22 = Resistor [tolerance=±5% resistance=27k package=THT]
  R23 = Resistor [tolerance=±5% resistance=27k package=THT]
  Q3 = PNP-Transistor [part_number=S9012 package="TO92 [THT]"]
  SCREEN = female pin header, 8 pins [form="♀ (female)"]
  J3 = Screw terminal - 2 pins [package=THT]
  J4 = Screw terminal - 2 pins [package=THT]
  ROTARYSW = female pin header, 5 pins [form="♀ (female)"]
  R24 = Resistor [tolerance=±5% resistance=10k package=THT]
  IC1 = IC, DIP package, 6 pins [chip_label=IC part_number=SVR5-04]
  TP = female pin header, 3 pins [form="♀ (female)"]
  J5 = Screw terminal - 2 pins [package=THT]

nets:
  N1: U1.RESET, R4.Pin_1
  N2: U1.D0_(RX), SCREEN.pin2
  N3: U1.D1_(TX), R16.Pin_1, SCREEN.pin3
  N4: U1.D2, SCREEN.pin5
  N5: U1.D3_(PWM), R15.Pin_1, SCREEN.pin4
  N6: U1.D4, C7.0, R2.Pin_1, R3.Pin_1
  VCC: U1.VCC, U1.AVCC, C5.0, C6.0, R1.Pin_0, R3.Pin_0, R4.Pin_0, C8.+, SCREEN.pin7
  GND: U1.GND, C2.1, C3.1, C4.1, C5.1, C6.1, R2.Pin_0, C8.-, C11.1, IC3.B, 9V.GND, R21.Pin_1, SCREEN.pin8, J3.pin2, J4.pin2, J5.pin1
  N7: U1.XLAT1, C4.0, XTAL1.pin_1
  N8: U1.XLAT2, C3.0, XTAL1.pin_0
  N9: U1.D5_(PWM), SCREEN.pin6
  N10: U1.D6_(PWM), R23.Pin_1
  N11: U1.D7, Q2.C, R22.Pin_1
  N12: U1.D8, R9.Pin_0
  N13: U1.D9_(PWM), R10.Pin_0
  N14: U1.D10_(PWM), R11.Pin_0
  N15: U1.D11_(PWM), R12.Pin_0
  N16: U1.D12, R13.Pin_0
  N17: U1.D13, R14.Pin_0
  N18: U1.AREF, C11.0
  TP1: U1.A0, R9.Pin_1, R10.Pin_1, IC1.pin4, TP.pin1
  TP2: U1.A1, R11.Pin_1, R12.Pin_1, J4.pin1, IC1.pin6, TP.pin2
  TP3: U1.A2, R14.Pin_1, R13.Pin_1, IC1.pin3, TP.pin3
  N19: U1.A3, R19.Pin_1, R20.Pin_1
  N20: U1.A4, IC3.E, IC3.C, R18.Pin_1
  N21: U1.A5, R7.Pin_1, R8.Pin_1
  N22: LED1.cathode, Q1.C
  N23: LED1.anode, R5.Pin_0, ROTARYSW.pin4
  N24: Q1.E, C1.1, IC2.E, Q2.E, R8.Pin_0, ROTARYSW.pin2
  N25: Q1.B, C2.0, R21.Pin_0, R23.Pin_0
  N26: C1.0, IC2.C, R22.Pin_0
  N27: IC2.B, C9.1, C10.+, R7.Pin_0, Q3.E
  N28: Q2.B, ROTARYSW.pin5
  F-input: C7.1, J5.pin2
  N29: R1.Pin_1, SCREEN.pin1
  N30: C9.0, C10.-
  N31: R5.Pin_1, R6.Pin_0, Q3.B
  VEXT: R6.Pin_1, 9V.VCC, Q3.C
  N32: R15.Pin_0, R17.Pin_1, ROTARYSW.pin1
  N33: R16.Pin_0, ROTARYSW.pin3, R24.Pin_1
  N34: R17.Pin_0, R18.Pin_0, D1.1, C12.1, R24.Pin_0, IC1.pin5
  N35: D1.2, C12.0
  Vext: R19.Pin_0, J3.pin1
  N36: R20.Pin_0, IC1.pin2

notes:
  I haven't laid out the parts for a breadboard build (obviously!!)
  this is only a partial draft schematic. I mainly used this to record part orientation and interconnection for testing the circuit during construction
