# Fritzing sketch DPS3005BenchPowerSupply (saved by Fritzing 0.9.2b)

parts:
  U1 = Transformer [package=transformer_smd]
  D1 = Rectifier Diode [part_number=1N4001 package="Melf DO-213 AB [SMD]"]
  C1 = Electrolytic Capacitor [capacitance=82µF voltage=450V package="100 mil [THT, electrolytic]"]
  MAINS = screw terminal, 3 pins
  D2 = Rectifier Diode [part_number=1N4001 package="Melf DO-213 AB [SMD]"]
  D3 = Rectifier Diode [part_number=1N4001 package="Melf DO-213 AB [SMD]"]
  D4 = Rectifier Diode [part_number=1N4001 package="Melf DO-213 AB [SMD]"]
  DPS3005 = screw terminal, 4 pins
  DCOUT = Screw terminal - 2 pins [package=THT]
  F1 = FUSE [package=fuse_5mm]
  S1 = Round Pushbutton

nets:
  N1: U1.1, S1.leg1
  N2: U1.2, MAINS.pin2
  N3: U1.3, D1.cathode, D4.anode
  N4: U1.4, D2.cathode, D3.anode
  N5: D1.anode, C1.-, D2.anode, DPS3005.pin2
  N6: C1.+, D3.cathode, D4.cathode, DPS3005.pin1
  L: MAINS.pin1, F1.1
  E/GND: MAINS.pin3
  N7: DPS3005.pin3, DCOUT.pin2
  N8: DPS3005.pin4, DCOUT.pin1
  N9: F1.2, S1.leg0
