# Fritzing sketch FoamCutter (saved by Fritzing 0.9.2b)
breadboards: 1

parts:
  L1 = Inductor [part_number="nichrome wire" package="400 mil [THT]"]
  VCC = Battery
  S1 = Pushbutton [package="[THT]"]

nets:
  GND: L1.pin_0, VCC.-
  N1: L1.pin_1, S1.Pin_1, S1.Pin_2
  N2: VCC.+, S1.Pin_3, S1.Pin_4
