# Fritzing sketch FrequencyCounterKit (saved by Fritzing 0.9.2b)
breadboards: 1

parts:
  LED5 = 7 Segment Display
  IC1 = PIC16F88-DIP [part_number=PIC16F628 package=dil18]
  R1 = Resistor [tolerance=±5% resistance=10k package=THT]
  R2 = Resistor [tolerance=±5% resistance=10k package=THT]
  D1 = Rectifier Diode [part_number=1N4148 package="300 mil [THT]"]
  D2 = Rectifier Diode [part_number=1N4148 package="300 mil [THT]"]
  D3 = Rectifier Diode [part_number=1N4148 package="300 mil [THT]"]
  XTAL1 = Crystal [frequency="20 MHz" package=THT]
  C1 = Ceramic Capacitor [capacitance=22pF package="100 mil [THT, multilayer]"]
  C2 = CAP_ADJ [part_number=10-40pF package=ctz3]
  S1 = Pushbutton [package=THT]
  D4 = Rectifier Diode [part_number=1N4148 package="300 mil [THT]"]
  Q1 = NPN-Transistor [part_number=S9014 package="TO92 [THT]"]
  LED1 = 7 Segment Display
  LED2 = 7 Segment Display
  LED3 = 7 Segment Display
  LED4 = 7 Segment Display
  R3 = Resistor [tolerance=±5% resistance=1k package=THT]
  R4 = Resistor [tolerance=±5% resistance=1k package=THT]
  R5 = Resistor [tolerance=±5% resistance=1k package=THT]
  R6 = Resistor [tolerance=±5% resistance=1k package=THT]
  R7 = Resistor [tolerance=±5% resistance=1k package=THT]
  R8 = Resistor [tolerance=±5% resistance=1k package=THT]
  R9 = Resistor [tolerance=±5% resistance=1k package=THT]
  R10 = Resistor [tolerance=±5% resistance=1k package=THT]
  R11 = Resistor [tolerance=±5% resistance=1k package=THT]
  R12 = Resistor [tolerance=±5% resistance=100k package=THT]
  Q2 = NPN-Transistor [part_number=S9018 package="TO92 [THT]"]
  C3 = Ceramic Capacitor [capacitance=22pF package="100 mil [THT, multilayer]"]
  C4 = Ceramic Capacitor [capacitance=22pF package="100 mil [THT, multilayer]"]
  C5 = Ceramic Capacitor [capacitance=1nF package="100 mil [THT, multilayer]"]
  C6 = Ceramic Capacitor [capacitance=100nF package="100 mil [THT, multilayer]"]
  IC2 = Voltage Regulator [part_number=7550A-1 package=to-92]
  J2 = female pin header, 3 pins [form="♀ (female)"]
  J1 = female pin header, 3 pins [form="♀ (female)"]
  J3 = Power Jack [package=power_jack_combo]

nets:
  g: LED5.Segment_A#1, LED1.Segment_A#1, LED2.Segment_A#1, LED3.Segment_A#1, LED4.Segment_A#1, R10.Pin_1
  f: LED5.Segment_F, LED1.Segment_F, LED2.Segment_F, LED3.Segment_F, LED4.Segment_F, R9.Pin_1
  N1: LED5.common_cathode, Q1.C
  e: LED5.Segment_E, LED1.Segment_E, LED2.Segment_E, LED3.Segment_E, LED4.Segment_E, R3.Pin_1
  d: LED5.Segment_D, LED1.Segment_D, LED2.Segment_D, LED3.Segment_D, LED4.Segment_D, R6.Pin_1
  dp: LED5.Segment_DP, LED1.Segment_DP, LED2.Segment_DP, LED3.Segment_DP, LED4.Segment_DP, R4.Pin_1
  c: LED5.Segment_C, LED1.Segment_C, LED2.Segment_C, LED3.Segment_C, LED4.Segment_C, R5.Pin_1
  b: LED5.Segment_B, LED1.Segment_B, LED2.Segment_B, LED3.Segment_B, LED4.Segment_B, R7.Pin_1
  a: LED5.Segment_A#10, LED1.Segment_A#10, LED2.Segment_A#10, LED3.Segment_A#10, LED4.Segment_A#10, R8.Pin_1
  N2: IC1.RA2_AN2, D1.cathode, LED2.common_cathode
  N3: IC1.RA3_AN3, R1.Pin_0, LED1.common_cathode
  N4: IC1.RA4_AN4, C5.0, J2.pin1
  N5: IC1.RA5_MCLR, R2.Pin_1, S1.leg1
  GND: IC1.VSS, C1.0, C2.4, S1.leg0, D4.cathode, R11.Pin_1, C4.0, C6.1, IC2.GND, J1.pin1, J3.GND
  N6: IC1.RB0_INT, R6.Pin_0
  N7: IC1.RB1_SDA, R4.Pin_0
  N8: IC1.RB2_RX, R5.Pin_0
  N9: IC1.RB3, R3.Pin_0
  N10: IC1.RB4_SCL, R9.Pin_0
  N11: IC1.RB5_TX, R10.Pin_0
  N12: IC1.RB6_PGC, R8.Pin_0
  N13: IC1.RB7_PGD, R7.Pin_0
  N14: IC1.VDD, R2.Pin_0, C6.0, IC2.OUT
  N15: IC1.RA6_OSC2, XTAL1.pin_0, C1.1
  N16: IC1.RA7_OSC1, XTAL1.pin_1, C2.3
  N17: IC1.RA0_AN0, D2.cathode, LED3.common_cathode
  N18: IC1.RA1_AN1, D3.cathode, LED4.common_cathode
  N19: R1.Pin_1, D1.anode, D2.anode, D3.anode, Q1.B
  N20: D4.anode, Q1.E
  N21: R11.Pin_0, Q2.E
  N22: R12.Pin_0, Q2.B, C3.1, J1.pin3
  VIN: R12.Pin_1, Q2.C, IC2.IN, J2.pin2, J3.PWR
  N23: C3.0, C4.1, C5.1
  N24: J2.pin3, J3.GNDBREAK

notes:
  I haven't bothered to layout the breadboard as this build is direct to PCB
