# Fritzing sketch FunctionGeneratorKit (saved by Fritzing 0.9.2b)
breadboards: 1

parts:
  IC1 = IC, DIP package, 16 pins [chip_label=IC part_number=XR2206CP]
  12V = Power plug
  R1 = Resistor [tolerance=±5% resistance=1k package=THT]
  R2 = Rotary Potentiometer (Small) [maximum_resistance=500kΩ package=THT]
  R3 = Resistor [tolerance=±5% resistance=5.1k package=THT]
  R6 = Resistor [tolerance=±5% resistance=5.1k package=THT]
  R5 = Resistor [tolerance=±5% resistance=5.1k package=THT]
  R4 = Resistor [tolerance=±5% resistance=330k package=THT]
  R7 = Rotary Potentiometer (Small) [maximum_resistance=500kΩ package=THT]
  R8 = Rotary Potentiometer (Small) [maximum_resistance=100kΩ package=THT]
  C1 = Electrolytic Capacitor [capacitance=100µF package="100 mil [THT, electrolytic]"]
  C4 = Electrolytic Capacitor [capacitance=10µF package="100 mil [THT, electrolytic]"]
  C3 = Electrolytic Capacitor [capacitance=10µF package="100 mil [THT, electrolytic]"]
  C2 = Ceramic Capacitor [capacitance=100nF package="100 mil [THT, multilayer]"]
  C5 = Ceramic Capacitor [capacitance=1µF package="100 mil [THT, multilayer]"]
  C6 = Ceramic Capacitor [capacitance=47nF package="100 mil [THT, multilayer]"]
  C7 = Ceramic Capacitor [capacitance=2.2nF package="100 mil [THT, multilayer]"]
  C8 = Ceramic Capacitor [capacitance=100pF package="100 mil [THT, multilayer]"]
  J3 = shrouded pin header, 10 pins [form="♂ (shrouded male)"]
  J1 = female pin header, 2 pins [form="♀ (female)"]
  J2 = female pin header, 2 pins [form="♀ (female)"]  # not connected
  P1 = screw terminal, 3 pins

nets:
  GND: IC1.pin1, IC1.pin12, 12V.GND, R5.Pin_1, R8.leg2, C1.-, C3.-, C2.0, P1.pin3
  N1: IC1.pin2, P1.pin1
  N2: IC1.pin3, R2.leg1, R2.wiper
  VCC: IC1.pin4, 12V.VCC, R1.Pin_0, R3.Pin_0, C1.+, C2.1
  N3: IC1.pin5, J3.pin1, J3.pin2, J3.pin3, J3.pin4, J3.pin5
  N4: IC1.pin6, C4.-, C5.0, C6.0, C7.0, C8.0
  N5: IC1.pin7, R6.Pin_0
  N6: IC1.pin10, C3.+
  N7: IC1.pin11, R1.Pin_1, P1.pin2
  N8: IC1.pin13, R4.Pin_1
  N9: IC1.pin14, J1.pin1
  N10: R2.leg2, R3.Pin_1, R5.Pin_0
  N11: R6.Pin_1, R7.leg1, R7.wiper
  N12: R4.Pin_0, J1.pin2
  N13: R7.leg2, R8.leg1, R8.wiper
  N14: C4.+, J3.pin6
  N15: C5.1, J3.pin7
  N16: C6.1, J3.pin8
  N17: C7.1, J3.pin9
  N18: C8.1, J3.pin10
