# Fritzing sketch HiLoLogicTesterKit (saved by Fritzing 0.9.2b)
breadboards: 1

parts:
  5-15V = Power plug
  U1 = IC, DIP package, 16 pins [chip_label=CD4511]
  LED2 = 7 Segment Display
  VT1 = NPN-Transistor [part_number=9014 package="TO92 [THT]"]
  R1 = Resistor [tolerance=±5% resistance=2k package=THT]
  R2 = Resistor [tolerance=±5% resistance=1M package=THT]
  R3 = Resistor [tolerance=±5% resistance=1M package=THT]
  R4 = Resistor [tolerance=±5% resistance=120k package=THT]
  R5 = Resistor [tolerance=±5% resistance=1k package=THT]
  R6 = Resistor [tolerance=±5% resistance=10k package=THT]
  R7 = Resistor [tolerance=±5% resistance=51 package=THT]
  VD1 = Rectifier Diode [part_number=1N4148 package="300 mil [THT]"]
  VT2 = NPN-Transistor [part_number=9014 package="TO92 [THT]"]
  C1 = Ceramic Capacitor [capacitance=220pF package="100 mil [THT, multilayer]"]
  C2 = Electrolytic Capacitor [capacitance=4.7µF package="100 mil [THT, electrolytic]"]
  INPUT = female pin header, 4 pins [form="♀ (female)"]
  LED1 = LED - 5mm [color="Red (633nm)" package="5 mm [THT]"]
  C3 = Ceramic Capacitor [capacitance=47nF package="100 mil [THT, multilayer]"]

nets:
  GND: 5-15V.GND, U1.pin5, U1.pin6, U1.pin7, U1.pin8, R6.Pin_1, VT2.E, C1.0, C2.-, INPUT.pin4
  5V: 5-15V.VCC, U1.pin3, U1.pin16, R2.Pin_0, R3.Pin_0, C2.+, INPUT.pin1, LED1.anode
  N1: U1.pin1, VT1.B, R1.Pin_1, R2.Pin_1, VD1.anode, C3.0
  N2: U1.pin2, U1.pin4, R3.Pin_1, R4.Pin_0, VD1.cathode, C1.1
  N3: U1.pin9, LED2.Segment_A#1
  N4: U1.pin10, LED2.Segment_C, LED2.Segment_B
  N5: U1.pin12, LED2.Segment_D
  N6: U1.pin14, LED2.Segment_E
  N7: U1.pin15, LED2.Segment_F
  N8: LED2.common_cathode#8, R7.Pin_0
  N9: VT1.E, R6.Pin_0
  N10: VT1.C, R4.Pin_1
  N11: R1.Pin_0, INPUT.pin2, INPUT.pin3, C3.1
  N12: R5.Pin_0, LED1.cathode
  N13: R5.Pin_1, VT2.B
  N14: R7.Pin_1, VT2.C
