# Fritzing sketch LightControlSwitchKit (saved by Fritzing 0.9.2b)
breadboards: 1

parts:
  Q1 = NPN-Transistor [part_number=8050 package="TO92 [THT]"]
  J1 = Power plug
  Q2 = NPN-Transistor [part_number=8050 package="TO92 [THT]"]
  R1 = Resistor [tolerance=±5% resistance=4.7k package=THT]
  LED1 = LED - 5mm [color="Red (633nm)" package="5 mm [THT]"]
  J2 = Photocell (LDR) [package=THT]
  R2 = Resistor [tolerance=±5% resistance=510k package=THT]
  C1 = Ceramic Capacitor [capacitance=100nF package="100 mil [THT, multilayer]"]
  U1 = LM393 [package=so08]
  J3 = SWITCH-DPDT [package=ayz0202]
  R3 = Trimmer Potentiometer [maximum_resistance=10kΩ package=THT]
  C2 = Electrolytic Capacitor [capacitance=10µF package="100 mil [THT, electrolytic]"]
  R4 = Resistor [tolerance=±5% resistance=10k package=THT]
  R5 = Resistor [tolerance=±5% resistance=2.2k package=THT]
  K1 = songle relay
  R6 = Resistor [tolerance=±5% resistance=10k package=THT]
  D1 = Rectifier Diode [part_number=1N4007 package="300 mil [THT]"]
  R7 = Resistor [tolerance=±5% resistance=2.2k package=THT]
  LED2 = LED - 5mm [color="Red (633nm)" package="5 mm [THT]"]

nets:
  GND: Q1.E, J1.GND, Q2.E, LED1.cathode, J2.pin_0, C1.0, U1.G1_V-, R3.leg2
  N1: Q1.B, J3.1
  N2: Q1.C, Q2.C, J3.4, K1.A, R6.Pin_1, D1.anode, LED2.cathode
  5V: J1.VCC, R1.Pin_0, R2.Pin_0, U1.G1_V+, R3.leg1, R4.Pin_0, K1.B, R6.Pin_0, D1.cathode, R7.Pin_0
  N3: Q2.B, J3.3, J3.5
  N4: R1.Pin_1, LED1.anode
  N5: J2.pin_1, R2.Pin_1, C1.1, U1.G1_-IN, C2.+
  N6: U1.G1_OUT, C2.-, R4.Pin_1, R5.Pin_0
  N7: U1.G1_+IN, R3.wiper
  N8: J3.2, R5.Pin_1
  N9: R7.Pin_1, LED2.anode
