# Fritzing sketch LowCurrentReferenceDIY (saved by Fritzing 1.0.1rc)
breadboards: 1

parts:
  IC1 = IC, DIP package, 8 pins [chip_label=REF200 part_number=REF200]
  5V = Power plug
  meter1 = Resistor [tolerance=±5% power=0.25W resistance=220 package=THT]
  IC2 = IC, DIP package, 8 pins [chip_label=REF200 part_number=REF200]
  meter2 = Resistor [tolerance=±5% power=0.25W resistance=220 package=THT]
  IC3 = IC, DIP package, 8 pins [chip_label=REF200 part_number=REF200]
  meter3 = Resistor [tolerance=±5% power=0.25W resistance=220 package=THT]
  IC4 = IC, DIP package, 8 pins [chip_label=REF200 part_number=REF200]
  meter4 = Resistor [tolerance=±5% power=0.25W resistance=220 package=THT]

nets:
  N1: IC1.pin1, meter1.Pin_0
  Vs+: IC1.pin8, 5V.VCC, IC2.pin7, IC2.pin8, IC3.pin4, IC3.pin7, IC3.pin8, IC4.pin4, IC4.pin7, IC4.pin8
  GND: 5V.GND, meter1.Pin_1, meter2.Pin_1, meter3.Pin_1, meter4.Pin_1
  N2: IC2.pin1, IC2.pin2, meter2.Pin_0
  N3: IC3.pin1, IC3.pin3, meter3.Pin_0
  N4: IC3.pin2, IC3.pin5
  N5: IC4.pin1, IC4.pin2, IC4.pin5
  N6: IC4.pin3, meter4.Pin_0

notes:
  100µA
  200µA
  300µA
  400µA
