# Fritzing sketch MetalDetectorKit (saved by Fritzing 0.9.2b)
breadboards: 1

parts:
  5V = Power plug
  C1 = Ceramic Capacitor [capacitance=100nF package="100 mil [THT, multilayer]"]
  Q1 = NPN-Transistor [part_number=S9018 package="TO92 [THT]"]
  Q2 = PNP-Transistor [part_number=S9012 package="TO92 [THT]"]
  Q3 = PNP-Transistor [part_number=S9012 package="TO92 [THT]"]
  R1 = Resistor [tolerance=±5% resistance=200k package=THT]
  VR1 = Trimmer Potentiometer [maximum_resistance=100Ω package=THT]
  C2 = Ceramic Capacitor [capacitance=2.2nF package="100 mil [THT, multilayer]"]
  C3 = Ceramic Capacitor [capacitance=2.2nF package="100 mil [THT, multilayer]"]
  C4 = Ceramic Capacitor [capacitance=100nF package="100 mil [THT, multilayer]"]
  R2 = Resistor [tolerance=±5% resistance=2k package=THT]
  R3 = Resistor [tolerance=±5% resistance=470 package=THT]
  L1 = Inductor [package="400 mil [THT]"]
  L2 = Inductor [package="400 mil [THT]"]
  C5 = Electrolytic Capacitor [capacitance=100µF package="100 mil [THT, electrolytic]"]
  LED1 = LED - 5mm [color="Red (633nm)" package="5 mm [THT]"]
  SP1 = Piezo Speaker
  SW1 = Toggle Switch [package=THT]

nets:
  GND: 5V.GND, C1.0, VR1.leg1, VR1.wiper, R2.Pin_1, R3.Pin_1, C5.-, SP1.pin1
  N1: 5V.VCC, SW1.L2
  N2: C1.1, Q2.E, Q3.E, R1.Pin_0, C3.0, C4.1, L1.pin_0, L2.pin_0, SW1.COM
  N3: Q1.E, VR1.leg2
  N4: Q1.B, R1.Pin_1, C2.0
  N5: Q1.C, Q2.B, C3.1, L2.pin_1
  N6: Q2.C, Q3.B, C4.0, R2.Pin_0
  N7: Q3.C, C5.+, LED1.anode, SP1.pin2
  N8: C2.1, L1.pin_1
  N9: R3.Pin_0, LED1.cathode
