# Fritzing sketch MilliVoltmeterDIY (saved by Fritzing 0.9.2b)
breadboards: 2

parts:
  Part1 = Arduino Uno (Rev3)
  IC1 = IC, DIP package, 8 pins [chip_label=1019 part_number=LT1019]
  IC2 = IC, DIP package, 8 pins [chip_label=2400 part_number=LTC2400]
  R1 = Resistor [tolerance=±5% resistance=5 package=THT]
  C1 = Electrolytic Capacitor [capacitance=2.2µF package="100 mil [THT, electrolytic]"]
  R2 = Resistor [tolerance=±5% resistance=100k package=THT]
  R3 = Resistor [tolerance=±5% resistance=1M package=THT]
  LCD1 = LCD screen
  R4 = Resistor [tolerance=±5% resistance=220 package=THT]
  R5 = Trimmer Potentiometer [maximum_resistance=10kΩ package=THT]
  BTN_CAL = Pushbutton [package="[THT]"]
  BTN_PRECISION = Pushbutton [package="[THT]"]
  BTN_2_FUNCTION = Pushbutton [package="[THT]"]
  R6 = Resistor [tolerance=±5% resistance=100k package=THT]
  R7 = Resistor [tolerance=±5% resistance=220k package=THT]
  R8 = Resistor [tolerance=±5% resistance=10k package=THT]
  R9 = Resistor [tolerance=±5% resistance=10k package=THT]
  L1 = Inductor [inductance=100µH package="400 mil [THT]"]
  C2 = Electrolytic Capacitor [capacitance=10µF package="100 mil [THT, electrolytic]"]
  C3 = Ceramic Capacitor [capacitance=100nF package="100 mil [THT, multilayer]"]
  C4 = Ceramic Capacitor [capacitance=10nF package="100 mil [THT, multilayer]"]

nets:
  N1: Part1.A0, BTN_CAL.Pin_1, BTN_CAL.Pin_2
  N2: Part1.A1, R6.Pin_1, R7.Pin_1
  N3: Part1.D8, BTN_2_FUNCTION.Pin_1, BTN_2_FUNCTION.Pin_2
  N4: Part1.D9_PWM, BTN_PRECISION.Pin_1, BTN_PRECISION.Pin_2
  CS: Part1.D10_PWM/SS, IC2.pin5, R8.Pin_0
  SDA: Part1.D12/MISO, IC2.pin6
  SCK: Part1.D13/SCK, IC2.pin7, R9.Pin_0
  N5: Part1.D2, LCD1.DB7
  N6: Part1.D3_PWM, LCD1.DB6
  N7: Part1.D4, LCD1.DB5
  N8: Part1.D5_PWM, LCD1.DB4
  N9: Part1.D6_PWM, LCD1.E
  N10: Part1.D7, LCD1.RS
  VBATT/VCC: Part1.5V, LCD1.VDD, R4.Pin_1, R5.leg2, R7.Pin_0, L1.pin_0
  GND: Part1.GND, IC1.pin4, IC2.pin4, C1.-, R2.Pin_1, LCD1.VSS, LCD1.R/W, LCD1.LED-, R5.leg1, BTN_CAL.Pin_3, BTN_CAL.Pin_4, BTN_PRECISION.Pin_3, BTN_PRECISION.Pin_4, BTN_2_FUNCTION.Pin_3, BTN_2_FUNCTION.Pin_4, R6.Pin_0, C2.-, C3.0, C4.0
  N11: IC1.pin2, IC2.pin1, IC2.pin8, R8.Pin_1, R9.Pin_1, L1.pin_1, C2.+, C3.1, C4.1
  CALIBRATE: IC1.pin6, IC2.pin2, R1.Pin_0
  N12: IC2.pin3, R2.Pin_0, R3.Pin_1
  N13: R1.Pin_1, C1.+
  VIN: R3.Pin_0
  N14: LCD1.V0, R5.wiper
  N15: LCD1.LED+, R4.Pin_0

notes:
  VIN
  CALIBRATE
