# Fritzing sketch PLJ1601 (saved by Fritzing 1.0.1rc)
breadboards: 1

parts:
  R1 = Rotary Potentiometer (Small) [maximum_resistance=10kΩ knob_status=50% power=0.5W package=THT]
  C1 = Ceramic Capacitor [capacitance=100nF voltage=35V package="100 mil [THT, multilayer]"]
  SIGNAL_IN = female pin header, 2 pins [form="♀ (female)"]
  PLJ-1601_INPUT = female pin header, 2 pins [form="♀ (female)"]

nets:
  GND: R1.leg1, SIGNAL_IN.pin2, PLJ-1601_INPUT.pin2
  N1: R1.wiper, C1.0
  N2: R1.leg2, SIGNAL_IN.pin1
  N3: C1.1, PLJ-1601_INPUT.pin1

notes:
  SIGNAL IN
  PLJ-1601 INPUT
