# Fritzing sketch PowerMeterATTinyLoSideAutoSwitch (saved by Fritzing 0.9.2b)
breadboards: 1

parts:
  IC1 = IC, DIP package, 10 pins [chip_label=ina226]
  Rshunt = Resistor [tolerance=±5% resistance=0.20 package=THT]
  R1 = Resistor [tolerance=±5% resistance=10k package=THT]
  R2 = Resistor [tolerance=±5% resistance=10k package=THT]
  R3 = Resistor [tolerance=±5% resistance=10k package=THT]
  C1 = Ceramic Capacitor [capacitance=100nF package="100 mil [THT, multilayer]"]
  RLOAD = Resistor [tolerance=±5% resistance=50 power=5W package=THT]
  VLOAD = Power plug
  OLED1 = 128x32 I2C Monochrome OLED Display
  U1 = attiny85 [package=dip]
  Part1 = LilyPad Coin Cell Battery Holder
  Q1 = Basic FET N-Channel [part_number=AO3400 package="D2Pak [SMD]"]
  VLOAD_SWITCH = Pushbutton [part_number="normally closed DC Jack 3rd pin" package=THT]
  R4 = Resistor [tolerance=±5% resistance=920k package=THT]

nets:
  VGND: IC1.pin1, IC1.pin2, IC1.pin7, C1.0, OLED1.GND, U1.Pin_4, Q1.drain
  ALERT: IC1.pin3, R3.Pin_0
  SDA: IC1.pin4, R2.Pin_0, OLED1.SDA, U1.Pin_5
  SCL: IC1.pin5, R1.Pin_0, OLED1.SCL, U1.Pin_7
  3V: IC1.pin6, R1.Pin_1, R2.Pin_1, R3.Pin_1, C1.1, OLED1.3.3V, U1.Pin_8, Part1.+, R4.Pin_0
  N1: IC1.pin8, IC1.pin9, Rshunt.Pin_1, RLOAD.Pin_1
  N2: IC1.pin10, Rshunt.Pin_0, VLOAD.VCC
  GND: RLOAD.Pin_0, VLOAD.GND, Part1.-, Q1.source, VLOAD_SWITCH.leg0
  N3: Q1.Gate, VLOAD_SWITCH.leg1, R4.Pin_1
