# Fritzing sketch PowerMeterArduino (saved by Fritzing 0.9.2b)
breadboards: 1

parts:
  Part1 = Arduino Uno (Rev3)
  IC1 = IC, DIP package, 10 pins [chip_label=ina226]
  Rshunt = Resistor [tolerance=±5% resistance=0.20 package=THT]
  R1 = Resistor [tolerance=±5% resistance=10k package=THT]
  R2 = Resistor [tolerance=±5% resistance=10k package=THT]
  R3 = Resistor [tolerance=±5% resistance=10k package=THT]
  C1 = Ceramic Capacitor [capacitance=100nF package="100 mil [THT, multilayer]"]
  RLOAD = Resistor [tolerance=±5% resistance=50 power=5W package=THT]
  VLOAD = Power plug
  OLED1 = 128x32 I2C Monochrome OLED Display

nets:
  SDA: Part1.A4/SDA, IC1.pin4, R2.Pin_0, OLED1.SDA
  SCL: Part1.A5/SCL, IC1.pin5, R1.Pin_0, OLED1.SCL
  GND: Part1.GND, IC1.pin1, IC1.pin2, IC1.pin7, C1.0, RLOAD.Pin_0, VLOAD.GND, OLED1.GND
  3.3V: Part1.3V3, IC1.pin6, R1.Pin_1, R2.Pin_1, R3.Pin_1, C1.1, OLED1.3.3V
  VS: Part1.5V
  ALERT: IC1.pin3, R3.Pin_0
  N1: IC1.pin8, IC1.pin9, Rshunt.Pin_1, RLOAD.Pin_1
  N2: IC1.pin10, Rshunt.Pin_0, VLOAD.VCC
