# Fritzing sketch SprayBooth (saved by Fritzing 0.9.2b)
breadboards: 1

parts:
  12V = Power plug
  S1 = Toggle Switch [package=THT]
  LED1 = LEDs [part_number="cool white array x 36 (12V)" package=led-1206]
  LED2 = LEDs [part_number="warm white array x 18 (12V)" package=led-1206]
  FAN1 = DC Motor
  S2 = Toggle Switch [package=THT]

nets:
  GND: 12V.GND, S1.L2, S2.L2
  VCC: 12V.VCC, LED1.A, LED2.A, FAN1.pin_1
  N1: S1.COM, LED1.C, LED2.C
  N2: FAN1.pin_2, S2.COM
