# Fritzing sketch WaterLevelControlKit (saved by Fritzing 0.9.2b)
breadboards: 1

parts:
  J3 = Power plug
  IC1 = LM324 [package=dil16]
  U1 = RELAY [package=relay-t9a]
  Q1 = NPN-Transistor [part_number=S8050 package="TO92 [THT]"]
  Q2 = NPN-Transistor [part_number=S8050 package="TO92 [THT]"]
  D1 = Rectifier Diode [part_number=1N4148 package="300 mil [THT]"]
  D2 = Rectifier Diode [part_number=1N4148 package="300 mil [THT]"]
  D4 = Rectifier Diode [part_number=1N4148 package="300 mil [THT]"]
  D5 = Rectifier Diode [part_number=1N4148 package="300 mil [THT]"]
  D9 = Rectifier Diode [part_number=1N4007 package="300 mil [THT]"]
  R20 = Resistor [tolerance=±5% resistance=2.2k package=THT]
  D8 = LED - 5mm [color="Red (633nm)" package="5 mm [THT]"]
  S1 = SWITCH-DPDT [package=ayz0202]
  R21 = Resistor [tolerance=±5% resistance=10k package=THT]
  R22 = Resistor [tolerance=±5% resistance=10k package=THT]
  C6 = Electrolytic Capacitor [capacitance=100µF package="100 mil [THT, electrolytic]"]
  C5 = Ceramic Capacitor [capacitance=100nF package="100 mil [THT, multilayer]"]
  R19 = Resistor [tolerance=±5% resistance=47k package=THT]
  C2 = Ceramic Capacitor [capacitance=100nF package="100 mil [THT, multilayer]"]
  C4 = Ceramic Capacitor [capacitance=100nF package="100 mil [THT, multilayer]"]
  C3 = Ceramic Capacitor [capacitance=100nF package="100 mil [THT, multilayer]"]
  R4 = Resistor [tolerance=±5% resistance=1M package=THT]
  J2 = female pin header, 2 pins [form="♀ (female)"]
  C7 = Ceramic Capacitor [capacitance=100nF package="100 mil [THT, multilayer]"]
  C8 = Ceramic Capacitor [capacitance=100nF package="100 mil [THT, multilayer]"]
  J1 = female pin header, 2 pins [form="♀ (female)"]
  C9 = Ceramic Capacitor [capacitance=100nF package="100 mil [THT, multilayer]"]
  R13 = Resistor [tolerance=±5% resistance=1M package=THT]
  R2 = Resistor [tolerance=±5% resistance=47k package=THT]
  C1 = Ceramic Capacitor [capacitance=22nF package="100 mil [THT, multilayer]"]
  R3 = Resistor [tolerance=±5% resistance=47k package=THT]
  R1 = Resistor [tolerance=±5% resistance=47k package=THT]
  R12 = Resistor [tolerance=±5% resistance=47k package=THT]
  R10 = Resistor [tolerance=±5% resistance=4.7k package=THT]
  R11 = Resistor [tolerance=±5% resistance=2.2k package=THT]
  C10 = Electrolytic Capacitor [capacitance=10µF package="100 mil [THT, electrolytic]"]
  R5 = Resistor [tolerance=±5% resistance=1k package=THT]
  R14 = Resistor [tolerance=±5% resistance=1k package=THT]
  R18 = Resistor [tolerance=±5% resistance=47k package=THT]
  D3 = LED - 5mm [color="Green (570nm)" package="5 mm [THT]"]
  R7 = Resistor [tolerance=±5% resistance=220 package=THT]
  R6 = Resistor [tolerance=±5% resistance=100k package=THT]
  R9 = Resistor [tolerance=±5% resistance=1k package=THT]
  D7 = LED - 5mm [color="Yellow (595nm)" package="5 mm [THT]"]
  R17 = Resistor [tolerance=±5% resistance=2.2k package=THT]
  D6 = LED - 5mm [color="Red (633nm)" package="5 mm [THT]"]
  R15 = Resistor [tolerance=±5% resistance=100k package=THT]
  R8 = Resistor [tolerance=±5% resistance=47k package=THT]
  R16 = Resistor [tolerance=±5% resistance=47k package=THT]

nets:
  GND: J3.GND, IC1.GND, Q1.E, Q2.E, D1.anode, D4.anode, C6.-, C5.0, C4.0, R4.Pin_1, C9.0, R13.Pin_1, C1.0, R12.Pin_1, R11.Pin_0, C10.-, D6.cathode
  5V: J3.VCC, IC1.V+, U1.COIL1, D9.cathode, R20.Pin_1, R22.Pin_0, C6.+, C5.1, R1.Pin_1, R10.Pin_0, D3.anode
  SIG: IC1.OUT1, C3.0, C8.0, R2.Pin_0, R3.Pin_0
  IN1-: IC1.IN1-, R2.Pin_1, C1.1
  IN1+: IC1.IN1+, R3.Pin_1, R1.Pin_0, R12.Pin_0
  IN2+: IC1.IN2+, R5.Pin_0, R6.Pin_0
  IN2-: IC1.IN2-, D2.cathode, C4.1, R4.Pin_0
  OUT2: IC1.OUT2, R7.Pin_1, R6.Pin_1, R9.Pin_0, R8.Pin_0
  OUT3: IC1.OUT3, D7.cathode, R17.Pin_0, R15.Pin_1, R16.Pin_0
  IN3-: IC1.IN3-, D5.cathode, C9.1, R13.Pin_0
  IN3+: IC1.IN3+, R14.Pin_0, R15.Pin_0
  IN4+: IC1.IN4+, R19.Pin_1, R18.Pin_1
  VIN: IC1.IN4-, R8.Pin_1, R16.Pin_1
  N1: IC1.OUT4, R21.Pin_0, R19.Pin_0
  N2: U1.COIL2, Q2.C, D9.anode, D8.cathode
  N3: Q1.B, S1.3
  N4: Q1.C, S1.6, R22.Pin_1
  N5: Q2.B, S1.1, S1.5
  N6: D1.cathode, D2.anode, C2.1
  N7: D4.cathode, D5.anode, C7.1
  N8: R20.Pin_0, D8.anode
  RESULT: S1.2, R21.Pin_1
  N9: C2.0, J2.pin2
  N10: C3.1, J2.pin1
  N11: C7.0, J1.pin2
  N12: C8.1, J1.pin1
  VREF: R10.Pin_1, R11.Pin_1, C10.+, R5.Pin_1, R14.Pin_1, R18.Pin_0
  N13: D3.cathode, R7.Pin_0
  N14: R9.Pin_1, D7.anode
  N15: R17.Pin_1, D6.anode

custom parts:
  LM324: LM324 Quad OpAmp
