# Fritzing sketch hp-torch-laser (saved by Fritzing 1.0.1rc)
breadboards: 1

parts:
  Part1 = LilyPad Coin Cell Battery Holder
  S1 = Pushbutton [package="[THT]"]
  LED = LED - 5mm [color="White (8000K)" current=0.030A package="5 mm [THT]"]
  R1 = Resistor [tolerance=±5% power=0.25W resistance=60 package=THT]
  R2 = Resistor [tolerance=±5% power=0.25W resistance=180 package=THT]
  LASER = LED - 5mm [color="Red (633nm)" current=0.030A package="5 mm [THT]"]
  S2 = Pushbutton [package="[THT]"]

nets:
  GND: Part1.-, LED.cathode, R2.Pin_0
  3V: Part1.+, R1.Pin_0, S2.Pin_3, S2.Pin_4
  N1: S1.Pin_1, S1.Pin_2, LED.anode
  N2: S1.Pin_3, S1.Pin_4, R1.Pin_1
  N3: R2.Pin_1, LASER.cathode
  N4: LASER.anode, S2.Pin_1, S2.Pin_2
