# Fritzing sketch FretBoard (saved by Fritzing 0.9.0b)

parts:
  5V2A = Power plug
  LEDARRAY1 = Neopixel Strip -- White (30/m)
  R1 = Resistor [tolerance=±5% resistance=1k package=THT]
  C1 = Electrolytic Capacitor [capacitance=1mF package="100 mil [THT, electrolytic]"]
  Part3 = Arduino Ethernet Shield (Rev3)

nets:
  GND: 5V2A.GND, LEDARRAY1.GND, C1.-, Part3.GND
  VCC: 5V2A.VCC, LEDARRAY1.+5V, C1.+, Part3.5V
  N1: LEDARRAY1.DI, R1.Pin_0
  N2: R1.Pin_1, Part3.PWM_D6

notes:
  (or other)

custom parts:
  Neopixel Strip -- White (30/m): Neopixel Strip, White, 30 pixels per meter.
