# Fritzing sketch cuttle_blinky_example (saved by Fritzing 0.9.2b)
breadboards: 1

parts:
  B1 = TheCuttle
  R1 = Resistor [tolerance=±5% resistance=220 package=THT]
  LED1 = LED - 5mm [color="Red (633nm)" package="5 mm [THT]"]

nets:
  N1: B1.D13, R1.Pin_0
  GND: B1.GND#21, LED1.cathode
  N2: R1.Pin_1, LED1.anode

custom parts:
  TheCuttle: Boldport Cuttle Arduino-compatible Atmega328-based board
