# Fritzing sketch Girabot (saved by Fritzing 0.9.0b)
breadboards: 2

parts:
  R1 = Photocell (LDR) [package=THT]
  R3 = Resistor [tolerance=±5% resistance=4.7k package=THT]
  R4 = Resistor [tolerance=±5% resistance=4.7k package=THT]
  R5 = Resistor [tolerance=±5% resistance=1k package=THT]
  R2 = Trimmer Potentiometer [maximum_resistance=20kΩ package=THT]
  R6 = Resistor [tolerance=±5% resistance=1k package=THT]
  R7 = Photocell (LDR) [package=THT]
  R8 = Trimmer Potentiometer [maximum_resistance=20kΩ package=THT]
  R9 = Resistor [tolerance=±5% resistance=4.7k package=THT]
  R10 = Resistor [tolerance=±5% resistance=4.7k package=THT]
  IC2 = LM324 [package=dil16]
  Part2 = Arduino Nano (Rev3.0)
  Battery = Battery block 9V
  LED2 = LED - 3mm [color="Green (570nm)" package="3 mm [THT]"]
  LED1 = LED - 3mm [color="Red (633nm)" package="3 mm [THT]"]
  IC1 = Voltage Regulator - 5V [package="DPak [SMD]"]
  C1 = Electrolytic Capacitor [capacitance=100µF package="100 mil [THT, electrolytic]"]
  C2 = Ceramic Capacitor [capacitance=100nF package="100 mil [THT, multilayer]"]
  S1 = SPST Switch [package=switch-spdt_kit]
  IC3 = LM386 [part_number=LM386 package=dip08]
  J1 = Piezo Speaker
  C3 = Ceramic Capacitor [capacitance=100nF package="100 mil [THT, multilayer]"]
  C4 = Electrolytic Capacitor [capacitance=100µF package="100 mil [THT, electrolytic]"]
  R11 = Resistor [tolerance=±5% resistance=22k package=THT]
  R12 = Resistor [tolerance=±5% resistance=22k package=THT]
  R13 = Resistor [tolerance=±5% resistance=100k package=THT]
  MIC1 = Microphone
  R14 = Resistor [tolerance=±5% resistance=10k package=THT]
  C5 = Electrolytic Capacitor [capacitance=1µF package="100 mil [THT, electrolytic]"]
  R15 = Resistor [tolerance=±5% resistance=2.2k package=THT]
  J2 = Basic Servo
  C6 = Ceramic Capacitor [capacitance=10nF package="100 mil [THT, multilayer]"]
  C7 = Ceramic Capacitor [capacitance=10nF package="100 mil [THT, multilayer]"]
  C8 = Ceramic Capacitor [capacitance=10nF package="100 mil [THT, multilayer]"]
  R16 = Trimmer Potentiometer [maximum_resistance=200kΩ package=THT]

nets:
  LDR_ENABLE: R1.pin_0, R2.leg2, R7.pin_0, R8.leg2, Part2.D9
  N1: R1.pin_1, R4.Pin_0, IC2.IN2-
  N2: R3.Pin_0, R2.wiper, IC2.IN2+
  GND: R3.Pin_1, R4.Pin_1, R9.Pin_1, R10.Pin_1, IC2.GND, Part2.GND, Battery.-, LED2.cathode, LED1.cathode, IC1.GND, C1.-, C2.0, IC3.+IN, IC3.V-, J1.pin1, R11.Pin_0, MIC1.pin1, J2.gnd, C6.0, C7.0, C8.1
  LDR2OUT: R5.Pin_0, IC2.OUT2, Part2.D8
  N3: R5.Pin_1, LED1.anode
  LDR1OUT: R6.Pin_0, IC2.OUT1, Part2.D7
  N4: R6.Pin_1, LED2.anode
  N5: R7.pin_1, R10.Pin_0, IC2.IN1-
  N6: R8.wiper, R9.Pin_0, IC2.IN1+
  Vcc(5): IC2.V+, Part2.5V, IC1.output_voltage, C2.1, R12.Pin_0, R14.Pin_1, J2.vcc, C6.1, C8.0
  MIC_AMP_OUT: IC2.OUT3, Part2.A0, R13.Pin_0
  MIC_IN(-): IC2.IN3-, R15.Pin_1, R16.leg2
  MIC_IN(+): IC2.IN3+, R11.Pin_1, R12.Pin_1
  AUDIO_OUT: Part2.D6, C3.0
  MOTOR_CONTROL: Part2.D11/MOSI, J2.pulse
  N7: Battery.+, S1.P
  Vcc(9): IC1.input_voltage, C1.+, S1.S, IC3.V+, C7.1
  N8: IC3.-IN, C3.1
  N9: IC3.OUT, C4.+
  N10: J1.pin2, C4.-
  N11: R13.Pin_1, R16.wiper
  N12: MIC1.pin2, R14.Pin_0, C5.+
  N13: C5.-, R15.Pin_0

notes:
  Power Supply
  LDR bridges (2)
  9V unregulated rail + GND
  5V regulated rail + GND
  Speaker Subsystem
  Microphone Input
  Motor Drive Subsystem

custom parts:
  LM324: LM324 Quad OpAmp
