# Fritzing sketch Vivian (saved by Fritzing 0.9.2b)
breadboards: 1

parts:
  Q1 = PNP-Transistor [part_number=2N3906 package="TO92 [THT]"]
  Q2 = NPN-Transistor [part_number=2N3904 package="TO92 [THT]"]
  R1 = Resistor [tolerance=±5% resistance=2.2k package=THT]
  FLED1 = LED - 5mm [color="Red (633nm)" package="5 mm [THT]"]
  FLED2 = LED - 5mm [color="Red (633nm)" package="5 mm [THT]"]
  M1 = DC Motor
  C1 = Electrolytic Capacitor [capacitance=3.3mF package="100 mil [THT, electrolytic]"]
  C2 = Electrolytic Capacitor [capacitance=3.3mF package="100 mil [THT, electrolytic]"]
  C3 = Electrolytic Capacitor [capacitance=3.3mF package="100 mil [THT, electrolytic]"]
  D1 = Rectifier Diode [part_number=1N5711 package="300 mil [THT]"]
  L1 = Inductor [inductance=2.2mH package="400 mil [THT]"]
  IC1 = IC, DIP package, 4 pins [chip_label=IC part_number=QX5252]
  PVC1 = SOLAR-IXYS [package=solarbit-12x1]

nets:
  N1: Q1.E, M1.pin_1, C1.+, C2.+, C3.+, D1.cathode
  N2: Q1.B, R1.Pin_0, FLED1.anode, FLED2.anode
  N3: Q1.C, Q2.B
  GND: Q2.E, FLED1.cathode, FLED2.cathode, C1.-, C2.-, C3.-, IC1.pin3, PVC1.A
  N4: Q2.C, R1.Pin_1, M1.pin_2
  N5: D1.anode, L1.pin_1, IC1.pin4
  N6: L1.pin_0, IC1.pin2, PVC1.C
