# Fritzing sketch ElectroMechanicalClockMechanism (saved by Fritzing 1.0.1rc)
breadboards: 1

parts:
  Q1 = NPN-Transistor [part_number=2N3904 package="TO92 [THT]"]
  R1 = Resistor [tolerance=±5% power=0.25W resistance=1k package=THT]
  R2 = Resistor [tolerance=±5% power=0.25W resistance=10k package=THT]
  CLOCK = female pin header, 3 pins [form="♀ (female)"]
  U1 = IC, DIP package, 16 pins [chip_label=CD4017 part_number=CD4017]
  LED1 = LED - 3mm [color="Red (633nm)" current=0.030A package="3 mm [THT]"]
  R3 = Resistor [tolerance=±5% power=0.25W resistance=1k package=THT]
  BAT1 = Battery Holders [package=battery-aaa]
  BAT2 = Battery Holders [package=battery-aaa]

nets:
  GND: Q1.E, CLOCK.pin3, U1.pin8, U1.pin13, R3.Pin_0, BAT1.-
  N1: Q1.B, R1.Pin_1
  CLK: Q1.C, R2.Pin_1, U1.pin14
  8Hz Pulse: R1.Pin_0, CLOCK.pin2
  3V: R2.Pin_0, U1.pin16, BAT2.+
  1.5V: CLOCK.pin1, BAT1.+, BAT2.-
  1Hz Pulse: U1.pin3, LED1.anode
  N2: U1.pin9, U1.pin15
  N3: LED1.cathode, R3.Pin_1

notes:
  Clock Mechanism
