# Fritzing sketch HomopolarJouleThiefBlinky (saved by Fritzing 0.9.2b)
breadboards: 1

parts:
  L1 = Inductor [package="400 mil [THT]"]
  C1 = Electrolytic Capacitor [capacitance=10µF package="100 mil [THT, electrolytic]"]
  D1 = Rectifier Diode [part_number=1N5819 package="300 mil [THT]"]
  1_5V = Battery
  LED1 = smd LED [color="White (8000K)" package="0805 [SMD]"]

nets:
  N1: L1.pin_0, C1.-, 1_5V.+, LED1.cathode
  N2: L1.pin_1, D1.anode, 1_5V.-
  N3: C1.+, D1.cathode, LED1.anode

notes:
  battery connection high frequency make/break
