# Fritzing sketch NanoLev (saved by Fritzing 1.0.7)
breadboards: 1

parts:
  Part1 = Arduino Nano (Rev3.0) (ICSP)
  TCT40-16-T1 = female pin header, 2 pins [form="♀ (female)"]
  TCT40-16-T2 = female pin header, 2 pins [form="♀ (female)"]

nets:
  GND: Part1.GND
  T2-: Part1.A3, TCT40-16-T2.pin2
  T2+: Part1.A2, TCT40-16-T2.pin1
  T1-: Part1.A1, TCT40-16-T1.pin2
  T1+: Part1.A0, TCT40-16-T1.pin1

notes:
  TCT40-16 T1
  TCT40-16 T2
