# Fritzing sketch UltrasonicLevitatorKit (saved by Fritzing 1.0.7)
breadboards: 1

parts:
  J1 = Power plug
  C3 = Electrolytic Capacitor [capacitance=100µF voltage=35V package="100 mil [THT, electrolytic]"]
  U3 = IC, DIP package, 8 pins [chip_label=TC4427]
  U2 = IC, DIP package, 8 pins [chip_label=STC15F104W]
  C2 = Ceramic Capacitor [capacitance=100nF voltage=35V package="100 mil [THT, multilayer]"]
  C1 = Ceramic Capacitor [capacitance=100nF voltage=35V package="100 mil [THT, multilayer]"]
  U1 = V_REG_LD1117VXX [package=78xxl]
  R1 = Resistor [tolerance=±5% power=0.25W resistance=4.7k package=THT]
  LED1 = LED - 3mm [color="Red (633nm)" current=0.030A package="3 mm [THT]"]
  J3 = female pin header, 2 pins [form="♀ (female)"]
  J4 = female pin header, 2 pins [form="♀ (female)"]
  J2 = female pin header, 4 pins [form="♀ (female)"]

nets:
  GND: J1.GND, C3.-, U3.pin3, U2.pin4, C2.1, C1.1, U1.GND, J2.pin4
  VIN: J1.VCC, C3.+, U3.pin6, C2.0, U1.IN
  P3.2: U3.pin2, U2.pin7
  P3.3: U3.pin4, U2.pin8
  OUTB: U3.pin5, J3.pin2, J4.pin2
  OUTA: U3.pin7, J3.pin1, J4.pin1
  P3.4: U2.pin1, LED1.cathode
  VOUT: U2.pin2, C1.0, U1.OUT, R1.Pin_0, J2.pin1
  P3.0: U2.pin5, J2.pin2
  P3.1: U2.pin6, J2.pin3
  N1: R1.Pin_1, LED1.anode

notes:
  sensors
  Debug Header
