# Fritzing sketch LineFollowerKit (saved by Fritzing 0.9.2b)
breadboards: 1

parts:
  IC1 = LM393 [part_number=LM358 package=so08]
  BATTERY = Battery
  S1 = Toggle Switch [package=THT]
  R1 = Trimmer Potentiometer [maximum_resistance=10kΩ package=THT]
  R2 = Trimmer Potentiometer [maximum_resistance=10kΩ package=THT]
  R5 = Resistor [tolerance=±5% resistance=51 package=THT]
  C1 = Electrolytic Capacitor [capacitance=100µF package="100 mil [THT, electrolytic]"]
  D1 = LED - 5mm [color="Red (633nm)" package="5 mm [THT]"]
  D4 = LED - 5mm [color="Red (633nm)" package="5 mm [THT]"]
  R7 = Resistor [tolerance=±5% resistance=1k package=THT]
  R13 = Photocell (LDR) [package=THT]
  D5 = LED - 5mm [color="Red (633nm)" package="5 mm [THT]"]
  C2 = Electrolytic Capacitor [capacitance=100µF package="100 mil [THT, electrolytic]"]
  R6 = Resistor [tolerance=±5% resistance=51 package=THT]
  R8 = Resistor [tolerance=±5% resistance=1k package=THT]
  R14 = Photocell (LDR) [package=THT]
  Q1 = PNP-Transistor [part_number=S8550 package="TO92 [THT]"]
  Q2 = PNP-Transistor [part_number=S8550 package="TO92 [THT]"]
  R9 = Resistor [tolerance=±5% resistance=10 package=THT]
  R10 = Resistor [tolerance=±5% resistance=10 package=THT]
  M1 = DC Motor
  R11 = Resistor [tolerance=±5% resistance=51 package=THT]
  M2 = DC Motor
  D2 = LED - 5mm [color="Red (633nm)" package="5 mm [THT]"]
  R12 = Resistor [tolerance=±5% resistance=51 package=THT]

nets:
  N1: IC1.G1_OUT, R9.Pin_1
  N2: IC1.G1_-IN, IC1.G2_+IN, R2.leg2, R8.Pin_0
  N3: IC1.G1_+IN, IC1.G2_-IN, R1.leg2, R7.Pin_0
  GND: IC1.G1_V-, S1.L2, C1.-, D1.cathode, D4.cathode, R13.pin_1, D5.cathode, C2.-, R14.pin_1, M1.pin_2, M2.pin_2, D2.cathode
  N4: IC1.G2_OUT, R10.Pin_1
  VCC: IC1.G1_V+, BATTERY.+, R1.leg1, R1.wiper, R2.leg1, R2.wiper, R5.Pin_0, R6.Pin_0, Q1.E, Q2.E
  N5: BATTERY.-, S1.COM
  N6: R5.Pin_1, C1.+, D4.anode
  N7: D1.anode, R11.Pin_1
  N8: R7.Pin_1, R13.pin_0
  N9: D5.anode, C2.+, R6.Pin_1
  N10: R8.Pin_1, R14.pin_0
  N11: Q1.B, R9.Pin_0
  N12: Q1.C, M1.pin_1, R11.Pin_0
  N13: Q2.B, R10.Pin_0
  N14: Q2.C, M2.pin_1, R12.Pin_0
  N15: D2.anode, R12.Pin_1
