# Fritzing sketch JoystickServoControl (saved by Fritzing 0.9.0b)
breadboards: 1

parts:
  Part1 = Arduino Uno (Rev3)
  5V_DC = Power plug
  J1 = Basic Servo
  J2 = Basic Servo
  Part2 = Thumb Joystick

nets:
  N1: Part1.A0, Part2.HORZ
  N2: Part1.A1, Part2.VERT
  N3: Part1.D9_PWM, J2.pulse
  N4: Part1.D10_PWM/SS, J1.pulse
  GND: Part1.GND, 5V_DC.GND, J1.gnd, J2.gnd, Part2.GND
  5V: Part1.5V, Part2.VCC
  VCC: 5V_DC.VCC, J1.vcc, J2.vcc
