# Fritzing sketch LowPowerMiniServos (saved by Fritzing 0.9.2b)
breadboards: 1

parts:
  Part1 = Arduino Uno (Rev3)
  2_8-4_2V = Power plug
  J1 = Basic Servo
  Q1 = Basic FET N-Channel [package="TO220 [THT]"]
  R1 = Resistor [tolerance=±5% resistance=10k package=THT]
  R2 = Resistor [tolerance=±5% resistance=10k package=THT]

nets:
  SERVO_PWM: Part1.D9_PWM, Q1.drain, R1.Pin_1
  HV: Part1.5V, R1.Pin_0
  GND: Part1.GND, 2_8-4_2V.GND, J1.gnd
  LV: 2_8-4_2V.VCC, J1.vcc, Q1.gate, R2.Pin_0
  N1: J1.pulse, Q1.source, R2.Pin_1
