# Fritzing sketch MiniLinearServos (saved by Fritzing 0.9.2b)
breadboards: 1

parts:
  U2 = attiny85 [package=dip]
  5V = Power plug
  J1 = Basic Servo
  C1 = Ceramic Capacitor [capacitance=100nF package="100 mil [THT, multilayer]"]

nets:
  N1: U2.Pin_3, J1.pulse
  GND: U2.Pin_4, 5V.GND, J1.gnd, C1.1
  VCC: U2.Pin_8, 5V.VCC, J1.vcc, C1.0

notes:
  Linear servo
