# Fritzing sketch ServoTest (saved by Fritzing 0.9.0b)
breadboards: 1

parts:
  5V = 4 x AAA Battery Mount
  Part1 = Arduino Uno (Rev3)
  J1 = Basic Servo

nets:
  GND: 5V.-, Part1.GND, J1.gnd
  N1: 5V.+, J1.vcc
  N2: Part1.D9_PWM, J1.pulse
