# Fritzing sketch SolenoidMotor (saved by Fritzing 0.9.2b)
breadboards: 1

parts:
  L1 = Solenoid
  D1 = Rectifier Diode [part_number=1N4001 package="300 mil [THT]"]
  R1 = Resistor [tolerance=±5% resistance=1k package=THT]
  9-12V = Battery block 9V
  S1 = Reed switch [package=THT]
  LED1 = LED - 5mm [color="Blue (525nm)" package="5 mm [THT]"]

nets:
  N1: L1.pin1, D1.anode, R1.Pin_0, S1.pin_1
  N2: L1.pin2, D1.cathode, 9-12V.+, LED1.anode
  N3: R1.Pin_1, LED1.cathode
  N4: 9-12V.-, S1.pin_2
