# Fritzing sketch SimpleHBridge (saved by Fritzing 0.9.2b)
breadboards: 1

parts:
  Part1 = Arduino Uno (Rev3)
  M1 = Stepper Motor - Bipolar
  Q1 = 2N7000 FET N-Channel [part_number=2N7000 package=TO92]
  5V = Power plug
  S1 = Pushbutton [package="[THT]"]
  S2 = Pushbutton [package="[THT]"]
  S3 = Pushbutton [package="[THT]"]
  S4 = Pushbutton [package="[THT]"]
  Q2 = 2N7000 FET N-Channel [part_number=2N7000 package=TO92]
  Q3 = 2N7000 FET N-Channel [part_number=2N7000 package=TO92]
  Q4 = 2N7000 FET N-Channel [part_number=2N7000 package=TO92]
  Q5 = 2N7000 FET N-Channel [part_number=2N7000 package=TO92]
  Q6 = 2N7000 FET N-Channel [part_number=2N7000 package=TO92]
  Q7 = 2N7000 FET N-Channel [part_number=2N7000 package=TO92]
  Q8 = 2N7000 FET N-Channel [part_number=2N7000 package=TO92]
  R1 = Resistor [tolerance=±5% resistance=10k package=THT]
  R2 = Resistor [tolerance=±5% resistance=10k package=THT]
  R3 = Resistor [tolerance=±5% resistance=10k package=THT]
  R4 = Resistor [tolerance=±5% resistance=10k package=THT]
  R5 = Resistor [tolerance=±5% resistance=10k package=THT]
  R6 = Resistor [tolerance=±5% resistance=10k package=THT]
  R7 = Resistor [tolerance=±5% resistance=10k package=THT]
  R8 = Resistor [tolerance=±5% resistance=10k package=THT]
  D1 = Rectifier Diode [part_number=1N4007 package="300 mil [THT]"]
  D2 = Rectifier Diode [part_number=1N4001 package="300 mil [THT]"]
  D3 = Rectifier Diode [part_number=1N4007 package="300 mil [THT]"]
  D4 = Rectifier Diode [part_number=1N4001 package="300 mil [THT]"]
  D5 = Rectifier Diode [part_number=1N4007 package="300 mil [THT]"]
  D6 = Rectifier Diode [part_number=1N4001 package="300 mil [THT]"]
  D7 = Rectifier Diode [part_number=1N4007 package="300 mil [THT]"]
  D8 = Rectifier Diode [part_number=1N4001 package="300 mil [THT]"]

nets:
  CTL1: Part1.D8, S4.Pin_3, S4.Pin_4, Q6.gate, Q7.gate, R6.Pin_1, R7.Pin_1
  CTL2: Part1.D9_PWM, S3.Pin_3, S3.Pin_4, Q5.gate, Q8.gate, R5.Pin_1, R8.Pin_1
  CTL3: Part1.D10_PWM/SS, S2.Pin_1, S2.Pin_2, Q2.gate, Q3.gate, R2.Pin_1, R3.Pin_1
  CTL4: Part1.D11_PWM/MOSI, Q1.gate, S1.Pin_1, S1.Pin_2, Q4.gate, R1.Pin_1, R4.Pin_1
  GND: Part1.GND, 5V.GND, Q2.source, Q4.source, Q6.source, Q8.source, R1.Pin_0, R2.Pin_0, R3.Pin_0, R4.Pin_0, R5.Pin_0, R6.Pin_0, R7.Pin_0, R8.Pin_0, D2.anode, D4.anode, D6.anode, D8.anode
  N1: M1.A, Q1.source, Q2.drain, D1.anode, D2.cathode
  N2: M1.C, Q3.source, Q4.drain, D3.anode, D4.cathode
  N3: M1.B, Q5.source, Q6.drain, D5.anode, D6.cathode
  N4: M1.D, Q7.source, Q8.drain, D7.anode, D8.cathode
  VBAT: Q1.drain, 5V.VCC, S1.Pin_3, S1.Pin_4, S2.Pin_3, S2.Pin_4, S3.Pin_1, S3.Pin_2, S4.Pin_1, S4.Pin_2, Q3.drain, Q5.drain, Q7.drain, D1.cathode, D3.cathode, D5.cathode, D7.cathode

custom parts:
  2N7000 FET N-Channel: A 2N7000 MOSFET N-Channel Transistor
