# Fritzing sketch ULN2003Module (saved by Fritzing 0.9.2b)
breadboards: 1

parts:
  IC1 = ULN2003A [package="DIP16 [THT]"]
  5-12V = Power plug
  C1 = Ceramic Capacitor [capacitance=100nF package="100 mil [THT, multilayer]"]
  J3-POWER = female pin header, 2 pins [form="♀ (female)"]
  J2-OUT = female pin header, 5 pins [form="♀ (female)"]
  R1 = Resistor [tolerance=±5% resistance=470 package=THT]
  R2 = Resistor [tolerance=±5% resistance=470 package=THT]
  R3 = Resistor [tolerance=±5% resistance=470 package=THT]
  R4 = Resistor [tolerance=±5% resistance=470 package=THT]
  LED1 = LED - 3mm [color="Red (633nm)" package="3 mm [THT]"]
  LED2 = LED - 3mm [color="Red (633nm)" package="3 mm [THT]"]
  LED3 = LED - 3mm [color="Red (633nm)" package="3 mm [THT]"]
  LED4 = LED - 3mm [color="Red (633nm)" package="3 mm [THT]"]
  J1-IN = female pin header, 4 pins [form="♀ (female)"]

nets:
  N1: IC1.In_1, J1-IN.pin1
  N2: IC1.In_2, J1-IN.pin2
  N3: IC1.In_3, J1-IN.pin3
  N4: IC1.In_4, J1-IN.pin4
  N5: IC1.0V, 5-12V.GND, C1.1
  N6: IC1.COM_-_Common, 5-12V.VCC, C1.0, J3-POWER.pin1
  N7: IC1.Out_4, J2-OUT.pin4, LED4.cathode
  N8: IC1.Out_3, J2-OUT.pin3, LED3.cathode
  N9: IC1.Out_2, J2-OUT.pin2, LED2.cathode
  N10: IC1.Out_1, J2-OUT.pin1, LED1.cathode
  N11: J3-POWER.pin2, J2-OUT.pin5, R1.Pin_0, R2.Pin_0, R3.Pin_0, R4.Pin_0
  N12: R1.Pin_1, LED1.anode
  N13: R2.Pin_1, LED2.anode
  N14: R3.Pin_1, LED3.anode
  N15: R4.Pin_1, LED4.anode
