# Fritzing sketch LiteWings (saved by Fritzing 0.9.2b)
breadboards: 1

parts:
  VCC1 = Battery
  LED1 = smd LED [color="White (4500K)" package="0805 [SMD]"]
  R1 = Resistor [tolerance=±5% resistance=50 package=THT]
  R2 = Resistor [tolerance=±5% resistance=50 package=THT]

nets:
  N1: VCC1.-, R1.Pin_0
  N2: VCC1.+, R2.Pin_0
  N3: LED1.cathode, R1.Pin_1
  N4: LED1.anode, R2.Pin_1
