# Fritzing sketch Concorde (saved by Fritzing 0.9.2b)
breadboards: 1

parts:
  12V = Power plug
  R1 = Resistor [tolerance=±5% resistance=560 package=THT]
  LED1 = LED - 5mm [color="Red (633nm)" package="5 mm [THT]"]
  LED2 = LED - 5mm [color="Red (633nm)" package="5 mm [THT]"]
  R2 = Resistor [tolerance=±5% resistance=560 package=THT]
  LED3 = LED - 5mm [color="Red (633nm)" package="5 mm [THT]"]
  LED4 = LED - 5mm [color="Red (633nm)" package="5 mm [THT]"]
  12V_White_LED_Strip = Neopixel Strip -- White (30/m)

nets:
  GND: 12V.GND, R1.Pin_0, R2.Pin_0, 12V_White_LED_Strip.GND
  VCC: 12V.VCC, LED1.anode, LED3.anode, 12V_White_LED_Strip.+5V
  N1: R1.Pin_1, LED2.cathode
  N2: LED1.cathode, LED2.anode
  N3: R2.Pin_1, LED4.cathode
  N4: LED3.cathode, LED4.anode

notes:
  12V Daylight White LED Strip

custom parts:
  Neopixel Strip -- White (30/m): These NeoPixel strips have 30 digitally-addressable pixel LEDs per meter and are very affordable and are only 12.5 mm wide, 10 mm if you remove the strip from the casing.
