# Fritzing sketch Firefly (saved by Fritzing 0.9.2b)
breadboards: 1

parts:
  U2 = attiny85 [package=dip]
  5V = Power plug
  C1 = Ceramic Capacitor [capacitance=100nF package="100 mil [THT, multilayer]"]
  MIC1 = Microphone
  R1 = Resistor [tolerance=±5% resistance=470 package=THT]
  LED1 = LED - 3mm [color="Red (633nm)" package="3 mm [THT]"]
  U3 = TL072/TLE2072 Dual Op. Amp [part_number=TL072 package="DIP8 [THT]"]
  R3 = Resistor [tolerance=±5% resistance=10k package=THT]
  R4 = Resistor [tolerance=±5% resistance=2.2k package=THT]
  R5 = Resistor [tolerance=±5% resistance=1M package=THT]
  C2 = Ceramic Capacitor [capacitance=100nF package="100 mil [THT, multilayer]"]
  C3 = Ceramic Capacitor [capacitance=100nF package="100 mil [THT, multilayer]"]
  D1 = Rectifier Diode [part_number=1N4001 package="300 mil [THT]"]
  R6 = Resistor [tolerance=±5% resistance=68k package=THT]

nets:
  N1: U2.Pin_3, R1.Pin_0
  GND: U2.Pin_4, 5V.GND, C1.1, MIC1.pin1, LED1.cathode, U3.Pin_4, U3.Pin_5, C3.0, D1.cathode
  N2: U2.Pin_5, U3.Pin_7, R5.Pin_1, C3.1
  N3: U2.Pin_6, D1.anode, R6.Pin_1
  VCC: U2.Pin_8, 5V.VCC, C1.0, U3.Pin_8, R3.Pin_0, R6.Pin_0
  N4: MIC1.pin2, R3.Pin_1, C2.1
  N5: R1.Pin_1, LED1.anode
  N6: U3.Pin_6, R4.Pin_1, R5.Pin_0
  N7: R4.Pin_0, C2.0

custom parts:
  TL072/TLE2072 Dual Op. Amp: The classic LM 358 Dual Operational Amplifier (Op-Amp). The analog swiss-army knife.
