# Fritzing sketch GlowBall (saved by Fritzing 0.9.2b)
breadboards: 2

parts:
  U1 = LM 358 Dual Op-Amp [part_number=LM358 package="SO 08 [SMD]"]
  R4 = Resistor [tolerance=±5% resistance=100k package=THT]
  R7 = Resistor [tolerance=±5% resistance=47k package=THT]
  VR1 = Trimmer Potentiometer [maximum_resistance=100kΩ package=THT]
  C1 = Electrolytic Capacitor [capacitance=100µF package="100 mil [THT, electrolytic]"]
  R1 = Resistor [tolerance=±5% resistance=22k package=THT]
  12V = Power plug
  U2 = LM 358 Dual Op-Amp [part_number=LM358 package="SO 08 [SMD]"]
  R5 = Resistor [tolerance=±5% resistance=100k package=THT]
  R8 = Resistor [tolerance=±5% resistance=47k package=THT]
  C2 = Electrolytic Capacitor [capacitance=100µF package="100 mil [THT, electrolytic]"]
  R2 = Resistor [tolerance=±5% resistance=22k package=THT]
  U3 = LM 358 Dual Op-Amp [part_number=LM358 package="SO 08 [SMD]"]
  R6 = Resistor [tolerance=±5% resistance=100k package=THT]
  R9 = Resistor [tolerance=±5% resistance=47k package=THT]
  C3 = Electrolytic Capacitor [capacitance=100µF package="100 mil [THT, electrolytic]"]
  R3 = Resistor [tolerance=±5% resistance=22k package=THT]
  Q3 = PNP-Transistor [part_number=2N3906 package="TO92 [THT]"]
  Q2 = PNP-Transistor [part_number=2N3906 package="TO92 [THT]"]
  Q1 = PNP-Transistor [part_number=2N3906 package="TO92 [THT]"]
  LED1 = RGB LED - (4 legs) [package="5 mm [THT]"]
  R12 = Resistor [tolerance=±5% resistance=10k package=THT]
  R11 = Resistor [tolerance=±5% resistance=10k package=THT]
  R10 = Resistor [tolerance=±5% resistance=10k package=THT]
  R15 = Resistor [tolerance=±5% resistance=360 package=THT]
  R14 = Resistor [tolerance=±5% resistance=360 package=THT]
  R13 = Resistor [tolerance=±5% resistance=360 package=THT]
  S1 = Toggle Switch [package=THT]
  LED2 = RGB LED - (4 legs) [package="5 mm [THT]"]
  LED3 = RGB LED - (4 legs) [package="5 mm [THT]"]
  Q4 = PNP-Transistor [part_number=2N3906 package="TO92 [THT]"]
  VR2 = Trimmer Potentiometer [maximum_resistance=1kΩ package=THT]
  R16 = Resistor [tolerance=±5% resistance=10k package=THT]
  C4 = Electrolytic Capacitor [capacitance=100µF package="100 mil [THT, electrolytic]"]
  C5 = Ceramic Capacitor [capacitance=100nF package="100 mil [THT, multilayer]"]
  R20 = Resistor [tolerance=±5% resistance=1 package=THT]
  R19 = Resistor [tolerance=±5% resistance=1 package=THT]
  R18 = Resistor [tolerance=±5% resistance=1 package=THT]
  R17 = Resistor [tolerance=±5% resistance=1 package=THT]
  Q5 = NPN-Transistor [part_number=A42 package="TO92 [THT]"]
  D1 = Schottky Diode [part_number=1N5711 package="300 mil [THT]"]
  NEOPIXEL1 = Neopixel Strip -- White (60/m)

nets:
  OSCG: U1.connector0, R7.Pin_1, C1.+, R11.Pin_0
  N1: U1.connector1, C1.-, R1.Pin_1
  VREF: U1.connector2, U1.connector5, VR1.wiper, U2.connector2, U2.connector5, U3.connector2, U3.connector5
  GND: U1.connector3, VR1.leg2, 12V.GND, U2.connector3, U3.connector3, R15.Pin_1, R14.Pin_1, R13.Pin_1, R16.Pin_1, C5.0, NEOPIXEL1.GND
  N2: U1.connector4, R4.Pin_0, R7.Pin_0
  N3: U1.connector6, R4.Pin_1, R1.Pin_0
  VGLOW: U1.connector7, VR1.leg1, U2.connector7, U3.connector7, LED1.common_anode, S1.L2, LED2.common_anode, LED3.common_anode
  N4: 12V.VCC, S1.COM
  OSCR: U2.connector0, R8.Pin_1, C2.+, R10.Pin_0
  N5: U2.connector1, C2.-, R2.Pin_1
  N6: U2.connector4, R5.Pin_0, R8.Pin_0
  N7: U2.connector6, R5.Pin_1, R2.Pin_0
  OSCB: U3.connector0, R9.Pin_1, C3.+, R12.Pin_0
  N8: U3.connector1, C3.-, R3.Pin_1
  N9: U3.connector4, R6.Pin_0, R9.Pin_0
  N10: U3.connector6, R6.Pin_1, R3.Pin_0
  N11: Q3.E, R15.Pin_0
  N12: Q3.B, R12.Pin_1
  N13: Q3.C, LED1.blue_cathode, LED2.blue_cathode, LED3.blue_cathode
  N14: Q2.E, R14.Pin_0
  N15: Q2.B, R11.Pin_1
  N16: Q2.C, LED1.green_cathode, LED2.green_cathode, LED3.green_cathode
  N17: Q1.E, R13.Pin_0
  N18: Q1.B, R10.Pin_1
  N19: Q1.C, LED1.red_cathode, LED2.red_cathode, LED3.red_cathode
  VSTRIP: S1.L1, C4.+, C5.1, R20.Pin_1, R19.Pin_1, R18.Pin_1, R17.Pin_1, D1.anode
  N20: Q4.E, R20.Pin_0, R19.Pin_0, R18.Pin_0, R17.Pin_0, Q5.C
  N21: Q4.B, VR2.wiper
  N22: Q4.C, Q5.B
  N23: VR2.leg1, D1.cathode
  N24: VR2.leg2, R16.Pin_0, C4.-
  N25: Q5.E, NEOPIXEL1.+5V

notes:
  Note the intentionally reversed PNP orientation
  LED Glow Effect
  12V 3528 Strip (1m)
  LED Strip with dimmer
  Power
  Actually 12V 3528 (1m)

custom parts:
  Neopixel Strip -- White (60/m): Neopixel Strip, White, 60 pixels per meter.
