# Fritzing sketch Fire (saved by Fritzing 0.9.2b)
breadboards: 1

parts:
  U1 = LM 358 Dual Op-Amp [package="DIP8 [THT]"]
  5V = Power plug
  R1 = Resistor [tolerance=±5% resistance=100k package=THT]
  R2 = Resistor [tolerance=±5% resistance=100k package=THT]
  R3 = Resistor [tolerance=±5% resistance=100k package=THT]
  C1 = Electrolytic Capacitor [capacitance=4.7µF package="100 mil [THT, electrolytic]"]
  R4 = Resistor [tolerance=±5% resistance=22k package=THT]
  R6 = Resistor [tolerance=±5% resistance=100k package=THT]
  R5 = Resistor [tolerance=±5% resistance=10k package=THT]
  C2 = Electrolytic Capacitor [capacitance=47µF package="100 mil [THT, electrolytic]"]
  R7 = Resistor [tolerance=±5% resistance=51k package=THT]
  R8 = Resistor [tolerance=±5% resistance=47k package=THT]
  Q1 = 2N7000 FET N-Channel [part_number=2N7000 package=TO92]
  Q2 = 2N7000 FET N-Channel [part_number=2N7000 package=TO92]
  Rs = Resistor [tolerance=±5% resistance=4.7k package=THT]
  Rl = Resistor [tolerance=±5% resistance=10 package=THT]
  LED1 = smd LED [color="White (8000K)" part_number=5050 package="1206 [SMD]"]
  LED2 = smd LED [color="White (8000K)" part_number=5050 package="1206 [SMD]"]

nets:
  SQUARE: U1.connector0, R3.Pin_1, R4.Pin_1, R5.Pin_0
  N1: U1.connector1, C1.+, R4.Pin_0
  N2: U1.connector2, R1.Pin_1, R2.Pin_0, R3.Pin_0
  GND: U1.connector3, 5V.GND, R2.Pin_1, C1.-, R8.Pin_1, Rs.Pin_0, Rl.Pin_0
  N3: U1.connector4, R7.Pin_1, R8.Pin_0
  N4: U1.connector5, R6.Pin_1, R5.Pin_1, C2.+
  TRIANGLE: U1.connector6, R6.Pin_0, C2.-, Q1.gate, Q1.drain, Q2.gate
  5V: U1.connector7, 5V.VCC, R1.Pin_0, R7.Pin_0, LED1.anode, LED2.anode
  N5: Q1.source, Rs.Pin_1
  N6: Q2.drain, LED1.cathode, LED2.cathode
  N7: Q2.source, Rl.Pin_1

notes:
  CH1 - Square wave
  CH2 - Triangle wave

custom parts:
  2N7000 FET N-Channel: A 2N7000 MOSFET N-Channel Transistor
