# Fritzing sketch MiniGun (saved by Fritzing 0.9.2b)
breadboards: 1

parts:
  U1 = 555 Timer [package="DIP8 [THT]"]
  5V = Power plug
  R1 = Resistor [tolerance=±5% resistance=10k package=THT]
  R2 = Resistor [tolerance=±5% resistance=10k package=THT]
  R3 = Resistor [tolerance=±5% resistance=1k package=THT]
  C2 = Electrolytic Capacitor [capacitance=4.7µF package="100 mil [THT, electrolytic]"]
  R4 = Resistor [tolerance=±5% resistance=47 package=THT]
  LED_Rope = LED - 5mm [color="Yellow (574nm)" part_number="LED Rope" package="5 mm [THT]"]
  Q1 = PNP-Transistor [part_number=2N3906 package="TO92 [THT]"]

nets:
  GND: U1.Ground, 5V.GND, C2.-, R4.Pin_1
  N1: U1.Trigger, U1.Threshold, R2.Pin_1, C2.+
  N2: U1.Output, R3.Pin_0
  5V: U1.Reset, U1.Vcc_Supply_Voltage, 5V.VCC, R1.Pin_0, Q1.E
  N3: U1.Discharge, R1.Pin_1, R2.Pin_0
  N4: R3.Pin_1, Q1.B
  N5: R4.Pin_0, LED_Rope.cathode
  N6: LED_Rope.anode, Q1.C
