# Fritzing sketch Motors (saved by Fritzing 0.9.2b)
breadboards: 1

parts:
  U1 = 555 Timer [package="SO8 [SMD]"]
  R1 = Resistor [tolerance=±5% resistance=1k package=THT]
  D1 = Rectifier Diode [part_number=1N4148 package="300 mil [THT]"]
  D2 = Rectifier Diode [part_number=1N4148 package="300 mil [THT]"]
  R2 = Trimmer Potentiometer [maximum_resistance=10kΩ package=THT]
  M1 = DC Motor
  D3 = Rectifier Diode [part_number=1N4001 package="300 mil [THT]"]
  C1 = Ceramic Capacitor [capacitance=470nF package="100 mil [THT, multilayer]"]
  5V = Power plug

nets:
  GND: U1.Pin_1, M1.pin_1, D3.anode, C1.1, 5V.GND
  N1: U1.Pin_2, U1.Pin_6, R2.wiper, C1.0
  N2: U1.Pin_3, M1.pin_2, D3.cathode
  5V: U1.Pin_4, U1.Pin_8, R1.Pin_0, 5V.VCC
  N3: U1.Pin_7, R1.Pin_1, D1.anode, D2.cathode
  N4: D1.cathode, R2.leg2
  N5: D2.anode, R2.leg1
