# Fritzing sketch HurstPointLighthouse (saved by Fritzing 0.9.2b)
breadboards: 1

parts:
  U1 = 555 Timer [package="SO8 [SMD]"]
  LED1 = LED - 5mm [color="White (8000K)" package="5 mm [THT]"]
  S1 = Toggle Switch [package=THT]
  VCC1 = Battery block 9V
  U2 = 555 Timer [package="SO8 [SMD]"]
  R1 = Resistor [tolerance=±5% resistance=2M package=THT]
  D1 = Rectifier Diode [part_number=1N4148 package="300 mil [THT]"]
  C1 = Ceramic Capacitor [capacitance=100nF package="100 mil [THT, multilayer]"]
  C2 = Ceramic Capacitor [capacitance=100nF package="100 mil [THT, multilayer]"]
  D2 = Rectifier Diode [part_number=1N4148 package="300 mil [THT]"]
  R2 = Resistor [tolerance=±5% resistance=1M package=THT]
  C3 = Electrolytic Capacitor [capacitance=10µF package="100 mil [THT, electrolytic]"]
  C4 = Electrolytic Capacitor [capacitance=1µF package="100 mil [THT, electrolytic]"]
  R3 = Resistor [tolerance=±5% resistance=4.7k package=THT]
  R4 = Resistor [tolerance=±5% resistance=330k package=THT]
  C5 = Electrolytic Capacitor [capacitance=3.3µF package="100 mil [THT, electrolytic]"]
  R5 = Resistor [tolerance=±5% resistance=220 package=THT]
  LED2 = LED - 5mm [color="White (8000K)" package="5 mm [THT]"]
  LED3 = LED - 5mm [color="White (8000K)" package="5 mm [THT]"]

nets:
  GND: U1.Pin_1, LED1.cathode, VCC1.-, U2.Pin_1, C1.0, C2.0, C3.-, C4.-, C5.-, LED2.cathode, LED3.cathode
  N1: U1.Pin_2, U1.Pin_6, D1.cathode, R2.Pin_0, C3.+
  N2: U1.Pin_3, U2.Pin_4, R1.Pin_1, R2.Pin_1, C4.+
  VCC: U1.Pin_4, U1.Pin_8, S1.L2, U2.Pin_8, R3.Pin_0
  N3: U1.Pin_5, C1.1
  N4: LED1.anode, R5.Pin_1, LED2.anode, LED3.anode
  N5: S1.COM, VCC1.+
  N6: U2.Pin_2, U2.Pin_6, R4.Pin_1, C5.+
  N7: U2.Pin_3, D2.anode
  N8: U2.Pin_5, C2.1
  N9: U2.Pin_7, R3.Pin_1, R4.Pin_0
  N10: R1.Pin_0, D1.anode
  N11: D2.cathode, R5.Pin_0
