# Fritzing sketch Ki51Burma (saved by Fritzing 1.0.1rc)

parts:
  Part1 = LilyPad Coin Cell Battery Holder
  M1 = DC Motor [voltage_(max)=6V voltage_(min)=3V]

nets:
  N1: Part1.-, M1.pin_2
  N2: Part1.+, M1.pin_1
