# Fritzing sketch MitsubishiA5M2b (saved by Fritzing 0.9.2b)
breadboards: 1

parts:
  U3 = attiny85 [package=dip]
  M1 = DC Motor
  D1 = Rectifier Diode [part_number=1N4001 package="300 mil [THT]"]
  Q1 = Basic FET N-Channel [part_number=2N7000 package="DPak [SMD]"]
  R1 = Resistor [tolerance=±5% resistance=470 package=THT]
  C1 = Electrolytic Capacitor [capacitance=470µF package="100 mil [THT, electrolytic]"]
  C2 = Ceramic Capacitor [capacitance=100nF package="100 mil [THT, multilayer]"]
  R2 = Trimmer Potentiometer [maximum_resistance=10kΩ package=THT]
  Q2 = Basic FET N-Channel [part_number=2N7000 package="DPak [SMD]"]
  R3 = Resistor [tolerance=±5% resistance=470 package=THT]
  Q3 = Basic FET N-Channel [part_number=2N7000 package="DPak [SMD]"]
  R4 = Resistor [tolerance=±5% resistance=470 package=THT]
  Power = Battery [part_number="(3-5V ok)"]
  S1 = Toggle Switch [package=THT]
  R6 = Resistor [tolerance=±5% resistance=220 package=THT]
  R5 = Resistor [tolerance=±5% resistance=220 package=THT]
  LED1 = LED - 3mm [color="Red (633nm)" package="3 mm [THT]"]
  LED2 = LED - 3mm [color="Red (633nm)" package="3 mm [THT]"]
  LED3 = LED - 3mm [color="Yellow (595nm)" package="3 mm [THT]"]
  LED4 = LED - 3mm [color="Yellow (595nm)" package="3 mm [THT]"]
  LED5 = LED - 3mm [color="Red (633nm)" package="3 mm [THT]"]
  LED6 = LED - 3mm [color="Red (633nm)" package="3 mm [THT]"]
  LED7 = LED - 3mm [color="Yellow (595nm)" package="3 mm [THT]"]
  LED8 = LED - 3mm [color="Yellow (595nm)" package="3 mm [THT]"]

nets:
  FLAME2: U3.Pin_3, R4.Pin_0
  GND: U3.Pin_4, Q1.source, C1.-, C2.0, R2.leg1, Q2.source, Q3.source, Power.-
  PWM_OUT: U3.Pin_5, R1.Pin_0
  FLAME1: U3.Pin_6, R3.Pin_0
  PWM_LEVEL: U3.Pin_7, R2.wiper
  VCC: U3.Pin_8, M1.pin_1, D1.cathode, C1.+, C2.1, R2.leg2, S1.L2, LED1.anode, LED2.anode, LED3.anode, LED4.anode, LED5.anode, LED6.anode, LED7.anode, LED8.anode
  N1: M1.pin_2, D1.anode, Q1.drain
  N2: Q1.Gate, R1.Pin_1
  N3: Q2.Gate, R3.Pin_1
  N4: Q2.drain, R5.Pin_1
  N5: Q3.Gate, R4.Pin_1
  N6: Q3.drain, R6.Pin_1
  N7: Power.+, S1.COM
  N8: R6.Pin_0, LED5.cathode, LED6.cathode, LED7.cathode, LED8.cathode
  N9: R5.Pin_0, LED1.cathode, LED2.cathode, LED3.cathode, LED4.cathode
