# Fritzing sketch G3M3Model23 (saved by Fritzing 1.0.1rc)
breadboards: 1

parts:
  U1 = 555 Timer [package="SO8 [SMD]"]
  R1 = Resistor [tolerance=±5% resistance=1k power=0.25W package=THT]
  D1 = Rectifier Diode [part_number=1N4148 package="300 mil [THT]"]
  D2 = Rectifier Diode [part_number=1N4148 package="300 mil [THT]"]
  R2 = Trimmer Potentiometer [maximum_resistance=10kΩ knob_status=50% power=0.5W package=THT]
  M1 = DC Motor [voltage_(max)=6V voltage_(min)=3V]
  D3 = Rectifier Diode [part_number=1N4001 package="300 mil [THT]"]
  C1 = Ceramic Capacitor [capacitance=470nF voltage=35V package="100 mil [THT, multilayer]"]
  VCC = Battery
  M2 = DC Motor [voltage_(max)=6V voltage_(min)=3V]
  D4 = Rectifier Diode [part_number=1N4001 package="300 mil [THT]"]

nets:
  GND: U1.Pin_1, C1.1, VCC.-
  N1: U1.Pin_2, U1.Pin_6, R2.wiper, C1.0
  N2: U1.Pin_3, M1.pin_1, D3.anode, M2.pin_1, D4.anode
  3V: U1.Pin_4, U1.Pin_8, R1.Pin_0, M1.pin_2, D3.cathode, VCC.+, M2.pin_2, D4.cathode
  N3: U1.Pin_7, R1.Pin_1, D1.anode, D2.cathode
  N4: D1.cathode, R2.leg2
  N5: D2.anode, R2.leg1
