# Fritzing sketch YawataMaruUnyo (saved by Fritzing 0.9.2b)
breadboards: 1

parts:
  U1 = attiny85 [package=dip]
  12V = Power plug
  Buck_Converter = IC, DIP package, 4 pins [chip_label=Buck]
  LED1 = LED - 5mm [color="White (8000K)" package="5 mm [THT]"]
  LED2 = LED - 5mm [color="White (8000K)" package="5 mm [THT]"]
  LED3 = LED - 5mm [color="White (8000K)" package="5 mm [THT]"]
  LED4 = LED - 5mm [color="White (8000K)" package="5 mm [THT]"]
  Q1 = Basic FET N-Channel [part_number=2N7000 package="TO220 [THT]"]
  Q2 = Basic FET N-Channel [part_number=2N7000 package="TO220 [THT]"]
  Q3 = Basic FET N-Channel [part_number=2N7000 package="TO220 [THT]"]
  Q4 = Basic FET N-Channel [part_number=2N7000 package="TO220 [THT]"]

nets:
  PB3/U_front: U1.Pin_2, Q3.gate
  PB4/U_Rear: U1.Pin_3, Q4.gate
  GND: U1.Pin_4, 12V.GND, Buck_Converter.pin1, Buck_Converter.pin2, Q1.source, Q2.source, Q3.source, Q4.source
  PB0/YM_Rear: U1.Pin_5, Q1.gate
  PB1/YM_Front: U1.Pin_6, Q2.gate
  5V: U1.Pin_8, Buck_Converter.pin3
  12V: 12V.VCC, Buck_Converter.pin4, LED1.anode, LED2.anode, LED3.anode, LED4.anode
  N1: LED1.cathode, Q1.drain
  N2: LED2.cathode, Q2.drain
  N3: LED3.cathode, Q3.drain
  N4: LED4.cathode, Q4.drain

notes:
  12V LED strips x4
