# Fritzing sketch KickingBack (saved by Fritzing 0.9.2b)
breadboards: 1

parts:
  L1 = Solenoid
  D2 = Rectifier Diode [part_number=1N4001 package="300 mil [THT]"]
  VCC1 = Battery block 9V
  R7 = Resistor [tolerance=±5% resistance=1k package=THT]
  IC2 = 555 Timer [package="DIP8 [THT]"]
  C1 = Ceramic Capacitor [capacitance=100nF package="100 mil [THT, multilayer]"]
  C2 = Electrolytic Capacitor [capacitance=10µF package="100 mil [THT, electrolytic]"]
  R1 = Resistor [tolerance=±5% resistance=22k package=THT]
  IC1 = HALL-EFFECT [part_number=44E/938 package=sc70]
  R3 = Resistor [tolerance=±5% resistance=10k package=THT]
  Q1 = PNP-Transistor [part_number=2N3906 package="TO92 [THT]"]
  R4 = Resistor [tolerance=±5% resistance=1k package=THT]
  R5 = Resistor [tolerance=±5% resistance=10k package=THT]
  C3 = Ceramic Capacitor [capacitance=100nF package="100 mil [THT, multilayer]"]
  R6 = Resistor [tolerance=±5% resistance=10k package=THT]
  D1 = Rectifier Diode [part_number=1N4148 package="300 mil [THT]"]
  Q2 = PNP-Transistor [part_number=2N3906 package="TO92 [THT]"]
  R8 = Resistor [tolerance=±5% resistance=1k package=THT]
  LED1 = LED - 3mm [color="Blue (430nm)" package="3 mm [THT]"]
  S1 = Toggle Switch [package=THT]
  R2 = Trimmer Potentiometer [maximum_resistance=50kΩ package=THT]

nets:
  GND: L1.pin1, D2.anode, VCC1.-, IC2.Ground, C1.0, C2.-, IC1.GND, R5.Pin_1, R6.Pin_0, D1.anode, R8.Pin_0
  N1: L1.pin2, D2.cathode, Q2.C, LED1.anode
  N2: VCC1.+, S1.L2
  N3: R7.Pin_0, Q2.B
  N4: R7.Pin_1, IC2.Output
  N5: IC2.Trigger, C2.+, R2.leg1, R2.wiper
  9V: IC2.Reset, IC2.Vcc_Supply_Voltage, R1.Pin_0, IC1.VCC, R3.Pin_1, Q1.E, Q2.E, S1.COM
  N6: IC2.Control_Voltage, C1.1
  N7: IC2.Threshold, C3.0, R6.Pin_1, D1.cathode
  N8: IC2.Discharge, R1.Pin_1, R2.leg2
  N9: IC1.OUT, R3.Pin_0, R4.Pin_0
  N10: Q1.B, R4.Pin_1
  N11: Q1.C, R5.Pin_0, C3.1
  N12: R8.Pin_1, LED1.cathode
