# Fritzing sketch KubelMagic (saved by Fritzing 0.9.2b)
breadboards: 1

parts:
  R1a = Resistor [tolerance=±5% resistance=220 package=THT]
  R2a = Resistor [tolerance=±5% resistance=220 package=THT]
  R1 = Resistor [tolerance=±5% resistance=100k package=THT]
  R2 = Resistor [tolerance=±5% resistance=100k package=THT]
  C1 = Electrolytic Capacitor [capacitance=1µF package="100 mil [THT, electrolytic]"]
  LED1 = LED - 3mm [color="Red (633nm)" package="3 mm [THT]"]
  LED2 = LED - 3mm [color="Red (633nm)" package="3 mm [THT]"]
  C2 = Electrolytic Capacitor [capacitance=1µF package="100 mil [THT, electrolytic]"]
  Q1 = NPN-Transistor [part_number=2N3904 package="TO92 [THT]"]
  Q2 = NPN-Transistor [part_number=2N3904 package="TO92 [THT]"]
  VCC1 = Battery
  S1 = Tilt Switch [package=THT]

nets:
  N1: R1a.Pin_0, R2a.Pin_0, R1.Pin_0, R2.Pin_0, S1.Pin_2
  N2: R1a.Pin_1, LED1.anode
  N3: R2a.Pin_1, LED2.anode
  N4: R1.Pin_1, C1.-, Q2.B
  N5: R2.Pin_1, C2.-, Q1.B
  N6: C1.+, LED1.cathode, Q1.C
  N7: LED2.cathode, C2.+, Q2.C
  GND: Q1.E, Q2.E, VCC1.-
  N8: VCC1.+, S1.Pin_1
