# Fritzing sketch MetalEarthLeadGuitar (saved by Fritzing 0.9.2b)
circuit board: 6cm x 4cm
breadboards: 1

parts:
  C1 = Electrolytic Capacitor [capacitance=47µF package="100 mil [THT, electrolytic]"]
  R1 = Resistor [tolerance=±5% resistance=4.7k package=THT]
  R2 = Resistor [tolerance=±5% resistance=1M package=THT]
  C2 = Electrolytic Capacitor [capacitance=1µF package="100 mil [THT, electrolytic]"]
  MIC1 = Microphone
  R3 = Resistor [tolerance=±5% resistance=4.7k package=THT]
  Q1 = NPN-Transistor [part_number=2N3904 package="TO92 [THT]"]
  Q2 = NPN-Transistor [part_number=2N3904 package="TO92 [THT]"]
  LED1 = LED - 3mm [color="Blue (470nm)" package="3 mm [THT]"]
  LED2 = LED - 3mm [color="Blue (470nm)" package="3 mm [THT]"]
  LED3 = LED - 3mm [color="Blue (470nm)" package="3 mm [THT]"]
  LED4 = LED - 3mm [color="Blue (470nm)" package="3 mm [THT]"]
  LED5 = LED - 3mm [color="Blue (470nm)" package="3 mm [THT]"]
  5V = Power plug
  S1 = Toggle Switch [package=THT]

nets:
  GND: C1.-, MIC1.pin1, Q1.E, Q2.E, 5V.GND
  N1: C1.+, R1.Pin_0, R2.Pin_0, R3.Pin_0, LED1.anode, LED2.anode, LED3.anode, LED4.anode, LED5.anode, S1.L2
  N2: R1.Pin_1, C2.+, MIC1.pin2
  N3: R2.Pin_1, C2.-, Q1.B
  N4: R3.Pin_1, Q1.C, Q2.B
  N5: Q2.C, LED1.cathode, LED2.cathode, LED3.cathode, LED4.cathode, LED5.cathode
  N6: 5V.VCC, S1.COM
