# Fritzing sketch MongolWarriors (saved by Fritzing 0.9.2b)
breadboards: 1

parts:
  IC1 = IC, DIP package, 6 pins [chip_label=MT3608]
  D1 = Rectifier Diode [part_number=1N5819 package="300 mil [THT]"]
  L1 = Inductor [inductance=22µH package="400 mil [THT]"]
  C1 = Ceramic Capacitor [capacitance=22µF package="100 mil [THT, multilayer]"]
  C2 = Ceramic Capacitor [capacitance=22µF package="100 mil [THT, multilayer]"]
  R2 = Resistor [tolerance=±5% resistance=2.2k package=THT]
  R3 = Resistor [tolerance=±5% resistance=10k package=THT]
  R1 = Trimmer Potentiometer [maximum_resistance=100kΩ package=THT]
  VCC = Battery block 9V
  12V_LED_STRIP = female pin header, 2 pins [form="♀ (female)"]
  S1 = Toggle Switch [package=THT]

nets:
  N1: IC1.pin1, D1.anode, L1.pin_0
  GND: IC1.pin2, IC1.pin4, C1.0, C2.0, R2.Pin_1, R3.Pin_0, VCC.-, 12V_LED_STRIP.pin2
  N2: IC1.pin3, R2.Pin_0, R1.leg1, R1.wiper
  N3: IC1.pin5, L1.pin_1, C1.1, R3.Pin_1, S1.COM
  VOUT: D1.cathode, C2.1, R1.leg2, 12V_LED_STRIP.pin1
  N4: VCC.+, S1.L2

notes:
  12V Warm White LED Strip
  MT3608 Module set for 12V out
