# Fritzing sketch OneHertz (saved by Fritzing 1.0.1rc)
breadboards: 2

parts:
  U4 = IC, DIP package, 14 pins [chip_label=74LS73]
  U2 = 555 Timer [package="DIP8 [THT]"]
  U3 = 555 Timer [package="DIP8 [THT]"]
  Q1 = Basic FET N-Channel [part_number=2N7000 package="TO220 [THT]"]
  C2 = Ceramic Capacitor [capacitance=100nF voltage=35V package="100 mil [THT, multilayer]"]
  R3 = Resistor [tolerance=±5% power=0.25W resistance=4.7k package=THT]
  R4 = Resistor [tolerance=±5% power=0.25W resistance=10k package=THT]
  C3 = Electrolytic Capacitor [capacitance=10µF voltage=35V package="100 mil [THT, electrolytic]"]
  R5 = Resistor [tolerance=±5% power=0.25W resistance=1k package=THT]
  C4 = Ceramic Capacitor [capacitance=10nF voltage=35V package="100 mil [THT, multilayer]"]
  C5 = Electrolytic Capacitor [capacitance=10µF voltage=35V package="100 mil [THT, electrolytic]"]
  J1 = Piezo Speaker
  C6 = Electrolytic Capacitor [capacitance=100µF voltage=35V package="100 mil [THT, electrolytic]"]
  Clock_Module = female pin header, 3 pins [form="♀ (female)"]
  BAT1 = Battery Holders [package=battery-aaa]
  Q2 = NPN-Transistor [part_number=2N3904 package="TO92 [THT]"]
  R8 = Resistor [tolerance=±5% power=0.25W resistance=1k package=THT]
  R9 = Resistor [tolerance=±5% power=0.25W resistance=10k package=THT]
  U5 = IC, DIP package, 16 pins [chip_label=CD4017 part_number=CD4017]
  Q3 = Basic FET N-Channel [part_number=2N7000 package="TO220 [THT]"]
  L1 = Inductor [package="400 mil [THT]"]
  R10 = Resistor [tolerance=±5% power=0.25W resistance=4.7k package=THT]
  D1 = Rectifier Diode [part_number=1N5819 package="300 mil [THT]"]
  C7 = Electrolytic Capacitor [capacitance=2.2mF voltage=35V package="100 mil [THT, electrolytic]"]
  D2 = Rectifier Diode [part_number=1N4001 package="300 mil [THT]"]
  BAT2 = 4 x AAA Battery Mount
  S1 = SWITCH-DPDT [package=os]
  R11 = 12mm Trimmer Potentiometer (Large) [maximum_resistance=50k knob_status=50% power=0.5W package=THT]
  R12 = 12mm Trimmer Potentiometer (Large) [maximum_resistance=50k knob_status=50% power=0.5W package=THT]
  R13 = Resistor [tolerance=±5% power=0.25W resistance=3k package=THT]
  LED1 = LED - 3mm [color="Green (555nm)" current=0.030A package="3 mm [THT]"]
  R14 = Resistor [tolerance=±5% power=0.25W resistance=3k package=THT]
  LED2 = LED - 3mm [color="Green (555nm)" current=0.030A package="3 mm [THT]"]
  R15 = Resistor [tolerance=±5% power=0.25W resistance=470k package=THT]
  R16 = Resistor [tolerance=±5% power=0.25W resistance=470k package=THT]
  LED3 = LED - 5mm [color="Red (633nm)" current=0.030A package="5 mm [THT]"]
  LED4 = LED - 5mm [color="Green (555nm)" current=0.030A package="5 mm [THT]"]

nets:
  TICK: U4.pin1, U2.Output, U3.Control_Voltage, Q3.gate, R10.Pin_1, R13.Pin_0
  6V: U4.pin2, U4.pin3, U4.pin4, U4.pin14, U2.Reset, U2.Vcc_Supply_Voltage, U3.Reset, U3.Vcc_Supply_Voltage, R3.Pin_0, R4.Pin_1, R5.Pin_0, C6.+, R9.Pin_0, U5.pin16, D1.anode, S1.4
  GND: U4.pin11, U2.Ground, U3.Ground, C3.-, C4.0, J1.pin1, C6.-, Clock_Module.pin3, BAT1.-, Q2.E, U5.pin8, U5.pin13, Q3.source, R10.Pin_0, C7.-, BAT2.-, LED1.cathode, LED2.cathode, LED3.cathode, LED4.cathode
  FNOTCH: U4.pin12, Q1.gate, R16.Pin_0
  ~FNOTCH: U4.pin13, R15.Pin_0
  N1: U2.Trigger, C2.1, R4.Pin_0
  N2: U2.Threshold, U2.Discharge, R3.Pin_1, C3.+
  N3: U3.Trigger, U3.Threshold, Q1.source, C4.1, R12.leg1, R12.wiper
  AF: U3.Output, C5.+, R14.Pin_0
  N4: U3.Discharge, R5.Pin_1, R11.leg2
  N5: Q1.drain, R11.leg1, R11.wiper, R12.leg2
  1Hz Pulse: C2.0, U5.pin3
  N6: C5.-, J1.pin2
  1.5V: Clock_Module.pin1, S1.1
  8Hz Pulse: Clock_Module.pin2, R8.Pin_0
  N7: BAT1.+, S1.2
  N8: Q2.B, R8.Pin_1
  CLK: Q2.C, R9.Pin_1, U5.pin14
  N9: U5.pin9, U5.pin15
  N10: Q3.drain, L1.pin_1, D2.anode
  N11: L1.pin_0, D1.cathode, C7.+, D2.cathode
  N12: BAT2.+, S1.5
  N13: R13.Pin_1, LED1.anode
  N14: R14.Pin_1, LED2.anode
  N15: R15.Pin_1, LED3.anode
  N16: R16.Pin_1, LED4.anode

notes:
  Clock Mechanism
