# Fritzing sketch WarHawk40K (saved by Fritzing 0.9.2b)
breadboards: 1

parts:
  IC1 = IC, DIP package, 16 pins [chip_label=CD4060]
  5V = Power plug
  C1 = Ceramic Capacitor [capacitance=100nF package="100 mil [THT, multilayer]"]
  R2 = Resistor [tolerance=±5% resistance=10k package=THT]
  R1 = Resistor [tolerance=±5% resistance=10k package=THT]
  LRr = LED - 3mm [color="Red (633nm)" package="3 mm [THT]"]
  LRl = LED - 3mm [color="Red (633nm)" package="3 mm [THT]"]
  LY = LED - 3mm [color="Yellow (595nm)" package="3 mm [THT]"]
  LBl = LED - 3mm [color="Blue (430nm)" package="3 mm [THT]"]
  LBc = LED - 3mm [color="Blue (430nm)" package="3 mm [THT]"]
  LBr = LED - 3mm [color="Blue (430nm)" package="3 mm [THT]"]
  LG = LED - 3mm [color="Green (555nm)" package="3 mm [THT]"]
  RBlr = Resistor [tolerance=±5% resistance=1k package=THT]
  RR = Resistor [tolerance=±5% resistance=1k package=THT]
  RG = Resistor [tolerance=±5% resistance=220 package=THT]
  RBc = Resistor [tolerance=±5% resistance=1k package=THT]
  RY = Resistor [tolerance=±5% resistance=220 package=THT]

nets:
  D7: IC1.pin1, RR.Pin_1
  D2: IC1.pin4
  D1: IC1.pin5
  D3: IC1.pin6, RBlr.Pin_0
  D0: IC1.pin7
  GND: IC1.pin8, IC1.pin12, 5V.GND, LRr.cathode, LRl.cathode, LY.cathode, LBl.cathode, LBc.cathode, LBr.cathode, LG.cathode
  N1: IC1.pin9, C1.0
  N2: IC1.pin10, R1.Pin_0
  N3: IC1.pin11, R2.Pin_0
  D5: IC1.pin13, RY.Pin_1
  D4: IC1.pin14, RBc.Pin_1
  D6: IC1.pin15, RG.Pin_1
  VDD: IC1.pin16, 5V.VCC
  N4: C1.1, R2.Pin_1, R1.Pin_1
  N5: LRr.anode, LRl.anode, RR.Pin_0
  N6: LY.anode, RY.Pin_0
  N7: LBl.anode, LBr.anode, RBlr.Pin_1
  N8: LBc.anode, RBc.Pin_0
  N9: LG.anode, RG.Pin_0
