# Fritzing sketch Pollen8 (saved by Fritzing 1.0.1rc)
breadboards: 1

parts:
  U1 = 555 Timer [package="DIP8 [THT]"]
  U3 = IC, DIP package, 16 pins [chip_label=CD4017 part_number=CD4017]
  3-5V = Power plug
  C1 = Electrolytic Capacitor [capacitance=10µF package="100 mil [THT, electrolytic]"]
  R1 = Resistor [tolerance=±5% resistance=2.2k power=0.25W package=THT]
  LED2 = LED - 5mm [color="Red (633nm)" current=0.030A package="5 mm [THT]"]
  LED3 = LED - 5mm [color="Red (633nm)" current=0.030A package="5 mm [THT]"]
  LED4 = LED - 5mm [color="Red (633nm)" current=0.030A package="5 mm [THT]"]
  LED5 = LED - 5mm [color="Red (633nm)" current=0.030A package="5 mm [THT]"]
  RL1 = Resistor [tolerance=±5% resistance=220 power=0.25W package=THT]
  RL2 = Resistor [tolerance=±5% resistance=220 power=0.25W package=THT]
  RL3 = Resistor [tolerance=±5% resistance=220 power=0.25W package=THT]
  RL4 = Resistor [tolerance=±5% resistance=220 power=0.25W package=THT]
  RL5 = Resistor [tolerance=±5% resistance=220 power=0.25W package=THT]
  LED1 = LED - 5mm [color="Red (633nm)" current=0.030A package="5 mm [THT]"]
  U2 = IC, DIP package, 16 pins [chip_label=CD4017 part_number=CD4017]
  S1 = Toggle Switch [package=THT]
  R2 = Photocell (LDR) [power=0.25W dark_resistance_@0.01lx=300kΩ light_resistance_@100lx=400Ω luminance=10lx package=THT]

nets:
  GND: U1.Ground, U3.pin8, U3.pin13, U3.pin15, 3-5V.GND, C1.-, RL1.Pin_1, RL2.Pin_1, RL3.Pin_1, RL4.Pin_1, RL5.Pin_1, U2.pin8, U2.pin13, U2.pin15
  N1: U1.Trigger, U1.Threshold, C1.+, R2.pin_1
  CLK: U1.Output, U3.pin14, U2.pin14
  VCC: U1.Reset, U1.Vcc_Supply_Voltage, U3.pin16, R1.Pin_1, U2.pin16, S1.L2
  N2: U1.Discharge, R1.Pin_0, R2.pin_0
  L0: U3.pin3, LED2.anode, LED3.anode, LED4.anode, LED5.anode, LED1.anode
  N3: 3-5V.VCC, S1.COM
  N4: LED2.cathode, RL2.Pin_0
  N5: LED3.cathode, RL3.Pin_0
  N6: LED4.cathode, RL4.Pin_0
  N7: LED5.cathode, RL5.Pin_0
  N8: RL1.Pin_0, LED1.cathode

notes:
  e.g. up to 5 LEDs per output
