# Fritzing sketch HarrierGR1 (saved by Fritzing 0.9.2b)
breadboards: 2

parts:
  9-9_5V = Power plug
  L1 = Inductor [inductance=100µH package="400 mil [THT]"]
  C2 = Ceramic Capacitor [capacitance=1µF package="100 mil [THT, multilayer]"]
  R1 = Resistor [tolerance=±5% resistance=1M package=THT]
  C1 = Ceramic Capacitor [capacitance=10nF package="100 mil [THT, multilayer]"]
  Q1 = NPN-Transistor [part_number=BC337 package="TO92 [THT]"]
  Q2 = NPN-Transistor [part_number=BC337 package="TO92 [THT]"]
  C3 = Ceramic Capacitor [capacitance=100nF package="100 mil [THT, multilayer]"]
  R2 = Resistor [tolerance=±5% resistance=100k package=THT]
  R3 = Resistor [tolerance=±5% resistance=1M package=THT]
  C4 = Ceramic Capacitor [capacitance=100nF package="100 mil [THT, multilayer]"]
  IC1 = IC, DIP package, 16 pins [chip_label=CD4046]
  C5 = Ceramic Capacitor [capacitance=100nF package="100 mil [THT, multilayer]"]
  R4 = Resistor [tolerance=±5% resistance=330k package=THT]
  R5 = Resistor [tolerance=±5% resistance=47k package=THT]
  R6 = Resistor [tolerance=±5% resistance=4.7k package=THT]
  C6 = Ceramic Capacitor [capacitance=100nF package="100 mil [THT, multilayer]"]
  R7 = Resistor [tolerance=±5% resistance=100k package=THT]
  C7 = Electrolytic Capacitor [capacitance=47µF voltage=16V package="100 mil [THT, electrolytic]"]
  IC2 = LM386 [part_number=LM386 package=dip08]
  R8 = Trimmer Potentiometer [maximum_resistance=10kΩ package=THT]
  C8 = Electrolytic Capacitor [capacitance=100µF voltage=25V package="100 mil [THT, electrolytic]"]
  J1 = Piezo Speaker
  R9 = Trimmer Potentiometer [maximum_resistance=500kΩ package=THT]
  S1 = Toggle Switch [package=THT]
  S2 = Toggle Switch [package=THT]
  IC3 = 555 Timer [package="DIP8 [THT]"]
  IC4 = 555 Timer [package="DIP8 [THT]"]
  LED1 = smd LED [color="White (8000K)" part_number="Ground Flood" package="0805 [SMD]"]
  LED2 = smd LED [color="Green (555nm)" part_number="Starboard Nav" package="0805 [SMD]"]
  LED3 = smd LED [color="Red (633nm)" part_number="Port Nav" package="0805 [SMD]"]
  LED4 = smd LED [color="Red (633nm)" part_number="Dome Nav Strobe" package="0805 [SMD]"]
  R10 = Resistor [tolerance=±5% resistance=4.7k package=THT]
  R11 = Resistor [tolerance=±5% resistance=4.7k package=THT]
  R12 = Resistor [tolerance=±5% resistance=1.2k package=THT]
  R13 = Resistor [tolerance=±5% resistance=470k package=THT]
  R14 = Resistor [tolerance=±5% resistance=47k package=THT]
  R15 = Resistor [tolerance=±5% resistance=680k package=THT]
  C9 = Ceramic Capacitor [capacitance=1µF package="100 mil [THT, multilayer]"]
  C10 = Ceramic Capacitor [capacitance=100nF package="100 mil [THT, multilayer]"]
  D1 = Rectifier Diode [part_number=1N4148 package="300 mil [THT]"]
  R16 = Resistor [tolerance=±5% resistance=10k package=THT]
  R17 = Resistor [tolerance=±5% resistance=100k package=THT]
  C11 = Ceramic Capacitor [capacitance=1µF package="100 mil [THT, multilayer]"]
  C12 = Electrolytic Capacitor [capacitance=220µF voltage=16V package="100 mil [THT, electrolytic]"]
  D2 = Rectifier Diode [part_number=1N4001 package="300 mil [THT]"]
  D3 = Rectifier Diode [part_number=1N4001 package="300 mil [THT]"]
  C13 = Ceramic Capacitor [capacitance=100nF voltage=16V package="100 mil [THT, multilayer]"]

nets:
  GND: 9-9_5V.GND, L1.pin_1, C2.1, Q2.E, IC1.pin5, IC1.pin8, R5.Pin_1, R6.Pin_1, C7.-, IC2.-INPUT, IC2.GND, R8.leg2, J1.pin1, IC3.Ground, IC4.Ground, LED1.cathode, LED2.cathode, LED3.cathode, LED4.cathode, C9.0, D1.anode, C11.1, C12.-, C13.0
  N1: 9-9_5V.VCC, S1.COM, S2.COM
  N2: L1.pin_0, C2.0, C1.1, Q1.B
  N3: R1.Pin_0, Q1.E, C3.0
  VENG: R1.Pin_1, C1.0, R2.Pin_0, IC1.pin16, R7.Pin_1, IC2.Vs, S1.L2, C12.+
  N4: Q2.B, C3.1, R3.Pin_0
  N5: Q2.C, R2.Pin_1, R3.Pin_1, C4.0
  MIX_OUT/NOISE_OUT: C4.1, R4.Pin_1, R8.leg1
  N6: IC1.pin3, IC1.pin4, C5.0
  N7: IC1.pin6, C6.1
  N8: IC1.pin7, C6.0
  N9: IC1.pin9, R7.Pin_0, C7.+
  N10: IC1.pin11, R6.Pin_0
  N11: IC1.pin12, R5.Pin_0
  VCO_OUT: C5.1, R9.leg2
  N12: R4.Pin_0, R9.leg1, R9.wiper
  N13: IC2.+INPUT, R8.wiper
  N14: IC2.Vout, C8.+
  N15: C8.-, J1.pin2
  N16: S2.L2, D2.anode
  N17: IC3.Trigger, IC3.Threshold, R15.Pin_1, C9.1
  N18: IC3.Output, C10.0
  VNAV: IC3.Reset, IC3.Vcc_Supply_Voltage, IC4.Reset, IC4.Vcc_Supply_Voltage, R10.Pin_1, R11.Pin_1, R12.Pin_1, R14.Pin_0, R16.Pin_0, R17.Pin_0, D3.cathode, C13.1
  N19: IC3.Discharge, R14.Pin_1, R15.Pin_0
  N20: IC4.Trigger, C10.1, D1.cathode, R16.Pin_1
  N21: IC4.Output, R13.Pin_1
  N22: IC4.Threshold, IC4.Discharge, R17.Pin_1, C11.0
  N23: LED1.anode, R10.Pin_0
  N24: LED2.anode, R11.Pin_0
  N25: LED3.anode, R12.Pin_0
  N26: LED4.anode, R13.Pin_0
  N27: D2.cathode, D3.anode

notes:
  Jet Engine Sound Simulation
  Navigation Lights
  Power and controls

custom parts:
  LM386: low voltage audio power amplifier
