# Fritzing sketch Typhoon (saved by Fritzing 0.9.2b)
breadboards: 1

parts:
  3V = Power plug
  M1 = DC Motor
  D2 = Rectifier Diode [part_number=1N4001 package="300 mil [THT]"]
  S1 = Toggle Switch [package=THT]
  R5 = Resistor [tolerance=±5% resistance=100 package=THT]
  LED1 = LED - 5mm [color="Red (633nm)" part_number="RGB Fast Flash" package="5 mm [THT]"]
  C1 = Electrolytic Capacitor [capacitance=100µF package="100 mil [THT, electrolytic]"]
  C2 = Ceramic Capacitor [capacitance=100nF package="100 mil [THT, multilayer]"]
  LED2 = LED - 5mm [color="Red (633nm)" part_number="RGB Fast Flash" package="5 mm [THT]"]
  Q2 = NPN-Transistor [part_number=A42 package="TO92 [THT]"]
  Q1 = PNP-Transistor [part_number=2N3906 package="TO92 [THT]"]
  R5_2 = Trimmer Potentiometer [maximum_resistance=100kΩ package=THT]
  R1 = Resistor [tolerance=±5% resistance=1 package=THT]
  R2 = Resistor [tolerance=±5% resistance=1 package=THT]
  R3 = Resistor [tolerance=±5% resistance=1 package=THT]
  R4 = Resistor [tolerance=±5% resistance=1 package=THT]
  D1 = Schottky Diode [part_number=1N5819 package="300 mil [THT]"]
  R6 = Resistor [tolerance=±5% resistance=10k package=THT]
  C3 = Electrolytic Capacitor [capacitance=100µF package="100 mil [THT, electrolytic]"]
  C4 = Ceramic Capacitor [capacitance=100nF package="100 mil [THT, multilayer]"]

nets:
  GND: 3V.GND, M1.pin_1, D2.anode, LED1.cathode, C1.-, C2.0, LED2.cathode, R6.Pin_0, C4.0
  N1: 3V.VCC, S1.COM
  N2: M1.pin_2, D2.cathode, Q2.E
  VCC: S1.L2, R5.Pin_0, C1.+, C2.1, R1.Pin_0, R2.Pin_0, R3.Pin_0, R4.Pin_0, D1.anode, C3.+, C4.1
  N3: R5.Pin_1, LED1.anode, LED2.anode
  N4: Q2.B, Q1.C
  N5: Q2.C, Q1.E, R1.Pin_1, R2.Pin_1, R3.Pin_1, R4.Pin_1
  N6: Q1.B, R5_2.wiper
  N7: R5_2.leg1, R6.Pin_1, C3.-
  N8: R5_2.leg2, D1.cathode
