# Fritzing sketch RaceToJitra (saved by Fritzing 0.9.2b)
breadboards: 1

parts:
  IC1 = IC, DIP package, 4 pins [chip_label="MC34063 Boost Converter"]
  CONN1 = USB connector [package=THT]
  12V_LED_Strip = Neopixel Strip -- White (30/m)

nets:
  N1: IC1.pin1, CONN1.5V
  N2: IC1.pin2, CONN1.GND, CONN1.chassis5, CONN1.chassis6
  N3: IC1.pin3, 12V_LED_Strip.GND
  N4: IC1.pin4, 12V_LED_Strip.+5V

notes:
  12V Cool White LED Strip

custom parts:
  Neopixel Strip -- White (30/m): Neopixel Strip, White, 30 pixels per meter.
