# Fritzing sketch Schnellboot (saved by Fritzing 0.9.2b)
breadboards: 1

parts:
  IC1 = LM324 [package=dil16]
  Q1 = NPN-Transistor [part_number=2N3904 package="TO92 [THT]"]
  R1 = Resistor [tolerance=±5% resistance=220 package=THT]
  R2 = Resistor [tolerance=±5% resistance=100 package=THT]
  R3 = Resistor [tolerance=±5% resistance=47k package=THT]
  R4 = Resistor [tolerance=±5% resistance=47k package=THT]
  C1 = Electrolytic Capacitor [capacitance=33µF package="100 mil [THT, electrolytic]"]
  R5 = Resistor [tolerance=±5% resistance=47k package=THT]
  R6 = Resistor [tolerance=±5% resistance=100k package=THT]
  R7 = Resistor [tolerance=±5% resistance=47k package=THT]
  X1 = USB Connectors [package=usb-minib-nostop]
  LED1 = LED - 3mm [color="Green (555nm)" package="3 mm [THT]"]
  LED2 = LED - 3mm [color="Blue (430nm)" package="3 mm [THT]"]
  LED3 = LED - 3mm [color="White (8000K)" package="3 mm [THT]"]
  LED4 = LED - 3mm [color="White (8000K)" package="3 mm [THT]"]
  R8 = Resistor [tolerance=±5% resistance=220 package=THT]
  R9 = Resistor [tolerance=±5% resistance=220 package=THT]
  LED5 = LED - 3mm [color="Blue (430nm)" package="3 mm [THT]"]
  LED6 = LED - 3mm [color="Green (555nm)" package="3 mm [THT]"]
  R10 = Resistor [tolerance=±5% resistance=220 package=THT]
  R11 = Resistor [tolerance=±5% resistance=100 package=THT]
  Q2 = NPN-Transistor [part_number=2N3904 package="TO92 [THT]"]
  R12 = Resistor [tolerance=±5% resistance=100k package=THT]
  C2 = Electrolytic Capacitor [capacitance=33µF package="100 mil [THT, electrolytic]"]
  R13 = Resistor [tolerance=±5% resistance=47k package=THT]
  R14 = Resistor [tolerance=±5% resistance=47k package=THT]
  R15 = Resistor [tolerance=±5% resistance=47k package=THT]
  R16 = Resistor [tolerance=±5% resistance=47k package=THT]

nets:
  OSC1: IC1.OUT1, Q1.B, C1.+, R7.Pin_1
  N1: IC1.IN1-, C1.-, R5.Pin_1
  N2: IC1.IN1+, IC1.IN2-, R3.Pin_0, R4.Pin_1
  Vdd: IC1.V+, Q1.E, R4.Pin_0, X1.VBUS, R8.Pin_0, R9.Pin_0, Q2.E, R16.Pin_0
  N3: IC1.IN2+, R6.Pin_0, R7.Pin_0
  N4: IC1.OUT2, R5.Pin_0, R6.Pin_1
  N5: IC1.OUT3, R12.Pin_1, R13.Pin_0
  N6: IC1.IN3-, IC1.IN4+, R15.Pin_0, R16.Pin_1
  N7: IC1.IN3+, R12.Pin_0, R14.Pin_0
  GND: IC1.GND, R3.Pin_1, X1.GND, LED1.cathode, LED2.cathode, LED3.cathode, LED4.cathode, LED5.cathode, LED6.cathode, R15.Pin_1
  N8: IC1.IN4-, C2.-, R13.Pin_1
  OSC2: IC1.OUT4, Q2.B, C2.+, R14.Pin_1
  N9: Q1.C, R1.Pin_0, R2.Pin_0
  N10: R1.Pin_1, LED1.anode
  N11: R2.Pin_1, LED2.anode
  N12: LED3.anode, R8.Pin_1
  N13: LED4.anode, R9.Pin_1
  N14: LED5.anode, R11.Pin_1
  N15: LED6.anode, R10.Pin_1
  N16: R10.Pin_0, R11.Pin_0, Q2.C

custom parts:
  LM324: LM324 Quad OpAmp
