# Fritzing sketch Vc (saved by Fritzing 0.9.2b)
breadboards: 1

parts:
  Part1 = LilyPad Coin Cell Battery Holder
  LED1 = LED - 5mm [color="Yellow (595nm)" part_number="Candle Flicker" package="5 mm [THT]"]
  LED2 = LED - 5mm [color="Yellow (595nm)" part_number="Candle Flicker" package="5 mm [THT]"]
  LED3 = LED - 5mm [color="Yellow (595nm)" part_number="Candle Flicker" package="5 mm [THT]"]
  LED4 = LED - 5mm [color="Yellow (595nm)" part_number="Candle Flicker" package="5 mm [THT]"]

nets:
  GND: Part1.-, LED1.cathode, LED2.cathode, LED3.cathode, LED4.cathode
  N1: Part1.+, LED1.anode, LED2.anode, LED3.anode, LED4.anode
