# Fritzing sketch TornadoECR (saved by Fritzing 0.9.2b)
breadboards: 1

parts:
  1_5V = Battery
  L1 = Inductor [package="400 mil [THT]"]
  L2 = Inductor [package="400 mil [THT]"]
  Q1 = NPN-Transistor [part_number=2N3904 package="TO92 [THT]"]
  R1 = Resistor [tolerance=±5% resistance=1.2k package=THT]
  L3 = Inductor [package="400 mil [THT]"]
  LED1 = LED - 3mm [color="Orange (620nm)" package="3 mm [THT]"]
  LED2 = LED - 3mm [color="Orange (620nm)" package="3 mm [THT]"]

nets:
  GND: 1_5V.-, Q1.E
  N1: 1_5V.+, L1.pin_1, L2.pin_0
  N2: L1.pin_0, R1.Pin_0
  N3: L2.pin_1, Q1.C
  N4: Q1.B, R1.Pin_1
  N5: L3.pin_0, LED1.anode, LED2.cathode
  N6: L3.pin_1, LED1.cathode, LED2.anode

notes:
  1.5V
  coils wound around toroid
