# Fritzing sketch Module (saved by Fritzing 0.9.2b)
breadboards: 1

parts:
  U1 = attiny85 [package=dip]
  >3V = Power plug
  D1 = Zener Diode [part_number=1N4733 breakdown_voltage=5.1V package="Melf DO-213 AB [SMD]"]
  R1 = Resistor [tolerance=±5% resistance=100 package=THT]
  R2 = Resistor [tolerance=±5% resistance=10k package=THT]
  LED1 = LED - 5mm [color="Red (633nm)" package="5 mm [THT]"]
  RLED = Resistor [tolerance=±5% resistance=220 package=THT]
  Q1 = Basic FET N-Channel [part_number=2N7000 package="TO220 [THT]"]

nets:
  GND: U1.Pin_4, >3V.GND, D1.anode, Q1.source
  N1: U1.Pin_5, R2.Pin_0
  VCC: U1.Pin_8, D1.cathode, R1.Pin_1
  VIN: >3V.VCC, R1.Pin_0, RLED.Pin_0
  N2: R2.Pin_1, Q1.gate
  LED_SINK: LED1.cathode, Q1.drain
  N3: LED1.anode, RLED.Pin_1
