# Fritzing sketch TydiriumStrobe (saved by Fritzing 0.9.2b)
breadboards: 1

parts:
  U1 = attiny85 [package=dip]
  LED1 = LED - 3mm [color="White (4500K)" package="3 mm [THT]"]
  S1 = Toggle Switch [package=THT]
  R1 = Resistor [tolerance=±5% resistance=100 package=THT]
  LED2 = LED - 3mm [color="White (4500K)" package="3 mm [THT]"]
  R2 = Resistor [tolerance=±5% resistance=100 package=THT]
  LED3 = LED - 3mm [color="White (4500K)" package="3 mm [THT]"]
  LED4 = LED - 3mm [color="White (4500K)" package="3 mm [THT]"]
  LED5 = LED - 3mm [color="White (4500K)" package="3 mm [THT]"]
  LED6 = LED - 3mm [color="White (4500K)" package="3 mm [THT]"]
  LED7 = LED - 3mm [color="White (4500K)" package="3 mm [THT]"]
  R3 = Resistor [tolerance=±5% resistance=100 package=THT]
  R4 = Resistor [tolerance=±5% resistance=100 package=THT]
  R5 = Resistor [tolerance=±5% resistance=100 package=THT]
  R6 = Resistor [tolerance=±5% resistance=100 package=THT]
  Part1 = LilyPad Coin Cell Battery Holder

nets:
  GND: U1.Pin_4, LED1.cathode, S1.L2, LED2.cathode, R2.Pin_1, R3.Pin_1, R4.Pin_1, R5.Pin_1, R6.Pin_1
  LED_CTRL: U1.Pin_5, LED3.anode, LED4.anode, LED5.anode, LED6.anode, LED7.anode
  3V: U1.Pin_8, R1.Pin_1, Part1.+
  N1: LED1.anode, R1.Pin_0, LED2.anode
  N2: S1.COM, Part1.-
  N3: R2.Pin_0, LED3.cathode
  N4: LED4.cathode, R3.Pin_0
  N5: LED5.cathode, R4.Pin_0
  N6: LED6.cathode, R5.Pin_0
  N7: LED7.cathode, R6.Pin_0
