# Fritzing sketch UNCFDreadnought (saved by Fritzing 0.9.2b)
breadboards: 1

parts:
  R1 = Resistor [tolerance=±5% resistance=220 package=THT]
  LED1 = LED - 3mm [color="Blue (430nm)" package="3 mm [THT]"]
  R2 = Resistor [tolerance=±5% resistance=220 package=THT]
  R3 = Resistor [tolerance=±5% resistance=220 package=THT]
  LED2 = LED - 3mm [color="Red (633nm)" package="3 mm [THT]"]
  LED3 = LED - 3mm [color="Red (633nm)" package="3 mm [THT]"]
  LED4 = LED - 5mm [color="White (8000K)" package="5 mm [THT]"]
  JP1 = USB_MICROB_PLUG [package=micro-b-ra-th]
  R4 = Resistor [tolerance=±5% resistance=220 package=THT]
  LED5 = LED - 3mm [color="Yellow (574nm)" package="3 mm [THT]"]
  LED6 = LED - 3mm [color="Yellow (574nm)" package="3 mm [THT]"]
  R5 = Resistor [tolerance=±5% resistance=220 package=THT]
  LED7 = LED - 3mm [color="Yellow (574nm)" package="3 mm [THT]"]
  LED8 = LED - 3mm [color="Yellow (574nm)" package="3 mm [THT]"]
  LED9 = LED - 3mm [color="Yellow (574nm)" package="3 mm [THT]"]
  LED10 = LED - 3mm [color="Yellow (574nm)" package="3 mm [THT]"]
  LED11 = LED - 3mm [color="Yellow (574nm)" package="3 mm [THT]"]
  LED12 = LED - 3mm [color="Yellow (574nm)" package="3 mm [THT]"]

nets:
  5V: R1.Pin_0, R2.Pin_0, R3.Pin_0, JP1.VCC, R4.Pin_0, R5.Pin_0
  N1: R1.Pin_1, LED1.anode
  GND: LED1.cathode, LED2.cathode, LED3.cathode, LED4.cathode, JP1.GND, LED5.cathode, LED6.cathode, LED7.cathode, LED8.cathode, LED9.cathode, LED10.cathode, LED11.cathode, LED12.cathode
  N2: R2.Pin_1, LED2.anode, LED3.anode
  N3: R3.Pin_1, LED4.anode
  N4: R4.Pin_1, LED5.anode, LED6.anode
  N5: R5.Pin_1, LED7.anode, LED8.anode, LED9.anode, LED10.anode, LED11.anode, LED12.anode

notes:
  YF Wave Motion Engine
  YF Wave Motion Gun
  YF Portholes
  M22 Wave Motion Gun
  M22 Explosive Cloud
