# Fritzing sketch TeddyBearViking (saved by Fritzing 0.9.2b)
breadboards: 1

parts:
  CR2032 = LilyPad Coin Cell Battery Holder
  LED1 = LED - 5mm [color="Yellow (595nm)" part_number="Candle Flicker" package="5 mm [THT]"]

nets:
  N1: CR2032.-, LED1.cathode
  N2: CR2032.+, LED1.anode
