# Fritzing sketch WyLed (saved by Fritzing 0.9.2b)
breadboards: 2

parts:
  R1 = Resistor [tolerance=±5% resistance=10k package=THT]
  C1 = Electrolytic Capacitor [capacitance=220µF package="100 mil [THT, electrolytic]"]
  C2 = Ceramic Capacitor [capacitance=100nF package="100 mil [THT, multilayer]"]
  IC1 = IC, DIP package, 28 pins [chip_label=TM1638 part_number=TM1638]
  U1 = attiny85 [package=dip]
  5V = Power plug
  MIC2 = Microphone
  R6 = Resistor [tolerance=±5% resistance=10k package=THT]
  U3 = TL072/TLE2072 Dual Op. Amp [part_number=TL072 package="DIP8 [THT]"]
  C3 = Electrolytic Capacitor [capacitance=1µF package="100 mil [THT, electrolytic]"]
  R7 = Resistor [tolerance=±5% resistance=2.2k package=THT]
  R8 = Resistor [tolerance=±5% resistance=560k package=THT]
  R9 = Trimmer Potentiometer [maximum_resistance=100kΩ package=THT]
  U4 = SN74LS14N [package="DIP14 [THT]"]
  R10 = Resistor [tolerance=±5% resistance=4.7k package=THT]
  C4 = Electrolytic Capacitor [capacitance=10µF package="100 mil [THT, electrolytic]"]
  U5 = SMA420564 [part_number=SMA420564]
  Q1 = Basic FET N-Channel [part_number=2N7000 package="TO220 [THT]"]
  LED1 = LED - 3mm [color="Green (570nm)" package="3 mm [THT]"]
  R11 = Resistor [tolerance=±5% resistance=1.2k package=THT]
  R12 = Resistor [tolerance=±5% resistance=1.2k package=THT]
  LED2 = LED - 3mm [color="Green (570nm)" package="3 mm [THT]"]

nets:
  VCC: R1.Pin_0, C1.+, C2.1, IC1.pin4, U1.Pin_8, 5V.VCC, R6.Pin_0, U3.Pin_8, R9.leg2, U4.VCC, R11.Pin_0, LED2.anode
  MOSI: R1.Pin_1, IC1.pin26, U1.Pin_5
  GND: C1.-, C2.0, IC1.pin18, U1.Pin_4, 5V.GND, MIC2.pin2, U3.Pin_3, U3.Pin_4, R9.leg1, U4.GND, R10.Pin_0, C4.-, LED1.cathode, R12.Pin_0
  K1: IC1.pin1, Q1.source
  SEGA: IC1.pin5, U5.A, Q1.drain
  SEGB: IC1.pin6, U5.B
  SEGC: IC1.pin7, U5.C
  SEGD: IC1.pin8, U5.D
  SEGE: IC1.pin9, U5.E
  SEGF: IC1.pin10, U5.F
  SEGG: IC1.pin11, U5.G
  SEGDP: IC1.pin12, U5.dp
  DIG3: IC1.pin21, U5.D1
  DIG2: IC1.pin22, U5.D2
  DIG1: IC1.pin23, U5.D3
  DIG0: IC1.pin24, U5.D4
  SCK: IC1.pin27, U1.Pin_6
  CS: IC1.pin28, U1.Pin_7
  N1: MIC2.pin1, R6.Pin_1, C3.+
  N2: U3.Pin_1, U3.Pin_5, R8.Pin_1
  N3: U3.Pin_2, R7.Pin_1, R8.Pin_0
  N4: U3.Pin_6, R9.wiper
  N5: U3.Pin_7, U4.6A, R10.Pin_1, C4.+
  N6: C3.-, R7.Pin_0
  N7: U4.5Y, Q1.gate
  N8: U4.5A, U4.6Y
  N9: LED1.anode, R11.Pin_1
  N10: R12.Pin_1, LED2.cathode

notes:
  10x LED total (just for bling)
  LED bling (10 in total - 5 in each arrangement)

custom parts:
  TL072/TLE2072 Dual Op. Amp: The classic LM 358 Dual Operational Amplifier (Op-Amp). The analog swiss-army knife.
