# Fritzing sketch Receiver (saved by Fritzing 0.9.2b)
breadboards: 1

parts:
  RX_M2 = RF-LINK_RX [package=rf-link_rx]
  microSD2 = MicroSD Breakout
  Part2 = Arduino Nano (Rev3.0)
  RX_LED = LED - 3mm [color="Yellow (574nm)" package="3 mm [THT]"]
  RX_LED1 = LED - 3mm [color="White (8000K)" package="3 mm [THT]"]
  Q1 = Basic FET N-Channel [part_number=2N7000 package="TO220 [THT]"]
  R1 = Resistor [tolerance=±5% resistance=10k package=THT]
  R2 = Resistor [tolerance=±5% resistance=910 package=THT]
  R3 = Resistor [tolerance=±5% resistance=330 package=THT]
  IC1 = LM386 [package=dip08]
  R4 = Trimmer Potentiometer [maximum_resistance=10kΩ package=THT]
  C1 = Electrolytic Capacitor [capacitance=220µF package="100 mil [THT, electrolytic]"]
  SPKR1 = Loudspeaker
  Q3 = Basic FET P-Channel [part_number=BS250 package="DPak [SMD]"]
  R5 = Resistor [tolerance=±5% resistance=10k package=THT]
  C2 = Ceramic Capacitor [capacitance=47nF package="100 mil [THT, multilayer]"]
  R6 = Resistor [tolerance=±5% resistance=10 package=THT]
  C3 = Ceramic Capacitor [capacitance=100nF package="100 mil [THT, multilayer]"]
  C4 = Electrolytic Capacitor [capacitance=10µF package="100 mil [THT, electrolytic]"]
  C5 = Ceramic Capacitor [capacitance=100nF package="100 mil [THT, multilayer]"]
  PLAY = Pushbutton [part_number=N/C package=THT]

nets:
  GND: RX_M2.GND, microSD2.GND, Part2.GND, Q1.source, R1.Pin_0, IC1.-INPUT, IC1.GND, R4.leg1, SPKR1.pin2, R6.Pin_0, C3.1, C5.0, PLAY.leg1
  DATA_RX: RX_M2.DATA, Part2.D3
  5V: RX_M2.+5V, microSD2.5V, Part2.5V, RX_LED.anode, RX_LED1.anode, Q3.source, R5.Pin_0, C5.1
  N1: microSD2.CS, Part2.D10
  N2: microSD2.DI, Part2.D11/MOSI
  N3: microSD2.DO, Part2.D12/MISO
  N4: microSD2.CLK, Part2.D13/SCK
  N5: Part2.D2, PLAY.leg0
  LED_EN: Part2.D5, Q1.gate, R1.Pin_1
  AUDIO_EN: Part2.D6, Q3.Gate, R5.Pin_1
  AUDIO_OUT: Part2.D9, R4.leg2
  N6: RX_LED.cathode, R3.Pin_0
  N7: RX_LED1.cathode, R2.Pin_0
  N8: Q1.drain, R2.Pin_1, R3.Pin_1
  N9: IC1.GAIN, C4.-, C4.+
  N10: IC1.+INPUT, R4.wiper
  N11: IC1.Vout, C1.+, C2.1
  N12: IC1.Vs, Q3.drain, C3.0
  N13: C1.-, SPKR1.pin1
  N14: C2.0, R6.Pin_1

custom parts:
  MicroSD Breakout: 5V-ready microSD Breakout with Level Shifter
  LM386: low voltage audio power amplifier
