# Fritzing sketch Transmitter (saved by Fritzing 0.9.2b)
breadboards: 1

parts:
  TX_M1 = RF-LINK_TX [package=rf-link_tx]
  VPP = Battery block 9V
  Part2 = Arduino Nano (Rev3.0)
  R3 = Resistor [tolerance=±5% resistance=220 package=THT]
  LED1 = LED - 3mm [color="Blue (430nm)" package="3 mm [THT]"]
  Q1 = Basic FET P-Channel [part_number=BS250 package="DPak [SMD]"]
  R1 = Resistor [tolerance=±5% resistance=1M package=THT]
  TRIGGER = Pushbutton [package="[THT]"]
  R2 = Resistor [tolerance=±5% resistance=4.7k package=THT]
  C1 = Electrolytic Capacitor [capacitance=2.2µF package="100 mil [THT, electrolytic]"]
  Q2 = NPN-Transistor [part_number=2N3904 package="TO92 [THT]"]

nets:
  N1: TX_M1.DATA, Part2.D4
  GND: TX_M1.GND, VPP.-, Part2.GND, R3.Pin_1, TRIGGER.Pin_1, TRIGGER.Pin_2, C1.-, Q2.E
  VPP: TX_M1.+5V, Part2.VIN, Q1.drain
  9V: VPP.+, Q1.source, R1.Pin_0
  INDICATOR: Part2.D5, LED1.anode
  POWERHOLD: Part2.D6, R2.Pin_0
  5V: Part2.5V
  N2: R3.Pin_0, LED1.cathode
  N3: Q1.Gate, R1.Pin_1, TRIGGER.Pin_3, TRIGGER.Pin_4, C1.+, Q2.C
  N4: R2.Pin_1, Q2.B
