# Fritzing sketch arzamatron (saved by Fritzing 0.9.2b)
breadboards: 1

parts:
  Part1 = Arduino Uno (Rev3)
  Q1 = Basic FET N-Channel [package="D2Pak [SMD]"]
  Q2 = Basic FET N-Channel [package="D2Pak [SMD]"]
  STRIP2 = LED - 5mm [color="White (4500K)" package="5 mm [THT]"]
  STRIP1 = LED - 5mm [color="Blue (430nm)" package="5 mm [THT]"]
  R1 = Resistor [tolerance=±5% resistance=10k package=THT]
  R2 = Resistor [tolerance=±5% resistance=10k package=THT]
  12V = Power plug
  MIC1 = MAX4466 Electret Microphone Breakout Board
  R3 = Trimmer Potentiometer [maximum_resistance=100kΩ package=THT]
  U1 = Voltage Regulator - 5V [package="DPak [SMD]"]
  C1 = Electrolytic Capacitor [capacitance=22µF package="100 mil [THT, electrolytic]"]
  C2 = Ceramic Capacitor [capacitance=100nF package="100 mil [THT, multilayer]"]

nets:
  N1: Part1.A0, MIC1.out
  N2: Part1.A1, R3.wiper
  GND: Part1.GND, Q1.source, Q2.source, 12V.GND, MIC1.GND, R3.leg2, U1.GND, C1.-, C2.0
  N3: Part1.D5_PWM, R2.Pin_0
  N4: Part1.D6_PWM, R1.Pin_0
  5V: Part1.5V, MIC1.VCC, R3.leg1, U1.output_voltage, C1.+, C2.1
  N5: Q1.Gate, R2.Pin_1
  N6: Q1.drain, STRIP1.cathode
  N7: Q2.Gate, R1.Pin_1
  N8: Q2.drain, STRIP2.cathode
  12V: STRIP2.anode, STRIP1.anode, 12V.VCC, U1.input_voltage

custom parts:
  MAX4466 Electret Microphone Breakout Board: MAX4466 Electrec Microphone Breakout Board
