# Fritzing sketch lamp (saved by Fritzing 0.9.2b)
breadboards: 1

parts:
  CR2032 = LilyPad Coin Cell Battery Holder
  S1 = Toggle Switch [package=THT]
  4xSnowflakes = female pin header, 2 pins [form="♀ (female)"]

nets:
  GND: CR2032.-, 4xSnowflakes.pin2
  N1: CR2032.+, S1.COM
  N2: S1.L2, 4xSnowflakes.pin1

notes:
  connect to 4 snowflakes in parallel
