# Fritzing sketch LEDArrayDemos (saved by Fritzing 1.0.1rc)
breadboards: 1

parts:
  Part1 = Arduino Uno (Rev3)
  5V2A = Power plug
  LEDARRAY1 = Neopixel Strip -- White (30/m)
  R1 = Resistor [tolerance=±5% resistance=1k power=0.25W package=THT]
  C1 = Electrolytic Capacitor [capacitance=1mF voltage=35V package="100 mil [THT, electrolytic]"]

nets:
  GND: Part1.GND, 5V2A.GND, LEDARRAY1.GND, C1.-
  N1: Part1.D6_PWM, R1.Pin_1
  VCC: 5V2A.VCC, LEDARRAY1.+5V, C1.+
  N2: LEDARRAY1.DI, R1.Pin_0

notes:
  (or other)

custom parts:
  Neopixel Strip -- White (30/m): Neopixel Strip, White, 30 pixels per meter.
