# Fritzing sketch SimplestInverter (saved by Fritzing 0.9.0b)
breadboards: 1

parts:
  Part1 = Arduino Uno (Rev3)
  Q2 = NPN-Transistor [package="TO92 [THT]"]
  LED1 = LED - 5mm [color="Red (633nm)" package="5 mm [THT]"]
  R1 = Resistor [tolerance=±5% resistance=4.7k package=THT]
  R2 = Resistor [tolerance=±5% resistance=10k package=THT]

nets:
  N1: Part1.A0, Q2.C, LED1.anode, R1.Pin_1
  N2: Part1.D8, R2.Pin_0
  N3: Part1.5V, R1.Pin_0
  N4: Part1.GND, Q2.E, LED1.cathode
  N5: Q2.B, R2.Pin_1
