# Fritzing sketch LEDx16Module (saved by Fritzing 0.9.2b)
breadboards: 1

parts:
  IC1 = IC, DIP package, 16 pins [chip_label="OSHChip V1.0"]
  IC2 = IC, DIP package, 10 pins [chip_label=LEDx16]
  IC3 = IC, DIP package, 4 pins [chip_label=SMPS]
  VCC1 = Battery block 9V

nets:
  N1: IC1.pin4, IC2.pin8
  N2: IC1.pin6, IC2.pin10
  N3: IC1.pin7, IC2.pin9
  GND: IC1.pin8, IC2.pin7, IC3.pin2
  VCC: IC1.pin16, IC2.pin6, IC3.pin3
  N4: IC3.pin1, VCC1.-
  N5: IC3.pin4, VCC1.+
