# Fritzing sketch blinky (saved by Fritzing 0.9.2b)
breadboards: 1

parts:
  IC1 = IC, DIP package, 16 pins [chip_label="OSHChip V1.0"]
  3_3V = Power plug
  LED1 = LED - 3mm [color="Yellow (574nm)" package="3 mm [THT]"]
  R1 = Resistor [tolerance=±5% resistance=1k package=THT]

nets:
  N1: IC1.pin7, R1.Pin_0
  GND: IC1.pin8, 3_3V.GND
  VCC: IC1.pin16, 3_3V.VCC, LED1.anode
  N2: LED1.cathode, R1.Pin_1
