# Fritzing sketch GettingBlinky-patched (saved by Fritzing 1.0.1rc)
breadboards: 1

parts:
  IC1 = IC, DIP package, 8 pins [chip_label=PIC12 part_number=PIC12F675]
  P1 = female pin header, 6 pins [form="♀ (female)"]
  JP1 = Jumper [package=sj_2s]
  JP2 = Jumper [package=sj_2s]
  JP3 = Jumper [package=sj_2s]
  JP4 = Jumper [package=sj_2s]
  JP5 = Jumper [package=sj_2s]
  JP6 = Jumper [package=sj_2s]
  JP7 = Jumper [package=sj_2s]
  JP8 = Jumper [package=sj_2s]
  5V_Power = Power plug
  S1 = Pushbutton [package=THT]
  D1 = LED - 5mm [color="Red (633nm)" current=0.030A package="5 mm [THT]"]
  D2 = LED - 5mm [color="Red (633nm)" current=0.030A package="5 mm [THT]"]
  KEY1 = Pushbutton [package="[THT]"]
  KEY2 = Pushbutton [package="[THT]"]
  R1 = Resistor [tolerance=±5% resistance=1k power=0.25W package=THT]
  R2 = Resistor [tolerance=±5% resistance=1k power=0.25W package=THT]
  RESET = Pushbutton [package="[THT]"]
  R5 = Resistor [tolerance=±5% resistance=10k power=0.25W package=THT]
  C4 = Ceramic Capacitor [capacitance=100nF package="100 mil [THT, multilayer]"]
  C1 = Ceramic Capacitor [capacitance=47µF package="100 mil [THT, multilayer]"]
  C2 = Ceramic Capacitor [capacitance=100nF package="100 mil [THT, multilayer]"]
  R3 = Resistor [tolerance=±5% resistance=1k power=0.25W package=THT]
  D3 = LED - 5mm [color="Red (633nm)" current=0.030A package="5 mm [THT]"]
  R6 = Resistor [tolerance=±5% resistance=10k power=0.25W package=THT]
  R4 = Resistor [tolerance=±5% resistance=10k power=0.25W package=THT]
  VR1 = Trimmer Potentiometer [maximum_resistance=10kΩ knob_status=50% power=0.5W package=THT]

nets:
  VDD: IC1.pin1, P1.pin2, JP1.1, JP1.2, S1.leg0, R1.Pin_0, R2.Pin_0, R5.Pin_0, C1.1, C2.1, R3.Pin_0, R6.Pin_0, R4.Pin_0, VR1.leg2
  N1: IC1.pin2, JP2.2
  N2: IC1.pin3, JP3.2
  VPP: IC1.pin4, P1.pin1, JP4.2
  N3: IC1.pin5, JP5.1
  PGC: IC1.pin6, P1.pin5, JP6.1
  PGD: IC1.pin7, P1.pin4, JP7.1
  GND: IC1.pin8, P1.pin3, JP8.1, JP8.2, 5V_Power.GND, KEY1.Pin_1, KEY2.Pin_3, RESET.Pin_3, C4.0, C1.0, C2.0, D3.cathode, VR1.leg1
  N4: JP2.1, KEY2.Pin_1, KEY2.Pin_2, R4.Pin_1
  ADC: JP3.1, VR1.wiper
  N5: JP4.1, RESET.Pin_1, RESET.Pin_2, R5.Pin_1, C4.1
  N6: JP5.2, KEY1.Pin_3, R6.Pin_1
  N7: JP6.2, D2.cathode
  N8: JP7.2, D1.cathode
  N9: 5V_Power.VCC, S1.leg1
  N10: D1.anode, R1.Pin_1
  N11: D2.anode, R2.Pin_1
  N12: R3.Pin_1, D3.anode

notes:
  VPP-modified board design
  I haven't bothered to lay out the breadboard
