# Fritzing sketch GettingBlinky (saved by Fritzing 0.9.2b)
breadboards: 1

parts:
  IC1 = IC, DIP package, 8 pins [chip_label=PIC12 part_number=PIC12F675]
  P1 = female pin header, 6 pins [form="♀ (female)"]
  JP1 = Jumper [package=sj_2s]
  JP2 = Jumper [package=sj_2s]
  JP3 = Jumper [package=sj_2s]
  JP4 = Jumper [package=sj_2s]
  JP5 = Jumper [package=sj_2s]
  JP6 = Jumper [package=sj_2s]
  JP7 = Jumper [package=sj_2s]
  JP8 = Jumper [package=sj_2s]
  5V_Power = Power plug
  S1 = Pushbutton [package=THT]
  LED1 = LED - 5mm [color="Red (633nm)" package="5 mm [THT]"]
  LED2 = LED - 5mm [color="Red (633nm)" package="5 mm [THT]"]
  KEY1 = Pushbutton [package="[THT]"]
  KEY2 = Pushbutton [package="[THT]"]
  R1 = Resistor [tolerance=±5% resistance=1k package=THT]
  R2 = Resistor [tolerance=±5% resistance=1k package=THT]
  RESET = Pushbutton [package="[THT]"]
  R5 = Resistor [tolerance=±5% resistance=10k package=THT]
  C4 = Ceramic Capacitor [capacitance=100nF package="100 mil [THT, multilayer]"]
  C1 = Ceramic Capacitor [capacitance=47µF package="100 mil [THT, multilayer]"]
  C2 = Ceramic Capacitor [capacitance=100nF package="100 mil [THT, multilayer]"]
  R3 = Resistor [tolerance=±5% resistance=1k package=THT]
  LED3 = LED - 5mm [color="Red (633nm)" package="5 mm [THT]"]
  R6 = Resistor [tolerance=±5% resistance=10k package=THT]
  R4 = Resistor [tolerance=±5% resistance=10k package=THT]
  VR1 = Trimmer Potentiometer [maximum_resistance=10kΩ package=THT]

nets:
  VDD: IC1.pin1, P1.pin2, JP1.1, JP1.2, S1.leg0, R1.Pin_0, R2.Pin_0, R5.Pin_0, C1.1, C2.1, R3.Pin_0, R6.Pin_0, R4.Pin_0, VR1.leg2
  N1: IC1.pin2, JP2.2
  N2: IC1.pin3, JP3.2
  VPP(ALT): IC1.pin4, JP4.2
  N3: IC1.pin5, JP5.1
  PGC: IC1.pin6, P1.pin5, JP6.1
  PGD: IC1.pin7, P1.pin4, JP7.1
  GND: IC1.pin8, P1.pin3, JP8.1, JP8.2, 5V_Power.GND, KEY1.Pin_1, KEY2.Pin_3, RESET.Pin_3, C4.0, C1.0, C2.0, LED3.cathode, VR1.leg1
  VPP: P1.pin1, JP4.1, RESET.Pin_1, RESET.Pin_2, R5.Pin_1, C4.1
  N4: JP2.1, KEY2.Pin_1, KEY2.Pin_2, R4.Pin_1
  ADC: JP3.1, VR1.wiper
  N5: JP5.2, KEY1.Pin_3, R6.Pin_1
  N6: JP6.2, LED2.cathode
  N7: JP7.2, LED1.cathode
  N8: 5V_Power.VCC, S1.leg1
  N9: LED1.anode, R1.Pin_1
  N10: LED2.anode, R2.Pin_1
  N11: R3.Pin_1, LED3.anode

notes:
  Mod: connect VPP instead to VPP(ALT), so that it is not pumping voltage into the RESET filter
  I haven't bothered to lay out the breadboard
