# Fritzing sketch UsingC (saved by Fritzing 0.9.2b)
breadboards: 1

parts:
  IC1 = IC, DIP package, 8 pins [chip_label=PIC12 part_number=PIC12F675]
  PICKit = female pin header, 6 pins [form="♀ (female)"]
  5V_Power = Power plug
  LED1 = LED - 5mm [color="Red (633nm)" package="5 mm [THT]"]
  LED2 = LED - 5mm [color="Green (570nm)" package="5 mm [THT]"]
  R1 = Resistor [tolerance=±5% resistance=1k package=THT]
  R2 = Resistor [tolerance=±5% resistance=1k package=THT]

nets:
  VDD: IC1.pin1, PICKit.pin2, 5V_Power.VCC, R1.Pin_0, R2.Pin_0
  VPP: IC1.pin4, PICKit.pin1
  PGC: IC1.pin6, PICKit.pin5, LED2.cathode
  PGD: IC1.pin7, PICKit.pin4, LED1.cathode
  GND: IC1.pin8, PICKit.pin3, 5V_Power.GND
  N1: LED1.anode, R1.Pin_1
  N2: LED2.anode, R2.Pin_1

notes:
  PICkit
  5V Power (when PICkit not connected)
