# Fritzing sketch PIC16F84ABlinky (saved by Fritzing 0.9.2b)
breadboards: 1

parts:
  PICKit3 = female pin header, 6 pins [form="♀ (female)"]
  3-5V_Ext_Power = Power plug
  IC1 = IC, DIP package, 18 pins [chip_label=PIC16F84]
  XTAL1 = Crystal [frequency="4 MHz" package=THT]
  C1 = Ceramic Capacitor [capacitance=100nF package="100 mil [THT, multilayer]"]
  R1 = Resistor [tolerance=±5% resistance=10k package=THT]
  D1 = Rectifier Diode [part_number=1N5819 package="300 mil [THT]"]
  C2 = Ceramic Capacitor [capacitance=20pF package="100 mil [THT, multilayer]"]
  C3 = Ceramic Capacitor [capacitance=20pF package="100 mil [THT, multilayer]"]
  R2 = Resistor [tolerance=±5% resistance=620 package=THT]
  D2 = Rectifier Diode [part_number=1N5819 package="300 mil [THT]"]
  LED1 = LED - 3mm [color="White (8000K)" package="3 mm [THT]"]

nets:
  VPP: PICKit3.pin1, D2.anode
  VDD: PICKit3.pin2, 3-5V_Ext_Power.VCC, IC1.pin14, R1.Pin_1
  GND: PICKit3.pin3, 3-5V_Ext_Power.GND, IC1.pin5, C1.0, C2.0, C3.1, LED1.cathode
  PGD: PICKit3.pin4, IC1.pin13
  PGC: PICKit3.pin5, IC1.pin12
  RA3: IC1.pin2, R2.Pin_1
  N1: IC1.pin4, D1.cathode, D2.cathode
  N2: IC1.pin15, XTAL1.pin_1, C2.1
  N3: IC1.pin16, XTAL1.pin_0, C3.0
  N4: C1.1, R1.Pin_0, D1.anode
  N5: R2.Pin_0, LED1.anode

notes:
  NB: I haven't trusted/tested connecting external power while also having the PICKit connected at the same time
  PICKit3
  Optional External Power
