# Fritzing sketch TedsClock (saved by Fritzing 0.9.2b)
breadboards: 1

parts:
  IC1 = IC, DIP package, 18 pins [chip_label=PIC16F84]
  XTAL1 = Crystal [frequency="32 kHz" package=THT]
  R1 = Resistor [tolerance=±5% resistance=10k package=THT]
  C2 = Ceramic Capacitor [capacitance=100pF package="100 mil [THT, multilayer]"]
  C3 = Ceramic Capacitor [capacitance=100pF package="100 mil [THT, multilayer]"]
  C4 = Ceramic Capacitor [capacitance=100nF package="100 mil [THT, multilayer]"]
  3V = LilyPad Coin Cell Battery Holder
  LED1 = LED - 3mm [color="Yellow (585nm)" package="3 mm [THT]"]
  R2 = Resistor [tolerance=±5% resistance=180 package=THT]
  LED2 = LED - 3mm [color="Yellow (585nm)" package="3 mm [THT]"]
  R3 = Resistor [tolerance=±5% resistance=180 package=THT]
  LED3 = LED - 3mm [color="Yellow (585nm)" package="3 mm [THT]"]
  R4 = Resistor [tolerance=±5% resistance=180 package=THT]
  LED4 = LED - 3mm [color="Yellow (585nm)" package="3 mm [THT]"]
  R5 = Resistor [tolerance=±5% resistance=180 package=THT]
  LED5 = LED - 3mm [color="Yellow (585nm)" package="3 mm [THT]"]
  LED6 = LED - 3mm [color="Yellow (585nm)" package="3 mm [THT]"]
  R6 = Resistor [tolerance=±5% resistance=180 package=THT]
  R7 = Resistor [tolerance=±5% resistance=180 package=THT]
  LED7 = LED - 3mm [color="Yellow (585nm)" package="3 mm [THT]"]
  R8 = Resistor [tolerance=±5% resistance=180 package=THT]
  LED8 = LED - 3mm [color="Yellow (585nm)" package="3 mm [THT]"]
  R9 = Resistor [tolerance=±5% resistance=180 package=THT]
  S1 = Pushbutton [part_number="Hour Adjust" package="[THT]"]
  R10 = Resistor [tolerance=±5% resistance=180 package=THT]
  LED9 = LED - 3mm [color="Yellow (585nm)" package="3 mm [THT]"]
  R11 = Resistor [tolerance=±5% resistance=180 package=THT]
  LED10 = LED - 3mm [color="Yellow (585nm)" package="3 mm [THT]"]
  R12 = Resistor [tolerance=±5% resistance=180 package=THT]
  LED11 = LED - 3mm [color="Yellow (585nm)" package="3 mm [THT]"]
  LED12 = LED - 3mm [color="Yellow (585nm)" package="3 mm [THT]"]
  R13 = Resistor [tolerance=±5% resistance=180 package=THT]
  R14 = Resistor [tolerance=±5% resistance=1k package=THT]
  R15 = Resistor [tolerance=±5% resistance=1k package=THT]
  S2 = Pushbutton [part_number="Minute Adjust" package="[THT]"]
  R16 = Resistor [tolerance=±5% resistance=10k package=THT]
  R17 = Resistor [tolerance=±5% resistance=10k package=THT]

nets:
  N1: IC1.pin1, R13.Pin_1
  N2: IC1.pin2, S1.Pin_3, S1.Pin_4, R12.Pin_1
  N3: IC1.pin4, R1.Pin_0
  GND: IC1.pin5, C2.0, C3.1, C4.0, 3V.-, LED1.cathode, LED2.cathode, LED3.cathode, LED4.cathode, LED5.cathode, LED6.cathode, LED7.cathode, LED8.cathode, LED9.cathode, LED10.cathode, LED11.cathode, LED12.cathode, R16.Pin_1, R17.Pin_1
  N4: IC1.pin6, R11.Pin_1
  N5: IC1.pin7, R10.Pin_1
  N6: IC1.pin8, R9.Pin_1, S2.Pin_3, S2.Pin_4
  N7: IC1.pin9, R8.Pin_1
  N8: IC1.pin10, R7.Pin_1
  N9: IC1.pin11, R6.Pin_1
  N10: IC1.pin12, R5.Pin_1
  N11: IC1.pin13, R4.Pin_1
  VDD: IC1.pin14, R1.Pin_1, C4.1, 3V.+, R14.Pin_1, R15.Pin_1
  N12: IC1.pin15, XTAL1.pin_1, C2.1
  N13: IC1.pin16, XTAL1.pin_0, C3.0
  N14: IC1.pin17, R3.Pin_1
  N15: IC1.pin18, R2.Pin_1
  N16: LED1.anode, R2.Pin_0
  N17: LED2.anode, R3.Pin_0
  N18: LED3.anode, R4.Pin_0
  N19: LED4.anode, R5.Pin_0
  N20: LED5.anode, R6.Pin_0
  N21: LED6.anode, R7.Pin_0
  N22: LED7.anode, R8.Pin_0
  N23: LED8.anode, R9.Pin_0, R16.Pin_0
  N24: S1.Pin_1, S1.Pin_2, R14.Pin_0
  N25: R10.Pin_0, LED9.anode
  N26: R11.Pin_0, LED10.anode
  N27: R12.Pin_0, LED11.anode, R17.Pin_0
  N28: LED12.anode, R13.Pin_0
  N29: R15.Pin_0, S2.Pin_1, S2.Pin_2
