# Fritzing sketch OpAmpTransmitter (saved by Fritzing 0.9.2b)
breadboards: 1

parts:
  9V = Power plug
  C1 = Ceramic Capacitor [capacitance=100pF package="100 mil [THT, multilayer]"]
  R1 = Resistor [tolerance=±5% resistance=15k package=THT]
  R2 = Resistor [tolerance=±5% resistance=10k package=THT]
  R3 = Trimmer Potentiometer [maximum_resistance=10kΩ package=THT]
  R4 = Resistor [tolerance=±5% resistance=1k package=THT]
  R5 = Resistor [tolerance=±5% resistance=10k package=THT]
  C2 = Ceramic Capacitor [capacitance=1nF package="100 mil [THT, multilayer]"]
  R6 = Resistor [tolerance=±5% resistance=10k package=THT]
  C3 = Ceramic Capacitor [capacitance=100pF package="100 mil [THT, multilayer]"]
  ANT1 = Antenna
  R9 = Resistor [tolerance=±5% resistance=1M package=THT]
  TRS1 = Audio Jack (TRS) 3.5mm [package="PG203J [THT]"]
  IC1 = LM324 [part_number=LF347N package=dil16]
  Q1 = 2N7000 FET N-Channel [part_number=J201 package=TO92]
  R10 = Resistor [tolerance=±5% resistance=3.3k package=THT]
  C4 = Ceramic Capacitor [capacitance=100nF package="100 mil [THT, multilayer]"]
  R11 = Trimmer Potentiometer [maximum_resistance=10kΩ package=THT]
  C5 = Ceramic Capacitor [capacitance=47nF package="100 mil [THT, multilayer]"]
  R12 = Resistor [tolerance=±5% resistance=100k package=THT]
  C6 = Ceramic Capacitor [capacitance=100nF package="100 mil [THT, multilayer]"]
  C7 = Ceramic Capacitor [capacitance=10nF package="100 mil [THT, multilayer]"]

nets:
  GND: 9V.GND, C1.0, R2.Pin_1, R9.Pin_0, TRS1.Sleeve, IC1.GND, R10.Pin_0, R12.Pin_1, C6.1, C7.1
  VCC: 9V.VCC, R1.Pin_1, IC1.V+, Q1.drain, C6.0, C7.0
  N1: C1.1, R3.leg2, IC1.IN4-
  N2: R1.Pin_0, R2.Pin_0, R5.Pin_1, IC1.IN4+
  N3: R3.wiper, R4.Pin_0
  N4: R4.Pin_1, R5.Pin_0, C2.1, IC1.OUT4
  N5: C2.0, R6.Pin_0
  N6: R6.Pin_1, IC1.IN1+, R12.Pin_0
  N7: C3.0, IC1.OUT1
  N8: C3.1, ANT1.antenna_lead
  N9: R9.Pin_1, Q1.gate, C4.1
  N10: TRS1.Tip, C4.0
  N11: IC1.IN1-, R11.wiper
  N12: Q1.source, R10.Pin_1, C5.0
  N13: R11.leg1, C5.1

custom parts:
  LM324: LM324 Quad OpAmp
  2N7000 FET N-Channel: A 2N7000 MOSFET N-Channel Transistor
