# Fritzing sketch SimpleCrystalTransmitter (saved by Fritzing 0.9.2b)
breadboards: 1

parts:
  5V = Power plug
  IC1 = IC, DIP package, 14 pins [chip_label=MCO-1510A part_number=NCH060C]
  T1 = Transformer [package=transformer]
  AUDIO_IN = Audio Jack (TRS) 3.5mm [package="4Ucon 08780 [THT]"]
  C1 = Ceramic Capacitor [capacitance=100nF package="100 mil [THT, multilayer]"]
  L1 = Inductor [inductance=220µH package="400 mil [THT]"]
  C2 = Ceramic Capacitor [capacitance=560pF package="100 mil [THT, multilayer]"]
  C3 = Ceramic Capacitor [capacitance=47pF package="100 mil [THT, multilayer]"]
  ANT1 = Antenna

nets:
  GND: 5V.GND, IC1.pin7, C2.0, C3.0
  N1: 5V.VCC, T1.4
  N2: IC1.pin8, C1.0
  N3: IC1.pin14, T1.3
  N4: T1.1, AUDIO_IN.Sleeve
  N5: T1.2, AUDIO_IN.Tip
  N6: C1.1, L1.pin_0, C2.1
  N7: L1.pin_1, C3.1, ANT1.antenna_lead
