# Fritzing sketch SingleTransistorTransmitter (saved by Fritzing 0.9.2b)
breadboards: 1

parts:
  PS = Power plug [part_number=9V]
  Q1 = NPN-Transistor [part_number=S9013 package="TO92 [THT]"]
  L1 = Inductor [inductance=330µH package="400 mil [THT]"]
  L2 = Inductor [inductance=220µH package="400 mil [THT]"]
  ANT1 = Antenna
  R1 = Rotary Potentiometer (Small) [maximum_resistance=100kΩ package=THT]
  C2 = Ceramic Capacitor [capacitance=100nF package="100 mil [THT, multilayer]"]
  R2 = Resistor [tolerance=±5% resistance=10k package=THT]
  C3 = Ceramic Capacitor [capacitance=20pF package="100 mil [THT, multilayer]"]
  C4 = Variable Capacitor [capacitance=100nF max_capacitance=160pF min_capacitance=20pF voltage=35V]
  C1 = Electrolytic Capacitor [capacitance=100µF package="100 mil [THT, electrolytic]"]
  C5 = Ceramic Capacitor [capacitance=220pF package="100 mil [THT, multilayer]"]
  R3 = Resistor [tolerance=±5% resistance=3.3k package=THT]
  C6 = Ceramic Capacitor [capacitance=100nF package="100 mil [THT, multilayer]"]
  C7 = Ceramic Capacitor [capacitance=560pF package="100 mil [THT, multilayer]"]
  C8 = Ceramic Capacitor [capacitance=47pF package="100 mil [THT, multilayer]"]

nets:
  GND: PS.GND, L1.pin_1, R1.leg1, C1.-, R3.Pin_1, C7.1, C8.1
  N1: PS.VCC, Q1.C, R1.leg2, C1.+
  N2: Q1.E, C5.0, R3.Pin_0, C6.1
  N3: Q1.B, R2.Pin_1, C3.1, C4.1, C4.2, C5.1
  N4: L1.pin_0, C3.0, C4.0
  N5: L2.pin_0, C6.0, C7.0
  N6: L2.pin_1, ANT1.antenna_lead, C8.0
  N7: R1.wiper, C2.0, R2.Pin_0
  SIGNAL_IN: C2.1

notes:
  Signal In
