# Fritzing sketch SimplestDirectReceiver (saved by Fritzing 0.9.2b)
breadboards: 1

parts:
  Q1 = NPN-Transistor [part_number=S9014 package="TO92 [THT]"]
  Q2 = NPN-Transistor [part_number=S9014 package="TO92 [THT]"]
  C1 = Variable Capacitor [capacitance=100nF max_capacitance=20pF min_capacitance=5pF voltage=35V]
  5V = Power plug
  ANT1 = Antenna
  C2 = Ceramic Capacitor [capacitance=10pF package="100 mil [THT, multilayer]"]
  L1 = Inductor [inductance=0.54µH package="400 mil [THT]"]
  R1 = Resistor [tolerance=±5% resistance=22k package=THT]
  C3 = Ceramic Capacitor [capacitance=100nF package="100 mil [THT, multilayer]"]
  IC1 = LM386 [package=dip08]
  R2 = Trimmer Potentiometer [maximum_resistance=10kΩ package=THT]
  C4 = Electrolytic Capacitor [capacitance=100µF package="100 mil [THT, electrolytic]"]
  SPKR1 = Loudspeaker

nets:
  GND: Q1.E, Q2.E, 5V.GND, IC1.-INPUT, IC1.GND, R2.leg1, SPKR1.pin2
  N1: Q1.B, Q2.C, C1.0, L1.pin_1
  N2: Q1.C, C1.1, C2.0, L1.pin_0, R1.Pin_0
  N3: Q2.B, C3.0
  N4: 5V.VCC, R1.Pin_1, IC1.Vs
  N5: ANT1.antenna_lead, C2.1
  N6: C3.1, R2.leg2
  N7: IC1.+INPUT, R2.wiper
  N8: IC1.Vout, C4.+
  N9: C4.-, SPKR1.pin1

custom parts:
  LM386: low voltage audio power amplifier
