# Fritzing sketch SingleStageTransmitterKit (saved by Fritzing 0.9.2b)
breadboards: 1

parts:
  9V = Power plug
  S1 = Toggle Switch [package=THT]
  C1 = Ceramic Capacitor [capacitance=22nF package="100 mil [THT, multilayer]"]
  R1 = Resistor [tolerance=±5% resistance=10k package=THT]
  C2 = Electrolytic Capacitor [capacitance=10µF package="100 mil [THT, electrolytic]"]
  MIC1 = Microphone
  R2 = Resistor [tolerance=±5% resistance=27k package=THT]
  R3 = Resistor [tolerance=±5% resistance=4.7k package=THT]
  C3 = Ceramic Capacitor [capacitance=10nF package="100 mil [THT, multilayer]"]
  R4 = Resistor [tolerance=±5% resistance=270 package=THT]
  TR1 = NPN-Transistor [package="TO92 [THT]"]
  VC1 = Variable Capacitor [capacitance=100nF max_capacitance=10pF min_capacitance=2pF voltage=35V]
  COIL = Inductor [package="400 mil [THT]"]
  C4 = Ceramic Capacitor [capacitance=5pF package="100 mil [THT, multilayer]"]
  C5 = Ceramic Capacitor [capacitance=5pF package="100 mil [THT, multilayer]"]
  ANT1 = Antenna

nets:
  G/GND: 9V.GND, C1.1, MIC1.pin1, R3.Pin_1, C3.1, R4.Pin_1
  +B: 9V.VCC, S1.COM
  +9V: S1.L1, C1.0, R1.Pin_0, R2.Pin_0, VC1.1, VC1.2, COIL.pin_0
  N1: R1.Pin_1, C2.+, MIC1.pin2
  N2: C2.-, R2.Pin_1, R3.Pin_0, C3.0, TR1.B
  N3: R4.Pin_0, TR1.E, C4.1
  N4: TR1.C, VC1.0, COIL.pin_1, C4.0, C5.1
  ANT: C5.0, ANT1.antenna_lead
