# Fritzing sketch TEA5767 (saved by Fritzing 0.9.2b)
breadboards: 1

parts:
  Part1 = Arduino Uno (Rev3)
  IC1 = IC, DIP package, 10 pins [chip_label=TEA5767]
  ANT1 = Antenna
  R2 = Resistor [tolerance=±5% resistance=10k package=THT]
  R1 = Resistor [tolerance=±5% resistance=10k package=THT]
  TRS1 = Audio Jack (TRS) 3.5mm [package="4Ucon 08780 [THT]"]

nets:
  N1: Part1.A4/SDA, IC1.pin1, R1.Pin_1
  N2: Part1.A5/SCL, IC1.pin2, R2.Pin_1
  GND: Part1.GND, IC1.pin3, IC1.pin6, TRS1.Sleeve
  VCC: Part1.5V, IC1.pin5, R2.Pin_0, R1.Pin_0
  N3: IC1.pin7, TRS1.Ring
  N4: IC1.pin8, TRS1.Tip
  N5: IC1.pin10, ANT1.antenna_lead
