# Fritzing sketch ThreeStageTransmitter (saved by Fritzing 0.9.2b)
breadboards: 1

parts:
  R3 = Resistor [tolerance=±5% resistance=10k package=THT]
  C2 = Ceramic Capacitor [capacitance=100nF package="100 mil [THT, multilayer]"]
  C1 = Ceramic Capacitor [capacitance=22nF package="100 mil [THT, multilayer]"]
  C3 = Ceramic Capacitor [capacitance=1nF package="100 mil [THT, multilayer]"]
  C4 = Ceramic Capacitor [capacitance=33pF package="100 mil [THT, multilayer]"]
  C5 = Ceramic Capacitor [capacitance=15pF package="100 mil [THT, multilayer]"]
  C6 = Ceramic Capacitor [capacitance=10pF package="100 mil [THT, multilayer]"]
  C7 = Ceramic Capacitor [capacitance=15pF package="100 mil [THT, multilayer]"]
  C8 = Ceramic Capacitor [capacitance=22nF package="100 mil [THT, multilayer]"]
  ANT1 = Antenna [part_number=165cm]
  MIC1 = Microphone
  Q1 = NPN-Transistor [part_number=2N3904 package="TO92 [THT]"]
  Q2 = NPN-Transistor [part_number=2N3904 package="TO92 [THT]"]
  Q3 = NPN-Transistor [part_number=2N3904 package="TO92 [THT]"]
  L1 = Inductor [part_number=4T package="400 mil [THT]"]
  L2 = Inductor [inductance=1µH package="400 mil [THT]"]
  VCC = Battery block 9V
  R1 = Resistor [tolerance=±5% resistance=68k package=THT]
  R2 = Resistor [tolerance=±5% resistance=1M package=THT]
  R5 = Resistor [tolerance=±5% resistance=100 package=THT]
  R6 = Resistor [tolerance=±5% resistance=68k package=THT]
  R4 = Resistor [tolerance=±5% resistance=47k package=THT]
  C9 = Ceramic Capacitor [capacitance=33pF package="100 mil [THT, multilayer]"]
  R7 = Resistor [tolerance=±5% resistance=2.2k package=THT]
  LED1 = LED - 3mm [color="Green (570nm)" package="3 mm [THT]"]
  S1 = Toggle Switch [package=THT]

nets:
  N1: R3.Pin_0, C4.1, C8.1, L1.pin_0, L2.pin_0, R1.Pin_1, R6.Pin_0, R4.Pin_0, C9.1, R7.Pin_0, S1.L1
  N2: R3.Pin_1, C2.0, Q1.C, R2.Pin_1
  N3: C2.1, C3.1, Q2.B, R4.Pin_1
  N4: C1.0, MIC1.pin2, R1.Pin_0
  N5: C1.1, Q1.B, R2.Pin_0
  N6: C3.0, C8.0, MIC1.pin1, Q1.E, Q3.E, VCC.-, R5.Pin_1, LED1.cathode
  N7: C4.0, C5.1, C6.1, Q2.C, L1.pin_1, C9.0
  N8: C5.0, Q2.E, R5.Pin_0
  N9: C6.0, Q3.B, R6.Pin_1
  N10: C7.0, Q3.C, L2.pin_1
  N11: C7.1, ANT1.antenna_lead
  N12: VCC.+, S1.COM
  N13: R7.Pin_1, LED1.anode

notes:
  pre-amp
  100MHz Oscillator
  RF Output
