# Fritzing sketch TwoStageTransmitter (saved by Fritzing 0.9.2b)
breadboards: 1

parts:
  R4 = Resistor [tolerance=±5% resistance=10k package=THT]
  C1 = Ceramic Capacitor [capacitance=100nF package="100 mil [THT, multilayer]"]
  C2 = Ceramic Capacitor [capacitance=100nF package="100 mil [THT, multilayer]"]
  C5 = Ceramic Capacitor [capacitance=4pF package="100 mil [THT, multilayer]"]
  ANT1 = Antenna [part_number=165cm]
  MIC1 = Microphone
  Q1 = NPN-Transistor [part_number=2N3904 package="TO92 [THT]"]
  Q2 = NPN-Transistor [part_number=2N3904 package="TO92 [THT]"]
  L1 = Inductor [inductance=0.11µH package="400 mil [THT]"]
  VCC = Battery block 9V
  R1 = Resistor [tolerance=±5% resistance=10k package=THT]
  R2 = Resistor [tolerance=±5% resistance=1M package=THT]
  R5 = Resistor [tolerance=±5% resistance=100 package=THT]
  R6 = Resistor [tolerance=±5% resistance=10k package=THT]
  R3 = Resistor [tolerance=±5% resistance=100k package=THT]
  C3 = Ceramic Capacitor [capacitance=10nF package="100 mil [THT, multilayer]"]
  C4 = Variable Capacitor [capacitance=100nF max_capacitance=430pF min_capacitance=10pF voltage=35V]
  R7 = Resistor [tolerance=±5% resistance=1k package=THT]
  C6 = Electrolytic Capacitor [capacitance=10µF package="100 mil [THT, electrolytic]"]
  C7 = Ceramic Capacitor [capacitance=100nF package="100 mil [THT, multilayer]"]

nets:
  N1: R4.Pin_0, C2.1, Q1.C
  N2: R4.Pin_1, L1.pin_0, VCC.+, R1.Pin_1, R2.Pin_1, R6.Pin_1, C3.0, C4.1, C6.+, C7.1
  N3: C1.0, MIC1.pin2, R1.Pin_0
  N4: C1.1, Q1.B, R2.Pin_0, R3.Pin_0
  N5: C2.0, Q2.B, R6.Pin_0, C3.1
  N6: C5.0, ANT1.antenna_lead, Q2.C, L1.pin_1, C4.0
  N7: C5.1, Q2.E, R7.Pin_1
  GND: MIC1.pin1, VCC.-, R5.Pin_0, R3.Pin_1, R7.Pin_0, C6.-, C7.0
  N8: Q1.E, R5.Pin_1
