# Fritzing sketch HamClock (saved by Fritzing 1.0.1rc)
breadboards: 1

parts:
  Raspberry_Pi1 = Raspberry Pi B+
  LED1 = LED - 3mm [color="White (8000K)" current=0.030A package="3 mm [THT]"]
  R1 = Resistor [tolerance=±5% power=0.25W resistance=1k package=THT]
  R2 = Resistor [tolerance=±5% power=0.25W resistance=10k package=THT]
  GY-BME280-3_3_Module1 = female pin header, 6 pins [form="♀ (female)"]
  LED2 = LED - 3mm [color="Yellow (592nm)" current=0.030A package="3 mm [THT]"]
  R3 = Resistor [tolerance=±5% power=0.25W resistance=10k package=THT]
  R4 = Resistor [tolerance=±5% power=0.25W resistance=1k package=THT]
  S1 = Pushbutton [package="[THT]"]
  LED3 = LED - 3mm [color="Green (555nm)" current=0.030A package="3 mm [THT]"]
  R5 = Resistor [tolerance=±5% power=0.25W resistance=20k package=THT]
  R6 = Resistor [tolerance=±5% power=0.25W resistance=680 package=THT]
  LED4 = LED - 3mm [color="Red (633nm)" current=0.030A package="3 mm [THT]"]
  R7 = Resistor [tolerance=±5% power=0.25W resistance=20k package=THT]
  R8 = Resistor [tolerance=±5% power=0.25W resistance=1.2k package=THT]
  S2 = Pushbutton [package="[THT]"]
  S3 = Pushbutton [package="[THT]"]

nets:
  3.3V: Raspberry_Pi1.3v3, GY-BME280-3_3_Module1.pin1, R5.Pin_1, R6.Pin_1, R7.Pin_1, R8.Pin_1
  SDA: Raspberry_Pi1.GPIO2, GY-BME280-3_3_Module1.pin4
  SCL: Raspberry_Pi1.GPIO3, GY-BME280-3_3_Module1.pin3
  AL_2: Raspberry_Pi1.GPIO5, S1.Pin_3, S1.Pin_4
  AL_1: Raspberry_Pi1.GPIO6, R3.Pin_1, R4.Pin_1
  CD_2: Raspberry_Pi1.GPIO13, LED4.cathode, R7.Pin_0
  CD_3: Raspberry_Pi1.GPIO19, LED3.cathode, R5.Pin_0
  CD_4: Raspberry_Pi1.GPIO26, S2.Pin_3, S2.Pin_4
  OA_1: Raspberry_Pi1.GPIO21, S3.Pin_3, S3.Pin_4
  SA_1: Raspberry_Pi1.GPIO20, R1.Pin_1, R2.Pin_1
  GND: Raspberry_Pi1.GND, LED1.cathode, R2.Pin_0, GY-BME280-3_3_Module1.pin2, LED2.cathode, R3.Pin_0, S1.Pin_1, S1.Pin_2, S2.Pin_1, S2.Pin_2, S3.Pin_1, S3.Pin_2
  N1: LED1.anode, R1.Pin_0
  CSB: GY-BME280-3_3_Module1.pin5
  SDO: GY-BME280-3_3_Module1.pin6
  N2: LED2.anode, R4.Pin_0
  N3: LED3.anode, R6.Pin_0
  N4: LED4.anode, R8.Pin_0

notes:
  Satellite Up
  GY-BME280-3.3 Module
  Alarm
  Countdown Timer
  Silence Alarm
  Restart Timer
  On the Air
  Reset Timer
