# Fritzing sketch SimpleDemo (saved by Fritzing 1.0.1rc)
breadboards: 2

parts:
  TX_M1 = RF-LINK_TX [package=rf-link_tx]
  RX_M2 = RF-LINK_RX [package=rf-link_rx]
  5V = Power plug
  5V_2 = Power plug
  HT12E = IC, DIP package, 18 pins [chip_label=HT12E]
  SW1 = DIP SWITCH [package=dipswitch-02]
  SW2 = DIP SWITCH [package=dipswitch-02]
  S1 = Pushbutton [package="[THT]"]
  R1 = Resistor [tolerance=±5% power=0.25W resistance=1M package=THT]
  HT12D = IC, DIP package, 18 pins [chip_label=HT12D]
  R2 = Resistor [tolerance=±5% power=0.25W resistance=47k package=THT]
  LED1 = LED - 3mm [color="Green (555nm)" current=0.030A package="3 mm [THT]"]
  LED2 = LED - 3mm [color="Green (555nm)" current=0.030A package="3 mm [THT]"]
  LED3 = LED - 3mm [color="Green (555nm)" current=0.030A package="3 mm [THT]"]
  LED4 = LED - 3mm [color="Green (555nm)" current=0.030A package="3 mm [THT]"]
  R3 = Resistor [tolerance=±5% power=0.25W resistance=1k package=THT]
  LED5 = LED - 3mm [color="Red (633nm)" current=0.030A package="3 mm [THT]"]
  R4 = Resistor [tolerance=±5% power=0.25W resistance=1k package=THT]

nets:
  N1: TX_M1.DATA, HT12E.pin17
  TX_GND: TX_M1.GND, 5V_2.GND, HT12E.pin3, HT12E.pin9, SW1.1, SW1.2, SW2.1, SW2.2, S1.Pin_3, S1.Pin_4
  TX_VCC: TX_M1.+5V, 5V_2.VCC, HT12E.pin18
  RX_GND: RX_M2.GND, 5V.GND, HT12D.pin3, HT12D.pin9, R4.Pin_0
  N2: RX_M2.DATA, HT12D.pin14
  RX_VCC: RX_M2.+5V, 5V.VCC, HT12D.pin18, R3.Pin_1
  N3: HT12E.pin10, SW2.3
  N4: HT12E.pin11, SW2.4
  N5: HT12E.pin12, SW1.3
  N6: HT12E.pin13, SW1.4
  N7: HT12E.pin14, S1.Pin_1, S1.Pin_2
  N8: HT12E.pin15, R1.Pin_0
  N9: HT12E.pin16, R1.Pin_1
  N10: HT12D.pin10, LED1.cathode
  N11: HT12D.pin11, LED2.cathode
  N12: HT12D.pin12, LED3.cathode
  N13: HT12D.pin13, LED4.cathode
  N14: HT12D.pin15, R2.Pin_0
  N15: HT12D.pin16, R2.Pin_1
  VT: HT12D.pin17, LED5.anode
  N16: LED1.anode, LED2.anode, LED3.anode, LED4.anode, R3.Pin_0
  N17: LED5.cathode, R4.Pin_1

notes:
  Transmitter
  Receiver
