# Fritzing sketch RFDoorbell (saved by Fritzing 0.9.2b)
breadboards: 2

parts:
  TX_M1 = RF-LINK_TX [package=rf-link_tx]
  RX_M2 = RF-LINK_RX [package=rf-link_rx]
  TX_S1 = Pushbutton [package="[THT]"]
  TX_R2 = Resistor [tolerance=±5% resistance=1k package=THT]
  TX_VCC1 = Battery block 9V
  RX_R2 = Resistor [tolerance=±5% resistance=12k package=THT]
  RX_R1 = Resistor [tolerance=±5% resistance=6k part_number=12kΩ||12kΩ package=THT]
  C1 = Ceramic Capacitor [capacitance=100nF package="100 mil [THT, multilayer]"]
  C2 = Electrolytic Capacitor [capacitance=1µF package="100 mil [THT, electrolytic]"]
  TX_LED = LED - 3mm [color="Blue (430nm)" package="3 mm [THT]"]
  IC1 = LM741 [package=dip08]
  C3 = Ceramic Capacitor [capacitance=1µF package="100 mil [THT, multilayer]"]
  5V = Power plug
  R1 = Resistor [tolerance=±5% resistance=100k package=THT]
  2N3904 = NPN-Transistor [package="TO92 [THT]"]
  HS-088 = female pin header, 5 pins [form="♀ (female)"]
  SPKR1 = Loudspeaker
  R2 = Resistor [tolerance=±5% resistance=47 part_number=0- package=THT]

nets:
  N1: TX_M1.DATA, TX_M1.+5V, TX_S1.Pin_1, TX_S1.Pin_2, TX_LED.anode
  N2: TX_M1.GND, TX_R2.Pin_0, TX_VCC1.-
  GND: RX_M2.GND, RX_R2.Pin_0, C1.1, C2.-, IC1.V-, 5V.GND, R1.Pin_0, 2N3904.E, HS-088.pin2
  N3: RX_M2.DATA, C1.0, C2.+, IC1.+INPUT
  5V: RX_M2.+5V, RX_R1.Pin_1, IC1.V+, 5V.VCC, HS-088.pin1, R2.Pin_0
  N4: TX_S1.Pin_3, TX_S1.Pin_4, TX_VCC1.+
  N5: TX_R2.Pin_1, TX_LED.cathode
  N6: RX_R2.Pin_1, RX_R1.Pin_0, IC1.-INPUT
  N7: IC1.+OFFSET, IC1.NC
  N8: IC1.OUTPUT, C3.0
  N9: C3.1, R1.Pin_1, HS-088.pin5
  N10: 2N3904.B, HS-088.pin3
  N11: 2N3904.C, HS-088.pin4, SPKR1.pin1
  N12: SPKR1.pin2, R2.Pin_1

notes:
  HS-088

custom parts:
  LM741: General Purpose Operational Amplifier
