# Fritzing sketch RFSwitch_LowPowerTx (saved by Fritzing 1.0.1rc)
breadboards: 2

parts:
  TX_M1 = RF-LINK_TX [package=rf-link_tx]
  RX_M2 = RF-LINK_RX [package=rf-link_rx]
  TX_S1 = Pushbutton [package="[THT]"]
  TX_R1 = Resistor [tolerance=±5% resistance=10k power=0.25W package=THT]
  TX_R2 = Resistor [tolerance=±5% resistance=1k power=0.25W package=THT]
  TX_LED = LED - 5mm [color="Green (555nm)" current=0.030A package="5 mm [THT]"]
  TX_VCC1 = Battery block 9V
  RX_IC1 = LM324 [package=dil16]
  RX_LED = LED - 5mm [color="Green (555nm)" current=0.030A package="5 mm [THT]"]
  RX_R1 = Resistor [tolerance=±5% resistance=1k power=0.25W package=THT]
  RX_R3 = Resistor [tolerance=±5% resistance=10k power=0.25W package=THT]
  RX_R2 = Resistor [tolerance=±5% resistance=4.7k power=0.25W package=THT]
  C1 = Ceramic Capacitor [capacitance=100nF package="100 mil [THT, multilayer]"]
  C2 = Electrolytic Capacitor [capacitance=1µF package="100 mil [THT, electrolytic]"]
  5V = Power plug

nets:
  N1: TX_M1.DATA, TX_M1.+5V, TX_S1.Pin_1, TX_S1.Pin_2, TX_R1.Pin_1, TX_LED.anode
  N2: TX_M1.GND, TX_R1.Pin_0, TX_R2.Pin_0, TX_VCC1.-
  GND: RX_M2.GND, RX_IC1.GND, RX_R1.Pin_0, RX_R3.Pin_0, C1.1, C2.-, 5V.GND
  N3: RX_M2.DATA, RX_IC1.IN4+, C1.0, C2.+
  +5V: RX_M2.+5V, RX_IC1.V+, RX_R2.Pin_1, 5V.VCC
  N4: TX_S1.Pin_3, TX_S1.Pin_4, TX_VCC1.+
  N5: TX_R2.Pin_1, TX_LED.cathode
  N6: RX_IC1.IN4-, RX_R3.Pin_1, RX_R2.Pin_0
  N7: RX_IC1.OUT4, RX_LED.anode
  N8: RX_LED.cathode, RX_R1.Pin_1

notes:
  Transmitter
  Receiver

custom parts:
  LM324: LM324 Quad OpAmp
