# Fritzing sketch RFSwitchASK (saved by Fritzing 0.9.0b)
breadboards: 2

parts:
  TX_M1 = RF-LINK_TX [package=rf-link_tx]
  RX_M2 = RF-LINK_RX [package=rf-link_rx]
  TX_R1 = Resistor [tolerance=±5% resistance=1k package=THT]
  TX_LED = LED - 5mm [color="Blue (430nm)" package="5 mm [THT]"]
  TX_VCC1 = Battery block 9V
  RX_LED = LED - 5mm [color="Blue (430nm)" package="5 mm [THT]"]
  RX_R1 = Resistor [tolerance=±5% resistance=1k package=THT]
  Part1 = Arduino Uno (Rev3)
  Part2 = Arduino Nano (Rev3.0)

nets:
  N1: TX_M1.DATA, Part2.D12/MISO
  GND: TX_M1.GND, TX_R1.Pin_1, TX_VCC1.-, Part2.GND
  +5V: TX_M1.+5V, Part2.5V
  GND_2: RX_M2.GND, RX_R1.Pin_0, Part1.GND
  N2: RX_M2.DATA, Part1.D11_PWM/MOSI
  +5V_2: RX_M2.+5V, Part1.5V
  N3: TX_R1.Pin_0, TX_LED.cathode
  N4: TX_LED.anode, Part2.D6
  N5: TX_VCC1.+, Part2.VIN
  N6: RX_LED.cathode, RX_R1.Pin_1
  N7: RX_LED.anode, Part1.D6_PWM
