# Fritzing sketch RemoteControl2202J (saved by Fritzing 1.0.7)
breadboards: 1

parts:
  R1 = Relay [part_number=FRS1B-S package=THT]
  R2 = Relay [part_number=FRS1B-S package=THT]
  Power = Power plug
  LED1 = LED - 3mm [color="Red (633nm)" current=0.030A package="3 mm [THT]"]
  R1_2 = Resistor [tolerance=±5% power=0.25W resistance=1k package=THT]
  R2_2 = Resistor [tolerance=±5% power=0.25W resistance=1k package=THT]
  LED2 = LED - 3mm [color="Green (555nm)" current=0.030A package="3 mm [THT]"]
  R3 = Resistor [tolerance=±5% power=0.25W resistance=1k package=THT]
  LED3 = LED - 3mm [color="Red (633nm)" current=0.030A package="3 mm [THT]"]
  R4 = Resistor [tolerance=±5% power=0.25W resistance=1k package=THT]
  LED4 = LED - 3mm [color="Green (555nm)" current=0.030A package="3 mm [THT]"]

nets:
  NO1: R1.A, LED2.cathode
  COM1/COM2/GND: R1.C1, R1.C2, R2.C1, R2.C2, Power.GND
  NC1: R1.B, LED1.cathode
  NO2: R2.A, LED4.cathode
  NC2: R2.B, LED3.cathode
  5V: Power.VCC, R1_2.Pin_0, R2_2.Pin_0, R3.Pin_0, R4.Pin_0
  N1: LED1.anode, R1_2.Pin_1
  N2: R2_2.Pin_1, LED2.anode
  N3: R3.Pin_1, LED3.anode
  N4: R4.Pin_1, LED4.anode

notes:
  2022J Relays
  2022J Relay 1
  2022J Relay 2
