# Fritzing sketch CodePracticeOscillator (saved by Fritzing 0.9.2b)
breadboards: 1

parts:
  5V = Power plug
  R1 = Trimmer Potentiometer [maximum_resistance=10kΩ package=THT]
  Q1 = PNP-Transistor [part_number=2N3906 package="TO92 [THT]"]
  Q2 = NPN-Transistor [part_number=2N3904 package="TO92 [THT]"]
  S1 = Pushbutton [package=THT]
  J1 = Piezo Speaker
  C1 = Ceramic Capacitor [capacitance=100nF package="100 mil [THT, multilayer]"]
  R2 = Resistor [tolerance=±5% resistance=47k package=THT]
  R3 = Resistor [tolerance=±5% resistance=1k package=THT]

nets:
  GND: 5V.GND, Q2.E, J1.pin1
  N1: 5V.VCC, Q1.E, S1.leg0
  N2: R1.leg1, R1.wiper, S1.leg1
  N3: R1.leg2, R2.Pin_0
  N4: Q1.B, Q2.C
  N5: Q1.C, J1.pin2, R3.Pin_1
  N6: Q2.B, C1.1, R2.Pin_1
  N7: C1.0, R3.Pin_0
