# Fritzing sketch RandomCodePractice (saved by Fritzing 0.9.2b)
breadboards: 1

parts:
  Part1 = Arduino Uno (Rev3)
  DISPLAY = LCD screen 16x2 IIC [part_number="1602 LCD I2C"]
  SPEED_SELECT = Rotary Potentiometer (Small) [maximum_resistance=100kΩ package=THT]
  PIEZO1 = Piezo Speaker
  CHARACTER_MODE = Toggle Switch [part_number="SPDT Centre Off" package=THT]
  R1 = Resistor [tolerance=±5% resistance=10k package=THT]
  R2 = Resistor [tolerance=±5% resistance=10k package=THT]

nets:
  N1: Part1.A0, SPEED_SELECT.wiper
  N2: Part1.A1, CHARACTER_MODE.COM, R1.Pin_1, R2.Pin_0
  N3: Part1.A4/SDA, DISPLAY.SDA
  N4: Part1.A5/SCL, DISPLAY.SCL
  N5: Part1.D11_PWM/MOSI, PIEZO1.pin2
  5V: Part1.5V, DISPLAY.VCC, SPEED_SELECT.leg2, CHARACTER_MODE.L2, R1.Pin_0
  GND: Part1.GND, DISPLAY.GND, SPEED_SELECT.leg1, PIEZO1.pin1, CHARACTER_MODE.L1, R2.Pin_1

custom parts:
  LCD screen 16x2 IIC: LCD screen with HD44780 controller enables showing text, symbols, value or anything else that comes from Croduino/Arduino. It is capable of showing 16 symbols in two lines and therefore can be used in many projects that need to send clearly visible and legible output information.. • Color of symbols: White • Backlight: Blue • Dimensions: 80 x 36 x 12 mm • Screen dimensions: 64.5 x 16 mm •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
