# Fritzing sketch RandomCodePractice_v2 (saved by Fritzing 1.0.7)
breadboards: 1

parts:
  DISPLAY = LCD screen 16x2 IIC [part_number="1602 LCD I2C"]
  SPEED_SELECT = Rotary Potentiometer (Small) [maximum_resistance=100kΩ knob_status=50% power=0.5W package=THT]
  PIEZO1 = Piezo Speaker
  CHARACTER_MODE = Toggle Switch [part_number="SPDT Centre Off" package=THT]
  R1 = Resistor [tolerance=±5% resistance=10k power=0.25W package=THT]
  R2 = Resistor [tolerance=±5% resistance=10k power=0.25W package=THT]
  Part2 = Arduino Nano (Rev3.0)
  U1 = AUDIO-JACK2 [package=audio-jack]

nets:
  GND: DISPLAY.GND, SPEED_SELECT.leg1, PIEZO1.pin1, CHARACTER_MODE.L1, R2.Pin_1, Part2.GND, U1.SLEEVE
  5V: DISPLAY.VCC, SPEED_SELECT.leg2, CHARACTER_MODE.L2, R1.Pin_0, Part2.5V
  SDA: DISPLAY.SDA, Part2.A4
  SCL: DISPLAY.SCL, Part2.A5
  SPEED: SPEED_SELECT.wiper, Part2.A0
  OUT_BYPASS: PIEZO1.pin2, U1.TSH
  MODE: CHARACTER_MODE.COM, R1.Pin_1, R2.Pin_0, Part2.A1
  OUT: Part2.D11/MOSI, U1.TIP

custom parts:
  LCD screen 16x2 IIC: LCD screen with HD44780 controller enables showing text, symbols, value or anything else that comes from Croduino/Arduino. It is capable of showing 16 symbols in two lines and therefore can be used in many projects that need to send clearly visible and legible output information.. • Color of symbols: White • Backlight: Blue • Dimensions: 80 x 36 x 12 mm • Screen dimensions: 64.5 x 16 mm •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
