# Fritzing sketch About (saved by Fritzing 1.0.1rc)
breadboards: 1

parts:
  Mod2 = Raspberry Pi Pico
  R1 = Resistor [tolerance=±5% resistance=2k power=0.25W package="0603 [SMD]"]
  LED1 = smd LED [color="Red (633nm)" current=0.030A package="0603 [SMD]"]
  R2 = Resistor [tolerance=±5% resistance=2k power=0.25W package="0603 [SMD]"]
  LED2 = smd LED [color="Red (633nm)" current=0.030A package="0603 [SMD]"]
  LED3 = smd LED [color="Red (633nm)" current=0.030A package="0603 [SMD]"]
  R3 = Resistor [tolerance=±5% resistance=2k power=0.25W package="0603 [SMD]"]
  R4 = Resistor [tolerance=±5% resistance=2k power=0.25W package="0603 [SMD]"]
  LED4 = smd LED [color="Red (633nm)" current=0.030A package="0603 [SMD]"]
  LED5 = smd LED [color="Red (633nm)" current=0.030A package="0603 [SMD]"]
  R5 = Resistor [tolerance=±5% resistance=2k power=0.25W package="0603 [SMD]"]
  LED6 = smd LED [color="Red (633nm)" current=0.030A package="0603 [SMD]"]
  R6 = Resistor [tolerance=±5% resistance=2k power=0.25W package="0603 [SMD]"]
  LED7 = smd LED [color="Red (633nm)" current=0.030A package="0603 [SMD]"]
  R7 = Resistor [tolerance=±5% resistance=2k power=0.25W package="0603 [SMD]"]

nets:
  GND: Mod2.pin_3, Mod2.pin_8, Mod2.pin_13, Mod2.pin_18, Mod2.pin_23, Mod2.pin_28, Mod2.pin_33, Mod2.pin_38, R1.Pin_1, R2.Pin_1, R3.Pin_1, R4.Pin_1, R5.Pin_1, R6.Pin_1, R7.Pin_1
  GP7: Mod2.pin_10, LED1.anode
  GP8: Mod2.pin_11, LED2.anode
  GP9: Mod2.pin_12, LED3.anode
  GP10: Mod2.pin_14, LED4.anode
  GP11: Mod2.pin_15, LED5.anode
  GP12: Mod2.pin_16, LED6.anode
  GP13: Mod2.pin_17, LED7.anode
  N1: R1.Pin_0, LED1.cathode
  N2: R2.Pin_0, LED2.cathode
  N3: LED3.cathode, R3.Pin_0
  N4: R4.Pin_0, LED4.cathode
  N5: LED5.cathode, R5.Pin_0
  N6: LED6.cathode, R6.Pin_0
  N7: LED7.cathode, R7.Pin_0

custom parts:
  Raspberry Pi Pico: Raspberry Pi Pico. Based around the RP2040 microcontroller the Pico is a low cost microcontroller device bringing Raspberry Pi quality, cost, and easy of use to the microcontroller space. Jan 2021, Split part in to two versions: tht (this one) and SMD. This one will drill holes for a .1 in header in pcb to allow plugging in the module as well as providing pads to solder the module to the top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
