# Fritzing sketch About (saved by Fritzing 1.0.1rc)
breadboards: 1

parts:
  Mod3 = Raspberry Pi Pico W
  Part1 = LCD1602-I2C
  BB2 = 4-Line Bi-Directional Level Shifter

nets:
  GND: Mod3.pin_3, Mod3.pin_8, Mod3.pin_13, Mod3.pin_18, Mod3.pin_23, Mod3.pin_28, Mod3.pin_33, Mod3.pin_38, Part1.GND, BB2.GND#16
  SDA-LV: Mod3.pin_6, BB2.A1
  SCL-LV: Mod3.pin_7, BB2.A2
  3V3: Mod3.pin_36, BB2.LV
  VBUS: Mod3.pin_40, Part1.VCC, BB2.HV
  SDA: Part1.SDA, BB2.B1
  SCL: Part1.SCL, BB2.B2

custom parts:
  Raspberry Pi Pico W: Raspberry Pi Pico W. Based around the RP2040 microcontroller the Pico W is a low cost microcontroller device bringing Raspberry Pi quality, cost, and easy of use to the microcontroller space. The areas marked KEEPOUT in pcb silkscreen should not have traces running through them to avoid shorts on a soldered in module!
  LCD1602-I2C: A standard character display, usually with 2x16 characters. Comes in many colors with LCM1602 IIC attached.
  4-Line Bi-Directional Level Shifter: 4-Channel Bi-Directional Level Shifter
