# Fritzing sketch i2c (saved by Fritzing 1.0.1rc)
breadboards: 1

parts:
  Raspberry_Pi1 = Raspberry Pi B+
  GY-BME280-3_3_Module1 = female pin header, 6 pins [form="♀ (female)"]
  GY-BMP180-3_3_Module2 = female pin header, 6 pins [form="♀ (female)"]

nets:
  3.3V/SDO2: Raspberry_Pi1.3v3, GY-BME280-3_3_Module1.pin1, GY-BMP180-3_3_Module2.pin1, GY-BMP180-3_3_Module2.pin6
  SDA: Raspberry_Pi1.GPIO2, GY-BME280-3_3_Module1.pin4, GY-BMP180-3_3_Module2.pin4
  SCL: Raspberry_Pi1.GPIO3, GY-BME280-3_3_Module1.pin3, GY-BMP180-3_3_Module2.pin3
  GND: Raspberry_Pi1.GND, GY-BME280-3_3_Module1.pin2, GY-BMP180-3_3_Module2.pin2
  CSB1: GY-BME280-3_3_Module1.pin5
  SDO1: GY-BME280-3_3_Module1.pin6
  CSB2: GY-BMP180-3_3_Module2.pin5

notes:
  GY-BME280-3.3 Module
  addr 0x76
  GY-BMP180-3.3 Module
  addr 0x77
