# Fritzing sketch rust (saved by Fritzing 1.0.1rc)
breadboards: 1

parts:
  Raspberry_Pi1 = Raspberry Pi B+
  LED1 = LED - 3mm [color="Red (633nm)" current=0.030A package="3 mm [THT]"]
  R1 = Resistor [tolerance=±5% power=0.25W resistance=1k package=THT]

nets:
  GND: Raspberry_Pi1.GND, LED1.cathode
  N1: Raspberry_Pi1.GPIO23, R1.Pin_1
  N2: LED1.anode, R1.Pin_0
