# Fritzing sketch BluePill (saved by Fritzing 0.9.2b)
breadboards: 1

parts:
  Part2 = BluePill
  Part3 = FTDI Basic Programmer

nets:
  GND3: Part2.GND3, Part3.GND
  N1: Part2.5V, Part3.POWER
  N2: Part2.A10, Part3.TXO
  N3: Part2.A9, Part3.RXI
