# Fritzing sketch 2d6-ATtiny85-final (saved by Fritzing 1.0.7)
breadboards: 1

parts:
  R1 = Resistor [tolerance=±5% resistance=10k power=0.25W package=THT]
  C1 = Electrolytic Capacitor [capacitance=10µF voltage=35V package="100 mil [THT, electrolytic]"]
  C2 = Ceramic Capacitor [capacitance=100nF voltage=35V package="100 mil [THT, multilayer]"]
  7_Segment1 = 7 Segment Display
  7_Segment0 = 7 Segment Display
  IC1 = IC, DIP package, 28 pins [chip_label=TM1638 part_number=TM1638]
  S1-ROLL = Pushbutton [package="[THT]"]
  D1 = Rectifier Diode [part_number=1N4148 package="300 mil [THT]"]
  D2 = Rectifier Diode [part_number=1N4148 package="300 mil [THT]"]
  S2-1d6/2d6 = Toggle Switch [package=THT]
  U1 = attiny85 [package=dip]
  REG1 = IC, DIP package, 6 pins [chip_label="Boost Converter"]
  BATT1 = BATTERY-2 [package=battery-aa]
  S3-POWER = Toggle Switch [package=THT]

nets:
  VCC: R1.Pin_0, C1.+, C2.1, IC1.pin4, U1.Pin_8, REG1.pin6
  MOSI: R1.Pin_1, IC1.pin26, U1.Pin_6
  GND: C1.-, C2.0, IC1.pin18, U1.Pin_4, REG1.pin5, BATT1.-1
  SEGG: 7_Segment1.Segment_A#1, 7_Segment0.Segment_A#1, IC1.pin11
  SEGF: 7_Segment1.Segment_F, 7_Segment0.Segment_F, IC1.pin10
  SEGE: 7_Segment1.Segment_E, 7_Segment0.Segment_E, IC1.pin9
  SEGD: 7_Segment1.Segment_D, 7_Segment0.Segment_D, IC1.pin8
  SEGDP: 7_Segment1.Segment_DP, 7_Segment0.Segment_DP, IC1.pin12
  SEGC: 7_Segment1.Segment_C, 7_Segment0.Segment_C, IC1.pin7
  DIG1: 7_Segment1.common_cathode#8, IC1.pin23
  SEGB: 7_Segment1.Segment_B, 7_Segment0.Segment_B, IC1.pin6, D2.anode
  SEGA: 7_Segment1.Segment_A#10, 7_Segment0.Segment_A#10, IC1.pin5, D1.anode
  DIG0: 7_Segment0.common_cathode#8, IC1.pin24
  K1: IC1.pin1, S1-ROLL.Pin_1, S1-ROLL.Pin_2, S2-1d6/2d6.L2
  SCK: IC1.pin27, U1.Pin_7
  CS: IC1.pin28, U1.Pin_5
  N1: S1-ROLL.Pin_3, S1-ROLL.Pin_4, D1.cathode
  N2: D2.cathode, S2-1d6/2d6.COM
  N3: REG1.pin4, S3-POWER.L1
  N4: BATT1.+1, S3-POWER.COM
