# Fritzing sketch BasicDemoCycle (saved by Fritzing 0.9.2b)
breadboards: 1

parts:
  Part1 = Arduino Uno (Rev3)
  U1 = AD9833 Module

nets:
  PROBE: Part1.A0, U1.OUT
  N1: Part1.D10_PWM/SS, U1.FSYNC
  N2: Part1.D11_PWM/MOSI, U1.SDATA
  N3: Part1.D13/SCK, U1.SCLK
  VCC: Part1.5V, U1.VCC
  GND: Part1.GND, U1.DGND, U1.AGND

custom parts:
  AD9833 Module: programmable waveform generator
