# Fritzing sketch ATmegaBreadboard (saved by Fritzing 0.9.2b)
breadboards: 1

parts:
  U1 = atmega328 [package=dip]
  XTAL1 = Crystal [frequency="16 Mhz" package=THT]
  C1 = Ceramic Capacitor [capacitance=22pF package="100 mil [THT, multilayer]"]
  C2 = Ceramic Capacitor [capacitance=22pF package="100 mil [THT, multilayer]"]
  R1 = Resistor [tolerance=±5% resistance=10k package=THT]
  5V = Power plug
  RESET = Pushbutton [package="[THT]"]

nets:
  N1: U1.RESET, R1.Pin_1, RESET.Pin_1, RESET.Pin_2
  vcc: U1.VCC, U1.AVCC, R1.Pin_0, 5V.VCC
  GND: U1.GND, C1.0, C2.1, 5V.GND, RESET.Pin_3, RESET.Pin_4
  N2: U1.XLAT1, XTAL1.pin_1, C2.0
  N3: U1.XLAT2, XTAL1.pin_0, C1.1
