# Fritzing sketch ATmegaISPShield (saved by Fritzing 0.9.2b)
breadboards: 1

parts:
  Part1 = Arduino Uno (Rev3)
  U1 = atmega328 [package=dip]
  XTAL1 = Crystal [frequency="16 Mhz" package=THT]
  C1 = Ceramic Capacitor [capacitance=22pF package="100 mil [THT, multilayer]"]
  C2 = Ceramic Capacitor [capacitance=22pF package="100 mil [THT, multilayer]"]
  R4 = Resistor [tolerance=±5% resistance=10k package=THT]
  LED1 = LED - 3mm [color="Green (570nm)" package="3 mm [THT]"]
  LED2 = LED - 3mm [color="Green (570nm)" package="3 mm [THT]"]
  LED3 = LED - 3mm [color="Green (570nm)" package="3 mm [THT]"]
  R1 = Resistor [tolerance=±5% resistance=2.2k package=THT]
  R2 = Resistor [tolerance=±5% resistance=2.2k package=THT]
  R3 = Resistor [tolerance=±5% resistance=2.2k package=THT]

nets:
  N1: Part1.D10_PWM/SS, U1.RESET, R4.Pin_1
  N2: Part1.D11_PWM/MOSI, U1.D11_(PWM), LED3.anode
  N3: Part1.D12/MISO, U1.D12, LED2.anode
  N4: Part1.D13/SCK, U1.D13, LED1.anode
  GND: Part1.GND, U1.GND, C1.0, C2.1, R1.Pin_1, R2.Pin_1, R3.Pin_1
  vcc: Part1.5V, U1.VCC, U1.AVCC, R4.Pin_0
  N5: U1.XLAT1, XTAL1.pin_1, C2.0
  N6: U1.XLAT2, XTAL1.pin_0, C1.1
  N7: LED1.cathode, R1.Pin_0
  N8: LED2.cathode, R2.Pin_0
  N9: LED3.cathode, R3.Pin_0
