# Fritzing sketch ATmegaSerialProgrammer (saved by Fritzing 0.9.2b)
breadboards: 1

parts:
  U1 = atmega328 [package=dip]
  XTAL1 = Crystal [frequency="16 Mhz" package=THT]
  C1 = Ceramic Capacitor [capacitance=22pF package="100 mil [THT, multilayer]"]
  C2 = Ceramic Capacitor [capacitance=22pF package="100 mil [THT, multilayer]"]
  R1 = Resistor [tolerance=±5% resistance=10k package=THT]
  ALT_5V = Power plug
  RESET = Pushbutton [package="[THT]"]
  R2 = Resistor [tolerance=±5% resistance=1k package=THT]
  LED1 = LED - 3mm [color="Blue (430nm)" package="3 mm [THT]"]
  Part1 = FTDI Basic Programmer
  C3 = Ceramic Capacitor [capacitance=100nF package="100 mil [THT, multilayer]"]

nets:
  N1: U1.RESET, R1.Pin_1, RESET.Pin_1, RESET.Pin_2, C3.0
  TXD: U1.D0_(RX), Part1.TXO
  RXD: U1.D1_(TX), Part1.RXI
  vcc: U1.VCC, U1.AVCC, R1.Pin_0, ALT_5V.VCC, Part1.POWER
  GND: U1.GND, C1.0, C2.1, ALT_5V.GND, RESET.Pin_3, RESET.Pin_4, LED1.cathode, Part1.GND
  N2: U1.XLAT1, XTAL1.pin_0, C1.1
  N3: U1.XLAT2, XTAL1.pin_1, C2.0
  N4: U1.D13, R2.Pin_0
  N5: R2.Pin_1, LED1.anode
  DTR: Part1.DTR, C3.1
