# Fritzing sketch ATmegaViaArduinoISP (saved by Fritzing 0.9.2b)
breadboards: 1

parts:
  Part1 = Arduino Uno (Rev3)
  U1 = atmega328 [package=dip]
  XTAL1 = Crystal [frequency="16 Mhz" package=THT]
  C1 = Ceramic Capacitor [capacitance=22pF package="100 mil [THT, multilayer]"]
  C2 = Ceramic Capacitor [capacitance=22pF package="100 mil [THT, multilayer]"]
  R1 = Resistor [tolerance=±5% resistance=10k package=THT]
  ICSP = shrouded pin header, 6 pins [form="♂ (shrouded male)"]

nets:
  RESET: Part1.D10_PWM/SS, U1.RESET, R1.Pin_1, ICSP.pin3
  MOSI: Part1.D11_PWM/MOSI, U1.D11_(PWM), ICSP.pin5
  MISO: Part1.D12/MISO, U1.D12, ICSP.pin1
  SCK: Part1.D13/SCK, U1.D13, ICSP.pin2
  GND: Part1.GND, U1.GND, C1.0, C2.1, ICSP.pin4
  vcc: Part1.5V, U1.VCC, U1.AVCC, R1.Pin_0, ICSP.pin6
  N1: U1.XLAT1, XTAL1.pin_1, C2.0
  N2: U1.XLAT2, XTAL1.pin_0, C1.1

notes:
  optional ICSP connector
