# Fritzing sketch FlickeringFireEffect (saved by Fritzing 0.9.2b)
breadboards: 1

parts:
  U3 = attiny85 [package=dip]
  3-5V = Power plug
  Q1 = Basic FET N-Channel [part_number=2N7000 package="DPak [SMD]"]
  R1 = Resistor [tolerance=±5% resistance=470 package=THT]
  C1 = Electrolytic Capacitor [capacitance=470µF package="100 mil [THT, electrolytic]"]
  C2 = Ceramic Capacitor [capacitance=100nF package="100 mil [THT, multilayer]"]
  R2 = Trimmer Potentiometer [maximum_resistance=100kΩ package=THT]
  R3 = Resistor [tolerance=±5% resistance=470 package=THT]
  LED1 = LED - 3mm [color="Red (633nm)" package="3 mm [THT]"]
  Q2 = Basic FET N-Channel [part_number=2N7000 package="DPak [SMD]"]
  R4 = Resistor [tolerance=±5% resistance=470 package=THT]
  R5 = Resistor [tolerance=±5% resistance=470 package=THT]
  LED2 = LED - 3mm [color="Red (633nm)" package="3 mm [THT]"]
  Q3 = Basic FET N-Channel [part_number=2N7000 package="DPak [SMD]"]
  R6 = Resistor [tolerance=±5% resistance=470 package=THT]
  R7 = Resistor [tolerance=±5% resistance=470 package=THT]
  LED3 = LED - 3mm [color="Red (633nm)" package="3 mm [THT]"]

nets:
  PWM1: U3.Pin_3, R1.Pin_0
  GND: U3.Pin_4, 3-5V.GND, Q1.source, C1.-, C2.0, R2.leg1, Q2.source, Q3.source
  PWM3: U3.Pin_5, R6.Pin_0
  PWM2: U3.Pin_6, R4.Pin_0
  N1: U3.Pin_7, R2.wiper
  VCC: U3.Pin_8, 3-5V.VCC, C1.+, C2.1, R2.leg2, LED1.anode, LED2.anode, LED3.anode
  N2: Q1.Gate, R1.Pin_1
  N3: Q1.drain, R3.Pin_1
  N4: R3.Pin_0, LED1.cathode
  N5: Q2.Gate, R4.Pin_1
  N6: Q2.drain, R5.Pin_1
  N7: R5.Pin_0, LED2.cathode
  N8: Q3.Gate, R6.Pin_1
  N9: Q3.drain, R7.Pin_1
  N10: R7.Pin_0, LED3.cathode
