# Fritzing sketch HardwareInterrupt (saved by Fritzing 0.9.2b)
breadboards: 1

parts:
  Part1 = Arduino Uno (Rev3)
  U2 = attiny85 [package=dip]
  R1 = Resistor [tolerance=±5% resistance=1k package=THT]
  LED1 = LED - 5mm [color="Green (555nm)" package="5 mm [THT]"]
  S1 = Pushbutton [package="[THT]"]
  R2 = Resistor [tolerance=±5% resistance=10k package=THT]

nets:
  SS: Part1.D10_PWM/SS, U2.Pin_1
  MOSI: Part1.D11_PWM/MOSI, U2.Pin_5
  MISO: Part1.D12/MISO, U2.Pin_6
  SCK: Part1.D13/SCK, U2.Pin_7, S1.Pin_3, S1.Pin_4, R2.Pin_0
  GND: Part1.GND, U2.Pin_4, R1.Pin_0, R2.Pin_1
  vcc: Part1.5V, U2.Pin_8, S1.Pin_1, S1.Pin_2
  N1: U2.Pin_3, LED1.anode
  N2: R1.Pin_1, LED1.cathode

notes:
  Arduino Uno as ISP
  After uploading code with the Uno ISP, it may be detached and power of 1.8-5.5V supplied to the ATtiny rails
