# Fritzing sketch PinChangeInterrupts (saved by Fritzing 0.9.2b)
breadboards: 1

parts:
  U2 = attiny85 [package=dip]
  LED1 = LED - 3mm [color="White (8000K)" package="3 mm [THT]"]
  R1 = Resistor [tolerance=±5% resistance=1k package=THT]
  Power_plug1 = Power plug
  S1 = Pushbutton [package="[THT]"]

nets:
  N1: U2.Pin_2, S1.Pin_1, S1.Pin_2
  GND: U2.Pin_4, R1.Pin_0, Power_plug1.GND, S1.Pin_3, S1.Pin_4
  N2: U2.Pin_5, LED1.anode
  VCC: U2.Pin_8, Power_plug1.VCC
  N3: LED1.cathode, R1.Pin_1
