# Fritzing sketch ProgrammingWithArduinoISP (saved by Fritzing 0.9.0b)
breadboards: 1

parts:
  Part1 = Arduino Uno (Rev3)
  U2 = attiny85 [package=dip]

nets:
  N1: Part1.D10_PWM/SS, U2.Pin_1
  N2: Part1.D11_PWM/MOSI, U2.Pin_5
  N3: Part1.D12/MISO, U2.Pin_6
  N4: Part1.D13/SCK, U2.Pin_7
  GND: Part1.GND, U2.Pin_4
  vcc: Part1.5V, U2.Pin_8
