# Fritzing sketch PwmMotorControl (saved by Fritzing 0.9.2b)
breadboards: 1

parts:
  U3 = attiny85 [package=dip]
  5V = Power plug
  M1 = DC Motor
  D1 = Rectifier Diode [part_number=1N4001 package="300 mil [THT]"]
  Q1 = Basic FET N-Channel [part_number=2N7000 package="DPak [SMD]"]
  R1 = Resistor [tolerance=±5% resistance=220 package=THT]
  C1 = Electrolytic Capacitor [capacitance=470µF package="100 mil [THT, electrolytic]"]
  C2 = Ceramic Capacitor [capacitance=100nF package="100 mil [THT, multilayer]"]
  R2 = Trimmer Potentiometer [maximum_resistance=10kΩ package=THT]

nets:
  GND: U3.Pin_4, 5V.GND, Q1.source, C1.-, C2.0, R2.leg1
  N1: U3.Pin_5, R1.Pin_0
  N2: U3.Pin_7, R2.wiper
  VCC: U3.Pin_8, 5V.VCC, M1.pin_1, D1.cathode, C1.+, C2.1, R2.leg2
  N3: M1.pin_2, D1.anode, Q1.drain
  N4: Q1.Gate, R1.Pin_1
