# Fritzing sketch BasicDemo (saved by Fritzing 0.9.2b)
breadboards: 1

parts:
  OLED1 = 128x32 I2C Monochrome OLED Display
  R1 = Resistor [tolerance=±5% resistance=10k package=THT]
  R2 = Resistor [tolerance=±5% resistance=10k package=THT]
  3_3V = Power plug
  U1 = attiny85 [package=dip]

nets:
  SDA: OLED1.SDA, R2.Pin_1, U1.Pin_5
  SCL: OLED1.SCL, R1.Pin_1, U1.Pin_7
  GND: OLED1.GND, 3_3V.GND, U1.Pin_4
  VCC: OLED1.3.3V, R1.Pin_0, R2.Pin_0, 3_3V.VCC, U1.Pin_8
