# Fritzing sketch SoftwarePWM (saved by Fritzing 0.9.2b)
breadboards: 1

parts:
  U3 = attiny85 [package=dip]
  5V = Power plug
  LED3 = LED - 5mm [color="Red (633nm)" package="5 mm [THT]"]
  LED2 = LED - 5mm [color="Red (633nm)" package="5 mm [THT]"]
  LED1 = LED - 5mm [color="Red (633nm)" package="5 mm [THT]"]
  R3 = Resistor [tolerance=±5% resistance=1k package=THT]
  R2 = Resistor [tolerance=±5% resistance=1k package=THT]
  R1 = Resistor [tolerance=±5% resistance=1k package=THT]

nets:
  GND: U3.Pin_4, 5V.GND, R3.Pin_1, R2.Pin_1, R1.Pin_1
  CH2-PB0: U3.Pin_5, LED1.anode
  CH1-PB1: U3.Pin_6, LED2.anode
  CH3-PB2: U3.Pin_7, LED3.anode
  VCC: U3.Pin_8, 5V.VCC
  N1: LED3.cathode, R3.Pin_0
  N2: LED2.cathode, R2.Pin_0
  N3: LED1.cathode, R1.Pin_0

notes:
  CH1 PB1
  CH2 PB0
  CH3 PB2
