# Fritzing sketch TinyBlink (saved by Fritzing 1.0.7)
breadboards: 1

parts:
  U2 = attiny85 [package=dip]
  LED1 = LED - 3mm [color="Green (555nm)" current=0.030A package="3 mm [THT]"]
  LED2 = LED - 3mm [color="Blue (430nm)" current=0.030A package="3 mm [THT]"]
  R1 = Resistor [tolerance=±5% resistance=1k power=0.25W package=THT]
  5V = Power plug

nets:
  GND: U2.Pin_4, R1.Pin_0, 5V.GND
  N1: U2.Pin_5, LED2.anode
  N2: U2.Pin_6, LED1.anode
  VCC: U2.Pin_8, 5V.VCC
  N3: LED1.cathode, LED2.cathode, R1.Pin_1
