# Fritzing sketch TotalSleep (saved by Fritzing 1.0.7)
breadboards: 1

parts:
  U2 = attiny85 [package=dip]
  R3 = Resistor [tolerance=±5% resistance=1k power=0.25W package=THT]
  RESET = Pushbutton [package="[THT]"]
  C1 = Ceramic Capacitor [capacitance=220nF voltage=35V package="100 mil [THT, multilayer]"]
  LED1 = LED - 3mm [color="Red (633nm)" current=0.030A package="3 mm [THT]"]
  R1 = Resistor [tolerance=±5% power=0.25W resistance=1M package=THT]
  Q1 = Basic FET P-Channel [part_number=BS250 package="DPak [SMD]"]
  R2 = Resistor [tolerance=±5% power=0.25W resistance=4.7k package=THT]
  Power_plug1 = Power plug
  Q2 = NPN-Transistor [part_number=2N3904 package="TO92 [THT]"]
  LED2 = LED - 3mm [color="Green (555nm)" current=0.030A package="3 mm [THT]"]
  R4 = Resistor [tolerance=±5% resistance=1k power=0.25W package=THT]
  CH1 = Multimeter straight red probe
  CH2 = Multimeter straight red probe
  CH3 = Multimeter straight red probe
  CH4 = Multimeter straight red probe

nets:
  N1: U2.Pin_3, LED1.anode
  GND: U2.Pin_4, R3.Pin_0, RESET.Pin_1, RESET.Pin_2, C1.0, Power_plug1.GND, Q2.E, R4.Pin_0
  POWER_EN: U2.Pin_5, R2.Pin_1, CH3.Probe_tip_2
  VDD: U2.Pin_8, Q1.drain, LED2.anode, CH2.Probe_tip_2
  N2: R3.Pin_1, LED1.cathode
  N3: RESET.Pin_3, RESET.Pin_4, C1.1, R1.Pin_0, Q1.Gate, Q2.C, CH4.Probe_tip_2
  5V: R1.Pin_1, Q1.source, Power_plug1.VCC, CH1.Probe_tip_2
  N4: R2.Pin_0, Q2.B
  N5: LED2.cathode, R4.Pin_1

notes:
  CH1
  CH2
  CH3
  CH4
