# Fritzing sketch ATtinyProgrammingShield (saved by Fritzing 0.9.2b)
breadboards: 1

parts:
  Part1 = Arduino Uno (Rev3)
  U2 = attiny85 [package=dip]
  R1 = Resistor [tolerance=±5% resistance=1k package=THT]
  LED1 = LED - 3mm [color="Red (633nm)" package="3 mm [THT]"]
  LED2 = LED - 3mm [color="Green (555nm)" package="3 mm [THT]"]

nets:
  N1: Part1.D10_PWM/SS, U2.Pin_1
  N2: Part1.D11_PWM/MOSI, U2.Pin_5, LED2.anode
  N3: Part1.D12/MISO, U2.Pin_6, LED1.anode
  N4: Part1.D13/SCK, U2.Pin_7
  GND: Part1.GND, U2.Pin_4, R1.Pin_1
  vcc: Part1.5V, U2.Pin_8
  N5: R1.Pin_0, LED1.cathode, LED2.cathode
