# Fritzing sketch AnalogComparator (saved by Fritzing 0.9.2b)
breadboards: 1

parts:
  Part1 = Arduino Uno (Rev3)
  R1 = Resistor [tolerance=±5% resistance=10k package=THT]
  R2 = Resistor [tolerance=±5% resistance=10k package=THT]
  R3 = Photocell (LDR) [package=THT]
  R4 = Resistor [tolerance=±5% resistance=3.3k package=THT]
  R5 = Resistor [tolerance=±5% resistance=1k package=THT]
  LED1 = LED - 3mm [color="Green (570nm)" package="3 mm [THT]"]

nets:
  N1: Part1.D8, LED1.anode
  AIN0: Part1.D6_PWM, R3.pin_0, R4.Pin_1
  AIN1: Part1.D7, R1.Pin_1, R2.Pin_0
  VCC: Part1.5V, R1.Pin_0, R4.Pin_0
  GND: Part1.GND, R2.Pin_1, R3.pin_1, R5.Pin_1
  N2: R5.Pin_0, LED1.cathode
