# Fritzing sketch CH340 (saved by Fritzing 1.0.1rc)
breadboards: 1

parts:
  Part1 = Arduino Nano (Rev3.0)
  R1 = Resistor [tolerance=±5% power=0.25W resistance=220 package=THT]
  LED1 = LED - 5mm [color="Red (633nm)" current=0.030A package="5 mm [THT]"]

nets:
  GND: Part1.GND, LED1.cathode
  N1: Part1.D13/SCK, R1.Pin_0
  N2: R1.Pin_1, LED1.anode
