# Fritzing sketch SimpleSamplePlayer (saved by Fritzing 0.9.2b)
breadboards: 1

parts:
  Part1 = Arduino Uno (Rev3)
  SPEAKER = Piezo Speaker
  R1 = Resistor [tolerance=±5% resistance=100 package=THT]
  PLAY = Pushbutton [package="[THT]"]

nets:
  N1: Part1.D11_PWM/MOSI, R1.Pin_0
  GND: Part1.GND, SPEAKER.pin1, PLAY.Pin_1, PLAY.Pin_2
  N2: Part1.D2, PLAY.Pin_3, PLAY.Pin_4
  N3: SPEAKER.pin2, R1.Pin_1
