# Fritzing sketch AudioDSP (saved by Fritzing 0.9.2b)
breadboards: 1

parts:
  Part1 = Arduino Uno (Rev3)
  IC1 = Dual Op-Amp [part_number=LMC6482 package=dip08]
  R6 = Resistor [tolerance=±5% resistance=4.7k package=THT]
  C5 = Ceramic Capacitor [capacitance=10nF package="100 mil [THT, multilayer]"]
  R2 = Resistor [tolerance=±5% resistance=100k package=THT]
  C4 = Ceramic Capacitor [capacitance=330pF package="100 mil [THT, multilayer]"]
  RV1 = Rotary Potentiometer (Small) [maximum_resistance=100kΩ package=THT]
  JACK-IN = AMPHENOL - ACJS-MHDR [package=ACJS-MHDR]
  R4 = Resistor [tolerance=±5% resistance=10k package=THT]
  C3 = Electrolytic Capacitor [capacitance=4.7µF package="100 mil [THT, electrolytic]"]
  R2_2 = Resistor [tolerance=±5% resistance=1M package=THT]
  C1 = Ceramic Capacitor [capacitance=100nF package="100 mil [THT, multilayer]"]
  R1 = Resistor [tolerance=±5% resistance=1M package=THT]
  JACK-OUT = AMPHENOL - ACJS-MHDR [package=ACJS-MHDR]
  C10 = Electrolytic Capacitor [capacitance=4.7µF package="100 mil [THT, electrolytic]"]
  C7 = Ceramic Capacitor [capacitance=10nF package="100 mil [THT, multilayer]"]
  C8 = Ceramic Capacitor [capacitance=10nF package="100 mil [THT, multilayer]"]
  C11 = Ceramic Capacitor [capacitance=100nF package="100 mil [THT, multilayer]"]
  C9 = Ceramic Capacitor [capacitance=10nF package="100 mil [THT, multilayer]"]
  R13 = Resistor [tolerance=±5% resistance=4.7k package=THT]
  R12 = Resistor [tolerance=±5% resistance=4.7k package=THT]
  R10 = Resistor [tolerance=±5% resistance=4.7k package=THT]
  R11 = Resistor [tolerance=±5% resistance=1.2M package=THT]
  S3 = Pushbutton [part_number=right package=THT]
  S4 = Pushbutton [part_number=left package=THT]
  R9 = Resistor [tolerance=±5% resistance=4.7k package=THT]
  D1 = LED - 5mm [color="Blue (470nm)" package="5 mm [THT]"]
  S1 = SWITCH-DPDT [package=gpi-152-3013]
  S1c = Toggle Switch [package=THT]
  C12 = Electrolytic Capacitor [capacitance=4.7µF package="100 mil [THT, electrolytic]"]
  S2 = Toggle Switch [package=THT]
  R14 = Resistor [tolerance=±5% resistance=4.7k package=THT]
  R15 = Resistor [tolerance=±5% resistance=47k package=THT]

nets:
  A0: Part1.A0, R6.Pin_0, C5.1
  N1: Part1.A4/SDA, S3.leg1
  N2: Part1.A5/SCL, S4.leg1
  PWM9: Part1.D9_PWM, R10.Pin_0
  PWM10: Part1.D10_PWM/SS, R11.Pin_0
  DIG12: Part1.D12/MISO, S1c.COM
  N3: Part1.D13/SCK, R9.Pin_0
  GND: Part1.GND, IC1.A_V-, C5.0, JACK-IN.Sleeve_(1), C3.-, R1.Pin_0, JACK-OUT.Sleeve_(4), C7.1, C8.1, C11.0, S3.leg0, S4.leg0, D1.cathode, S1c.L2, C12.-, S2.L2, R15.Pin_0
  N4: Part1.D2, S2.COM
  VCC: Part1.5V, IC1.A_V+, R2_2.Pin_0, C11.1, C12.+
  N5: IC1.A_OUT, IC1.A_-IN, C10.+, C9.0
  N6: IC1.A_+IN, C8.0, R13.Pin_1
  N7: IC1.B_+IN, R14.Pin_1
  N8: IC1.B_-IN, R2.Pin_1, C4.1, RV1.leg1, RV1.wiper
  N9: IC1.B_OUT, R6.Pin_1, R2.Pin_0, C4.0
  N10: RV1.leg2, R4.Pin_0
  N11: JACK-IN.Tip_(3), S1.2
  N12: R4.Pin_1, C3.+
  N13: R2_2.Pin_1, C1.1, R1.Pin_1, R14.Pin_0
  FXin: C1.0, S1.1, R15.Pin_1
  N14: JACK-OUT.Tip_(6), S1.5
  FXout: C10.-, S1.4
  N15: C7.0, R12.Pin_0, R10.Pin_1, R11.Pin_1
  N16: C9.1, R13.Pin_0, R12.Pin_1
  N17: R9.Pin_1, D1.anode
  N18: S1.3, S1.6

notes:
  S1 & S1c actually represent a single 3PDT stomp switch
