# Fritzing sketch ATtiny (saved by Fritzing 0.9.2b)
breadboards: 1

parts:
  U3 = attiny85 [package=dip]
  5V = Power plug
  S1 = Pushbutton [package="[THT]"]
  R1 = Resistor [tolerance=±5% resistance=10k package=THT]

nets:
  CH4-PB3: U3.Pin_2
  CH3-PB4: U3.Pin_3
  GND: U3.Pin_4, 5V.GND, R1.Pin_0
  CH2-PB0: U3.Pin_5
  CH1-PB1: U3.Pin_6
  N1: U3.Pin_7, S1.Pin_1, S1.Pin_2, R1.Pin_1
  VCC: U3.Pin_8, 5V.VCC, S1.Pin_3, S1.Pin_4

notes:
  CH1 PB1
  CH2 PB0
  CH3 PB4
  CH4 PB3
