# Fritzing sketch AvrHardwarePWM (saved by Fritzing 0.9.2b)
breadboards: 1

parts:
  Part1 = Arduino Uno (Rev3)
  S1 = Pushbutton [package="[THT]"]
  R1 = Resistor [tolerance=±5% resistance=10k package=THT]

nets:
  SCOPE_T1a: Part1.D9_PWM
  SCOPE_T1b: Part1.D10_PWM/SS
  SCOPE_T2a: Part1.D11_PWM/MOSI
  BTN: Part1.D12/MISO, S1.Pin_1, S1.Pin_2, R1.Pin_0
  GND: Part1.GND, R1.Pin_1
  SCOPE_T2b: Part1.D3_PWM
  SCOPE_T0b: Part1.D5_PWM
  SCOPE_T0a: Part1.D6_PWM
  VCC: Part1.5V, S1.Pin_3, S1.Pin_4

notes:
  PWM outputs for scope probes
