# Fritzing sketch CapacitiveTouchOrgan (saved by Fritzing 0.9.2b)
breadboards: 1

parts:
  Part1 = Arduino Uno (Rev3)
  Part2 = MPR121 Breakout
  BB1 = 4-Line Bi-Directional Level Shifter
  SPKR = Piezo Speaker
  R1 = Resistor [tolerance=±5% resistance=100 package=THT]

nets:
  N1: Part1.A4/SDA, BB1.B2
  N2: Part1.A5/SCL, BB1.B3
  N3: Part1.D8, R1.Pin_0
  GND: Part1.GND, Part2.GND, BB1.GND, SPKR.pin1
  TOUCH_IRQ: Part1.D2, Part2.~IRQ
  3V3: Part1.3V3, Part2.3.3V, BB1.LV
  5V: Part1.5V, BB1.HV
  N4: Part2.SCL, BB1.A3
  N5: Part2.SDA, BB1.A2
  N6: SPKR.pin2, R1.Pin_1

custom parts:
  4-Line Bi-Directional Level Shifter: 4-Channel Bi-Directional Level Shifter
