# Fritzing sketch ChainBlocks (saved by Fritzing 0.9.2b)
breadboards: 1

parts:
  IC1 = IC, DIP package, 14 pins [chip_label=MCP42010]
  Part2 = Arduino Nano (Rev3.0)

nets:
  LATCH: IC1.pin1, Part2.D9
  CLOCK: IC1.pin2, Part2.D13/SCK
  DATA: IC1.pin3, Part2.D11/MOSI
  GND/VSS: IC1.pin4, IC1.pin5, IC1.pin10, Part2.GND
  CH2: IC1.pin6
  VDD: IC1.pin7, IC1.pin8, IC1.pin11, IC1.pin12, IC1.pin14, Part2.5V
  CH1: IC1.pin9

notes:
  CH1
  CH2
