# Fritzing sketch ClassicNokia (saved by Fritzing 0.9.2b)
breadboards: 1

parts:
  Part1 = Arduino Uno (Rev3)
  R1 = Resistor [tolerance=±5% resistance=100 package=THT]
  SPKR1 = Loudspeaker

nets:
  N1: Part1.GND, SPKR1.pin1
  N2: Part1.D6_PWM, R1.Pin_0
  N3: R1.Pin_1, SPKR1.pin2
