# Fritzing sketch CounterModule (saved by Fritzing 0.9.2b)
breadboards: 1

parts:
  IC1 = IC, DIP package, 16 pins [chip_label=CD4017 part_number=CD4017]
  Part1 = Arduino Uno (Rev3)
  LED1 = LED - 3mm [color="Red (633nm)" package="3 mm [THT]"]
  LED2 = LED - 3mm [color="Red (633nm)" package="3 mm [THT]"]
  LED3 = LED - 3mm [color="Red (633nm)" package="3 mm [THT]"]
  LED4 = LED - 3mm [color="Red (633nm)" package="3 mm [THT]"]
  LED5 = LED - 3mm [color="Red (633nm)" package="3 mm [THT]"]
  LED7 = LED - 3mm [color="Red (633nm)" package="3 mm [THT]"]
  LED6 = LED - 3mm [color="Red (633nm)" package="3 mm [THT]"]
  LED8 = LED - 3mm [color="Red (633nm)" package="3 mm [THT]"]
  LED9 = LED - 3mm [color="Red (633nm)" package="3 mm [THT]"]
  LED10 = LED - 3mm [color="Red (633nm)" package="3 mm [THT]"]
  LED11 = LED - 3mm [color="Green (555nm)" package="3 mm [THT]"]
  R12 = Resistor [tolerance=±5% resistance=100k package=THT]
  R13 = Resistor [tolerance=±5% resistance=100k package=THT]
  R11 = Resistor [tolerance=±5% resistance=680 package=THT]
  R1 = Resistor [tolerance=±5% resistance=680 package=THT]
  R2 = Resistor [tolerance=±5% resistance=680 package=THT]
  R3 = Resistor [tolerance=±5% resistance=680 package=THT]
  R4 = Resistor [tolerance=±5% resistance=680 package=THT]
  R5 = Resistor [tolerance=±5% resistance=680 package=THT]
  R8 = Resistor [tolerance=±5% resistance=680 package=THT]
  R7 = Resistor [tolerance=±5% resistance=680 package=THT]
  R10 = Resistor [tolerance=±5% resistance=680 package=THT]
  R9 = Resistor [tolerance=±5% resistance=680 package=THT]
  R6 = Resistor [tolerance=±5% resistance=680 package=THT]

nets:
  Q5: IC1.pin1, LED6.anode
  Q1: IC1.pin2, LED2.anode
  Q0: IC1.pin3, LED1.anode
  Q2: IC1.pin4, LED3.anode
  Q6: IC1.pin5, LED7.anode
  Q7: IC1.pin6, LED8.anode
  Q3: IC1.pin7, LED4.anode
  GND: IC1.pin8, Part1.GND, R12.Pin_0, R13.Pin_0, R11.Pin_1, R1.Pin_1, R2.Pin_1, R3.Pin_1, R4.Pin_1, R5.Pin_1, R8.Pin_1, R7.Pin_1, R10.Pin_1, R9.Pin_1, R6.Pin_1
  Q8: IC1.pin9, LED9.anode
  Q4: IC1.pin10, LED5.anode
  Q9: IC1.pin11, LED10.anode
  CARRY: IC1.pin12, LED11.anode
  CLOCK_ENABLE: IC1.pin13, Part1.D10_PWM/SS, R12.Pin_1
  CLOCK: IC1.pin14, Part1.D11_PWM/MOSI
  RESET: IC1.pin15, Part1.D12/MISO, R13.Pin_1
  VCC: IC1.pin16, Part1.5V
  N1: LED1.cathode, R1.Pin_0
  N2: LED2.cathode, R2.Pin_0
  N3: LED3.cathode, R3.Pin_0
  N4: LED4.cathode, R4.Pin_0
  N5: LED5.cathode, R5.Pin_0
  N6: LED7.cathode, R7.Pin_0
  N7: LED6.cathode, R6.Pin_0
  N8: LED8.cathode, R8.Pin_0
  N9: LED9.cathode, R9.Pin_0
  N10: LED10.cathode, R10.Pin_0
  N11: LED11.cathode, R11.Pin_0

notes:
  The Arduino is just used to drive a test signal to the board
