# Fritzing sketch UnifiedSensorTest (saved by Fritzing 1.0.1rc)
breadboards: 1

parts:
  Part1 = Arduino Uno (Rev3)
  DHT1 = DHT11 Humitidy and Temperature Sensor
  R1 = Resistor [tolerance=±5% resistance=5.1k power=0.25W package=THT]
  C1 = Ceramic Capacitor [capacitance=100nF voltage=35V package="100 mil [THT, multilayer]"]

nets:
  DATA: Part1.D2, DHT1.DATA, R1.Pin_1
  VCC: Part1.5V, DHT1.VDD, R1.Pin_0, C1.1
  GND: Part1.GND, DHT1.GND, C1.0

notes:
  Pullup resistor and decoupling capacitor are included in the DHT11 module

custom parts:
  DHT11 Humitidy and Temperature Sensor: DHT11 Humidity and Temperature Sensor
