# Fritzing sketch Tester (saved by Fritzing 1.0.1rc)
breadboards: 1

parts:
  Part1 = Arduino Uno (Rev3)
  AM2 = AM2302 Humidity and Temperature Sensor

nets:
  DATA: Part1.D2, AM2.DATA
  VDD: Part1.5V, AM2.VDD
  GND: Part1.GND, AM2.GND
