# Fritzing sketch TimeDemo (saved by Fritzing 0.9.2b)
breadboards: 1

parts:
  Part1 = Arduino Uno (Rev3)
  RTC1 = DS1307 RTC Breakout [part_number=DS3231]

nets:
  N1: Part1.A4/SDA, RTC1.SDA
  N2: Part1.A5/SCL, RTC1.SCL
  GND: Part1.GND, RTC1.GND
  VCC: Part1.5V, RTC1.5V

custom parts:
  DS1307 RTC Breakout: DS1307 Real-time Clock Breakout Board with Battery
