# Fritzing sketch DicksonChargePump (saved by Fritzing 0.9.2b)
breadboards: 1

parts:
  D1 = Rectifier Diode [part_number=1N4148 package="300 mil [THT]"]
  D2 = Rectifier Diode [part_number=1N4148 package="300 mil [THT]"]
  D3 = Rectifier Diode [part_number=1N4148 package="300 mil [THT]"]
  D4 = Rectifier Diode [part_number=1N4148 package="300 mil [THT]"]
  C1 = Ceramic Capacitor [capacitance=220nF voltage=25V package="100 mil [THT, multilayer]"]
  C2 = Ceramic Capacitor [capacitance=220nF voltage=25V package="100 mil [THT, multilayer]"]
  C3 = Ceramic Capacitor [capacitance=220nF voltage=25V package="100 mil [THT, multilayer]"]
  C4 = Ceramic Capacitor [capacitance=1µF voltage=25V package="100 mil [THT, multilayer]"]
  Rcl = Resistor [tolerance=±5% resistance=2.2k package=THT]
  D5 = Zener Diode [part_number=1N4742 breakdown_voltage=12V package="300 mil [THT]"]
  Part4 = Arduino Uno (Rev3)
  RL = Resistor [tolerance=±5% resistance=10k package=THT]

nets:
  N1: D1.cathode, D2.anode, C1.1
  VCC: D1.anode, Part4.5V
  N2: D2.cathode, D3.anode, C2.1
  N3: D3.cathode, D4.anode, C3.1
  N4: D4.cathode, C4.1, Rcl.Pin_0
  PUMP_A: C1.0, C3.0, Part4.D3_PWM
  PUMP_B: C2.0, Part4.D11_PWM/MOSI
  GND: C4.0, D5.anode, Part4.GND, RL.Pin_0
  VHIGH: Rcl.Pin_1, D5.cathode, RL.Pin_1

notes:
  12V
  ~16V
