# Fritzing sketch DigitalInputWithAnalogPins (saved by Fritzing 0.9.2b)
breadboards: 1

parts:
  Part1 = Arduino Uno (Rev3)
  LED1 = LED - 3mm [color="Red (633nm)" package="3 mm [THT]"]
  LED2 = LED - 3mm [color="Red (633nm)" package="3 mm [THT]"]
  LED3 = LED - 3mm [color="Red (633nm)" package="3 mm [THT]"]
  LED4 = LED - 3mm [color="Red (633nm)" package="3 mm [THT]"]
  LED5 = LED - 3mm [color="Red (633nm)" package="3 mm [THT]"]
  R1 = Resistor [tolerance=±5% resistance=1k package=THT]
  R2 = Resistor [tolerance=±5% resistance=1k package=THT]
  R3 = Resistor [tolerance=±5% resistance=1k package=THT]
  R4 = Resistor [tolerance=±5% resistance=1k package=THT]
  R5 = Resistor [tolerance=±5% resistance=1k package=THT]
  R6 = Resistor [tolerance=±5% resistance=10k package=THT]
  S1 = Pushbutton [package=THT]

nets:
  N1: Part1.A0, LED1.anode
  N2: Part1.A1, LED2.anode
  N3: Part1.A2, LED3.anode
  N4: Part1.A3, LED4.anode
  N5: Part1.A4/SDA, LED5.anode
  N6: Part1.A5/SCL, R6.Pin_0, S1.leg1
  N7: Part1.5V, S1.leg0
  N8: Part1.GND, R1.Pin_1, R2.Pin_1, R3.Pin_1, R4.Pin_1, R5.Pin_1, R6.Pin_1
  N9: LED1.cathode, R1.Pin_0
  N10: LED2.cathode, R2.Pin_0
  N11: LED3.cathode, R3.Pin_0
  N12: LED4.cathode, R4.Pin_0
  N13: LED5.cathode, R5.Pin_0
