# Fritzing sketch BasicReadWrite (saved by Fritzing 0.9.2b)
breadboards: 1

parts:
  Part1 = Arduino Uno (Rev3)
  IC1 = IC, DIP package, 8 pins [chip_label=AT24C02 part_number=AT24C02BN]

nets:
  SDA: Part1.A4/SDA, IC1.pin5
  SCL: Part1.A5/SCL, IC1.pin6
  VCC: Part1.5V, IC1.pin8
  GND: Part1.GND, IC1.pin1, IC1.pin2, IC1.pin3, IC1.pin4, IC1.pin7
