# Fritzing sketch PEProgrammer (saved by Fritzing 0.9.2b)
breadboards: 1

parts:
  Part1 = Arduino Uno (Rev3)
  IC1 = IC, DIP package, 28 pins [chip_label=MCP23S17]
  IC3 = IC, DIP package, 24 pins [chip_label=AT28C16]

nets:
  IO6: Part1.D8, IC3.pin16
  IO7: Part1.D9_PWM, IC3.pin17
  CS: Part1.D10_PWM/SS, IC1.pin11
  MOSI: Part1.D11_PWM/MOSI, IC1.pin13
  MISO: Part1.D12/MISO, IC1.pin14
  SCK: Part1.D13/SCK, IC1.pin12
  GND: Part1.GND, IC1.pin10, IC1.pin15, IC1.pin16, IC1.pin17, IC3.pin12
  IO0: Part1.D2, IC3.pin9
  IO1: Part1.D3_PWM, IC3.pin10
  IO2: Part1.D4, IC3.pin11
  IO3: Part1.D5_PWM, IC3.pin13
  IO4: Part1.D6_PWM, IC3.pin14
  IO5: Part1.D7, IC3.pin15
  VDD: Part1.5V, IC1.pin9, IC1.pin18, IC3.pin24
  GPB0: IC1.pin1, IC3.pin23
  GPB1: IC1.pin2, IC3.pin22
  GPB2: IC1.pin3, IC3.pin19
  GPB3: IC1.pin4, IC3.pin21
  GPB4: IC1.pin5, IC3.pin20
  GPB5: IC1.pin6, IC3.pin18
  GPA0: IC1.pin21, IC3.pin8
  GPA1: IC1.pin22, IC3.pin7
  GPA2: IC1.pin23, IC3.pin6
  GPA3: IC1.pin24, IC3.pin5
  GPA4: IC1.pin25, IC3.pin4
  GPA5: IC1.pin26, IC3.pin3
  GPA6: IC1.pin27, IC3.pin2
  GPA7: IC1.pin28, IC3.pin1
