# Fritzing sketch SerialTest (saved by Fritzing 0.9.2b)
breadboards: 1

parts:
  U1 = ESP8266 WiFi Module [part_number=ESP8266]
  Part1 = FTDI Basic Programmer
  R1 = Resistor [tolerance=±5% resistance=10k package=THT]
  BB1 = 4-Line Bi-Directional Level Shifter
  5-9V = Power plug
  C1 = Electrolytic Capacitor [capacitance=100µF package="100 mil [THT, electrolytic]"]
  U3 = Voltage Regulator - 3.3V [part_number=LM1117-3.3 package="TO220 [THT]"]
  C2 = Electrolytic Capacitor [capacitance=10µF package="100 mil [THT, electrolytic]"]

nets:
  N1: U1.RXD, BB1.A1
  V33: U1.VCC, U1.RST, U1.CH_PD, R1.Pin_0, BB1.LV, C1.+, U3.output_voltage, C2.+
  N2: U1.GPIO_0, R1.Pin_1
  GND: U1.GND, BB1.GND#6, 5-9V.GND, C1.-, U3.GND, C2.-
  N3: U1.TXD, BB1.A2
  N4: Part1.RXI, BB1.B2
  N5: Part1.TXO, BB1.B1
  N6: Part1.POWER, BB1.HV
  N7: Part1.GND, BB1.GND#16
  N8: 5-9V.VCC, U3.input_voltage

custom parts:
  ESP8266 WiFi Module: Generic WiFi Module based on the ESP8266 with onboard PCB antenna and UART communications
  4-Line Bi-Directional Level Shifter: 4-Channel Bi-Directional Level Shifter
