# Fritzing sketch ElectretADC (saved by Fritzing 0.9.0b)
breadboards: 1

parts:
  Part1 = Arduino Uno (Rev3)
  R1 = Resistor [tolerance=±5% resistance=22k package=THT]
  R2 = Resistor [tolerance=±5% resistance=22k package=THT]
  IC1 = IC, DIP package, 14 pins [chip_label=LM324N]
  Ra2 = Resistor [tolerance=±5% resistance=22k package=THT]
  MIC1 = Microphone
  C1 = Electrolytic Capacitor [capacitance=1µF package="100 mil [THT, electrolytic]"]
  Ra1 = Resistor [tolerance=±5% resistance=1k package=THT]

nets:
  N1: Part1.A0, R2.Pin_0, IC1.pin3, C1.-
  N2: Part1.A1, IC1.pin1, Ra2.Pin_0
  N3: Part1.GND, R2.Pin_1, IC1.pin11, MIC1.pin1, Ra1.Pin_1
  N4: Part1.5V, R1.Pin_0, IC1.pin4
  N5: R1.Pin_1, MIC1.pin2, C1.+
  N6: IC1.pin2, Ra2.Pin_1, Ra1.Pin_0
