# Fritzing sketch ElectretTrigger (saved by Fritzing 0.9.0b)
breadboards: 1

parts:
  Part1 = Arduino Uno (Rev3)
  R5 = Resistor [tolerance=±5% resistance=10k package=THT]
  R1 = Resistor [tolerance=±5% resistance=2.2k package=THT]
  R3 = Resistor [tolerance=±5% resistance=22k package=THT]
  MIC1 = Microphone
  C1 = Electrolytic Capacitor [capacitance=1µF package="100 mil [THT, electrolytic]"]
  P1 = Piezo Speaker
  R4 = Resistor [tolerance=±5% resistance=22k package=THT]
  IC1 = LM324 [package=dil16]
  R2 = Resistor [tolerance=±5% resistance=330k package=THT]

nets:
  N1: Part1.A0, IC1.OUT1, R2.Pin_1
  GND: Part1.GND, MIC1.pin1, P1.pin1, R4.Pin_1, IC1.GND
  N2: Part1.D3_PWM, P1.pin2
  N3: Part1.5V, R5.Pin_0, R3.Pin_0, IC1.V+
  N4: R5.Pin_1, MIC1.pin2, C1.+
  N5: R1.Pin_0, C1.-
  N6: R1.Pin_1, IC1.IN1-, R2.Pin_0
  N7: R3.Pin_1, R4.Pin_0, IC1.IN1+

custom parts:
  LM324: LM324 Quad OpAmp
