# Fritzing sketch FastAnalogRead (saved by Fritzing 0.9.2b)
breadboards: 1

parts:
  Part1 = Arduino Uno (Rev3)
  R1 = Trimmer Potentiometer [maximum_resistance=10kΩ package=THT]

nets:
  N1: Part1.A0, R1.wiper
  VCC: Part1.5V, R1.leg1
  GND: Part1.GND, R1.leg2
