# Fritzing sketch HeartQuotes (saved by Fritzing 0.9.2b)
breadboards: 1

parts:
  Part1 = Arduino Ethernet Shield (Rev3)
  R1 = Resistor [tolerance=±5% resistance=10k package=THT]
  S2 = Pushbutton [package="[THT]"]
  R2 = Resistor [tolerance=±5% resistance=220 package=THT]
  LCD1 = LCD screen
  R3 = Resistor [tolerance=±5% resistance=220 package=THT]
  R4 = Rotary Potentiometer (Small) [maximum_resistance=100kΩ package=THT]

nets:
  GND: Part1.GND, R1.Pin_1, LCD1.VSS, LCD1.R/W, LCD1.LED-, R4.leg1
  N1: Part1.D8, LCD1.RS
  N2: Part1.PWM_D9, LCD1.E
  N3: Part1.D2, LCD1.DB7
  N4: Part1.PWM_D3, LCD1.DB6
  N5: Part1.SDCS, LCD1.DB5
  N6: Part1.PWM_D6, LCD1.DB4
  N7: Part1.D7, R1.Pin_0, S2.Pin_3, S2.Pin_4
  VCC: Part1.5V, R2.Pin_1, LCD1.VDD, R3.Pin_1, R4.leg2
  N8: S2.Pin_1, S2.Pin_2, R2.Pin_0
  N9: LCD1.V0, R4.wiper
  N10: LCD1.LED+, R3.Pin_0
