# Fritzing sketch HitTheLights (saved by Fritzing 0.9.0b)
breadboards: 1

parts:
  LCD1 = LCD screen
  Part1 = Arduino Uno (Rev3)
  R1 = Resistor [tolerance=±5% resistance=220 package=THT]
  VR1 = Rotary Potentiometer (Small) [maximum_resistance=50kΩ package=THT]
  LED1 = LED - 5mm [color="Red (633nm)" package="5 mm [THT]"]
  R2 = Resistor [tolerance=±5% resistance=4.7k package=THT]
  R3 = Resistor [tolerance=±5% resistance=4.7k package=THT]
  R4 = Resistor [tolerance=±5% resistance=4.7k package=THT]
  R5 = Resistor [tolerance=±5% resistance=4.7k package=THT]
  LED2 = LED - 5mm [color="Red (633nm)" package="5 mm [THT]"]
  LED3 = LED - 5mm [color="Red (633nm)" package="5 mm [THT]"]
  LED4 = LED - 5mm [color="Red (633nm)" package="5 mm [THT]"]
  S1 = Pushbutton [package="[THT]"]
  R6 = Resistor [tolerance=±5% resistance=10k package=THT]

nets:
  VSS: LCD1.VSS, LCD1.R/W, LCD1.LED-, Part1.GND, VR1.leg1, R2.Pin_0, R3.Pin_0, R4.Pin_0, R5.Pin_0, R6.Pin_0
  VDD: LCD1.VDD, Part1.5V, R1.Pin_0, VR1.leg2, S1.Pin_3, S1.Pin_4
  N1: LCD1.V0, VR1.wiper
  N2: LCD1.RS, Part1.D7
  N3: LCD1.E, Part1.D8
  N4: LCD1.DB4, Part1.D9_PWM
  N5: LCD1.DB5, Part1.D10_PWM/SS
  N6: LCD1.DB6, Part1.D11_PWM/MOSI
  N7: LCD1.DB7, Part1.D12/MISO
  N8: LCD1.LED+, R1.Pin_1
  N9: Part1.D2, S1.Pin_1, S1.Pin_2, R6.Pin_1
  N10: Part1.D3_PWM, LED1.anode
  N11: Part1.D4, LED2.anode
  N12: Part1.D5_PWM, LED3.anode
  N13: Part1.D6_PWM, LED4.anode
  N14: LED1.cathode, R2.Pin_1
  N15: R3.Pin_1, LED2.cathode
  N16: R4.Pin_1, LED3.cathode
  N17: R5.Pin_1, LED4.cathode
