# Fritzing sketch I2CScanner (saved by Fritzing 0.9.2b)
breadboards: 1

parts:
  Part1 = Arduino Uno (Rev3)
  R1 = Resistor [tolerance=±5% resistance=4.7k package=THT]
  R2 = Resistor [tolerance=±5% resistance=4.7k package=THT]

nets:
  SDA: Part1.A4/SDA, R1.Pin_1
  SCL: Part1.A5/SCL, R2.Pin_1
  VCC: Part1.5V, R1.Pin_0, R2.Pin_0

notes:
  SDA
  SCL
  Optional pull-up resistors - if not allready present in-circuit
