# Fritzing sketch Dumper (saved by Fritzing 0.9.2b)
breadboards: 1

parts:
  Part1 = Arduino Uno (Rev3)
  IR1 = TSOP312.., 314.. [package=THT]

nets:
  GND: Part1.GND, IR1.GND
  N1: Part1.D2, IR1.Data
  5V: Part1.5V, IR1.Vs
