# Fritzing sketch TestIR (saved by Fritzing 0.9.0b)
breadboards: 1

parts:
  IR1 = TSOP312.., 314.. [package=THT]
  R1 = Resistor [tolerance=±5% resistance=1k package=THT]
  Part1 = Arduino Uno (Rev3)
  LED1 = LED - 3mm [color="Blue (430nm)" package="3 mm [THT]"]

nets:
  GND: IR1.GND, Part1.GND, LED1.cathode
  N1: IR1.Vs, Part1.5V
  N2: IR1.Data, R1.Pin_1, Part1.D2
  N3: R1.Pin_0, LED1.anode
