# Fritzing sketch JarabeTapatio (saved by Fritzing 0.9.0b)
breadboards: 1

parts:
  J1 = Piezo Speaker
  Part1 = Arduino Nano (Rev3.0)
  U1 = LM386 [part_number=LM386 package=dip08]
  C2 = Electrolytic Capacitor [capacitance=100µF package="100 mil [THT, electrolytic]"]
  VCC1 = Battery block 9V
  C1 = Ceramic Capacitor [capacitance=100nF package="100 mil [THT, multilayer]"]

nets:
  N1: J1.pin1, Part1.GND, U1.+IN, U1.V-, VCC1.-
  N2: J1.pin2, C2.-
  N3: Part1.D6, C1.0
  N4: Part1.VIN, U1.V+, VCC1.+
  N5: U1.-IN, C1.1
  N6: U1.OUT, C2.+
