# Fritzing sketch KeyboardMatrixModule (saved by Fritzing 0.9.2b)

parts:
  S1 = Pushbutton [package="[THT]"]
  S2 = Pushbutton [package="[THT]"]
  S3 = Pushbutton [package="[THT]"]
  S4 = Pushbutton [package="[THT]"]
  K1 = Pushbutton [package="[THT]"]
  K2 = Pushbutton [package="[THT]"]
  K3 = Pushbutton [package="[THT]"]
  K4 = Pushbutton [package="[THT]"]
  K5 = Pushbutton [package="[THT]"]
  K6 = Pushbutton [package="[THT]"]
  K7 = Pushbutton [package="[THT]"]
  K8 = Pushbutton [package="[THT]"]
  K9 = Pushbutton [package="[THT]"]
  K10 = Pushbutton [package="[THT]"]
  K11 = Pushbutton [package="[THT]"]
  K12 = Pushbutton [package="[THT]"]
  R1 = Resistor [tolerance=±5% resistance=10k package=THT]
  R2 = Resistor [tolerance=±5% resistance=10k package=THT]
  R3 = Resistor [tolerance=±5% resistance=10k package=THT]
  R4 = Resistor [tolerance=±5% resistance=10k package=THT]
  LED1 = LED - 5mm [color="Red (633nm)" package="5 mm [THT]"]
  LED2 = LED - 5mm [color="Red (633nm)" package="5 mm [THT]"]
  LED3 = LED - 5mm [color="Red (633nm)" package="5 mm [THT]"]
  LED4 = LED - 5mm [color="Red (633nm)" package="5 mm [THT]"]
  LED5 = LED - 5mm [color="Red (633nm)" package="5 mm [THT]"]
  LED6 = LED - 5mm [color="Red (633nm)" package="5 mm [THT]"]
  LED7 = LED - 5mm [color="Red (633nm)" package="5 mm [THT]"]
  LED8 = LED - 5mm [color="Red (633nm)" package="5 mm [THT]"]
  R6 = Resistor [tolerance=±5% resistance=1k package=THT]
  R5 = Resistor [tolerance=±5% resistance=1k package=THT]
  R7 = Resistor [tolerance=±5% resistance=1k package=THT]
  R8 = Resistor [tolerance=±5% resistance=1k package=THT]
  R9 = Resistor [tolerance=±5% resistance=1k package=THT]
  R10 = Resistor [tolerance=±5% resistance=1k package=THT]
  R11 = Resistor [tolerance=±5% resistance=1k package=THT]
  R12 = Resistor [tolerance=±5% resistance=1k package=THT]
  KEYA = shrouded pin header, 10 pins [form="♂ (shrouded male)"]
  LED = shrouded pin header, 10 pins [form="♂ (shrouded male)"]
  KEYB = shrouded pin header, 6 pins [form="♂ (shrouded male)"]
  K13 = Pushbutton [package="[THT]"]
  K14 = Pushbutton [package="[THT]"]
  K15 = Pushbutton [package="[THT]"]
  K16 = Pushbutton [package="[THT]"]

nets:
  S1: S1.Pin_1, S1.Pin_2, R1.Pin_1, KEYB.pin4
  GND: S1.Pin_3, S1.Pin_4, S2.Pin_3, S2.Pin_4, S3.Pin_3, S3.Pin_4, S4.Pin_3, S4.Pin_4, KEYB.pin1
  S2: S2.Pin_1, S2.Pin_2, R2.Pin_1, KEYB.pin3
  S3: S3.Pin_1, S3.Pin_2, R3.Pin_1, KEYB.pin5
  S4: S4.Pin_1, S4.Pin_2, R4.Pin_1, KEYB.pin2
  R1: K1.Pin_2, K5.Pin_2, K9.Pin_2, KEYA.pin8, K13.Pin_2
  L1: K1.Pin_3, K1.Pin_4, K2.Pin_3, K2.Pin_4, K3.Pin_3, K3.Pin_4, K4.Pin_4, KEYA.pin6
  R2: K2.Pin_1, K2.Pin_2, K6.Pin_1, K6.Pin_2, K10.Pin_2, KEYA.pin3, K14.Pin_2
  R3: K3.Pin_2, K7.Pin_2, K11.Pin_2, KEYA.pin9, K15.Pin_2
  R4: K4.Pin_2, K8.Pin_2, K12.Pin_2, KEYA.pin2, K16.Pin_2
  L2: K5.Pin_3, K5.Pin_4, K6.Pin_3, K6.Pin_4, K7.Pin_3, K7.Pin_4, K8.Pin_4, KEYA.pin5
  L3: K9.Pin_3, K9.Pin_4, K10.Pin_3, K10.Pin_4, K11.Pin_3, K11.Pin_4, K12.Pin_4, KEYA.pin7
  VCC: R1.Pin_0, R2.Pin_0, R3.Pin_0, R4.Pin_0, LED1.anode, LED2.anode, LED3.anode, LED4.anode, LED5.anode, LED6.anode, LED7.anode, LED8.anode, LED.pin10, KEYB.pin6
  N1: LED1.cathode, R5.Pin_1
  N2: LED2.cathode, R6.Pin_1
  N3: LED3.cathode, R7.Pin_1
  N4: LED4.cathode, R8.Pin_1
  N5: LED5.cathode, R9.Pin_1
  N6: LED6.cathode, R10.Pin_1
  N7: LED7.cathode, R11.Pin_1
  N8: LED8.cathode, R12.Pin_1
  D2: R6.Pin_0, LED.pin5
  D1: R5.Pin_0, LED.pin6
  D3: R7.Pin_0, LED.pin7
  D4: R8.Pin_0, LED.pin4
  D5: R9.Pin_0, LED.pin8
  D6: R10.Pin_0, LED.pin3
  D7: R11.Pin_0, LED.pin9
  D8: R12.Pin_0, LED.pin2
  L4: KEYA.pin4, K13.Pin_3, K13.Pin_4, K14.Pin_3, K14.Pin_4, K15.Pin_3, K15.Pin_4, K16.Pin_4

notes:
  I haven't bothered to fully layout a breadboard for the keyboard matrix module - these are all the parts in roughly their position on the board though
