# Fritzing sketch SwitchInterrupts (saved by Fritzing 0.9.2b)

parts:
  KEYA = shrouded pin header, 10 pins [form="♂ (shrouded male)"]
  LED = shrouded pin header, 10 pins [form="♂ (shrouded male)"]
  KEYB = shrouded pin header, 6 pins [form="♂ (shrouded male)"]
  Part1 = Arduino Uno (Rev3)

nets:
  R4: KEYA.pin2
  R2: KEYA.pin3
  L4: KEYA.pin4
  L2: KEYA.pin5
  L1: KEYA.pin6
  L3: KEYA.pin7
  R1: KEYA.pin8
  R3: KEYA.pin9
  D8: LED.pin2
  D6: LED.pin3
  D4: LED.pin4
  D2: LED.pin5
  D1: LED.pin6
  D3: LED.pin7
  D5: LED.pin8
  D7: LED.pin9
  VCC: LED.pin10, KEYB.pin6, Part1.5V
  GND: KEYB.pin1, Part1.GND
  S4: KEYB.pin2, Part1.D5_PWM
  S2: KEYB.pin3, Part1.D3_PWM
  S1: KEYB.pin4, Part1.D2
  S3: KEYB.pin5, Part1.D4

notes:
  These are the three connectors on the KeyboardMatrixModule
