# Fritzing sketch I2CAdapter (saved by Fritzing 0.9.2b)

parts:
  Part1 = Arduino Uno (Rev3)
  LCD1 = LCD screen  # not connected
  I2C_Adapter = female pin header, 4 pins [form="♀ (female)"]

nets:
  SDA: Part1.A4/SDA, I2C_Adapter.pin3
  SCL: Part1.A5/SCL, I2C_Adapter.pin4
  VCC: Part1.5V, I2C_Adapter.pin2
  GND: Part1.GND, I2C_Adapter.pin1
