# Fritzing sketch CD4026BucketBrigade (saved by Fritzing 0.9.2b)
breadboards: 2

parts:
  R1 = Resistor [tolerance=±5% resistance=220 package=THT]
  7_Segment = 7 Segment Display
  R2 = Resistor [tolerance=±5% resistance=220 package=THT]
  R3 = Resistor [tolerance=±5% resistance=220 package=THT]
  R4 = Resistor [tolerance=±5% resistance=220 package=THT]
  R5 = Resistor [tolerance=±5% resistance=220 package=THT]
  R6 = Resistor [tolerance=±5% resistance=220 package=THT]
  R7 = Resistor [tolerance=±5% resistance=220 package=THT]
  Part2 = Arduino Uno (Rev3)
  IC1 = IC, DIP package, 16 pins [chip_label=CD4026]
  IC2 = IC, DIP package, 16 pins [chip_label=CD4026]
  7_Segment1 = 7 Segment Display
  R8 = Resistor [tolerance=±5% resistance=220 package=THT]
  R9 = Resistor [tolerance=±5% resistance=220 package=THT]
  R10 = Resistor [tolerance=±5% resistance=220 package=THT]
  R11 = Resistor [tolerance=±5% resistance=220 package=THT]
  R12 = Resistor [tolerance=±5% resistance=220 package=THT]
  R13 = Resistor [tolerance=±5% resistance=220 package=THT]
  R14 = Resistor [tolerance=±5% resistance=220 package=THT]

nets:
  A: R1.Pin_0, IC1.pin10
  N1: R1.Pin_1, 7_Segment.Segment_A
  N2: 7_Segment.Segment_E, R5.Pin_1
  N3: 7_Segment.Segment_D, R4.Pin_1
  GND: 7_Segment.common_cathode, Part2.GND, IC1.pin2, IC1.pin8, IC2.pin2, IC2.pin8, 7_Segment1.common_cathode
  N4: 7_Segment.Segment_C, R3.Pin_1
  N5: 7_Segment.Segment_B, R2.Pin_1
  N6: 7_Segment.Segment_F, R6.Pin_1
  N7: 7_Segment.Segment_G, R7.Pin_1
  B: R2.Pin_0, IC1.pin12
  C: R3.Pin_0, IC1.pin13
  D: R4.Pin_0, IC1.pin9
  E: R5.Pin_0, IC1.pin11
  F: R6.Pin_0, IC1.pin6
  G: R7.Pin_0, IC1.pin7
  N8: Part2.D8, IC1.pin1
  RESET: Part2.D9_PWM, IC1.pin15, IC2.pin15
  VDD: Part2.5V, IC1.pin3, IC1.pin16, IC2.pin3, IC2.pin16
  N9: IC1.pin5, IC2.pin1
  F2: IC2.pin6, R13.Pin_1
  G2: IC2.pin7, R14.Pin_1
  D2: IC2.pin9, R11.Pin_1
  A2: IC2.pin10, R8.Pin_0
  E2: IC2.pin11, R12.Pin_1
  B2: IC2.pin12, R9.Pin_0
  C2: IC2.pin13, R10.Pin_0
  N10: 7_Segment1.Segment_E, R12.Pin_0
  N11: 7_Segment1.Segment_D, R11.Pin_0
  N12: 7_Segment1.Segment_C, R10.Pin_1
  N13: 7_Segment1.Segment_B, R9.Pin_1
  N14: 7_Segment1.Segment_A, R8.Pin_1
  N15: 7_Segment1.Segment_F, R13.Pin_0
  N16: 7_Segment1.Segment_G, R14.Pin_0

notes:
  this pattern can be repeated for any number of digits
