# Fritzing sketch CD4026Drive (saved by Fritzing 0.9.2b)
breadboards: 1

parts:
  R1 = Resistor [tolerance=±5% resistance=220 package=THT]
  7_Segment = 7 Segment Display
  R2 = Resistor [tolerance=±5% resistance=220 package=THT]
  R3 = Resistor [tolerance=±5% resistance=220 package=THT]
  R4 = Resistor [tolerance=±5% resistance=220 package=THT]
  R5 = Resistor [tolerance=±5% resistance=220 package=THT]
  R6 = Resistor [tolerance=±5% resistance=220 package=THT]
  R7 = Resistor [tolerance=±5% resistance=220 package=THT]
  Part2 = Arduino Uno (Rev3)
  IC1 = IC, DIP package, 16 pins [chip_label=CD4026]

nets:
  A: R1.Pin_0, IC1.pin10
  N1: R1.Pin_1, 7_Segment.Segment_A
  N2: 7_Segment.Segment_E, R5.Pin_1
  N3: 7_Segment.Segment_D, R4.Pin_1
  GND: 7_Segment.common_cathode, Part2.GND, IC1.pin2, IC1.pin8
  N4: 7_Segment.Segment_C, R3.Pin_1
  N5: 7_Segment.Segment_B, R2.Pin_1
  N6: 7_Segment.Segment_F, R6.Pin_1
  N7: 7_Segment.Segment_G, R7.Pin_1
  B: R2.Pin_0, IC1.pin12
  C: R3.Pin_0, IC1.pin13
  D: R4.Pin_0, IC1.pin9
  E: R5.Pin_0, IC1.pin11
  F: R6.Pin_0, IC1.pin6
  G: R7.Pin_0, IC1.pin7
  CLK: Part2.D8, IC1.pin1
  RESET: Part2.D9_PWM, IC1.pin15
  VDD: Part2.5V, IC1.pin3, IC1.pin16
