# Fritzing sketch CombinationalLogicDriver (saved by Fritzing 0.9.2b)
breadboards: 2

parts:
  Part1 = Arduino Uno (Rev3)
  IC9 = IC, DIP package, 14 pins [chip_label=74LS386]
  IC8 = IC, DIP package, 14 pins [chip_label=74LS132]
  IC2 = 74LS02 [package=dil14]
  IC1 = Hex Inverter Schmitt Trigger SN74HC14 [part_number=74LS14 package="DIP (Dual Inline)"]
  IC6 = IC, DIP package, 14 pins [chip_label=74LS32]
  IC3 = 74LS02 [package=dil14]
  IC4 = 74LS02 [package=dil14]
  IC5 = 74LS02 [package=dil14]
  IC7 = IC, DIP package, 14 pins [chip_label=74LS32]
  7_Segment1 = 7 Segment Display
  R1 = Resistor [tolerance=±5% resistance=220 package=THT]
  R2 = Resistor [tolerance=±5% resistance=220 package=THT]
  R3 = Resistor [tolerance=±5% resistance=220 package=THT]
  R4 = Resistor [tolerance=±5% resistance=220 package=THT]
  R5 = Resistor [tolerance=±5% resistance=220 package=THT]
  R6 = Resistor [tolerance=±5% resistance=220 package=THT]
  R7 = Resistor [tolerance=±5% resistance=220 package=THT]

nets:
  GND: Part1.GND, IC9.pin7, IC8.pin7, IC2.GND, IC1.GND, IC6.pin7, IC3.GND, IC4.GND, IC5.GND, IC7.pin7, 7_Segment1.common_cathode#8
  w: Part1.D2, IC2.B1, IC2.A2, IC1.1A, IC3.A3, IC7.pin2
  x: Part1.D3_PWM, IC9.pin1, IC2.A1, IC2.A3, IC2.B4, IC1.2A, IC3.A4, IC4.B2
  y: Part1.D4, IC9.pin5, IC2.B2, IC2.B3, IC1.3A, IC6.pin1, IC4.A1, IC4.A3
  z: Part1.D5_PWM, IC9.pin2, IC9.pin6, IC2.A4, IC1.4A, IC3.B1, IC3.B2, IC4.A4
  VCC: Part1.5V, IC9.pin14, IC8.pin14, IC2.VCC, IC1.VCC, IC6.pin14, IC3.VCC, IC4.VCC, IC5.VCC, IC7.pin14
  ic9a: IC9.pin3, IC8.pin10
  ic9b: IC9.pin4, IC8.pin2
  ic3c: IC8.pin1, IC3.Y3
  b: IC8.pin3, R2.Pin_0
  nor_z_not_y: IC8.pin4, IC6.pin9, IC3.Y2
  nor_w_x: IC8.pin5, IC2.Y1
  c: IC8.pin6, R3.Pin_1
  a: IC8.pin8, R1.Pin_0
  nor_w_y: IC8.pin9, IC2.Y2, IC4.B4
  g: IC8.pin11, R7.Pin_0
  ic7c: IC8.pin12, IC7.pin8
  not_w: IC8.pin13, IC1.1Y
  nor_x_y: IC2.Y3, IC7.pin10
  nor_x_z: IC2.Y4, IC6.pin10
  not_x: IC1.2Y, IC3.A1, IC3.B3, IC5.A1, IC5.A2
  not_y: IC1.3Y, IC6.pin5, IC3.A2
  not_z: IC1.4Y, IC6.pin2, IC6.pin4, IC3.B4, IC4.B1
  or_ynotz: IC6.pin3, IC5.B1
  or_noty_notz: IC6.pin6, IC5.B2
  e: IC6.pin8, R5.Pin_1
  ic6d: IC6.pin11, IC7.pin1
  nor_y_nor_xnotz: IC6.pin12, IC4.Y3
  nor_znotx: IC6.pin13, IC3.Y1
  nor_x_not_z: IC3.Y4, IC4.B3
  nor_y_not_z: IC4.Y1, IC4.A2
  ic4b: IC4.Y2, IC7.pin5
  ic4d: IC4.Y4, IC7.pin12
  ic5a: IC5.Y1, IC7.pin4
  ic5b: IC5.Y2, IC7.pin9
  f: IC7.pin3, R6.Pin_0
  ic7b: IC7.pin6, IC7.pin13
  d: IC7.pin11, R4.Pin_1
  N1: 7_Segment1.Segment_A#1, R7.Pin_1
  N2: 7_Segment1.Segment_F, R6.Pin_1
  N3: 7_Segment1.Segment_E, R5.Pin_0
  N4: 7_Segment1.Segment_D, R4.Pin_0
  N5: 7_Segment1.Segment_C, R3.Pin_0
  N6: 7_Segment1.Segment_B, R2.Pin_1
  N7: 7_Segment1.Segment_A#10, R1.Pin_1

custom parts:
  74LS02: 74LS02 Quad 2-input NOR
