# Fritzing sketch DirectDrive (saved by Fritzing 0.9.2b)
breadboards: 1

parts:
  Part2 = Arduino Mega 2560 (Rev3)
  R1 = Resistor [tolerance=±5% resistance=220 package=THT]
  7_Segment3 = 7 Segment Display
  R2 = Resistor [tolerance=±5% resistance=220 package=THT]
  R3 = Resistor [tolerance=±5% resistance=220 package=THT]
  R4 = Resistor [tolerance=±5% resistance=220 package=THT]
  R5 = Resistor [tolerance=±5% resistance=220 package=THT]
  R6 = Resistor [tolerance=±5% resistance=220 package=THT]
  R7 = Resistor [tolerance=±5% resistance=220 package=THT]
  R8 = Resistor [tolerance=±5% resistance=220 package=THT]

nets:
  N1: Part2.GND, 7_Segment3.common_cathode
  N2: Part2.D9_PWM, R8.Pin_0
  N3: Part2.D8_PWM, R7.Pin_0
  N4: Part2.D2_PWM, R1.Pin_0
  N5: Part2.D3_PWM, R2.Pin_0
  N6: Part2.D4_PWM, R3.Pin_0
  N7: Part2.D5_PWM, R4.Pin_0
  N8: Part2.D6_PWM, R5.Pin_0
  N9: Part2.D7_PWM, R6.Pin_0
  N10: R1.Pin_1, 7_Segment3.Segment_A
  N11: 7_Segment3.Segment_E, R5.Pin_1
  N12: 7_Segment3.Segment_D, R4.Pin_1
  N13: 7_Segment3.Segment_C, R3.Pin_1
  N14: 7_Segment3.Segment_DP, R8.Pin_1
  N15: 7_Segment3.Segment_B, R2.Pin_1
  N16: 7_Segment3.Segment_F, R6.Pin_1
  N17: 7_Segment3.Segment_G, R7.Pin_1
