# Fritzing sketch LedControlDemo (saved by Fritzing 0.9.2b)
breadboards: 1

parts:
  Part1 = Arduino Uno (Rev3)
  U1 = MAX7219 [part_number=MAX7219 package=dil24]
  R1 = Resistor [tolerance=±5% resistance=10k package=THT]
  C1 = Electrolytic Capacitor [capacitance=10µF package="100 mil [THT, electrolytic]"]
  C2 = Ceramic Capacitor [capacitance=100nF package="100 mil [THT, multilayer]"]
  7_Segment1 = 7 Segment Display
  7_Segment0 = 7 Segment Display

nets:
  CS: Part1.D10_PWM/SS, U1.LOAD
  MOSI: Part1.D11_PWM/MOSI, U1.DIN
  SCK: Part1.D13/SCK, U1.CLK
  GND: Part1.GND, U1.GND, C1.-, C2.0
  VCC: Part1.5V, U1.VCC, R1.Pin_0, C1.+, C2.1
  DIG0: U1.DIG0, 7_Segment0.common_cathode#8
  DIG1: U1.DIG1, 7_Segment1.common_cathode#8
  SEGA: U1.SEGA, 7_Segment1.Segment_A#10, 7_Segment0.Segment_A#10
  SEGF: U1.SEGF, 7_Segment1.Segment_F, 7_Segment0.Segment_F
  SEGB: U1.SEGB, 7_Segment1.Segment_B, 7_Segment0.Segment_B
  SEGG: U1.SEGG, 7_Segment1.Segment_A#1, 7_Segment0.Segment_A#1
  N1: U1.ISET, R1.Pin_1
  SEGC: U1.SEGC, 7_Segment1.Segment_C, 7_Segment0.Segment_C
  SEGE: U1.SEGE, 7_Segment1.Segment_E, 7_Segment0.Segment_E
  SEGDP: U1.SEGDP, 7_Segment1.Segment_DP, 7_Segment0.Segment_DP
  SEGD: U1.SEGD, 7_Segment1.Segment_D, 7_Segment0.Segment_D
