# Fritzing sketch ShiftDriveSPI (saved by Fritzing 0.9.2b)
breadboards: 1

parts:
  R1 = Resistor [tolerance=±5% resistance=220 package=THT]
  7_Segment3 = 7 Segment Display
  R2 = Resistor [tolerance=±5% resistance=220 package=THT]
  R3 = Resistor [tolerance=±5% resistance=220 package=THT]
  R4 = Resistor [tolerance=±5% resistance=220 package=THT]
  R5 = Resistor [tolerance=±5% resistance=220 package=THT]
  R6 = Resistor [tolerance=±5% resistance=220 package=THT]
  R7 = Resistor [tolerance=±5% resistance=220 package=THT]
  R8 = Resistor [tolerance=±5% resistance=220 package=THT]
  U1 = 74HC595 [package="DIP16 [THT]"]
  Part2 = Arduino Uno (Rev3)

nets:
  ssA: R1.Pin_0, U1.Q0
  N1: R1.Pin_1, 7_Segment3.Segment_A
  N2: 7_Segment3.Segment_E, R5.Pin_1
  N3: 7_Segment3.Segment_D, R4.Pin_1
  GND: 7_Segment3.common_cathode, U1.GND, U1.OE, Part2.GND
  N4: 7_Segment3.Segment_C, R3.Pin_1
  N5: 7_Segment3.Segment_DP, R8.Pin_1
  N6: 7_Segment3.Segment_B, R2.Pin_1
  N7: 7_Segment3.Segment_F, R6.Pin_1
  N8: 7_Segment3.Segment_G, R7.Pin_1
  ssB: R2.Pin_0, U1.Q1
  ssC: R3.Pin_0, U1.Q2
  ssD: R4.Pin_0, U1.Q3
  ssE: R5.Pin_0, U1.Q4
  ssF: R6.Pin_0, U1.Q5
  ssG: R7.Pin_0, U1.Q6
  ssDP: R8.Pin_0, U1.Q7
  Vcc: U1.MR, U1.VCC, Part2.5V
  CLOCK: U1.SH_CP, Part2.D13/SCK
  LATCH: U1.ST_CP, Part2.D4
  DATA: U1.DS, Part2.D11_PWM/MOSI
