# Fritzing sketch MaxRawDemo (saved by Fritzing 0.9.2b)

parts:
  Part1 = LED Matrix - Serial Interface - Red/Green/Blue
  Part2 = Arduino Uno (Rev3)

nets:
  N1: Part1.SCK, Part2.D12/MISO
  N2: Part1.CS, Part2.D11_PWM/MOSI
  GND: Part1.GND, Part2.GND
  N3: Part1.MOSI, Part2.D10_PWM/SS
  VCC: Part1.VCC, Part2.5V
