# Fritzing sketch Mini4 (saved by Fritzing 0.9.2b)
breadboards: 2

parts:
  RL1 = Resistor [tolerance=±5% resistance=10k package=THT]
  Part1 = Arduino Uno (Rev3)
  U2 = 74HC595 [package="DIP16 [THT]"]
  RL2 = Resistor [tolerance=±5% resistance=10k package=THT]
  RL3 = Resistor [tolerance=±5% resistance=10k package=THT]
  RL4 = Resistor [tolerance=±5% resistance=10k package=THT]
  U3 = 74HC595 [package="DIP16 [THT]"]
  QL1 = 2N7000 FET N-Channel [part_number=2N7000 package=TO92]
  QL2 = 2N7000 FET N-Channel [part_number=2N7000 package=TO92]
  QL3 = 2N7000 FET N-Channel [part_number=2N7000 package=TO92]
  QL4 = 2N7000 FET N-Channel [part_number=2N7000 package=TO92]
  U4 = 74HC595 [package="DIP16 [THT]"]
  U5 = atmega328 [package=dip]
  R1 = Resistor [tolerance=±5% resistance=10k package=THT]
  XTAL1 = Crystal [frequency="16 Mhz" package=THT]
  C1 = Ceramic Capacitor [capacitance=22pF package="100 mil [THT, multilayer]"]
  C2 = Ceramic Capacitor [capacitance=22pF package="100 mil [THT, multilayer]"]
  Power_Supply = Battery block 9V
  U6 = Voltage Regulator - 5V [part_number=LM7805 package="DPak [SMD]"]
  Cp1 = Electrolytic Capacitor [capacitance=100µF package="100 mil [THT, electrolytic]"]
  Cp3 = Electrolytic Capacitor [capacitance=100µF package="100 mil [THT, electrolytic]"]
  Cp2 = Ceramic Capacitor [capacitance=100nF package="100 mil [THT, multilayer]"]
  LC1L1 = LED - 3mm [color="Blue (430nm)" package="3 mm [THT]"]
  LC1L2 = LED - 3mm [color="Blue (430nm)" package="3 mm [THT]"]
  LC1L3 = LED - 3mm [color="Blue (430nm)" package="3 mm [THT]"]
  LC1L4 = LED - 3mm [color="Blue (430nm)" package="3 mm [THT]"]
  RC1 = Resistor [tolerance=±5% resistance=220 package=THT]
  LC2L4 = LED - 3mm [color="Blue (430nm)" package="3 mm [THT]"]
  LC2L3 = LED - 3mm [color="Blue (430nm)" package="3 mm [THT]"]
  LC2L2 = LED - 3mm [color="Blue (430nm)" package="3 mm [THT]"]
  LC2L1 = LED - 3mm [color="Blue (430nm)" package="3 mm [THT]"]
  RC2 = Resistor [tolerance=±5% resistance=220 package=THT]
  LC16L4 = LED - 3mm [color="Blue (430nm)" package="3 mm [THT]"]
  LC16L3 = LED - 3mm [color="Blue (430nm)" package="3 mm [THT]"]
  LC16L2 = LED - 3mm [color="Blue (430nm)" package="3 mm [THT]"]
  LC16L1 = LED - 3mm [color="Blue (430nm)" package="3 mm [THT]"]
  RC16 = Resistor [tolerance=±5% resistance=220 package=THT]
  LU1 = LED - 3mm [color="Red (633nm)" package="3 mm [THT]"]
  RLU1 = Resistor [tolerance=±5% resistance=330 package=THT]
  LU2 = LED - 3mm [color="Green (570nm)" package="3 mm [THT]"]
  RLU2 = Resistor [tolerance=±5% resistance=330 package=THT]
  LU3 = LED - 3mm [color="Yellow (595nm)" package="3 mm [THT]"]
  LU4 = LED - 3mm [color="Blue (525nm)" part_number=solid package="3 mm [THT]"]
  RLU3 = Resistor [tolerance=±5% resistance=1k package=THT]
  RLU4 = Resistor [tolerance=±5% resistance=1k package=THT]

nets:
  LL1: RL1.Pin_0, U4.Q4
  N1: RL1.Pin_1, QL1.gate
  SS: Part1.D10_PWM/SS, U5.RESET, R1.Pin_0
  MOSI: Part1.D11_PWM/MOSI, U5.D11_(PWM)
  MISO: Part1.D12/MISO, U5.D12
  SCK: Part1.D13/SCK, U5.D13
  GND: Part1.GND, U2.GND, U2.OE, U3.GND, U3.OE, QL1.source, QL2.source, QL3.source, QL4.source, U4.GND, U4.OE, U5.GND, C1.0, C2.0, Power_Supply.-, U6.GND, Cp1.-, Cp3.-, Cp2.0, RLU1.Pin_1, RLU2.Pin_1, RLU3.Pin_1, RLU4.Pin_1
  LC10: U2.Q1
  LC11: U2.Q2
  LC12: U2.Q3
  LC13: U2.Q4
  LC14: U2.Q5
  LC15: U2.Q6
  LC16: U2.Q7, RC16.Pin_0
  N2: U2.Q7', U4.DS
  Vcc: U2.MR, U2.VCC, U3.MR, U3.VCC, U4.MR, U4.VCC, U5.VCC, U5.AVCC, R1.Pin_1, U6.output_voltage, Cp3.+, Cp2.1
  SH_CP: U2.SH_CP, U3.SH_CP, U4.SH_CP, U5.D3_(PWM)
  ST_CP: U2.ST_CP, U3.ST_CP, U4.ST_CP, U5.D4
  N3: U2.DS, U3.Q7'
  LC9: U2.Q0
  LL2: RL2.Pin_0, U4.Q5
  N4: RL2.Pin_1, QL2.gate
  LL3: RL3.Pin_0, U4.Q6
  N5: RL3.Pin_1, QL3.gate
  LL4: RL4.Pin_0, U4.Q7
  N6: RL4.Pin_1, QL4.gate
  LC2: U3.Q1, RC2.Pin_0
  LC3: U3.Q2
  LC4: U3.Q3
  LC5: U3.Q4
  LC6: U3.Q5
  LC7: U3.Q6
  LC8: U3.Q7
  DS: U3.DS, U5.D5_(PWM)
  LC1: U3.Q0, RC1.Pin_0
  LCa1: QL1.drain, LC1L1.cathode, LC2L1.cathode, LC16L1.cathode
  LCa2: QL2.drain, LC1L2.cathode, LC2L2.cathode, LC16L2.cathode
  LCa3: QL3.drain, LC1L3.cathode, LC2L3.cathode, LC16L3.cathode
  LCa4: QL4.drain, LC1L4.cathode, LC2L4.cathode, LC16L4.cathode
  LU2: U4.Q1, LU2.anode
  LU3: U4.Q2, LU3.anode
  LU4: U4.Q3, LU4.anode
  LU1: U4.Q0, LU1.anode
  N7: U5.XLAT1, XTAL1.pin_1, C2.1
  N8: U5.XLAT2, XTAL1.pin_0, C1.1
  N9: Power_Supply.+, U6.input_voltage, Cp1.+
  N10: LC1L1.anode, LC1L2.anode, LC1L3.anode, LC1L4.anode, RC1.Pin_1
  N11: LC2L4.anode, LC2L3.anode, LC2L2.anode, LC2L1.anode, RC2.Pin_1
  N12: LC16L4.anode, LC16L3.anode, LC16L2.anode, LC16L1.anode, RC16.Pin_1
  N13: LU1.cathode, RLU1.Pin_0
  N14: LU2.cathode, RLU2.Pin_0
  N15: LU3.cathode, RLU3.Pin_0
  N16: LU4.cathode, RLU4.Pin_0

notes:
  Arduino ISP
  5V Regulated Power Supply
  ..and 13 more columns of LEDs here just like col 1,2,16
  MCU
  Latched Register Array
  LED Cathode Controls
  16x LED Columns
  Utility LEDs
  plus 13 more like this for LC3-LC15

custom parts:
  2N7000 FET N-Channel: A 2N7000 MOSFET N-Channel Transistor
