# Fritzing sketch LEDx16Module_demo (saved by Fritzing 0.9.2b)
breadboards: 1

parts:
  Part2 = Arduino Uno (Rev3)
  IC1 = IC, DIP package, 10 pins [chip_label=LEDx16]

nets:
  DATA: Part2.D11_PWM/MOSI, IC1.pin10
  CLOCK: Part2.D13/SCK, IC1.pin9
  GND: Part2.GND, IC1.pin7
  LATCH: Part2.D4, IC1.pin8
  Vcc: Part2.5V, IC1.pin6
