# Fritzing sketch AdafruitHardwareSPI (saved by Fritzing 0.9.2b)
breadboards: 1

parts:
  Part1 = Arduino Uno (Rev3)
  Nokia_5110_LCD_Module2 = Nokia5110LCDModule

nets:
  N1: Part1.D11_PWM/MOSI, Nokia_5110_LCD_Module2.6_DN_(MOSI)
  N2: Part1.D13/SCK, Nokia_5110_LCD_Module2.SCLK
  GND: Part1.GND, Nokia_5110_LCD_Module2.Grnd
  N3: Part1.D5_PWM, Nokia_5110_LCD_Module2.D/C
  N4: Part1.D6_PWM, Nokia_5110_LCD_Module2.SCE
  N5: Part1.D7, Nokia_5110_LCD_Module2.RST
  VCC: Part1.5V, Nokia_5110_LCD_Module2.Vcc

custom parts:
  : Nokia 5110 LCD with 8 pin. It's a 45mm*45mm module part. Description: The Nokia 5110 is a basic graphic LCD screen for lots of applications. It was originally intended for as a cell phone screen. This one is mounted on an easy to solder PCB. It uses the PCD8544 controller. The PCD8544 is a low power CMOS LCD controller/driver, designed to drive a graphic display of 48 rows and 84 columns. All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
