# Fritzing sketch AdafruitSoftwareSPI (saved by Fritzing 0.9.2b)
breadboards: 1

parts:
  Part1 = Arduino Uno (Rev3)
  LCD = Nokia5110LCDModule

nets:
  N1: Part1.D8, LCD.6_DN_(MOSI)
  N2: Part1.D9_PWM, LCD.SCLK
  GND: Part1.GND, LCD.Grnd
  N3: Part1.D5_PWM, LCD.D/C
  N4: Part1.D6_PWM, LCD.SCE
  N5: Part1.D7, LCD.RST
  VCC: Part1.5V, LCD.Vcc

custom parts:
  : Nokia 5110 LCD with 8 pin. It's a 45mm*45mm module part. Description: The Nokia 5110 is a basic graphic LCD screen for lots of applications. It was originally intended for as a cell phone screen. This one is mounted on an easy to solder PCB. It uses the PCD8544 controller. The PCD8544 is a low power CMOS LCD controller/driver, designed to drive a graphic display of 48 rows and 84 columns. All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
