# Fritzing sketch DoubleShiftWithFETs (saved by Fritzing 0.9.0b)
breadboards: 1

parts:
  R1c = Resistor [tolerance=±5% resistance=1k package=THT]
  R1b = Resistor [tolerance=±5% resistance=10k package=THT]
  Part1 = Arduino Uno (Rev3)
  U2 = 74HC595 [package="DIP16 [THT]"]
  U1 = SMA420564 [part_number=SMA420564]
  R2b = Resistor [tolerance=±5% resistance=10k package=THT]
  R2c = Resistor [tolerance=±5% resistance=1k package=THT]
  R3b = Resistor [tolerance=±5% resistance=10k package=THT]
  R4b = Resistor [tolerance=±5% resistance=10k package=THT]
  R3c = Resistor [tolerance=±5% resistance=1k package=THT]
  R4c = Resistor [tolerance=±5% resistance=1k package=THT]
  U3 = 74HC595 [package="DIP16 [THT]"]
  Q1 = 2N7000 FET N-Channel [part_number=2N7000 package=TO92]
  Q2 = 2N7000 FET N-Channel [part_number=2N7000 package=TO92]
  Q3 = 2N7000 FET N-Channel [part_number=2N7000 package=TO92]
  Q4 = 2N7000 FET N-Channel [part_number=2N7000 package=TO92]

nets:
  D1-: R1c.Pin_0, U1.D1
  N1: R1c.Pin_1, Q1.drain
  D1ctl: R1b.Pin_0, U3.Q0
  N2: R1b.Pin_1, Q1.gate
  GND: Part1.GND, U2.GND, U2.OE, U3.GND, U3.OE, Q1.source, Q2.source, Q3.source, Q4.source
  N3: Part1.D3_PWM, U2.DS
  N4: Part1.D4, U2.ST_CP, U3.ST_CP
  N5: Part1.D5_PWM, U2.SH_CP, U3.SH_CP
  Vcc: Part1.5V, U2.MR, U2.VCC, U3.MR, U3.VCC
  N6: U2.Q1, U1.B
  N7: U2.Q2, U1.C
  N8: U2.Q3, U1.D
  N9: U2.Q4, U1.E
  N10: U2.Q5, U1.F
  N11: U2.Q6, U1.G
  N12: U2.Q7, U1.dp
  N13: U2.Q7', U3.DS
  N14: U2.Q0, U1.A
  D4-: U1.D4, R4c.Pin_0
  D2-: U1.D2, R2c.Pin_0
  D3-: U1.D3, R3c.Pin_0
  D2ctl: R2b.Pin_0, U3.Q1
  N15: R2b.Pin_1, Q2.gate
  N16: R2c.Pin_1, Q2.drain
  D3ctl: R3b.Pin_0, U3.Q2
  N17: R3b.Pin_1, Q3.gate
  D4ctl: R4b.Pin_0, U3.Q3
  N18: R4b.Pin_1, Q4.gate
  N19: R3c.Pin_1, Q3.drain
  N20: R4c.Pin_1, Q4.drain

custom parts:
  2N7000 FET N-Channel: A 2N7000 MOSFET N-Channel Transistor
