# Fritzing sketch LedCurrentControl (saved by Fritzing 0.9.2b)
breadboards: 1

parts:
  Part1 = Arduino Uno (Rev3)
  Q2 = MOSFET-NCHANNEL [part_number=IRF3205 package=to220v]
  LED1 = LED - 3mm [color="Blue (430nm)" package="3 mm [THT]"]
  LED2 = LED - 3mm [color="Blue (430nm)" package="3 mm [THT]"]
  LED3 = LED - 3mm [color="Blue (430nm)" package="3 mm [THT]"]
  R1 = Resistor [tolerance=±5% resistance=220 package=THT]
  Q1 = MOSFET-NCHANNEL [part_number=IRF3205 package=to220v]
  C1 = Electrolytic Capacitor [capacitance=47µF package="100 mil [THT, electrolytic]"]
  R2 = Resistor [tolerance=±5% resistance=220 package=THT]
  LED_Power_(12V) = Power plug
  R3 = Rotary Potentiometer (Small) [maximum_resistance=10kΩ package=THT]

nets:
  N1: Part1.A0, R3.wiper
  N2: Part1.D6_PWM, R2.Pin_0
  5V: Part1.5V, R3.leg1
  GND: Part1.GND, Q2.S, Q1.S, C1.-, LED_Power_(12V).GND, R3.leg2
  N3: Q2.G, Q1.G, Q1.D, C1.+, R2.Pin_1
  LED Array Cathode: Q2.D, R1.Pin_1
  N4: LED1.cathode, LED2.anode
  N5: LED1.anode, LED_Power_(12V).VCC
  N6: LED2.cathode, LED3.anode
  N7: LED3.cathode, R1.Pin_0

notes:
  12V LED strip or equivalent
