# Fritzing sketch LedPanelDisplay72R02 (saved by Fritzing 0.9.2b)
breadboards: 1

parts:
  Part1 = Arduino Uno (Rev3)
  U1 = IC, DIP package, 28 pins [chip_label=72R02]
  S1 = 74HC595 [package="DIP16 [THT]"]
  S2 = 74HC595 [package="DIP16 [THT]"]
  S3 = 74HC595 [package="DIP16 [THT]"]
  R1 = Resistor [tolerance=±5% resistance=470 package=THT]
  R2 = Resistor [tolerance=±5% resistance=470 package=THT]
  R3 = Resistor [tolerance=±5% resistance=470 package=THT]
  R4 = Resistor [tolerance=±5% resistance=470 package=THT]
  R5 = Resistor [tolerance=±5% resistance=470 package=THT]
  R6 = Resistor [tolerance=±5% resistance=470 package=THT]
  R7 = Resistor [tolerance=±5% resistance=470 package=THT]
  R8 = Resistor [tolerance=±5% resistance=470 package=THT]
  R9 = Resistor [tolerance=±5% resistance=470 package=THT]
  R10 = Resistor [tolerance=±5% resistance=470 package=THT]
  R11 = Resistor [tolerance=±5% resistance=470 package=THT]
  R12 = Resistor [tolerance=±5% resistance=470 package=THT]
  R13 = Resistor [tolerance=±5% resistance=470 package=THT]
  R14 = Resistor [tolerance=±5% resistance=470 package=THT]

nets:
  CS: Part1.D8, S1.ST_CP, S2.ST_CP, S3.ST_CP
  DATA: Part1.D11_PWM/MOSI, S3.DS
  SCK: Part1.D13/SCK, S1.SH_CP, S2.SH_CP, S3.SH_CP
  VCC: Part1.5V, S1.MR, S1.VCC, S2.MR, S2.VCC, S3.MR, S3.VCC
  GND: Part1.GND, S1.GND, S1.OE, S2.GND, S2.OE, S3.GND, S3.OE, R1.Pin_1, R2.Pin_1, R3.Pin_1, R4.Pin_1, R5.Pin_1, R6.Pin_1, R7.Pin_1
  N1: U1.pin1, R7.Pin_0
  N2: U1.pin2, S3.Q6
  N3: U1.pin3, R6.Pin_0
  N4: U1.pin4, S3.Q5
  N5: U1.pin5, R5.Pin_0
  N6: U1.pin6, S3.Q4
  N7: U1.pin7, R4.Pin_0
  N8: U1.pin8, S3.Q3
  N9: U1.pin9, R3.Pin_0
  N10: U1.pin10, S3.Q2
  N11: U1.pin11, R2.Pin_0
  N12: U1.pin12, S3.Q1
  N13: U1.pin13, R1.Pin_0
  N14: U1.pin14, S3.Q0
  N15: U1.pin15, S2.Q4
  N16: U1.pin16, S2.Q5
  N17: U1.pin17, R8.Pin_1
  N18: U1.pin18, S2.Q6
  N19: U1.pin19, R9.Pin_1
  N20: U1.pin20, S2.Q2
  N21: U1.pin21, R10.Pin_1
  N22: U1.pin22, R14.Pin_1
  N23: U1.pin23, R13.Pin_1
  N24: U1.pin24, S2.Q1
  N25: U1.pin25, R12.Pin_1
  N26: U1.pin26, S2.Q7
  N27: U1.pin27, R11.Pin_1
  N28: U1.pin28, S2.Q3
  N29: S1.Q1, R8.Pin_0
  N30: S1.Q2, R9.Pin_0
  N31: S1.Q3, R10.Pin_0
  N32: S1.Q4, R14.Pin_0
  N33: S1.Q5, R13.Pin_0
  N34: S1.Q6, R12.Pin_0
  N35: S1.Q7, R11.Pin_0
  N36: S1.DS, S2.Q7'
  N37: S2.DS, S3.Q7'
