# Fritzing sketch LedTemperatureDisplay (saved by Fritzing 0.9.0b)
breadboards: 1

parts:
  R1c = Resistor [tolerance=±5% resistance=1k package=THT]
  R1b = Resistor [tolerance=±5% resistance=10k package=THT]
  Part1 = Arduino Uno (Rev3)
  U2 = 74HC595 [package="DIP16 [THT]"]
  Q1 = NPN-Transistor [part_number=S9013 package="TO92 [THT]"]
  Q2 = NPN-Transistor [part_number=S9013 package="TO92 [THT]"]
  R2b = Resistor [tolerance=±5% resistance=10k package=THT]
  R2c = Resistor [tolerance=±5% resistance=1k package=THT]
  Q3 = NPN-Transistor [part_number=S9013 package="TO92 [THT]"]
  Q4 = NPN-Transistor [part_number=S9013 package="TO92 [THT]"]
  R3b = Resistor [tolerance=±5% resistance=10k package=THT]
  R4b = Resistor [tolerance=±5% resistance=10k package=THT]
  R3c = Resistor [tolerance=±5% resistance=1k package=THT]
  R4c = Resistor [tolerance=±5% resistance=1k package=THT]
  U3 = SMA420564 [part_number=SMA420564]
  T1 = LM35 Temperature Sensor [package="TO92 [THT]"]

nets:
  D1-: R1c.Pin_0, U3.D1
  N1: R1c.Pin_1, Q1.C
  D1ctl: R1b.Pin_0, Part1.D6_PWM
  N2: R1b.Pin_1, Q1.B
  N3: Part1.A0, T1.Vout
  D3ctl: Part1.D8, R3b.Pin_0
  D4ctl: Part1.D9_PWM, R4b.Pin_0
  GND: Part1.GND, U2.GND, U2.OE, Q1.E, Q2.E, Q3.E, Q4.E, T1.GND
  N4: Part1.D3_PWM, U2.DS
  N5: Part1.D4, U2.ST_CP
  N6: Part1.D5_PWM, U2.SH_CP
  D2ctl: Part1.D7, R2b.Pin_0
  5V: Part1.5V, U2.MR, U2.VCC, T1.+Vs
  N7: U2.Q1, U3.B
  N8: U2.Q2, U3.C
  N9: U2.Q3, U3.D
  N10: U2.Q4, U3.E
  N11: U2.Q5, U3.F
  N12: U2.Q6, U3.G
  N13: U2.Q7, U3.dp
  N14: U2.Q0, U3.A
  N15: Q2.B, R2b.Pin_1
  N16: Q2.C, R2c.Pin_1
  D2-: R2c.Pin_0, U3.D2
  N17: Q3.B, R3b.Pin_1
  N18: Q3.C, R3c.Pin_1
  N19: Q4.B, R4b.Pin_1
  N20: Q4.C, R4c.Pin_1
  D3-: R3c.Pin_0, U3.D3
  D4-: R4c.Pin_0, U3.D4
