# Fritzing sketch LevelIndicatorLM3915 (saved by Fritzing 0.9.0b)
breadboards: 1

parts:
  IC1 = LM3915 [package=THT]
  LED1 = LED - 3mm [color="Yellow (595nm)" package="3 mm [THT]"]
  LED2 = LED - 3mm [color="Yellow (595nm)" package="3 mm [THT]"]
  LED3 = LED - 3mm [color="Yellow (595nm)" package="3 mm [THT]"]
  LED4 = LED - 3mm [color="Yellow (595nm)" package="3 mm [THT]"]
  LED5 = LED - 3mm [color="Yellow (595nm)" package="3 mm [THT]"]
  LED6 = LED - 3mm [color="Yellow (595nm)" package="3 mm [THT]"]
  LED7 = LED - 3mm [color="Yellow (595nm)" package="3 mm [THT]"]
  LED9 = LED - 3mm [color="Red (633nm)" package="3 mm [THT]"]
  LED8 = LED - 3mm [color="Yellow (595nm)" package="3 mm [THT]"]
  LED10 = LED - 3mm [color="Red (633nm)" package="3 mm [THT]"]
  R5 = Resistor [tolerance=±5% resistance=220 package=THT]
  R1 = Resistor [tolerance=±5% resistance=1k package=THT]
  R4 = Resistor [tolerance=±5% resistance=1k package=THT]
  R3 = Resistor [tolerance=±5% resistance=1k package=THT]
  C1 = Ceramic Capacitor [capacitance=100nF package="100 mil [THT, multilayer]"]
  C2 = Ceramic Capacitor [capacitance=100nF package="100 mil [THT, multilayer]"]
  Part1 = Arduino Uno (Rev3)
  R2 = Resistor [tolerance=±5% resistance=1k package=THT]
  R6 = Resistor [tolerance=±5% resistance=10k package=THT]
  C3 = Electrolytic Capacitor [capacitance=10µF package="100 mil [THT, electrolytic]"]

nets:
  N1: IC1.OUT1, LED1.cathode
  GND: IC1.V-, IC1.R_LO, C1.0, C2.1, Part1.GND, R2.Pin_1, R6.Pin_1, C3.-
  vcc: IC1.V+, R5.Pin_0, C1.1, Part1.5V
  N2: IC1.SIG, Part1.D6_PWM, R6.Pin_0, C3.+
  N3: IC1.R_HIGH, IC1.REF_OUT, R1.Pin_0
  N4: IC1.REF_ADJ, R1.Pin_1, R2.Pin_0
  N5: IC1.MODE, Part1.D7
  N6: IC1.OUT10, R4.Pin_0
  N7: IC1.OUT9, R3.Pin_0
  N8: IC1.OUT8, LED8.cathode
  N9: IC1.OUT7, LED7.cathode
  N10: IC1.OUT6, LED6.cathode
  N11: IC1.OUT5, LED5.cathode
  N12: IC1.OUT4, LED4.cathode
  N13: IC1.OUT3, LED3.cathode
  N14: IC1.OUT2, LED2.cathode
  N15: LED1.anode, LED2.anode, LED3.anode, LED4.anode, LED5.anode, LED6.anode, LED7.anode, LED9.anode, LED8.anode, LED10.anode, R5.Pin_1, C2.0
  N16: LED9.cathode, R3.Pin_1
  N17: LED10.cathode, R4.Pin_1

custom parts:
  LM3915: Dot/Bar Display Driver
