# Fritzing sketch LightOrNot (saved by Fritzing 0.9.2b)
breadboards: 1

parts:
  Part1 = Arduino Uno (Rev3)
  R1 = Photocell (LDR) [package=THT]
  R2 = Resistor [tolerance=±5% resistance=10k package=THT]
  R3 = Resistor [tolerance=±5% resistance=220 package=THT]
  LED1 = LED - 5mm [color="Red (633nm)" package="5 mm [THT]"]

nets:
  N1: Part1.A0, R1.pin_1, R2.Pin_0
  N2: Part1.D2, LED1.anode
  VCC: Part1.5V, R1.pin_0
  GND: Part1.GND, R2.Pin_1, R3.Pin_0
  N3: R3.Pin_1, LED1.cathode
