# Fritzing sketch MakerUno (saved by Fritzing 0.9.2b)
breadboards: 1

parts:
  U1 = atmega328 [package=dip]
  DS12 = LED - 5mm [color="Red (633nm)" package="5 mm [THT]"]
  R22 = Resistor [tolerance=±5% resistance=10k package=THT]
  Q1 = NPN-Transistor [package="TO92 [THT]"]
  Q13 = Basic FET N-Channel [package="TO220 [THT]"]
  LS1 = Piezo Speaker
  R8 = Resistor [tolerance=±5% resistance=1k package=THT]
  R33 = Resistor [tolerance=±5% resistance=3.3M package=THT]
  Q12 = Basic FET N-Channel [package="TO220 [THT]"]
  R21 = Resistor [tolerance=±5% resistance=10k package=THT]
  DS11 = LED - 5mm [color="Red (633nm)" package="5 mm [THT]"]
  R32 = Resistor [tolerance=±5% resistance=3.3M package=THT]
  DS6 = LED - 5mm [color="Red (633nm)" package="5 mm [THT]"]
  R16 = Resistor [tolerance=±5% resistance=10k package=THT]
  R27 = Resistor [tolerance=±5% resistance=3.3M package=THT]
  Q7 = Basic FET N-Channel [package="TO220 [THT]"]
  R9 = Resistor [tolerance=±5% resistance=1k package=THT]
  S3 = Pushbutton [package=THT]
  S1 = Toggle Switch [package=THT]

nets:
  D2: U1.D2, Q13.gate, R33.Pin_1, R9.Pin_1
  D3: U1.D3_(PWM), Q12.gate, R32.Pin_1
  VCC: U1.VCC, DS12.anode, LS1.pin2, DS11.anode, DS6.anode
  GND: U1.GND, Q1.E, Q13.source, R33.Pin_0, Q12.source, R32.Pin_0, R27.Pin_0, Q7.source, S3.leg0
  D8: U1.D8, R8.Pin_1, R27.Pin_1, Q7.gate
  N1: DS12.cathode, R22.Pin_1
  N2: R22.Pin_0, Q13.drain
  N3: Q1.B, S1.L1
  N4: Q1.C, LS1.pin1
  N5: R8.Pin_0, S1.COM
  N6: Q12.drain, R21.Pin_0
  N7: R21.Pin_1, DS11.cathode
  N8: DS6.cathode, R16.Pin_1
  N9: R16.Pin_0, Q7.drain
  N10: R9.Pin_0, S3.leg1

notes:
  not laid out - incomplete
  LED and Buzzer connected to D8
  LED and push-button connected to D2
  LED connected to digital pins D3-D7,D9-D13
  Partial schematic of features on digital pins
