# Fritzing sketch MonostablePulseExtender (saved by Fritzing 0.9.0b)
breadboards: 1

parts:
  IC1 = 74LS122 [package=dil14]
  R2 = Resistor [tolerance=±5% resistance=100k package=THT]
  C2 = Electrolytic Capacitor [capacitance=33µF package="100 mil [THT, electrolytic]"]
  LED1 = LED - 3mm [color="Red (633nm)" package="3 mm [THT]"]
  LED2 = LED - 3mm [color="Green (555nm)" package="3 mm [THT]"]
  R3 = Resistor [tolerance=±5% resistance=1k package=THT]
  Part1 = Arduino Uno (Rev3)

nets:
  GND: IC1.A1, IC1.A2, IC1.GND, IC1.Cext, C2.-, R3.Pin_0, Part1.GND
  SIGNAL: IC1.B1, Part1.D7
  Vcc: IC1.B2, IC1.CLR, IC1.VCC, R2.Pin_0, Part1.5V
  N1: IC1.-Q, LED1.anode
  Qread: IC1.Q, LED2.anode, Part1.A0
  N2: IC1.Rext/Cext, R2.Pin_1, C2.+
  N3: LED1.cathode, LED2.cathode, R3.Pin_1

custom parts:
  74LS122: 74LS122 Monostable
