# Fritzing sketch MotorControlPWM (saved by Fritzing 0.9.0b)
breadboards: 1

parts:
  M1 = DC Motor
  D1 = Rectifier Diode [part_number=1N4001 package="300 mil [THT]"]
  Q1 = NPN-Transistor [part_number=S9013 package="TO92 [THT]"]
  Part1 = Arduino Uno (Rev3)
  VCC1 = 4 x AAA Battery Mount
  R1 = Resistor [tolerance=±5% resistance=1k package=THT]

nets:
  N1: M1.pin_1, D1.cathode, VCC1.+
  N2: M1.pin_2, D1.anode, Q1.C
  N3: Q1.E, Part1.GND, VCC1.-
  N4: Q1.B, R1.Pin_1
  N5: Part1.D3_PWM, R1.Pin_0
