# Fritzing sketch MultiSlaveSPI (saved by Fritzing 0.9.2b)
breadboards: 2

parts:
  R1 = Resistor [tolerance=±5% resistance=220 package=THT]
  7_Segment3 = 7 Segment Display
  R2 = Resistor [tolerance=±5% resistance=220 package=THT]
  R3 = Resistor [tolerance=±5% resistance=220 package=THT]
  R4 = Resistor [tolerance=±5% resistance=220 package=THT]
  R5 = Resistor [tolerance=±5% resistance=220 package=THT]
  R6 = Resistor [tolerance=±5% resistance=220 package=THT]
  R7 = Resistor [tolerance=±5% resistance=220 package=THT]
  R8 = Resistor [tolerance=±5% resistance=220 package=THT]
  U1 = 74HC595 [package="DIP16 [THT]"]
  Part2 = Arduino Uno (Rev3)
  R14 = Resistor [tolerance=±5% resistance=100k package=THT]
  R15 = Resistor [tolerance=±5% resistance=100k package=THT]
  R16 = Resistor [tolerance=±5% resistance=680 package=THT]
  R17 = Resistor [tolerance=±5% resistance=680 package=THT]
  R18 = Resistor [tolerance=±5% resistance=680 package=THT]
  R19 = Resistor [tolerance=±5% resistance=680 package=THT]
  R20 = Resistor [tolerance=±5% resistance=680 package=THT]
  R21 = Resistor [tolerance=±5% resistance=680 package=THT]
  R22 = Resistor [tolerance=±5% resistance=680 package=THT]
  R23 = Resistor [tolerance=±5% resistance=680 package=THT]
  R24 = Resistor [tolerance=±5% resistance=680 package=THT]
  R25 = Resistor [tolerance=±5% resistance=680 package=THT]
  R26 = Resistor [tolerance=±5% resistance=680 package=THT]
  LED12 = LED - 3mm [color="Green (555nm)" package="3 mm [THT]"]
  LED13 = LED - 3mm [color="Red (633nm)" package="3 mm [THT]"]
  LED14 = LED - 3mm [color="Red (633nm)" package="3 mm [THT]"]
  LED15 = LED - 3mm [color="Red (633nm)" package="3 mm [THT]"]
  LED16 = LED - 3mm [color="Red (633nm)" package="3 mm [THT]"]
  LED17 = LED - 3mm [color="Red (633nm)" package="3 mm [THT]"]
  LED18 = LED - 3mm [color="Red (633nm)" package="3 mm [THT]"]
  LED19 = LED - 3mm [color="Red (633nm)" package="3 mm [THT]"]
  LED20 = LED - 3mm [color="Red (633nm)" package="3 mm [THT]"]
  LED21 = LED - 3mm [color="Red (633nm)" package="3 mm [THT]"]
  LED22 = LED - 3mm [color="Red (633nm)" package="3 mm [THT]"]
  IC2 = IC, DIP package, 16 pins [chip_label=CD4017 part_number=CD4017]

nets:
  ssA: R1.Pin_0, U1.Q0
  N1: R1.Pin_1, 7_Segment3.Segment_A
  N2: 7_Segment3.Segment_E, R5.Pin_1
  N3: 7_Segment3.Segment_D, R4.Pin_1
  GND: 7_Segment3.common_cathode, U1.GND, U1.OE, Part2.GND, R14.Pin_0, R15.Pin_0, R16.Pin_1, R17.Pin_1, R18.Pin_1, R19.Pin_1, R20.Pin_1, R21.Pin_1, R22.Pin_1, R23.Pin_1, R24.Pin_1, R25.Pin_1, R26.Pin_1, IC2.pin8
  N4: 7_Segment3.Segment_C, R3.Pin_1
  N5: 7_Segment3.Segment_DP, R8.Pin_1
  N6: 7_Segment3.Segment_B, R2.Pin_1
  N7: 7_Segment3.Segment_F, R6.Pin_1
  N8: 7_Segment3.Segment_G, R7.Pin_1
  ssB: R2.Pin_0, U1.Q1
  ssC: R3.Pin_0, U1.Q2
  ssD: R4.Pin_0, U1.Q3
  ssE: R5.Pin_0, U1.Q4
  ssF: R6.Pin_0, U1.Q5
  ssG: R7.Pin_0, U1.Q6
  ssDP: R8.Pin_0, U1.Q7
  Vcc: U1.MR, U1.VCC, Part2.5V, IC2.pin16
  CLOCK: U1.SH_CP, Part2.D13/SCK, IC2.pin14
  LED_LATCH: U1.ST_CP, Part2.D4
  DATA: U1.DS, Part2.D11_PWM/MOSI
  COUNTER_LATCH: Part2.D3_PWM, R15.Pin_1, IC2.pin13
  N9: R14.Pin_1, IC2.pin15
  N10: R16.Pin_0, LED17.cathode
  N11: R17.Pin_0, LED14.cathode
  N12: R18.Pin_0, LED13.cathode
  N13: R19.Pin_0, LED16.cathode
  N14: R20.Pin_0, LED15.cathode
  N15: R21.Pin_0, LED18.cathode
  N16: R22.Pin_0, LED19.cathode
  N17: R23.Pin_0, LED20.cathode
  N18: R24.Pin_0, LED21.cathode
  N19: R25.Pin_0, LED22.cathode
  N20: R26.Pin_0, LED12.cathode
  CARRY: LED12.anode, IC2.pin12
  Q9: LED13.anode, IC2.pin11
  Q8: LED14.anode, IC2.pin9
  Q7: LED15.anode, IC2.pin6
  Q6: LED16.anode, IC2.pin5
  Q5: LED17.anode, IC2.pin1
  Q4: LED18.anode, IC2.pin10
  Q3: LED19.anode, IC2.pin7
  Q2: LED20.anode, IC2.pin4
  Q1: LED21.anode, IC2.pin2
  Q0: LED22.anode, IC2.pin3

notes:
  Counter Module
  7-segment LED Controller
  7-segment LED Module
