# Fritzing sketch ExpansionBoard (saved by Fritzing 0.9.2b)
breadboards: 1

parts:
  IC1 = Voltage Regulator AMS1117 [package=sot223]
  Part1 = Arduino Nano (Rev3.0)
  7-12V = Power plug
  LED1 = smd LED [color="Red (633nm)" package="0603 [SMD]"]
  R1 = Resistor [tolerance=±5% resistance=1k package=THT]
  D1 = Rectifier Diode [part_number=1N4007 package="300 mil [THT]"]
  S-RESET = Pushbutton [package=THT]
  C1 = Electrolytic Capacitor [capacitance=100µF voltage=25V package="100 mil [THT, electrolytic]"]
  C2 = Ceramic Capacitor [capacitance=100nF voltage=25V package="100 mil [THT, multilayer]"]
  C3 = Tantalum Capacitor [capacitance=100µF package="100 mil [THT, tantalum]"]
  C4 = Ceramic Capacitor [capacitance=100nF package="100 mil [THT, multilayer]"]
  C5 = Tantalum Capacitor [capacitance=100µF package="100 mil [THT, tantalum]"]
  C6 = Ceramic Capacitor [capacitance=100nF package="100 mil [THT, multilayer]"]

nets:
  GND: IC1.GND, Part1.GND, 7-12V.GND, R1.Pin_1, S-RESET.leg0, C1.-, C2.0, C3.-, C4.0, C5.-, C6.0
  3V3: IC1.OUT, C5.+, C6.1
  5V: IC1.IN, Part1.5V, LED1.anode, C3.+, C4.1
  N1: Part1.RESET, S-RESET.leg1
  VIN: Part1.VIN, D1.cathode, C1.+, C2.1
  N2: 7-12V.VCC, D1.anode
  N3: LED1.cathode, R1.Pin_0
