# Fritzing sketch ArdWinVaders (saved by Fritzing 0.9.2b)
breadboards: 1

parts:
  OLED1 = 128x64 Monochrom OLED Display with SPI Control
  Arduino1 = Arduino Mini (Rev5)
  SwF = Pushbutton [package="[THT]"]
  SwL = Pushbutton [package="[THT]"]
  SwR = Pushbutton [package="[THT]"]
  RSwR = Resistor [tolerance=±5% resistance=10k package=THT]
  RSwL = Resistor [tolerance=±5% resistance=10k package=THT]
  RSwF = Resistor [tolerance=±5% resistance=10k package=THT]
  J1 = Piezo Speaker
  R1 = Resistor [tolerance=±5% resistance=100 package=THT]

nets:
  N1: OLED1.Data, Arduino1.D9_PWM
  N2: OLED1.Clock, Arduino1.D10_PWM
  N3: OLED1.SA0/DC, Arduino1.D11_PWM
  N4: OLED1.CS, Arduino1.D12
  Vcc: OLED1.Vin, Arduino1.VCC, SwF.Pin_1, SwF.Pin_2, SwL.Pin_1, SwL.Pin_2, SwR.Pin_1, SwR.Pin_2
  GND: OLED1.GND, Arduino1.GND, RSwR.Pin_0, RSwL.Pin_0, RSwF.Pin_0, J1.pin1
  N5: Arduino1.D2, SwF.Pin_3, SwF.Pin_4, RSwF.Pin_1
  N6: Arduino1.D3_PWM, SwR.Pin_3, SwR.Pin_4, RSwR.Pin_1
  N7: Arduino1.D4, SwL.Pin_3, SwL.Pin_4, RSwL.Pin_1
  N8: Arduino1.D6_PWM, R1.Pin_0
  N9: J1.pin2, R1.Pin_1

notes:
  some OLED units don't break out the RESET pin - hence shown not connected
