# Fritzing sketch SSD1306BareBack (saved by Fritzing 0.9.2b)
breadboards: 1

parts:
  OLED1 = 128x64 Monochrom OLED Display with SPI Control
  Arduino1 = Arduino Mini (Rev5)

nets:
  N1: OLED1.Data, Arduino1.D9_PWM
  N2: OLED1.Clock, Arduino1.D10_PWM
  N3: OLED1.SA0/DC, Arduino1.D11_PWM
  N4: OLED1.CS, Arduino1.D12
  PROBE: OLED1.Vin, Arduino1.VCC, Arduino1.A0
  GND: OLED1.GND, Arduino1.GND

notes:
  some units don't break out the RESET pin - hence shown not connected
  ..or plugged into any 0-3.3V source that is worth measuring
