# Fritzing sketch SSD1306_u8g2 (saved by Fritzing 0.9.2b)
breadboards: 1

parts:
  Part1 = Arduino Uno (Rev3)
  OLED1 = 128x32 I2C Monochrome OLED Display
  R1 = Resistor [tolerance=±5% resistance=10k package=THT]
  R2 = Resistor [tolerance=±5% resistance=10k package=THT]

nets:
  N1: Part1.A4/SDA, OLED1.SDA, R2.Pin_1
  N2: Part1.A5/SCL, OLED1.SCL, R1.Pin_1
  VCC: Part1.3V3, OLED1.3.3V, R1.Pin_0, R2.Pin_0
  GND: Part1.GND, OLED1.GND
