# Fritzing sketch PiezoVibrationDetector (saved by Fritzing 0.9.2b)
breadboards: 1

parts:
  Part1 = Arduino Uno (Rev3)
  R1 = Trimmer Potentiometer [maximum_resistance=100kΩ package=THT]
  PIEZO = Crystal [frequency="16 Mhz" package=THT]
  D1 = Zener Diode [part_number=1N4728A breakdown_voltage=3.3V package="300 mil [THT]"]

nets:
  N1: Part1.D6_PWM, PIEZO.pin_0, D1.cathode
  N2: Part1.D7, R1.wiper
  N3: Part1.5V, R1.leg1
  GND: Part1.GND, R1.leg2, PIEZO.pin_1, D1.anode

notes:
  ^^ actually a piezo transducer, not a crystal oscillator, but the same idea
