# Fritzing sketch Popcorn (saved by Fritzing 0.9.0b)
breadboards: 1

parts:
  Part1 = Arduino Uno (Rev3)
  J1 = Piezo Speaker
  R1 = Resistor [tolerance=±5% resistance=1k package=THT]
  LED1 = LED - 5mm [color="Red (633nm)" package="5 mm [THT]"]

nets:
  N1: Part1.GND, J1.pin1, LED1.cathode
  N2: Part1.D6_PWM, J1.pin2, R1.Pin_0
  N3: R1.Pin_1, LED1.anode
