# Fritzing sketch MultiVoltageGPIO (saved by Fritzing 0.9.2b)
breadboards: 1

parts:
  D1 = Rectifier Diode [part_number=1N4148 package="300 mil [THT]"]
  D2 = Rectifier Diode [part_number=1N4148 package="300 mil [THT]"]
  D3 = Rectifier Diode [part_number=1N4148 package="300 mil [THT]"]
  D4 = Rectifier Diode [part_number=1N4148 package="300 mil [THT]"]
  C1 = Ceramic Capacitor [capacitance=220nF voltage=25V package="100 mil [THT, multilayer]"]
  C2 = Ceramic Capacitor [capacitance=220nF voltage=25V package="100 mil [THT, multilayer]"]
  C3 = Ceramic Capacitor [capacitance=220nF voltage=25V package="100 mil [THT, multilayer]"]
  C4 = Ceramic Capacitor [capacitance=1µF voltage=25V package="100 mil [THT, multilayer]"]
  Rcl = Resistor [tolerance=±5% resistance=2.2k package=THT]
  D5 = Zener Diode [part_number=1N4742 breakdown_voltage=12V package="300 mil [THT]"]
  Part4 = Arduino Uno (Rev3)
  Q1 = Basic FET P-Channel [part_number=BS250 package="DPak [SMD]"]
  R1 = Resistor [tolerance=±5% resistance=100k package=THT]
  Q2 = NPN-Transistor [part_number=2N3904 package="TO92 [THT]"]
  R2 = Resistor [tolerance=±5% resistance=10k package=THT]
  Q3 = NPN-Transistor [part_number=2N3904 package="TO92 [THT]"]
  Q4 = NPN-Transistor [part_number=2N3904 package="TO92 [THT]"]
  R3 = Resistor [tolerance=±5% resistance=10k package=THT]
  R4 = Resistor [tolerance=±5% resistance=10k package=THT]
  D6 = Rectifier Diode [part_number=1N5819 package="300 mil [THT]"]
  RL = Resistor [tolerance=±5% resistance=10k package=THT]
  LED1 = LED - 3mm [color="Red (633nm)" package="3 mm [THT]"]

nets:
  N1: D1.cathode, D2.anode, C1.1
  5V: D1.anode, Part4.5V, R3.Pin_0
  N2: D2.cathode, D3.anode, C2.1
  N3: D3.cathode, D4.anode, C3.1
  N4: D4.cathode, C4.1, Rcl.Pin_0
  PUMP_A: C1.0, C3.0, Part4.D3_PWM
  PUMP_B: C2.0, Part4.D11_PWM/MOSI
  GND: C4.0, D5.anode, Part4.GND, Q2.E, Q3.E, Q4.E, LED1.cathode
  VHIGH: Rcl.Pin_1, D5.cathode, Q1.source, R1.Pin_0
  VHIGH_IO: Part4.D4, R2.Pin_1
  VLOW_IO: Part4.D5_PWM, R4.Pin_0, D6.anode
  N5: Q1.Gate, R1.Pin_1, Q2.C
  VOUT: Q1.drain, Q3.C, D6.cathode, RL.Pin_0
  N6: Q2.B, R2.Pin_0
  N7: Q3.B, Q4.C, R3.Pin_1
  N8: Q4.B, R4.Pin_1
  N9: RL.Pin_1, LED1.anode

notes:
  12V
  ~16V
