# Fritzing sketch PrecisionTimer (saved by Fritzing 0.9.2b)
breadboards: 1

parts:
  Part1 = Arduino Uno (Rev3)
  START-STOP = Pushbutton [package="[THT]"]

nets:
  GND: Part1.GND, START-STOP.Pin_1, START-STOP.Pin_2
  N1: Part1.D2, START-STOP.Pin_3, START-STOP.Pin_4
