# Fritzing sketch R2RDAC (saved by Fritzing 0.9.2b)
breadboards: 1

parts:
  WaveGenerator = Arduino Uno (Rev3)
  Rb0 = Resistor [tolerance=±5% resistance=2k package=THT]
  Rd0 = Resistor [tolerance=±5% resistance=2k package=THT]
  Rb1 = Resistor [tolerance=±5% resistance=2k package=THT]
  Rd1 = Resistor [tolerance=±5% resistance=1k package=THT]
  Rb2 = Resistor [tolerance=±5% resistance=2k package=THT]
  Rd2 = Resistor [tolerance=±5% resistance=1k package=THT]
  Rb3 = Resistor [tolerance=±5% resistance=2k package=THT]
  Rd3 = Resistor [tolerance=±5% resistance=1k package=THT]
  Rb4 = Resistor [tolerance=±5% resistance=2k package=THT]
  Rd4 = Resistor [tolerance=±5% resistance=1k package=THT]
  Rb5 = Resistor [tolerance=±5% resistance=2k package=THT]
  Rd5 = Resistor [tolerance=±5% resistance=1k package=THT]
  Rb6 = Resistor [tolerance=±5% resistance=2k package=THT]
  Rd6 = Resistor [tolerance=±5% resistance=1k package=THT]
  Rb7 = Resistor [tolerance=±5% resistance=2k package=THT]
  Rd7 = Resistor [tolerance=±5% resistance=1k package=THT]
  Rd8 = Resistor [tolerance=±5% resistance=1k package=THT]
  Rb8 = Resistor [tolerance=±5% resistance=2k package=THT]
  Rb9 = Resistor [tolerance=±5% resistance=2k package=THT]
  Rd9 = Resistor [tolerance=±5% resistance=1k package=THT]
  Rb10 = Resistor [tolerance=±5% resistance=2k package=THT]
  Rb11 = Resistor [tolerance=±5% resistance=2k package=THT]
  Rb12 = Resistor [tolerance=±5% resistance=2k package=THT]
  Rb13 = Resistor [tolerance=±5% resistance=2k package=THT]
  Rb14 = Resistor [tolerance=±5% resistance=2k package=THT]
  Rb15 = Resistor [tolerance=±5% resistance=2k package=THT]
  Rd10 = Resistor [tolerance=±5% resistance=1k package=THT]
  Rd11 = Resistor [tolerance=±5% resistance=1k package=THT]
  Rd12 = Resistor [tolerance=±5% resistance=1k package=THT]
  Rd13 = Resistor [tolerance=±5% resistance=1k package=THT]
  Rd14 = Resistor [tolerance=±5% resistance=1k package=THT]
  Rd15 = Resistor [tolerance=±5% resistance=1k package=THT]
  U1 = 74HC595 [package="DIP16 [THT]"]
  U2 = 74HC595 [package="DIP16 [THT]"]
  OUT_LED1 = LED - 3mm [color="Green (555nm)" package="3 mm [THT]"]
  OUT_R1 = Resistor [tolerance=±5% resistance=1k package=THT]
  Monitor = Arduino Mega 2560 (Rev3)
  IC1 = LM324 [package=dil16]
  R1 = Resistor [tolerance=±5% resistance=10k package=THT]
  R2 = Resistor [tolerance=±5% resistance=4.7k package=THT]

nets:
  GND: WaveGenerator.GND, Rd0.Pin_0, U1.GND, U1.OE, U2.GND, U2.OE, OUT_R1.Pin_1, Monitor.GND, IC1.GND, R1.Pin_1
  N1: WaveGenerator.D5_PWM, U1.DS
  N2: WaveGenerator.D6_PWM, U1.ST_CP, U2.ST_CP
  N3: WaveGenerator.D7, U1.SH_CP, U2.SH_CP
  VCC: WaveGenerator.5V, U1.MR, U1.VCC, U2.MR, U2.VCC, IC1.V+
  N4: Rb0.Pin_0, Rd0.Pin_1, Rd1.Pin_0
  b0: Rb0.Pin_1, U2.Q7
  N5: Rb1.Pin_0, Rd1.Pin_1, Rd2.Pin_0
  b1: Rb1.Pin_1, U2.Q6
  N6: Rb2.Pin_0, Rd2.Pin_1, Rd3.Pin_0
  b2: Rb2.Pin_1, U2.Q5
  N7: Rb3.Pin_0, Rd3.Pin_1, Rd4.Pin_0
  b3: Rb3.Pin_1, U2.Q4
  N8: Rb4.Pin_0, Rd4.Pin_1, Rd5.Pin_0
  b4: Rb4.Pin_1, U2.Q3
  N9: Rb5.Pin_0, Rd5.Pin_1, Rd6.Pin_0
  b5: Rb5.Pin_1, U2.Q2
  N10: Rb6.Pin_0, Rd6.Pin_1, Rd7.Pin_0
  b6: Rb6.Pin_1, U2.Q1
  N11: Rb7.Pin_0, Rd7.Pin_1, Rd8.Pin_0
  b7: Rb7.Pin_1, U2.Q0
  N12: Rd8.Pin_1, Rb8.Pin_0, Rd9.Pin_0
  b8: Rb8.Pin_1, U1.Q7
  N13: Rb9.Pin_0, Rd9.Pin_1, Rd10.Pin_0
  b9: Rb9.Pin_1, U1.Q6
  N14: Rb10.Pin_0, Rd10.Pin_1, Rd11.Pin_0
  b10: Rb10.Pin_1, U1.Q5
  N15: Rb11.Pin_0, Rd11.Pin_1, Rd12.Pin_0
  b11: Rb11.Pin_1, U1.Q4
  N16: Rb12.Pin_0, Rd12.Pin_1, Rd13.Pin_0
  b12: Rb12.Pin_1, U1.Q3
  N17: Rb13.Pin_0, Rd13.Pin_1, Rd14.Pin_0
  b13: Rb13.Pin_1, U1.Q2
  N18: Rb14.Pin_0, Rd14.Pin_1, Rd15.Pin_0
  b14: Rb14.Pin_1, U1.Q1
  AOUT: Rb15.Pin_0, Rd15.Pin_1, R2.Pin_1
  b15: Rb15.Pin_1, U1.Q0
  N19: U1.Q7', U2.DS
  N20: OUT_LED1.cathode, OUT_R1.Pin_0
  BOUT: OUT_LED1.anode, Monitor.A0, IC1.OUT3, IC1.IN3-
  N21: IC1.IN3+, R1.Pin_0, R2.Pin_0

notes:
  Arduino for output monitoring
  digital waveform generator
  Output unity buffer

custom parts:
  LM324: LM324 Quad OpAmp
