# Fritzing sketch CardCounter (saved by Fritzing 0.9.2b)
breadboards: 1

parts:
  Part1 = Arduino Uno (Rev3)
  U1 = RFID USB Reader
  LED1 = LED - 5mm [color="Red (633nm)" package="5 mm [THT]"]
  LED2 = LED - 5mm [color="Green (555nm)" package="5 mm [THT]"]
  R1 = Resistor [tolerance=±5% resistance=470 package=THT]
  R2 = Resistor [tolerance=±5% resistance=470 package=THT]
  LED3 = LED - 5mm [color="Yellow (595nm)" package="5 mm [THT]"]
  R3 = Resistor [tolerance=±5% resistance=470 package=THT]

nets:
  RST: Part1.D9_PWM, U1.TX-O
  SDA: Part1.D10_PWM/SS, U1.GNDT
  MOSI: Part1.D11_PWM/MOSI, U1.ANT2
  MISO: Part1.D12/MISO, U1.ANT1
  SCK: Part1.D13/SCK, U1.CP
  N1: Part1.D5_PWM, LED1.anode
  N2: Part1.D6_PWM, LED2.anode
  N3: Part1.D7, LED3.anode
  3V3: Part1.3V3, U1.VCC
  GND: Part1.GND, U1.GND, R1.Pin_0, R2.Pin_0, R3.Pin_0
  N4: LED1.cathode, R1.Pin_1
  N5: LED2.cathode, R2.Pin_1
  N6: LED3.cathode, R3.Pin_1
