# Fritzing sketch DeviceDumper (saved by Fritzing 0.9.2b)
breadboards: 1

parts:
  Part1 = Arduino Uno (Rev3)
  U1 = RFID USB Reader

nets:
  RST: Part1.D9_PWM, U1.TX-O
  SDA: Part1.D10_PWM/SS, U1.GNDT
  MOSI: Part1.D11_PWM/MOSI, U1.ANT2
  MISO: Part1.D12/MISO, U1.ANT1
  SCK: Part1.D13/SCK, U1.CP
  GND: Part1.GND, U1.GND
  3V3: Part1.3V3, U1.VCC
