# Fritzing sketch RelayControlTest (saved by Fritzing 0.9.0b)
breadboards: 1

parts:
  Part1 = Arduino Uno (Rev3)
  VCC1 = Battery block 9V
  LED1 = LED - 5mm [color="Red (633nm)" package="5 mm [THT]"]
  M1 = DC Motor
  R1 = Resistor [tolerance=±5% resistance=1k package=THT]
  Part2 = songle relay
  Q1 = NPN-Transistor [part_number=S9013 package="TO92 [THT]"]
  D1 = Rectifier Diode [part_number=1N4007 package="300 mil [THT]"]
  R2 = Resistor [tolerance=±5% resistance=10k package=THT]
  R3 = Resistor [tolerance=±5% resistance=1k package=THT]

nets:
  N1: Part1.D6_PWM, R3.Pin_0
  5V: Part1.5V, Part2.VCC, D1.cathode
  N2: Part1.GND, Q1.E, R2.Pin_1
  GND: VCC1.-, M1.pin_1, R1.Pin_1
  N3: VCC1.+, Part2.GND
  N4: LED1.cathode, R1.Pin_0
  N5: LED1.anode, Part2.A
  N6: M1.pin_2, Part2.B
  N7: Part2.IN, Q1.C, D1.anode
  N8: Q1.B, R2.Pin_0, R3.Pin_1

notes:
  NO
  NC
