# Fritzing sketch RelayModuleTest (saved by Fritzing 0.9.0b)
breadboards: 1

parts:
  KY-1 = Keyes Relay [package=THT]
  Part1 = Arduino Uno (Rev3)
  VCC1 = Battery block 9V
  LED1 = LED - 5mm [color="Red (633nm)" package="5 mm [THT]"]
  M1 = DC Motor
  R1 = Resistor [tolerance=±5% resistance=1k package=THT]

nets:
  N1: KY-1.signal, Part1.D6_PWM
  N2: KY-1.power, Part1.5V
  N3: KY-1.ground, Part1.GND
  N4: KY-1.NC, LED1.anode
  N5: KY-1.C, VCC1.+
  N6: KY-1.NO, M1.pin_2
  GND: VCC1.-, M1.pin_1, R1.Pin_1
  N7: LED1.cathode, R1.Pin_0

notes:
  NO
  NC

custom parts:
  Keyes Relay: The Keyes 5V relay module is suitable for SCM development, home appliance control. It uses a 5V~12V TIL control signal which can control DC / AC signal.
