# Fritzing sketch RgbOhmMeter (saved by Fritzing 0.9.2b)
breadboards: 1

parts:
  Part1 = Arduino Uno (Rev3)
  LCD1 = LCD screen  # not connected
  LCD_I2C_Adapter = female pin header, 4 pins [form="♀ (female)"]
  Rx = Resistor [tolerance=±5% resistance=220 package=THT]
  R1 = Resistor [tolerance=±5% resistance=220 package=THT]
  R2 = Resistor [tolerance=±5% resistance=1k package=THT]
  R3 = Resistor [tolerance=±5% resistance=10k package=THT]
  R4 = Resistor [tolerance=±5% resistance=100k package=THT]
  C1 = Ceramic Capacitor [capacitance=100nF package="100 mil [THT, multilayer]"]
  LED1 = RGB LED - (4 legs) [package="5 mm [THT]"]
  R5 = Resistor [tolerance=±5% resistance=1.5k package=THT]
  R6 = Resistor [tolerance=±5% resistance=1.2k package=THT]
  R7 = Resistor [tolerance=±5% resistance=680k package=THT]
  LED2 = RGB LED - (4 legs) [package="5 mm [THT]"]
  LED3 = RGB LED - (4 legs) [package="5 mm [THT]"]

nets:
  Vm: Part1.A0, Rx.Pin_0, R1.Pin_1, R2.Pin_1, R3.Pin_1, R4.Pin_1, C1.1
  SDA: Part1.A4/SDA, LCD_I2C_Adapter.pin3
  SCL: Part1.A5/SCL, LCD_I2C_Adapter.pin4
  N1: Part1.D8, LED3.common_anode
  PWM_R: Part1.D9_PWM, R5.Pin_1
  PWM_G: Part1.D10_PWM/SS, R6.Pin_1
  PWM_B: Part1.D11_PWM/MOSI, R7.Pin_1
  N2: Part1.D2, R1.Pin_0
  N3: Part1.D3_PWM, R2.Pin_0
  N4: Part1.D4, R3.Pin_0
  N5: Part1.D5_PWM, R4.Pin_0
  N6: Part1.D6_PWM, LED1.common_anode
  N7: Part1.D7, LED2.common_anode
  VCC: Part1.5V, LCD_I2C_Adapter.pin2
  GND: Part1.GND, LCD_I2C_Adapter.pin1, Rx.Pin_1, C1.0
  N8: LED1.red_cathode, R5.Pin_0, LED2.red_cathode, LED3.red_cathode
  N9: LED1.green_cathode, R6.Pin_0, LED2.green_cathode, LED3.green_cathode
  N10: LED1.blue_cathode, R7.Pin_0, LED2.blue_cathode, LED3.blue_cathode

notes:
  DUT (Rx)
