# Fritzing sketch RotaryEncoderISR (saved by Fritzing 0.9.2b)
breadboards: 1

parts:
  Part1 = Arduino Uno (Rev3)
  RE1 = Rotary Encoder [package=THT]

nets:
  N1: Part1.GND, RE1.EncoderPinC
  N2: Part1.D2, RE1.EncoderPinB
  N3: Part1.D4, RE1.EncoderPinA
