# Fritzing sketch RotaryEncoderISR_hw_debounce (saved by Fritzing 0.9.2b)
breadboards: 1

parts:
  Part1 = Arduino Uno (Rev3)
  RE1 = Rotary Encoder [package=THT]
  R1 = Resistor [tolerance=±5% resistance=10k package=THT]
  R2 = Resistor [tolerance=±5% resistance=10k package=THT]
  R3 = Resistor [tolerance=±5% resistance=10k package=THT]
  R4 = Resistor [tolerance=±5% resistance=10k package=THT]
  C1 = Ceramic Capacitor [capacitance=10nF package="100 mil [THT, multilayer]"]
  C2 = Ceramic Capacitor [capacitance=10nF package="100 mil [THT, multilayer]"]

nets:
  N1: Part1.GND, RE1.EncoderPinC, C1.1, C2.0
  N2: Part1.D2, R2.Pin_0, C1.0
  N3: Part1.D4, R1.Pin_0, C2.1
  N4: Part1.5V, R3.Pin_1, R4.Pin_1
  N5: RE1.EncoderPinA, R1.Pin_1, R3.Pin_0
  N6: RE1.EncoderPinB, R2.Pin_1, R4.Pin_0
