# Fritzing sketch RotaryEncoderMethods (saved by Fritzing 0.9.2b)
breadboards: 1

parts:
  Part1 = Arduino Uno (Rev3)
  RE1 = Rotary Encoder [package=THT]
  LED1 = LED - 3mm [color="Red (633nm)" package="3 mm [THT]"]
  LED2 = LED - 3mm [color="Green (555nm)" package="3 mm [THT]"]
  R1 = Resistor [tolerance=±5% resistance=1k package=THT]
  R2 = Resistor [tolerance=±5% resistance=1k package=THT]

nets:
  N1: Part1.GND, RE1.EncoderPinC, R1.Pin_1, R2.Pin_1
  N2: Part1.D2, RE1.EncoderPinB
  N3: Part1.D3_PWM, RE1.EncoderPinA
  N4: Part1.D5_PWM, LED2.anode
  N5: Part1.D6_PWM, LED1.anode
  N6: LED1.cathode, R1.Pin_0
  N7: LED2.cathode, R2.Pin_0
