# Fritzing sketch RotaryEncoderMethods_hw_debounce (saved by Fritzing 0.9.2b)
breadboards: 1

parts:
  Part1 = Arduino Uno (Rev3)
  RE1 = Rotary Encoder [package=THT]
  LED1 = LED - 3mm [color="Red (633nm)" package="3 mm [THT]"]
  LED2 = LED - 3mm [color="Green (555nm)" package="3 mm [THT]"]
  R1 = Resistor [tolerance=±5% resistance=1k package=THT]
  R2 = Resistor [tolerance=±5% resistance=1k package=THT]
  R4 = Resistor [tolerance=±5% resistance=10k package=THT]
  C1 = Ceramic Capacitor [capacitance=100nF package="100 mil [THT, multilayer]"]
  C2 = Ceramic Capacitor [capacitance=100nF package="100 mil [THT, multilayer]"]
  R6 = Resistor [tolerance=±5% resistance=10k package=THT]

nets:
  GND: Part1.GND, RE1.EncoderPinC, R1.Pin_1, R2.Pin_1, C1.1, C2.0
  N1: Part1.D2, C2.1, R6.Pin_0
  N2: Part1.D3_PWM, R4.Pin_0, C1.0
  N3: Part1.D5_PWM, LED2.anode
  N4: Part1.D6_PWM, LED1.anode
  N5: RE1.EncoderPinA, R4.Pin_1
  N6: RE1.EncoderPinB, R6.Pin_1
  N7: LED1.cathode, R1.Pin_0
  N8: LED2.cathode, R2.Pin_0
