# Fritzing sketch RotaryEncoderModule (saved by Fritzing 0.9.2b)
breadboards: 1

parts:
  Part1 = Arduino Uno (Rev3)
  ENCODER1 = Rotary Encoder with Knob
  Part2 = LED Matrix - Serial Interface - Red/Green/Blue

nets:
  N1: Part1.D10_PWM/SS, Part2.MOSI
  N2: Part1.D11_PWM/MOSI, Part2.CS
  N3: Part1.D12/MISO, Part2.SCK
  CLK: Part1.D2, ENCODER1.no_name_yet#1
  DT: Part1.D3_PWM, ENCODER1.no_name_yet#2
  SW: Part1.D4, ENCODER1.no_name_yet#3
  VCC: Part1.5V, ENCODER1.no_name_yet#4, Part2.VCC
  GND: Part1.GND, ENCODER1.no_name_yet#5, Part2.GND

notes:
  This is not the correct part. Read net labels instead of part pin labels.
  This is not the correct part. Read net labels instead of pin connections.

custom parts:
  Rotary Encoder with Knob: Rotary Encoder with 1/4" Shaft and Knob
