# Fritzing sketch Simple7SegmentDisplay (saved by Fritzing 0.9.0b)
breadboards: 1

parts:
  U1 = 7-SEGMENT-DISPLAY [package=7-segment-display]
  Part2 = Arduino Mega 2560 (Rev3)
  R1 = Resistor [tolerance=±5% resistance=220 package=THT]
  R2 = Resistor [tolerance=±5% resistance=220 package=THT]

nets:
  N1: U1.E, Part2.D8_PWM
  N2: U1.D, Part2.D6_PWM
  N3: U1.G1, Part2.D5_PWM
  N4: U1.C, R1.Pin_1
  N5: U1.DP, Part2.D4_PWM
  N6: U1.B, Part2.D9_PWM
  N7: U1.A, Part2.D3_PWM
  N8: U1.G2, Part2.D2_PWM
  N9: U1.F, R2.Pin_0
  N10: U1.G, Part2.D7_PWM
  N11: Part2.GND, R1.Pin_0, R2.Pin_1
