# Fritzing sketch SolenoidControl (saved by Fritzing 0.9.2b)
breadboards: 1

parts:
  L1 = Solenoid
  D1 = Rectifier Diode [part_number=1N4001 package="300 mil [THT]"]
  Part1 = Arduino Uno (Rev3)
  VCC1 = Battery block 9V
  Q1 = NPN-Transistor [part_number=S9013 package="TO92 [THT]"]
  R1 = Resistor [tolerance=±5% resistance=1k package=THT]

nets:
  N1: L1.pin1, D1.anode, Q1.C
  N2: L1.pin2, D1.cathode, VCC1.+
  N3: Part1.D8, R1.Pin_1
  N4: Part1.GND, VCC1.-, Q1.E
  N5: Q1.B, R1.Pin_0
