# Fritzing sketch StereoLightTrigger (saved by Fritzing 0.9.0b)
breadboards: 1

parts:
  R1 = Photocell (LDR) [package=THT]
  R3 = Resistor [tolerance=±5% resistance=4.7k package=THT]
  R4 = Resistor [tolerance=±5% resistance=4.7k package=THT]
  LED1 = LED - 5mm [color="Red (633nm)" package="5 mm [THT]"]
  R5 = Resistor [tolerance=±5% resistance=1k package=THT]
  R2 = Trimmer Potentiometer [maximum_resistance=50kΩ package=THT]
  R6 = Resistor [tolerance=±5% resistance=1k package=THT]
  LED2 = LED - 5mm [color="Green (570nm)" package="5 mm [THT]"]
  R7 = Photocell (LDR) [package=THT]
  R8 = Trimmer Potentiometer [maximum_resistance=50kΩ package=THT]
  R9 = Resistor [tolerance=±5% resistance=4.7k package=THT]
  R10 = Resistor [tolerance=±5% resistance=4.7k package=THT]
  IC1 = LM324 [package=dil16]
  Part2 = Arduino Nano (Rev3.0)
  R11 = Resistor [tolerance=±5% resistance=1k package=THT]
  R12 = Resistor [tolerance=±5% resistance=1k package=THT]
  LED3 = LED - 3mm [color="Red (633nm)" package="3 mm [THT]"]
  LED4 = LED - 3mm [color="Green (570nm)" package="3 mm [THT]"]
  Vcc = Power plug [part_number=5V]

nets:
  5V: R1.pin_0, R2.leg2, R7.pin_0, R8.leg2, IC1.V+, Part2.5V, Vcc.VCC
  N1: R1.pin_1, R4.Pin_0, IC1.IN1-
  N2: R3.Pin_0, R2.wiper, IC1.IN1+
  GND: R3.Pin_1, R4.Pin_1, LED1.cathode, LED2.cathode, R9.Pin_1, R10.Pin_1, IC1.GND, Part2.GND, LED3.cathode, LED4.cathode, Vcc.GND
  N3: LED1.anode, R5.Pin_1
  N4: R5.Pin_0, IC1.OUT1, Part2.D2
  N5: R6.Pin_0, IC1.OUT2, Part2.D3
  N6: R6.Pin_1, LED2.anode
  N7: R7.pin_1, R10.Pin_0, IC1.IN2-
  N8: R8.wiper, R9.Pin_0, IC1.IN2+
  N9: Part2.D7, R11.Pin_0
  N10: Part2.D8, R12.Pin_0
  N11: R11.Pin_1, LED3.anode
  N12: R12.Pin_1, LED4.anode

custom parts:
  LM324: LM324 Quad OpAmp
