# Fritzing sketch SwitchInputs (saved by Fritzing 1.0.1rc)
breadboards: 1

parts:
  Part1 = Arduino Uno (Rev3)
  S1 = Pushbutton [package="[THT]"]
  S2 = Pushbutton [package="[THT]"]
  R1 = Resistor [tolerance=±5% power=0.25W resistance=10k package=THT]
  LED1 = LED - 3mm [color="Red (633nm)" current=0.030A package="3 mm [THT]"]
  R2 = Resistor [tolerance=±5% power=0.25W resistance=470 package=THT]
  R3 = Resistor [tolerance=±5% power=0.25W resistance=10k package=THT]
  LED2 = LED - 3mm [color="Red (633nm)" current=0.030A package="3 mm [THT]"]
  R4 = Resistor [tolerance=±5% power=0.25W resistance=470 package=THT]
  S3 = Pushbutton [package="[THT]"]
  LED3 = LED - 3mm [color="Red (633nm)" current=0.030A package="3 mm [THT]"]
  R5 = Resistor [tolerance=±5% power=0.25W resistance=470 package=THT]

nets:
  pinA: Part1.D2, S1.Pin_3, S1.Pin_4, R1.Pin_1
  pinA_led: Part1.D3_PWM, LED1.anode
  pinB: Part1.D4, S2.Pin_3, S2.Pin_4, R3.Pin_1
  pinB_led: Part1.D5_PWM, LED2.anode
  pinC: Part1.D6_PWM, S3.Pin_3, S3.Pin_4
  pinC_led: Part1.D7, LED3.anode
  5V: Part1.5V, S2.Pin_1, S2.Pin_2, R1.Pin_0
  GND: Part1.GND, S1.Pin_1, S1.Pin_2, R2.Pin_0, R3.Pin_0, R4.Pin_0, S3.Pin_1, S3.Pin_2, R5.Pin_0
  N1: LED1.cathode, R2.Pin_1
  N2: LED2.cathode, R4.Pin_1
  N3: LED3.cathode, R5.Pin_1
