# Fritzing sketch Color128x128 (saved by Fritzing 0.9.2b)
breadboards: 1

parts:
  Part1 = Arduino Uno (Rev3)
  J1 = female pin header, 8 pins [form="♀ (female)"]

nets:
  RESET: Part1.D8, J1.pin5
  A0: Part1.D9_PWM, J1.pin4
  CS: Part1.D10_PWM/SS, J1.pin6
  SDA: Part1.D11_PWM/MOSI, J1.pin3
  SCK: Part1.D13/SCK, J1.pin2
  LED/VCC: Part1.5V, J1.pin1, J1.pin8
  GND: Part1.GND, J1.pin7

notes:
  Note: this is a 5V "cheat". It does work but is probably not good for the LCD long term. 3.3V with level shifters is recommended for use with 5V MCUs
