# Fritzing sketch TemperatureLoggerTypeK (saved by Fritzing 0.9.2b)
breadboards: 1

parts:
  Part1 = Arduino Uno (Rev3)
  Nokia_5110_LCD_Module1 = Nokia5110LCDModule
  U1 = TL072/TLE2072 Dual Op. Amp [part_number=LM358 package="DIP8 [THT]"]
  T1 = Temperature Sensor (Thermistor) [thermistor_type=PTC part_number="Type K" package=THT]
  R2 = Resistor [tolerance=±5% resistance=330k package=THT]
  R1 = Resistor [tolerance=±5% resistance=1k package=THT]
  T2 = LM35 Temperature Sensor [package="TO92 [THT]"]
  C1 = Ceramic Capacitor [capacitance=100nF package="100 mil [THT, multilayer]"]

nets:
  N1: Part1.A0, U1.Pin_6, U1.Pin_7
  N2: Part1.A1, T2.Vout
  RST: Part1.D8, Nokia_5110_LCD_Module1.RST
  DC: Part1.D9_PWM, Nokia_5110_LCD_Module1.D/C
  SCE: Part1.D10_PWM/SS, Nokia_5110_LCD_Module1.SCE
  DN: Part1.D11_PWM/MOSI, Nokia_5110_LCD_Module1.6_DN_(MOSI)
  SCLK: Part1.D13/SCK, Nokia_5110_LCD_Module1.SCLK
  VCC: Part1.5V, Nokia_5110_LCD_Module1.Vcc, U1.Pin_8, T2.+Vs
  GND: Part1.GND, Nokia_5110_LCD_Module1.Grnd, Nokia_5110_LCD_Module1.LED, U1.Pin_4, T1.pin_0, R1.Pin_0, T2.GND, C1.0
  N3: U1.Pin_1, U1.Pin_5, R2.Pin_1
  N4: U1.Pin_2, R2.Pin_0, R1.Pin_1
  N5: U1.Pin_3, T1.pin_1, C1.1

custom parts:
  : Nokia 5110 LCD with 8 pin. It's a 45mm*45mm module part. Description: The Nokia 5110 is a basic graphic LCD screen for lots of applications. It was originally intended for as a cell phone screen. This one is mounted on an easy to solder PCB. It uses the PCD8544 controller. The PCD8544 is a low power CMOS LCD controller/driver, designed to drive a graphic display of 48 rows and 84 columns. All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
  TL072/TLE2072 Dual Op. Amp: The classic LM 358 Dual Operational Amplifier (Op-Amp). The analog swiss-army knife.
