# Fritzing sketch Lucky4DOracle (saved by Fritzing 0.9.2b)
breadboards: 1

parts:
  Part1 = Arduino Nano (Rev3.0)
  S1 = Pushbutton [package="[THT]"]
  5V2A = Power plug
  JP-QR701 = female pin header, 6 pins [form="♀ (female)"]
  J1 = male pin header, 2 pins [form="♂ (male)"]
  S2 = Toggle Switch [package=THT]

nets:
  GND: Part1.GND, S1.Pin_1, S1.Pin_2, 5V2A.GND, JP-QR701.pin1, JP-QR701.pin4
  N1: Part1.D2, S1.Pin_3, S1.Pin_4
  RXM/TXD: Part1.D5, JP-QR701.pin6
  RXD/TXM: Part1.D6, JP-QR701.pin5
  OPTIONAL_5V: Part1.5V, J1.pin2
  N2: 5V2A.VCC, S2.COM
  VH: JP-QR701.pin3, J1.pin1, S2.L2

notes:
  JP-QR701 Connector
