# Fritzing sketch TheToneRanger (saved by Fritzing 0.9.2b)
breadboards: 1

parts:
  Part1 = Arduino Uno (Rev3)
  VL53L0X1 = female pin header, 6 pins [form="♀ (female)"]
  SPK1 = Piezo Speaker
  Q1 = NPN-Transistor [package="TO92 [THT]"]
  R1 = Resistor [tolerance=±5% resistance=1k package=THT]

nets:
  SDA: Part1.A4/SDA, VL53L0X1.pin4
  SCL: Part1.A5/SCL, VL53L0X1.pin3
  N1: Part1.D8, R1.Pin_0
  GND: Part1.GND, VL53L0X1.pin2, Q1.E
  VCC: Part1.5V, VL53L0X1.pin1, SPK1.pin2
  G: VL53L0X1.pin5
  X: VL53L0X1.pin6
  N2: SPK1.pin1, Q1.C
  N3: Q1.B, R1.Pin_1
