# Fritzing sketch VariableFrequencyRunwayLEDs (saved by Fritzing 0.9.2b)
breadboards: 2

parts:
  IC1 = IC, DIP package, 8 pins [chip_label=LM331]
  C1 = Ceramic Capacitor [capacitance=100nF package="100 mil [THT, multilayer]"]
  C2 = Ceramic Capacitor [capacitance=1µF package="100 mil [THT, multilayer]"]
  R4 = Resistor [tolerance=±5% resistance=10k package=THT]
  R3 = Resistor [tolerance=±5% resistance=3.3k package=THT]
  R2 = Resistor [tolerance=±5% resistance=100k package=THT]
  R1 = Resistor [tolerance=±5% resistance=1M package=THT]
  Part1 = Arduino Uno (Rev3)
  R5 = Resistor [tolerance=±5% resistance=2M package=THT]
  IC3 = IC, DIP package, 16 pins [chip_label=CD4017 part_number=CD4017]
  R6 = Resistor [tolerance=±5% resistance=1k package=THT]
  R7 = Resistor [tolerance=±5% resistance=1k package=THT]
  R8 = Resistor [tolerance=±5% resistance=1k package=THT]
  LED1 = LED - 3mm [color="Blue (470nm)" package="3 mm [THT]"]
  LED2 = LED - 3mm [color="Blue (470nm)" package="3 mm [THT]"]
  LED4 = LED - 3mm [color="Blue (470nm)" package="3 mm [THT]"]
  LED5 = LED - 3mm [color="Blue (470nm)" package="3 mm [THT]"]
  LED6 = LED - 3mm [color="Blue (470nm)" package="3 mm [THT]"]
  LED3 = LED - 3mm [color="Blue (470nm)" package="3 mm [THT]"]
  LED7 = LED - 3mm [color="Blue (470nm)" package="3 mm [THT]"]
  LED8 = LED - 3mm [color="Blue (470nm)" package="3 mm [THT]"]
  R9 = Resistor [tolerance=±5% resistance=1k package=THT]
  LED9 = LED - 3mm [color="Blue (470nm)" package="3 mm [THT]"]
  LED10 = LED - 3mm [color="Blue (470nm)" package="3 mm [THT]"]
  R10 = Resistor [tolerance=±5% resistance=1k package=THT]
  LED11 = LED - 3mm [color="Blue (470nm)" package="3 mm [THT]"]
  LED12 = LED - 3mm [color="Blue (470nm)" package="3 mm [THT]"]
  R11 = Resistor [tolerance=±5% resistance=1k package=THT]
  LED13 = LED - 3mm [color="Blue (470nm)" package="3 mm [THT]"]
  LED14 = LED - 3mm [color="Blue (470nm)" package="3 mm [THT]"]
  R12 = Resistor [tolerance=±5% resistance=1k package=THT]
  LED15 = LED - 3mm [color="Blue (470nm)" package="3 mm [THT]"]
  LED16 = LED - 3mm [color="Blue (470nm)" package="3 mm [THT]"]
  R13 = Resistor [tolerance=±5% resistance=1k package=THT]
  LED17 = LED - 3mm [color="Blue (470nm)" package="3 mm [THT]"]
  LED18 = LED - 3mm [color="Blue (470nm)" package="3 mm [THT]"]
  R14 = Resistor [tolerance=±5% resistance=1k package=THT]
  LED19 = LED - 3mm [color="Blue (470nm)" package="3 mm [THT]"]
  LED20 = LED - 3mm [color="Blue (470nm)" package="3 mm [THT]"]
  R15 = Resistor [tolerance=±5% resistance=1k package=THT]

nets:
  N1: IC1.pin1, IC1.pin6, C2.1, R2.Pin_0
  N2: IC1.pin2, IC1.pin7, R4.Pin_0
  CLK: IC1.pin3, R3.Pin_1, IC3.pin14
  GND: IC1.pin4, C1.0, C2.0, R4.Pin_1, R2.Pin_1, Part1.GND, IC3.pin8, IC3.pin13, IC3.pin15, LED1.cathode, LED2.cathode, LED4.cathode, LED5.cathode, LED6.cathode, LED3.cathode, LED7.cathode, LED8.cathode, LED9.cathode, LED10.cathode, LED11.cathode, LED12.cathode, LED13.cathode, LED14.cathode, LED15.cathode, LED16.cathode, LED17.cathode, LED18.cathode, LED19.cathode, LED20.cathode
  N3: IC1.pin5, C1.1, R1.Pin_0, R5.Pin_1
  Vs: IC1.pin8, R3.Pin_0, R1.Pin_1, Part1.5V, IC3.pin16
  PWM: Part1.D10_PWM/SS, R5.Pin_0
  Q5: IC3.pin1, R11.Pin_1
  Q1: IC3.pin2, R7.Pin_1
  Q0: IC3.pin3, R6.Pin_1
  Q2: IC3.pin4, R8.Pin_1
  Q6: IC3.pin5, R12.Pin_1
  Q7: IC3.pin6, R13.Pin_1
  Q3: IC3.pin7, R9.Pin_1
  Q8: IC3.pin9, R14.Pin_1
  Q4: IC3.pin10, R10.Pin_1
  Q9: IC3.pin11, R15.Pin_1
  N4: R6.Pin_0, LED1.anode, LED2.anode
  N5: R7.Pin_0, LED4.anode, LED3.anode
  N6: R8.Pin_0, LED5.anode, LED6.anode
  N7: LED7.anode, LED8.anode, R9.Pin_0
  N8: LED9.anode, LED10.anode, R10.Pin_0
  N9: LED11.anode, LED12.anode, R11.Pin_0
  N10: LED13.anode, LED14.anode, R12.Pin_0
  N11: LED15.anode, LED16.anode, R13.Pin_0
  N12: LED17.anode, LED18.anode, R14.Pin_0
  N13: LED19.anode, LED20.anode, R15.Pin_0
