# Fritzing sketch VariableLED (saved by Fritzing 1.0.1rc)
breadboards: 1

parts:
  Part1 = Arduino Uno (Rev3)
  R1 = Resistor [tolerance=±5% resistance=220 power=0.25W package=THT]
  R2 = Rotary Potentiometer (Small) [maximum_resistance=50kΩ knob_status=50% power=0.5W package=THT]
  LED1 = LED - 3mm [color="Red (633nm)" current=0.030A package="3 mm [THT]"]
  CH1 = Multimeter straight red probe

nets:
  N1: Part1.A0, R2.wiper
  N2: Part1.D9_PWM, LED1.anode, CH1.Probe_tip
  VCC: Part1.5V, R2.leg1
  GND: Part1.GND, R1.Pin_0, R2.leg2
  N3: R1.Pin_1, LED1.cathode

notes:
  CH1
