# Fritzing sketch VoltageSelfMeasurement (saved by Fritzing 0.9.2b)

parts:
  Part1 = Arduino Uno (Rev3)
  C1 = Ceramic Capacitor [capacitance=10nF package="100 mil [THT, multilayer]"]

nets:
  GND: Part1.GND, C1.1
  N1: Part1.AREF, C1.0
