# Fritzing sketch XYplotter (saved by Fritzing 0.9.2b)
breadboards: 1

parts:
  Part1 = Arduino Uno (Rev3)
  IC1 = IC, DIP package, 14 pins [chip_label=MCP42010]

nets:
  LATCH: Part1.D9_PWM, IC1.pin1
  DATA: Part1.D11_PWM/MOSI, IC1.pin3
  CLOCK: Part1.D13/SCK, IC1.pin2
  GND/VSS: Part1.GND, IC1.pin4, IC1.pin5, IC1.pin10
  VDD: Part1.5V, IC1.pin7, IC1.pin8, IC1.pin11, IC1.pin12, IC1.pin14
  CH2: IC1.pin6
  CH1: IC1.pin9

notes:
  CH1
  CH2
