# Fritzing sketch move-nums (saved by Fritzing 1.0.1rc)
breadboards: 1

parts:
  Part1 = Arduino Uno (Rev3)
  ENCODER1 = Rotary Encoder with Knob
  Part2 = LED Matrix - Serial Interface - Red/Green/Blue
  7-seg_Module = female pin header, 5 pins [form="♀ (female)"]
  5V_Power_Supply = Power plug

nets:
  7SEG_CS: Part1.D9_PWM, 7-seg_Module.pin2
  MATRIX_CS: Part1.D10_PWM/SS, Part2.CS
  MOSI: Part1.D11_PWM/MOSI, Part2.MOSI, 7-seg_Module.pin3
  SCK: Part1.D13/SCK, Part2.SCK, 7-seg_Module.pin1
  CLK: Part1.D2, ENCODER1.no_name_yet#1
  DT: Part1.D3_PWM, ENCODER1.no_name_yet#2
  SW: Part1.D4, ENCODER1.no_name_yet#3
  GND: Part1.GND, ENCODER1.no_name_yet#5, Part2.GND, 7-seg_Module.pin4, 5V_Power_Supply.GND
  VCC: ENCODER1.no_name_yet#4, Part2.VCC, 7-seg_Module.pin5, 5V_Power_Supply.VCC

notes:
  This is not the correct part. Read net labels instead of part pin labels.
  This is not the correct part. Read net labels instead of pin connections.
  7-Segment Module

custom parts:
  Rotary Encoder with Knob: Rotary Encoder with 1/4" Shaft and Knob
