# Fritzing sketch PingPong (saved by Fritzing 0.9.2b)
breadboards: 1

parts:
  Part1 = Arduino Uno (Rev3)
  Part2 = NRF24L01
  R1 = Resistor [tolerance=±5% resistance=1k package=THT]
  LED1 = LED - 5mm [color="Red (633nm)" package="5 mm [THT]"]

nets:
  GND/PONG_ENABLE: Part1.D8, Part1.GND, Part2.GND, R1.Pin_0
  CE: Part1.D9_PWM, Part2.CE
  CSN: Part1.D10_PWM/SS, Part2.CSN
  MOSI: Part1.D11_PWM/MOSI, Part2.MOSI
  MISO: Part1.D12/MISO, Part2.MISO
  SCK: Part1.D13/SCK, Part2.SCK
  N1: Part1.D7, LED1.anode
  3V3: Part1.3V3, Part2.VCC
  N2: R1.Pin_1, LED1.cathode

notes:
  pin 8 connected to ground for "pong" node. Left unconnected for "ping" node
