# Fritzing sketch Scanner (saved by Fritzing 0.9.2b)
breadboards: 1

parts:
  Part1 = Arduino Uno (Rev3)
  MOD2 = Nokia5110LCDModule
  3_3V = Power plug
  MOD1 = NRF24L01
  S1 = Pushbutton [package="[THT]"]

nets:
  N1: Part1.D8, MOD1.CE
  N2: Part1.D9_PWM, MOD1.CSN
  N3: Part1.D11_PWM/MOSI, MOD1.MOSI
  N4: Part1.D12/MISO, MOD1.MISO
  N5: Part1.D13/SCK, MOD1.SCK
  GND: Part1.GND, MOD2.Grnd, 3_3V.GND, MOD1.GND, S1.Pin_3, S1.Pin_4
  N6: Part1.D2, S1.Pin_1, S1.Pin_2
  N7: Part1.D3_PWM, MOD2.D/C
  N8: Part1.D4, MOD2.SCE
  N9: Part1.D5_PWM, MOD2.RST
  N10: Part1.D6_PWM, MOD2.6_DN_(MOSI)
  N11: Part1.D7, MOD2.SCLK
  5V: Part1.5V, MOD2.Vcc
  3V3: 3_3V.VCC, MOD1.VCC

custom parts:
  : Nokia 5110 LCD with 8 pin. It's a 45mm*45mm module part. Description: The Nokia 5110 is a basic graphic LCD screen for lots of applications. It was originally intended for as a cell phone screen. This one is mounted on an easy to solder PCB. It uses the PCD8544 controller. The PCD8544 is a low power CMOS LCD controller/driver, designed to drive a graphic display of 48 rows and 84 columns. All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
