# Fritzing sketch tin_counter (saved by Fritzing 0.9.2b)
breadboards: 1

parts:
  Part1 = Arduino Uno (Rev3)
  Part2 = SRF05 Ultrasonic Rangefinder
  LED1 = LED - 5mm [color="Red (633nm)" package="5 mm [THT]"]
  LED2 = LED - 5mm [color="Green (570nm)" package="5 mm [THT]"]
  R1 = Resistor [tolerance=±5% resistance=560 package=THT]
  R2 = Resistor [tolerance=±5% resistance=560 package=THT]
  LABEL_SWITCH = Pushbutton [package=THT]
  BUZZER = Piezo Speaker

nets:
  N1: Part1.A0, LABEL_SWITCH.leg0
  N2: Part1.D9_PWM, BUZZER.pin1
  N3: Part1.D10_PWM/SS, LED1.anode
  N4: Part1.D11_PWM/MOSI, LED2.anode
  N5: Part1.D12/MISO, Part2.Echo
  N6: Part1.D13/SCK, Part2.Trig
  VCC: Part1.5V, Part2.VCC, LABEL_SWITCH.leg1
  GND: Part1.GND, Part2.GND, R1.Pin_1, R2.Pin_1, BUZZER.pin2
  N7: LED1.cathode, R1.Pin_0
  N8: LED2.cathode, R2.Pin_0

notes:
  Tin-label contact
